// Digital circuit 32BIT ADDER.dig as structural Verilog
module _32BIT_ADDER (
  input  [31:0] _32BIT_A_IN,
  input  [31:0] _32BIT_B_IN,
  input  CARRY_IN,
  output [31:0] _32BIT_RESULT
);

  wire and_1_out, and_2_out, and_3_out, and_4_out, and_5_out, and_6_out, and_7_out, and_8_out, and_9_out,
       and_10_out, and_11_out, and_12_out, and_13_out, and_14_out, and_15_out, and_16_out, and_17_out,
       and_18_out, and_19_out, and_20_out, and_21_out, and_22_out, and_23_out, and_24_out, and_25_out,
       and_26_out, and_27_out, and_28_out, and_29_out, and_30_out, and_31_out, and_32_out, and_33_out,
       and_34_out, and_35_out, and_36_out, and_37_out, and_38_out, and_39_out, and_40_out, and_41_out,
       and_42_out, and_43_out, and_44_out, and_45_out, and_46_out, and_47_out, and_48_out, and_49_out,
       and_50_out, and_51_out, and_52_out, and_53_out, and_54_out, and_55_out, and_56_out, and_57_out,
       and_58_out, and_59_out, and_60_out, and_61_out, and_62_out, and_63_out, and_64_out, or_1_out,
       or_2_out, or_3_out, or_4_out, or_5_out, or_6_out, or_7_out, or_8_out, or_9_out, or_10_out, or_11_out,
       or_12_out, or_13_out, or_14_out, or_15_out, or_16_out, or_17_out, or_18_out, or_19_out, or_20_out,
       or_21_out, or_22_out, or_23_out, or_24_out, or_25_out, or_26_out, or_27_out, or_28_out, or_29_out,
       or_30_out, or_31_out, xor_1_out, xor_2_out, xor_3_out, xor_4_out, xor_5_out, xor_6_out, xor_7_out,
       xor_8_out, xor_9_out, xor_10_out, xor_11_out, xor_12_out, xor_13_out, xor_14_out, xor_15_out,
       xor_16_out, xor_17_out, xor_18_out, xor_19_out, xor_20_out, xor_21_out, xor_22_out, xor_23_out,
       xor_24_out, xor_25_out, xor_26_out, xor_27_out, xor_28_out, xor_29_out, xor_30_out, xor_31_out,
       xor_32_out;

  xor xor_1 (xor_1_out, _32BIT_A_IN[0], _32BIT_B_IN[0]);
  and and_1 (and_1_out, _32BIT_A_IN[0], _32BIT_B_IN[0]);
  xor xor_2 (xor_2_out, _32BIT_A_IN[1], _32BIT_B_IN[1]);
  and and_2 (and_2_out, _32BIT_A_IN[1], _32BIT_B_IN[1]);
  xor xor_3 (xor_3_out, _32BIT_A_IN[2], _32BIT_B_IN[2]);
  and and_3 (and_3_out, _32BIT_A_IN[2], _32BIT_B_IN[2]);
  xor xor_4 (xor_4_out, _32BIT_A_IN[3], _32BIT_B_IN[3]);
  and and_4 (and_4_out, _32BIT_A_IN[3], _32BIT_B_IN[3]);
  xor xor_5 (xor_5_out, _32BIT_A_IN[4], _32BIT_B_IN[4]);
  and and_5 (and_5_out, _32BIT_A_IN[4], _32BIT_B_IN[4]);
  xor xor_6 (xor_6_out, _32BIT_A_IN[5], _32BIT_B_IN[5]);
  and and_6 (and_6_out, _32BIT_A_IN[5], _32BIT_B_IN[5]);
  xor xor_7 (xor_7_out, _32BIT_A_IN[6], _32BIT_B_IN[6]);
  and and_7 (and_7_out, _32BIT_A_IN[6], _32BIT_B_IN[6]);
  xor xor_8 (xor_8_out, _32BIT_A_IN[7], _32BIT_B_IN[7]);
  and and_8 (and_8_out, _32BIT_A_IN[7], _32BIT_B_IN[7]);
  xor xor_9 (xor_9_out, _32BIT_A_IN[8], _32BIT_B_IN[8]);
  and and_9 (and_9_out, _32BIT_A_IN[8], _32BIT_B_IN[8]);
  xor xor_10 (xor_10_out, _32BIT_A_IN[9], _32BIT_B_IN[9]);
  and and_10 (and_10_out, _32BIT_A_IN[9], _32BIT_B_IN[9]);
  xor xor_11 (xor_11_out, _32BIT_A_IN[10], _32BIT_B_IN[10]);
  and and_11 (and_11_out, _32BIT_A_IN[10], _32BIT_B_IN[10]);
  xor xor_12 (xor_12_out, _32BIT_A_IN[11], _32BIT_B_IN[11]);
  and and_12 (and_12_out, _32BIT_A_IN[11], _32BIT_B_IN[11]);
  xor xor_13 (xor_13_out, _32BIT_A_IN[12], _32BIT_B_IN[12]);
  and and_13 (and_13_out, _32BIT_A_IN[12], _32BIT_B_IN[12]);
  xor xor_14 (xor_14_out, _32BIT_A_IN[13], _32BIT_B_IN[13]);
  and and_14 (and_14_out, _32BIT_A_IN[13], _32BIT_B_IN[13]);
  xor xor_15 (xor_15_out, _32BIT_A_IN[14], _32BIT_B_IN[14]);
  and and_15 (and_15_out, _32BIT_A_IN[14], _32BIT_B_IN[14]);
  xor xor_16 (xor_16_out, _32BIT_A_IN[15], _32BIT_B_IN[15]);
  and and_16 (and_16_out, _32BIT_A_IN[15], _32BIT_B_IN[15]);
  xor xor_17 (xor_17_out, _32BIT_A_IN[16], _32BIT_B_IN[16]);
  and and_17 (and_17_out, _32BIT_A_IN[16], _32BIT_B_IN[16]);
  xor xor_18 (xor_18_out, _32BIT_A_IN[17], _32BIT_B_IN[17]);
  and and_18 (and_18_out, _32BIT_A_IN[17], _32BIT_B_IN[17]);
  xor xor_19 (xor_19_out, _32BIT_A_IN[18], _32BIT_B_IN[18]);
  and and_19 (and_19_out, _32BIT_A_IN[18], _32BIT_B_IN[18]);
  xor xor_20 (xor_20_out, _32BIT_A_IN[19], _32BIT_B_IN[19]);
  and and_20 (and_20_out, _32BIT_A_IN[19], _32BIT_B_IN[19]);
  xor xor_21 (xor_21_out, _32BIT_A_IN[20], _32BIT_B_IN[20]);
  and and_21 (and_21_out, _32BIT_A_IN[20], _32BIT_B_IN[20]);
  xor xor_22 (xor_22_out, _32BIT_A_IN[21], _32BIT_B_IN[21]);
  and and_22 (and_22_out, _32BIT_A_IN[21], _32BIT_B_IN[21]);
  xor xor_23 (xor_23_out, _32BIT_A_IN[22], _32BIT_B_IN[22]);
  and and_23 (and_23_out, _32BIT_A_IN[22], _32BIT_B_IN[22]);
  xor xor_24 (xor_24_out, _32BIT_A_IN[23], _32BIT_B_IN[23]);
  and and_24 (and_24_out, _32BIT_A_IN[23], _32BIT_B_IN[23]);
  xor xor_25 (xor_25_out, _32BIT_A_IN[24], _32BIT_B_IN[24]);
  and and_25 (and_25_out, _32BIT_A_IN[24], _32BIT_B_IN[24]);
  xor xor_26 (xor_26_out, _32BIT_A_IN[25], _32BIT_B_IN[25]);
  and and_26 (and_26_out, _32BIT_A_IN[25], _32BIT_B_IN[25]);
  xor xor_27 (xor_27_out, _32BIT_A_IN[26], _32BIT_B_IN[26]);
  and and_27 (and_27_out, _32BIT_A_IN[26], _32BIT_B_IN[26]);
  xor xor_28 (xor_28_out, _32BIT_A_IN[27], _32BIT_B_IN[27]);
  and and_28 (and_28_out, _32BIT_A_IN[27], _32BIT_B_IN[27]);
  xor xor_29 (xor_29_out, _32BIT_A_IN[28], _32BIT_B_IN[28]);
  and and_29 (and_29_out, _32BIT_A_IN[28], _32BIT_B_IN[28]);
  xor xor_30 (xor_30_out, _32BIT_A_IN[29], _32BIT_B_IN[29]);
  and and_30 (and_30_out, _32BIT_A_IN[29], _32BIT_B_IN[29]);
  xor xor_31 (xor_31_out, _32BIT_A_IN[30], _32BIT_B_IN[30]);
  and and_31 (and_31_out, _32BIT_A_IN[30], _32BIT_B_IN[30]);
  xor xor_32 (xor_32_out, _32BIT_A_IN[31], _32BIT_B_IN[31]);
  and and_32 (and_32_out, _32BIT_A_IN[31], _32BIT_B_IN[31]);
  or or_1 (or_1_out, and_33_out, and_1_out);
  or or_2 (or_2_out, and_34_out, and_2_out);
  or or_3 (or_3_out, and_35_out, and_3_out);
  or or_4 (or_4_out, and_36_out, and_4_out);
  or or_5 (or_5_out, and_37_out, and_5_out);
  or or_6 (or_6_out, and_38_out, and_6_out);
  or or_7 (or_7_out, and_39_out, and_7_out);
  or or_8 (or_8_out, and_40_out, and_8_out);
  or or_9 (or_9_out, and_41_out, and_9_out);
  or or_10 (or_10_out, and_42_out, and_10_out);
  or or_11 (or_11_out, and_43_out, and_11_out);
  or or_12 (or_12_out, and_44_out, and_12_out);
  or or_13 (or_13_out, and_45_out, and_13_out);
  or or_14 (or_14_out, and_46_out, and_14_out);
  or or_15 (or_15_out, and_47_out, and_15_out);
  or or_16 (or_16_out, and_48_out, and_16_out);
  or or_17 (or_17_out, and_49_out, and_17_out);
  or or_18 (or_18_out, and_50_out, and_18_out);
  or or_19 (or_19_out, and_51_out, and_19_out);
  or or_20 (or_20_out, and_52_out, and_20_out);
  or or_21 (or_21_out, and_53_out, and_21_out);
  or or_22 (or_22_out, and_54_out, and_22_out);
  or or_23 (or_23_out, and_55_out, and_23_out);
  or or_24 (or_24_out, and_56_out, and_24_out);
  or or_25 (or_25_out, and_57_out, and_25_out);
  or or_26 (or_26_out, and_58_out, and_26_out);
  or or_27 (or_27_out, and_59_out, and_27_out);
  or or_28 (or_28_out, and_60_out, and_28_out);
  or or_29 (or_29_out, and_61_out, and_29_out);
  or or_30 (or_30_out, and_62_out, and_30_out);
  or or_31 (or_31_out, and_63_out, and_31_out);
  // Or or_32 has open pins: In_1=and_64_out, In_2=and_32_out, out=open
  xor xor_33 (_32BIT_RESULT[0], xor_1_out, CARRY_IN);
  and and_33 (and_33_out, CARRY_IN, xor_1_out);
  xor xor_34 (_32BIT_RESULT[1], xor_2_out, or_1_out);
  and and_34 (and_34_out, or_1_out, xor_2_out);
  xor xor_35 (_32BIT_RESULT[2], xor_3_out, or_2_out);
  and and_35 (and_35_out, or_2_out, xor_3_out);
  xor xor_36 (_32BIT_RESULT[3], xor_4_out, or_3_out);
  and and_36 (and_36_out, or_3_out, xor_4_out);
  xor xor_37 (_32BIT_RESULT[4], xor_5_out, or_4_out);
  and and_37 (and_37_out, or_4_out, xor_5_out);
  xor xor_38 (_32BIT_RESULT[5], xor_6_out, or_5_out);
  and and_38 (and_38_out, or_5_out, xor_6_out);
  xor xor_39 (_32BIT_RESULT[6], xor_7_out, or_6_out);
  and and_39 (and_39_out, or_6_out, xor_7_out);
  xor xor_40 (_32BIT_RESULT[7], xor_8_out, or_7_out);
  and and_40 (and_40_out, or_7_out, xor_8_out);
  xor xor_41 (_32BIT_RESULT[8], xor_9_out, or_8_out);
  and and_41 (and_41_out, or_8_out, xor_9_out);
  xor xor_42 (_32BIT_RESULT[9], xor_10_out, or_9_out);
  and and_42 (and_42_out, or_9_out, xor_10_out);
  xor xor_43 (_32BIT_RESULT[10], xor_11_out, or_10_out);
  and and_43 (and_43_out, or_10_out, xor_11_out);
  xor xor_44 (_32BIT_RESULT[11], xor_12_out, or_11_out);
  and and_44 (and_44_out, or_11_out, xor_12_out);
  xor xor_45 (_32BIT_RESULT[12], xor_13_out, or_12_out);
  and and_45 (and_45_out, or_12_out, xor_13_out);
  xor xor_46 (_32BIT_RESULT[13], xor_14_out, or_13_out);
  and and_46 (and_46_out, or_13_out, xor_14_out);
  xor xor_47 (_32BIT_RESULT[14], xor_15_out, or_14_out);
  and and_47 (and_47_out, or_14_out, xor_15_out);
  xor xor_48 (_32BIT_RESULT[15], xor_16_out, or_15_out);
  and and_48 (and_48_out, or_15_out, xor_16_out);
  xor xor_49 (_32BIT_RESULT[16], xor_17_out, or_16_out);
  and and_49 (and_49_out, or_16_out, xor_17_out);
  xor xor_50 (_32BIT_RESULT[17], xor_18_out, or_17_out);
  and and_50 (and_50_out, or_17_out, xor_18_out);
  xor xor_51 (_32BIT_RESULT[18], xor_19_out, or_18_out);
  and and_51 (and_51_out, or_18_out, xor_19_out);
  xor xor_52 (_32BIT_RESULT[19], xor_20_out, or_19_out);
  and and_52 (and_52_out, or_19_out, xor_20_out);
  xor xor_53 (_32BIT_RESULT[20], xor_21_out, or_20_out);
  and and_53 (and_53_out, or_20_out, xor_21_out);
  xor xor_54 (_32BIT_RESULT[21], xor_22_out, or_21_out);
  and and_54 (and_54_out, or_21_out, xor_22_out);
  xor xor_55 (_32BIT_RESULT[22], xor_23_out, or_22_out);
  and and_55 (and_55_out, or_22_out, xor_23_out);
  xor xor_56 (_32BIT_RESULT[23], xor_24_out, or_23_out);
  and and_56 (and_56_out, or_23_out, xor_24_out);
  xor xor_57 (_32BIT_RESULT[24], xor_25_out, or_24_out);
  and and_57 (and_57_out, or_24_out, xor_25_out);
  xor xor_58 (_32BIT_RESULT[25], xor_26_out, or_25_out);
  and and_58 (and_58_out, or_25_out, xor_26_out);
  xor xor_59 (_32BIT_RESULT[26], xor_27_out, or_26_out);
  and and_59 (and_59_out, or_26_out, xor_27_out);
  xor xor_60 (_32BIT_RESULT[27], xor_28_out, or_27_out);
  and and_60 (and_60_out, or_27_out, xor_28_out);
  xor xor_61 (_32BIT_RESULT[28], xor_29_out, or_28_out);
  and and_61 (and_61_out, or_28_out, xor_29_out);
  xor xor_62 (_32BIT_RESULT[29], xor_30_out, or_29_out);
  and and_62 (and_62_out, or_29_out, xor_30_out);
  xor xor_63 (_32BIT_RESULT[30], xor_31_out, or_30_out);
  and and_63 (and_63_out, or_30_out, xor_31_out);
  xor xor_64 (_32BIT_RESULT[31], xor_32_out, or_31_out);
  and and_64 (and_64_out, or_31_out, xor_32_out);
  // Pins of 1 and 32 bits meet at _32BIT_A_IN
  // Pins of 1 and 32 bits meet at _32BIT_B_IN
  // Pins of 1 and 32 bits meet at _32BIT_RESULT
endmodule
