// Digital circuit 32BIT ALU.dig as structural Verilog
module _32BIT_ALU (
);

  _32BIT_TWOSCOMPLEMENTER _32bit_twoscomplementer_1 ();  // open: _32BIT_IN, INVERT_ALL, PROPAGATE_ENABLE, _32BIT_OUT
endmodule
