// Digital circuit 32BIT REGISTER.dig as structural Verilog
module _32BIT_REGISTER (
  input  RESET,
  input  WRITE_ENABLE,
  input  [31:0] _32BIT_DATA_IN,
  output [31:0] _32BIT_STATE
);

  wire and_1_out, and_2_out, and_3_out, and_4_out, and_5_out, and_6_out, and_7_out, and_8_out, and_9_out,
       and_10_out, and_11_out, and_12_out, and_13_out, and_14_out, and_15_out, and_16_out, and_17_out,
       and_18_out, and_19_out, and_20_out, and_21_out, and_22_out, and_23_out, and_24_out, and_25_out,
       and_27_out, and_29_out, and_30_out, and_31_out, and_32_out, and_33_out, and_34_out;

  and and_1 (and_1_out, _32BIT_DATA_IN[0], WRITE_ENABLE);
  and and_2 (and_2_out, _32BIT_DATA_IN[1], WRITE_ENABLE);
  and and_3 (and_3_out, _32BIT_DATA_IN[2], WRITE_ENABLE);
  and and_4 (and_4_out, _32BIT_DATA_IN[3], WRITE_ENABLE);
  and and_5 (and_5_out, _32BIT_DATA_IN[4], WRITE_ENABLE);
  and and_6 (and_6_out, _32BIT_DATA_IN[5], WRITE_ENABLE);
  and and_7 (and_7_out, _32BIT_DATA_IN[6], WRITE_ENABLE);
  and and_8 (and_8_out, _32BIT_DATA_IN[7], WRITE_ENABLE);
  and and_9 (and_9_out, _32BIT_DATA_IN[8], WRITE_ENABLE);
  and and_10 (and_10_out, _32BIT_DATA_IN[9], WRITE_ENABLE);
  and and_11 (and_11_out, _32BIT_DATA_IN[10], WRITE_ENABLE);
  and and_12 (and_12_out, _32BIT_DATA_IN[11], WRITE_ENABLE);
  and and_13 (and_13_out, _32BIT_DATA_IN[12], WRITE_ENABLE);
  and and_14 (and_14_out, _32BIT_DATA_IN[13], WRITE_ENABLE);
  and and_15 (and_15_out, _32BIT_DATA_IN[14], WRITE_ENABLE);
  and and_16 (and_16_out, _32BIT_DATA_IN[15], WRITE_ENABLE);
  and and_17 (and_17_out, _32BIT_DATA_IN[16], WRITE_ENABLE);
  and and_18 (and_18_out, _32BIT_DATA_IN[17], WRITE_ENABLE);
  and and_19 (and_19_out, _32BIT_DATA_IN[18], WRITE_ENABLE);
  and and_20 (and_20_out, _32BIT_DATA_IN[19], WRITE_ENABLE);
  and and_21 (and_21_out, _32BIT_DATA_IN[20], WRITE_ENABLE);
  and and_22 (and_22_out, _32BIT_DATA_IN[21], WRITE_ENABLE);
  and and_23 (and_23_out, _32BIT_DATA_IN[22], WRITE_ENABLE);
  and and_24 (and_24_out, _32BIT_DATA_IN[23], WRITE_ENABLE);
  and and_25 (and_25_out, _32BIT_DATA_IN[24], WRITE_ENABLE);
  and and_26 (and_25_out, _32BIT_DATA_IN[24], WRITE_ENABLE);
  and and_27 (and_27_out, _32BIT_DATA_IN[25], WRITE_ENABLE);
  and and_28 (and_27_out, _32BIT_DATA_IN[25], WRITE_ENABLE);
  and and_29 (and_29_out, _32BIT_DATA_IN[26], WRITE_ENABLE);
  and and_30 (and_30_out, _32BIT_DATA_IN[27], WRITE_ENABLE);
  and and_31 (and_31_out, _32BIT_DATA_IN[28], WRITE_ENABLE);
  and and_32 (and_32_out, _32BIT_DATA_IN[29], WRITE_ENABLE);
  and and_33 (and_33_out, _32BIT_DATA_IN[30], WRITE_ENABLE);
  and and_34 (and_34_out, _32BIT_DATA_IN[31], WRITE_ENABLE);
  SRLATCH srlatch_1 (.SET(and_1_out), .RESET(RESET), .STATE(_32BIT_STATE[0]));
  SRLATCH srlatch_2 (.SET(and_2_out), .RESET(RESET), .STATE(_32BIT_STATE[1]));
  SRLATCH srlatch_3 (.SET(and_3_out), .RESET(RESET), .STATE(_32BIT_STATE[2]));
  SRLATCH srlatch_4 (.SET(and_4_out), .RESET(RESET), .STATE(_32BIT_STATE[3]));
  SRLATCH srlatch_5 (.SET(and_5_out), .RESET(RESET), .STATE(_32BIT_STATE[4]));
  SRLATCH srlatch_6 (.SET(and_5_out), .RESET(RESET), .STATE(_32BIT_STATE[4]));
  SRLATCH srlatch_7 (.SET(and_6_out), .RESET(RESET), .STATE(_32BIT_STATE[5]));
  SRLATCH srlatch_8 (.SET(and_6_out), .RESET(RESET), .STATE(_32BIT_STATE[5]));
  SRLATCH srlatch_9 (.SET(and_7_out), .RESET(RESET), .STATE(_32BIT_STATE[6]));
  SRLATCH srlatch_10 (.SET(and_8_out), .RESET(RESET), .STATE(_32BIT_STATE[7]));
  SRLATCH srlatch_11 (.SET(and_8_out), .RESET(RESET), .STATE(_32BIT_STATE[7]));
  SRLATCH srlatch_12 (.SET(and_8_out), .RESET(RESET), .STATE(_32BIT_STATE[7]));
  SRLATCH srlatch_13 (.SET(and_9_out), .RESET(RESET), .STATE(_32BIT_STATE[8]));
  SRLATCH srlatch_14 (.SET(and_9_out), .RESET(RESET), .STATE(_32BIT_STATE[8]));
  SRLATCH srlatch_15 (.SET(and_9_out), .RESET(RESET), .STATE(_32BIT_STATE[8]));
  SRLATCH srlatch_16 (.SET(and_10_out), .RESET(RESET), .STATE(_32BIT_STATE[9]));
  SRLATCH srlatch_17 (.SET(and_10_out), .RESET(RESET), .STATE(_32BIT_STATE[9]));
  SRLATCH srlatch_18 (.SET(and_11_out), .RESET(RESET), .STATE(_32BIT_STATE[10]));
  SRLATCH srlatch_19 (.SET(and_11_out), .RESET(RESET), .STATE(_32BIT_STATE[10]));
  SRLATCH srlatch_20 (.SET(and_12_out), .RESET(RESET), .STATE(_32BIT_STATE[11]));
  SRLATCH srlatch_21 (.SET(and_12_out), .RESET(RESET), .STATE(_32BIT_STATE[11]));
  SRLATCH srlatch_22 (.SET(and_13_out), .RESET(RESET), .STATE(_32BIT_STATE[12]));
  SRLATCH srlatch_23 (.SET(and_13_out), .RESET(RESET), .STATE(_32BIT_STATE[12]));
  SRLATCH srlatch_24 (.SET(and_13_out), .RESET(RESET), .STATE(_32BIT_STATE[12]));
  SRLATCH srlatch_25 (.SET(and_14_out), .RESET(RESET), .STATE(_32BIT_STATE[13]));
  SRLATCH srlatch_26 (.SET(and_14_out), .RESET(RESET), .STATE(_32BIT_STATE[13]));
  SRLATCH srlatch_27 (.SET(and_14_out), .RESET(RESET), .STATE(_32BIT_STATE[13]));
  SRLATCH srlatch_28 (.SET(and_15_out), .RESET(RESET), .STATE(_32BIT_STATE[14]));
  SRLATCH srlatch_29 (.SET(and_15_out), .RESET(RESET), .STATE(_32BIT_STATE[14]));
  SRLATCH srlatch_30 (.SET(and_16_out), .RESET(RESET), .STATE(_32BIT_STATE[15]));
  SRLATCH srlatch_31 (.SET(and_16_out), .RESET(RESET), .STATE(_32BIT_STATE[15]));
  SRLATCH srlatch_32 (.SET(and_16_out), .RESET(RESET), .STATE(_32BIT_STATE[15]));
  SRLATCH srlatch_33 (.SET(and_16_out), .RESET(RESET), .STATE(_32BIT_STATE[15]));
  SRLATCH srlatch_34 (.SET(and_17_out), .RESET(RESET), .STATE(_32BIT_STATE[16]));
  SRLATCH srlatch_35 (.SET(and_17_out), .RESET(RESET), .STATE(_32BIT_STATE[16]));
  SRLATCH srlatch_36 (.SET(and_17_out), .RESET(RESET), .STATE(_32BIT_STATE[16]));
  SRLATCH srlatch_37 (.SET(and_17_out), .RESET(RESET), .STATE(_32BIT_STATE[16]));
  SRLATCH srlatch_38 (.SET(and_18_out), .RESET(RESET), .STATE(_32BIT_STATE[17]));
  SRLATCH srlatch_39 (.SET(and_18_out), .RESET(RESET), .STATE(_32BIT_STATE[17]));
  SRLATCH srlatch_40 (.SET(and_18_out), .RESET(RESET), .STATE(_32BIT_STATE[17]));
  SRLATCH srlatch_41 (.SET(and_19_out), .RESET(RESET), .STATE(_32BIT_STATE[18]));
  SRLATCH srlatch_42 (.SET(and_19_out), .RESET(RESET), .STATE(_32BIT_STATE[18]));
  SRLATCH srlatch_43 (.SET(and_19_out), .RESET(RESET), .STATE(_32BIT_STATE[18]));
  SRLATCH srlatch_44 (.SET(and_20_out), .RESET(RESET), .STATE(_32BIT_STATE[19]));
  SRLATCH srlatch_45 (.SET(and_20_out), .RESET(RESET), .STATE(_32BIT_STATE[19]));
  SRLATCH srlatch_46 (.SET(and_20_out), .RESET(RESET), .STATE(_32BIT_STATE[19]));
  SRLATCH srlatch_47 (.SET(and_21_out), .RESET(RESET), .STATE(_32BIT_STATE[20]));
  SRLATCH srlatch_48 (.SET(and_21_out), .RESET(RESET), .STATE(_32BIT_STATE[20]));
  SRLATCH srlatch_49 (.SET(and_21_out), .RESET(RESET), .STATE(_32BIT_STATE[20]));
  SRLATCH srlatch_50 (.SET(and_21_out), .RESET(RESET), .STATE(_32BIT_STATE[20]));
  SRLATCH srlatch_51 (.SET(and_22_out), .RESET(RESET), .STATE(_32BIT_STATE[21]));
  SRLATCH srlatch_52 (.SET(and_22_out), .RESET(RESET), .STATE(_32BIT_STATE[21]));
  SRLATCH srlatch_53 (.SET(and_22_out), .RESET(RESET), .STATE(_32BIT_STATE[21]));
  SRLATCH srlatch_54 (.SET(and_22_out), .RESET(RESET), .STATE(_32BIT_STATE[21]));
  SRLATCH srlatch_55 (.SET(and_23_out), .RESET(RESET), .STATE(_32BIT_STATE[22]));
  SRLATCH srlatch_56 (.SET(and_23_out), .RESET(RESET), .STATE(_32BIT_STATE[22]));
  SRLATCH srlatch_57 (.SET(and_23_out), .RESET(RESET), .STATE(_32BIT_STATE[22]));
  SRLATCH srlatch_58 (.SET(and_24_out), .RESET(RESET), .STATE(_32BIT_STATE[23]));
  SRLATCH srlatch_59 (.SET(and_24_out), .RESET(RESET), .STATE(_32BIT_STATE[23]));
  SRLATCH srlatch_60 (.SET(and_24_out), .RESET(RESET), .STATE(_32BIT_STATE[23]));
  SRLATCH srlatch_61 (.SET(and_24_out), .RESET(RESET), .STATE(_32BIT_STATE[23]));
  SRLATCH srlatch_62 (.SET(and_24_out), .RESET(RESET), .STATE(_32BIT_STATE[23]));
  SRLATCH srlatch_63 (.SET(and_25_out), .RESET(RESET), .STATE(_32BIT_STATE[24]));
  SRLATCH srlatch_64 (.SET(and_25_out), .RESET(RESET), .STATE(_32BIT_STATE[24]));
  SRLATCH srlatch_65 (.SET(and_25_out), .RESET(RESET), .STATE(_32BIT_STATE[24]));
  SRLATCH srlatch_66 (.SET(and_25_out), .RESET(RESET), .STATE(_32BIT_STATE[24]));
  SRLATCH srlatch_67 (.SET(and_25_out), .RESET(RESET), .STATE(_32BIT_STATE[24]));
  SRLATCH srlatch_68 (.SET(and_25_out), .RESET(RESET), .STATE(_32BIT_STATE[24]));
  SRLATCH srlatch_69 (.SET(and_25_out), .RESET(RESET), .STATE(_32BIT_STATE[24]));
  SRLATCH srlatch_70 (.SET(and_27_out), .RESET(RESET), .STATE(_32BIT_STATE[25]));
  SRLATCH srlatch_71 (.SET(and_27_out), .RESET(RESET), .STATE(_32BIT_STATE[25]));
  SRLATCH srlatch_72 (.SET(and_27_out), .RESET(RESET), .STATE(_32BIT_STATE[25]));
  SRLATCH srlatch_73 (.SET(and_27_out), .RESET(RESET), .STATE(_32BIT_STATE[25]));
  SRLATCH srlatch_74 (.SET(and_27_out), .RESET(RESET), .STATE(_32BIT_STATE[25]));
  SRLATCH srlatch_75 (.SET(and_27_out), .RESET(RESET), .STATE(_32BIT_STATE[25]));
  SRLATCH srlatch_76 (.SET(and_29_out), .RESET(RESET), .STATE(_32BIT_STATE[26]));
  SRLATCH srlatch_77 (.SET(and_29_out), .RESET(RESET), .STATE(_32BIT_STATE[26]));
  SRLATCH srlatch_78 (.SET(and_29_out), .RESET(RESET), .STATE(_32BIT_STATE[26]));
  SRLATCH srlatch_79 (.SET(and_29_out), .RESET(RESET), .STATE(_32BIT_STATE[26]));
  SRLATCH srlatch_80 (.SET(and_30_out), .RESET(RESET), .STATE(_32BIT_STATE[27]));
  SRLATCH srlatch_81 (.SET(and_30_out), .RESET(RESET), .STATE(_32BIT_STATE[27]));
  SRLATCH srlatch_82 (.SET(and_30_out), .RESET(RESET), .STATE(_32BIT_STATE[27]));
  SRLATCH srlatch_83 (.SET(and_30_out), .RESET(RESET), .STATE(_32BIT_STATE[27]));
  SRLATCH srlatch_84 (.SET(and_31_out), .RESET(RESET), .STATE(_32BIT_STATE[28]));
  SRLATCH srlatch_85 (.SET(and_31_out), .RESET(RESET), .STATE(_32BIT_STATE[28]));
  SRLATCH srlatch_86 (.SET(and_31_out), .RESET(RESET), .STATE(_32BIT_STATE[28]));
  SRLATCH srlatch_87 (.SET(and_32_out), .RESET(RESET), .STATE(_32BIT_STATE[29]));
  SRLATCH srlatch_88 (.SET(and_32_out), .RESET(RESET), .STATE(_32BIT_STATE[29]));
  SRLATCH srlatch_89 (.SET(and_32_out), .RESET(RESET), .STATE(_32BIT_STATE[29]));
  SRLATCH srlatch_90 (.SET(and_32_out), .RESET(RESET), .STATE(_32BIT_STATE[29]));
  SRLATCH srlatch_91 (.SET(and_32_out), .RESET(RESET), .STATE(_32BIT_STATE[29]));
  SRLATCH srlatch_92 (.SET(and_33_out), .RESET(RESET), .STATE(_32BIT_STATE[30]));
  SRLATCH srlatch_93 (.SET(and_33_out), .RESET(RESET), .STATE(_32BIT_STATE[30]));
  SRLATCH srlatch_94 (.SET(and_33_out), .RESET(RESET), .STATE(_32BIT_STATE[30]));
  SRLATCH srlatch_95 (.SET(and_33_out), .RESET(RESET), .STATE(_32BIT_STATE[30]));
  SRLATCH srlatch_96 (.SET(and_33_out), .RESET(RESET), .STATE(_32BIT_STATE[30]));
  SRLATCH srlatch_97 (.SET(and_34_out), .RESET(RESET), .STATE(_32BIT_STATE[31]));
  SRLATCH srlatch_98 (.SET(and_34_out), .RESET(RESET), .STATE(_32BIT_STATE[31]));
  SRLATCH srlatch_99 (.SET(and_34_out), .RESET(RESET), .STATE(_32BIT_STATE[31]));
  SRLATCH srlatch_100 (.SET(and_34_out), .RESET(RESET), .STATE(_32BIT_STATE[31]));
endmodule
