// Digital circuit 32BIT TOGGLE XOR.dig as structural Verilog
module _32BIT_TOGGLE_XOR (
  input  [31:0] _32BIT_IN,
  input  XOR,
  output [31:0] _32BIT_OUT
);

  xor xor_1 (_32BIT_OUT[0], XOR, _32BIT_IN[0]);
  xor xor_2 (_32BIT_OUT[1], XOR, _32BIT_IN[1]);
  xor xor_3 (_32BIT_OUT[2], XOR, _32BIT_IN[2]);
  xor xor_4 (_32BIT_OUT[3], XOR, _32BIT_IN[3]);
  xor xor_5 (_32BIT_OUT[4], XOR, _32BIT_IN[4]);
  xor xor_6 (_32BIT_OUT[5], XOR, _32BIT_IN[5]);
  xor xor_7 (_32BIT_OUT[6], XOR, _32BIT_IN[6]);
  xor xor_8 (_32BIT_OUT[7], XOR, _32BIT_IN[7]);
  xor xor_9 (_32BIT_OUT[8], XOR, _32BIT_IN[8]);
  xor xor_10 (_32BIT_OUT[9], XOR, _32BIT_IN[9]);
  xor xor_11 (_32BIT_OUT[10], XOR, _32BIT_IN[10]);
  xor xor_12 (_32BIT_OUT[11], XOR, _32BIT_IN[11]);
  xor xor_13 (_32BIT_OUT[12], XOR, _32BIT_IN[12]);
  xor xor_14 (_32BIT_OUT[13], XOR, _32BIT_IN[13]);
  xor xor_15 (_32BIT_OUT[14], XOR, _32BIT_IN[14]);
  xor xor_16 (_32BIT_OUT[15], XOR, _32BIT_IN[15]);
  xor xor_17 (_32BIT_OUT[16], XOR, _32BIT_IN[16]);
  xor xor_18 (_32BIT_OUT[17], XOR, _32BIT_IN[17]);
  xor xor_19 (_32BIT_OUT[18], XOR, _32BIT_IN[18]);
  xor xor_20 (_32BIT_OUT[19], XOR, _32BIT_IN[19]);
  xor xor_21 (_32BIT_OUT[20], XOR, _32BIT_IN[20]);
  xor xor_22 (_32BIT_OUT[21], XOR, _32BIT_IN[21]);
  xor xor_23 (_32BIT_OUT[22], XOR, _32BIT_IN[22]);
  xor xor_24 (_32BIT_OUT[23], XOR, _32BIT_IN[23]);
  xor xor_25 (_32BIT_OUT[24], XOR, _32BIT_IN[24]);
  xor xor_26 (_32BIT_OUT[25], XOR, _32BIT_IN[25]);
  xor xor_27 (_32BIT_OUT[26], XOR, _32BIT_IN[26]);
  xor xor_28 (_32BIT_OUT[27], XOR, _32BIT_IN[27]);
  xor xor_29 (_32BIT_OUT[28], XOR, _32BIT_IN[28]);
  xor xor_30 (_32BIT_OUT[29], XOR, _32BIT_IN[29]);
  xor xor_31 (_32BIT_OUT[30], XOR, _32BIT_IN[30]);
  xor xor_32 (_32BIT_OUT[31], XOR, _32BIT_IN[31]);
endmodule
