// Digital circuit 32BIT TWOSCOMPLEMENTER.dig as structural Verilog
module _32BIT_TWOSCOMPLEMENTER (
  input  [31:0] _32BIT_IN,
  input  INVERT_ALL,
  input  PROPAGATE_ENABLE,
  output [31:0] _32BIT_OUT
);

  wire and_1_out, and_2_out, and_3_out, and_4_out, and_5_out, and_6_out, and_7_out, and_8_out, and_9_out,
       and_10_out, and_11_out, and_12_out, and_13_out, and_14_out, and_15_out, and_16_out, and_17_out,
       and_18_out, and_19_out, and_20_out, and_21_out, and_22_out, and_23_out, and_24_out, and_25_out,
       and_26_out, and_27_out, and_28_out, and_29_out, and_30_out, or_1_out, or_2_out, or_3_out, or_4_out,
       or_5_out, or_6_out, or_7_out, or_8_out, or_9_out, or_10_out, or_11_out, or_12_out, or_13_out,
       or_14_out, or_15_out, or_16_out, or_17_out, or_18_out, or_19_out, or_20_out, or_21_out, or_22_out,
       or_23_out, or_24_out, or_25_out, or_26_out, or_27_out, or_28_out, or_29_out, or_30_out, or_31_out;

  or or_1 (or_1_out, and_1_out, INVERT_ALL);
  or or_2 (or_2_out, and_2_out, or_1_out);
  or or_3 (or_3_out, and_3_out, or_2_out);
  or or_4 (or_4_out, and_4_out, or_3_out);
  or or_5 (or_5_out, and_5_out, or_4_out);
  or or_6 (or_6_out, and_6_out, or_5_out);
  or or_7 (or_7_out, and_7_out, or_6_out);
  or or_8 (or_8_out, and_8_out, or_7_out);
  or or_9 (or_9_out, and_9_out, or_8_out);
  or or_10 (or_10_out, and_10_out, or_9_out);
  or or_11 (or_11_out, and_11_out, or_10_out);
  or or_12 (or_12_out, and_12_out, or_11_out);
  or or_13 (or_13_out, and_13_out, or_12_out);
  or or_14 (or_14_out, and_14_out, or_13_out);
  or or_15 (or_15_out, and_15_out, or_14_out);
  or or_16 (or_16_out, and_16_out, or_15_out);
  or or_17 (or_17_out, and_17_out, or_16_out);
  or or_18 (or_18_out, and_18_out, or_17_out);
  or or_19 (or_19_out, and_19_out, or_18_out);
  or or_20 (or_20_out, and_20_out, or_19_out);
  or or_21 (or_21_out, and_21_out, or_20_out);
  or or_22 (or_22_out, and_22_out, or_21_out);
  or or_23 (or_23_out, and_23_out, or_22_out);
  or or_24 (or_24_out, and_24_out, or_23_out);
  or or_25 (or_25_out, and_25_out, or_24_out);
  or or_26 (or_26_out, and_26_out, or_25_out);
  or or_27 (or_27_out, and_27_out, or_26_out);
  or or_28 (or_28_out, and_28_out, or_27_out);
  or or_29 (or_29_out, and_29_out, or_28_out);
  or or_30 (or_30_out, and_30_out, or_29_out);
  or or_31 (or_31_out, PROPAGATE_ENABLE, or_30_out);
  xor xor_1 (_32BIT_OUT[0], INVERT_ALL, _32BIT_IN[0]);
  xor xor_2 (_32BIT_OUT[1], or_1_out, _32BIT_IN[1]);
  xor xor_3 (_32BIT_OUT[2], or_2_out, _32BIT_IN[2]);
  xor xor_4 (_32BIT_OUT[3], or_3_out, _32BIT_IN[3]);
  xor xor_5 (_32BIT_OUT[4], or_4_out, _32BIT_IN[4]);
  xor xor_6 (_32BIT_OUT[5], or_5_out, _32BIT_IN[5]);
  xor xor_7 (_32BIT_OUT[6], or_6_out, _32BIT_IN[6]);
  xor xor_8 (_32BIT_OUT[7], or_7_out, _32BIT_IN[7]);
  xor xor_9 (_32BIT_OUT[8], or_8_out, _32BIT_IN[8]);
  xor xor_10 (_32BIT_OUT[9], or_9_out, _32BIT_IN[9]);
  xor xor_11 (_32BIT_OUT[10], or_10_out, _32BIT_IN[10]);
  xor xor_12 (_32BIT_OUT[11], or_11_out, _32BIT_IN[11]);
  xor xor_13 (_32BIT_OUT[12], or_12_out, _32BIT_IN[12]);
  xor xor_14 (_32BIT_OUT[13], or_13_out, _32BIT_IN[13]);
  xor xor_15 (_32BIT_OUT[14], or_14_out, _32BIT_IN[14]);
  xor xor_16 (_32BIT_OUT[15], or_15_out, _32BIT_IN[15]);
  xor xor_17 (_32BIT_OUT[16], or_16_out, _32BIT_IN[16]);
  xor xor_18 (_32BIT_OUT[17], or_17_out, _32BIT_IN[17]);
  xor xor_19 (_32BIT_OUT[18], or_18_out, _32BIT_IN[18]);
  xor xor_20 (_32BIT_OUT[19], or_19_out, _32BIT_IN[19]);
  xor xor_21 (_32BIT_OUT[20], or_20_out, _32BIT_IN[20]);
  xor xor_22 (_32BIT_OUT[21], or_21_out, _32BIT_IN[21]);
  xor xor_23 (_32BIT_OUT[22], or_22_out, _32BIT_IN[22]);
  xor xor_24 (_32BIT_OUT[23], or_23_out, _32BIT_IN[23]);
  xor xor_25 (_32BIT_OUT[24], or_24_out, _32BIT_IN[24]);
  xor xor_26 (_32BIT_OUT[25], or_25_out, _32BIT_IN[25]);
  xor xor_27 (_32BIT_OUT[26], or_26_out, _32BIT_IN[26]);
  xor xor_28 (_32BIT_OUT[27], or_27_out, _32BIT_IN[27]);
  xor xor_29 (_32BIT_OUT[28], or_28_out, _32BIT_IN[28]);
  xor xor_30 (_32BIT_OUT[29], or_29_out, _32BIT_IN[29]);
  xor xor_31 (_32BIT_OUT[30], or_30_out, _32BIT_IN[30]);
  xor xor_32 (_32BIT_OUT[31], or_31_out, _32BIT_IN[31]);
  and and_1 (and_1_out, _32BIT_OUT[0], PROPAGATE_ENABLE);
  and and_2 (and_2_out, _32BIT_OUT[1], PROPAGATE_ENABLE);
  and and_3 (and_3_out, _32BIT_OUT[2], PROPAGATE_ENABLE);
  and and_4 (and_4_out, _32BIT_OUT[3], PROPAGATE_ENABLE);
  and and_5 (and_5_out, _32BIT_OUT[4], PROPAGATE_ENABLE);
  and and_6 (and_6_out, _32BIT_OUT[5], PROPAGATE_ENABLE);
  and and_7 (and_7_out, _32BIT_OUT[6], PROPAGATE_ENABLE);
  and and_8 (and_8_out, _32BIT_OUT[7], PROPAGATE_ENABLE);
  and and_9 (and_9_out, _32BIT_OUT[8], PROPAGATE_ENABLE);
  and and_10 (and_10_out, _32BIT_OUT[9], PROPAGATE_ENABLE);
  and and_11 (and_11_out, _32BIT_OUT[10], PROPAGATE_ENABLE);
  and and_12 (and_12_out, _32BIT_OUT[11], PROPAGATE_ENABLE);
  and and_13 (and_13_out, _32BIT_OUT[12], PROPAGATE_ENABLE);
  and and_14 (and_14_out, _32BIT_OUT[13], PROPAGATE_ENABLE);
  and and_15 (and_15_out, _32BIT_OUT[14], PROPAGATE_ENABLE);
  and and_16 (and_16_out, _32BIT_OUT[15], PROPAGATE_ENABLE);
  and and_17 (and_17_out, _32BIT_OUT[16], PROPAGATE_ENABLE);
  and and_18 (and_18_out, _32BIT_OUT[17], PROPAGATE_ENABLE);
  and and_19 (and_19_out, _32BIT_OUT[18], PROPAGATE_ENABLE);
  and and_20 (and_20_out, _32BIT_OUT[19], PROPAGATE_ENABLE);
  and and_21 (and_21_out, _32BIT_OUT[20], PROPAGATE_ENABLE);
  and and_22 (and_22_out, _32BIT_OUT[21], PROPAGATE_ENABLE);
  and and_23 (and_23_out, _32BIT_OUT[22], PROPAGATE_ENABLE);
  and and_24 (and_24_out, _32BIT_OUT[23], PROPAGATE_ENABLE);
  and and_25 (and_25_out, _32BIT_OUT[24], PROPAGATE_ENABLE);
  and and_26 (and_26_out, _32BIT_OUT[25], PROPAGATE_ENABLE);
  and and_27 (and_27_out, _32BIT_OUT[26], PROPAGATE_ENABLE);
  and and_28 (and_28_out, _32BIT_OUT[27], PROPAGATE_ENABLE);
  and and_29 (and_29_out, _32BIT_OUT[28], PROPAGATE_ENABLE);
  and and_30 (and_30_out, _32BIT_OUT[29], PROPAGATE_ENABLE);
  and and_31 (PROPAGATE_ENABLE, _32BIT_OUT[30], PROPAGATE_ENABLE);
endmodule
