// Digital circuit SRLATCH.dig as structural Verilog
module SRLATCH (
  input  SET,
  input  RESET,
  output STATE
);

  wire or_1_out;

  or or_1 (or_1_out, SET, STATE);
  and and_1 (STATE, or_1_out, ~RESET);  // And
endmodule
