// Logisim project branck.circ as structural Verilog
module Bit16_Add (
  input  Carry_In,
  input  [15:0] Bit16_A,
  input  [15:0] Bit16_B,
  output [15:0] Bit16_Result,
  output Carry_Out
);

  wire and_1_out, and_2_out, and_3_out, and_4_out, and_5_out, and_6_out, and_7_out, and_8_out, and_9_out,
       and_10_out, and_11_out, and_12_out, and_13_out, and_14_out, and_15_out, and_16_out,
       bit4_cla_logic_1_c2, bit4_cla_logic_1_c3, bit4_cla_logic_1_c4, bit4_cla_logic_1_cout,
       bit4_cla_logic_1_pg, bit4_cla_logic_2_c2, bit4_cla_logic_2_c3, bit4_cla_logic_2_c4,
       bit4_cla_logic_2_cout, bit4_cla_logic_2_pg, bit4_cla_logic_3_c2, bit4_cla_logic_3_c3,
       bit4_cla_logic_3_c4, bit4_cla_logic_3_cout, bit4_cla_logic_3_pg, bit4_cla_logic_4_c2,
       bit4_cla_logic_4_c3, bit4_cla_logic_4_c4, bit4_cla_logic_4_cout, bit4_cla_logic_4_pg,
       bit4_cla_logic_5_c2, bit4_cla_logic_5_c3, bit4_cla_logic_5_c4, xor_1_out, xor_2_out, xor_3_out,
       xor_4_out, xor_5_out, xor_6_out, xor_7_out, xor_8_out, xor_9_out, xor_10_out, xor_11_out, xor_12_out,
       xor_13_out, xor_14_out, xor_15_out, xor_16_out;

  xor xor_1 (xor_1_out, Bit16_A[0], Bit16_B[0]);
  and and_1 (and_1_out, Bit16_B[0], Bit16_A[0]);
  xor xor_2 (xor_2_out, Bit16_A[1], Bit16_B[1]);
  and and_2 (and_2_out, Bit16_B[1], Bit16_A[1]);
  xor xor_3 (xor_3_out, Bit16_A[2], Bit16_B[2]);
  and and_3 (and_3_out, Bit16_B[2], Bit16_A[2]);
  xor xor_4 (xor_4_out, Bit16_A[3], Bit16_B[3]);
  and and_4 (and_4_out, Bit16_B[3], Bit16_A[3]);
  xor xor_5 (xor_5_out, Bit16_A[4], Bit16_B[4]);
  and and_5 (and_5_out, Bit16_B[4], Bit16_A[4]);
  xor xor_6 (xor_6_out, Bit16_A[5], Bit16_B[5]);
  and and_6 (and_6_out, Bit16_B[5], Bit16_A[5]);
  xor xor_7 (xor_7_out, Bit16_A[6], Bit16_B[6]);
  and and_7 (and_7_out, Bit16_B[6], Bit16_A[6]);
  xor xor_8 (xor_8_out, Bit16_A[7], Bit16_B[7]);
  and and_8 (and_8_out, Bit16_B[7], Bit16_A[7]);
  xor xor_9 (xor_9_out, Bit16_A[8], Bit16_B[8]);
  and and_9 (and_9_out, Bit16_B[8], Bit16_A[8]);
  xor xor_10 (xor_10_out, Bit16_A[9], Bit16_B[9]);
  and and_10 (and_10_out, Bit16_B[9], Bit16_A[9]);
  xor xor_11 (xor_11_out, Bit16_A[10], Bit16_B[10]);
  and and_11 (and_11_out, Bit16_B[10], Bit16_A[10]);
  xor xor_12 (xor_12_out, Bit16_A[11], Bit16_B[11]);
  and and_12 (and_12_out, Bit16_B[11], Bit16_A[11]);
  xor xor_13 (xor_13_out, Bit16_A[12], Bit16_B[12]);
  and and_13 (and_13_out, Bit16_B[12], Bit16_A[12]);
  xor xor_14 (xor_14_out, Bit16_A[13], Bit16_B[13]);
  and and_14 (and_14_out, Bit16_B[13], Bit16_A[13]);
  xor xor_15 (xor_15_out, Bit16_A[14], Bit16_B[14]);
  and and_15 (and_15_out, Bit16_B[14], Bit16_A[14]);
  xor xor_16 (xor_16_out, Bit16_A[15], Bit16_B[15]);
  and and_16 (and_16_out, Bit16_B[15], Bit16_A[15]);
  xor xor_17 (Bit16_Result[0], Carry_In, xor_1_out);
  xor xor_18 (Bit16_Result[1], bit4_cla_logic_1_c2, xor_2_out);
  xor xor_19 (Bit16_Result[2], bit4_cla_logic_1_c3, xor_3_out);
  xor xor_20 (Bit16_Result[3], bit4_cla_logic_1_c4, xor_4_out);
  xor xor_21 (Bit16_Result[4], bit4_cla_logic_5_c2, xor_5_out);
  xor xor_22 (Bit16_Result[5], bit4_cla_logic_2_c2, xor_6_out);
  xor xor_23 (Bit16_Result[6], bit4_cla_logic_2_c3, xor_7_out);
  xor xor_24 (Bit16_Result[7], bit4_cla_logic_2_c4, xor_8_out);
  xor xor_25 (Bit16_Result[8], bit4_cla_logic_5_c3, xor_9_out);
  xor xor_26 (Bit16_Result[9], bit4_cla_logic_3_c2, xor_10_out);
  xor xor_27 (Bit16_Result[10], bit4_cla_logic_3_c3, xor_11_out);
  xor xor_28 (Bit16_Result[11], bit4_cla_logic_3_c4, xor_12_out);
  xor xor_29 (Bit16_Result[12], bit4_cla_logic_5_c4, xor_13_out);
  xor xor_30 (Bit16_Result[13], bit4_cla_logic_4_c2, xor_14_out);
  xor xor_31 (Bit16_Result[14], bit4_cla_logic_4_c3, xor_15_out);
  xor xor_32 (Bit16_Result[15], bit4_cla_logic_4_c4, xor_16_out);
  Bit4_CLA_Logic bit4_cla_logic_1 (
    .Cin(Carry_In), .P1(xor_1_out), .G1(and_1_out), .P2(xor_2_out), .G2(and_2_out), .P3(xor_3_out),
    .G3(and_3_out), .P4(xor_4_out), .G4(and_4_out), .C2(bit4_cla_logic_1_c2), .C3(bit4_cla_logic_1_c3),
    .C4(bit4_cla_logic_1_c4), .COUT(bit4_cla_logic_1_cout), .PG(bit4_cla_logic_1_pg));
  Bit4_CLA_Logic bit4_cla_logic_2 (
    .Cin(bit4_cla_logic_5_c2), .P1(xor_5_out), .G1(and_5_out), .P2(xor_6_out), .G2(and_6_out),
    .P3(xor_7_out), .G3(and_7_out), .P4(xor_8_out), .G4(and_8_out), .C2(bit4_cla_logic_2_c2),
    .C3(bit4_cla_logic_2_c3), .C4(bit4_cla_logic_2_c4), .COUT(bit4_cla_logic_2_cout), .PG(bit4_cla_logic_2_pg));
  Bit4_CLA_Logic bit4_cla_logic_3 (
    .Cin(bit4_cla_logic_5_c3), .P1(xor_9_out), .G1(and_9_out), .P2(xor_10_out), .G2(and_10_out),
    .P3(xor_11_out), .G3(and_11_out), .P4(xor_12_out), .G4(and_12_out), .C2(bit4_cla_logic_3_c2),
    .C3(bit4_cla_logic_3_c3), .C4(bit4_cla_logic_3_c4), .COUT(bit4_cla_logic_3_cout), .PG(bit4_cla_logic_3_pg));
  Bit4_CLA_Logic bit4_cla_logic_4 (
    .Cin(bit4_cla_logic_5_c4), .P1(xor_13_out), .G1(and_13_out), .P2(xor_14_out), .G2(and_14_out),
    .P3(xor_15_out), .G3(and_15_out), .P4(xor_16_out), .G4(and_16_out), .C2(bit4_cla_logic_4_c2),
    .C3(bit4_cla_logic_4_c3), .C4(bit4_cla_logic_4_c4), .COUT(bit4_cla_logic_4_cout), .PG(bit4_cla_logic_4_pg));
  Bit4_CLA_Logic bit4_cla_logic_5 (
    .Cin(Carry_In), .P1(bit4_cla_logic_1_pg), .G1(bit4_cla_logic_1_cout), .P2(bit4_cla_logic_2_pg),
    .G2(bit4_cla_logic_2_cout), .P3(bit4_cla_logic_3_pg), .G3(bit4_cla_logic_3_cout),
    .P4(bit4_cla_logic_4_pg), .G4(bit4_cla_logic_4_cout), .C2(bit4_cla_logic_5_c2), .C3(bit4_cla_logic_5_c3),
    .C4(bit4_cla_logic_5_c4), .COUT(Carry_Out));  // open: PG
endmodule

module Bit16_ALU (
  input  in_1,
  input  in_2,
  input  Clock,
  input  [4:0] Bit5_Opcode,
  input  Signed_Integer_Operation,
  input  [15:0] Bit16_A,
  input  [15:0] Bit16_B,
  input  in_8,
  input  fpop,
  input  [3:0] PLACEHOLDER,
  input  [15:0] PLACEHOLDER2,
  input  in_12,
  input  [15:0] in_13,
  input  [15:0] in_14,
  input  in_15,
  input  [23:0] in_16,
  input  [23:0] in_17,
  input  in_18,
  input  in_19,
  output CPU_WAIT_FOR_ALU_OP,
  output Carry,
  output Borrow,
  output Negative,
  output Overflow,
  output Zero,
  output [15:0] out_26,
  output out_27,
  output [23:0] out_28,
  output [23:0] out_29
);

  wire and_1_out, and_2_out, and_3_out, and_4_out, and_5_out, and_6_out, and_7_out, and_8_out, and_9_out,
       and_10_out, and_11_out, and_12_out, and_13_out, and_14_out, and_15_out, and_16_out, and_17_out,
       and_18_out, and_19_out, and_20_out, and_21_out, and_22_out, and_23_out, and_24_out, and_25_out,
       and_26_out, and_27_out, and_28_out, and_29_out, and_30_out, and_31_out, and_32_out, and_33_out,
       and_34_out, bit5_adder_1_cout, bit24_adder_1_bit16_c_out, bit24_adder_1_c_out,
       bit24_adder_2_bit16_c_out, bit24_adder_2_c_out, d_ff_2_qn, d_ff_3_qn, d_ff_4_qn, d_ff_5_qn, d_ff_6_qn,
       demultiplexer_1_out1, demultiplexer_1_out2, demultiplexer_1_out4, demultiplexer_1_out11,
       demultiplexer_2_out0, demultiplexer_2_out1, demultiplexer_2_out2, demultiplexer_2_out3,
       demultiplexer_2_out4, demultiplexer_2_out5, demultiplexer_2_out6, demultiplexer_2_out7,
       demultiplexer_2_out8, demultiplexer_2_out9, demultiplexer_2_out10, demultiplexer_2_out11,
       demultiplexer_2_out12, demultiplexer_2_out13, demultiplexer_2_out14, demultiplexer_2_out15,
       demultiplexer_2_out16, demultiplexer_2_out17, demultiplexer_2_out18, demultiplexer_2_out19,
       demultiplexer_2_out20, demultiplexer_2_out21, demultiplexer_2_out22, demultiplexer_2_out23,
       demultiplexer_3_out0, demultiplexer_3_out1, demultiplexer_3_out2, demultiplexer_3_out3,
       demultiplexer_3_out4, demultiplexer_3_out5, demultiplexer_3_out6, demultiplexer_3_out7,
       demultiplexer_3_out8, demultiplexer_3_out9, demultiplexer_3_out10, demultiplexer_3_out11,
       demultiplexer_3_out12, demultiplexer_3_out13, demultiplexer_3_out14, demultiplexer_3_out15,
       demultiplexer_3_out16, demultiplexer_3_out17, demultiplexer_3_out18, demultiplexer_3_out19,
       demultiplexer_3_out20, demultiplexer_3_out21, demultiplexer_3_out22, demultiplexer_3_out23, nor_1_out,
       not_1_out, not_2_out, not_3_out, not_4_out, not_5_out, not_6_out, not_7_out, not_8_out, or_1_out,
       or_2_out, or_3_out, or_4_out, or_8_out, or_13_out;
  wire [0:0] or_14_out;
  wire [3:0] bit4_controlled_buffer_1_bit4_out, bit4_controlled_buffer_2_bit4_out,
       bit4_twos_complementer_1_bit4_result, bit5_adder_1_bit5_result, or_6_out;
  wire [4:0] bit5_twos_complementer_1_bit5_result, d_ff_6_q;
  wire [4:4] bit5_adder_1_bit5_result_2;
  wire [14:0] undriven_2;
  wire [15:0] bit16_controlled_buffer_1_bit16_out, bit16_controlled_buffer_2_bit16_out,
       bit16_multiplier_1_p1, bit16_multiplier_1_p2, or_5_out, twos_complementer_1_bit16_result,
       twos_complementer_2_bit16_result;
  wire [15:10] undriven;
  wire [23:0] bit16_to_bit24_1_bit24, bit16_to_bit24_2_bit24, bit16_to_bit24_3_bit24, bit16_to_bit24_4_bit24,
       bit16t24_right_shift_1_bit24_result, bit24_adder_1_bit24_result, bit24_adder_2_bit24_result,
       bit24_controlled_buffer_1_bit24_out, bit24_controlled_buffer_2_bit24_out,
       bit24_controlled_buffer_3_bit24_out, bit24_controlled_buffer_4_bit24_out,
       bit24_controlled_buffer_5_bit24_out, bit24_controlled_buffer_6_bit24_out,
       bit24_controlled_buffer_7_bit24_out, bit24_controlled_buffer_8_bit24_out,
       bit24_divider_1_bit24_adder_a, bit24_divider_1_bit24_adder_b, or_7_out, or_10_out, or_11_out,
       or_12_out, register_1_q, s_r_ff_24_q;

  // Probe on in_13[14:10]
  // Probe on in_13[14:10]
  // Probe on in_13[14:10]
  // Probe on in_14[14:10]
  // Probe on in_14[14:10]
  // Probe on in_14[14:10]
  Bit5_Twos_Complementer bit5_twos_complementer_1 (
    .Bit5_In(in_14[14:10]), .Bit5_Result(bit5_twos_complementer_1_bit5_result));
  // Probe on {bit5_adder_1_bit5_result_2[4], bit5_adder_1_bit5_result}
  // Probe on {bit5_adder_1_bit5_result_2[4], bit5_adder_1_bit5_result}
  // Probe on {bit5_adder_1_bit5_result_2[4], bit5_adder_1_bit5_result}
  Bit5_Adder bit5_adder_1 (
    .Cin(in_12), .Bit5_A(in_13[14:10]), .Bit5_B(bit5_twos_complementer_1_bit5_result),
    .Bit5_Result({bit5_adder_1_bit5_result_2[4], bit5_adder_1_bit5_result}), .Cout(bit5_adder_1_cout));
  // Probe on {6'b000001, in_14[9:0]}
  // Probe on {6'b000001, in_14[9:0]}
  // Probe on {6'b000001, in_14[9:0]}
  // Probe on {6'b000001, in_13[9:0]}
  // Probe on {6'b000001, in_13[9:0]}
  // Probe on {6'b000001, in_13[9:0]}
  D_Flip_Flop #(.trigger("falling")) d_ff_1 (.clk(in_2));  // open: D, Q, Qn, preset, reset
  // Probe on Bit16_A
  // Probe on Bit16_B
  Demultiplexer #(.select(4)) demultiplexer_1 (
    .out1(demultiplexer_1_out1), .out2(demultiplexer_1_out2), .out4(demultiplexer_1_out4),
    .out11(demultiplexer_1_out11), .in(not_1_out), .sel(Bit5_Opcode[3:0]));  // open: out0, out3, out5, out6, out7, out8, out9, out10, out12, out13, out14, out15
  not not_1 (not_1_out, Bit5_Opcode[4]);
  // Probe on {in_8, undriven_2}
  and and_1 (and_1_out, fpop, ~bit5_adder_1_cout);  // AND_Gate
  and and_2 (and_2_out, fpop, bit5_adder_1_cout);
  and and_3 (and_3_out, ~Bit5_Opcode[2], Bit5_Opcode[3], not_1_out);  // AND_Gate
  and and_4 (and_4_out, Bit5_Opcode[3], not_1_out, ~Bit5_Opcode[2], or_2_out);  // AND_Gate
  Bit4_Twos_Complementer bit4_twos_complementer_1 (
    .Bit4_In(bit5_adder_1_bit5_result), .Bit4_Result(bit4_twos_complementer_1_bit4_result));
  not not_2 (not_2_out, bit5_adder_1_bit5_result_2[4]);
  or or_1 (or_1_out, demultiplexer_1_out1, demultiplexer_1_out2);
  or or_2 (or_2_out, demultiplexer_1_out4, demultiplexer_1_out11);
  or or_3 (or_3_out, and_4_out, and_3_out, Signed_Integer_Operation);
  or or_4 (or_4_out, and_4_out, Signed_Integer_Operation);
  Demultiplexer #(.select(5)) demultiplexer_2 (
    .out0(demultiplexer_2_out0), .out1(demultiplexer_2_out1), .out2(demultiplexer_2_out2),
    .out3(demultiplexer_2_out3), .out4(demultiplexer_2_out4), .out5(demultiplexer_2_out5),
    .out6(demultiplexer_2_out6), .out7(demultiplexer_2_out7), .out8(demultiplexer_2_out8),
    .out9(demultiplexer_2_out9), .out10(demultiplexer_2_out10), .out11(demultiplexer_2_out11),
    .out12(demultiplexer_2_out12), .out13(demultiplexer_2_out13), .out14(demultiplexer_2_out14),
    .out15(demultiplexer_2_out15), .out16(demultiplexer_2_out16), .out17(demultiplexer_2_out17),
    .out18(demultiplexer_2_out18), .out19(demultiplexer_2_out19), .out20(demultiplexer_2_out20),
    .out21(demultiplexer_2_out21), .out22(demultiplexer_2_out22), .out23(demultiplexer_2_out23),
    .in(and_5_out), .sel(d_ff_6_q));  // open: out24, out25, out26, out27, out28, out29, out30, out31
  and and_5 (and_5_out, or_13_out, or_2_out);
  Bit16_Controlled_Buffer bit16_controlled_buffer_1 (
    .Enable(and_2_out), .Bit16_In({6'b000001, in_14[9:0]}), .Bit16_Out(bit16_controlled_buffer_1_bit16_out));
  Bit16_Controlled_Buffer bit16_controlled_buffer_2 (
    .Enable(and_1_out), .Bit16_In({6'b000001, in_13[9:0]}), .Bit16_Out(bit16_controlled_buffer_2_bit16_out));
  Bit4_Controlled_Buffer bit4_controlled_buffer_1 (
    .Bit4_In(bit4_twos_complementer_1_bit4_result), .Enable(bit5_adder_1_bit5_result_2[4]),
    .Bit4_Out(bit4_controlled_buffer_1_bit4_out));
  Bit4_Controlled_Buffer bit4_controlled_buffer_2 (
    .Bit4_In(bit5_adder_1_bit5_result), .Enable(not_2_out), .Bit4_Out(bit4_controlled_buffer_2_bit4_out));
  S_R_Flip_Flop s_r_ff_1 (
    .S(demultiplexer_2_out23), .R(in_1), .clk(and_6_out), .Q(s_r_ff_24_q[23]), .reset(not_4_out));  // open: Qn, preset
  not not_3 (not_3_out, or_2_out);
  assign or_5_out = bit16_controlled_buffer_1_bit16_out | PLACEHOLDER2 | bit16_controlled_buffer_2_bit16_out;  // OR_Gate or_5, 16 bits wide
  assign or_6_out = bit4_controlled_buffer_1_bit4_out | PLACEHOLDER | bit4_controlled_buffer_2_bit4_out;  // OR_Gate or_6, 4 bits wide
  // Probe on or_6_out
  // Probe on or_6_out
  // Probe on or_6_out
  S_R_Flip_Flop s_r_ff_2 (
    .S(demultiplexer_2_out22), .R(in_1), .clk(and_6_out), .Q(s_r_ff_24_q[22]), .reset(not_4_out));  // open: Qn, preset
  nor nor_1 (nor_1_out, d_ff_6_q[4], d_ff_6_q[3], d_ff_6_q[2], d_ff_6_q[1], ~or_2_out);  // NOR_Gate
  and and_6 (and_6_out, or_2_out, Clock);
  not not_4 (not_4_out, or_2_out);
  Bit16_To_Bit24 bit16_to_bit24_1 (.Bit16({6'b000001, in_14[9:0]}), .Bit24(bit16_to_bit24_1_bit24));
  Bit16_To_Bit24 bit16_to_bit24_2 (.Bit16({6'b000001, in_13[9:0]}), .Bit24(bit16_to_bit24_2_bit24));
  D_Flip_Flop #(.trigger("falling")) d_ff_2 (
    .D(d_ff_2_qn), .clk(and_6_out), .Q(d_ff_6_q[4]), .Qn(d_ff_2_qn), .reset(not_4_out));  // open: preset
  Bit24_Controlled_Buffer bit24_controlled_buffer_1 (
    .Enable(not_3_out), .Bit24_In(bit16_to_bit24_3_bit24), .Bit24_Out(bit24_controlled_buffer_1_bit24_out));
  Bit16_To_Bit24 bit16_to_bit24_3 (.Bit16(twos_complementer_1_bit16_result), .Bit24(bit16_to_bit24_3_bit24));
  Twos_Complementer twos_complementer_1 (
    .Cut_MSB(or_3_out), .Bit16_Input(Bit16_A), .Bit16_Result(twos_complementer_1_bit16_result));  // open: Floating_Point_Bit_Strip, Allow_Twos_Complement
  Twos_Complementer twos_complementer_2 (
    .Cut_MSB(or_4_out), .Allow_Twos_Complement(demultiplexer_1_out2), .Bit16_Input(Bit16_B),
    .Bit16_Result(twos_complementer_2_bit16_result));  // open: Floating_Point_Bit_Strip
  S_R_Flip_Flop s_r_ff_3 (
    .S(demultiplexer_2_out21), .R(in_1), .clk(and_6_out), .Q(s_r_ff_24_q[21]), .reset(not_4_out));  // open: Qn, preset
  D_Flip_Flop #(.trigger("falling")) d_ff_3 (
    .D(d_ff_3_qn), .clk(d_ff_6_q[4]), .Q(d_ff_6_q[3]), .Qn(d_ff_3_qn), .reset(not_4_out));  // open: preset
  assign or_7_out = register_1_q | bit24_controlled_buffer_1_bit24_out;  // OR_Gate or_7, 24 bits wide
  Bit24_Adder bit24_adder_1 (
    .Bit24_A(bit24_divider_1_bit24_adder_a), .Bit24_B(bit24_divider_1_bit24_adder_b),
    .Bit16_C_OUT(bit24_adder_1_bit16_c_out), .Bit24_Result(bit24_adder_1_bit24_result),
    .C_OUT(bit24_adder_1_c_out));  // open: C_In
  S_R_Flip_Flop s_r_ff_4 (
    .S(demultiplexer_2_out20), .R(in_1), .clk(and_6_out), .Q(s_r_ff_24_q[20]), .reset(not_4_out));  // open: Qn, preset
  D_Flip_Flop #(.trigger("falling")) d_ff_4 (
    .D(d_ff_4_qn), .clk(d_ff_6_q[3]), .Q(d_ff_6_q[2]), .Qn(d_ff_4_qn), .reset(not_4_out));  // open: preset
  // Probe on bit16t24_right_shift_1_bit24_result
  // Probe on bit16t24_right_shift_1_bit24_result
  // Probe on bit16t24_right_shift_1_bit24_result
  Bit16T24_Right_Shift bit16t24_right_shift_1 (
    .Bit16_Data(or_5_out), .Bit4_Shift(or_6_out), .Bit24_Result(bit16t24_right_shift_1_bit24_result),
    .Bit16_Result(out_26));  // open: Shift_Overflow_For_Bit16
  Bit24_Divider bit24_divider_1 (
    .Clock(in_15), .Bit24_Dividend(in_16), .Bit24_Divisor(in_17), .Int_Div(in_19), .FLOAT_Div(in_18),
    .Bit16_C_Out_Adder(bit24_adder_1_bit16_c_out), .Bit24_Result(bit24_adder_1_bit24_result),
    .C_Out_Adder(bit24_adder_1_c_out), .Divider_Running(out_27), .Bit24_Remainder(out_28),
    .Bit24_Quotient(out_29), .Bit24_Adder_A(bit24_divider_1_bit24_adder_a),
    .Bit24_Adder_B(bit24_divider_1_bit24_adder_b));
  S_R_Flip_Flop s_r_ff_5 (
    .S(demultiplexer_2_out19), .R(in_1), .clk(and_6_out), .Q(s_r_ff_24_q[19]), .reset(not_4_out));  // open: Qn, preset
  Demultiplexer #(.select(5)) demultiplexer_3 (
    .out0(demultiplexer_3_out0), .out1(demultiplexer_3_out1), .out2(demultiplexer_3_out2),
    .out3(demultiplexer_3_out3), .out4(demultiplexer_3_out4), .out5(demultiplexer_3_out5),
    .out6(demultiplexer_3_out6), .out7(demultiplexer_3_out7), .out8(demultiplexer_3_out8),
    .out9(demultiplexer_3_out9), .out10(demultiplexer_3_out10), .out11(demultiplexer_3_out11),
    .out12(demultiplexer_3_out12), .out13(demultiplexer_3_out13), .out14(demultiplexer_3_out14),
    .out15(demultiplexer_3_out15), .out16(demultiplexer_3_out16), .out17(demultiplexer_3_out17),
    .out18(demultiplexer_3_out18), .out19(demultiplexer_3_out19), .out20(demultiplexer_3_out20),
    .out21(demultiplexer_3_out21), .out22(demultiplexer_3_out22), .out23(demultiplexer_3_out23),
    .sel(d_ff_6_q));  // open: out24, out25, out26, out27, out28, out29, out30, out31, in
  D_Flip_Flop #(.trigger("falling")) d_ff_5 (
    .D(d_ff_5_qn), .clk(d_ff_6_q[2]), .Q(d_ff_6_q[1]), .Qn(d_ff_5_qn), .reset(not_4_out));  // open: preset
  Bit16_To_Bit24 bit16_to_bit24_4 (.Bit16(twos_complementer_2_bit16_result), .Bit24(bit16_to_bit24_4_bit24));
  not not_5 (not_5_out, and_1_out);
  not not_6 (not_6_out, and_2_out);
  S_R_Flip_Flop s_r_ff_6 (
    .S(demultiplexer_2_out18), .R(in_1), .clk(and_6_out), .Q(s_r_ff_24_q[18]), .reset(not_4_out));  // open: Qn, preset
  D_Flip_Flop #(.trigger("falling")) d_ff_6 (
    .D(d_ff_6_qn), .clk(d_ff_6_q[1]), .Q(d_ff_6_q[0]), .Qn(d_ff_6_qn));  // open: preset, reset
  not not_7 (not_7_out, or_2_out);
  not not_8 (not_8_out, or_13_out);
  S_R_Flip_Flop s_r_ff_7 (
    .S(demultiplexer_2_out17), .R(in_1), .clk(and_6_out), .Q(s_r_ff_24_q[17]), .reset(not_4_out));  // open: Qn, preset
  Register #(.trigger("falling"), .width(24)) register_1 (
    .D({or_10_out[22:0], or_14_out[0]}), .en(or_2_out), .clk(and_6_out), .Q(register_1_q), .clr(or_8_out));
  or or_8 (or_8_out, not_7_out, not_4_out);
  S_R_Flip_Flop s_r_ff_8 (
    .S(demultiplexer_2_out16), .R(in_1), .clk(and_6_out), .Q(s_r_ff_24_q[16]), .reset(not_4_out));  // open: Qn, preset
  and and_7 (and_7_out, ~d_ff_6_q[4], d_ff_6_q[3], d_ff_6_q[2], d_ff_6_q[1], d_ff_6_q[0], demultiplexer_1_out4);  // AND_Gate
  and and_8 (and_8_out, d_ff_6_q[4], d_ff_6_q[3], ~d_ff_6_q[2], ~d_ff_6_q[1], ~d_ff_6_q[0], demultiplexer_1_out11);  // AND_Gate
  Bit24_Controlled_Buffer bit24_controlled_buffer_2 (
    .Enable(and_1_out), .Bit24_In(bit16t24_right_shift_1_bit24_result),
    .Bit24_Out(bit24_controlled_buffer_2_bit24_out));
  Bit24_Controlled_Buffer bit24_controlled_buffer_3 (
    .Enable(or_1_out), .Bit24_In(bit16_to_bit24_4_bit24), .Bit24_Out(bit24_controlled_buffer_3_bit24_out));
  Bit24_Controlled_Buffer bit24_controlled_buffer_4 (
    .Enable(and_2_out), .Bit24_In(bit16t24_right_shift_1_bit24_result),
    .Bit24_Out(bit24_controlled_buffer_4_bit24_out));
  Bit24_Controlled_Buffer bit24_controlled_buffer_5 (
    .Enable(not_5_out), .Bit24_In(bit16_to_bit24_2_bit24), .Bit24_Out(bit24_controlled_buffer_5_bit24_out));
  Bit24_Controlled_Buffer bit24_controlled_buffer_6 (
    .Enable(not_6_out), .Bit24_In(bit16_to_bit24_1_bit24), .Bit24_Out(bit24_controlled_buffer_6_bit24_out));
  S_R_Flip_Flop s_r_ff_9 (
    .S(demultiplexer_2_out15), .R(in_1), .clk(and_6_out), .Q(s_r_ff_24_q[15]), .reset(not_4_out));  // open: Qn, preset
  or or_9 (CPU_WAIT_FOR_ALU_OP, and_7_out, and_8_out);
  Bit24_Controlled_Buffer bit24_controlled_buffer_7 (
    .Enable(not_8_out), .Bit24_In(register_1_q), .Bit24_Out(bit24_controlled_buffer_7_bit24_out));
  Bit24_Controlled_Buffer bit24_controlled_buffer_8 (
    .Enable(or_13_out), .Bit24_In(bit24_adder_2_bit24_result), .Bit24_Out(bit24_controlled_buffer_8_bit24_out));
  S_R_Flip_Flop s_r_ff_10 (
    .S(demultiplexer_2_out14), .R(in_1), .clk(and_6_out), .Q(s_r_ff_24_q[14]), .reset(not_4_out));  // open: Qn, preset
  and and_9 (and_9_out, demultiplexer_3_out23, bit16_to_bit24_3_bit24[23]);
  and and_10 (and_10_out, demultiplexer_3_out22, bit16_to_bit24_3_bit24[22]);
  assign or_10_out = bit24_controlled_buffer_7_bit24_out | bit24_controlled_buffer_8_bit24_out;  // OR_Gate or_10, 24 bits wide
  assign or_11_out = or_7_out | bit24_controlled_buffer_5_bit24_out | bit24_controlled_buffer_2_bit24_out;  // OR_Gate or_11, 24 bits wide
  assign or_12_out = bit24_controlled_buffer_3_bit24_out | bit24_controlled_buffer_6_bit24_out | bit24_controlled_buffer_4_bit24_out;  // OR_Gate or_12, 24 bits wide
  and and_11 (and_11_out, demultiplexer_3_out21, bit16_to_bit24_3_bit24[21]);
  and and_12 (and_12_out, demultiplexer_3_out20, bit16_to_bit24_3_bit24[20]);
  S_R_Flip_Flop s_r_ff_11 (
    .S(demultiplexer_2_out13), .R(in_1), .clk(and_6_out), .Q(s_r_ff_24_q[13]), .reset(not_4_out));  // open: Qn, preset
  and and_13 (and_13_out, demultiplexer_3_out19, bit16_to_bit24_3_bit24[19]);
  and and_14 (and_14_out, demultiplexer_3_out18, bit16_to_bit24_3_bit24[18]);
  and and_15 (and_15_out, demultiplexer_3_out17, bit16_to_bit24_3_bit24[17]);
  S_R_Flip_Flop s_r_ff_12 (
    .S(demultiplexer_2_out12), .R(in_1), .clk(and_6_out), .Q(s_r_ff_24_q[12]), .reset(not_4_out));  // open: Qn, preset
  and and_16 (and_16_out, demultiplexer_3_out16, bit16_to_bit24_3_bit24[16]);
  and and_17 (and_17_out, demultiplexer_3_out15, bit16_to_bit24_3_bit24[15]);
  and and_18 (and_18_out, demultiplexer_3_out14, bit16_to_bit24_3_bit24[14]);
  or or_13 (or_13_out, and_19_out, and_22_out);
  and and_19 (and_19_out, demultiplexer_1_out11, bit24_adder_2_c_out);
  Bit24_Adder bit24_adder_2 (
    .Bit24_A(or_11_out), .Bit24_B(or_12_out), .Bit16_C_OUT(bit24_adder_2_bit16_c_out),
    .Bit24_Result(bit24_adder_2_bit24_result), .C_OUT(bit24_adder_2_c_out));  // open: C_In
  S_R_Flip_Flop s_r_ff_13 (
    .S(demultiplexer_2_out11), .R(in_1), .clk(and_6_out), .Q(s_r_ff_24_q[11]), .reset(not_4_out));  // open: Qn, preset
  and and_20 (and_20_out, demultiplexer_3_out13, bit16_to_bit24_3_bit24[13]);
  and and_21 (and_21_out, demultiplexer_3_out12, bit16_to_bit24_3_bit24[12]);
  and and_22 (and_22_out, demultiplexer_1_out4, bit24_adder_2_bit16_c_out);
  S_R_Flip_Flop s_r_ff_14 (
    .S(demultiplexer_2_out10), .R(in_1), .clk(and_6_out), .Q(s_r_ff_24_q[10]), .reset(not_4_out));  // open: Qn, preset
  and and_23 (and_23_out, demultiplexer_3_out11, bit16_to_bit24_3_bit24[11]);
  and and_24 (and_24_out, demultiplexer_3_out10, bit16_to_bit24_3_bit24[10]);
  and and_25 (and_25_out, demultiplexer_3_out9, bit16_to_bit24_3_bit24[9]);
  S_R_Flip_Flop s_r_ff_15 (
    .S(demultiplexer_2_out9), .R(in_1), .clk(and_6_out), .Q(s_r_ff_24_q[9]), .reset(not_4_out));  // open: Qn, preset
  and and_26 (and_26_out, demultiplexer_3_out8, bit16_to_bit24_3_bit24[8]);
  and and_27 (and_27_out, demultiplexer_3_out7, bit16_to_bit24_3_bit24[7]);
  and and_28 (and_28_out, demultiplexer_3_out6, bit16_to_bit24_3_bit24[6]);
  S_R_Flip_Flop s_r_ff_16 (
    .S(demultiplexer_2_out8), .R(in_1), .clk(and_6_out), .Q(s_r_ff_24_q[8]), .reset(not_4_out));  // open: Qn, preset
  and and_29 (and_29_out, demultiplexer_3_out5, bit16_to_bit24_3_bit24[5]);
  and and_30 (and_30_out, demultiplexer_3_out4, bit16_to_bit24_3_bit24[4]);
  Bit16_Controlled_Buffer bit16_controlled_buffer_3 (.Bit16_In({undriven, undriven_2[9:0]}));  // open: Enable, Bit16_Out
  S_R_Flip_Flop s_r_ff_17 (
    .S(demultiplexer_2_out7), .R(in_1), .clk(and_6_out), .Q(s_r_ff_24_q[7]), .reset(not_4_out));  // open: Qn, preset
  and and_31 (and_31_out, demultiplexer_3_out3, bit16_to_bit24_3_bit24[3]);
  and and_32 (and_32_out, demultiplexer_3_out2, bit16_to_bit24_3_bit24[2]);
  and and_33 (and_33_out, demultiplexer_3_out1, bit16_to_bit24_3_bit24[1]);
  S_R_Flip_Flop s_r_ff_18 (
    .S(demultiplexer_2_out6), .R(in_1), .clk(and_6_out), .Q(s_r_ff_24_q[6]), .reset(not_4_out));  // open: Qn, preset
  and and_34 (and_34_out, demultiplexer_3_out0, bit16_to_bit24_3_bit24[0]);
  or or_14 (or_14_out[0], and_34_out, and_33_out, and_32_out, and_31_out, and_30_out, and_29_out, and_28_out, and_27_out, and_26_out, and_25_out, and_24_out, and_23_out, and_21_out, and_20_out, and_18_out, and_17_out, and_16_out, and_15_out, and_14_out, and_13_out, and_12_out, and_11_out, and_10_out, and_9_out);
  S_R_Flip_Flop s_r_ff_19 (
    .S(demultiplexer_2_out5), .R(in_1), .clk(and_6_out), .Q(s_r_ff_24_q[5]), .reset(not_4_out));  // open: Qn, preset
  S_R_Flip_Flop s_r_ff_20 (
    .S(demultiplexer_2_out4), .R(in_1), .clk(and_6_out), .Q(s_r_ff_24_q[4]), .reset(not_4_out));  // open: Qn, preset
  S_R_Flip_Flop s_r_ff_21 (
    .S(demultiplexer_2_out3), .R(in_1), .clk(and_6_out), .Q(s_r_ff_24_q[3]), .reset(not_4_out));  // open: Qn, preset
  S_R_Flip_Flop s_r_ff_22 (
    .S(demultiplexer_2_out2), .R(in_1), .clk(and_6_out), .Q(s_r_ff_24_q[2]), .reset(not_4_out));  // open: Qn, preset
  // Bit16_Multiplier bit16_multiplier_1: pin names not known; wires that end beside it: bit16_multiplier_1_p1, bit16_multiplier_1_p2
  S_R_Flip_Flop s_r_ff_23 (
    .S(demultiplexer_2_out1), .R(in_1), .clk(and_6_out), .Q(s_r_ff_24_q[1]), .reset(not_4_out));  // open: Qn, preset
  S_R_Flip_Flop s_r_ff_24 (
    .S(demultiplexer_2_out0), .R(in_1), .clk(and_6_out), .Q(s_r_ff_24_q[0]), .reset(not_4_out));  // open: Qn, preset
  Bit16_Controlled_Buffer bit16_controlled_buffer_4 (.Bit16_In(bit16_multiplier_1_p1));  // open: Enable, Bit16_Out
  Bit16_Controlled_Buffer bit16_controlled_buffer_5 (.Bit16_In(bit16_multiplier_1_p2));  // open: Enable, Bit16_Out

  // Notes on the sheet:
  //   FP OP
  //   FP DIV
  //   FDIV
  //   IDIV
  //   this line may go low 1 clock before its meant to
  //   unsigned subtraction carry
  //   LSB IS FAR LEFT. SPLITTER NEEDS INVERSION
endmodule

module Twos_Complementer (
  input  Floating_Point_Bit_Strip,
  input  Cut_MSB,
  input  Allow_Twos_Complement,
  input  [15:0] Bit16_Input,
  output [15:0] Bit16_Result
);

  wire and_1_out, and_2_out, and_3_out, and_4_out, and_5_out, and_6_out, and_7_out, and_8_out, and_9_out,
       and_10_out, and_11_out, and_12_out, and_13_out, and_14_out, and_15_out, or_1_out, or_2_out, or_3_out,
       or_4_out, or_5_out, or_6_out, or_7_out, or_8_out, or_9_out, or_10_out, or_11_out, or_12_out,
       or_13_out, or_14_out, or_15_out, xor_10_out, xor_11_out, xor_12_out, xor_13_out, xor_14_out,
       xor_15_out;

  or or_1 (or_1_out, Floating_Point_Bit_Strip, Cut_MSB);
  and and_1 (and_1_out, Bit16_Input[0], Allow_Twos_Complement);
  and and_2 (and_2_out, Bit16_Result[1], Allow_Twos_Complement);
  or or_2 (or_2_out, and_1_out, and_2_out);
  and and_3 (and_3_out, Bit16_Result[2], Allow_Twos_Complement);
  or or_3 (or_3_out, and_1_out, and_2_out, and_3_out);
  and and_4 (and_4_out, Bit16_Result[3], Allow_Twos_Complement);
  or or_4 (or_4_out, and_1_out, and_2_out, and_3_out, and_4_out);
  and and_5 (and_5_out, Bit16_Result[4], Allow_Twos_Complement);
  or or_5 (or_5_out, and_1_out, and_2_out, and_3_out, and_4_out, and_5_out);
  and and_6 (and_6_out, Bit16_Result[5], Allow_Twos_Complement);
  or or_6 (or_6_out, and_1_out, and_2_out, and_3_out, and_4_out, and_5_out, and_6_out);
  and and_7 (and_7_out, Bit16_Result[6], Allow_Twos_Complement);
  or or_7 (or_7_out, and_1_out, and_2_out, and_3_out, and_4_out, and_5_out, and_6_out, and_7_out);
  and and_8 (and_8_out, Bit16_Result[7], Allow_Twos_Complement);
  or or_8 (or_8_out, and_1_out, and_2_out, and_3_out, and_4_out, and_5_out, and_6_out, and_7_out, and_8_out);
  and and_9 (and_9_out, Bit16_Result[8], Allow_Twos_Complement);
  or or_9 (or_9_out, and_1_out, and_2_out, and_3_out, and_4_out, and_5_out, and_6_out, and_7_out, and_8_out, and_9_out);
  and and_10 (and_10_out, Bit16_Result[9], Allow_Twos_Complement);
  or or_10 (or_10_out, and_1_out, and_2_out, and_3_out, and_4_out, and_5_out, and_6_out, and_7_out, and_8_out, and_9_out, and_10_out);
  and and_11 (and_11_out, xor_10_out, Allow_Twos_Complement);
  or or_11 (or_11_out, and_1_out, and_2_out, and_3_out, and_4_out, and_5_out, and_6_out, and_7_out, and_8_out, and_9_out, and_10_out, and_11_out);
  and and_12 (and_12_out, xor_11_out, Allow_Twos_Complement);
  or or_12 (or_12_out, and_1_out, and_2_out, and_3_out, and_4_out, and_5_out, and_6_out, and_7_out, and_8_out, and_9_out, and_10_out, and_11_out, and_12_out);
  and and_13 (and_13_out, xor_12_out, Allow_Twos_Complement);
  or or_13 (or_13_out, and_1_out, and_2_out, and_3_out, and_4_out, and_5_out, and_6_out, and_7_out, and_8_out, and_9_out, and_10_out, and_11_out, and_12_out, and_13_out);
  and and_14 (and_14_out, xor_13_out, Allow_Twos_Complement);
  or or_14 (or_14_out, and_1_out, and_2_out, and_3_out, and_4_out, and_5_out, and_6_out, and_7_out, and_8_out, and_9_out, and_10_out, and_11_out, and_12_out, and_13_out, and_14_out);
  and and_15 (and_15_out, xor_14_out, Allow_Twos_Complement);
  or or_15 (or_15_out, and_1_out, and_2_out, and_3_out, and_4_out, and_5_out, and_6_out, and_7_out, and_8_out, and_9_out, and_10_out, and_11_out, and_12_out, and_13_out, and_14_out, and_15_out);
  xor xor_1 (Bit16_Result[1], and_1_out, Bit16_Input[1]);
  xor xor_2 (Bit16_Result[2], or_2_out, Bit16_Input[2]);
  xor xor_3 (Bit16_Result[3], or_3_out, Bit16_Input[3]);
  xor xor_4 (Bit16_Result[4], or_4_out, Bit16_Input[4]);
  xor xor_5 (Bit16_Result[5], or_5_out, Bit16_Input[5]);
  xor xor_6 (Bit16_Result[6], or_6_out, Bit16_Input[6]);
  xor xor_7 (Bit16_Result[7], or_7_out, Bit16_Input[7]);
  xor xor_8 (Bit16_Result[8], or_8_out, Bit16_Input[8]);
  xor xor_9 (Bit16_Result[9], or_9_out, Bit16_Input[9]);
  xor xor_10 (xor_10_out, or_10_out, Bit16_Input[10]);
  xor xor_11 (xor_11_out, or_11_out, Bit16_Input[11]);
  xor xor_12 (xor_12_out, or_12_out, Bit16_Input[12]);
  xor xor_13 (xor_13_out, or_13_out, Bit16_Input[13]);
  xor xor_14 (xor_14_out, or_14_out, Bit16_Input[14]);
  and and_16 (Bit16_Result[15], ~or_1_out, xor_15_out);  // AND_Gate
  xor xor_15 (xor_15_out, or_15_out, Bit16_Input[15]);
  or or_16 (Bit16_Result[10], Floating_Point_Bit_Strip, xor_10_out);
  and and_17 (Bit16_Result[11], ~Floating_Point_Bit_Strip, xor_11_out);  // AND_Gate
  and and_18 (Bit16_Result[12], ~Floating_Point_Bit_Strip, xor_12_out);  // AND_Gate
  and and_19 (Bit16_Result[13], ~Floating_Point_Bit_Strip, xor_13_out);  // AND_Gate
  and and_20 (Bit16_Result[14], ~Floating_Point_Bit_Strip, xor_14_out);  // AND_Gate

  assign Bit16_Result[0] = Bit16_Input[0];

  // Notes on the sheet:
  //   bc "implied" leading bit
endmodule
module Bit16_Multiplier (
  input  [15:0] Bit16_B,
  input  [15:0] Bit16_A,
  output [15:0] Lower_Word,
  output [15:0] Upper_Word
);

  wire and_1_out, and_2_out, and_3_out, and_4_out, and_5_out, and_6_out, and_7_out, and_8_out, and_9_out,
       and_10_out, and_11_out, and_12_out, and_13_out, and_14_out, and_15_out, and_16_out, and_17_out,
       and_18_out, and_19_out, and_20_out, and_21_out, and_22_out, and_23_out, and_24_out, and_25_out,
       and_26_out, and_27_out, and_28_out, and_29_out, and_30_out, and_31_out, and_32_out, and_33_out,
       and_34_out, and_35_out, and_36_out, and_37_out, and_38_out, and_39_out, and_40_out, and_41_out,
       and_42_out, and_43_out, and_44_out, and_45_out, and_46_out, and_47_out, and_48_out, and_49_out,
       and_50_out, and_51_out, and_52_out, and_53_out, and_54_out, and_55_out, and_56_out, and_57_out,
       and_58_out, and_59_out, and_60_out, and_61_out, and_62_out, and_63_out, and_64_out, and_65_out,
       and_66_out, and_67_out, and_68_out, and_69_out, and_70_out, and_71_out, and_72_out, and_73_out,
       and_74_out, and_75_out, and_76_out, and_77_out, and_78_out, and_79_out, and_80_out, and_81_out,
       and_82_out, and_83_out, and_84_out, and_85_out, and_86_out, and_87_out, and_88_out, and_89_out,
       and_90_out, and_91_out, and_92_out, and_93_out, and_94_out, and_95_out, and_96_out, and_97_out,
       and_98_out, and_99_out, and_100_out, and_101_out, and_102_out, and_103_out, and_104_out, and_105_out,
       and_106_out, and_107_out, and_108_out, and_109_out, and_110_out, and_111_out, and_112_out,
       and_113_out, and_114_out, and_115_out, and_116_out, and_117_out, and_118_out, and_119_out,
       and_120_out, and_121_out, and_122_out, and_123_out, and_124_out, and_125_out, and_126_out,
       and_127_out, and_128_out, and_129_out, and_130_out, and_131_out, and_132_out, and_133_out,
       and_134_out, and_135_out, and_136_out, and_137_out, and_138_out, and_139_out, and_140_out,
       and_141_out, and_142_out, and_143_out, and_144_out, and_145_out, and_146_out, and_147_out,
       and_148_out, and_149_out, and_150_out, and_151_out, and_152_out, and_153_out, and_154_out,
       and_155_out, and_156_out, and_157_out, and_158_out, and_159_out, and_160_out, and_161_out,
       and_162_out, and_163_out, and_164_out, and_165_out, and_166_out, and_167_out, and_168_out,
       and_169_out, and_170_out, and_171_out, and_172_out, and_173_out, and_174_out, and_175_out,
       and_176_out, and_177_out, and_178_out, and_179_out, and_180_out, and_181_out, and_182_out,
       and_183_out, and_184_out, and_185_out, and_186_out, and_187_out, and_188_out, and_189_out,
       and_190_out, and_191_out, and_192_out, and_193_out, and_194_out, and_195_out, and_196_out,
       and_197_out, and_198_out, and_199_out, and_200_out, and_201_out, and_202_out, and_203_out,
       and_204_out, and_205_out, and_206_out, and_207_out, and_208_out, and_209_out, and_210_out,
       and_211_out, and_212_out, and_213_out, and_214_out, and_215_out, and_216_out, and_217_out,
       and_218_out, and_219_out, and_220_out, and_221_out, and_222_out, and_223_out, and_224_out,
       and_225_out, and_226_out, and_227_out, and_228_out, and_229_out, and_230_out, and_231_out,
       and_232_out, and_233_out, and_234_out, and_235_out, and_236_out, and_237_out, and_238_out,
       and_239_out, and_240_out, and_241_out, and_242_out, and_243_out, and_244_out, and_245_out,
       and_246_out, and_247_out, and_248_out, and_249_out, and_250_out, and_251_out, and_252_out,
       and_253_out, and_254_out, and_255_out, and_256_out, and_257_out, and_258_out, and_259_out,
       and_260_out, and_261_out, and_262_out, and_263_out, and_264_out, and_265_out, and_266_out,
       and_267_out, and_268_out, and_269_out, and_270_out, and_271_out, and_272_out, and_273_out,
       and_274_out, and_275_out, and_276_out, and_277_out, and_278_out, and_279_out, and_280_out,
       and_281_out, and_282_out, and_283_out, and_284_out, and_285_out, and_286_out, and_287_out,
       and_288_out, and_289_out, and_290_out, and_291_out, and_292_out, and_293_out, and_294_out,
       and_295_out, and_296_out, and_297_out, and_298_out, and_299_out, and_300_out, and_301_out,
       and_302_out, and_303_out, and_304_out, and_305_out, and_306_out, and_307_out, and_308_out,
       and_309_out, and_310_out, and_311_out, and_312_out, and_313_out, and_314_out, and_315_out,
       and_316_out, and_317_out, and_318_out, and_319_out, and_320_out, and_321_out, and_322_out,
       and_323_out, and_324_out, and_325_out, and_326_out, and_327_out, and_328_out, and_329_out,
       and_330_out, and_331_out, and_332_out, and_333_out, and_334_out, and_335_out, and_336_out,
       and_337_out, and_338_out, and_339_out, and_340_out, and_341_out, and_342_out, and_343_out,
       and_344_out, and_345_out, and_346_out, and_347_out, and_348_out, and_349_out, and_350_out,
       and_351_out, and_352_out, and_353_out, and_354_out, and_355_out, and_356_out, and_357_out,
       and_358_out, and_359_out, and_360_out, and_361_out, and_362_out, and_363_out, and_364_out,
       and_365_out, and_366_out, and_367_out, and_368_out, and_369_out, and_370_out, and_371_out,
       and_372_out, and_373_out, and_374_out, and_375_out, and_376_out, and_377_out, and_378_out,
       and_379_out, and_380_out, and_381_out, and_382_out, and_383_out, and_384_out, and_385_out,
       and_386_out, and_387_out, and_388_out, and_389_out, and_390_out, and_391_out, and_392_out,
       and_393_out, and_394_out, and_395_out, and_396_out, and_397_out, and_398_out, and_399_out,
       and_400_out, and_401_out, and_402_out, and_403_out, and_404_out, and_405_out, and_406_out,
       and_407_out, and_408_out, and_409_out, and_410_out, and_411_out, and_412_out, and_413_out,
       and_414_out, and_415_out, and_416_out, and_417_out, and_418_out, and_419_out, and_420_out,
       and_421_out, and_422_out, and_423_out, and_424_out, and_425_out, and_426_out, and_427_out,
       and_428_out, and_429_out, and_430_out, and_431_out, and_432_out, and_433_out, and_434_out,
       and_435_out, and_436_out, and_437_out, and_438_out, and_439_out, and_440_out, and_441_out,
       and_442_out, and_443_out, and_444_out, and_445_out, and_446_out, and_447_out, and_448_out,
       and_449_out, and_450_out, and_451_out, and_452_out, and_453_out, and_454_out, and_455_out,
       and_456_out, and_457_out, and_458_out, and_459_out, and_460_out, and_461_out, and_462_out,
       and_463_out, and_464_out, and_465_out, and_466_out, and_467_out, and_468_out, and_469_out,
       and_470_out, and_471_out, and_472_out, and_473_out, and_474_out, and_475_out, and_476_out,
       and_477_out, and_478_out, and_479_out, and_480_out, and_481_out, and_482_out, and_483_out,
       and_484_out, and_485_out, and_486_out, and_487_out, and_488_out, and_489_out, and_490_out,
       and_491_out, and_492_out, and_493_out, and_494_out, and_495_out, and_496_out, and_497_out,
       and_498_out, and_499_out, and_500_out, and_501_out, and_502_out, and_503_out, and_504_out,
       and_505_out, and_506_out, and_507_out, and_508_out, and_509_out, and_510_out, and_511_out,
       and_512_out, and_513_out, and_514_out, and_515_out, and_516_out, and_517_out, and_518_out,
       and_519_out, and_520_out, and_521_out, and_522_out, and_523_out, and_524_out, and_525_out,
       and_526_out, and_527_out, and_528_out, and_529_out, and_530_out, and_531_out, and_532_out,
       and_533_out, and_534_out, and_535_out, and_536_out, and_537_out, and_538_out, and_539_out,
       and_540_out, and_541_out, and_542_out, and_543_out, and_544_out, and_545_out, and_546_out,
       and_547_out, and_548_out, and_549_out, and_550_out, and_551_out, and_552_out, and_553_out,
       and_554_out, and_555_out, and_556_out, and_557_out, and_558_out, and_559_out, and_560_out,
       and_561_out, and_562_out, and_563_out, and_564_out, and_565_out, and_566_out, and_567_out,
       and_568_out, and_569_out, and_570_out, and_571_out, and_572_out, and_573_out, and_574_out,
       and_575_out, and_576_out, and_577_out, and_578_out, and_579_out, and_580_out, and_581_out,
       and_582_out, and_583_out, and_584_out, and_585_out, and_586_out, and_587_out, and_588_out,
       and_589_out, and_590_out, and_591_out, and_592_out, and_593_out, and_594_out, and_595_out,
       and_596_out, and_597_out, and_598_out, and_599_out, and_600_out, and_601_out, and_602_out,
       and_603_out, and_604_out, and_605_out, and_606_out, and_607_out, and_608_out, and_609_out,
       and_610_out, and_611_out, and_612_out, and_613_out, and_614_out, and_615_out, and_616_out,
       and_617_out, and_618_out, and_619_out, and_620_out, and_621_out, and_622_out, and_623_out,
       and_624_out, and_625_out, and_626_out, and_627_out, and_628_out, and_629_out, and_630_out,
       and_631_out, and_632_out, and_633_out, and_634_out, and_635_out, and_636_out, and_637_out,
       and_638_out, and_639_out, and_640_out, and_641_out, and_642_out, and_643_out, and_644_out,
       and_645_out, and_646_out, and_647_out, and_648_out, and_649_out, and_650_out, and_651_out,
       and_652_out, and_653_out, and_654_out, and_655_out, and_656_out, and_657_out, and_658_out,
       and_659_out, and_660_out, and_661_out, and_662_out, and_663_out, and_664_out, and_665_out,
       and_666_out, and_667_out, and_668_out, and_669_out, and_670_out, and_671_out, and_672_out,
       and_673_out, and_674_out, and_675_out, and_676_out, and_677_out, and_678_out, and_679_out,
       and_680_out, and_681_out, and_682_out, and_683_out, and_684_out, and_685_out, and_686_out,
       and_687_out, and_688_out, and_689_out, and_690_out, and_691_out, and_692_out, and_693_out,
       and_694_out, and_695_out, and_696_out, and_697_out, and_698_out, and_699_out, and_700_out,
       and_701_out, and_702_out, and_703_out, and_704_out, and_705_out, and_706_out, and_707_out,
       and_708_out, and_709_out, and_710_out, and_711_out, and_712_out, and_713_out, and_714_out,
       and_715_out, and_716_out, and_717_out, and_718_out, and_719_out, or_2_out, or_3_out, or_4_out,
       or_5_out, or_6_out, or_7_out, or_8_out, or_9_out, or_10_out, or_11_out, or_12_out, or_13_out,
       or_14_out, or_15_out, or_16_out, or_17_out, or_18_out, or_19_out, or_20_out, or_21_out, or_22_out,
       or_23_out, or_24_out, or_25_out, or_26_out, or_27_out, or_28_out, or_29_out, or_30_out, or_31_out,
       or_32_out, or_33_out, or_34_out, or_35_out, or_36_out, or_37_out, or_38_out, or_39_out, or_40_out,
       or_41_out, or_42_out, or_43_out, or_44_out, or_45_out, or_46_out, or_47_out, or_48_out, or_49_out,
       or_50_out, or_51_out, or_52_out, or_53_out, or_54_out, or_55_out, or_56_out, or_57_out, or_58_out,
       or_59_out, or_60_out, or_61_out, or_62_out, or_63_out, or_64_out, or_65_out, or_66_out, or_67_out,
       or_68_out, or_69_out, or_70_out, or_71_out, or_72_out, or_73_out, or_74_out, or_75_out, or_76_out,
       or_77_out, or_78_out, or_79_out, or_80_out, or_81_out, or_82_out, or_83_out, or_84_out, or_85_out,
       or_86_out, or_87_out, or_88_out, or_89_out, or_90_out, or_91_out, or_92_out, or_93_out, or_94_out,
       or_95_out, or_96_out, or_97_out, or_98_out, or_99_out, or_100_out, or_101_out, or_102_out, or_103_out,
       or_104_out, or_105_out, or_106_out, or_107_out, or_108_out, or_109_out, or_110_out, or_111_out,
       or_112_out, or_113_out, or_114_out, or_115_out, or_116_out, or_117_out, or_118_out, or_119_out,
       or_120_out, or_121_out, or_122_out, or_123_out, or_124_out, or_125_out, or_126_out, or_127_out,
       or_128_out, or_129_out, or_130_out, or_131_out, or_132_out, or_133_out, or_134_out, or_135_out,
       or_136_out, or_137_out, or_138_out, or_139_out, or_140_out, or_141_out, or_142_out, or_143_out,
       or_144_out, or_145_out, or_146_out, or_147_out, or_148_out, or_149_out, or_150_out, or_151_out,
       or_152_out, or_153_out, or_154_out, or_155_out, or_156_out, or_157_out, or_158_out, or_159_out,
       or_160_out, or_161_out, or_162_out, or_163_out, or_164_out, or_165_out, or_166_out, or_167_out,
       or_168_out, or_169_out, or_170_out, or_171_out, or_172_out, or_173_out, or_174_out, or_175_out,
       or_176_out, or_177_out, or_178_out, or_179_out, or_180_out, or_181_out, or_182_out, or_183_out,
       or_184_out, or_185_out, or_186_out, or_187_out, or_188_out, or_189_out, or_190_out, or_191_out,
       or_192_out, or_193_out, or_194_out, or_195_out, or_196_out, or_197_out, or_198_out, or_199_out,
       or_200_out, or_201_out, or_202_out, or_203_out, or_204_out, or_205_out, or_206_out, or_207_out,
       or_208_out, or_209_out, or_210_out, or_211_out, or_212_out, or_213_out, or_214_out, or_215_out,
       or_216_out, or_217_out, or_218_out, or_219_out, or_220_out, or_221_out, or_222_out, or_223_out,
       or_224_out, xor_1_out, xor_3_out, xor_4_out, xor_5_out, xor_7_out, xor_8_out, xor_9_out, xor_10_out,
       xor_11_out, xor_13_out, xor_14_out, xor_15_out, xor_16_out, xor_17_out, xor_18_out, xor_19_out,
       xor_21_out, xor_22_out, xor_23_out, xor_24_out, xor_25_out, xor_26_out, xor_27_out, xor_28_out,
       xor_29_out, xor_31_out, xor_32_out, xor_33_out, xor_34_out, xor_35_out, xor_36_out, xor_37_out,
       xor_38_out, xor_39_out, xor_40_out, xor_41_out, xor_43_out, xor_44_out, xor_45_out, xor_46_out,
       xor_47_out, xor_48_out, xor_49_out, xor_50_out, xor_51_out, xor_52_out, xor_53_out, xor_54_out,
       xor_55_out, xor_57_out, xor_58_out, xor_59_out, xor_60_out, xor_61_out, xor_62_out, xor_63_out,
       xor_64_out, xor_65_out, xor_66_out, xor_67_out, xor_68_out, xor_69_out, xor_70_out, xor_71_out,
       xor_73_out, xor_74_out, xor_75_out, xor_76_out, xor_77_out, xor_78_out, xor_79_out, xor_80_out,
       xor_81_out, xor_82_out, xor_83_out, xor_84_out, xor_85_out, xor_86_out, xor_87_out, xor_88_out,
       xor_89_out, xor_91_out, xor_92_out, xor_93_out, xor_94_out, xor_95_out, xor_96_out, xor_97_out,
       xor_98_out, xor_99_out, xor_100_out, xor_101_out, xor_102_out, xor_103_out, xor_104_out, xor_105_out,
       xor_106_out, xor_107_out, xor_108_out, xor_109_out, xor_111_out, xor_112_out, xor_113_out,
       xor_114_out, xor_115_out, xor_116_out, xor_117_out, xor_118_out, xor_119_out, xor_120_out,
       xor_121_out, xor_122_out, xor_123_out, xor_124_out, xor_125_out, xor_126_out, xor_127_out,
       xor_128_out, xor_129_out, xor_130_out, xor_131_out, xor_133_out, xor_134_out, xor_135_out,
       xor_136_out, xor_137_out, xor_138_out, xor_139_out, xor_140_out, xor_141_out, xor_142_out,
       xor_143_out, xor_144_out, xor_145_out, xor_146_out, xor_147_out, xor_148_out, xor_149_out,
       xor_150_out, xor_151_out, xor_152_out, xor_153_out, xor_154_out, xor_155_out, xor_157_out,
       xor_158_out, xor_159_out, xor_160_out, xor_161_out, xor_162_out, xor_163_out, xor_164_out,
       xor_165_out, xor_166_out, xor_167_out, xor_168_out, xor_169_out, xor_170_out, xor_171_out,
       xor_172_out, xor_173_out, xor_174_out, xor_175_out, xor_176_out, xor_177_out, xor_178_out,
       xor_179_out, xor_180_out, xor_181_out, xor_183_out, xor_184_out, xor_185_out, xor_186_out,
       xor_187_out, xor_188_out, xor_189_out, xor_190_out, xor_191_out, xor_192_out, xor_193_out,
       xor_194_out, xor_195_out, xor_196_out, xor_197_out, xor_198_out, xor_199_out, xor_200_out,
       xor_201_out, xor_202_out, xor_203_out, xor_204_out, xor_205_out, xor_206_out, xor_207_out,
       xor_208_out, xor_209_out, xor_211_out, xor_212_out, xor_213_out, xor_214_out, xor_215_out,
       xor_216_out, xor_217_out, xor_218_out, xor_219_out, xor_220_out, xor_221_out, xor_222_out,
       xor_223_out, xor_224_out, xor_225_out, xor_226_out, xor_227_out, xor_228_out, xor_229_out,
       xor_230_out, xor_231_out, xor_232_out, xor_233_out, xor_234_out, xor_235_out, xor_236_out,
       xor_237_out, xor_238_out, xor_240_out, xor_241_out, xor_242_out, xor_243_out, xor_244_out,
       xor_245_out, xor_246_out, xor_247_out, xor_248_out, xor_249_out, xor_250_out, xor_251_out,
       xor_252_out, xor_253_out, xor_254_out, xor_255_out, xor_256_out, xor_257_out, xor_258_out,
       xor_259_out, xor_260_out, xor_261_out, xor_262_out, xor_263_out, xor_264_out, xor_265_out,
       xor_266_out, xor_267_out, xor_269_out, xor_270_out, xor_271_out, xor_272_out, xor_273_out,
       xor_274_out, xor_275_out, xor_276_out, xor_277_out, xor_278_out, xor_279_out, xor_280_out,
       xor_281_out, xor_282_out, xor_283_out, xor_284_out, xor_285_out, xor_286_out, xor_287_out,
       xor_288_out, xor_289_out, xor_290_out, xor_291_out, xor_292_out, xor_293_out, xor_294_out,
       xor_296_out, xor_297_out, xor_298_out, xor_299_out, xor_300_out, xor_301_out, xor_302_out,
       xor_303_out, xor_304_out, xor_305_out, xor_306_out, xor_307_out, xor_308_out, xor_309_out,
       xor_310_out, xor_311_out, xor_312_out, xor_313_out, xor_314_out, xor_315_out, xor_316_out,
       xor_317_out, xor_318_out, xor_319_out, xor_321_out, xor_322_out, xor_323_out, xor_324_out,
       xor_325_out, xor_326_out, xor_327_out, xor_328_out, xor_329_out, xor_330_out, xor_331_out,
       xor_332_out, xor_333_out, xor_334_out, xor_335_out, xor_336_out, xor_337_out, xor_338_out,
       xor_339_out, xor_340_out, xor_341_out, xor_342_out, xor_344_out, xor_345_out, xor_346_out,
       xor_347_out, xor_348_out, xor_349_out, xor_350_out, xor_351_out, xor_352_out, xor_353_out,
       xor_354_out, xor_355_out, xor_356_out, xor_357_out, xor_358_out, xor_359_out, xor_360_out,
       xor_361_out, xor_362_out, xor_363_out, xor_365_out, xor_366_out, xor_367_out, xor_368_out,
       xor_369_out, xor_370_out, xor_371_out, xor_372_out, xor_373_out, xor_374_out, xor_375_out,
       xor_376_out, xor_377_out, xor_378_out, xor_379_out, xor_380_out, xor_381_out, xor_382_out,
       xor_384_out, xor_385_out, xor_386_out, xor_387_out, xor_388_out, xor_389_out, xor_390_out,
       xor_391_out, xor_392_out, xor_393_out, xor_394_out, xor_395_out, xor_396_out, xor_397_out,
       xor_398_out, xor_399_out, xor_401_out, xor_402_out, xor_403_out, xor_404_out, xor_405_out,
       xor_406_out, xor_407_out, xor_408_out, xor_409_out, xor_410_out, xor_411_out, xor_412_out,
       xor_413_out, xor_414_out, xor_416_out, xor_417_out, xor_418_out, xor_419_out, xor_420_out,
       xor_421_out, xor_422_out, xor_423_out, xor_424_out, xor_425_out, xor_426_out, xor_427_out,
       xor_429_out, xor_430_out, xor_431_out, xor_432_out, xor_433_out, xor_434_out, xor_435_out,
       xor_436_out, xor_437_out, xor_438_out, xor_440_out, xor_441_out, xor_442_out, xor_443_out,
       xor_444_out, xor_445_out, xor_446_out, xor_447_out, xor_449_out, xor_450_out, xor_451_out,
       xor_452_out, xor_453_out, xor_454_out, xor_456_out, xor_457_out, xor_458_out, xor_459_out,
       xor_461_out, xor_462_out;

  or or_1 (Upper_Word[15], and_3_out, and_2_out);
  and and_1 (and_1_out, Bit16_A[15], Bit16_B[15]);
  xor xor_1 (xor_1_out, and_1_out, or_2_out);
  and and_2 (and_2_out, or_3_out, xor_1_out);
  xor xor_2 (Upper_Word[14], xor_1_out, or_3_out);
  and and_3 (and_3_out, and_1_out, or_2_out);
  or or_2 (or_2_out, and_8_out, and_5_out);
  or or_3 (or_3_out, and_9_out, and_7_out);
  and and_4 (and_4_out, Bit16_A[14], Bit16_B[15]);
  xor xor_3 (xor_3_out, and_4_out, or_4_out);
  and and_5 (and_5_out, or_5_out, xor_3_out);
  xor xor_4 (xor_4_out, xor_3_out, or_5_out);
  and and_6 (and_6_out, Bit16_A[15], Bit16_B[14]);
  xor xor_5 (xor_5_out, and_6_out, xor_4_out);
  and and_7 (and_7_out, or_6_out, xor_5_out);
  xor xor_6 (Upper_Word[13], xor_5_out, or_6_out);
  and and_8 (and_8_out, and_4_out, or_4_out);
  and and_9 (and_9_out, and_6_out, xor_4_out);
  or or_4 (or_4_out, and_16_out, and_11_out);
  or or_5 (or_5_out, and_17_out, and_13_out);
  or or_6 (or_6_out, and_18_out, and_15_out);
  and and_10 (and_10_out, Bit16_A[13], Bit16_B[15]);
  xor xor_7 (xor_7_out, and_10_out, or_7_out);
  and and_11 (and_11_out, or_8_out, xor_7_out);
  xor xor_8 (xor_8_out, xor_7_out, or_8_out);
  and and_12 (and_12_out, Bit16_A[14], Bit16_B[14]);
  xor xor_9 (xor_9_out, and_12_out, xor_8_out);
  and and_13 (and_13_out, or_9_out, xor_9_out);
  xor xor_10 (xor_10_out, xor_9_out, or_9_out);
  and and_14 (and_14_out, Bit16_A[15], Bit16_B[13]);
  xor xor_11 (xor_11_out, and_14_out, xor_10_out);
  and and_15 (and_15_out, or_10_out, xor_11_out);
  xor xor_12 (Upper_Word[12], xor_11_out, or_10_out);
  and and_16 (and_16_out, and_10_out, or_7_out);
  and and_17 (and_17_out, and_12_out, xor_8_out);
  and and_18 (and_18_out, and_14_out, xor_10_out);
  or or_7 (or_7_out, and_27_out, and_20_out);
  or or_8 (or_8_out, and_28_out, and_22_out);
  or or_9 (or_9_out, and_29_out, and_24_out);
  or or_10 (or_10_out, and_30_out, and_26_out);
  and and_19 (and_19_out, Bit16_A[12], Bit16_B[15]);
  xor xor_13 (xor_13_out, and_19_out, or_11_out);
  and and_20 (and_20_out, or_12_out, xor_13_out);
  xor xor_14 (xor_14_out, xor_13_out, or_12_out);
  and and_21 (and_21_out, Bit16_A[13], Bit16_B[14]);
  xor xor_15 (xor_15_out, and_21_out, xor_14_out);
  and and_22 (and_22_out, or_13_out, xor_15_out);
  xor xor_16 (xor_16_out, xor_15_out, or_13_out);
  and and_23 (and_23_out, Bit16_A[14], Bit16_B[13]);
  xor xor_17 (xor_17_out, and_23_out, xor_16_out);
  and and_24 (and_24_out, or_14_out, xor_17_out);
  xor xor_18 (xor_18_out, xor_17_out, or_14_out);
  and and_25 (and_25_out, Bit16_A[15], Bit16_B[12]);
  xor xor_19 (xor_19_out, and_25_out, xor_18_out);
  and and_26 (and_26_out, or_15_out, xor_19_out);
  xor xor_20 (Upper_Word[11], xor_19_out, or_15_out);
  and and_27 (and_27_out, and_19_out, or_11_out);
  and and_28 (and_28_out, and_21_out, xor_14_out);
  and and_29 (and_29_out, and_23_out, xor_16_out);
  and and_30 (and_30_out, and_25_out, xor_18_out);
  or or_11 (or_11_out, and_41_out, and_32_out);
  or or_12 (or_12_out, and_42_out, and_34_out);
  or or_13 (or_13_out, and_43_out, and_36_out);
  or or_14 (or_14_out, and_44_out, and_38_out);
  or or_15 (or_15_out, and_45_out, and_40_out);
  and and_31 (and_31_out, Bit16_A[11], Bit16_B[15]);
  xor xor_21 (xor_21_out, and_31_out, or_16_out);
  and and_32 (and_32_out, or_17_out, xor_21_out);
  xor xor_22 (xor_22_out, xor_21_out, or_17_out);
  and and_33 (and_33_out, Bit16_A[12], Bit16_B[14]);
  xor xor_23 (xor_23_out, and_33_out, xor_22_out);
  and and_34 (and_34_out, or_18_out, xor_23_out);
  xor xor_24 (xor_24_out, xor_23_out, or_18_out);
  and and_35 (and_35_out, Bit16_A[13], Bit16_B[13]);
  xor xor_25 (xor_25_out, and_35_out, xor_24_out);
  and and_36 (and_36_out, or_19_out, xor_25_out);
  xor xor_26 (xor_26_out, xor_25_out, or_19_out);
  and and_37 (and_37_out, Bit16_A[14], Bit16_B[12]);
  xor xor_27 (xor_27_out, and_37_out, xor_26_out);
  and and_38 (and_38_out, or_20_out, xor_27_out);
  xor xor_28 (xor_28_out, xor_27_out, or_20_out);
  and and_39 (and_39_out, Bit16_A[15], Bit16_B[11]);
  xor xor_29 (xor_29_out, and_39_out, xor_28_out);
  and and_40 (and_40_out, or_21_out, xor_29_out);
  xor xor_30 (Upper_Word[10], xor_29_out, or_21_out);
  and and_41 (and_41_out, and_31_out, or_16_out);
  and and_42 (and_42_out, and_33_out, xor_22_out);
  and and_43 (and_43_out, and_35_out, xor_24_out);
  and and_44 (and_44_out, and_37_out, xor_26_out);
  and and_45 (and_45_out, and_39_out, xor_28_out);
  or or_16 (or_16_out, and_58_out, and_47_out);
  or or_17 (or_17_out, and_59_out, and_49_out);
  or or_18 (or_18_out, and_60_out, and_51_out);
  or or_19 (or_19_out, and_61_out, and_53_out);
  or or_20 (or_20_out, and_62_out, and_55_out);
  or or_21 (or_21_out, and_63_out, and_57_out);
  and and_46 (and_46_out, Bit16_A[10], Bit16_B[15]);
  xor xor_31 (xor_31_out, and_46_out, or_22_out);
  and and_47 (and_47_out, or_23_out, xor_31_out);
  xor xor_32 (xor_32_out, xor_31_out, or_23_out);
  and and_48 (and_48_out, Bit16_A[11], Bit16_B[14]);
  xor xor_33 (xor_33_out, and_48_out, xor_32_out);
  and and_49 (and_49_out, or_24_out, xor_33_out);
  xor xor_34 (xor_34_out, xor_33_out, or_24_out);
  and and_50 (and_50_out, Bit16_A[12], Bit16_B[13]);
  xor xor_35 (xor_35_out, and_50_out, xor_34_out);
  and and_51 (and_51_out, or_25_out, xor_35_out);
  xor xor_36 (xor_36_out, xor_35_out, or_25_out);
  and and_52 (and_52_out, Bit16_A[13], Bit16_B[12]);
  xor xor_37 (xor_37_out, and_52_out, xor_36_out);
  and and_53 (and_53_out, or_26_out, xor_37_out);
  xor xor_38 (xor_38_out, xor_37_out, or_26_out);
  and and_54 (and_54_out, Bit16_A[14], Bit16_B[11]);
  xor xor_39 (xor_39_out, and_54_out, xor_38_out);
  and and_55 (and_55_out, or_27_out, xor_39_out);
  xor xor_40 (xor_40_out, xor_39_out, or_27_out);
  and and_56 (and_56_out, Bit16_A[15], Bit16_B[10]);
  xor xor_41 (xor_41_out, and_56_out, xor_40_out);
  and and_57 (and_57_out, or_28_out, xor_41_out);
  xor xor_42 (Upper_Word[9], xor_41_out, or_28_out);
  and and_58 (and_58_out, and_46_out, or_22_out);
  and and_59 (and_59_out, and_48_out, xor_32_out);
  and and_60 (and_60_out, and_50_out, xor_34_out);
  and and_61 (and_61_out, and_52_out, xor_36_out);
  and and_62 (and_62_out, and_54_out, xor_38_out);
  and and_63 (and_63_out, and_56_out, xor_40_out);
  or or_22 (or_22_out, and_78_out, and_65_out);
  or or_23 (or_23_out, and_79_out, and_67_out);
  or or_24 (or_24_out, and_80_out, and_69_out);
  or or_25 (or_25_out, and_81_out, and_71_out);
  or or_26 (or_26_out, and_82_out, and_73_out);
  or or_27 (or_27_out, and_83_out, and_75_out);
  or or_28 (or_28_out, and_84_out, and_77_out);
  and and_64 (and_64_out, Bit16_A[9], Bit16_B[15]);
  xor xor_43 (xor_43_out, and_64_out, or_29_out);
  and and_65 (and_65_out, or_30_out, xor_43_out);
  xor xor_44 (xor_44_out, xor_43_out, or_30_out);
  and and_66 (and_66_out, Bit16_A[10], Bit16_B[14]);
  xor xor_45 (xor_45_out, and_66_out, xor_44_out);
  and and_67 (and_67_out, or_31_out, xor_45_out);
  xor xor_46 (xor_46_out, xor_45_out, or_31_out);
  and and_68 (and_68_out, Bit16_A[11], Bit16_B[13]);
  xor xor_47 (xor_47_out, and_68_out, xor_46_out);
  and and_69 (and_69_out, or_32_out, xor_47_out);
  xor xor_48 (xor_48_out, xor_47_out, or_32_out);
  and and_70 (and_70_out, Bit16_A[12], Bit16_B[12]);
  xor xor_49 (xor_49_out, and_70_out, xor_48_out);
  and and_71 (and_71_out, or_33_out, xor_49_out);
  xor xor_50 (xor_50_out, xor_49_out, or_33_out);
  and and_72 (and_72_out, Bit16_A[13], Bit16_B[11]);
  xor xor_51 (xor_51_out, and_72_out, xor_50_out);
  and and_73 (and_73_out, or_34_out, xor_51_out);
  xor xor_52 (xor_52_out, xor_51_out, or_34_out);
  and and_74 (and_74_out, Bit16_A[14], Bit16_B[10]);
  xor xor_53 (xor_53_out, and_74_out, xor_52_out);
  and and_75 (and_75_out, or_35_out, xor_53_out);
  xor xor_54 (xor_54_out, xor_53_out, or_35_out);
  and and_76 (and_76_out, Bit16_A[15], Bit16_B[9]);
  xor xor_55 (xor_55_out, and_76_out, xor_54_out);
  and and_77 (and_77_out, or_36_out, xor_55_out);
  xor xor_56 (Upper_Word[8], xor_55_out, or_36_out);
  and and_78 (and_78_out, and_64_out, or_29_out);
  and and_79 (and_79_out, and_66_out, xor_44_out);
  and and_80 (and_80_out, and_68_out, xor_46_out);
  and and_81 (and_81_out, and_70_out, xor_48_out);
  and and_82 (and_82_out, and_72_out, xor_50_out);
  and and_83 (and_83_out, and_74_out, xor_52_out);
  and and_84 (and_84_out, and_76_out, xor_54_out);
  or or_29 (or_29_out, and_101_out, and_86_out);
  or or_30 (or_30_out, and_102_out, and_88_out);
  or or_31 (or_31_out, and_103_out, and_90_out);
  or or_32 (or_32_out, and_104_out, and_92_out);
  or or_33 (or_33_out, and_105_out, and_94_out);
  or or_34 (or_34_out, and_106_out, and_96_out);
  or or_35 (or_35_out, and_107_out, and_98_out);
  or or_36 (or_36_out, and_108_out, and_100_out);
  and and_85 (and_85_out, Bit16_A[8], Bit16_B[15]);
  xor xor_57 (xor_57_out, and_85_out, or_37_out);
  and and_86 (and_86_out, or_38_out, xor_57_out);
  xor xor_58 (xor_58_out, xor_57_out, or_38_out);
  and and_87 (and_87_out, Bit16_A[9], Bit16_B[14]);
  xor xor_59 (xor_59_out, and_87_out, xor_58_out);
  and and_88 (and_88_out, or_39_out, xor_59_out);
  xor xor_60 (xor_60_out, xor_59_out, or_39_out);
  and and_89 (and_89_out, Bit16_A[10], Bit16_B[13]);
  xor xor_61 (xor_61_out, and_89_out, xor_60_out);
  and and_90 (and_90_out, or_40_out, xor_61_out);
  xor xor_62 (xor_62_out, xor_61_out, or_40_out);
  and and_91 (and_91_out, Bit16_A[11], Bit16_B[12]);
  xor xor_63 (xor_63_out, and_91_out, xor_62_out);
  and and_92 (and_92_out, or_41_out, xor_63_out);
  xor xor_64 (xor_64_out, xor_63_out, or_41_out);
  and and_93 (and_93_out, Bit16_A[12], Bit16_B[11]);
  xor xor_65 (xor_65_out, and_93_out, xor_64_out);
  and and_94 (and_94_out, or_42_out, xor_65_out);
  xor xor_66 (xor_66_out, xor_65_out, or_42_out);
  and and_95 (and_95_out, Bit16_A[13], Bit16_B[10]);
  xor xor_67 (xor_67_out, and_95_out, xor_66_out);
  and and_96 (and_96_out, or_43_out, xor_67_out);
  xor xor_68 (xor_68_out, xor_67_out, or_43_out);
  and and_97 (and_97_out, Bit16_A[14], Bit16_B[9]);
  xor xor_69 (xor_69_out, and_97_out, xor_68_out);
  and and_98 (and_98_out, or_44_out, xor_69_out);
  xor xor_70 (xor_70_out, xor_69_out, or_44_out);
  and and_99 (and_99_out, Bit16_A[15], Bit16_B[8]);
  xor xor_71 (xor_71_out, and_99_out, xor_70_out);
  and and_100 (and_100_out, or_45_out, xor_71_out);
  xor xor_72 (Upper_Word[7], xor_71_out, or_45_out);
  and and_101 (and_101_out, and_85_out, or_37_out);
  and and_102 (and_102_out, and_87_out, xor_58_out);
  and and_103 (and_103_out, and_89_out, xor_60_out);
  and and_104 (and_104_out, and_91_out, xor_62_out);
  and and_105 (and_105_out, and_93_out, xor_64_out);
  and and_106 (and_106_out, and_95_out, xor_66_out);
  and and_107 (and_107_out, and_97_out, xor_68_out);
  and and_108 (and_108_out, and_99_out, xor_70_out);
  or or_37 (or_37_out, and_127_out, and_110_out);
  or or_38 (or_38_out, and_128_out, and_112_out);
  or or_39 (or_39_out, and_129_out, and_114_out);
  or or_40 (or_40_out, and_130_out, and_116_out);
  or or_41 (or_41_out, and_131_out, and_118_out);
  or or_42 (or_42_out, and_132_out, and_120_out);
  or or_43 (or_43_out, and_133_out, and_122_out);
  or or_44 (or_44_out, and_134_out, and_124_out);
  or or_45 (or_45_out, and_135_out, and_126_out);
  and and_109 (and_109_out, Bit16_A[7], Bit16_B[15]);
  xor xor_73 (xor_73_out, and_109_out, or_46_out);
  and and_110 (and_110_out, or_47_out, xor_73_out);
  xor xor_74 (xor_74_out, xor_73_out, or_47_out);
  and and_111 (and_111_out, Bit16_A[8], Bit16_B[14]);
  xor xor_75 (xor_75_out, and_111_out, xor_74_out);
  and and_112 (and_112_out, or_48_out, xor_75_out);
  xor xor_76 (xor_76_out, xor_75_out, or_48_out);
  and and_113 (and_113_out, Bit16_A[9], Bit16_B[13]);
  xor xor_77 (xor_77_out, and_113_out, xor_76_out);
  and and_114 (and_114_out, or_49_out, xor_77_out);
  xor xor_78 (xor_78_out, xor_77_out, or_49_out);
  and and_115 (and_115_out, Bit16_A[10], Bit16_B[12]);
  xor xor_79 (xor_79_out, and_115_out, xor_78_out);
  and and_116 (and_116_out, or_50_out, xor_79_out);
  xor xor_80 (xor_80_out, xor_79_out, or_50_out);
  and and_117 (and_117_out, Bit16_A[11], Bit16_B[11]);
  xor xor_81 (xor_81_out, and_117_out, xor_80_out);
  and and_118 (and_118_out, or_51_out, xor_81_out);
  xor xor_82 (xor_82_out, xor_81_out, or_51_out);
  and and_119 (and_119_out, Bit16_A[12], Bit16_B[10]);
  xor xor_83 (xor_83_out, and_119_out, xor_82_out);
  and and_120 (and_120_out, or_52_out, xor_83_out);
  xor xor_84 (xor_84_out, xor_83_out, or_52_out);
  and and_121 (and_121_out, Bit16_A[13], Bit16_B[9]);
  xor xor_85 (xor_85_out, and_121_out, xor_84_out);
  and and_122 (and_122_out, or_53_out, xor_85_out);
  xor xor_86 (xor_86_out, xor_85_out, or_53_out);
  and and_123 (and_123_out, Bit16_A[14], Bit16_B[8]);
  xor xor_87 (xor_87_out, and_123_out, xor_86_out);
  and and_124 (and_124_out, or_54_out, xor_87_out);
  xor xor_88 (xor_88_out, xor_87_out, or_54_out);
  and and_125 (and_125_out, Bit16_A[15], Bit16_B[7]);
  xor xor_89 (xor_89_out, and_125_out, xor_88_out);
  and and_126 (and_126_out, or_55_out, xor_89_out);
  xor xor_90 (Upper_Word[6], xor_89_out, or_55_out);
  and and_127 (and_127_out, and_109_out, or_46_out);
  and and_128 (and_128_out, and_111_out, xor_74_out);
  and and_129 (and_129_out, and_113_out, xor_76_out);
  and and_130 (and_130_out, and_115_out, xor_78_out);
  and and_131 (and_131_out, and_117_out, xor_80_out);
  and and_132 (and_132_out, and_119_out, xor_82_out);
  and and_133 (and_133_out, and_121_out, xor_84_out);
  and and_134 (and_134_out, and_123_out, xor_86_out);
  and and_135 (and_135_out, and_125_out, xor_88_out);
  or or_46 (or_46_out, and_156_out, and_137_out);
  or or_47 (or_47_out, and_157_out, and_139_out);
  or or_48 (or_48_out, and_158_out, and_141_out);
  or or_49 (or_49_out, and_159_out, and_143_out);
  or or_50 (or_50_out, and_160_out, and_145_out);
  or or_51 (or_51_out, and_161_out, and_147_out);
  or or_52 (or_52_out, and_162_out, and_149_out);
  or or_53 (or_53_out, and_163_out, and_151_out);
  or or_54 (or_54_out, and_164_out, and_153_out);
  or or_55 (or_55_out, and_165_out, and_155_out);
  and and_136 (and_136_out, Bit16_A[6], Bit16_B[15]);
  xor xor_91 (xor_91_out, and_136_out, or_56_out);
  and and_137 (and_137_out, or_57_out, xor_91_out);
  xor xor_92 (xor_92_out, xor_91_out, or_57_out);
  and and_138 (and_138_out, Bit16_A[7], Bit16_B[14]);
  xor xor_93 (xor_93_out, and_138_out, xor_92_out);
  and and_139 (and_139_out, or_58_out, xor_93_out);
  xor xor_94 (xor_94_out, xor_93_out, or_58_out);
  and and_140 (and_140_out, Bit16_A[8], Bit16_B[13]);
  xor xor_95 (xor_95_out, and_140_out, xor_94_out);
  and and_141 (and_141_out, or_59_out, xor_95_out);
  xor xor_96 (xor_96_out, xor_95_out, or_59_out);
  and and_142 (and_142_out, Bit16_A[9], Bit16_B[12]);
  xor xor_97 (xor_97_out, and_142_out, xor_96_out);
  and and_143 (and_143_out, or_60_out, xor_97_out);
  xor xor_98 (xor_98_out, xor_97_out, or_60_out);
  and and_144 (and_144_out, Bit16_A[10], Bit16_B[11]);
  xor xor_99 (xor_99_out, and_144_out, xor_98_out);
  and and_145 (and_145_out, or_61_out, xor_99_out);
  xor xor_100 (xor_100_out, xor_99_out, or_61_out);
  and and_146 (and_146_out, Bit16_A[11], Bit16_B[10]);
  xor xor_101 (xor_101_out, and_146_out, xor_100_out);
  and and_147 (and_147_out, or_62_out, xor_101_out);
  xor xor_102 (xor_102_out, xor_101_out, or_62_out);
  and and_148 (and_148_out, Bit16_A[12], Bit16_B[9]);
  xor xor_103 (xor_103_out, and_148_out, xor_102_out);
  and and_149 (and_149_out, or_63_out, xor_103_out);
  xor xor_104 (xor_104_out, xor_103_out, or_63_out);
  and and_150 (and_150_out, Bit16_A[13], Bit16_B[8]);
  xor xor_105 (xor_105_out, and_150_out, xor_104_out);
  and and_151 (and_151_out, or_64_out, xor_105_out);
  xor xor_106 (xor_106_out, xor_105_out, or_64_out);
  and and_152 (and_152_out, Bit16_A[14], Bit16_B[7]);
  xor xor_107 (xor_107_out, and_152_out, xor_106_out);
  and and_153 (and_153_out, or_65_out, xor_107_out);
  xor xor_108 (xor_108_out, xor_107_out, or_65_out);
  and and_154 (and_154_out, Bit16_A[15], Bit16_B[6]);
  xor xor_109 (xor_109_out, and_154_out, xor_108_out);
  and and_155 (and_155_out, or_66_out, xor_109_out);
  xor xor_110 (Upper_Word[5], xor_109_out, or_66_out);
  and and_156 (and_156_out, and_136_out, or_56_out);
  and and_157 (and_157_out, and_138_out, xor_92_out);
  and and_158 (and_158_out, and_140_out, xor_94_out);
  and and_159 (and_159_out, and_142_out, xor_96_out);
  and and_160 (and_160_out, and_144_out, xor_98_out);
  and and_161 (and_161_out, and_146_out, xor_100_out);
  and and_162 (and_162_out, and_148_out, xor_102_out);
  and and_163 (and_163_out, and_150_out, xor_104_out);
  and and_164 (and_164_out, and_152_out, xor_106_out);
  and and_165 (and_165_out, and_154_out, xor_108_out);
  or or_56 (or_56_out, and_188_out, and_167_out);
  or or_57 (or_57_out, and_189_out, and_169_out);
  or or_58 (or_58_out, and_190_out, and_171_out);
  or or_59 (or_59_out, and_191_out, and_173_out);
  or or_60 (or_60_out, and_192_out, and_175_out);
  or or_61 (or_61_out, and_193_out, and_177_out);
  or or_62 (or_62_out, and_194_out, and_179_out);
  or or_63 (or_63_out, and_195_out, and_181_out);
  or or_64 (or_64_out, and_196_out, and_183_out);
  or or_65 (or_65_out, and_197_out, and_185_out);
  or or_66 (or_66_out, and_198_out, and_187_out);
  and and_166 (and_166_out, Bit16_A[5], Bit16_B[15]);
  xor xor_111 (xor_111_out, and_166_out, or_67_out);
  and and_167 (and_167_out, or_68_out, xor_111_out);
  xor xor_112 (xor_112_out, xor_111_out, or_68_out);
  and and_168 (and_168_out, Bit16_A[6], Bit16_B[14]);
  xor xor_113 (xor_113_out, and_168_out, xor_112_out);
  and and_169 (and_169_out, or_69_out, xor_113_out);
  xor xor_114 (xor_114_out, xor_113_out, or_69_out);
  and and_170 (and_170_out, Bit16_A[7], Bit16_B[13]);
  xor xor_115 (xor_115_out, and_170_out, xor_114_out);
  and and_171 (and_171_out, or_70_out, xor_115_out);
  xor xor_116 (xor_116_out, xor_115_out, or_70_out);
  and and_172 (and_172_out, Bit16_A[8], Bit16_B[12]);
  xor xor_117 (xor_117_out, and_172_out, xor_116_out);
  and and_173 (and_173_out, or_71_out, xor_117_out);
  xor xor_118 (xor_118_out, xor_117_out, or_71_out);
  and and_174 (and_174_out, Bit16_A[9], Bit16_B[11]);
  xor xor_119 (xor_119_out, and_174_out, xor_118_out);
  and and_175 (and_175_out, or_72_out, xor_119_out);
  xor xor_120 (xor_120_out, xor_119_out, or_72_out);
  and and_176 (and_176_out, Bit16_A[10], Bit16_B[10]);
  xor xor_121 (xor_121_out, and_176_out, xor_120_out);
  and and_177 (and_177_out, or_73_out, xor_121_out);
  xor xor_122 (xor_122_out, xor_121_out, or_73_out);
  and and_178 (and_178_out, Bit16_A[11], Bit16_B[9]);
  xor xor_123 (xor_123_out, and_178_out, xor_122_out);
  and and_179 (and_179_out, or_74_out, xor_123_out);
  xor xor_124 (xor_124_out, xor_123_out, or_74_out);
  and and_180 (and_180_out, Bit16_A[12], Bit16_B[8]);
  xor xor_125 (xor_125_out, and_180_out, xor_124_out);
  and and_181 (and_181_out, or_75_out, xor_125_out);
  xor xor_126 (xor_126_out, xor_125_out, or_75_out);
  and and_182 (and_182_out, Bit16_A[13], Bit16_B[7]);
  xor xor_127 (xor_127_out, and_182_out, xor_126_out);
  and and_183 (and_183_out, or_76_out, xor_127_out);
  xor xor_128 (xor_128_out, xor_127_out, or_76_out);
  and and_184 (and_184_out, Bit16_A[14], Bit16_B[6]);
  xor xor_129 (xor_129_out, and_184_out, xor_128_out);
  and and_185 (and_185_out, or_77_out, xor_129_out);
  xor xor_130 (xor_130_out, xor_129_out, or_77_out);
  and and_186 (and_186_out, Bit16_A[15], Bit16_B[5]);
  xor xor_131 (xor_131_out, and_186_out, xor_130_out);
  and and_187 (and_187_out, or_78_out, xor_131_out);
  xor xor_132 (Upper_Word[4], xor_131_out, or_78_out);
  and and_188 (and_188_out, and_166_out, or_67_out);
  and and_189 (and_189_out, and_168_out, xor_112_out);
  and and_190 (and_190_out, and_170_out, xor_114_out);
  and and_191 (and_191_out, and_172_out, xor_116_out);
  and and_192 (and_192_out, and_174_out, xor_118_out);
  and and_193 (and_193_out, and_176_out, xor_120_out);
  and and_194 (and_194_out, and_178_out, xor_122_out);
  and and_195 (and_195_out, and_180_out, xor_124_out);
  and and_196 (and_196_out, and_182_out, xor_126_out);
  and and_197 (and_197_out, and_184_out, xor_128_out);
  and and_198 (and_198_out, and_186_out, xor_130_out);
  or or_67 (or_67_out, and_223_out, and_200_out);
  or or_68 (or_68_out, and_224_out, and_202_out);
  or or_69 (or_69_out, and_225_out, and_204_out);
  or or_70 (or_70_out, and_226_out, and_206_out);
  or or_71 (or_71_out, and_227_out, and_208_out);
  or or_72 (or_72_out, and_228_out, and_210_out);
  or or_73 (or_73_out, and_229_out, and_212_out);
  or or_74 (or_74_out, and_230_out, and_214_out);
  or or_75 (or_75_out, and_231_out, and_216_out);
  or or_76 (or_76_out, and_232_out, and_218_out);
  or or_77 (or_77_out, and_233_out, and_220_out);
  or or_78 (or_78_out, and_234_out, and_222_out);
  and and_199 (and_199_out, Bit16_A[4], Bit16_B[15]);
  xor xor_133 (xor_133_out, and_199_out, or_79_out);
  and and_200 (and_200_out, or_80_out, xor_133_out);
  xor xor_134 (xor_134_out, xor_133_out, or_80_out);
  and and_201 (and_201_out, Bit16_A[5], Bit16_B[14]);
  xor xor_135 (xor_135_out, and_201_out, xor_134_out);
  and and_202 (and_202_out, or_81_out, xor_135_out);
  xor xor_136 (xor_136_out, xor_135_out, or_81_out);
  and and_203 (and_203_out, Bit16_A[6], Bit16_B[13]);
  xor xor_137 (xor_137_out, and_203_out, xor_136_out);
  and and_204 (and_204_out, or_82_out, xor_137_out);
  xor xor_138 (xor_138_out, xor_137_out, or_82_out);
  and and_205 (and_205_out, Bit16_A[7], Bit16_B[12]);
  xor xor_139 (xor_139_out, and_205_out, xor_138_out);
  and and_206 (and_206_out, or_83_out, xor_139_out);
  xor xor_140 (xor_140_out, xor_139_out, or_83_out);
  and and_207 (and_207_out, Bit16_A[8], Bit16_B[11]);
  xor xor_141 (xor_141_out, and_207_out, xor_140_out);
  and and_208 (and_208_out, or_84_out, xor_141_out);
  xor xor_142 (xor_142_out, xor_141_out, or_84_out);
  and and_209 (and_209_out, Bit16_A[9], Bit16_B[10]);
  xor xor_143 (xor_143_out, and_209_out, xor_142_out);
  and and_210 (and_210_out, or_85_out, xor_143_out);
  xor xor_144 (xor_144_out, xor_143_out, or_85_out);
  and and_211 (and_211_out, Bit16_A[10], Bit16_B[9]);
  xor xor_145 (xor_145_out, and_211_out, xor_144_out);
  and and_212 (and_212_out, or_86_out, xor_145_out);
  xor xor_146 (xor_146_out, xor_145_out, or_86_out);
  and and_213 (and_213_out, Bit16_A[11], Bit16_B[8]);
  xor xor_147 (xor_147_out, and_213_out, xor_146_out);
  and and_214 (and_214_out, or_87_out, xor_147_out);
  xor xor_148 (xor_148_out, xor_147_out, or_87_out);
  and and_215 (and_215_out, Bit16_A[12], Bit16_B[7]);
  xor xor_149 (xor_149_out, and_215_out, xor_148_out);
  and and_216 (and_216_out, or_88_out, xor_149_out);
  xor xor_150 (xor_150_out, xor_149_out, or_88_out);
  and and_217 (and_217_out, Bit16_A[13], Bit16_B[6]);
  xor xor_151 (xor_151_out, and_217_out, xor_150_out);
  and and_218 (and_218_out, or_89_out, xor_151_out);
  xor xor_152 (xor_152_out, xor_151_out, or_89_out);
  and and_219 (and_219_out, Bit16_A[14], Bit16_B[5]);
  xor xor_153 (xor_153_out, and_219_out, xor_152_out);
  and and_220 (and_220_out, or_90_out, xor_153_out);
  xor xor_154 (xor_154_out, xor_153_out, or_90_out);
  and and_221 (and_221_out, Bit16_A[15], Bit16_B[4]);
  xor xor_155 (xor_155_out, and_221_out, xor_154_out);
  and and_222 (and_222_out, or_91_out, xor_155_out);
  xor xor_156 (Upper_Word[3], xor_155_out, or_91_out);
  and and_223 (and_223_out, and_199_out, or_79_out);
  and and_224 (and_224_out, and_201_out, xor_134_out);
  and and_225 (and_225_out, and_203_out, xor_136_out);
  and and_226 (and_226_out, and_205_out, xor_138_out);
  and and_227 (and_227_out, and_207_out, xor_140_out);
  and and_228 (and_228_out, and_209_out, xor_142_out);
  and and_229 (and_229_out, and_211_out, xor_144_out);
  and and_230 (and_230_out, and_213_out, xor_146_out);
  and and_231 (and_231_out, and_215_out, xor_148_out);
  and and_232 (and_232_out, and_217_out, xor_150_out);
  and and_233 (and_233_out, and_219_out, xor_152_out);
  and and_234 (and_234_out, and_221_out, xor_154_out);
  or or_79 (or_79_out, and_261_out, and_236_out);
  or or_80 (or_80_out, and_262_out, and_238_out);
  or or_81 (or_81_out, and_263_out, and_240_out);
  or or_82 (or_82_out, and_264_out, and_242_out);
  or or_83 (or_83_out, and_265_out, and_244_out);
  or or_84 (or_84_out, and_266_out, and_246_out);
  or or_85 (or_85_out, and_267_out, and_248_out);
  or or_86 (or_86_out, and_268_out, and_250_out);
  or or_87 (or_87_out, and_269_out, and_252_out);
  or or_88 (or_88_out, and_270_out, and_254_out);
  or or_89 (or_89_out, and_271_out, and_256_out);
  or or_90 (or_90_out, and_272_out, and_258_out);
  or or_91 (or_91_out, and_273_out, and_260_out);
  and and_235 (and_235_out, Bit16_A[3], Bit16_B[15]);
  xor xor_157 (xor_157_out, and_235_out, or_92_out);
  and and_236 (and_236_out, or_93_out, xor_157_out);
  xor xor_158 (xor_158_out, xor_157_out, or_93_out);
  and and_237 (and_237_out, Bit16_A[4], Bit16_B[14]);
  xor xor_159 (xor_159_out, and_237_out, xor_158_out);
  and and_238 (and_238_out, or_94_out, xor_159_out);
  xor xor_160 (xor_160_out, xor_159_out, or_94_out);
  and and_239 (and_239_out, Bit16_A[5], Bit16_B[13]);
  xor xor_161 (xor_161_out, and_239_out, xor_160_out);
  and and_240 (and_240_out, or_95_out, xor_161_out);
  xor xor_162 (xor_162_out, xor_161_out, or_95_out);
  and and_241 (and_241_out, Bit16_A[6], Bit16_B[12]);
  xor xor_163 (xor_163_out, and_241_out, xor_162_out);
  and and_242 (and_242_out, or_96_out, xor_163_out);
  xor xor_164 (xor_164_out, xor_163_out, or_96_out);
  and and_243 (and_243_out, Bit16_A[7], Bit16_B[11]);
  xor xor_165 (xor_165_out, and_243_out, xor_164_out);
  and and_244 (and_244_out, or_97_out, xor_165_out);
  xor xor_166 (xor_166_out, xor_165_out, or_97_out);
  and and_245 (and_245_out, Bit16_A[8], Bit16_B[10]);
  xor xor_167 (xor_167_out, and_245_out, xor_166_out);
  and and_246 (and_246_out, or_98_out, xor_167_out);
  xor xor_168 (xor_168_out, xor_167_out, or_98_out);
  and and_247 (and_247_out, Bit16_A[9], Bit16_B[9]);
  xor xor_169 (xor_169_out, and_247_out, xor_168_out);
  and and_248 (and_248_out, or_99_out, xor_169_out);
  xor xor_170 (xor_170_out, xor_169_out, or_99_out);
  and and_249 (and_249_out, Bit16_A[10], Bit16_B[8]);
  xor xor_171 (xor_171_out, and_249_out, xor_170_out);
  and and_250 (and_250_out, or_100_out, xor_171_out);
  xor xor_172 (xor_172_out, xor_171_out, or_100_out);
  and and_251 (and_251_out, Bit16_A[11], Bit16_B[7]);
  xor xor_173 (xor_173_out, and_251_out, xor_172_out);
  and and_252 (and_252_out, or_101_out, xor_173_out);
  xor xor_174 (xor_174_out, xor_173_out, or_101_out);
  and and_253 (and_253_out, Bit16_A[12], Bit16_B[6]);
  xor xor_175 (xor_175_out, and_253_out, xor_174_out);
  and and_254 (and_254_out, or_102_out, xor_175_out);
  xor xor_176 (xor_176_out, xor_175_out, or_102_out);
  and and_255 (and_255_out, Bit16_A[13], Bit16_B[5]);
  xor xor_177 (xor_177_out, and_255_out, xor_176_out);
  and and_256 (and_256_out, or_103_out, xor_177_out);
  xor xor_178 (xor_178_out, xor_177_out, or_103_out);
  and and_257 (and_257_out, Bit16_A[14], Bit16_B[4]);
  xor xor_179 (xor_179_out, and_257_out, xor_178_out);
  and and_258 (and_258_out, or_104_out, xor_179_out);
  xor xor_180 (xor_180_out, xor_179_out, or_104_out);
  and and_259 (and_259_out, Bit16_A[15], Bit16_B[3]);
  xor xor_181 (xor_181_out, and_259_out, xor_180_out);
  and and_260 (and_260_out, or_105_out, xor_181_out);
  xor xor_182 (Upper_Word[2], xor_181_out, or_105_out);
  and and_261 (and_261_out, and_235_out, or_92_out);
  and and_262 (and_262_out, and_237_out, xor_158_out);
  and and_263 (and_263_out, and_239_out, xor_160_out);
  and and_264 (and_264_out, and_241_out, xor_162_out);
  and and_265 (and_265_out, and_243_out, xor_164_out);
  and and_266 (and_266_out, and_245_out, xor_166_out);
  and and_267 (and_267_out, and_247_out, xor_168_out);
  and and_268 (and_268_out, and_249_out, xor_170_out);
  and and_269 (and_269_out, and_251_out, xor_172_out);
  and and_270 (and_270_out, and_253_out, xor_174_out);
  and and_271 (and_271_out, and_255_out, xor_176_out);
  and and_272 (and_272_out, and_257_out, xor_178_out);
  and and_273 (and_273_out, and_259_out, xor_180_out);
  or or_92 (or_92_out, and_302_out, and_275_out);
  or or_93 (or_93_out, and_303_out, and_277_out);
  or or_94 (or_94_out, and_304_out, and_279_out);
  or or_95 (or_95_out, and_305_out, and_281_out);
  or or_96 (or_96_out, and_306_out, and_283_out);
  or or_97 (or_97_out, and_307_out, and_285_out);
  or or_98 (or_98_out, and_308_out, and_287_out);
  or or_99 (or_99_out, and_309_out, and_289_out);
  or or_100 (or_100_out, and_310_out, and_291_out);
  or or_101 (or_101_out, and_311_out, and_293_out);
  or or_102 (or_102_out, and_312_out, and_295_out);
  or or_103 (or_103_out, and_313_out, and_297_out);
  or or_104 (or_104_out, and_314_out, and_299_out);
  or or_105 (or_105_out, and_315_out, and_301_out);
  and and_274 (and_274_out, Bit16_A[2], Bit16_B[15]);
  xor xor_183 (xor_183_out, and_274_out, and_317_out);
  and and_275 (and_275_out, or_106_out, xor_183_out);
  xor xor_184 (xor_184_out, xor_183_out, or_106_out);
  and and_276 (and_276_out, Bit16_A[3], Bit16_B[14]);
  xor xor_185 (xor_185_out, and_276_out, xor_184_out);
  and and_277 (and_277_out, or_107_out, xor_185_out);
  xor xor_186 (xor_186_out, xor_185_out, or_107_out);
  and and_278 (and_278_out, Bit16_A[4], Bit16_B[13]);
  xor xor_187 (xor_187_out, and_278_out, xor_186_out);
  and and_279 (and_279_out, or_108_out, xor_187_out);
  xor xor_188 (xor_188_out, xor_187_out, or_108_out);
  and and_280 (and_280_out, Bit16_A[5], Bit16_B[12]);
  xor xor_189 (xor_189_out, and_280_out, xor_188_out);
  and and_281 (and_281_out, or_109_out, xor_189_out);
  xor xor_190 (xor_190_out, xor_189_out, or_109_out);
  and and_282 (and_282_out, Bit16_A[6], Bit16_B[11]);
  xor xor_191 (xor_191_out, and_282_out, xor_190_out);
  and and_283 (and_283_out, or_110_out, xor_191_out);
  xor xor_192 (xor_192_out, xor_191_out, or_110_out);
  and and_284 (and_284_out, Bit16_A[7], Bit16_B[10]);
  xor xor_193 (xor_193_out, and_284_out, xor_192_out);
  and and_285 (and_285_out, or_111_out, xor_193_out);
  xor xor_194 (xor_194_out, xor_193_out, or_111_out);
  and and_286 (and_286_out, Bit16_A[8], Bit16_B[9]);
  xor xor_195 (xor_195_out, and_286_out, xor_194_out);
  and and_287 (and_287_out, or_112_out, xor_195_out);
  xor xor_196 (xor_196_out, xor_195_out, or_112_out);
  and and_288 (and_288_out, Bit16_A[9], Bit16_B[8]);
  xor xor_197 (xor_197_out, and_288_out, xor_196_out);
  and and_289 (and_289_out, or_113_out, xor_197_out);
  xor xor_198 (xor_198_out, xor_197_out, or_113_out);
  and and_290 (and_290_out, Bit16_A[10], Bit16_B[7]);
  xor xor_199 (xor_199_out, and_290_out, xor_198_out);
  and and_291 (and_291_out, or_114_out, xor_199_out);
  xor xor_200 (xor_200_out, xor_199_out, or_114_out);
  and and_292 (and_292_out, Bit16_A[11], Bit16_B[6]);
  xor xor_201 (xor_201_out, and_292_out, xor_200_out);
  and and_293 (and_293_out, or_115_out, xor_201_out);
  xor xor_202 (xor_202_out, xor_201_out, or_115_out);
  and and_294 (and_294_out, Bit16_A[12], Bit16_B[5]);
  xor xor_203 (xor_203_out, and_294_out, xor_202_out);
  and and_295 (and_295_out, or_116_out, xor_203_out);
  xor xor_204 (xor_204_out, xor_203_out, or_116_out);
  and and_296 (and_296_out, Bit16_A[13], Bit16_B[4]);
  xor xor_205 (xor_205_out, and_296_out, xor_204_out);
  and and_297 (and_297_out, or_117_out, xor_205_out);
  xor xor_206 (xor_206_out, xor_205_out, or_117_out);
  and and_298 (and_298_out, Bit16_A[14], Bit16_B[3]);
  xor xor_207 (xor_207_out, and_298_out, xor_206_out);
  and and_299 (and_299_out, or_118_out, xor_207_out);
  xor xor_208 (xor_208_out, xor_207_out, or_118_out);
  and and_300 (and_300_out, Bit16_A[15], Bit16_B[2]);
  xor xor_209 (xor_209_out, and_300_out, xor_208_out);
  and and_301 (and_301_out, or_119_out, xor_209_out);
  xor xor_210 (Upper_Word[1], xor_209_out, or_119_out);
  and and_302 (and_302_out, and_274_out, and_317_out);
  and and_303 (and_303_out, and_276_out, xor_184_out);
  and and_304 (and_304_out, and_278_out, xor_186_out);
  and and_305 (and_305_out, and_280_out, xor_188_out);
  and and_306 (and_306_out, and_282_out, xor_190_out);
  and and_307 (and_307_out, and_284_out, xor_192_out);
  and and_308 (and_308_out, and_286_out, xor_194_out);
  and and_309 (and_309_out, and_288_out, xor_196_out);
  and and_310 (and_310_out, and_290_out, xor_198_out);
  and and_311 (and_311_out, and_292_out, xor_200_out);
  and and_312 (and_312_out, and_294_out, xor_202_out);
  and and_313 (and_313_out, and_296_out, xor_204_out);
  and and_314 (and_314_out, and_298_out, xor_206_out);
  and and_315 (and_315_out, and_300_out, xor_208_out);
  or or_106 (or_106_out, and_346_out, and_319_out);
  or or_107 (or_107_out, and_347_out, and_321_out);
  or or_108 (or_108_out, and_348_out, and_323_out);
  or or_109 (or_109_out, and_349_out, and_325_out);
  or or_110 (or_110_out, and_350_out, and_327_out);
  or or_111 (or_111_out, and_351_out, and_329_out);
  or or_112 (or_112_out, and_352_out, and_331_out);
  or or_113 (or_113_out, and_353_out, and_333_out);
  or or_114 (or_114_out, and_354_out, and_335_out);
  or or_115 (or_115_out, and_355_out, and_337_out);
  or or_116 (or_116_out, and_356_out, and_339_out);
  or or_117 (or_117_out, and_357_out, and_341_out);
  or or_118 (or_118_out, and_358_out, and_343_out);
  or or_119 (or_119_out, and_359_out, and_345_out);
  and and_316 (and_316_out, Bit16_A[1], Bit16_B[15]);
  and and_317 (and_317_out, or_120_out, and_316_out);
  xor xor_211 (xor_211_out, and_316_out, or_120_out);
  and and_318 (and_318_out, Bit16_A[2], Bit16_B[14]);
  xor xor_212 (xor_212_out, and_318_out, xor_211_out);
  and and_319 (and_319_out, or_121_out, xor_212_out);
  xor xor_213 (xor_213_out, xor_212_out, or_121_out);
  and and_320 (and_320_out, Bit16_A[3], Bit16_B[13]);
  xor xor_214 (xor_214_out, and_320_out, xor_213_out);
  and and_321 (and_321_out, or_122_out, xor_214_out);
  xor xor_215 (xor_215_out, xor_214_out, or_122_out);
  and and_322 (and_322_out, Bit16_A[4], Bit16_B[12]);
  xor xor_216 (xor_216_out, and_322_out, xor_215_out);
  and and_323 (and_323_out, or_123_out, xor_216_out);
  xor xor_217 (xor_217_out, xor_216_out, or_123_out);
  and and_324 (and_324_out, Bit16_A[5], Bit16_B[11]);
  xor xor_218 (xor_218_out, and_324_out, xor_217_out);
  and and_325 (and_325_out, or_124_out, xor_218_out);
  xor xor_219 (xor_219_out, xor_218_out, or_124_out);
  and and_326 (and_326_out, Bit16_A[6], Bit16_B[10]);
  xor xor_220 (xor_220_out, and_326_out, xor_219_out);
  and and_327 (and_327_out, or_125_out, xor_220_out);
  xor xor_221 (xor_221_out, xor_220_out, or_125_out);
  and and_328 (and_328_out, Bit16_A[7], Bit16_B[9]);
  xor xor_222 (xor_222_out, and_328_out, xor_221_out);
  and and_329 (and_329_out, or_126_out, xor_222_out);
  xor xor_223 (xor_223_out, xor_222_out, or_126_out);
  and and_330 (and_330_out, Bit16_A[8], Bit16_B[8]);
  xor xor_224 (xor_224_out, and_330_out, xor_223_out);
  and and_331 (and_331_out, or_127_out, xor_224_out);
  xor xor_225 (xor_225_out, xor_224_out, or_127_out);
  and and_332 (and_332_out, Bit16_A[9], Bit16_B[7]);
  xor xor_226 (xor_226_out, and_332_out, xor_225_out);
  and and_333 (and_333_out, or_128_out, xor_226_out);
  xor xor_227 (xor_227_out, xor_226_out, or_128_out);
  and and_334 (and_334_out, Bit16_A[10], Bit16_B[6]);
  xor xor_228 (xor_228_out, and_334_out, xor_227_out);
  and and_335 (and_335_out, or_129_out, xor_228_out);
  xor xor_229 (xor_229_out, xor_228_out, or_129_out);
  and and_336 (and_336_out, Bit16_A[11], Bit16_B[5]);
  xor xor_230 (xor_230_out, and_336_out, xor_229_out);
  and and_337 (and_337_out, or_130_out, xor_230_out);
  xor xor_231 (xor_231_out, xor_230_out, or_130_out);
  and and_338 (and_338_out, Bit16_A[12], Bit16_B[4]);
  xor xor_232 (xor_232_out, and_338_out, xor_231_out);
  and and_339 (and_339_out, or_131_out, xor_232_out);
  xor xor_233 (xor_233_out, xor_232_out, or_131_out);
  and and_340 (and_340_out, Bit16_A[13], Bit16_B[3]);
  xor xor_234 (xor_234_out, and_340_out, xor_233_out);
  and and_341 (and_341_out, or_132_out, xor_234_out);
  xor xor_235 (xor_235_out, xor_234_out, or_132_out);
  and and_342 (and_342_out, Bit16_A[14], Bit16_B[2]);
  xor xor_236 (xor_236_out, and_342_out, xor_235_out);
  and and_343 (and_343_out, or_133_out, xor_236_out);
  xor xor_237 (xor_237_out, xor_236_out, or_133_out);
  and and_344 (and_344_out, Bit16_A[15], Bit16_B[1]);
  xor xor_238 (xor_238_out, and_344_out, xor_237_out);
  and and_345 (and_345_out, and_404_out, xor_238_out);
  xor xor_239 (Upper_Word[0], xor_238_out, and_404_out);
  and and_346 (and_346_out, and_318_out, xor_211_out);
  and and_347 (and_347_out, and_320_out, xor_213_out);
  and and_348 (and_348_out, and_322_out, xor_215_out);
  and and_349 (and_349_out, and_324_out, xor_217_out);
  and and_350 (and_350_out, and_326_out, xor_219_out);
  and and_351 (and_351_out, and_328_out, xor_221_out);
  and and_352 (and_352_out, and_330_out, xor_223_out);
  and and_353 (and_353_out, and_332_out, xor_225_out);
  and and_354 (and_354_out, and_334_out, xor_227_out);
  and and_355 (and_355_out, and_336_out, xor_229_out);
  and and_356 (and_356_out, and_338_out, xor_231_out);
  and and_357 (and_357_out, and_340_out, xor_233_out);
  and and_358 (and_358_out, and_342_out, xor_235_out);
  and and_359 (and_359_out, and_344_out, xor_237_out);
  and and_360 (and_360_out, Bit16_A[0], Bit16_B[15]);
  or or_120 (or_120_out, and_390_out, and_362_out);
  or or_121 (or_121_out, and_391_out, and_364_out);
  or or_122 (or_122_out, and_392_out, and_366_out);
  or or_123 (or_123_out, and_393_out, and_368_out);
  or or_124 (or_124_out, and_394_out, and_370_out);
  or or_125 (or_125_out, and_395_out, and_372_out);
  or or_126 (or_126_out, and_396_out, and_374_out);
  or or_127 (or_127_out, and_397_out, and_376_out);
  or or_128 (or_128_out, and_398_out, and_378_out);
  or or_129 (or_129_out, and_399_out, and_380_out);
  or or_130 (or_130_out, and_400_out, and_382_out);
  or or_131 (or_131_out, and_401_out, and_384_out);
  or or_132 (or_132_out, and_402_out, and_386_out);
  or or_133 (or_133_out, and_403_out, and_388_out);
  and and_361 (and_361_out, Bit16_A[1], Bit16_B[14]);
  xor xor_240 (xor_240_out, and_361_out, and_360_out);
  and and_362 (and_362_out, or_134_out, xor_240_out);
  xor xor_241 (xor_241_out, xor_240_out, or_134_out);
  and and_363 (and_363_out, Bit16_A[2], Bit16_B[13]);
  xor xor_242 (xor_242_out, and_363_out, xor_241_out);
  and and_364 (and_364_out, or_135_out, xor_242_out);
  xor xor_243 (xor_243_out, xor_242_out, or_135_out);
  and and_365 (and_365_out, Bit16_A[3], Bit16_B[12]);
  xor xor_244 (xor_244_out, and_365_out, xor_243_out);
  and and_366 (and_366_out, or_136_out, xor_244_out);
  xor xor_245 (xor_245_out, xor_244_out, or_136_out);
  and and_367 (and_367_out, Bit16_A[4], Bit16_B[11]);
  xor xor_246 (xor_246_out, and_367_out, xor_245_out);
  and and_368 (and_368_out, or_137_out, xor_246_out);
  xor xor_247 (xor_247_out, xor_246_out, or_137_out);
  and and_369 (and_369_out, Bit16_A[5], Bit16_B[10]);
  xor xor_248 (xor_248_out, and_369_out, xor_247_out);
  and and_370 (and_370_out, or_138_out, xor_248_out);
  xor xor_249 (xor_249_out, xor_248_out, or_138_out);
  and and_371 (and_371_out, Bit16_A[6], Bit16_B[9]);
  xor xor_250 (xor_250_out, and_371_out, xor_249_out);
  and and_372 (and_372_out, or_139_out, xor_250_out);
  xor xor_251 (xor_251_out, xor_250_out, or_139_out);
  and and_373 (and_373_out, Bit16_A[7], Bit16_B[8]);
  xor xor_252 (xor_252_out, and_373_out, xor_251_out);
  and and_374 (and_374_out, or_140_out, xor_252_out);
  xor xor_253 (xor_253_out, xor_252_out, or_140_out);
  and and_375 (and_375_out, Bit16_A[8], Bit16_B[7]);
  xor xor_254 (xor_254_out, and_375_out, xor_253_out);
  and and_376 (and_376_out, or_141_out, xor_254_out);
  xor xor_255 (xor_255_out, xor_254_out, or_141_out);
  and and_377 (and_377_out, Bit16_A[9], Bit16_B[6]);
  xor xor_256 (xor_256_out, and_377_out, xor_255_out);
  and and_378 (and_378_out, or_142_out, xor_256_out);
  xor xor_257 (xor_257_out, xor_256_out, or_142_out);
  and and_379 (and_379_out, Bit16_A[10], Bit16_B[5]);
  xor xor_258 (xor_258_out, and_379_out, xor_257_out);
  and and_380 (and_380_out, or_143_out, xor_258_out);
  xor xor_259 (xor_259_out, xor_258_out, or_143_out);
  and and_381 (and_381_out, Bit16_A[11], Bit16_B[4]);
  xor xor_260 (xor_260_out, and_381_out, xor_259_out);
  and and_382 (and_382_out, or_144_out, xor_260_out);
  xor xor_261 (xor_261_out, xor_260_out, or_144_out);
  and and_383 (and_383_out, Bit16_A[12], Bit16_B[3]);
  xor xor_262 (xor_262_out, and_383_out, xor_261_out);
  and and_384 (and_384_out, or_145_out, xor_262_out);
  xor xor_263 (xor_263_out, xor_262_out, or_145_out);
  and and_385 (and_385_out, Bit16_A[13], Bit16_B[2]);
  xor xor_264 (xor_264_out, and_385_out, xor_263_out);
  and and_386 (and_386_out, or_146_out, xor_264_out);
  xor xor_265 (xor_265_out, xor_264_out, or_146_out);
  and and_387 (and_387_out, Bit16_A[14], Bit16_B[1]);
  xor xor_266 (xor_266_out, and_387_out, xor_265_out);
  and and_388 (and_388_out, and_446_out, xor_266_out);
  xor xor_267 (xor_267_out, xor_266_out, and_446_out);
  and and_389 (and_389_out, Bit16_A[15], Bit16_B[0]);
  xor xor_268 (Lower_Word[15], and_389_out, xor_267_out);
  and and_390 (and_390_out, and_361_out, and_360_out);
  and and_391 (and_391_out, and_363_out, xor_241_out);
  and and_392 (and_392_out, and_365_out, xor_243_out);
  and and_393 (and_393_out, and_367_out, xor_245_out);
  and and_394 (and_394_out, and_369_out, xor_247_out);
  and and_395 (and_395_out, and_371_out, xor_249_out);
  and and_396 (and_396_out, and_373_out, xor_251_out);
  and and_397 (and_397_out, and_375_out, xor_253_out);
  and and_398 (and_398_out, and_377_out, xor_255_out);
  and and_399 (and_399_out, and_379_out, xor_257_out);
  and and_400 (and_400_out, and_381_out, xor_259_out);
  and and_401 (and_401_out, and_383_out, xor_261_out);
  and and_402 (and_402_out, and_385_out, xor_263_out);
  and and_403 (and_403_out, and_387_out, xor_265_out);
  and and_404 (and_404_out, and_389_out, xor_267_out);
  and and_405 (and_405_out, Bit16_A[0], Bit16_B[14]);
  or or_134 (or_134_out, and_433_out, and_407_out);
  or or_135 (or_135_out, and_434_out, and_409_out);
  or or_136 (or_136_out, and_435_out, and_411_out);
  or or_137 (or_137_out, and_436_out, and_413_out);
  or or_138 (or_138_out, and_437_out, and_415_out);
  or or_139 (or_139_out, and_438_out, and_417_out);
  or or_140 (or_140_out, and_439_out, and_419_out);
  or or_141 (or_141_out, and_440_out, and_421_out);
  or or_142 (or_142_out, and_441_out, and_423_out);
  or or_143 (or_143_out, and_442_out, and_425_out);
  or or_144 (or_144_out, and_443_out, and_427_out);
  or or_145 (or_145_out, and_444_out, and_429_out);
  or or_146 (or_146_out, and_445_out, and_431_out);
  and and_406 (and_406_out, Bit16_A[1], Bit16_B[13]);
  xor xor_269 (xor_269_out, and_406_out, and_405_out);
  and and_407 (and_407_out, or_147_out, xor_269_out);
  xor xor_270 (xor_270_out, xor_269_out, or_147_out);
  and and_408 (and_408_out, Bit16_A[2], Bit16_B[12]);
  xor xor_271 (xor_271_out, and_408_out, xor_270_out);
  and and_409 (and_409_out, or_148_out, xor_271_out);
  xor xor_272 (xor_272_out, xor_271_out, or_148_out);
  and and_410 (and_410_out, Bit16_A[3], Bit16_B[11]);
  xor xor_273 (xor_273_out, and_410_out, xor_272_out);
  and and_411 (and_411_out, or_149_out, xor_273_out);
  xor xor_274 (xor_274_out, xor_273_out, or_149_out);
  and and_412 (and_412_out, Bit16_A[4], Bit16_B[10]);
  xor xor_275 (xor_275_out, and_412_out, xor_274_out);
  and and_413 (and_413_out, or_150_out, xor_275_out);
  xor xor_276 (xor_276_out, xor_275_out, or_150_out);
  and and_414 (and_414_out, Bit16_A[5], Bit16_B[9]);
  xor xor_277 (xor_277_out, and_414_out, xor_276_out);
  and and_415 (and_415_out, or_151_out, xor_277_out);
  xor xor_278 (xor_278_out, xor_277_out, or_151_out);
  and and_416 (and_416_out, Bit16_A[6], Bit16_B[8]);
  xor xor_279 (xor_279_out, and_416_out, xor_278_out);
  and and_417 (and_417_out, or_152_out, xor_279_out);
  xor xor_280 (xor_280_out, xor_279_out, or_152_out);
  and and_418 (and_418_out, Bit16_A[7], Bit16_B[7]);
  xor xor_281 (xor_281_out, and_418_out, xor_280_out);
  and and_419 (and_419_out, or_153_out, xor_281_out);
  xor xor_282 (xor_282_out, xor_281_out, or_153_out);
  and and_420 (and_420_out, Bit16_A[8], Bit16_B[6]);
  xor xor_283 (xor_283_out, and_420_out, xor_282_out);
  and and_421 (and_421_out, or_154_out, xor_283_out);
  xor xor_284 (xor_284_out, xor_283_out, or_154_out);
  and and_422 (and_422_out, Bit16_A[9], Bit16_B[5]);
  xor xor_285 (xor_285_out, and_422_out, xor_284_out);
  and and_423 (and_423_out, or_155_out, xor_285_out);
  xor xor_286 (xor_286_out, xor_285_out, or_155_out);
  and and_424 (and_424_out, Bit16_A[10], Bit16_B[4]);
  xor xor_287 (xor_287_out, and_424_out, xor_286_out);
  and and_425 (and_425_out, or_156_out, xor_287_out);
  xor xor_288 (xor_288_out, xor_287_out, or_156_out);
  and and_426 (and_426_out, Bit16_A[11], Bit16_B[3]);
  xor xor_289 (xor_289_out, and_426_out, xor_288_out);
  and and_427 (and_427_out, or_157_out, xor_289_out);
  xor xor_290 (xor_290_out, xor_289_out, or_157_out);
  and and_428 (and_428_out, Bit16_A[12], Bit16_B[2]);
  xor xor_291 (xor_291_out, and_428_out, xor_290_out);
  and and_429 (and_429_out, or_158_out, xor_291_out);
  xor xor_292 (xor_292_out, xor_291_out, or_158_out);
  and and_430 (and_430_out, Bit16_A[13], Bit16_B[1]);
  xor xor_293 (xor_293_out, and_430_out, xor_292_out);
  and and_431 (and_431_out, and_485_out, xor_293_out);
  xor xor_294 (xor_294_out, xor_293_out, and_485_out);
  and and_432 (and_432_out, Bit16_A[14], Bit16_B[0]);
  xor xor_295 (Lower_Word[14], and_432_out, xor_294_out);
  and and_433 (and_433_out, and_406_out, and_405_out);
  and and_434 (and_434_out, and_408_out, xor_270_out);
  and and_435 (and_435_out, and_410_out, xor_272_out);
  and and_436 (and_436_out, and_412_out, xor_274_out);
  and and_437 (and_437_out, and_414_out, xor_276_out);
  and and_438 (and_438_out, and_416_out, xor_278_out);
  and and_439 (and_439_out, and_418_out, xor_280_out);
  and and_440 (and_440_out, and_420_out, xor_282_out);
  and and_441 (and_441_out, and_422_out, xor_284_out);
  and and_442 (and_442_out, and_424_out, xor_286_out);
  and and_443 (and_443_out, and_426_out, xor_288_out);
  and and_444 (and_444_out, and_428_out, xor_290_out);
  and and_445 (and_445_out, and_430_out, xor_292_out);
  and and_446 (and_446_out, and_432_out, xor_294_out);
  and and_447 (and_447_out, Bit16_A[0], Bit16_B[13]);
  or or_147 (or_147_out, and_473_out, and_449_out);
  or or_148 (or_148_out, and_474_out, and_451_out);
  or or_149 (or_149_out, and_475_out, and_453_out);
  or or_150 (or_150_out, and_476_out, and_455_out);
  or or_151 (or_151_out, and_477_out, and_457_out);
  or or_152 (or_152_out, and_478_out, and_459_out);
  or or_153 (or_153_out, and_479_out, and_461_out);
  or or_154 (or_154_out, and_480_out, and_463_out);
  or or_155 (or_155_out, and_481_out, and_465_out);
  or or_156 (or_156_out, and_482_out, and_467_out);
  or or_157 (or_157_out, and_483_out, and_469_out);
  or or_158 (or_158_out, and_484_out, and_471_out);
  and and_448 (and_448_out, Bit16_A[1], Bit16_B[12]);
  xor xor_296 (xor_296_out, and_448_out, and_447_out);
  and and_449 (and_449_out, or_159_out, xor_296_out);
  xor xor_297 (xor_297_out, xor_296_out, or_159_out);
  and and_450 (and_450_out, Bit16_A[2], Bit16_B[11]);
  xor xor_298 (xor_298_out, and_450_out, xor_297_out);
  and and_451 (and_451_out, or_160_out, xor_298_out);
  xor xor_299 (xor_299_out, xor_298_out, or_160_out);
  and and_452 (and_452_out, Bit16_A[3], Bit16_B[10]);
  xor xor_300 (xor_300_out, and_452_out, xor_299_out);
  and and_453 (and_453_out, or_161_out, xor_300_out);
  xor xor_301 (xor_301_out, xor_300_out, or_161_out);
  and and_454 (and_454_out, Bit16_A[4], Bit16_B[9]);
  xor xor_302 (xor_302_out, and_454_out, xor_301_out);
  and and_455 (and_455_out, or_162_out, xor_302_out);
  xor xor_303 (xor_303_out, xor_302_out, or_162_out);
  and and_456 (and_456_out, Bit16_A[5], Bit16_B[8]);
  xor xor_304 (xor_304_out, and_456_out, xor_303_out);
  and and_457 (and_457_out, or_163_out, xor_304_out);
  xor xor_305 (xor_305_out, xor_304_out, or_163_out);
  and and_458 (and_458_out, Bit16_A[6], Bit16_B[7]);
  xor xor_306 (xor_306_out, and_458_out, xor_305_out);
  and and_459 (and_459_out, or_164_out, xor_306_out);
  xor xor_307 (xor_307_out, xor_306_out, or_164_out);
  and and_460 (and_460_out, Bit16_A[7], Bit16_B[6]);
  xor xor_308 (xor_308_out, and_460_out, xor_307_out);
  and and_461 (and_461_out, or_165_out, xor_308_out);
  xor xor_309 (xor_309_out, xor_308_out, or_165_out);
  and and_462 (and_462_out, Bit16_A[8], Bit16_B[5]);
  xor xor_310 (xor_310_out, and_462_out, xor_309_out);
  and and_463 (and_463_out, or_166_out, xor_310_out);
  xor xor_311 (xor_311_out, xor_310_out, or_166_out);
  and and_464 (and_464_out, Bit16_A[9], Bit16_B[4]);
  xor xor_312 (xor_312_out, and_464_out, xor_311_out);
  and and_465 (and_465_out, or_167_out, xor_312_out);
  xor xor_313 (xor_313_out, xor_312_out, or_167_out);
  and and_466 (and_466_out, Bit16_A[10], Bit16_B[3]);
  xor xor_314 (xor_314_out, and_466_out, xor_313_out);
  and and_467 (and_467_out, or_168_out, xor_314_out);
  xor xor_315 (xor_315_out, xor_314_out, or_168_out);
  and and_468 (and_468_out, Bit16_A[11], Bit16_B[2]);
  xor xor_316 (xor_316_out, and_468_out, xor_315_out);
  and and_469 (and_469_out, or_169_out, xor_316_out);
  xor xor_317 (xor_317_out, xor_316_out, or_169_out);
  and and_470 (and_470_out, Bit16_A[12], Bit16_B[1]);
  xor xor_318 (xor_318_out, and_470_out, xor_317_out);
  and and_471 (and_471_out, and_521_out, xor_318_out);
  xor xor_319 (xor_319_out, xor_318_out, and_521_out);
  and and_472 (and_472_out, Bit16_A[13], Bit16_B[0]);
  xor xor_320 (Lower_Word[13], and_472_out, xor_319_out);
  and and_473 (and_473_out, and_448_out, and_447_out);
  and and_474 (and_474_out, and_450_out, xor_297_out);
  and and_475 (and_475_out, and_452_out, xor_299_out);
  and and_476 (and_476_out, and_454_out, xor_301_out);
  and and_477 (and_477_out, and_456_out, xor_303_out);
  and and_478 (and_478_out, and_458_out, xor_305_out);
  and and_479 (and_479_out, and_460_out, xor_307_out);
  and and_480 (and_480_out, and_462_out, xor_309_out);
  and and_481 (and_481_out, and_464_out, xor_311_out);
  and and_482 (and_482_out, and_466_out, xor_313_out);
  and and_483 (and_483_out, and_468_out, xor_315_out);
  and and_484 (and_484_out, and_470_out, xor_317_out);
  and and_485 (and_485_out, and_472_out, xor_319_out);
  and and_486 (and_486_out, Bit16_A[0], Bit16_B[12]);
  or or_159 (or_159_out, and_510_out, and_488_out);
  or or_160 (or_160_out, and_511_out, and_490_out);
  or or_161 (or_161_out, and_512_out, and_492_out);
  or or_162 (or_162_out, and_513_out, and_494_out);
  or or_163 (or_163_out, and_514_out, and_496_out);
  or or_164 (or_164_out, and_515_out, and_498_out);
  or or_165 (or_165_out, and_516_out, and_500_out);
  or or_166 (or_166_out, and_517_out, and_502_out);
  or or_167 (or_167_out, and_518_out, and_504_out);
  or or_168 (or_168_out, and_519_out, and_506_out);
  or or_169 (or_169_out, and_520_out, and_508_out);
  and and_487 (and_487_out, Bit16_A[1], Bit16_B[11]);
  xor xor_321 (xor_321_out, and_487_out, and_486_out);
  and and_488 (and_488_out, or_170_out, xor_321_out);
  xor xor_322 (xor_322_out, xor_321_out, or_170_out);
  and and_489 (and_489_out, Bit16_A[2], Bit16_B[10]);
  xor xor_323 (xor_323_out, and_489_out, xor_322_out);
  and and_490 (and_490_out, or_171_out, xor_323_out);
  xor xor_324 (xor_324_out, xor_323_out, or_171_out);
  and and_491 (and_491_out, Bit16_A[3], Bit16_B[9]);
  xor xor_325 (xor_325_out, and_491_out, xor_324_out);
  and and_492 (and_492_out, or_172_out, xor_325_out);
  xor xor_326 (xor_326_out, xor_325_out, or_172_out);
  and and_493 (and_493_out, Bit16_A[4], Bit16_B[8]);
  xor xor_327 (xor_327_out, and_493_out, xor_326_out);
  and and_494 (and_494_out, or_173_out, xor_327_out);
  xor xor_328 (xor_328_out, xor_327_out, or_173_out);
  and and_495 (and_495_out, Bit16_A[5], Bit16_B[7]);
  xor xor_329 (xor_329_out, and_495_out, xor_328_out);
  and and_496 (and_496_out, or_174_out, xor_329_out);
  xor xor_330 (xor_330_out, xor_329_out, or_174_out);
  and and_497 (and_497_out, Bit16_A[6], Bit16_B[6]);
  xor xor_331 (xor_331_out, and_497_out, xor_330_out);
  and and_498 (and_498_out, or_175_out, xor_331_out);
  xor xor_332 (xor_332_out, xor_331_out, or_175_out);
  and and_499 (and_499_out, Bit16_A[7], Bit16_B[5]);
  xor xor_333 (xor_333_out, and_499_out, xor_332_out);
  and and_500 (and_500_out, or_176_out, xor_333_out);
  xor xor_334 (xor_334_out, xor_333_out, or_176_out);
  and and_501 (and_501_out, Bit16_A[8], Bit16_B[4]);
  xor xor_335 (xor_335_out, and_501_out, xor_334_out);
  and and_502 (and_502_out, or_177_out, xor_335_out);
  xor xor_336 (xor_336_out, xor_335_out, or_177_out);
  and and_503 (and_503_out, Bit16_A[9], Bit16_B[3]);
  xor xor_337 (xor_337_out, and_503_out, xor_336_out);
  and and_504 (and_504_out, or_178_out, xor_337_out);
  xor xor_338 (xor_338_out, xor_337_out, or_178_out);
  and and_505 (and_505_out, Bit16_A[10], Bit16_B[2]);
  xor xor_339 (xor_339_out, and_505_out, xor_338_out);
  and and_506 (and_506_out, or_179_out, xor_339_out);
  xor xor_340 (xor_340_out, xor_339_out, or_179_out);
  and and_507 (and_507_out, Bit16_A[11], Bit16_B[1]);
  xor xor_341 (xor_341_out, and_507_out, xor_340_out);
  and and_508 (and_508_out, and_554_out, xor_341_out);
  xor xor_342 (xor_342_out, xor_341_out, and_554_out);
  and and_509 (and_509_out, Bit16_A[12], Bit16_B[0]);
  xor xor_343 (Lower_Word[12], and_509_out, xor_342_out);
  and and_510 (and_510_out, and_487_out, and_486_out);
  and and_511 (and_511_out, and_489_out, xor_322_out);
  and and_512 (and_512_out, and_491_out, xor_324_out);
  and and_513 (and_513_out, and_493_out, xor_326_out);
  and and_514 (and_514_out, and_495_out, xor_328_out);
  and and_515 (and_515_out, and_497_out, xor_330_out);
  and and_516 (and_516_out, and_499_out, xor_332_out);
  and and_517 (and_517_out, and_501_out, xor_334_out);
  and and_518 (and_518_out, and_503_out, xor_336_out);
  and and_519 (and_519_out, and_505_out, xor_338_out);
  and and_520 (and_520_out, and_507_out, xor_340_out);
  and and_521 (and_521_out, and_509_out, xor_342_out);
  and and_522 (and_522_out, Bit16_A[0], Bit16_B[11]);
  or or_170 (or_170_out, and_544_out, and_524_out);
  or or_171 (or_171_out, and_545_out, and_526_out);
  or or_172 (or_172_out, and_546_out, and_528_out);
  or or_173 (or_173_out, and_547_out, and_530_out);
  or or_174 (or_174_out, and_548_out, and_532_out);
  or or_175 (or_175_out, and_549_out, and_534_out);
  or or_176 (or_176_out, and_550_out, and_536_out);
  or or_177 (or_177_out, and_551_out, and_538_out);
  or or_178 (or_178_out, and_552_out, and_540_out);
  or or_179 (or_179_out, and_553_out, and_542_out);
  and and_523 (and_523_out, Bit16_A[1], Bit16_B[10]);
  xor xor_344 (xor_344_out, and_523_out, and_522_out);
  and and_524 (and_524_out, or_180_out, xor_344_out);
  xor xor_345 (xor_345_out, xor_344_out, or_180_out);
  and and_525 (and_525_out, Bit16_A[2], Bit16_B[9]);
  xor xor_346 (xor_346_out, and_525_out, xor_345_out);
  and and_526 (and_526_out, or_181_out, xor_346_out);
  xor xor_347 (xor_347_out, xor_346_out, or_181_out);
  and and_527 (and_527_out, Bit16_A[3], Bit16_B[8]);
  xor xor_348 (xor_348_out, and_527_out, xor_347_out);
  and and_528 (and_528_out, or_182_out, xor_348_out);
  xor xor_349 (xor_349_out, xor_348_out, or_182_out);
  and and_529 (and_529_out, Bit16_A[4], Bit16_B[7]);
  xor xor_350 (xor_350_out, and_529_out, xor_349_out);
  and and_530 (and_530_out, or_183_out, xor_350_out);
  xor xor_351 (xor_351_out, xor_350_out, or_183_out);
  and and_531 (and_531_out, Bit16_A[5], Bit16_B[6]);
  xor xor_352 (xor_352_out, and_531_out, xor_351_out);
  and and_532 (and_532_out, or_184_out, xor_352_out);
  xor xor_353 (xor_353_out, xor_352_out, or_184_out);
  and and_533 (and_533_out, Bit16_A[6], Bit16_B[5]);
  xor xor_354 (xor_354_out, and_533_out, xor_353_out);
  and and_534 (and_534_out, or_185_out, xor_354_out);
  xor xor_355 (xor_355_out, xor_354_out, or_185_out);
  and and_535 (and_535_out, Bit16_A[7], Bit16_B[4]);
  xor xor_356 (xor_356_out, and_535_out, xor_355_out);
  and and_536 (and_536_out, or_186_out, xor_356_out);
  xor xor_357 (xor_357_out, xor_356_out, or_186_out);
  and and_537 (and_537_out, Bit16_A[8], Bit16_B[3]);
  xor xor_358 (xor_358_out, and_537_out, xor_357_out);
  and and_538 (and_538_out, or_187_out, xor_358_out);
  xor xor_359 (xor_359_out, xor_358_out, or_187_out);
  and and_539 (and_539_out, Bit16_A[9], Bit16_B[2]);
  xor xor_360 (xor_360_out, and_539_out, xor_359_out);
  and and_540 (and_540_out, or_188_out, xor_360_out);
  xor xor_361 (xor_361_out, xor_360_out, or_188_out);
  and and_541 (and_541_out, Bit16_A[10], Bit16_B[1]);
  xor xor_362 (xor_362_out, and_541_out, xor_361_out);
  and and_542 (and_542_out, and_584_out, xor_362_out);
  xor xor_363 (xor_363_out, xor_362_out, and_584_out);
  and and_543 (and_543_out, Bit16_A[11], Bit16_B[0]);
  xor xor_364 (Lower_Word[11], and_543_out, xor_363_out);
  and and_544 (and_544_out, and_523_out, and_522_out);
  and and_545 (and_545_out, and_525_out, xor_345_out);
  and and_546 (and_546_out, and_527_out, xor_347_out);
  and and_547 (and_547_out, and_529_out, xor_349_out);
  and and_548 (and_548_out, and_531_out, xor_351_out);
  and and_549 (and_549_out, and_533_out, xor_353_out);
  and and_550 (and_550_out, and_535_out, xor_355_out);
  and and_551 (and_551_out, and_537_out, xor_357_out);
  and and_552 (and_552_out, and_539_out, xor_359_out);
  and and_553 (and_553_out, and_541_out, xor_361_out);
  and and_554 (and_554_out, and_543_out, xor_363_out);
  and and_555 (and_555_out, Bit16_A[0], Bit16_B[10]);
  or or_180 (or_180_out, and_575_out, and_557_out);
  or or_181 (or_181_out, and_576_out, and_559_out);
  or or_182 (or_182_out, and_577_out, and_561_out);
  or or_183 (or_183_out, and_578_out, and_563_out);
  or or_184 (or_184_out, and_579_out, and_565_out);
  or or_185 (or_185_out, and_580_out, and_567_out);
  or or_186 (or_186_out, and_581_out, and_569_out);
  or or_187 (or_187_out, and_582_out, and_571_out);
  or or_188 (or_188_out, and_583_out, and_573_out);
  and and_556 (and_556_out, Bit16_A[1], Bit16_B[9]);
  xor xor_365 (xor_365_out, and_556_out, and_555_out);
  and and_557 (and_557_out, or_189_out, xor_365_out);
  xor xor_366 (xor_366_out, xor_365_out, or_189_out);
  and and_558 (and_558_out, Bit16_A[2], Bit16_B[8]);
  xor xor_367 (xor_367_out, and_558_out, xor_366_out);
  and and_559 (and_559_out, or_190_out, xor_367_out);
  xor xor_368 (xor_368_out, xor_367_out, or_190_out);
  and and_560 (and_560_out, Bit16_A[3], Bit16_B[7]);
  xor xor_369 (xor_369_out, and_560_out, xor_368_out);
  and and_561 (and_561_out, or_191_out, xor_369_out);
  xor xor_370 (xor_370_out, xor_369_out, or_191_out);
  and and_562 (and_562_out, Bit16_A[4], Bit16_B[6]);
  xor xor_371 (xor_371_out, and_562_out, xor_370_out);
  and and_563 (and_563_out, or_192_out, xor_371_out);
  xor xor_372 (xor_372_out, xor_371_out, or_192_out);
  and and_564 (and_564_out, Bit16_A[5], Bit16_B[5]);
  xor xor_373 (xor_373_out, and_564_out, xor_372_out);
  and and_565 (and_565_out, or_193_out, xor_373_out);
  xor xor_374 (xor_374_out, xor_373_out, or_193_out);
  and and_566 (and_566_out, Bit16_A[6], Bit16_B[4]);
  xor xor_375 (xor_375_out, and_566_out, xor_374_out);
  and and_567 (and_567_out, or_194_out, xor_375_out);
  xor xor_376 (xor_376_out, xor_375_out, or_194_out);
  and and_568 (and_568_out, Bit16_A[7], Bit16_B[3]);
  xor xor_377 (xor_377_out, and_568_out, xor_376_out);
  and and_569 (and_569_out, or_195_out, xor_377_out);
  xor xor_378 (xor_378_out, xor_377_out, or_195_out);
  and and_570 (and_570_out, Bit16_A[8], Bit16_B[2]);
  xor xor_379 (xor_379_out, and_570_out, xor_378_out);
  and and_571 (and_571_out, or_196_out, xor_379_out);
  xor xor_380 (xor_380_out, xor_379_out, or_196_out);
  and and_572 (and_572_out, Bit16_A[9], Bit16_B[1]);
  xor xor_381 (xor_381_out, and_572_out, xor_380_out);
  and and_573 (and_573_out, and_611_out, xor_381_out);
  xor xor_382 (xor_382_out, xor_381_out, and_611_out);
  and and_574 (and_574_out, Bit16_A[10], Bit16_B[0]);
  xor xor_383 (Lower_Word[10], and_574_out, xor_382_out);
  and and_575 (and_575_out, and_556_out, and_555_out);
  and and_576 (and_576_out, and_558_out, xor_366_out);
  and and_577 (and_577_out, and_560_out, xor_368_out);
  and and_578 (and_578_out, and_562_out, xor_370_out);
  and and_579 (and_579_out, and_564_out, xor_372_out);
  and and_580 (and_580_out, and_566_out, xor_374_out);
  and and_581 (and_581_out, and_568_out, xor_376_out);
  and and_582 (and_582_out, and_570_out, xor_378_out);
  and and_583 (and_583_out, and_572_out, xor_380_out);
  and and_584 (and_584_out, and_574_out, xor_382_out);
  and and_585 (and_585_out, Bit16_A[0], Bit16_B[9]);
  or or_189 (or_189_out, and_603_out, and_587_out);
  or or_190 (or_190_out, and_604_out, and_589_out);
  or or_191 (or_191_out, and_605_out, and_591_out);
  or or_192 (or_192_out, and_606_out, and_593_out);
  or or_193 (or_193_out, and_607_out, and_595_out);
  or or_194 (or_194_out, and_608_out, and_597_out);
  or or_195 (or_195_out, and_609_out, and_599_out);
  or or_196 (or_196_out, and_610_out, and_601_out);
  and and_586 (and_586_out, Bit16_A[1], Bit16_B[8]);
  xor xor_384 (xor_384_out, and_586_out, and_585_out);
  and and_587 (and_587_out, or_197_out, xor_384_out);
  xor xor_385 (xor_385_out, xor_384_out, or_197_out);
  and and_588 (and_588_out, Bit16_A[2], Bit16_B[7]);
  xor xor_386 (xor_386_out, and_588_out, xor_385_out);
  and and_589 (and_589_out, or_198_out, xor_386_out);
  xor xor_387 (xor_387_out, xor_386_out, or_198_out);
  and and_590 (and_590_out, Bit16_A[3], Bit16_B[6]);
  xor xor_388 (xor_388_out, and_590_out, xor_387_out);
  and and_591 (and_591_out, or_199_out, xor_388_out);
  xor xor_389 (xor_389_out, xor_388_out, or_199_out);
  and and_592 (and_592_out, Bit16_A[4], Bit16_B[5]);
  xor xor_390 (xor_390_out, and_592_out, xor_389_out);
  and and_593 (and_593_out, or_200_out, xor_390_out);
  xor xor_391 (xor_391_out, xor_390_out, or_200_out);
  and and_594 (and_594_out, Bit16_A[5], Bit16_B[4]);
  xor xor_392 (xor_392_out, and_594_out, xor_391_out);
  and and_595 (and_595_out, or_201_out, xor_392_out);
  xor xor_393 (xor_393_out, xor_392_out, or_201_out);
  and and_596 (and_596_out, Bit16_A[6], Bit16_B[3]);
  xor xor_394 (xor_394_out, and_596_out, xor_393_out);
  and and_597 (and_597_out, or_202_out, xor_394_out);
  xor xor_395 (xor_395_out, xor_394_out, or_202_out);
  and and_598 (and_598_out, Bit16_A[7], Bit16_B[2]);
  xor xor_396 (xor_396_out, and_598_out, xor_395_out);
  and and_599 (and_599_out, or_203_out, xor_396_out);
  xor xor_397 (xor_397_out, xor_396_out, or_203_out);
  and and_600 (and_600_out, Bit16_A[8], Bit16_B[1]);
  xor xor_398 (xor_398_out, and_600_out, xor_397_out);
  and and_601 (and_601_out, and_635_out, xor_398_out);
  xor xor_399 (xor_399_out, xor_398_out, and_635_out);
  and and_602 (and_602_out, Bit16_A[9], Bit16_B[0]);
  xor xor_400 (Lower_Word[9], and_602_out, xor_399_out);
  and and_603 (and_603_out, and_586_out, and_585_out);
  and and_604 (and_604_out, and_588_out, xor_385_out);
  and and_605 (and_605_out, and_590_out, xor_387_out);
  and and_606 (and_606_out, and_592_out, xor_389_out);
  and and_607 (and_607_out, and_594_out, xor_391_out);
  and and_608 (and_608_out, and_596_out, xor_393_out);
  and and_609 (and_609_out, and_598_out, xor_395_out);
  and and_610 (and_610_out, and_600_out, xor_397_out);
  and and_611 (and_611_out, and_602_out, xor_399_out);
  and and_612 (and_612_out, Bit16_A[0], Bit16_B[8]);
  or or_197 (or_197_out, and_628_out, and_614_out);
  or or_198 (or_198_out, and_629_out, and_616_out);
  or or_199 (or_199_out, and_630_out, and_618_out);
  or or_200 (or_200_out, and_631_out, and_620_out);
  or or_201 (or_201_out, and_632_out, and_622_out);
  or or_202 (or_202_out, and_633_out, and_624_out);
  or or_203 (or_203_out, and_634_out, and_626_out);
  and and_613 (and_613_out, Bit16_A[1], Bit16_B[7]);
  xor xor_401 (xor_401_out, and_613_out, and_612_out);
  and and_614 (and_614_out, or_204_out, xor_401_out);
  xor xor_402 (xor_402_out, xor_401_out, or_204_out);
  and and_615 (and_615_out, Bit16_A[2], Bit16_B[6]);
  xor xor_403 (xor_403_out, and_615_out, xor_402_out);
  and and_616 (and_616_out, or_205_out, xor_403_out);
  xor xor_404 (xor_404_out, xor_403_out, or_205_out);
  and and_617 (and_617_out, Bit16_A[3], Bit16_B[5]);
  xor xor_405 (xor_405_out, and_617_out, xor_404_out);
  and and_618 (and_618_out, or_206_out, xor_405_out);
  xor xor_406 (xor_406_out, xor_405_out, or_206_out);
  and and_619 (and_619_out, Bit16_A[4], Bit16_B[4]);
  xor xor_407 (xor_407_out, and_619_out, xor_406_out);
  and and_620 (and_620_out, or_207_out, xor_407_out);
  xor xor_408 (xor_408_out, xor_407_out, or_207_out);
  and and_621 (and_621_out, Bit16_A[5], Bit16_B[3]);
  xor xor_409 (xor_409_out, and_621_out, xor_408_out);
  and and_622 (and_622_out, or_208_out, xor_409_out);
  xor xor_410 (xor_410_out, xor_409_out, or_208_out);
  and and_623 (and_623_out, Bit16_A[6], Bit16_B[2]);
  xor xor_411 (xor_411_out, and_623_out, xor_410_out);
  and and_624 (and_624_out, or_209_out, xor_411_out);
  xor xor_412 (xor_412_out, xor_411_out, or_209_out);
  and and_625 (and_625_out, Bit16_A[7], Bit16_B[1]);
  xor xor_413 (xor_413_out, and_625_out, xor_412_out);
  and and_626 (and_626_out, and_656_out, xor_413_out);
  xor xor_414 (xor_414_out, xor_413_out, and_656_out);
  and and_627 (and_627_out, Bit16_A[8], Bit16_B[0]);
  xor xor_415 (Lower_Word[8], and_627_out, xor_414_out);
  and and_628 (and_628_out, and_613_out, and_612_out);
  and and_629 (and_629_out, and_615_out, xor_402_out);
  and and_630 (and_630_out, and_617_out, xor_404_out);
  and and_631 (and_631_out, and_619_out, xor_406_out);
  and and_632 (and_632_out, and_621_out, xor_408_out);
  and and_633 (and_633_out, and_623_out, xor_410_out);
  and and_634 (and_634_out, and_625_out, xor_412_out);
  and and_635 (and_635_out, and_627_out, xor_414_out);
  and and_636 (and_636_out, Bit16_A[0], Bit16_B[7]);
  or or_204 (or_204_out, and_650_out, and_638_out);
  or or_205 (or_205_out, and_651_out, and_640_out);
  or or_206 (or_206_out, and_652_out, and_642_out);
  or or_207 (or_207_out, and_653_out, and_644_out);
  or or_208 (or_208_out, and_654_out, and_646_out);
  or or_209 (or_209_out, and_655_out, and_648_out);
  and and_637 (and_637_out, Bit16_A[1], Bit16_B[6]);
  xor xor_416 (xor_416_out, and_637_out, and_636_out);
  and and_638 (and_638_out, or_210_out, xor_416_out);
  xor xor_417 (xor_417_out, xor_416_out, or_210_out);
  and and_639 (and_639_out, Bit16_A[2], Bit16_B[5]);
  xor xor_418 (xor_418_out, and_639_out, xor_417_out);
  and and_640 (and_640_out, or_211_out, xor_418_out);
  xor xor_419 (xor_419_out, xor_418_out, or_211_out);
  and and_641 (and_641_out, Bit16_A[3], Bit16_B[4]);
  xor xor_420 (xor_420_out, and_641_out, xor_419_out);
  and and_642 (and_642_out, or_212_out, xor_420_out);
  xor xor_421 (xor_421_out, xor_420_out, or_212_out);
  and and_643 (and_643_out, Bit16_A[4], Bit16_B[3]);
  xor xor_422 (xor_422_out, and_643_out, xor_421_out);
  and and_644 (and_644_out, or_213_out, xor_422_out);
  xor xor_423 (xor_423_out, xor_422_out, or_213_out);
  and and_645 (and_645_out, Bit16_A[5], Bit16_B[2]);
  xor xor_424 (xor_424_out, and_645_out, xor_423_out);
  and and_646 (and_646_out, or_214_out, xor_424_out);
  xor xor_425 (xor_425_out, xor_424_out, or_214_out);
  and and_647 (and_647_out, Bit16_A[6], Bit16_B[1]);
  xor xor_426 (xor_426_out, and_647_out, xor_425_out);
  and and_648 (and_648_out, and_674_out, xor_426_out);
  xor xor_427 (xor_427_out, xor_426_out, and_674_out);
  and and_649 (and_649_out, Bit16_A[7], Bit16_B[0]);
  xor xor_428 (Lower_Word[7], and_649_out, xor_427_out);
  and and_650 (and_650_out, and_637_out, and_636_out);
  and and_651 (and_651_out, and_639_out, xor_417_out);
  and and_652 (and_652_out, and_641_out, xor_419_out);
  and and_653 (and_653_out, and_643_out, xor_421_out);
  and and_654 (and_654_out, and_645_out, xor_423_out);
  and and_655 (and_655_out, and_647_out, xor_425_out);
  and and_656 (and_656_out, and_649_out, xor_427_out);
  and and_657 (and_657_out, Bit16_A[0], Bit16_B[6]);
  or or_210 (or_210_out, and_669_out, and_659_out);
  or or_211 (or_211_out, and_670_out, and_661_out);
  or or_212 (or_212_out, and_671_out, and_663_out);
  or or_213 (or_213_out, and_672_out, and_665_out);
  or or_214 (or_214_out, and_673_out, and_667_out);
  and and_658 (and_658_out, Bit16_A[1], Bit16_B[5]);
  xor xor_429 (xor_429_out, and_658_out, and_657_out);
  and and_659 (and_659_out, or_215_out, xor_429_out);
  xor xor_430 (xor_430_out, xor_429_out, or_215_out);
  and and_660 (and_660_out, Bit16_A[2], Bit16_B[4]);
  xor xor_431 (xor_431_out, and_660_out, xor_430_out);
  and and_661 (and_661_out, or_216_out, xor_431_out);
  xor xor_432 (xor_432_out, xor_431_out, or_216_out);
  and and_662 (and_662_out, Bit16_A[3], Bit16_B[3]);
  xor xor_433 (xor_433_out, and_662_out, xor_432_out);
  and and_663 (and_663_out, or_217_out, xor_433_out);
  xor xor_434 (xor_434_out, xor_433_out, or_217_out);
  and and_664 (and_664_out, Bit16_A[4], Bit16_B[2]);
  xor xor_435 (xor_435_out, and_664_out, xor_434_out);
  and and_665 (and_665_out, or_218_out, xor_435_out);
  xor xor_436 (xor_436_out, xor_435_out, or_218_out);
  and and_666 (and_666_out, Bit16_A[5], Bit16_B[1]);
  xor xor_437 (xor_437_out, and_666_out, xor_436_out);
  and and_667 (and_667_out, and_689_out, xor_437_out);
  xor xor_438 (xor_438_out, xor_437_out, and_689_out);
  and and_668 (and_668_out, Bit16_A[6], Bit16_B[0]);
  xor xor_439 (Lower_Word[6], and_668_out, xor_438_out);
  and and_669 (and_669_out, and_658_out, and_657_out);
  and and_670 (and_670_out, and_660_out, xor_430_out);
  and and_671 (and_671_out, and_662_out, xor_432_out);
  and and_672 (and_672_out, and_664_out, xor_434_out);
  and and_673 (and_673_out, and_666_out, xor_436_out);
  and and_674 (and_674_out, and_668_out, xor_438_out);
  and and_675 (and_675_out, Bit16_A[0], Bit16_B[5]);
  or or_215 (or_215_out, and_685_out, and_677_out);
  or or_216 (or_216_out, and_686_out, and_679_out);
  or or_217 (or_217_out, and_687_out, and_681_out);
  or or_218 (or_218_out, and_688_out, and_683_out);
  and and_676 (and_676_out, Bit16_A[1], Bit16_B[4]);
  xor xor_440 (xor_440_out, and_676_out, and_675_out);
  and and_677 (and_677_out, or_219_out, xor_440_out);
  xor xor_441 (xor_441_out, xor_440_out, or_219_out);
  and and_678 (and_678_out, Bit16_A[2], Bit16_B[3]);
  xor xor_442 (xor_442_out, and_678_out, xor_441_out);
  and and_679 (and_679_out, or_220_out, xor_442_out);
  xor xor_443 (xor_443_out, xor_442_out, or_220_out);
  and and_680 (and_680_out, Bit16_A[3], Bit16_B[2]);
  xor xor_444 (xor_444_out, and_680_out, xor_443_out);
  and and_681 (and_681_out, or_221_out, xor_444_out);
  xor xor_445 (xor_445_out, xor_444_out, or_221_out);
  and and_682 (and_682_out, Bit16_A[4], Bit16_B[1]);
  xor xor_446 (xor_446_out, and_682_out, xor_445_out);
  and and_683 (and_683_out, and_701_out, xor_446_out);
  xor xor_447 (xor_447_out, xor_446_out, and_701_out);
  and and_684 (and_684_out, Bit16_A[5], Bit16_B[0]);
  xor xor_448 (Lower_Word[5], and_684_out, xor_447_out);
  and and_685 (and_685_out, and_676_out, and_675_out);
  and and_686 (and_686_out, and_678_out, xor_441_out);
  and and_687 (and_687_out, and_680_out, xor_443_out);
  and and_688 (and_688_out, and_682_out, xor_445_out);
  and and_689 (and_689_out, and_684_out, xor_447_out);
  and and_690 (and_690_out, Bit16_A[0], Bit16_B[4]);
  or or_219 (or_219_out, and_698_out, and_692_out);
  or or_220 (or_220_out, and_699_out, and_694_out);
  or or_221 (or_221_out, and_700_out, and_696_out);
  and and_691 (and_691_out, Bit16_A[1], Bit16_B[3]);
  xor xor_449 (xor_449_out, and_691_out, and_690_out);
  and and_692 (and_692_out, or_222_out, xor_449_out);
  xor xor_450 (xor_450_out, xor_449_out, or_222_out);
  and and_693 (and_693_out, Bit16_A[2], Bit16_B[2]);
  xor xor_451 (xor_451_out, and_693_out, xor_450_out);
  and and_694 (and_694_out, or_223_out, xor_451_out);
  xor xor_452 (xor_452_out, xor_451_out, or_223_out);
  and and_695 (and_695_out, Bit16_A[3], Bit16_B[1]);
  xor xor_453 (xor_453_out, and_695_out, xor_452_out);
  and and_696 (and_696_out, and_710_out, xor_453_out);
  xor xor_454 (xor_454_out, xor_453_out, and_710_out);
  and and_697 (and_697_out, Bit16_A[4], Bit16_B[0]);
  xor xor_455 (Lower_Word[4], and_697_out, xor_454_out);
  and and_698 (and_698_out, and_691_out, and_690_out);
  and and_699 (and_699_out, and_693_out, xor_450_out);
  and and_700 (and_700_out, and_695_out, xor_452_out);
  and and_701 (and_701_out, and_697_out, xor_454_out);
  and and_702 (and_702_out, Bit16_A[0], Bit16_B[3]);
  or or_222 (or_222_out, and_708_out, and_704_out);
  or or_223 (or_223_out, and_709_out, and_706_out);
  and and_703 (and_703_out, Bit16_A[1], Bit16_B[2]);
  xor xor_456 (xor_456_out, and_703_out, and_702_out);
  and and_704 (and_704_out, or_224_out, xor_456_out);
  xor xor_457 (xor_457_out, xor_456_out, or_224_out);
  and and_705 (and_705_out, Bit16_A[2], Bit16_B[1]);
  xor xor_458 (xor_458_out, and_705_out, xor_457_out);
  and and_706 (and_706_out, and_716_out, xor_458_out);
  xor xor_459 (xor_459_out, xor_458_out, and_716_out);
  and and_707 (and_707_out, Bit16_A[3], Bit16_B[0]);
  xor xor_460 (Lower_Word[3], and_707_out, xor_459_out);
  and and_708 (and_708_out, and_703_out, and_702_out);
  and and_709 (and_709_out, and_705_out, xor_457_out);
  and and_710 (and_710_out, and_707_out, xor_459_out);
  and and_711 (and_711_out, Bit16_A[0], Bit16_B[2]);
  or or_224 (or_224_out, and_715_out, and_713_out);
  and and_712 (and_712_out, Bit16_A[1], Bit16_B[1]);
  xor xor_461 (xor_461_out, and_712_out, and_711_out);
  and and_713 (and_713_out, and_719_out, xor_461_out);
  xor xor_462 (xor_462_out, xor_461_out, and_719_out);
  and and_714 (and_714_out, Bit16_A[2], Bit16_B[0]);
  xor xor_463 (Lower_Word[2], and_714_out, xor_462_out);
  and and_715 (and_715_out, and_712_out, and_711_out);
  and and_716 (and_716_out, and_714_out, xor_462_out);
  and and_717 (and_717_out, Bit16_A[0], Bit16_B[1]);
  and and_718 (and_718_out, Bit16_A[1], Bit16_B[0]);
  xor xor_464 (Lower_Word[1], and_718_out, and_717_out);
  and and_719 (and_719_out, and_718_out, and_717_out);
  and and_720 (Lower_Word[0], Bit16_A[0], Bit16_B[0]);
endmodule

module Bit16_Controlled_Buffer (
  input  Enable,
  input  [15:0] Bit16_In,
  output [15:0] Bit16_Out
);

  and and_1 (Bit16_Out[0], Bit16_In[0], Enable);
  and and_2 (Bit16_Out[1], Bit16_In[1], Enable);
  and and_3 (Bit16_Out[2], Bit16_In[2], Enable);
  and and_4 (Bit16_Out[3], Bit16_In[3], Enable);
  and and_5 (Bit16_Out[4], Bit16_In[4], Enable);
  and and_6 (Bit16_Out[5], Bit16_In[5], Enable);
  and and_7 (Bit16_Out[6], Bit16_In[6], Enable);
  and and_8 (Bit16_Out[7], Bit16_In[7], Enable);
  and and_9 (Bit16_Out[8], Bit16_In[8], Enable);
  and and_10 (Bit16_Out[9], Bit16_In[9], Enable);
  and and_11 (Bit16_Out[10], Bit16_In[10], Enable);
  and and_12 (Bit16_Out[11], Bit16_In[11], Enable);
  and and_13 (Bit16_Out[12], Bit16_In[12], Enable);
  and and_14 (Bit16_Out[13], Bit16_In[13], Enable);
  and and_15 (Bit16_Out[14], Bit16_In[14], Enable);
  and and_16 (Bit16_Out[15], Bit16_In[15], Enable);
endmodule
module Bit16_Divider (
  input  [15:0] Bit16_Dividend,
  input  [15:0] Bit16_Divisor,
  output [15:0] Bit16_Quotient,
  output [15:0] Bit16_Remainder
);

  wire and_1_out, and_2_out, and_3_out, and_4_out, and_5_out, and_6_out, and_7_out, and_8_out, and_9_out,
       and_10_out, and_11_out, and_12_out, and_13_out, and_14_out, and_15_out, not_1_out, not_2_out,
       not_3_out, not_4_out, not_5_out, not_6_out, not_7_out, not_8_out, not_9_out, not_10_out, not_11_out,
       not_12_out, not_13_out, not_14_out, not_15_out, not_16_out, or_1_out, or_2_out, or_3_out, or_4_out,
       or_5_out, or_6_out, or_7_out, or_8_out, or_9_out, or_10_out, or_11_out, or_12_out, or_13_out,
       or_14_out;
  wire [15:0] bit16_add_16_p1, bit16_controlled_buffer_1_bit16_out, bit16_controlled_buffer_2_bit16_out,
       bit16_controlled_buffer_3_bit16_out, bit16_controlled_buffer_4_bit16_out,
       bit16_controlled_buffer_5_bit16_out, bit16_controlled_buffer_6_bit16_out,
       bit16_controlled_buffer_7_bit16_out, bit16_controlled_buffer_8_bit16_out,
       bit16_controlled_buffer_9_bit16_out, bit16_controlled_buffer_10_bit16_out,
       bit16_controlled_buffer_11_bit16_out, bit16_controlled_buffer_12_bit16_out,
       bit16_controlled_buffer_13_bit16_out, bit16_controlled_buffer_14_bit16_out,
       bit16_controlled_buffer_15_bit16_out, bit16_controlled_buffer_16_bit16_out,
       bit16_controlled_buffer_17_bit16_out, bit16_controlled_buffer_18_bit16_out,
       bit16_controlled_buffer_19_bit16_out, bit16_controlled_buffer_20_bit16_out,
       bit16_controlled_buffer_21_bit16_out, bit16_controlled_buffer_22_bit16_out,
       bit16_controlled_buffer_23_bit16_out, bit16_controlled_buffer_24_bit16_out,
       bit16_controlled_buffer_25_bit16_out, bit16_controlled_buffer_26_bit16_out,
       bit16_controlled_buffer_27_bit16_out, bit16_controlled_buffer_28_bit16_out,
       bit16_controlled_buffer_29_bit16_out, bit16_controlled_buffer_30_bit16_out,
       bit16_controlled_buffer_31_bit16_out, bit16_controlled_buffer_32_bit16_out, or_29_out;
  wire [15:1] bit16_add_1_p1, bit16_add_2_p1, bit16_add_3_p1, bit16_add_4_p1, bit16_add_5_p1, bit16_add_6_p1,
       bit16_add_7_p1, bit16_add_8_p1, bit16_add_9_p1, bit16_add_10_p1, bit16_add_11_p1, bit16_add_12_p1,
       bit16_add_13_p1, bit16_add_14_p1, bit16_add_15_p1, or_15_out, or_16_out, or_17_out, or_18_out,
       or_19_out, or_20_out, or_21_out, or_22_out, or_23_out, or_24_out, or_25_out, or_26_out, or_27_out,
       or_28_out, xor_1_out;
  wire [15:15] bit16_add_1_p1_2, bit16_add_2_p1_2, bit16_add_3_p1_2, bit16_add_4_p1_2, bit16_add_5_p1_2,
       bit16_add_6_p1_2, bit16_add_7_p1_2, bit16_add_8_p1_2, bit16_add_9_p1_2, bit16_add_10_p1_2,
       bit16_add_11_p1_2, bit16_add_12_p1_2, bit16_add_13_p1_2, bit16_add_14_p1_2, bit16_add_15_p1_2,
       or_15_out_2, or_16_out_2, or_17_out_2, or_18_out_2, or_19_out_2, or_20_out_2, or_21_out_2,
       or_22_out_2, or_23_out_2, or_24_out_2, or_25_out_2, or_26_out_2, or_27_out_2, or_28_out_2;

  and and_1 (and_1_out, Bit16_Divisor[0], 1'b1);
  and and_2 (and_2_out, xor_1_out[1], 1'b1);
  or or_1 (or_1_out, and_1_out, and_2_out);
  and and_3 (and_3_out, xor_1_out[2], 1'b1);
  or or_2 (or_2_out, and_1_out, and_2_out, and_3_out);
  and and_4 (and_4_out, xor_1_out[3], 1'b1);
  or or_3 (or_3_out, and_1_out, and_2_out, and_3_out, and_4_out);
  and and_5 (and_5_out, xor_1_out[4], 1'b1);
  or or_4 (or_4_out, and_1_out, and_2_out, and_3_out, and_4_out, and_5_out);
  and and_6 (and_6_out, xor_1_out[5], 1'b1);
  or or_5 (or_5_out, and_1_out, and_2_out, and_3_out, and_4_out, and_5_out, and_6_out);
  and and_7 (and_7_out, xor_1_out[6], 1'b1);
  or or_6 (or_6_out, and_1_out, and_2_out, and_3_out, and_4_out, and_5_out, and_6_out, and_7_out);
  and and_8 (and_8_out, xor_1_out[7], 1'b1);
  or or_7 (or_7_out, and_1_out, and_2_out, and_3_out, and_4_out, and_5_out, and_6_out, and_7_out, and_8_out);
  and and_9 (and_9_out, xor_1_out[8], 1'b1);
  or or_8 (or_8_out, and_1_out, and_2_out, and_3_out, and_4_out, and_5_out, and_6_out, and_7_out, and_8_out, and_9_out);
  and and_10 (and_10_out, xor_1_out[9], 1'b1);
  or or_9 (or_9_out, and_1_out, and_2_out, and_3_out, and_4_out, and_5_out, and_6_out, and_7_out, and_8_out, and_9_out, and_10_out);
  and and_11 (and_11_out, xor_1_out[10], 1'b1);
  or or_10 (or_10_out, and_1_out, and_2_out, and_3_out, and_4_out, and_5_out, and_6_out, and_7_out, and_8_out, and_9_out, and_10_out, and_11_out);
  and and_12 (and_12_out, xor_1_out[11], 1'b1);
  or or_11 (or_11_out, and_1_out, and_2_out, and_3_out, and_4_out, and_5_out, and_6_out, and_7_out, and_8_out, and_9_out, and_10_out, and_11_out, and_12_out);
  and and_13 (and_13_out, xor_1_out[12], 1'b1);
  or or_12 (or_12_out, and_1_out, and_2_out, and_3_out, and_4_out, and_5_out, and_6_out, and_7_out, and_8_out, and_9_out, and_10_out, and_11_out, and_12_out, and_13_out);
  and and_14 (and_14_out, xor_1_out[13], 1'b1);
  or or_13 (or_13_out, and_1_out, and_2_out, and_3_out, and_4_out, and_5_out, and_6_out, and_7_out, and_8_out, and_9_out, and_10_out, and_11_out, and_12_out, and_13_out, and_14_out);
  and and_15 (and_15_out, xor_1_out[14], 1'b1);
  or or_14 (or_14_out, and_1_out, and_2_out, and_3_out, and_4_out, and_5_out, and_6_out, and_7_out, and_8_out, and_9_out, and_10_out, and_11_out, and_12_out, and_13_out, and_14_out, and_15_out);
  xor xor_1 (xor_1_out[1], and_1_out, Bit16_Divisor[1]);
  xor xor_2 (xor_1_out[2], or_1_out, Bit16_Divisor[2]);
  xor xor_3 (xor_1_out[3], or_2_out, Bit16_Divisor[3]);
  xor xor_4 (xor_1_out[4], or_3_out, Bit16_Divisor[4]);
  xor xor_5 (xor_1_out[5], or_4_out, Bit16_Divisor[5]);
  xor xor_6 (xor_1_out[6], or_5_out, Bit16_Divisor[6]);
  xor xor_7 (xor_1_out[7], or_6_out, Bit16_Divisor[7]);
  xor xor_8 (xor_1_out[8], or_7_out, Bit16_Divisor[8]);
  xor xor_9 (xor_1_out[9], or_8_out, Bit16_Divisor[9]);
  xor xor_10 (xor_1_out[10], or_9_out, Bit16_Divisor[10]);
  xor xor_11 (xor_1_out[11], or_10_out, Bit16_Divisor[11]);
  xor xor_12 (xor_1_out[12], or_11_out, Bit16_Divisor[12]);
  xor xor_13 (xor_1_out[13], or_12_out, Bit16_Divisor[13]);
  xor xor_14 (xor_1_out[14], or_13_out, Bit16_Divisor[14]);
  xor xor_15 (xor_1_out[15], or_14_out, Bit16_Divisor[15]);
  not not_1 (not_1_out, Bit16_Quotient[15]);
  not not_2 (not_2_out, Bit16_Quotient[14]);
  not not_3 (not_3_out, Bit16_Quotient[13]);
  not not_4 (not_4_out, Bit16_Quotient[12]);
  not not_5 (not_5_out, Bit16_Quotient[11]);
  not not_6 (not_6_out, Bit16_Quotient[10]);
  not not_7 (not_7_out, Bit16_Quotient[9]);
  not not_8 (not_8_out, Bit16_Quotient[8]);
  not not_9 (not_9_out, Bit16_Quotient[7]);
  not not_10 (not_10_out, Bit16_Quotient[6]);
  not not_11 (not_11_out, Bit16_Quotient[5]);
  not not_12 (not_12_out, Bit16_Quotient[4]);
  not not_13 (not_13_out, Bit16_Quotient[3]);
  not not_14 (not_14_out, Bit16_Quotient[2]);
  not not_15 (not_15_out, Bit16_Quotient[1]);
  not not_16 (not_16_out, Bit16_Quotient[0]);
  Bit16_Controlled_Buffer bit16_controlled_buffer_1 (
    .Enable(Bit16_Quotient[15]), .Bit16_In({bit16_add_11_p1, Bit16_Dividend[14]}),
    .Bit16_Out(bit16_controlled_buffer_1_bit16_out));
  Bit16_Controlled_Buffer bit16_controlled_buffer_2 (
    .Enable(not_1_out), .Bit16_In({{14{1'b0}}, Bit16_Dividend[15:14]}),
    .Bit16_Out(bit16_controlled_buffer_2_bit16_out));
  assign {or_15_out_2[15], or_15_out} = bit16_controlled_buffer_2_bit16_out | bit16_controlled_buffer_1_bit16_out;  // OR_Gate or_15, 16 bits wide
  // Bit16_Add bit16_add_1: pin names not known; wires that end beside it: {bit16_add_1_p1_2[15], bit16_add_1_p1}, Bit16_Quotient[14]
  Bit16_Controlled_Buffer bit16_controlled_buffer_3 (
    .Enable(Bit16_Quotient[14]), .Bit16_In({bit16_add_1_p1, Bit16_Dividend[13]}),
    .Bit16_Out(bit16_controlled_buffer_3_bit16_out));
  Bit16_Controlled_Buffer bit16_controlled_buffer_4 (
    .Enable(not_2_out), .Bit16_In({or_15_out, Bit16_Dividend[13]}),
    .Bit16_Out(bit16_controlled_buffer_4_bit16_out));
  assign {or_16_out_2[15], or_16_out} = bit16_controlled_buffer_4_bit16_out | bit16_controlled_buffer_3_bit16_out;  // OR_Gate or_16, 16 bits wide
  // Bit16_Add bit16_add_2: pin names not known; wires that end beside it: {bit16_add_2_p1_2[15], bit16_add_2_p1}, Bit16_Quotient[13]
  Bit16_Controlled_Buffer bit16_controlled_buffer_5 (
    .Enable(Bit16_Quotient[13]), .Bit16_In({bit16_add_2_p1, Bit16_Dividend[12]}),
    .Bit16_Out(bit16_controlled_buffer_5_bit16_out));
  Bit16_Controlled_Buffer bit16_controlled_buffer_6 (
    .Enable(not_3_out), .Bit16_In({or_16_out, Bit16_Dividend[12]}),
    .Bit16_Out(bit16_controlled_buffer_6_bit16_out));
  assign {or_17_out_2[15], or_17_out} = bit16_controlled_buffer_6_bit16_out | bit16_controlled_buffer_5_bit16_out;  // OR_Gate or_17, 16 bits wide
  // Bit16_Add bit16_add_3: pin names not known; wires that end beside it: {bit16_add_3_p1_2[15], bit16_add_3_p1}, Bit16_Quotient[12]
  Bit16_Controlled_Buffer bit16_controlled_buffer_7 (
    .Enable(Bit16_Quotient[12]), .Bit16_In({bit16_add_3_p1, Bit16_Dividend[11]}),
    .Bit16_Out(bit16_controlled_buffer_7_bit16_out));
  Bit16_Controlled_Buffer bit16_controlled_buffer_8 (
    .Enable(not_4_out), .Bit16_In({or_17_out, Bit16_Dividend[11]}),
    .Bit16_Out(bit16_controlled_buffer_8_bit16_out));
  assign {or_18_out_2[15], or_18_out} = bit16_controlled_buffer_8_bit16_out | bit16_controlled_buffer_7_bit16_out;  // OR_Gate or_18, 16 bits wide
  // Bit16_Add bit16_add_4: pin names not known; wires that end beside it: {bit16_add_4_p1_2[15], bit16_add_4_p1}, Bit16_Quotient[11]
  Bit16_Controlled_Buffer bit16_controlled_buffer_9 (
    .Enable(Bit16_Quotient[11]), .Bit16_In({bit16_add_4_p1, Bit16_Dividend[10]}),
    .Bit16_Out(bit16_controlled_buffer_9_bit16_out));
  Bit16_Controlled_Buffer bit16_controlled_buffer_10 (
    .Enable(not_5_out), .Bit16_In({or_18_out, Bit16_Dividend[10]}),
    .Bit16_Out(bit16_controlled_buffer_10_bit16_out));
  assign {or_19_out_2[15], or_19_out} = bit16_controlled_buffer_10_bit16_out | bit16_controlled_buffer_9_bit16_out;  // OR_Gate or_19, 16 bits wide
  Bit16_Controlled_Buffer bit16_controlled_buffer_11 (
    .Enable(Bit16_Quotient[10]), .Bit16_In({bit16_add_12_p1, Bit16_Dividend[9]}),
    .Bit16_Out(bit16_controlled_buffer_11_bit16_out));
  Bit16_Controlled_Buffer bit16_controlled_buffer_12 (
    .Enable(not_6_out), .Bit16_In({or_19_out, Bit16_Dividend[9]}),
    .Bit16_Out(bit16_controlled_buffer_12_bit16_out));
  assign {or_20_out_2[15], or_20_out} = bit16_controlled_buffer_12_bit16_out | bit16_controlled_buffer_11_bit16_out;  // OR_Gate or_20, 16 bits wide
  // Bit16_Add bit16_add_5: pin names not known; wires that end beside it: {bit16_add_5_p1_2[15], bit16_add_5_p1}, Bit16_Quotient[9]
  Bit16_Controlled_Buffer bit16_controlled_buffer_13 (
    .Enable(Bit16_Quotient[9]), .Bit16_In({bit16_add_5_p1, Bit16_Dividend[8]}),
    .Bit16_Out(bit16_controlled_buffer_13_bit16_out));
  Bit16_Controlled_Buffer bit16_controlled_buffer_14 (
    .Enable(not_7_out), .Bit16_In({or_20_out, Bit16_Dividend[8]}),
    .Bit16_Out(bit16_controlled_buffer_14_bit16_out));
  assign {or_21_out_2[15], or_21_out} = bit16_controlled_buffer_14_bit16_out | bit16_controlled_buffer_13_bit16_out;  // OR_Gate or_21, 16 bits wide
  Bit16_Controlled_Buffer bit16_controlled_buffer_15 (
    .Enable(Bit16_Quotient[8]), .Bit16_In({bit16_add_13_p1, Bit16_Dividend[7]}),
    .Bit16_Out(bit16_controlled_buffer_15_bit16_out));
  Bit16_Controlled_Buffer bit16_controlled_buffer_16 (
    .Enable(not_8_out), .Bit16_In({or_21_out, Bit16_Dividend[7]}),
    .Bit16_Out(bit16_controlled_buffer_16_bit16_out));
  assign {or_22_out_2[15], or_22_out} = bit16_controlled_buffer_16_bit16_out | bit16_controlled_buffer_15_bit16_out;  // OR_Gate or_22, 16 bits wide
  Bit16_Controlled_Buffer bit16_controlled_buffer_17 (
    .Enable(Bit16_Quotient[7]), .Bit16_In({bit16_add_14_p1, Bit16_Dividend[6]}),
    .Bit16_Out(bit16_controlled_buffer_17_bit16_out));
  Bit16_Controlled_Buffer bit16_controlled_buffer_18 (
    .Enable(not_9_out), .Bit16_In({or_22_out, Bit16_Dividend[6]}),
    .Bit16_Out(bit16_controlled_buffer_18_bit16_out));
  assign {or_23_out_2[15], or_23_out} = bit16_controlled_buffer_18_bit16_out | bit16_controlled_buffer_17_bit16_out;  // OR_Gate or_23, 16 bits wide
  // Bit16_Add bit16_add_6: pin names not known; wires that end beside it: {bit16_add_6_p1_2[15], bit16_add_6_p1}, Bit16_Quotient[6]
  Bit16_Controlled_Buffer bit16_controlled_buffer_19 (
    .Enable(Bit16_Quotient[6]), .Bit16_In({bit16_add_6_p1, Bit16_Dividend[5]}),
    .Bit16_Out(bit16_controlled_buffer_19_bit16_out));
  Bit16_Controlled_Buffer bit16_controlled_buffer_20 (
    .Enable(not_10_out), .Bit16_In({or_23_out, Bit16_Dividend[5]}),
    .Bit16_Out(bit16_controlled_buffer_20_bit16_out));
  assign {or_24_out_2[15], or_24_out} = bit16_controlled_buffer_20_bit16_out | bit16_controlled_buffer_19_bit16_out;  // OR_Gate or_24, 16 bits wide
  // Bit16_Add bit16_add_7: pin names not known; wires that end beside it: {bit16_add_7_p1_2[15], bit16_add_7_p1}, Bit16_Quotient[5]
  Bit16_Controlled_Buffer bit16_controlled_buffer_21 (
    .Enable(Bit16_Quotient[5]), .Bit16_In({bit16_add_7_p1, Bit16_Dividend[4]}),
    .Bit16_Out(bit16_controlled_buffer_21_bit16_out));
  Bit16_Controlled_Buffer bit16_controlled_buffer_22 (
    .Enable(not_11_out), .Bit16_In({or_24_out, Bit16_Dividend[4]}),
    .Bit16_Out(bit16_controlled_buffer_22_bit16_out));
  assign {or_25_out_2[15], or_25_out} = bit16_controlled_buffer_22_bit16_out | bit16_controlled_buffer_21_bit16_out;  // OR_Gate or_25, 16 bits wide
  // Bit16_Add bit16_add_8: pin names not known; wires that end beside it: {bit16_add_8_p1_2[15], bit16_add_8_p1}, Bit16_Quotient[4]
  Bit16_Controlled_Buffer bit16_controlled_buffer_23 (
    .Enable(Bit16_Quotient[4]), .Bit16_In({bit16_add_8_p1, Bit16_Dividend[3]}),
    .Bit16_Out(bit16_controlled_buffer_23_bit16_out));
  Bit16_Controlled_Buffer bit16_controlled_buffer_24 (
    .Enable(not_12_out), .Bit16_In({or_25_out, Bit16_Dividend[3]}),
    .Bit16_Out(bit16_controlled_buffer_24_bit16_out));
  assign {or_26_out_2[15], or_26_out} = bit16_controlled_buffer_24_bit16_out | bit16_controlled_buffer_23_bit16_out;  // OR_Gate or_26, 16 bits wide
  // Bit16_Add bit16_add_9: pin names not known; wires that end beside it: {bit16_add_9_p1_2[15], bit16_add_9_p1}, Bit16_Quotient[3]
  Bit16_Controlled_Buffer bit16_controlled_buffer_25 (
    .Enable(Bit16_Quotient[3]), .Bit16_In({bit16_add_9_p1, Bit16_Dividend[2]}),
    .Bit16_Out(bit16_controlled_buffer_25_bit16_out));
  Bit16_Controlled_Buffer bit16_controlled_buffer_26 (
    .Enable(not_13_out), .Bit16_In({or_26_out, Bit16_Dividend[2]}),
    .Bit16_Out(bit16_controlled_buffer_26_bit16_out));
  assign {or_27_out_2[15], or_27_out} = bit16_controlled_buffer_26_bit16_out | bit16_controlled_buffer_25_bit16_out;  // OR_Gate or_27, 16 bits wide
  // Bit16_Add bit16_add_10: pin names not known; wires that end beside it: {bit16_add_10_p1_2[15], bit16_add_10_p1}, Bit16_Quotient[2]
  Bit16_Controlled_Buffer bit16_controlled_buffer_27 (
    .Enable(Bit16_Quotient[2]), .Bit16_In({bit16_add_10_p1, Bit16_Dividend[1]}),
    .Bit16_Out(bit16_controlled_buffer_27_bit16_out));
  Bit16_Controlled_Buffer bit16_controlled_buffer_28 (
    .Enable(not_14_out), .Bit16_In({or_27_out, Bit16_Dividend[1]}),
    .Bit16_Out(bit16_controlled_buffer_28_bit16_out));
  assign {or_28_out_2[15], or_28_out} = bit16_controlled_buffer_28_bit16_out | bit16_controlled_buffer_27_bit16_out;  // OR_Gate or_28, 16 bits wide
  Bit16_Controlled_Buffer bit16_controlled_buffer_29 (
    .Enable(Bit16_Quotient[1]), .Bit16_In({bit16_add_15_p1, Bit16_Dividend[0]}),
    .Bit16_Out(bit16_controlled_buffer_29_bit16_out));
  Bit16_Controlled_Buffer bit16_controlled_buffer_30 (
    .Enable(not_15_out), .Bit16_In({or_28_out, Bit16_Dividend[0]}),
    .Bit16_Out(bit16_controlled_buffer_30_bit16_out));
  assign or_29_out = bit16_controlled_buffer_30_bit16_out | bit16_controlled_buffer_29_bit16_out;  // OR_Gate or_29, 16 bits wide
  Bit16_Controlled_Buffer bit16_controlled_buffer_31 (
    .Enable(Bit16_Quotient[0]), .Bit16_In(bit16_add_16_p1), .Bit16_Out(bit16_controlled_buffer_31_bit16_out));
  Bit16_Controlled_Buffer bit16_controlled_buffer_32 (
    .Enable(not_16_out), .Bit16_In(or_29_out), .Bit16_Out(bit16_controlled_buffer_32_bit16_out));
  // Bit16_Add bit16_add_11: pin names not known; wires that end beside it: {bit16_add_11_p1_2[15], bit16_add_11_p1}, Bit16_Quotient[15]
  // Bit16_Add bit16_add_12: pin names not known; wires that end beside it: {bit16_add_12_p1_2[15], bit16_add_12_p1}, Bit16_Quotient[10]
  // Bit16_Add bit16_add_13: pin names not known; wires that end beside it: {bit16_add_13_p1_2[15], bit16_add_13_p1}, Bit16_Quotient[8]
  // Bit16_Add bit16_add_14: pin names not known; wires that end beside it: {bit16_add_14_p1_2[15], bit16_add_14_p1}, Bit16_Quotient[7]
  // Bit16_Add bit16_add_15: pin names not known; wires that end beside it: {bit16_add_15_p1_2[15], bit16_add_15_p1}, Bit16_Quotient[1]
  // Bit16_Add bit16_add_16: pin names not known; wires that end beside it: bit16_add_16_p1, Bit16_Quotient[0]
  assign Bit16_Remainder = bit16_controlled_buffer_32_bit16_out | bit16_controlled_buffer_31_bit16_out;  // OR_Gate or_30, 16 bits wide
  // Probe on Bit16_Quotient
  // Probe on Bit16_Remainder
endmodule

module Bit4_CLA_Logic (
  input  Cin,
  input  P1,
  input  G1,
  input  P2,
  input  G2,
  input  P3,
  input  G3,
  input  P4,
  input  G4,
  output C2,
  output C3,
  output C4,
  output COUT,
  output PG
);

  wire and_1_out, and_2_out, and_3_out, and_4_out, and_5_out, and_6_out, and_7_out, and_8_out, and_9_out,
       and_10_out;

  or or_1 (C2, G1, and_1_out);
  or or_2 (C3, G2, and_2_out, and_3_out);
  or or_3 (C4, G3, and_4_out, and_5_out, and_6_out);
  or or_4 (COUT, G4, and_7_out, and_8_out, and_9_out, and_10_out);
  and and_1 (and_1_out, P1, Cin);
  and and_2 (and_2_out, P2, G1);
  and and_3 (and_3_out, P2, P1, Cin);
  and and_4 (and_4_out, G2, P3);
  and and_5 (and_5_out, P3, P2, G1);
  and and_6 (and_6_out, P3, P2, Cin, P1);
  and and_7 (and_7_out, G3, P4);
  and and_8 (and_8_out, P4, P3, G2);
  and and_9 (and_9_out, P4, P3, P2, G1);
  and and_10 (and_10_out, P4, P3, P2, P1, Cin);
  and and_11 (PG, P1, P2, P3, P4);
endmodule

module Bit16_Left_Shift (
  input  Arithmetic_Mode,
  input  Rotate_Mode,
  input  Right_Shift_Mode,
  input  [3:0] Bit4_Shift,
  input  [15:0] Bit16_Data,
  output [15:0] Bit16_Result,
  output Shift_Overflow
);

  wire and_1_out, and_2_out, and_3_out, and_4_out, and_5_out, and_6_out, and_7_out, and_8_out, and_9_out,
       and_10_out, and_11_out, and_12_out, and_13_out, and_14_out, and_15_out, and_16_out, and_17_out,
       and_18_out, and_19_out, and_20_out, and_21_out, and_22_out, and_23_out, and_24_out, and_25_out,
       and_26_out, and_27_out, and_28_out, and_29_out, and_30_out, and_31_out, and_32_out, and_33_out,
       and_34_out, and_35_out, and_36_out, and_37_out, and_38_out, and_39_out, and_40_out, and_41_out,
       and_42_out, and_43_out, and_44_out, and_45_out, and_46_out, and_47_out, and_48_out, and_49_out,
       and_50_out, and_51_out, and_52_out, and_53_out, and_54_out, and_55_out, and_56_out, and_57_out,
       and_58_out, and_59_out, and_60_out, and_61_out, and_62_out, and_63_out, and_64_out, and_65_out,
       and_66_out, and_67_out, and_68_out, and_69_out, and_70_out, and_71_out, and_72_out, and_73_out,
       and_74_out, and_75_out, and_76_out, and_77_out, and_78_out, and_79_out, and_80_out, and_81_out,
       and_82_out, and_83_out, and_84_out, and_85_out, and_86_out, and_87_out, and_88_out, and_89_out,
       and_90_out, and_91_out, and_92_out, and_93_out, and_94_out, and_95_out, and_96_out, and_97_out,
       and_98_out, and_99_out, and_100_out, and_101_out, and_102_out, and_103_out, and_104_out, and_105_out,
       and_106_out, and_107_out, and_108_out, and_109_out, and_110_out, and_111_out, and_112_out,
       and_113_out, and_114_out, and_115_out, and_116_out, and_117_out, and_118_out, and_119_out,
       and_120_out, and_121_out, and_122_out, and_123_out, and_124_out, and_125_out, and_126_out,
       and_127_out, and_128_out, and_129_out, and_130_out, and_131_out, and_132_out, and_133_out,
       and_134_out, and_135_out, and_136_out, and_137_out, and_138_out, and_139_out, and_140_out,
       and_141_out, and_142_out, and_143_out, and_144_out, and_145_out, and_146_out, and_147_out,
       and_148_out, and_149_out, and_150_out, and_151_out, and_152_out, and_153_out, and_154_out,
       and_155_out, and_156_out, and_157_out, and_158_out, and_159_out, or_2_out, or_3_out, or_4_out,
       or_6_out, or_7_out, or_8_out, or_10_out, or_11_out, or_12_out, or_14_out, or_15_out, or_16_out,
       or_18_out, or_19_out, or_20_out, or_22_out, or_23_out, or_24_out, or_26_out, or_27_out, or_28_out,
       or_30_out, or_31_out, or_32_out, or_34_out, or_35_out, or_36_out, or_38_out, or_39_out, or_40_out,
       or_42_out, or_43_out, or_44_out, or_46_out, or_47_out, or_48_out, or_50_out, or_51_out, or_52_out,
       or_54_out, or_55_out, or_56_out, or_58_out, or_59_out, or_60_out, or_62_out, or_63_out, or_64_out;
  wire [15:0] multiplexer_16_out, or_65_out;

  Multiplexer multiplexer_1 (
    .in0(Bit16_Data[15]), .in1(Bit16_Data[0]), .out(multiplexer_16_out[15]), .sel(Right_Shift_Mode));
  Multiplexer multiplexer_2 (
    .in0(Bit16_Data[14]), .in1(Bit16_Data[1]), .out(multiplexer_16_out[14]), .sel(Right_Shift_Mode));
  Multiplexer multiplexer_3 (
    .in0(Bit16_Data[13]), .in1(Bit16_Data[2]), .out(multiplexer_16_out[13]), .sel(Right_Shift_Mode));
  Multiplexer multiplexer_4 (
    .in0(Bit16_Data[12]), .in1(Bit16_Data[3]), .out(multiplexer_16_out[12]), .sel(Right_Shift_Mode));
  Multiplexer multiplexer_5 (
    .in0(Bit16_Data[11]), .in1(Bit16_Data[4]), .out(multiplexer_16_out[11]), .sel(Right_Shift_Mode));
  Multiplexer multiplexer_6 (
    .in0(Bit16_Data[10]), .in1(Bit16_Data[5]), .out(multiplexer_16_out[10]), .sel(Right_Shift_Mode));
  Multiplexer multiplexer_7 (
    .in0(Bit16_Data[9]), .in1(Bit16_Data[6]), .out(multiplexer_16_out[9]), .sel(Right_Shift_Mode));
  Multiplexer multiplexer_8 (
    .in0(Bit16_Data[8]), .in1(Bit16_Data[7]), .out(multiplexer_16_out[8]), .sel(Right_Shift_Mode));
  Multiplexer multiplexer_9 (
    .in0(Bit16_Data[7]), .in1(Bit16_Data[8]), .out(multiplexer_16_out[7]), .sel(Right_Shift_Mode));
  Multiplexer multiplexer_10 (
    .in0(Bit16_Data[6]), .in1(Bit16_Data[9]), .out(multiplexer_16_out[6]), .sel(Right_Shift_Mode));
  Multiplexer multiplexer_11 (
    .in0(Bit16_Data[5]), .in1(Bit16_Data[10]), .out(multiplexer_16_out[5]), .sel(Right_Shift_Mode));
  Multiplexer multiplexer_12 (
    .in0(Bit16_Data[4]), .in1(Bit16_Data[11]), .out(multiplexer_16_out[4]), .sel(Right_Shift_Mode));
  Multiplexer multiplexer_13 (
    .in0(Bit16_Data[3]), .in1(Bit16_Data[12]), .out(multiplexer_16_out[3]), .sel(Right_Shift_Mode));
  Multiplexer multiplexer_14 (
    .in0(Bit16_Data[2]), .in1(Bit16_Data[13]), .out(multiplexer_16_out[2]), .sel(Right_Shift_Mode));
  Multiplexer multiplexer_15 (
    .in0(Bit16_Data[1]), .in1(Bit16_Data[14]), .out(multiplexer_16_out[1]), .sel(Right_Shift_Mode));
  Multiplexer multiplexer_16 (
    .in0(Bit16_Data[0]), .in1(Bit16_Data[15]), .out(multiplexer_16_out[0]), .sel(Right_Shift_Mode));
  or or_1 (Shift_Overflow, and_6_out, and_8_out, and_16_out, and_10_out, and_18_out, and_26_out, and_34_out, and_12_out, and_20_out, and_28_out, and_36_out, and_44_out, and_53_out, and_60_out, and_68_out);
  and and_1 (and_1_out, ~Bit4_Shift[0], multiplexer_16_out[15]);  // AND_Gate
  and and_2 (and_2_out, ~Bit4_Shift[1], or_2_out);  // AND_Gate
  and and_3 (and_3_out, ~Bit4_Shift[2], or_3_out);  // AND_Gate
  and and_4 (and_4_out, ~Bit4_Shift[3], or_4_out);  // AND_Gate
  and and_5 (and_5_out, Arithmetic_Mode, Bit16_Data[15]);
  and and_6 (and_6_out, multiplexer_16_out[15], Bit4_Shift[0]);
  and and_7 (and_7_out, ~Bit4_Shift[0], multiplexer_16_out[14]);  // AND_Gate
  or or_2 (or_2_out, and_1_out, and_14_out);
  and and_8 (and_8_out, or_2_out, Bit4_Shift[1]);
  and and_9 (and_9_out, ~Bit4_Shift[1], or_6_out);  // AND_Gate
  or or_3 (or_3_out, and_2_out, and_24_out);
  and and_10 (and_10_out, or_3_out, Bit4_Shift[2]);
  and and_11 (and_11_out, ~Bit4_Shift[2], or_7_out);  // AND_Gate
  or or_4 (or_4_out, and_3_out, and_42_out);
  and and_12 (and_12_out, or_4_out, Bit4_Shift[3]);
  and and_13 (and_13_out, ~Bit4_Shift[3], or_8_out);  // AND_Gate
  or or_5 (or_65_out[15], and_4_out, and_76_out);
  and and_14 (and_14_out, multiplexer_16_out[14], Bit4_Shift[0]);
  and and_15 (and_15_out, ~Bit4_Shift[0], multiplexer_16_out[13]);  // AND_Gate
  or or_6 (or_6_out, and_7_out, and_22_out);
  and and_16 (and_16_out, or_6_out, Bit4_Shift[1]);
  and and_17 (and_17_out, ~Bit4_Shift[1], or_10_out);  // AND_Gate
  or or_7 (or_7_out, and_9_out, and_32_out);
  and and_18 (and_18_out, or_7_out, Bit4_Shift[2]);
  and and_19 (and_19_out, ~Bit4_Shift[2], or_11_out);  // AND_Gate
  or or_8 (or_8_out, and_11_out, and_51_out);
  and and_20 (and_20_out, or_8_out, Bit4_Shift[3]);
  and and_21 (and_21_out, ~Bit4_Shift[3], or_12_out);  // AND_Gate
  or or_9 (or_65_out[14], and_13_out, and_86_out);
  and and_22 (and_22_out, multiplexer_16_out[13], Bit4_Shift[0]);
  and and_23 (and_23_out, ~Bit4_Shift[0], multiplexer_16_out[12]);  // AND_Gate
  or or_10 (or_10_out, and_15_out, and_30_out);
  and and_24 (and_24_out, or_10_out, Bit4_Shift[1]);
  and and_25 (and_25_out, ~Bit4_Shift[1], or_14_out);  // AND_Gate
  or or_11 (or_11_out, and_17_out, and_40_out);
  and and_26 (and_26_out, or_11_out, Bit4_Shift[2]);
  and and_27 (and_27_out, ~Bit4_Shift[2], or_15_out);  // AND_Gate
  or or_12 (or_12_out, and_19_out, and_58_out);
  and and_28 (and_28_out, or_12_out, Bit4_Shift[3]);
  and and_29 (and_29_out, ~Bit4_Shift[3], or_16_out);  // AND_Gate
  or or_13 (or_65_out[13], and_21_out, and_96_out);
  and and_30 (and_30_out, multiplexer_16_out[12], Bit4_Shift[0]);
  and and_31 (and_31_out, ~Bit4_Shift[0], multiplexer_16_out[11]);  // AND_Gate
  or or_14 (or_14_out, and_23_out, and_38_out);
  and and_32 (and_32_out, or_14_out, Bit4_Shift[1]);
  and and_33 (and_33_out, ~Bit4_Shift[1], or_18_out);  // AND_Gate
  or or_15 (or_15_out, and_25_out, and_49_out);
  and and_34 (and_34_out, or_15_out, Bit4_Shift[2]);
  and and_35 (and_35_out, ~Bit4_Shift[2], or_19_out);  // AND_Gate
  or or_16 (or_16_out, and_27_out, and_66_out);
  and and_36 (and_36_out, or_16_out, Bit4_Shift[3]);
  and and_37 (and_37_out, ~Bit4_Shift[3], or_20_out);  // AND_Gate
  or or_17 (or_65_out[12], and_29_out, and_106_out);
  and and_38 (and_38_out, multiplexer_16_out[11], Bit4_Shift[0]);
  and and_39 (and_39_out, ~Bit4_Shift[0], multiplexer_16_out[10]);  // AND_Gate
  or or_18 (or_18_out, and_31_out, and_47_out);
  and and_40 (and_40_out, or_18_out, Bit4_Shift[1]);
  and and_41 (and_41_out, ~Bit4_Shift[1], or_22_out);  // AND_Gate
  or or_19 (or_19_out, and_33_out, and_56_out);
  and and_42 (and_42_out, or_19_out, Bit4_Shift[2]);
  and and_43 (and_43_out, ~Bit4_Shift[2], or_23_out);  // AND_Gate
  or or_20 (or_20_out, and_35_out, and_74_out);
  and and_44 (and_44_out, or_20_out, Bit4_Shift[3]);
  and and_45 (and_45_out, ~Bit4_Shift[3], or_24_out);  // AND_Gate
  or or_21 (or_65_out[11], and_37_out, and_118_out);
  and and_46 (and_46_out, ~Bit4_Shift[0], multiplexer_16_out[9]);  // AND_Gate
  and and_47 (and_47_out, multiplexer_16_out[10], Bit4_Shift[0]);
  or or_22 (or_22_out, and_39_out, and_54_out);
  and and_48 (and_48_out, ~Bit4_Shift[1], or_26_out);  // AND_Gate
  and and_49 (and_49_out, or_22_out, Bit4_Shift[1]);
  or or_23 (or_23_out, and_41_out, and_64_out);
  and and_50 (and_50_out, ~Bit4_Shift[2], or_27_out);  // AND_Gate
  and and_51 (and_51_out, or_23_out, Bit4_Shift[2]);
  or or_24 (or_24_out, and_43_out, and_84_out);
  and and_52 (and_52_out, ~Bit4_Shift[3], or_28_out);  // AND_Gate
  and and_53 (and_53_out, or_24_out, Bit4_Shift[3]);
  or or_25 (or_65_out[10], and_45_out, and_130_out);
  and and_54 (and_54_out, multiplexer_16_out[9], Bit4_Shift[0]);
  and and_55 (and_55_out, ~Bit4_Shift[0], multiplexer_16_out[8]);  // AND_Gate
  or or_26 (or_26_out, and_46_out, and_62_out);
  and and_56 (and_56_out, or_26_out, Bit4_Shift[1]);
  and and_57 (and_57_out, ~Bit4_Shift[1], or_30_out);  // AND_Gate
  or or_27 (or_27_out, and_48_out, and_72_out);
  and and_58 (and_58_out, or_27_out, Bit4_Shift[2]);
  and and_59 (and_59_out, ~Bit4_Shift[2], or_31_out);  // AND_Gate
  or or_28 (or_28_out, and_50_out, and_94_out);
  and and_60 (and_60_out, or_28_out, Bit4_Shift[3]);
  and and_61 (and_61_out, ~Bit4_Shift[3], or_32_out);  // AND_Gate
  or or_29 (or_65_out[9], and_52_out, and_144_out);
  and and_62 (and_62_out, multiplexer_16_out[8], Bit4_Shift[0]);
  and and_63 (and_63_out, ~Bit4_Shift[0], multiplexer_16_out[7]);  // AND_Gate
  or or_30 (or_30_out, and_55_out, and_70_out);
  and and_64 (and_64_out, or_30_out, Bit4_Shift[1]);
  and and_65 (and_65_out, ~Bit4_Shift[1], or_34_out);  // AND_Gate
  or or_31 (or_31_out, and_57_out, and_82_out);
  and and_66 (and_66_out, or_31_out, Bit4_Shift[2]);
  and and_67 (and_67_out, ~Bit4_Shift[2], or_35_out);  // AND_Gate
  or or_32 (or_32_out, and_59_out, and_104_out);
  and and_68 (and_68_out, or_32_out, Bit4_Shift[3]);
  and and_69 (and_69_out, ~Bit4_Shift[3], or_36_out);  // AND_Gate
  or or_33 (or_65_out[8], and_61_out, and_157_out);
  and and_70 (and_70_out, multiplexer_16_out[7], Bit4_Shift[0]);
  and and_71 (and_71_out, ~Bit4_Shift[0], multiplexer_16_out[6]);  // AND_Gate
  or or_34 (or_34_out, and_63_out, and_80_out);
  and and_72 (and_72_out, or_34_out, Bit4_Shift[1]);
  and and_73 (and_73_out, ~Bit4_Shift[1], or_38_out);  // AND_Gate
  or or_35 (or_35_out, and_65_out, and_92_out);
  and and_74 (and_74_out, or_35_out, Bit4_Shift[2]);
  and and_75 (and_75_out, ~Bit4_Shift[2], or_39_out);  // AND_Gate
  or or_36 (or_36_out, and_67_out, and_114_out);
  and and_76 (and_76_out, or_36_out, Bit4_Shift[3]);
  and and_77 (and_77_out, ~Bit4_Shift[3], or_40_out);  // AND_Gate
  and and_78 (and_78_out, Bit4_Shift[3], and_5_out);
  and and_79 (and_79_out, and_76_out, and_12_out, Rotate_Mode);
  or or_37 (or_65_out[7], and_69_out, and_78_out, and_79_out);
  and and_80 (and_80_out, multiplexer_16_out[6], Bit4_Shift[0]);
  and and_81 (and_81_out, ~Bit4_Shift[0], multiplexer_16_out[5]);  // AND_Gate
  or or_38 (or_38_out, and_71_out, and_90_out);
  and and_82 (and_82_out, or_38_out, Bit4_Shift[1]);
  and and_83 (and_83_out, ~Bit4_Shift[1], or_42_out);  // AND_Gate
  or or_39 (or_39_out, and_73_out, and_102_out);
  and and_84 (and_84_out, or_39_out, Bit4_Shift[2]);
  and and_85 (and_85_out, ~Bit4_Shift[2], or_43_out);  // AND_Gate
  or or_40 (or_40_out, and_75_out, and_126_out);
  and and_86 (and_86_out, or_40_out, Bit4_Shift[3]);
  and and_87 (and_87_out, ~Bit4_Shift[3], or_44_out);  // AND_Gate
  and and_88 (and_88_out, Bit4_Shift[3], and_5_out);
  and and_89 (and_89_out, and_86_out, and_20_out, Rotate_Mode);
  or or_41 (or_65_out[6], and_77_out, and_88_out, and_89_out);
  and and_90 (and_90_out, multiplexer_16_out[5], Bit4_Shift[0]);
  and and_91 (and_91_out, ~Bit4_Shift[0], multiplexer_16_out[4]);  // AND_Gate
  or or_42 (or_42_out, and_81_out, and_100_out);
  and and_92 (and_92_out, or_42_out, Bit4_Shift[1]);
  and and_93 (and_93_out, ~Bit4_Shift[1], or_46_out);  // AND_Gate
  or or_43 (or_43_out, and_83_out, and_112_out);
  and and_94 (and_94_out, or_43_out, Bit4_Shift[2]);
  and and_95 (and_95_out, ~Bit4_Shift[2], or_47_out);  // AND_Gate
  or or_44 (or_44_out, and_85_out, and_140_out);
  and and_96 (and_96_out, or_44_out, Bit4_Shift[3]);
  and and_97 (and_97_out, ~Bit4_Shift[3], or_48_out);  // AND_Gate
  and and_98 (and_98_out, Bit4_Shift[3], and_5_out);
  and and_99 (and_99_out, and_96_out, and_28_out, Rotate_Mode);
  or or_45 (or_65_out[5], and_87_out, and_98_out, and_99_out);
  and and_100 (and_100_out, multiplexer_16_out[4], Bit4_Shift[0]);
  and and_101 (and_101_out, ~Bit4_Shift[0], multiplexer_16_out[3]);  // AND_Gate
  or or_46 (or_46_out, and_91_out, and_110_out);
  and and_102 (and_102_out, or_46_out, Bit4_Shift[1]);
  and and_103 (and_103_out, ~Bit4_Shift[1], or_50_out);  // AND_Gate
  or or_47 (or_47_out, and_93_out, and_124_out);
  and and_104 (and_104_out, or_47_out, Bit4_Shift[2]);
  and and_105 (and_105_out, ~Bit4_Shift[2], or_51_out);  // AND_Gate
  or or_48 (or_48_out, and_95_out, and_154_out);
  and and_106 (and_106_out, or_48_out, Bit4_Shift[3]);
  and and_107 (and_107_out, ~Bit4_Shift[3], or_52_out);  // AND_Gate
  and and_108 (and_108_out, Bit4_Shift[3], and_5_out);
  and and_109 (and_109_out, and_106_out, and_36_out, Rotate_Mode);
  or or_49 (or_65_out[4], and_97_out, and_108_out, and_109_out);
  and and_110 (and_110_out, multiplexer_16_out[3], Bit4_Shift[0]);
  and and_111 (and_111_out, ~Bit4_Shift[0], multiplexer_16_out[2]);  // AND_Gate
  or or_50 (or_50_out, and_101_out, and_122_out);
  and and_112 (and_112_out, or_50_out, Bit4_Shift[1]);
  and and_113 (and_113_out, ~Bit4_Shift[1], or_54_out);  // AND_Gate
  or or_51 (or_51_out, and_103_out, and_136_out);
  and and_114 (and_114_out, or_51_out, Bit4_Shift[2]);
  and and_115 (and_115_out, ~Bit4_Shift[2], or_55_out);  // AND_Gate
  and and_116 (and_116_out, and_5_out, Bit4_Shift[2]);
  and and_117 (and_117_out, and_114_out, and_10_out, Rotate_Mode);
  or or_52 (or_52_out, and_105_out, and_116_out, and_117_out);
  and and_118 (and_118_out, or_52_out, Bit4_Shift[3]);
  and and_119 (and_119_out, ~Bit4_Shift[3], or_56_out);  // AND_Gate
  and and_120 (and_120_out, Bit4_Shift[3], and_5_out);
  and and_121 (and_121_out, and_118_out, and_44_out, Rotate_Mode);
  or or_53 (or_65_out[3], and_107_out, and_120_out, and_121_out);
  and and_122 (and_122_out, multiplexer_16_out[2], Bit4_Shift[0]);
  and and_123 (and_123_out, ~Bit4_Shift[0], multiplexer_16_out[1]);  // AND_Gate
  or or_54 (or_54_out, and_111_out, and_134_out);
  and and_124 (and_124_out, or_54_out, Bit4_Shift[1]);
  and and_125 (and_125_out, ~Bit4_Shift[1], or_58_out);  // AND_Gate
  or or_55 (or_55_out, and_113_out, and_151_out);
  and and_126 (and_126_out, or_55_out, Bit4_Shift[2]);
  and and_127 (and_127_out, ~Bit4_Shift[2], or_59_out);  // AND_Gate
  and and_128 (and_128_out, and_5_out, Bit4_Shift[2]);
  and and_129 (and_129_out, and_126_out, and_18_out, Rotate_Mode);
  or or_56 (or_56_out, and_115_out, and_128_out, and_129_out);
  and and_130 (and_130_out, or_56_out, Bit4_Shift[3]);
  and and_131 (and_131_out, ~Bit4_Shift[3], or_60_out);  // AND_Gate
  and and_132 (and_132_out, Bit4_Shift[3], and_5_out);
  and and_133 (and_133_out, and_130_out, and_53_out, Rotate_Mode);
  or or_57 (or_65_out[2], and_119_out, and_132_out, and_133_out);
  and and_134 (and_134_out, multiplexer_16_out[1], Bit4_Shift[0]);
  and and_135 (and_135_out, ~Bit4_Shift[0], multiplexer_16_out[0]);  // AND_Gate
  or or_58 (or_58_out, and_123_out, and_148_out);
  and and_136 (and_136_out, or_58_out, Bit4_Shift[1]);
  and and_137 (and_137_out, ~Bit4_Shift[1], or_62_out);  // AND_Gate
  and and_138 (and_138_out, Bit4_Shift[1], and_5_out);
  and and_139 (and_139_out, and_136_out, and_8_out, Rotate_Mode);
  or or_59 (or_59_out, and_125_out, and_138_out, and_139_out);
  and and_140 (and_140_out, or_59_out, Bit4_Shift[2]);
  and and_141 (and_141_out, ~Bit4_Shift[2], or_63_out);  // AND_Gate
  and and_142 (and_142_out, and_5_out, Bit4_Shift[2]);
  and and_143 (and_143_out, and_140_out, and_26_out, Rotate_Mode);
  or or_60 (or_60_out, and_127_out, and_142_out, and_143_out);
  and and_144 (and_144_out, or_60_out, Bit4_Shift[3]);
  and and_145 (and_145_out, ~Bit4_Shift[3], or_64_out);  // AND_Gate
  and and_146 (and_146_out, Bit4_Shift[3], and_5_out);
  and and_147 (and_147_out, and_144_out, and_60_out, Rotate_Mode);
  or or_61 (or_65_out[1], and_131_out, and_146_out, and_147_out);
  and and_148 (and_148_out, multiplexer_16_out[0], Bit4_Shift[0]);
  and and_149 (and_149_out, Bit4_Shift[0], and_5_out);
  and and_150 (and_150_out, and_148_out, and_6_out, Rotate_Mode);
  or or_62 (or_62_out, and_135_out, and_149_out, and_150_out);
  and and_151 (and_151_out, or_62_out, Bit4_Shift[1]);
  and and_152 (and_152_out, Bit4_Shift[1], and_5_out);
  and and_153 (and_153_out, and_151_out, and_16_out, Rotate_Mode);
  or or_63 (or_63_out, and_137_out, and_152_out, and_153_out);
  and and_154 (and_154_out, or_63_out, Bit4_Shift[2]);
  and and_155 (and_155_out, and_5_out, Bit4_Shift[2]);
  and and_156 (and_156_out, and_154_out, and_34_out, Rotate_Mode);
  or or_64 (or_64_out, and_141_out, and_155_out, and_156_out);
  and and_157 (and_157_out, or_64_out, Bit4_Shift[3]);
  and and_158 (and_158_out, Bit4_Shift[3], and_5_out);
  and and_159 (and_159_out, and_157_out, and_68_out, Rotate_Mode);
  or or_65 (or_65_out[0], and_145_out, and_158_out, and_159_out);
  Multiplexer multiplexer_17 (.in0(or_65_out[15]), .in1(or_65_out[0]), .out(Bit16_Result[15]), .sel(Right_Shift_Mode));
  Multiplexer multiplexer_18 (.in0(or_65_out[14]), .in1(or_65_out[1]), .out(Bit16_Result[14]), .sel(Right_Shift_Mode));
  Multiplexer multiplexer_19 (.in0(or_65_out[13]), .in1(or_65_out[2]), .out(Bit16_Result[13]), .sel(Right_Shift_Mode));
  Multiplexer multiplexer_20 (.in0(or_65_out[12]), .in1(or_65_out[3]), .out(Bit16_Result[12]), .sel(Right_Shift_Mode));
  Multiplexer multiplexer_21 (.in0(or_65_out[11]), .in1(or_65_out[4]), .out(Bit16_Result[11]), .sel(Right_Shift_Mode));
  Multiplexer multiplexer_22 (.in0(or_65_out[10]), .in1(or_65_out[5]), .out(Bit16_Result[10]), .sel(Right_Shift_Mode));
  Multiplexer multiplexer_23 (.in0(or_65_out[9]), .in1(or_65_out[6]), .out(Bit16_Result[9]), .sel(Right_Shift_Mode));
  Multiplexer multiplexer_24 (.in0(or_65_out[8]), .in1(or_65_out[7]), .out(Bit16_Result[8]), .sel(Right_Shift_Mode));
  Multiplexer multiplexer_25 (.in0(or_65_out[7]), .in1(or_65_out[8]), .out(Bit16_Result[7]), .sel(Right_Shift_Mode));
  Multiplexer multiplexer_26 (.in0(or_65_out[6]), .in1(or_65_out[9]), .out(Bit16_Result[6]), .sel(Right_Shift_Mode));
  Multiplexer multiplexer_27 (.in0(or_65_out[5]), .in1(or_65_out[10]), .out(Bit16_Result[5]), .sel(Right_Shift_Mode));
  Multiplexer multiplexer_28 (.in0(or_65_out[4]), .in1(or_65_out[11]), .out(Bit16_Result[4]), .sel(Right_Shift_Mode));
  Multiplexer multiplexer_29 (.in0(or_65_out[3]), .in1(or_65_out[12]), .out(Bit16_Result[3]), .sel(Right_Shift_Mode));
  Multiplexer multiplexer_30 (.in0(or_65_out[2]), .in1(or_65_out[13]), .out(Bit16_Result[2]), .sel(Right_Shift_Mode));
  Multiplexer multiplexer_31 (.in0(or_65_out[1]), .in1(or_65_out[14]), .out(Bit16_Result[1]), .sel(Right_Shift_Mode));
  Multiplexer multiplexer_32 (.in0(or_65_out[0]), .in1(or_65_out[15]), .out(Bit16_Result[0]), .sel(Right_Shift_Mode));
endmodule

module Bit16_Right_Shift (
  input  Rotate_Mode,
  input  [15:0] Bit16_Data,
  input  [3:0] Bit4_Shift,
  output [15:0] Bit16_Result,
  output Shift_Overflow
);

  wire and_1_out, and_2_out, and_3_out, and_4_out, and_5_out, and_6_out, and_7_out, and_8_out, and_9_out,
       and_10_out, and_11_out, and_12_out, and_13_out, and_14_out, and_15_out, and_16_out, and_17_out,
       and_18_out, and_19_out, and_20_out, and_21_out, and_22_out, and_23_out, and_24_out, and_25_out,
       and_26_out, and_27_out, and_28_out, and_29_out, and_30_out, and_31_out, and_32_out, and_33_out,
       and_34_out, and_35_out, and_36_out, and_37_out, and_38_out, and_39_out, and_40_out, and_41_out,
       and_42_out, and_43_out, and_44_out, and_45_out, and_46_out, and_47_out, and_48_out, and_49_out,
       and_50_out, and_51_out, and_52_out, and_53_out, and_54_out, and_55_out, and_56_out, and_57_out,
       and_58_out, and_59_out, and_60_out, and_61_out, and_62_out, and_63_out, and_64_out, and_65_out,
       and_66_out, and_67_out, and_68_out, and_69_out, and_70_out, and_71_out, and_72_out, and_73_out,
       and_74_out, and_75_out, and_76_out, and_77_out, and_78_out, and_79_out, and_80_out, and_81_out,
       and_82_out, and_83_out, and_84_out, and_85_out, and_86_out, and_87_out, and_88_out, and_89_out,
       and_90_out, and_91_out, and_92_out, and_93_out, and_94_out, and_95_out, and_96_out, and_97_out,
       and_98_out, and_99_out, and_100_out, and_101_out, and_102_out, and_103_out, and_104_out, and_105_out,
       and_106_out, and_107_out, and_108_out, and_109_out, and_110_out, and_111_out, and_112_out,
       and_113_out, and_114_out, and_115_out, and_116_out, and_117_out, and_118_out, and_119_out,
       and_120_out, and_121_out, and_122_out, and_123_out, and_124_out, and_125_out, and_126_out,
       and_127_out, and_128_out, and_129_out, and_130_out, and_131_out, and_132_out, and_133_out,
       and_134_out, and_135_out, and_136_out, and_137_out, and_138_out, and_139_out, and_140_out,
       and_141_out, and_142_out, and_143_out, or_2_out, or_3_out, or_4_out, or_6_out, or_7_out, or_8_out,
       or_10_out, or_11_out, or_12_out, or_14_out, or_15_out, or_16_out, or_18_out, or_19_out, or_20_out,
       or_22_out, or_23_out, or_24_out, or_26_out, or_27_out, or_28_out, or_30_out, or_31_out, or_32_out,
       or_34_out, or_35_out, or_36_out, or_38_out, or_39_out, or_40_out, or_42_out, or_43_out, or_44_out,
       or_46_out, or_47_out, or_48_out, or_50_out, or_51_out, or_52_out, or_54_out, or_55_out, or_56_out,
       or_58_out, or_59_out, or_60_out, or_62_out, or_63_out, or_64_out;

  or or_1 (Shift_Overflow, and_5_out, and_7_out, and_15_out, and_9_out, and_17_out, and_25_out, and_33_out, and_11_out, and_19_out, and_27_out, and_35_out, and_43_out, and_52_out, and_59_out, and_67_out);
  and and_1 (and_1_out, ~Bit4_Shift[0], Bit16_Data[0]);  // AND_Gate
  and and_2 (and_2_out, ~Bit4_Shift[1], or_2_out);  // AND_Gate
  and and_3 (and_3_out, ~Bit4_Shift[2], or_3_out);  // AND_Gate
  and and_4 (and_4_out, ~Bit4_Shift[3], or_4_out);  // AND_Gate
  and and_5 (and_5_out, Bit16_Data[0], Bit4_Shift[0]);
  and and_6 (and_6_out, ~Bit4_Shift[0], Bit16_Data[1]);  // AND_Gate
  or or_2 (or_2_out, and_1_out, and_13_out);
  and and_7 (and_7_out, or_2_out, Bit4_Shift[1]);
  and and_8 (and_8_out, ~Bit4_Shift[1], or_6_out);  // AND_Gate
  or or_3 (or_3_out, and_2_out, and_23_out);
  and and_9 (and_9_out, or_3_out, Bit4_Shift[2]);
  and and_10 (and_10_out, ~Bit4_Shift[2], or_7_out);  // AND_Gate
  or or_4 (or_4_out, and_3_out, and_41_out);
  and and_11 (and_11_out, or_4_out, Bit4_Shift[3]);
  and and_12 (and_12_out, ~Bit4_Shift[3], or_8_out);  // AND_Gate
  or or_5 (Bit16_Result[0], and_4_out, and_75_out);
  and and_13 (and_13_out, Bit16_Data[1], Bit4_Shift[0]);
  and and_14 (and_14_out, ~Bit4_Shift[0], Bit16_Data[2]);  // AND_Gate
  or or_6 (or_6_out, and_6_out, and_21_out);
  and and_15 (and_15_out, or_6_out, Bit4_Shift[1]);
  and and_16 (and_16_out, ~Bit4_Shift[1], or_10_out);  // AND_Gate
  or or_7 (or_7_out, and_8_out, and_31_out);
  and and_17 (and_17_out, or_7_out, Bit4_Shift[2]);
  and and_18 (and_18_out, ~Bit4_Shift[2], or_11_out);  // AND_Gate
  or or_8 (or_8_out, and_10_out, and_50_out);
  and and_19 (and_19_out, or_8_out, Bit4_Shift[3]);
  and and_20 (and_20_out, ~Bit4_Shift[3], or_12_out);  // AND_Gate
  or or_9 (Bit16_Result[1], and_12_out, and_84_out);
  and and_21 (and_21_out, Bit16_Data[2], Bit4_Shift[0]);
  and and_22 (and_22_out, ~Bit4_Shift[0], Bit16_Data[3]);  // AND_Gate
  or or_10 (or_10_out, and_14_out, and_29_out);
  and and_23 (and_23_out, or_10_out, Bit4_Shift[1]);
  and and_24 (and_24_out, ~Bit4_Shift[1], or_14_out);  // AND_Gate
  or or_11 (or_11_out, and_16_out, and_39_out);
  and and_25 (and_25_out, or_11_out, Bit4_Shift[2]);
  and and_26 (and_26_out, ~Bit4_Shift[2], or_15_out);  // AND_Gate
  or or_12 (or_12_out, and_18_out, and_57_out);
  and and_27 (and_27_out, or_12_out, Bit4_Shift[3]);
  and and_28 (and_28_out, ~Bit4_Shift[3], or_16_out);  // AND_Gate
  or or_13 (Bit16_Result[2], and_20_out, and_93_out);
  and and_29 (and_29_out, Bit16_Data[3], Bit4_Shift[0]);
  and and_30 (and_30_out, ~Bit4_Shift[0], Bit16_Data[4]);  // AND_Gate
  or or_14 (or_14_out, and_22_out, and_37_out);
  and and_31 (and_31_out, or_14_out, Bit4_Shift[1]);
  and and_32 (and_32_out, ~Bit4_Shift[1], or_18_out);  // AND_Gate
  or or_15 (or_15_out, and_24_out, and_48_out);
  and and_33 (and_33_out, or_15_out, Bit4_Shift[2]);
  and and_34 (and_34_out, ~Bit4_Shift[2], or_19_out);  // AND_Gate
  or or_16 (or_16_out, and_26_out, and_65_out);
  and and_35 (and_35_out, or_16_out, Bit4_Shift[3]);
  and and_36 (and_36_out, ~Bit4_Shift[3], or_20_out);  // AND_Gate
  or or_17 (Bit16_Result[3], and_28_out, and_102_out);
  and and_37 (and_37_out, Bit16_Data[4], Bit4_Shift[0]);
  and and_38 (and_38_out, ~Bit4_Shift[0], Bit16_Data[5]);  // AND_Gate
  or or_18 (or_18_out, and_30_out, and_46_out);
  and and_39 (and_39_out, or_18_out, Bit4_Shift[1]);
  and and_40 (and_40_out, ~Bit4_Shift[1], or_22_out);  // AND_Gate
  or or_19 (or_19_out, and_32_out, and_55_out);
  and and_41 (and_41_out, or_19_out, Bit4_Shift[2]);
  and and_42 (and_42_out, ~Bit4_Shift[2], or_23_out);  // AND_Gate
  or or_20 (or_20_out, and_34_out, and_73_out);
  and and_43 (and_43_out, or_20_out, Bit4_Shift[3]);
  and and_44 (and_44_out, ~Bit4_Shift[3], or_24_out);  // AND_Gate
  or or_21 (Bit16_Result[4], and_36_out, and_112_out);
  and and_45 (and_45_out, ~Bit4_Shift[0], Bit16_Data[6]);  // AND_Gate
  and and_46 (and_46_out, Bit16_Data[5], Bit4_Shift[0]);
  or or_22 (or_22_out, and_38_out, and_53_out);
  and and_47 (and_47_out, ~Bit4_Shift[1], or_26_out);  // AND_Gate
  and and_48 (and_48_out, or_22_out, Bit4_Shift[1]);
  or or_23 (or_23_out, and_40_out, and_63_out);
  and and_49 (and_49_out, ~Bit4_Shift[2], or_27_out);  // AND_Gate
  and and_50 (and_50_out, or_23_out, Bit4_Shift[2]);
  or or_24 (or_24_out, and_42_out, and_82_out);
  and and_51 (and_51_out, ~Bit4_Shift[3], or_28_out);  // AND_Gate
  and and_52 (and_52_out, or_24_out, Bit4_Shift[3]);
  or or_25 (Bit16_Result[5], and_44_out, and_122_out);
  and and_53 (and_53_out, Bit16_Data[6], Bit4_Shift[0]);
  and and_54 (and_54_out, ~Bit4_Shift[0], Bit16_Data[7]);  // AND_Gate
  or or_26 (or_26_out, and_45_out, and_61_out);
  and and_55 (and_55_out, or_26_out, Bit4_Shift[1]);
  and and_56 (and_56_out, ~Bit4_Shift[1], or_30_out);  // AND_Gate
  or or_27 (or_27_out, and_47_out, and_71_out);
  and and_57 (and_57_out, or_27_out, Bit4_Shift[2]);
  and and_58 (and_58_out, ~Bit4_Shift[2], or_31_out);  // AND_Gate
  or or_28 (or_28_out, and_49_out, and_91_out);
  and and_59 (and_59_out, or_28_out, Bit4_Shift[3]);
  and and_60 (and_60_out, ~Bit4_Shift[3], or_32_out);  // AND_Gate
  or or_29 (Bit16_Result[6], and_51_out, and_133_out);
  and and_61 (and_61_out, Bit16_Data[7], Bit4_Shift[0]);
  and and_62 (and_62_out, ~Bit4_Shift[0], Bit16_Data[8]);  // AND_Gate
  or or_30 (or_30_out, and_54_out, and_69_out);
  and and_63 (and_63_out, or_30_out, Bit4_Shift[1]);
  and and_64 (and_64_out, ~Bit4_Shift[1], or_34_out);  // AND_Gate
  or or_31 (or_31_out, and_56_out, and_80_out);
  and and_65 (and_65_out, or_31_out, Bit4_Shift[2]);
  and and_66 (and_66_out, ~Bit4_Shift[2], or_35_out);  // AND_Gate
  or or_32 (or_32_out, and_58_out, and_100_out);
  and and_67 (and_67_out, or_32_out, Bit4_Shift[3]);
  and and_68 (and_68_out, ~Bit4_Shift[3], or_36_out);  // AND_Gate
  or or_33 (Bit16_Result[7], and_60_out, and_142_out);
  and and_69 (and_69_out, Bit16_Data[8], Bit4_Shift[0]);
  and and_70 (and_70_out, ~Bit4_Shift[0], Bit16_Data[9]);  // AND_Gate
  or or_34 (or_34_out, and_62_out, and_78_out);
  and and_71 (and_71_out, or_34_out, Bit4_Shift[1]);
  and and_72 (and_72_out, ~Bit4_Shift[1], or_38_out);  // AND_Gate
  or or_35 (or_35_out, and_64_out, and_89_out);
  and and_73 (and_73_out, or_35_out, Bit4_Shift[2]);
  and and_74 (and_74_out, ~Bit4_Shift[2], or_39_out);  // AND_Gate
  or or_36 (or_36_out, and_66_out, and_109_out);
  and and_75 (and_75_out, or_36_out, Bit4_Shift[3]);
  and and_76 (and_76_out, ~Bit4_Shift[3], or_40_out);  // AND_Gate
  and and_77 (and_77_out, and_75_out, and_11_out, Rotate_Mode);
  or or_37 (Bit16_Result[8], and_68_out, and_77_out);
  and and_78 (and_78_out, Bit16_Data[9], Bit4_Shift[0]);
  and and_79 (and_79_out, ~Bit4_Shift[0], Bit16_Data[10]);  // AND_Gate
  or or_38 (or_38_out, and_70_out, and_87_out);
  and and_80 (and_80_out, or_38_out, Bit4_Shift[1]);
  and and_81 (and_81_out, ~Bit4_Shift[1], or_42_out);  // AND_Gate
  or or_39 (or_39_out, and_72_out, and_98_out);
  and and_82 (and_82_out, or_39_out, Bit4_Shift[2]);
  and and_83 (and_83_out, ~Bit4_Shift[2], or_43_out);  // AND_Gate
  or or_40 (or_40_out, and_74_out, and_119_out);
  and and_84 (and_84_out, or_40_out, Bit4_Shift[3]);
  and and_85 (and_85_out, ~Bit4_Shift[3], or_44_out);  // AND_Gate
  and and_86 (and_86_out, and_84_out, and_19_out, Rotate_Mode);
  or or_41 (Bit16_Result[9], and_76_out, and_86_out);
  and and_87 (and_87_out, Bit16_Data[10], Bit4_Shift[0]);
  and and_88 (and_88_out, ~Bit4_Shift[0], Bit16_Data[11]);  // AND_Gate
  or or_42 (or_42_out, and_79_out, and_96_out);
  and and_89 (and_89_out, or_42_out, Bit4_Shift[1]);
  and and_90 (and_90_out, ~Bit4_Shift[1], or_46_out);  // AND_Gate
  or or_43 (or_43_out, and_81_out, and_107_out);
  and and_91 (and_91_out, or_43_out, Bit4_Shift[2]);
  and and_92 (and_92_out, ~Bit4_Shift[2], or_47_out);  // AND_Gate
  or or_44 (or_44_out, and_83_out, and_130_out);
  and and_93 (and_93_out, or_44_out, Bit4_Shift[3]);
  and and_94 (and_94_out, ~Bit4_Shift[3], or_48_out);  // AND_Gate
  and and_95 (and_95_out, and_93_out, and_27_out, Rotate_Mode);
  or or_45 (Bit16_Result[10], and_85_out, and_95_out);
  and and_96 (and_96_out, Bit16_Data[11], Bit4_Shift[0]);
  and and_97 (and_97_out, ~Bit4_Shift[0], Bit16_Data[12]);  // AND_Gate
  or or_46 (or_46_out, and_88_out, and_105_out);
  and and_98 (and_98_out, or_46_out, Bit4_Shift[1]);
  and and_99 (and_99_out, ~Bit4_Shift[1], or_50_out);  // AND_Gate
  or or_47 (or_47_out, and_90_out, and_117_out);
  and and_100 (and_100_out, or_47_out, Bit4_Shift[2]);
  and and_101 (and_101_out, ~Bit4_Shift[2], or_51_out);  // AND_Gate
  or or_48 (or_48_out, and_92_out, and_140_out);
  and and_102 (and_102_out, or_48_out, Bit4_Shift[3]);
  and and_103 (and_103_out, ~Bit4_Shift[3], or_52_out);  // AND_Gate
  and and_104 (and_104_out, and_102_out, and_35_out, Rotate_Mode);
  or or_49 (Bit16_Result[11], and_94_out, and_104_out);
  and and_105 (and_105_out, Bit16_Data[12], Bit4_Shift[0]);
  and and_106 (and_106_out, ~Bit4_Shift[0], Bit16_Data[13]);  // AND_Gate
  or or_50 (or_50_out, and_97_out, and_115_out);
  and and_107 (and_107_out, or_50_out, Bit4_Shift[1]);
  and and_108 (and_108_out, ~Bit4_Shift[1], or_54_out);  // AND_Gate
  or or_51 (or_51_out, and_99_out, and_127_out);
  and and_109 (and_109_out, or_51_out, Bit4_Shift[2]);
  and and_110 (and_110_out, ~Bit4_Shift[2], or_55_out);  // AND_Gate
  and and_111 (and_111_out, and_109_out, and_9_out, Rotate_Mode);
  or or_52 (or_52_out, and_101_out, and_111_out);
  and and_112 (and_112_out, or_52_out, Bit4_Shift[3]);
  and and_113 (and_113_out, ~Bit4_Shift[3], or_56_out);  // AND_Gate
  and and_114 (and_114_out, and_112_out, and_43_out, Rotate_Mode);
  or or_53 (Bit16_Result[12], and_103_out, and_114_out);
  and and_115 (and_115_out, Bit16_Data[13], Bit4_Shift[0]);
  and and_116 (and_116_out, ~Bit4_Shift[0], Bit16_Data[14]);  // AND_Gate
  or or_54 (or_54_out, and_106_out, and_125_out);
  and and_117 (and_117_out, or_54_out, Bit4_Shift[1]);
  and and_118 (and_118_out, ~Bit4_Shift[1], or_58_out);  // AND_Gate
  or or_55 (or_55_out, and_108_out, and_138_out);
  and and_119 (and_119_out, or_55_out, Bit4_Shift[2]);
  and and_120 (and_120_out, ~Bit4_Shift[2], or_59_out);  // AND_Gate
  and and_121 (and_121_out, and_119_out, and_17_out, Rotate_Mode);
  or or_56 (or_56_out, and_110_out, and_121_out);
  and and_122 (and_122_out, or_56_out, Bit4_Shift[3]);
  and and_123 (and_123_out, ~Bit4_Shift[3], or_60_out);  // AND_Gate
  and and_124 (and_124_out, and_122_out, and_52_out, Rotate_Mode);
  or or_57 (Bit16_Result[13], and_113_out, and_124_out);
  and and_125 (and_125_out, Bit16_Data[14], Bit4_Shift[0]);
  and and_126 (and_126_out, ~Bit4_Shift[0], Bit16_Data[15]);  // AND_Gate
  or or_58 (or_58_out, and_116_out, and_136_out);
  and and_127 (and_127_out, or_58_out, Bit4_Shift[1]);
  and and_128 (and_128_out, ~Bit4_Shift[1], or_62_out);  // AND_Gate
  and and_129 (and_129_out, and_127_out, and_7_out, Rotate_Mode);
  or or_59 (or_59_out, and_118_out, and_129_out);
  and and_130 (and_130_out, or_59_out, Bit4_Shift[2]);
  and and_131 (and_131_out, ~Bit4_Shift[2], or_63_out);  // AND_Gate
  and and_132 (and_132_out, and_130_out, and_25_out, Rotate_Mode);
  or or_60 (or_60_out, and_120_out, and_132_out);
  and and_133 (and_133_out, or_60_out, Bit4_Shift[3]);
  and and_134 (and_134_out, ~Bit4_Shift[3], or_64_out);  // AND_Gate
  and and_135 (and_135_out, and_133_out, and_59_out, Rotate_Mode);
  or or_61 (Bit16_Result[14], and_123_out, and_135_out);
  and and_136 (and_136_out, Bit16_Data[15], Bit4_Shift[0]);
  and and_137 (and_137_out, and_136_out, and_5_out, Rotate_Mode);
  or or_62 (or_62_out, and_126_out, and_137_out);
  and and_138 (and_138_out, or_62_out, Bit4_Shift[1]);
  and and_139 (and_139_out, and_138_out, and_15_out, Rotate_Mode);
  or or_63 (or_63_out, and_128_out, and_139_out);
  and and_140 (and_140_out, or_63_out, Bit4_Shift[2]);
  and and_141 (and_141_out, and_140_out, and_33_out, Rotate_Mode);
  or or_64 (or_64_out, and_131_out, and_141_out);
  and and_142 (and_142_out, or_64_out, Bit4_Shift[3]);
  and and_143 (and_143_out, and_142_out, and_67_out, Rotate_Mode);
  or or_65 (Bit16_Result[15], and_134_out, and_143_out);
endmodule

module Bit4_Controlled_Buffer (
  input  [3:0] Bit4_In,
  input  Enable,
  output [3:0] Bit4_Out
);

  and and_1 (Bit4_Out[0], Bit4_In[0], Enable);
  and and_2 (Bit4_Out[1], Bit4_In[1], Enable);
  and and_3 (Bit4_Out[2], Bit4_In[2], Enable);
  and and_4 (Bit4_Out[3], Bit4_In[3], Enable);
endmodule

module Bit4_Twos_Complementer (
  input  [3:0] Bit4_In,
  output [3:0] Bit4_Result
);

  wire or_1_out, or_2_out;

  or or_1 (or_1_out, Bit4_In[0], Bit4_Result[1]);
  or or_2 (or_2_out, Bit4_In[0], Bit4_Result[1], Bit4_Result[2]);
  xor xor_1 (Bit4_Result[1], Bit4_In[1], Bit4_In[0]);
  xor xor_2 (Bit4_Result[2], Bit4_In[2], or_1_out);
  xor xor_3 (Bit4_Result[3], Bit4_In[3], or_2_out);

  assign Bit4_Result[0] = Bit4_In[0];
endmodule

module Bit4_Adder (
  input  Cin,
  input  [3:0] Bit4_A,
  input  [3:0] Bit4_B,
  output Cout,
  output [3:0] Bit4_Result
);

  wire and_1_out, and_2_out, and_3_out, and_4_out, bit4_cla_logic_1_c2, bit4_cla_logic_1_c3,
       bit4_cla_logic_1_c4, xor_1_out, xor_2_out, xor_3_out, xor_4_out;

  xor xor_1 (xor_1_out, Bit4_A[0], Bit4_B[0]);
  and and_1 (and_1_out, Bit4_B[0], Bit4_A[0]);
  xor xor_2 (xor_2_out, Bit4_A[1], Bit4_B[1]);
  and and_2 (and_2_out, Bit4_B[1], Bit4_A[1]);
  xor xor_3 (xor_3_out, Bit4_A[2], Bit4_B[2]);
  and and_3 (and_3_out, Bit4_B[2], Bit4_A[2]);
  xor xor_4 (xor_4_out, Bit4_A[3], Bit4_B[3]);
  and and_4 (and_4_out, Bit4_B[3], Bit4_A[3]);
  xor xor_5 (Bit4_Result[3], xor_4_out, Cin);
  xor xor_6 (Bit4_Result[2], xor_3_out, bit4_cla_logic_1_c2);
  xor xor_7 (Bit4_Result[0], xor_1_out, bit4_cla_logic_1_c4);
  xor xor_8 (Bit4_Result[1], xor_2_out, bit4_cla_logic_1_c3);
  Bit4_CLA_Logic bit4_cla_logic_1 (
    .Cin(Cin), .P1(xor_1_out), .G1(and_1_out), .P2(xor_2_out), .G2(and_2_out), .P3(xor_3_out),
    .G3(and_3_out), .P4(xor_4_out), .G4(and_4_out), .C2(bit4_cla_logic_1_c2), .C3(bit4_cla_logic_1_c3),
    .C4(bit4_cla_logic_1_c4), .COUT(Cout));  // open: PG
endmodule

module Bit5_Adder (
  input  Cin,
  input  [4:0] Bit5_A,
  input  [4:0] Bit5_B,
  output [4:0] Bit5_Result,
  output Cout
);

  wire and_1_out, and_2_out, and_3_out, and_4_out, and_5_out, and_6_out, and_7_out, and_8_out, and_9_out,
       and_10_out, and_11_out, and_12_out, and_13_out, and_14_out, and_15_out, and_16_out, and_17_out,
       and_18_out, and_19_out, and_20_out, or_1_out, or_2_out, or_3_out, or_4_out, xor_1_out, xor_2_out,
       xor_3_out, xor_4_out, xor_5_out;

  xor xor_1 (xor_1_out, Bit5_B[3], Bit5_A[3]);
  and and_1 (and_1_out, Bit5_A[3], Bit5_B[3]);
  xor xor_2 (xor_2_out, Bit5_B[4], Bit5_A[4]);
  and and_2 (and_2_out, Bit5_A[4], Bit5_B[4]);
  xor xor_3 (xor_3_out, Bit5_B[0], Bit5_A[0]);
  and and_3 (and_3_out, Bit5_A[0], Bit5_B[0]);
  xor xor_4 (xor_4_out, Bit5_B[1], Bit5_A[1]);
  and and_4 (and_4_out, Bit5_A[1], Bit5_B[1]);
  xor xor_5 (xor_5_out, Bit5_B[2], Bit5_A[2]);
  and and_5 (and_5_out, Bit5_A[2], Bit5_B[2]);
  xor xor_6 (Bit5_Result[3], or_3_out, xor_1_out);
  xor xor_7 (Bit5_Result[4], or_4_out, xor_2_out);
  xor xor_8 (Bit5_Result[2], or_2_out, xor_5_out);
  xor xor_9 (Bit5_Result[0], Cin, xor_3_out);
  or or_1 (or_1_out, and_3_out, and_6_out);
  xor xor_10 (Bit5_Result[1], or_1_out, xor_4_out);
  or or_2 (or_2_out, and_4_out, and_7_out, and_8_out);
  or or_3 (or_3_out, and_5_out, and_9_out, and_10_out, and_11_out);
  or or_4 (or_4_out, and_1_out, and_12_out, and_13_out, and_14_out, and_15_out);
  or or_5 (Cout, and_2_out, and_16_out, and_17_out, and_18_out, and_19_out, and_20_out);
  and and_6 (and_6_out, xor_3_out, Cin);
  and and_7 (and_7_out, xor_4_out, and_3_out);
  and and_8 (and_8_out, xor_4_out, xor_3_out, Cin);
  and and_9 (and_9_out, and_4_out, xor_5_out);
  and and_10 (and_10_out, xor_5_out, xor_4_out, and_3_out);
  and and_11 (and_11_out, xor_5_out, xor_4_out, Cin, xor_3_out);
  and and_12 (and_12_out, and_5_out, xor_1_out);
  and and_13 (and_13_out, xor_1_out, xor_5_out, and_4_out);
  and and_14 (and_14_out, xor_1_out, xor_5_out, xor_4_out, and_3_out);
  and and_15 (and_15_out, xor_1_out, xor_5_out, xor_4_out, xor_3_out, Cin);
  and and_16 (and_16_out, xor_2_out, and_1_out);
  and and_17 (and_17_out, xor_2_out, xor_1_out, and_5_out);
  and and_18 (and_18_out, xor_2_out, xor_1_out, xor_5_out, and_4_out);
  and and_19 (and_19_out, xor_2_out, xor_1_out, xor_5_out, xor_4_out, and_3_out);
  and and_20 (and_20_out, xor_2_out, xor_1_out, xor_5_out, xor_4_out, xor_3_out, Cin);

  // Notes on the sheet:
  //   0
endmodule

module Bit5_Twos_Complementer (
  input  [4:0] Bit5_In,
  output [4:0] Bit5_Result
);

  wire or_1_out, or_2_out, or_3_out;

  or or_1 (or_1_out, Bit5_In[0], Bit5_Result[1]);
  or or_2 (or_2_out, Bit5_In[0], Bit5_Result[1], Bit5_Result[2]);
  or or_3 (or_3_out, Bit5_Result[3], Bit5_Result[1], Bit5_Result[2], Bit5_In[0]);
  xor xor_1 (Bit5_Result[1], Bit5_In[1], Bit5_In[0]);
  xor xor_2 (Bit5_Result[2], Bit5_In[2], or_1_out);
  xor xor_3 (Bit5_Result[3], Bit5_In[3], or_2_out);
  xor xor_4 (Bit5_Result[4], or_3_out, Bit5_In[4]);

  assign Bit5_Result[0] = Bit5_In[0];
endmodule

module Bit16T24_Right_Shift (
  input  [15:0] Bit16_Data,
  input  [3:0] Bit4_Shift,
  output [23:0] Bit24_Result,
  output [15:0] Bit16_Result,
  output Shift_Overflow_For_Bit16
);

  wire and_1_out, and_2_out, and_3_out, and_4_out, and_5_out, and_6_out, and_7_out, and_8_out, and_9_out,
       and_10_out, and_11_out, and_12_out, and_13_out, and_14_out, and_15_out, and_16_out, and_17_out,
       and_18_out, and_19_out, and_20_out, and_21_out, and_22_out, and_23_out, and_24_out, and_25_out,
       and_26_out, and_27_out, and_28_out, and_29_out, and_30_out, and_31_out, and_32_out, and_33_out,
       and_34_out, and_35_out, and_36_out, and_37_out, and_38_out, and_39_out, and_40_out, and_41_out,
       and_42_out, and_43_out, and_44_out, and_45_out, and_46_out, and_47_out, and_48_out, and_49_out,
       and_50_out, and_51_out, and_52_out, and_53_out, and_54_out, and_55_out, and_56_out, and_57_out,
       and_58_out, and_59_out, and_60_out, and_61_out, and_62_out, and_63_out, and_64_out, and_65_out,
       and_66_out, and_67_out, and_68_out, and_69_out, and_70_out, and_71_out, and_72_out, and_73_out,
       and_74_out, and_75_out, and_76_out, and_77_out, and_78_out, and_79_out, and_80_out, and_81_out,
       and_82_out, and_83_out, and_84_out, and_86_out, and_87_out, and_88_out, and_89_out, and_90_out,
       and_91_out, and_92_out, and_94_out, and_95_out, and_96_out, and_97_out, and_98_out, and_99_out,
       and_100_out, and_102_out, and_103_out, and_104_out, and_105_out, and_106_out, and_107_out,
       and_108_out, and_110_out, and_111_out, and_112_out, and_113_out, and_114_out, and_115_out,
       and_116_out, and_118_out, and_119_out, and_120_out, and_121_out, and_122_out, and_123_out,
       and_124_out, and_126_out, and_127_out, and_128_out, and_129_out, and_130_out, and_131_out,
       and_132_out, and_134_out, and_135_out, and_136_out, and_137_out, and_138_out, and_139_out,
       and_140_out, and_142_out, or_6_out, or_8_out, or_10_out, or_11_out, or_13_out, or_14_out, or_16_out,
       or_17_out, or_18_out, or_20_out, or_21_out, or_22_out, or_24_out, or_25_out, or_26_out, or_28_out,
       or_29_out, or_30_out, or_32_out, or_33_out, or_34_out, or_36_out, or_37_out, or_38_out, or_40_out,
       or_41_out, or_42_out, or_44_out, or_45_out, or_46_out, or_48_out, or_49_out, or_50_out, or_51_out,
       or_52_out, or_53_out, or_54_out, or_55_out, or_56_out, or_57_out, or_58_out, or_59_out, or_60_out,
       or_61_out, or_62_out, or_63_out, or_64_out;

  or or_1 (Shift_Overflow_For_Bit16, and_16_out, and_18_out, and_26_out, and_20_out, and_28_out, and_36_out, and_44_out, and_22_out, and_30_out, and_38_out, and_46_out, and_54_out, and_62_out, and_70_out, and_78_out);
  or or_2 (Bit24_Result[0], and_2_out, and_22_out);
  or or_3 (Bit24_Result[1], and_4_out, and_30_out);
  or or_4 (Bit24_Result[2], and_8_out, and_38_out);
  or or_5 (Bit24_Result[3], and_14_out, and_46_out);
  or or_6 (or_6_out, and_6_out, and_20_out);
  and and_1 (and_1_out, ~Bit4_Shift[3], or_6_out);  // AND_Gate
  and and_2 (and_2_out, or_6_out, Bit4_Shift[3]);
  or or_7 (Bit24_Result[4], and_1_out, and_54_out);
  or or_8 (or_8_out, and_12_out, and_28_out);
  and and_3 (and_3_out, ~Bit4_Shift[3], or_8_out);  // AND_Gate
  and and_4 (and_4_out, or_8_out, Bit4_Shift[3]);
  or or_9 (Bit24_Result[5], and_3_out, and_62_out);
  or or_10 (or_10_out, and_10_out, and_18_out);
  and and_5 (and_5_out, ~Bit4_Shift[2], or_10_out);  // AND_Gate
  and and_6 (and_6_out, or_10_out, Bit4_Shift[2]);
  or or_11 (or_11_out, and_5_out, and_36_out);
  and and_7 (and_7_out, ~Bit4_Shift[3], or_11_out);  // AND_Gate
  and and_8 (and_8_out, or_11_out, Bit4_Shift[3]);
  or or_12 (Bit24_Result[6], and_7_out, and_70_out);
  and and_9 (and_9_out, ~Bit4_Shift[1], and_16_out);  // AND_Gate
  and and_10 (and_10_out, and_16_out, Bit4_Shift[1]);
  or or_13 (or_13_out, and_9_out, and_26_out);
  and and_11 (and_11_out, ~Bit4_Shift[2], or_13_out);  // AND_Gate
  and and_12 (and_12_out, or_13_out, Bit4_Shift[2]);
  or or_14 (or_14_out, and_11_out, and_44_out);
  and and_13 (and_13_out, ~Bit4_Shift[3], or_14_out);  // AND_Gate
  and and_14 (and_14_out, or_14_out, Bit4_Shift[3]);
  or or_15 (Bit24_Result[7], and_13_out, and_78_out);
  and and_15 (and_15_out, ~Bit4_Shift[0], Bit16_Data[0]);  // AND_Gate
  and and_16 (and_16_out, Bit16_Data[0], Bit4_Shift[0]);
  or or_16 (or_16_out, and_15_out, and_24_out);
  and and_17 (and_17_out, ~Bit4_Shift[1], or_16_out);  // AND_Gate
  and and_18 (and_18_out, or_16_out, Bit4_Shift[1]);
  or or_17 (or_17_out, and_17_out, and_34_out);
  and and_19 (and_19_out, ~Bit4_Shift[2], or_17_out);  // AND_Gate
  and and_20 (and_20_out, or_17_out, Bit4_Shift[2]);
  or or_18 (or_18_out, and_19_out, and_52_out);
  and and_21 (and_21_out, ~Bit4_Shift[3], or_18_out);  // AND_Gate
  and and_22 (and_22_out, or_18_out, Bit4_Shift[3]);
  or or_19 (Bit16_Result[0], and_21_out, and_86_out);
  and and_23 (and_23_out, ~Bit4_Shift[0], Bit16_Data[1]);  // AND_Gate
  and and_24 (and_24_out, Bit16_Data[1], Bit4_Shift[0]);
  or or_20 (or_20_out, and_23_out, and_32_out);
  and and_25 (and_25_out, ~Bit4_Shift[1], or_20_out);  // AND_Gate
  and and_26 (and_26_out, or_20_out, Bit4_Shift[1]);
  or or_21 (or_21_out, and_25_out, and_42_out);
  and and_27 (and_27_out, ~Bit4_Shift[2], or_21_out);  // AND_Gate
  and and_28 (and_28_out, or_21_out, Bit4_Shift[2]);
  or or_22 (or_22_out, and_27_out, and_60_out);
  and and_29 (and_29_out, ~Bit4_Shift[3], or_22_out);  // AND_Gate
  and and_30 (and_30_out, or_22_out, Bit4_Shift[3]);
  or or_23 (Bit16_Result[1], and_29_out, and_94_out);
  and and_31 (and_31_out, ~Bit4_Shift[0], Bit16_Data[2]);  // AND_Gate
  and and_32 (and_32_out, Bit16_Data[2], Bit4_Shift[0]);
  or or_24 (or_24_out, and_31_out, and_40_out);
  and and_33 (and_33_out, ~Bit4_Shift[1], or_24_out);  // AND_Gate
  and and_34 (and_34_out, or_24_out, Bit4_Shift[1]);
  or or_25 (or_25_out, and_33_out, and_50_out);
  and and_35 (and_35_out, ~Bit4_Shift[2], or_25_out);  // AND_Gate
  and and_36 (and_36_out, or_25_out, Bit4_Shift[2]);
  or or_26 (or_26_out, and_35_out, and_68_out);
  and and_37 (and_37_out, ~Bit4_Shift[3], or_26_out);  // AND_Gate
  and and_38 (and_38_out, or_26_out, Bit4_Shift[3]);
  or or_27 (Bit16_Result[2], and_37_out, and_102_out);
  and and_39 (and_39_out, ~Bit4_Shift[0], Bit16_Data[3]);  // AND_Gate
  and and_40 (and_40_out, Bit16_Data[3], Bit4_Shift[0]);
  or or_28 (or_28_out, and_39_out, and_48_out);
  and and_41 (and_41_out, ~Bit4_Shift[1], or_28_out);  // AND_Gate
  and and_42 (and_42_out, or_28_out, Bit4_Shift[1]);
  or or_29 (or_29_out, and_41_out, and_58_out);
  and and_43 (and_43_out, ~Bit4_Shift[2], or_29_out);  // AND_Gate
  and and_44 (and_44_out, or_29_out, Bit4_Shift[2]);
  or or_30 (or_30_out, and_43_out, and_76_out);
  and and_45 (and_45_out, ~Bit4_Shift[3], or_30_out);  // AND_Gate
  and and_46 (and_46_out, or_30_out, Bit4_Shift[3]);
  or or_31 (Bit16_Result[3], and_45_out, and_110_out);
  and and_47 (and_47_out, ~Bit4_Shift[0], Bit16_Data[4]);  // AND_Gate
  and and_48 (and_48_out, Bit16_Data[4], Bit4_Shift[0]);
  or or_32 (or_32_out, and_47_out, and_56_out);
  and and_49 (and_49_out, ~Bit4_Shift[1], or_32_out);  // AND_Gate
  and and_50 (and_50_out, or_32_out, Bit4_Shift[1]);
  or or_33 (or_33_out, and_49_out, and_66_out);
  and and_51 (and_51_out, ~Bit4_Shift[2], or_33_out);  // AND_Gate
  and and_52 (and_52_out, or_33_out, Bit4_Shift[2]);
  or or_34 (or_34_out, and_51_out, and_84_out);
  and and_53 (and_53_out, ~Bit4_Shift[3], or_34_out);  // AND_Gate
  and and_54 (and_54_out, or_34_out, Bit4_Shift[3]);
  or or_35 (Bit16_Result[4], and_53_out, and_118_out);
  and and_55 (and_55_out, ~Bit4_Shift[0], Bit16_Data[5]);  // AND_Gate
  and and_56 (and_56_out, Bit16_Data[5], Bit4_Shift[0]);
  or or_36 (or_36_out, and_55_out, and_64_out);
  and and_57 (and_57_out, ~Bit4_Shift[1], or_36_out);  // AND_Gate
  and and_58 (and_58_out, or_36_out, Bit4_Shift[1]);
  or or_37 (or_37_out, and_57_out, and_74_out);
  and and_59 (and_59_out, ~Bit4_Shift[2], or_37_out);  // AND_Gate
  and and_60 (and_60_out, or_37_out, Bit4_Shift[2]);
  or or_38 (or_38_out, and_59_out, and_92_out);
  and and_61 (and_61_out, ~Bit4_Shift[3], or_38_out);  // AND_Gate
  and and_62 (and_62_out, or_38_out, Bit4_Shift[3]);
  or or_39 (Bit16_Result[5], and_61_out, and_126_out);
  and and_63 (and_63_out, ~Bit4_Shift[0], Bit16_Data[6]);  // AND_Gate
  and and_64 (and_64_out, Bit16_Data[6], Bit4_Shift[0]);
  or or_40 (or_40_out, and_63_out, and_72_out);
  and and_65 (and_65_out, ~Bit4_Shift[1], or_40_out);  // AND_Gate
  and and_66 (and_66_out, or_40_out, Bit4_Shift[1]);
  or or_41 (or_41_out, and_65_out, and_82_out);
  and and_67 (and_67_out, ~Bit4_Shift[2], or_41_out);  // AND_Gate
  and and_68 (and_68_out, or_41_out, Bit4_Shift[2]);
  or or_42 (or_42_out, and_67_out, and_100_out);
  and and_69 (and_69_out, ~Bit4_Shift[3], or_42_out);  // AND_Gate
  and and_70 (and_70_out, or_42_out, Bit4_Shift[3]);
  or or_43 (Bit16_Result[6], and_69_out, and_134_out);
  and and_71 (and_71_out, ~Bit4_Shift[0], Bit16_Data[7]);  // AND_Gate
  and and_72 (and_72_out, Bit16_Data[7], Bit4_Shift[0]);
  or or_44 (or_44_out, and_71_out, and_80_out);
  and and_73 (and_73_out, ~Bit4_Shift[1], or_44_out);  // AND_Gate
  and and_74 (and_74_out, or_44_out, Bit4_Shift[1]);
  or or_45 (or_45_out, and_73_out, and_90_out);
  and and_75 (and_75_out, ~Bit4_Shift[2], or_45_out);  // AND_Gate
  and and_76 (and_76_out, or_45_out, Bit4_Shift[2]);
  or or_46 (or_46_out, and_75_out, and_108_out);
  and and_77 (and_77_out, ~Bit4_Shift[3], or_46_out);  // AND_Gate
  and and_78 (and_78_out, or_46_out, Bit4_Shift[3]);
  or or_47 (Bit16_Result[7], and_77_out, and_142_out);
  and and_79 (and_79_out, ~Bit4_Shift[0], Bit16_Data[8]);  // AND_Gate
  and and_80 (and_80_out, Bit16_Data[8], Bit4_Shift[0]);
  or or_48 (or_48_out, and_79_out, and_88_out);
  and and_81 (and_81_out, ~Bit4_Shift[1], or_48_out);  // AND_Gate
  and and_82 (and_82_out, or_48_out, Bit4_Shift[1]);
  or or_49 (or_49_out, and_81_out, and_98_out);
  and and_83 (and_83_out, ~Bit4_Shift[2], or_49_out);  // AND_Gate
  and and_84 (and_84_out, or_49_out, Bit4_Shift[2]);
  or or_50 (or_50_out, and_83_out, and_116_out);
  and and_85 (Bit16_Result[8], ~Bit4_Shift[3], or_50_out);  // AND_Gate
  and and_86 (and_86_out, or_50_out, Bit4_Shift[3]);
  and and_87 (and_87_out, ~Bit4_Shift[0], Bit16_Data[9]);  // AND_Gate
  and and_88 (and_88_out, Bit16_Data[9], Bit4_Shift[0]);
  or or_51 (or_51_out, and_87_out, and_96_out);
  and and_89 (and_89_out, ~Bit4_Shift[1], or_51_out);  // AND_Gate
  and and_90 (and_90_out, or_51_out, Bit4_Shift[1]);
  or or_52 (or_52_out, and_89_out, and_106_out);
  and and_91 (and_91_out, ~Bit4_Shift[2], or_52_out);  // AND_Gate
  and and_92 (and_92_out, or_52_out, Bit4_Shift[2]);
  or or_53 (or_53_out, and_91_out, and_124_out);
  and and_93 (Bit16_Result[9], ~Bit4_Shift[3], or_53_out);  // AND_Gate
  and and_94 (and_94_out, or_53_out, Bit4_Shift[3]);
  and and_95 (and_95_out, ~Bit4_Shift[0], Bit16_Data[10]);  // AND_Gate
  and and_96 (and_96_out, Bit16_Data[10], Bit4_Shift[0]);
  or or_54 (or_54_out, and_95_out, and_104_out);
  and and_97 (and_97_out, ~Bit4_Shift[1], or_54_out);  // AND_Gate
  and and_98 (and_98_out, or_54_out, Bit4_Shift[1]);
  or or_55 (or_55_out, and_97_out, and_114_out);
  and and_99 (and_99_out, ~Bit4_Shift[2], or_55_out);  // AND_Gate
  and and_100 (and_100_out, or_55_out, Bit4_Shift[2]);
  or or_56 (or_56_out, and_99_out, and_132_out);
  and and_101 (Bit16_Result[10], ~Bit4_Shift[3], or_56_out);  // AND_Gate
  and and_102 (and_102_out, or_56_out, Bit4_Shift[3]);
  and and_103 (and_103_out, ~Bit4_Shift[0], Bit16_Data[11]);  // AND_Gate
  and and_104 (and_104_out, Bit16_Data[11], Bit4_Shift[0]);
  or or_57 (or_57_out, and_103_out, and_112_out);
  and and_105 (and_105_out, ~Bit4_Shift[1], or_57_out);  // AND_Gate
  and and_106 (and_106_out, or_57_out, Bit4_Shift[1]);
  or or_58 (or_58_out, and_105_out, and_122_out);
  and and_107 (and_107_out, ~Bit4_Shift[2], or_58_out);  // AND_Gate
  and and_108 (and_108_out, or_58_out, Bit4_Shift[2]);
  or or_59 (or_59_out, and_107_out, and_140_out);
  and and_109 (Bit16_Result[11], ~Bit4_Shift[3], or_59_out);  // AND_Gate
  and and_110 (and_110_out, or_59_out, Bit4_Shift[3]);
  and and_111 (and_111_out, ~Bit4_Shift[0], Bit16_Data[12]);  // AND_Gate
  and and_112 (and_112_out, Bit16_Data[12], Bit4_Shift[0]);
  or or_60 (or_60_out, and_111_out, and_120_out);
  and and_113 (and_113_out, ~Bit4_Shift[1], or_60_out);  // AND_Gate
  and and_114 (and_114_out, or_60_out, Bit4_Shift[1]);
  or or_61 (or_61_out, and_113_out, and_130_out);
  and and_115 (and_115_out, ~Bit4_Shift[2], or_61_out);  // AND_Gate
  and and_116 (and_116_out, or_61_out, Bit4_Shift[2]);
  and and_117 (Bit16_Result[12], ~Bit4_Shift[3], and_115_out);  // AND_Gate
  and and_118 (and_118_out, and_115_out, Bit4_Shift[3]);
  and and_119 (and_119_out, ~Bit4_Shift[0], Bit16_Data[13]);  // AND_Gate
  and and_120 (and_120_out, Bit16_Data[13], Bit4_Shift[0]);
  or or_62 (or_62_out, and_119_out, and_128_out);
  and and_121 (and_121_out, ~Bit4_Shift[1], or_62_out);  // AND_Gate
  and and_122 (and_122_out, or_62_out, Bit4_Shift[1]);
  or or_63 (or_63_out, and_121_out, and_138_out);
  and and_123 (and_123_out, ~Bit4_Shift[2], or_63_out);  // AND_Gate
  and and_124 (and_124_out, or_63_out, Bit4_Shift[2]);
  and and_125 (Bit16_Result[13], ~Bit4_Shift[3], and_123_out);  // AND_Gate
  and and_126 (and_126_out, and_123_out, Bit4_Shift[3]);
  and and_127 (and_127_out, ~Bit4_Shift[0], Bit16_Data[14]);  // AND_Gate
  and and_128 (and_128_out, Bit16_Data[14], Bit4_Shift[0]);
  or or_64 (or_64_out, and_127_out, and_136_out);
  and and_129 (and_129_out, ~Bit4_Shift[1], or_64_out);  // AND_Gate
  and and_130 (and_130_out, or_64_out, Bit4_Shift[1]);
  and and_131 (and_131_out, ~Bit4_Shift[2], and_129_out);  // AND_Gate
  and and_132 (and_132_out, and_129_out, Bit4_Shift[2]);
  and and_133 (Bit16_Result[14], ~Bit4_Shift[3], and_131_out);  // AND_Gate
  and and_134 (and_134_out, and_131_out, Bit4_Shift[3]);
  and and_135 (and_135_out, ~Bit4_Shift[0], Bit16_Data[15]);  // AND_Gate
  and and_136 (and_136_out, Bit16_Data[15], Bit4_Shift[0]);
  and and_137 (and_137_out, ~Bit4_Shift[1], and_135_out);  // AND_Gate
  and and_138 (and_138_out, and_135_out, Bit4_Shift[1]);
  and and_139 (and_139_out, ~Bit4_Shift[2], and_137_out);  // AND_Gate
  and and_140 (and_140_out, and_137_out, Bit4_Shift[2]);
  and and_141 (Bit16_Result[15], ~Bit4_Shift[3], and_139_out);  // AND_Gate
  and and_142 (and_142_out, and_139_out, Bit4_Shift[3]);

  assign Bit24_Result[23:8] = Bit16_Result;
endmodule

module Bit16T24O16_Adder (
  input  FP_Op,
  input  Carry_In,
  input  [15:0] Bit16_A,
  input  [15:0] Bit16_B,
  output [15:0] Bit16_Result,
  output Carry_Out
);

  wire and_1_out, and_2_out, and_3_out, and_4_out, and_5_out, and_6_out, and_7_out, and_8_out, and_9_out,
       and_10_out, and_11_out, and_12_out, and_13_out, and_14_out, and_15_out, and_16_out, and_17_out,
       bit4_cla_logic_1_c2, bit4_cla_logic_1_c3, bit4_cla_logic_1_c4, bit4_cla_logic_1_cout,
       bit4_cla_logic_1_pg, bit4_cla_logic_2_c2, bit4_cla_logic_2_c3, bit4_cla_logic_2_c4,
       bit4_cla_logic_2_cout, bit4_cla_logic_2_pg, bit4_cla_logic_3_c2, bit4_cla_logic_3_c3,
       bit4_cla_logic_3_c4, bit4_cla_logic_3_cout, bit4_cla_logic_3_pg, bit4_cla_logic_4_c2,
       bit4_cla_logic_4_c3, bit4_cla_logic_4_c4, bit4_cla_logic_4_cout, bit4_cla_logic_4_pg,
       bit4_cla_logic_5_c2, bit4_cla_logic_5_c3, bit4_cla_logic_5_c4, bit4_cla_logic_5_cout, xor_1_out,
       xor_2_out, xor_3_out, xor_4_out, xor_5_out, xor_6_out, xor_7_out, xor_8_out, xor_9_out, xor_10_out,
       xor_11_out, xor_12_out, xor_13_out, xor_14_out, xor_15_out, xor_16_out;

  xor xor_1 (xor_1_out, Bit16_A[0], Bit16_B[0]);
  and and_1 (and_1_out, Bit16_B[0], Bit16_A[0]);
  xor xor_2 (xor_2_out, Bit16_A[1], Bit16_B[1]);
  and and_2 (and_2_out, Bit16_B[1], Bit16_A[1]);
  xor xor_3 (xor_3_out, Bit16_A[2], Bit16_B[2]);
  and and_3 (and_3_out, Bit16_B[2], Bit16_A[2]);
  xor xor_4 (xor_4_out, Bit16_A[3], Bit16_B[3]);
  and and_4 (and_4_out, Bit16_B[3], Bit16_A[3]);
  xor xor_5 (xor_5_out, Bit16_A[4], Bit16_B[4]);
  and and_5 (and_5_out, Bit16_B[4], Bit16_A[4]);
  xor xor_6 (xor_6_out, Bit16_A[5], Bit16_B[5]);
  and and_6 (and_6_out, Bit16_B[5], Bit16_A[5]);
  xor xor_7 (xor_7_out, Bit16_A[6], Bit16_B[6]);
  and and_7 (and_7_out, Bit16_B[6], Bit16_A[6]);
  xor xor_8 (xor_8_out, Bit16_A[7], Bit16_B[7]);
  and and_8 (and_8_out, Bit16_B[7], Bit16_A[7]);
  xor xor_9 (xor_9_out, Bit16_A[8], Bit16_B[8]);
  and and_9 (and_9_out, Bit16_B[8], Bit16_A[8]);
  xor xor_10 (xor_10_out, Bit16_A[9], Bit16_B[9]);
  and and_10 (and_10_out, Bit16_B[9], Bit16_A[9]);
  xor xor_11 (xor_11_out, Bit16_A[10], Bit16_B[10]);
  and and_11 (and_11_out, Bit16_B[10], Bit16_A[10]);
  xor xor_12 (xor_12_out, Bit16_A[11], Bit16_B[11]);
  and and_12 (and_12_out, Bit16_B[11], Bit16_A[11]);
  xor xor_13 (xor_13_out, Bit16_A[12], Bit16_B[12]);
  and and_13 (and_13_out, Bit16_B[12], Bit16_A[12]);
  xor xor_14 (xor_14_out, Bit16_A[13], Bit16_B[13]);
  and and_14 (and_14_out, Bit16_B[13], Bit16_A[13]);
  xor xor_15 (xor_15_out, Bit16_A[14], Bit16_B[14]);
  and and_15 (and_15_out, Bit16_B[14], Bit16_A[14]);
  xor xor_16 (xor_16_out, Bit16_A[15], Bit16_B[15]);
  and and_16 (and_16_out, Bit16_B[15], Bit16_A[15]);
  xor xor_17 (Bit16_Result[0], Carry_In, xor_1_out);
  xor xor_18 (Bit16_Result[1], bit4_cla_logic_1_c2, xor_2_out);
  xor xor_19 (Bit16_Result[2], bit4_cla_logic_1_c3, xor_3_out);
  xor xor_20 (Bit16_Result[3], bit4_cla_logic_1_c4, xor_4_out);
  xor xor_21 (Bit16_Result[4], bit4_cla_logic_5_c2, xor_5_out);
  xor xor_22 (Bit16_Result[5], bit4_cla_logic_2_c2, xor_6_out);
  xor xor_23 (Bit16_Result[6], bit4_cla_logic_2_c3, xor_7_out);
  xor xor_24 (Bit16_Result[7], bit4_cla_logic_2_c4, xor_8_out);
  xor xor_25 (Bit16_Result[8], bit4_cla_logic_5_c3, xor_9_out);
  xor xor_26 (Bit16_Result[9], bit4_cla_logic_3_c2, xor_10_out);
  xor xor_27 (Bit16_Result[10], bit4_cla_logic_3_c3, xor_11_out);
  xor xor_28 (Bit16_Result[11], bit4_cla_logic_3_c4, xor_12_out);
  xor xor_29 (Bit16_Result[12], bit4_cla_logic_5_c4, xor_13_out);
  xor xor_30 (Bit16_Result[13], bit4_cla_logic_4_c2, xor_14_out);
  xor xor_31 (Bit16_Result[14], bit4_cla_logic_4_c3, xor_15_out);
  xor xor_32 (Bit16_Result[15], bit4_cla_logic_4_c4, xor_16_out);
  Bit4_CLA_Logic bit4_cla_logic_1 (
    .Cin(Carry_In), .P1(xor_1_out), .G1(and_1_out), .P2(xor_2_out), .G2(and_2_out), .P3(xor_3_out),
    .G3(and_3_out), .P4(xor_4_out), .G4(and_4_out), .C2(bit4_cla_logic_1_c2), .C3(bit4_cla_logic_1_c3),
    .C4(bit4_cla_logic_1_c4), .COUT(bit4_cla_logic_1_cout), .PG(bit4_cla_logic_1_pg));
  Bit4_CLA_Logic bit4_cla_logic_2 (
    .Cin(bit4_cla_logic_5_c2), .P1(xor_5_out), .G1(and_5_out), .P2(xor_6_out), .G2(and_6_out),
    .P3(xor_7_out), .G3(and_7_out), .P4(xor_8_out), .G4(and_8_out), .C2(bit4_cla_logic_2_c2),
    .C3(bit4_cla_logic_2_c3), .C4(bit4_cla_logic_2_c4), .COUT(bit4_cla_logic_2_cout), .PG(bit4_cla_logic_2_pg));
  Bit4_CLA_Logic bit4_cla_logic_3 (
    .Cin(bit4_cla_logic_5_c3), .P1(xor_9_out), .G1(and_9_out), .P2(xor_10_out), .G2(and_10_out),
    .P3(xor_11_out), .G3(and_11_out), .P4(xor_12_out), .G4(and_12_out), .C2(bit4_cla_logic_3_c2),
    .C3(bit4_cla_logic_3_c3), .C4(bit4_cla_logic_3_c4), .COUT(bit4_cla_logic_3_cout), .PG(bit4_cla_logic_3_pg));
  Bit4_CLA_Logic bit4_cla_logic_4 (
    .Cin(bit4_cla_logic_5_c4), .P1(xor_13_out), .G1(and_13_out), .P2(xor_14_out), .G2(and_14_out),
    .P3(xor_15_out), .G3(and_15_out), .P4(xor_16_out), .G4(and_16_out), .C2(bit4_cla_logic_4_c2),
    .C3(bit4_cla_logic_4_c3), .C4(bit4_cla_logic_4_c4), .COUT(bit4_cla_logic_4_cout), .PG(bit4_cla_logic_4_pg));
  Bit4_CLA_Logic bit4_cla_logic_5 (
    .Cin(Carry_In), .P1(bit4_cla_logic_1_pg), .G1(bit4_cla_logic_1_cout), .P2(bit4_cla_logic_2_pg),
    .G2(bit4_cla_logic_2_cout), .P3(bit4_cla_logic_3_pg), .G3(bit4_cla_logic_3_cout),
    .P4(bit4_cla_logic_4_pg), .G4(bit4_cla_logic_4_cout), .C2(bit4_cla_logic_5_c2), .C3(bit4_cla_logic_5_c3),
    .C4(bit4_cla_logic_5_c4), .COUT(bit4_cla_logic_5_cout));  // open: PG
  and and_17 (and_17_out, Bit16_Result[11], FP_Op);
  or or_1 (Carry_Out, bit4_cla_logic_5_cout, and_17_out);
endmodule

module Bit8_CLA_Logic (
  input  C_In,
  input  P0,
  input  G0,
  input  P1,
  input  G1,
  input  P2,
  input  G2,
  input  P3,
  input  G3,
  input  P4,
  input  G4,
  input  P5,
  input  G5,
  input  P6,
  input  G6,
  input  P7,
  input  G7,
  output C1,
  output C2,
  output C3,
  output C4,
  output C5,
  output C6,
  output C7,
  output C_OUT,
  output PG
);

  wire and_1_out, and_2_out, and_3_out, and_4_out, and_5_out, and_6_out, and_7_out, and_8_out, and_9_out,
       and_10_out, and_11_out, and_12_out, and_13_out, and_14_out, and_15_out, and_16_out, and_17_out,
       and_18_out, and_19_out, and_20_out, and_21_out, and_22_out, and_23_out, and_24_out, and_25_out,
       and_26_out, and_27_out, and_28_out, and_29_out, and_30_out, and_31_out, and_32_out, and_33_out,
       and_34_out, and_35_out, and_36_out;

  and and_1 (and_1_out, C_In, P0);
  and and_2 (and_2_out, P1, G0);
  and and_3 (and_3_out, P1, P0, C_In);
  and and_4 (and_4_out, G1, P2);
  and and_5 (and_5_out, G0, P1, P2);
  and and_6 (and_6_out, C_In, P0, P1, P2);
  and and_7 (and_7_out, G2, P3);
  and and_8 (and_8_out, G1, P2, P3);
  and and_9 (and_9_out, G0, P1, P2, P3);
  and and_10 (and_10_out, C_In, P0, P1, P2, P3);
  and and_11 (and_11_out, G3, P4);
  and and_12 (and_12_out, G2, P3, P4);
  and and_13 (and_13_out, G1, P2, P3, P4);
  and and_14 (and_14_out, G0, P1, P2, P3, P4);
  and and_15 (and_15_out, C_In, P0, P1, P2, P3, P4);
  and and_16 (and_16_out, G4, P5);
  and and_17 (and_17_out, G3, P4, P5);
  and and_18 (and_18_out, G2, P3, P4, P5);
  and and_19 (and_19_out, G1, P2, P3, P4, P5);
  and and_20 (and_20_out, G0, P1, P2, P3, P4, P5);
  and and_21 (and_21_out, C_In, P0, P1, P2, P3, P4, P5);
  and and_22 (and_22_out, G5, P6);
  and and_23 (and_23_out, G4, P5, P6);
  and and_24 (and_24_out, G3, P4, P5, P6);
  and and_25 (and_25_out, G2, P3, P4, P5, P6);
  and and_26 (and_26_out, G1, P2, P3, P4, P5, P6);
  and and_27 (and_27_out, G0, P1, P2, P3, P4, P5, P6);
  and and_28 (and_28_out, C_In, P0, P1, P2, P3, P4, P5, P6);
  and and_29 (and_29_out, G6, P7);
  and and_30 (and_30_out, G5, P6, P7);
  and and_31 (and_31_out, G4, P5, P6, P7);
  and and_32 (and_32_out, G3, P4, P5, P6, P7);
  and and_33 (and_33_out, G2, P3, P4, P5, P6, P7);
  and and_34 (and_34_out, G1, P2, P3, P4, P5, P6, P7);
  and and_35 (and_35_out, G0, P1, P2, P3, P4, P5, P6, P7);
  and and_36 (and_36_out, C_In, P0, P1, P2, P3, P4, P5, P6, P7);
  and and_37 (PG, P7, P6, P5, P4, P3, P2, P1, P0);
  or or_1 (C1, and_1_out, G0);
  or or_2 (C2, G1, and_2_out, and_3_out);
  or or_3 (C3, G2, and_4_out, and_5_out, and_6_out);
  or or_4 (C4, G3, and_7_out, and_8_out, and_9_out, and_10_out);
  or or_5 (C5, G4, and_11_out, and_12_out, and_13_out, and_14_out, and_15_out);
  or or_6 (C6, G5, and_16_out, and_17_out, and_18_out, and_19_out, and_20_out, and_21_out);
  or or_7 (C7, G6, and_22_out, and_23_out, and_24_out, and_25_out, and_26_out, and_27_out, and_28_out);
  or or_8 (C_OUT, G7, and_29_out, and_30_out, and_31_out, and_32_out, and_33_out, and_34_out, and_35_out, and_36_out);
endmodule

module Bit3_CLA_Logic (
  input  C_In,
  input  P0,
  input  G0,
  input  P1,
  input  G1,
  input  P2,
  input  G2,
  output C1,
  output C2,
  output C_OUT,
  output PG
);

  wire and_1_out, and_2_out, and_3_out, and_4_out, and_5_out, and_6_out;

  and and_1 (and_1_out, C_In, P0);
  and and_2 (and_2_out, P1, G0);
  and and_3 (and_3_out, P1, P0, C_In);
  and and_4 (and_4_out, G1, P2);
  and and_5 (and_5_out, G0, P1, P2);
  and and_6 (and_6_out, C_In, P0, P1, P2);
  and and_7 (PG, P0, P1, P2);
  or or_1 (C1, and_1_out, G0);
  or or_2 (C2, G1, and_2_out, and_3_out);
  or or_3 (C_OUT, G2, and_4_out, and_5_out, and_6_out);
endmodule

module Bit24_Adder (
  input  C_In,
  input  [23:0] Bit24_A,
  input  [23:0] Bit24_B,
  output Bit16_C_OUT,
  output [23:0] Bit24_Result,
  output C_OUT
);

  wire and_1_out, and_2_out, and_3_out, and_4_out, and_5_out, and_6_out, and_7_out, and_8_out, and_9_out,
       and_10_out, and_11_out, and_12_out, and_13_out, and_14_out, and_15_out, and_16_out, and_17_out,
       and_18_out, and_19_out, and_20_out, and_21_out, and_22_out, and_23_out, and_24_out,
       bit3_cla_logic_1_c1, bit8_cla_logic_1_c1, bit8_cla_logic_1_c2, bit8_cla_logic_1_c3,
       bit8_cla_logic_1_c4, bit8_cla_logic_1_c5, bit8_cla_logic_1_c6, bit8_cla_logic_1_c7,
       bit8_cla_logic_1_c_out, bit8_cla_logic_1_pg, bit8_cla_logic_2_c1, bit8_cla_logic_2_c2,
       bit8_cla_logic_2_c3, bit8_cla_logic_2_c4, bit8_cla_logic_2_c5, bit8_cla_logic_2_c6,
       bit8_cla_logic_2_c7, bit8_cla_logic_2_c_out, bit8_cla_logic_2_pg, bit8_cla_logic_3_c1,
       bit8_cla_logic_3_c2, bit8_cla_logic_3_c3, bit8_cla_logic_3_c4, bit8_cla_logic_3_c5,
       bit8_cla_logic_3_c6, bit8_cla_logic_3_c7, bit8_cla_logic_3_c_out, bit8_cla_logic_3_pg, xor_1_out,
       xor_2_out, xor_3_out, xor_4_out, xor_5_out, xor_6_out, xor_7_out, xor_8_out, xor_9_out, xor_10_out,
       xor_11_out, xor_12_out, xor_13_out, xor_14_out, xor_15_out, xor_16_out, xor_17_out, xor_18_out,
       xor_19_out, xor_20_out, xor_21_out, xor_22_out, xor_23_out, xor_24_out;

  xor xor_1 (xor_1_out, Bit24_A[0], Bit24_B[0]);
  and and_1 (and_1_out, Bit24_B[0], Bit24_A[0]);
  xor xor_2 (xor_2_out, Bit24_A[1], Bit24_B[1]);
  and and_2 (and_2_out, Bit24_B[1], Bit24_A[1]);
  xor xor_3 (xor_3_out, Bit24_A[2], Bit24_B[2]);
  and and_3 (and_3_out, Bit24_B[2], Bit24_A[2]);
  xor xor_4 (xor_4_out, Bit24_A[3], Bit24_B[3]);
  and and_4 (and_4_out, Bit24_B[3], Bit24_A[3]);
  xor xor_5 (xor_5_out, Bit24_A[4], Bit24_B[4]);
  and and_5 (and_5_out, Bit24_B[4], Bit24_A[4]);
  xor xor_6 (xor_6_out, Bit24_A[5], Bit24_B[5]);
  and and_6 (and_6_out, Bit24_B[5], Bit24_A[5]);
  xor xor_7 (xor_7_out, Bit24_A[6], Bit24_B[6]);
  and and_7 (and_7_out, Bit24_B[6], Bit24_A[6]);
  xor xor_8 (xor_8_out, Bit24_A[7], Bit24_B[7]);
  and and_8 (and_8_out, Bit24_B[7], Bit24_A[7]);
  xor xor_9 (xor_9_out, Bit24_A[8], Bit24_B[8]);
  and and_9 (and_9_out, Bit24_B[8], Bit24_A[8]);
  xor xor_10 (xor_10_out, Bit24_A[9], Bit24_B[9]);
  and and_10 (and_10_out, Bit24_B[9], Bit24_A[9]);
  xor xor_11 (xor_11_out, Bit24_A[10], Bit24_B[10]);
  and and_11 (and_11_out, Bit24_B[10], Bit24_A[10]);
  xor xor_12 (xor_12_out, Bit24_A[11], Bit24_B[11]);
  and and_12 (and_12_out, Bit24_B[11], Bit24_A[11]);
  xor xor_13 (xor_13_out, Bit24_A[12], Bit24_B[12]);
  and and_13 (and_13_out, Bit24_B[12], Bit24_A[12]);
  xor xor_14 (xor_14_out, Bit24_A[13], Bit24_B[13]);
  and and_14 (and_14_out, Bit24_B[13], Bit24_A[13]);
  xor xor_15 (xor_15_out, Bit24_A[14], Bit24_B[14]);
  and and_15 (and_15_out, Bit24_B[14], Bit24_A[14]);
  xor xor_16 (xor_16_out, Bit24_A[15], Bit24_B[15]);
  and and_16 (and_16_out, Bit24_B[15], Bit24_A[15]);
  xor xor_17 (xor_17_out, Bit24_A[16], Bit24_B[16]);
  and and_17 (and_17_out, Bit24_B[16], Bit24_A[16]);
  xor xor_18 (xor_18_out, Bit24_A[17], Bit24_B[17]);
  and and_18 (and_18_out, Bit24_B[17], Bit24_A[17]);
  xor xor_19 (xor_19_out, Bit24_A[18], Bit24_B[18]);
  and and_19 (and_19_out, Bit24_B[18], Bit24_A[18]);
  xor xor_20 (xor_20_out, Bit24_A[19], Bit24_B[19]);
  and and_20 (and_20_out, Bit24_B[19], Bit24_A[19]);
  xor xor_21 (xor_21_out, Bit24_A[20], Bit24_B[20]);
  and and_21 (and_21_out, Bit24_B[20], Bit24_A[20]);
  xor xor_22 (xor_22_out, Bit24_A[21], Bit24_B[21]);
  and and_22 (and_22_out, Bit24_B[21], Bit24_A[21]);
  xor xor_23 (xor_23_out, Bit24_A[22], Bit24_B[22]);
  and and_23 (and_23_out, Bit24_B[22], Bit24_A[22]);
  xor xor_24 (xor_24_out, Bit24_A[23], Bit24_B[23]);
  and and_24 (and_24_out, Bit24_B[23], Bit24_A[23]);
  xor xor_25 (Bit24_Result[0], C_In, xor_1_out);
  xor xor_26 (Bit24_Result[1], bit8_cla_logic_1_c1, xor_2_out);
  xor xor_27 (Bit24_Result[2], bit8_cla_logic_1_c2, xor_3_out);
  xor xor_28 (Bit24_Result[3], bit8_cla_logic_1_c3, xor_4_out);
  xor xor_29 (Bit24_Result[4], bit8_cla_logic_1_c4, xor_5_out);
  xor xor_30 (Bit24_Result[5], bit8_cla_logic_1_c5, xor_6_out);
  xor xor_31 (Bit24_Result[6], bit8_cla_logic_1_c6, xor_7_out);
  xor xor_32 (Bit24_Result[7], bit8_cla_logic_1_c7, xor_8_out);
  xor xor_33 (Bit24_Result[8], bit3_cla_logic_1_c1, xor_9_out);
  xor xor_34 (Bit24_Result[9], bit8_cla_logic_2_c1, xor_10_out);
  xor xor_35 (Bit24_Result[10], bit8_cla_logic_2_c2, xor_11_out);
  xor xor_36 (Bit24_Result[11], bit8_cla_logic_2_c3, xor_12_out);
  xor xor_37 (Bit24_Result[12], bit8_cla_logic_2_c4, xor_13_out);
  xor xor_38 (Bit24_Result[13], bit8_cla_logic_2_c5, xor_14_out);
  xor xor_39 (Bit24_Result[14], bit8_cla_logic_2_c6, xor_15_out);
  xor xor_40 (Bit24_Result[15], bit8_cla_logic_2_c7, xor_16_out);
  xor xor_41 (Bit24_Result[16], Bit16_C_OUT, xor_17_out);
  xor xor_42 (Bit24_Result[17], bit8_cla_logic_3_c1, xor_18_out);
  xor xor_43 (Bit24_Result[18], bit8_cla_logic_3_c2, xor_19_out);
  xor xor_44 (Bit24_Result[19], bit8_cla_logic_3_c3, xor_20_out);
  xor xor_45 (Bit24_Result[20], bit8_cla_logic_3_c4, xor_21_out);
  xor xor_46 (Bit24_Result[21], bit8_cla_logic_3_c5, xor_22_out);
  xor xor_47 (Bit24_Result[22], bit8_cla_logic_3_c6, xor_23_out);
  xor xor_48 (Bit24_Result[23], bit8_cla_logic_3_c7, xor_24_out);
  Bit8_CLA_Logic bit8_cla_logic_1 (
    .C_In(C_In), .P0(xor_1_out), .G0(and_1_out), .P1(xor_2_out), .G1(and_2_out), .P2(xor_3_out),
    .G2(and_3_out), .P3(xor_4_out), .G3(and_4_out), .P4(xor_5_out), .G4(and_5_out), .P5(xor_6_out),
    .G5(and_6_out), .P6(xor_7_out), .G6(and_7_out), .P7(xor_8_out), .G7(and_8_out), .C1(bit8_cla_logic_1_c1),
    .C2(bit8_cla_logic_1_c2), .C3(bit8_cla_logic_1_c3), .C4(bit8_cla_logic_1_c4), .C5(bit8_cla_logic_1_c5),
    .C6(bit8_cla_logic_1_c6), .C7(bit8_cla_logic_1_c7), .C_OUT(bit8_cla_logic_1_c_out),
    .PG(bit8_cla_logic_1_pg));
  Bit8_CLA_Logic bit8_cla_logic_2 (
    .C_In(bit3_cla_logic_1_c1), .P0(xor_9_out), .G0(and_9_out), .P1(xor_10_out), .G1(and_10_out),
    .P2(xor_11_out), .G2(and_11_out), .P3(xor_12_out), .G3(and_12_out), .P4(xor_13_out), .G4(and_13_out),
    .P5(xor_14_out), .G5(and_14_out), .P6(xor_15_out), .G6(and_15_out), .P7(xor_16_out), .G7(and_16_out),
    .C1(bit8_cla_logic_2_c1), .C2(bit8_cla_logic_2_c2), .C3(bit8_cla_logic_2_c3), .C4(bit8_cla_logic_2_c4),
    .C5(bit8_cla_logic_2_c5), .C6(bit8_cla_logic_2_c6), .C7(bit8_cla_logic_2_c7),
    .C_OUT(bit8_cla_logic_2_c_out), .PG(bit8_cla_logic_2_pg));
  Bit8_CLA_Logic bit8_cla_logic_3 (
    .C_In(Bit16_C_OUT), .P0(xor_17_out), .G0(and_17_out), .P1(xor_18_out), .G1(and_18_out), .P2(xor_19_out),
    .G2(and_19_out), .P3(xor_20_out), .G3(and_20_out), .P4(xor_21_out), .G4(and_21_out), .P5(xor_22_out),
    .G5(and_22_out), .P6(xor_23_out), .G6(and_23_out), .P7(xor_24_out), .G7(and_24_out),
    .C1(bit8_cla_logic_3_c1), .C2(bit8_cla_logic_3_c2), .C3(bit8_cla_logic_3_c3), .C4(bit8_cla_logic_3_c4),
    .C5(bit8_cla_logic_3_c5), .C6(bit8_cla_logic_3_c6), .C7(bit8_cla_logic_3_c7),
    .C_OUT(bit8_cla_logic_3_c_out), .PG(bit8_cla_logic_3_pg));
  Bit3_CLA_Logic bit3_cla_logic_1 (
    .C_In(C_In), .P0(bit8_cla_logic_1_pg), .G0(bit8_cla_logic_1_c_out), .P1(bit8_cla_logic_2_pg),
    .G1(bit8_cla_logic_2_c_out), .P2(bit8_cla_logic_3_pg), .G2(bit8_cla_logic_3_c_out),
    .C1(bit3_cla_logic_1_c1), .C2(Bit16_C_OUT), .C_OUT(C_OUT));  // open: PG
endmodule

module Bit24_To_Bit16 (
  input  [23:0] Bit24,
  output [15:0] Bit16
);


  assign Bit16 = Bit24[23:8];
endmodule

module Bit16_To_Bit24 (
  input  [15:0] Bit16,
  output [23:0] Bit24
);


  assign Bit24 = {{8{1'b0}}, Bit16};
endmodule

module Bit24_Controlled_Buffer (
  input  Enable,
  input  [23:0] Bit24_In,
  output [23:0] Bit24_Out
);

  and and_1 (Bit24_Out[0], Bit24_In[0], Enable);
  and and_2 (Bit24_Out[1], Bit24_In[1], Enable);
  and and_3 (Bit24_Out[2], Bit24_In[2], Enable);
  and and_4 (Bit24_Out[3], Bit24_In[3], Enable);
  and and_5 (Bit24_Out[4], Bit24_In[4], Enable);
  and and_6 (Bit24_Out[5], Bit24_In[5], Enable);
  and and_7 (Bit24_Out[6], Bit24_In[6], Enable);
  and and_8 (Bit24_Out[7], Bit24_In[7], Enable);
  and and_9 (Bit24_Out[8], Bit24_In[8], Enable);
  and and_10 (Bit24_Out[9], Bit24_In[9], Enable);
  and and_11 (Bit24_Out[10], Bit24_In[10], Enable);
  and and_12 (Bit24_Out[11], Bit24_In[11], Enable);
  and and_13 (Bit24_Out[12], Bit24_In[12], Enable);
  and and_14 (Bit24_Out[13], Bit24_In[13], Enable);
  and and_15 (Bit24_Out[14], Bit24_In[14], Enable);
  and and_16 (Bit24_Out[15], Bit24_In[15], Enable);
  and and_17 (Bit24_Out[16], Bit24_In[16], Enable);
  and and_18 (Bit24_Out[17], Bit24_In[17], Enable);
  and and_19 (Bit24_Out[18], Bit24_In[18], Enable);
  and and_20 (Bit24_Out[19], Bit24_In[19], Enable);
  and and_21 (Bit24_Out[20], Bit24_In[20], Enable);
  and and_22 (Bit24_Out[21], Bit24_In[21], Enable);
  and and_23 (Bit24_Out[22], Bit24_In[22], Enable);
  and and_24 (Bit24_Out[23], Bit24_In[23], Enable);
endmodule

module alu2 (
  input  [3:0] Bit5_Opcode,
  input  Signed_Integer_Operation,
  input  [15:0] Bit16_Input_A,
  input  [15:0] Bit16_Input_B,
  input  [15:0] in_5,
  input  [15:0] in_6,
  input  in_7,
  input  [15:0] in_8,
  input  [15:0] in_9,
  input  [15:0] in_10,
  output [15:0] out_11,
  output [15:0] out_12,
  output [15:0] out_13,
  output [15:0] out_14,
  output [15:0] out_15,
  output [15:0] out_16,
  output [15:0] out_17
);

  wire bit16_float_exponent_unit_1_p10, bit16_float_exponent_unit_1_p11, bit16_float_exponent_unit_1_p12,
       bit24_adder_1_c_out, not_1_out, not_2_out, undriven;
  wire [1:0] bit24_adder_1_bit24_result_2;
  wire [3:0] bit16_float_exponent_unit_1_p6;
  wire [4:0] bit16_float_exponent_unit_1_p9;
  wire [13:0] bit16t24_right_shift_2_bit24_result;
  wire [15:0] bit16_float_exponent_unit_1_p5;
  wire [21:0] bit24_adder_1_bit24_result;
  wire [23:0] bit16_float_exponent_unit_1_p7, bit16_float_exponent_unit_1_p8,
       bit16t24_right_shift_1_bit24_result, bit24_controlled_buffer_1_bit24_out,
       bit24_controlled_buffer_2_bit24_out, bit24_controlled_buffer_3_bit24_out,
       bit24_controlled_buffer_4_bit24_out, bit24_twos_complementer_1_bit24_out,
       bit24_twos_complementer_2_bit24_out, or_1_out, or_2_out;
  wire [23:1] undriven_2;

  Demultiplexer #(.select(4)) demultiplexer_1 (
    .in(1'b1), .sel(Bit5_Opcode));  // open: out0, out1, out2, out3, out4, out5, out6, out7, out8, out9, out10, out11, out12, out13, out14, out15
  FPAdder #(.fpwidth(16)) fpadder_1 (.a(in_5), .b(in_6), .out(out_11));
  FPAdder #(.fpwidth(16)) fpadder_2 (.a(in_8), .b(in_9), .out(out_16));
  // fpu3 fpu3_1: pin names not known
  // Bit24_Divider bit24_divider_1: pin names not known
  // Bit16_Multiplier bit16_multiplier_1: pin names not known
  Bit16T24_Right_Shift bit16t24_right_shift_1 (
    .Bit16_Data(bit16_float_exponent_unit_1_p5), .Bit4_Shift(bit16_float_exponent_unit_1_p6),
    .Bit24_Result(bit16t24_right_shift_1_bit24_result));  // open: Bit16_Result, Shift_Overflow_For_Bit16
  // Bit16_Left_Shift bit16_left_shift_1: pin names not known
  // Bit16_Float_Exponent_Unit bit16_float_exponent_unit_1: pin names not known; wires that end beside it: bit16t24_right_shift_1_bit24_result, in_7, in_8, in_9, bit16_float_exponent_unit_1_p5, bit16_float_exponent_unit_1_p6, bit16_float_exponent_unit_1_p7, bit16_float_exponent_unit_1_p8, bit16_float_exponent_unit_1_p9, bit16_float_exponent_unit_1_p10, bit16_float_exponent_unit_1_p11, bit16_float_exponent_unit_1_p12
  not not_1 (not_1_out, bit16_float_exponent_unit_1_p11);
  Bit24_Twos_Complementer bit24_twos_complementer_1 (
    .Bit24_In(bit16_float_exponent_unit_1_p7), .Bit24_Out(bit24_twos_complementer_1_bit24_out));
  not not_2 (not_2_out, bit16_float_exponent_unit_1_p12);
  Bit24_Twos_Complementer bit24_twos_complementer_2 (
    .Bit24_In(bit16_float_exponent_unit_1_p8), .Bit24_Out(bit24_twos_complementer_2_bit24_out));
  Bit24_Controlled_Buffer bit24_controlled_buffer_1 (
    .Enable(not_1_out), .Bit24_In(bit16_float_exponent_unit_1_p7),
    .Bit24_Out(bit24_controlled_buffer_1_bit24_out));
  Bit24_Controlled_Buffer bit24_controlled_buffer_2 (
    .Enable(bit16_float_exponent_unit_1_p11), .Bit24_In(bit24_twos_complementer_1_bit24_out),
    .Bit24_Out(bit24_controlled_buffer_2_bit24_out));
  Bit24_Controlled_Buffer bit24_controlled_buffer_3 (
    .Enable(not_2_out), .Bit24_In(bit16_float_exponent_unit_1_p8),
    .Bit24_Out(bit24_controlled_buffer_3_bit24_out));
  Bit24_Controlled_Buffer bit24_controlled_buffer_4 (
    .Enable(bit16_float_exponent_unit_1_p12), .Bit24_In(bit24_twos_complementer_2_bit24_out),
    .Bit24_Out(bit24_controlled_buffer_4_bit24_out));
  assign or_1_out = bit24_controlled_buffer_1_bit24_out | bit24_controlled_buffer_2_bit24_out;  // OR_Gate or_1, 24 bits wide
  assign or_2_out = bit24_controlled_buffer_3_bit24_out | bit24_controlled_buffer_4_bit24_out;  // OR_Gate or_2, 24 bits wide
  Bit24_Adder bit24_adder_1 (
    .Bit24_A(or_1_out), .Bit24_B(or_2_out),
    .Bit24_Result({bit24_adder_1_bit24_result_2[0], bit24_adder_1_bit24_result_2[1], bit24_adder_1_bit24_result}),
    .C_OUT(bit24_adder_1_c_out));  // open: C_In, Bit16_C_OUT
  Priority_Encoder #(.select(5)) priority_encoder_1 (
    .in0(undriven_2[1]), .in1(undriven_2[2]), .in2(undriven_2[3]), .in3(undriven_2[4]), .in4(undriven_2[5]),
    .in5(undriven_2[6]), .in6(undriven_2[7]), .in7(undriven_2[8]), .in8(undriven_2[9]), .in9(undriven_2[10]),
    .in10(undriven_2[11]), .in11(undriven_2[12]), .in12(undriven_2[13]), .in13(undriven_2[14]),
    .in14(undriven_2[15]), .in15(undriven_2[16]), .in16(undriven_2[17]), .in17(undriven_2[18]),
    .in18(undriven_2[19]), .in19(undriven_2[20]), .in20(undriven_2[21]), .in21(undriven_2[22]),
    .in22(undriven_2[23]));  // open: in23, in24, in25, in26, in27, in28, in29, in30, in31, out, gs, en_out, en_in
  Bit5_Adder bit5_adder_1 (
    .Cin(undriven), .Bit5_A(bit16_float_exponent_unit_1_p9), .Bit5_B({3'b000, bit24_adder_1_bit24_result_2}),
    .Bit5_Result(out_12[14:10]));  // open: Cout
  Bit16T24_Right_Shift bit16t24_right_shift_2 (
    .Bit16_Data(bit24_adder_1_bit24_result[21:6]), .Bit4_Shift({3'b000, bit24_adder_1_bit24_result_2[0]}),
    .Bit24_Result({out_12[9:0], bit16t24_right_shift_2_bit24_result}));  // open: Bit16_Result, Shift_Overflow_For_Bit16

  assign out_12[15] = 1'b0;
  assign out_13 = {1'b0, out_12[14:0]};
  assign out_14 = in_9;
  assign out_15 = in_10;
  assign out_17 = out_16;
endmodule
module Bit24_Twos_Complementer (
  input  [23:0] Bit24_In,
  output [23:0] Bit24_Out
);

  wire or_1_out, or_2_out, or_3_out, or_4_out, or_5_out, or_6_out, or_7_out, or_8_out, or_9_out, or_10_out,
       or_11_out, or_12_out, or_13_out, or_14_out, or_15_out, or_16_out, or_17_out, or_18_out, or_19_out,
       or_20_out, or_21_out, or_22_out;

  or or_1 (or_1_out, Bit24_In[0], Bit24_Out[1]);
  or or_2 (or_2_out, Bit24_In[0], Bit24_Out[1], Bit24_Out[2]);
  or or_3 (or_3_out, Bit24_In[0], Bit24_Out[1], Bit24_Out[2], Bit24_Out[3]);
  or or_4 (or_4_out, Bit24_In[0], Bit24_Out[1], Bit24_Out[2], Bit24_Out[3], Bit24_Out[4]);
  or or_5 (or_5_out, Bit24_In[0], Bit24_Out[1], Bit24_Out[2], Bit24_Out[3], Bit24_Out[4], Bit24_Out[5]);
  or or_6 (or_6_out, Bit24_In[0], Bit24_Out[1], Bit24_Out[2], Bit24_Out[3], Bit24_Out[4], Bit24_Out[5], Bit24_Out[6]);
  or or_7 (or_7_out, Bit24_In[0], Bit24_Out[1], Bit24_Out[2], Bit24_Out[3], Bit24_Out[4], Bit24_Out[5], Bit24_Out[6], Bit24_Out[7]);
  or or_8 (or_8_out, Bit24_In[0], Bit24_Out[1], Bit24_Out[2], Bit24_Out[3], Bit24_Out[4], Bit24_Out[5], Bit24_Out[6], Bit24_Out[7], Bit24_Out[8]);
  or or_9 (or_9_out, Bit24_In[0], Bit24_Out[1], Bit24_Out[2], Bit24_Out[3], Bit24_Out[4], Bit24_Out[5], Bit24_Out[6], Bit24_Out[7], Bit24_Out[8], Bit24_Out[9]);
  or or_10 (or_10_out, Bit24_In[0], Bit24_Out[1], Bit24_Out[2], Bit24_Out[3], Bit24_Out[4], Bit24_Out[5], Bit24_Out[6], Bit24_Out[7], Bit24_Out[8], Bit24_Out[9], Bit24_Out[10]);
  or or_11 (or_11_out, Bit24_In[0], Bit24_Out[1], Bit24_Out[2], Bit24_Out[3], Bit24_Out[4], Bit24_Out[5], Bit24_Out[6], Bit24_Out[7], Bit24_Out[8], Bit24_Out[9], Bit24_Out[10], Bit24_Out[11]);
  or or_12 (or_12_out, Bit24_In[0], Bit24_Out[1], Bit24_Out[2], Bit24_Out[3], Bit24_Out[4], Bit24_Out[5], Bit24_Out[6], Bit24_Out[7], Bit24_Out[8], Bit24_Out[9], Bit24_Out[10], Bit24_Out[11], Bit24_Out[12]);
  or or_13 (or_13_out, Bit24_In[0], Bit24_Out[1], Bit24_Out[2], Bit24_Out[3], Bit24_Out[4], Bit24_Out[5], Bit24_Out[6], Bit24_Out[7], Bit24_Out[8], Bit24_Out[9], Bit24_Out[10], Bit24_Out[11], Bit24_Out[12], Bit24_Out[13]);
  or or_14 (or_14_out, Bit24_In[0], Bit24_Out[1], Bit24_Out[2], Bit24_Out[3], Bit24_Out[4], Bit24_Out[5], Bit24_Out[6], Bit24_Out[7], Bit24_Out[8], Bit24_Out[9], Bit24_Out[10], Bit24_Out[11], Bit24_Out[12], Bit24_Out[13], Bit24_Out[14]);
  or or_15 (or_15_out, Bit24_In[0], Bit24_Out[1], Bit24_Out[2], Bit24_Out[3], Bit24_Out[4], Bit24_Out[5], Bit24_Out[6], Bit24_Out[7], Bit24_Out[8], Bit24_Out[9], Bit24_Out[10], Bit24_Out[11], Bit24_Out[12], Bit24_Out[13], Bit24_Out[14], Bit24_Out[15]);
  or or_16 (or_16_out, Bit24_In[0], Bit24_Out[1], Bit24_Out[2], Bit24_Out[3], Bit24_Out[4], Bit24_Out[5], Bit24_Out[6], Bit24_Out[7], Bit24_Out[8], Bit24_Out[9], Bit24_Out[10], Bit24_Out[11], Bit24_Out[12], Bit24_Out[13], Bit24_Out[14], Bit24_Out[15], Bit24_Out[16]);
  or or_17 (or_17_out, Bit24_In[0], Bit24_Out[1], Bit24_Out[2], Bit24_Out[3], Bit24_Out[4], Bit24_Out[5], Bit24_Out[6], Bit24_Out[7], Bit24_Out[8], Bit24_Out[9], Bit24_Out[10], Bit24_Out[11], Bit24_Out[12], Bit24_Out[13], Bit24_Out[14], Bit24_Out[15], Bit24_Out[16], Bit24_Out[17]);
  or or_18 (or_18_out, Bit24_In[0], Bit24_Out[1], Bit24_Out[2], Bit24_Out[3], Bit24_Out[4], Bit24_Out[5], Bit24_Out[6], Bit24_Out[7], Bit24_Out[8], Bit24_Out[9], Bit24_Out[10], Bit24_Out[11], Bit24_Out[12], Bit24_Out[13], Bit24_Out[14], Bit24_Out[15], Bit24_Out[16], Bit24_Out[17], Bit24_Out[18]);
  or or_19 (or_19_out, Bit24_In[0], Bit24_Out[1], Bit24_Out[2], Bit24_Out[3], Bit24_Out[4], Bit24_Out[5], Bit24_Out[6], Bit24_Out[7], Bit24_Out[8], Bit24_Out[9], Bit24_Out[10], Bit24_Out[11], Bit24_Out[12], Bit24_Out[13], Bit24_Out[14], Bit24_Out[15], Bit24_Out[16], Bit24_Out[17], Bit24_Out[18], Bit24_Out[19]);
  or or_20 (or_20_out, Bit24_In[0], Bit24_Out[1], Bit24_Out[2], Bit24_Out[3], Bit24_Out[4], Bit24_Out[5], Bit24_Out[6], Bit24_Out[7], Bit24_Out[8], Bit24_Out[9], Bit24_Out[10], Bit24_Out[11], Bit24_Out[12], Bit24_Out[13], Bit24_Out[14], Bit24_Out[15], Bit24_Out[16], Bit24_Out[17], Bit24_Out[18], Bit24_Out[19], Bit24_Out[20]);
  or or_21 (or_21_out, Bit24_In[0], Bit24_Out[1], Bit24_Out[2], Bit24_Out[3], Bit24_Out[4], Bit24_Out[5], Bit24_Out[6], Bit24_Out[7], Bit24_Out[8], Bit24_Out[9], Bit24_Out[10], Bit24_Out[11], Bit24_Out[12], Bit24_Out[13], Bit24_Out[14], Bit24_Out[15], Bit24_Out[16], Bit24_Out[17], Bit24_Out[18], Bit24_Out[19], Bit24_Out[20], Bit24_Out[21]);
  or or_22 (or_22_out, Bit24_In[0], Bit24_Out[1], Bit24_Out[2], Bit24_Out[3], Bit24_Out[4], Bit24_Out[5], Bit24_Out[6], Bit24_Out[7], Bit24_Out[8], Bit24_Out[9], Bit24_Out[10], Bit24_Out[11], Bit24_Out[12], Bit24_Out[13], Bit24_Out[14], Bit24_Out[15], Bit24_Out[16], Bit24_Out[17], Bit24_Out[18], Bit24_Out[19], Bit24_Out[20], Bit24_Out[21], Bit24_Out[22]);
  xor xor_1 (Bit24_Out[1], Bit24_In[1], Bit24_In[0]);
  xor xor_2 (Bit24_Out[2], Bit24_In[2], or_1_out);
  xor xor_3 (Bit24_Out[3], Bit24_In[3], or_2_out);
  xor xor_4 (Bit24_Out[4], Bit24_In[4], or_3_out);
  xor xor_5 (Bit24_Out[5], Bit24_In[5], or_4_out);
  xor xor_6 (Bit24_Out[6], Bit24_In[6], or_5_out);
  xor xor_7 (Bit24_Out[7], Bit24_In[7], or_6_out);
  xor xor_8 (Bit24_Out[8], Bit24_In[8], or_7_out);
  xor xor_9 (Bit24_Out[9], Bit24_In[9], or_8_out);
  xor xor_10 (Bit24_Out[10], Bit24_In[10], or_9_out);
  xor xor_11 (Bit24_Out[11], Bit24_In[11], or_10_out);
  xor xor_12 (Bit24_Out[12], Bit24_In[12], or_11_out);
  xor xor_13 (Bit24_Out[13], Bit24_In[13], or_12_out);
  xor xor_14 (Bit24_Out[14], Bit24_In[14], or_13_out);
  xor xor_15 (Bit24_Out[15], Bit24_In[15], or_14_out);
  xor xor_16 (Bit24_Out[16], Bit24_In[16], or_15_out);
  xor xor_17 (Bit24_Out[17], Bit24_In[17], or_16_out);
  xor xor_18 (Bit24_Out[18], Bit24_In[18], or_17_out);
  xor xor_19 (Bit24_Out[19], Bit24_In[19], or_18_out);
  xor xor_20 (Bit24_Out[20], Bit24_In[20], or_19_out);
  xor xor_21 (Bit24_Out[21], Bit24_In[21], or_20_out);
  xor xor_22 (Bit24_Out[22], Bit24_In[22], or_21_out);
  xor xor_23 (Bit24_Out[23], Bit24_In[23], or_22_out);

  assign Bit24_Out[0] = Bit24_In[0];
endmodule

module Bit24_Divider (
  input  Clock,
  input  [23:0] Bit24_Dividend,
  input  [23:0] Bit24_Divisor,
  input  Int_Div,
  input  FLOAT_Div,
  input  Bit16_C_Out_Adder,
  input  [23:0] Bit24_Result,
  input  C_Out_Adder,
  output Divider_Running,
  output [23:0] Bit24_Remainder,
  output [23:0] Bit24_Quotient,
  output [23:0] Bit24_Adder_A,
  output [23:0] Bit24_Adder_B
);

  wire and_1_out, and_2_out, and_3_out, and_4_out, and_5_out, and_6_out, and_8_out, and_9_out, and_10_out,
       and_11_out, and_12_out, and_13_out, and_14_out, and_15_out, and_16_out, and_17_out, and_18_out,
       and_19_out, and_20_out, and_21_out, and_22_out, and_23_out, and_24_out, and_25_out, and_26_out,
       and_27_out, and_28_out, and_29_out, and_30_out, and_31_out, d_ff_1_q, d_ff_2_qn, d_ff_3_qn, d_ff_4_qn,
       d_ff_5_qn, d_ff_6_qn, d_ff_7_q, demultiplexer_1_out1, demultiplexer_1_out2, demultiplexer_1_out3,
       demultiplexer_1_out4, demultiplexer_1_out5, demultiplexer_1_out6, demultiplexer_1_out7,
       demultiplexer_1_out8, demultiplexer_1_out9, demultiplexer_1_out10, demultiplexer_1_out11,
       demultiplexer_1_out12, demultiplexer_1_out13, demultiplexer_1_out14, demultiplexer_1_out15,
       demultiplexer_1_out16, demultiplexer_1_out17, demultiplexer_1_out18, demultiplexer_1_out19,
       demultiplexer_1_out20, demultiplexer_1_out21, demultiplexer_1_out22, demultiplexer_1_out23,
       demultiplexer_1_out24, demultiplexer_2_out0, demultiplexer_2_out1, demultiplexer_2_out2,
       demultiplexer_2_out3, demultiplexer_2_out4, demultiplexer_2_out5, demultiplexer_2_out6,
       demultiplexer_2_out7, demultiplexer_2_out8, demultiplexer_2_out9, demultiplexer_2_out10,
       demultiplexer_2_out11, demultiplexer_2_out12, demultiplexer_2_out13, demultiplexer_2_out14,
       demultiplexer_2_out15, demultiplexer_2_out16, demultiplexer_2_out17, demultiplexer_2_out18,
       demultiplexer_2_out19, demultiplexer_2_out20, demultiplexer_2_out21, demultiplexer_2_out22,
       demultiplexer_2_out23, nor_1_out, not_1_out, or_1_out, or_2_out;
  wire [0:0] or_4_out;
  wire [4:0] d_ff_2_q;
  wire [23:0] bit24_controlled_buffer_1_bit24_out, bit24_controlled_buffer_2_bit24_out, or_3_out;

  D_Flip_Flop d_ff_1 (.D(nor_1_out), .clk(Clock), .Q(d_ff_1_q));  // open: Qn, preset, reset
  and and_1 (and_1_out, Int_Div, d_ff_1_q);
  nor nor_1 (nor_1_out, d_ff_2_q[0], d_ff_2_q[1], d_ff_2_q[2], d_ff_2_q[3], d_ff_2_q[4]);
  D_Flip_Flop #(.trigger("falling")) d_ff_2 (
    .D(d_ff_2_qn), .clk(and_2_out), .Q(d_ff_2_q[0]), .Qn(d_ff_2_qn), .reset(and_6_out));  // open: preset
  and and_2 (and_2_out, Clock, or_1_out);
  D_Flip_Flop #(.trigger("falling")) d_ff_3 (
    .D(d_ff_3_qn), .clk(d_ff_2_q[0]), .Q(d_ff_2_q[1]), .Qn(d_ff_3_qn), .reset(and_6_out));  // open: preset
  Bit24_Inverter bit24_inverter_1 (.Bit24_In(Bit24_Divisor), .Bit24_Out(Bit24_Adder_B));
  or or_1 (or_1_out, Int_Div, FLOAT_Div);
  D_Flip_Flop #(.trigger("falling")) d_ff_4 (
    .D(d_ff_4_qn), .clk(d_ff_2_q[1]), .Q(d_ff_2_q[2]), .Qn(d_ff_4_qn), .reset(and_6_out));  // open: preset
  D_Flip_Flop #(.trigger("falling")) d_ff_5 (
    .D(d_ff_5_qn), .clk(d_ff_2_q[2]), .Q(d_ff_2_q[3]), .Qn(d_ff_5_qn), .preset(and_1_out), .reset(and_6_out));
  D_Flip_Flop #(.trigger("falling")) d_ff_6 (
    .D(d_ff_6_qn), .clk(d_ff_2_q[3]), .Q(d_ff_2_q[4]), .Qn(d_ff_6_qn), .reset(and_6_out));  // open: preset
  Register #(.trigger("falling"), .width(24)) register_1 (
    .D({or_3_out[22:0], or_4_out[0]}), .en(or_1_out), .clk(and_2_out), .Q(Bit24_Adder_A), .clr(and_6_out));
  and and_3 (and_3_out, Int_Div, Bit16_C_Out_Adder);
  not not_1 (not_1_out, or_2_out);
  or or_2 (or_2_out, and_3_out, and_4_out);
  and and_4 (and_4_out, FLOAT_Div, C_Out_Adder);
  D_Flip_Flop #(.trigger("falling")) d_ff_7 (.D(and_5_out), .clk(and_2_out), .Q(d_ff_7_q));  // open: Qn, preset, reset
  and and_5 (and_5_out, d_ff_2_q[0], ~d_ff_2_q[1], ~d_ff_2_q[2], d_ff_2_q[3], d_ff_2_q[4], or_1_out);  // AND_Gate
  and and_6 (and_6_out, d_ff_7_q, and_2_out);
  Demultiplexer #(.select(5)) demultiplexer_1 (
    .out1(demultiplexer_1_out1), .out2(demultiplexer_1_out2), .out3(demultiplexer_1_out3),
    .out4(demultiplexer_1_out4), .out5(demultiplexer_1_out5), .out6(demultiplexer_1_out6),
    .out7(demultiplexer_1_out7), .out8(demultiplexer_1_out8), .out9(demultiplexer_1_out9),
    .out10(demultiplexer_1_out10), .out11(demultiplexer_1_out11), .out12(demultiplexer_1_out12),
    .out13(demultiplexer_1_out13), .out14(demultiplexer_1_out14), .out15(demultiplexer_1_out15),
    .out16(demultiplexer_1_out16), .out17(demultiplexer_1_out17), .out18(demultiplexer_1_out18),
    .out19(demultiplexer_1_out19), .out20(demultiplexer_1_out20), .out21(demultiplexer_1_out21),
    .out22(demultiplexer_1_out22), .out23(demultiplexer_1_out23), .out24(demultiplexer_1_out24),
    .in(or_2_out), .sel(d_ff_2_q));  // open: out0, out25, out26, out27, out28, out29, out30, out31
  Bit24_Controlled_Buffer bit24_controlled_buffer_1 (
    .Enable(not_1_out), .Bit24_In(Bit24_Adder_A), .Bit24_Out(bit24_controlled_buffer_1_bit24_out));
  Bit24_Controlled_Buffer bit24_controlled_buffer_2 (
    .Enable(or_2_out), .Bit24_In(Bit24_Result), .Bit24_Out(bit24_controlled_buffer_2_bit24_out));
  S_R_Flip_Flop s_r_ff_1 (
    .S(demultiplexer_1_out24), .R(and_6_out), .clk(and_2_out), .Q(Bit24_Quotient[0]), .reset(and_6_out));  // open: Qn, preset
  and and_7 (Divider_Running, ~and_5_out, or_1_out);  // AND_Gate
  assign or_3_out = bit24_controlled_buffer_1_bit24_out | bit24_controlled_buffer_2_bit24_out;  // OR_Gate or_3, 24 bits wide
  S_R_Flip_Flop s_r_ff_2 (
    .S(demultiplexer_1_out23), .R(and_6_out), .clk(and_2_out), .Q(Bit24_Quotient[1]), .reset(and_6_out));  // open: Qn, preset
  S_R_Flip_Flop s_r_ff_3 (
    .S(demultiplexer_1_out22), .R(and_6_out), .clk(and_2_out), .Q(Bit24_Quotient[2]), .reset(and_6_out));  // open: Qn, preset
  S_R_Flip_Flop s_r_ff_4 (
    .S(demultiplexer_1_out21), .R(and_6_out), .clk(and_2_out), .Q(Bit24_Quotient[3]), .reset(and_6_out));  // open: Qn, preset
  Demultiplexer #(.select(5)) demultiplexer_2 (
    .out0(demultiplexer_2_out0), .out1(demultiplexer_2_out1), .out2(demultiplexer_2_out2),
    .out3(demultiplexer_2_out3), .out4(demultiplexer_2_out4), .out5(demultiplexer_2_out5),
    .out6(demultiplexer_2_out6), .out7(demultiplexer_2_out7), .out8(demultiplexer_2_out8),
    .out9(demultiplexer_2_out9), .out10(demultiplexer_2_out10), .out11(demultiplexer_2_out11),
    .out12(demultiplexer_2_out12), .out13(demultiplexer_2_out13), .out14(demultiplexer_2_out14),
    .out15(demultiplexer_2_out15), .out16(demultiplexer_2_out16), .out17(demultiplexer_2_out17),
    .out18(demultiplexer_2_out18), .out19(demultiplexer_2_out19), .out20(demultiplexer_2_out20),
    .out21(demultiplexer_2_out21), .out22(demultiplexer_2_out22), .out23(demultiplexer_2_out23),
    .in(or_1_out), .sel(d_ff_2_q));  // open: out24, out25, out26, out27, out28, out29, out30, out31
  or or_4 (or_4_out[0], and_8_out, and_9_out, and_10_out, and_11_out, and_12_out, and_13_out, and_14_out, and_15_out, and_16_out, and_17_out, and_18_out, and_19_out, and_20_out, and_21_out, and_22_out, and_23_out, and_24_out, and_25_out, and_26_out, and_27_out, and_28_out, and_29_out, and_30_out, and_31_out);
  S_R_Flip_Flop s_r_ff_5 (
    .S(demultiplexer_1_out20), .R(and_6_out), .clk(and_2_out), .Q(Bit24_Quotient[4]), .reset(and_6_out));  // open: Qn, preset
  and and_8 (and_8_out, Bit24_Dividend[23], demultiplexer_2_out0);
  S_R_Flip_Flop s_r_ff_6 (
    .S(demultiplexer_1_out19), .R(and_6_out), .clk(and_2_out), .Q(Bit24_Quotient[5]), .reset(and_6_out));  // open: Qn, preset
  and and_9 (and_9_out, Bit24_Dividend[22], demultiplexer_2_out1);
  and and_10 (and_10_out, Bit24_Dividend[21], demultiplexer_2_out2);
  S_R_Flip_Flop s_r_ff_7 (
    .S(demultiplexer_1_out18), .R(and_6_out), .clk(and_2_out), .Q(Bit24_Quotient[6]), .reset(and_6_out));  // open: Qn, preset
  and and_11 (and_11_out, Bit24_Dividend[20], demultiplexer_2_out3);
  and and_12 (and_12_out, Bit24_Dividend[19], demultiplexer_2_out4);
  S_R_Flip_Flop s_r_ff_8 (
    .S(demultiplexer_1_out17), .R(and_6_out), .clk(and_2_out), .Q(Bit24_Quotient[7]), .reset(and_6_out));  // open: Qn, preset
  and and_13 (and_13_out, Bit24_Dividend[18], demultiplexer_2_out5);
  and and_14 (and_14_out, Bit24_Dividend[17], demultiplexer_2_out6);
  S_R_Flip_Flop s_r_ff_9 (
    .S(demultiplexer_1_out16), .R(and_6_out), .clk(and_2_out), .Q(Bit24_Quotient[8]), .reset(and_6_out));  // open: Qn, preset
  and and_15 (and_15_out, Bit24_Dividend[16], demultiplexer_2_out7);
  and and_16 (and_16_out, Bit24_Dividend[15], demultiplexer_2_out8);
  S_R_Flip_Flop s_r_ff_10 (
    .S(demultiplexer_1_out15), .R(and_6_out), .clk(and_2_out), .Q(Bit24_Quotient[9]), .reset(and_6_out));  // open: Qn, preset
  and and_17 (and_17_out, Bit24_Dividend[14], demultiplexer_2_out9);
  and and_18 (and_18_out, Bit24_Dividend[13], demultiplexer_2_out10);
  and and_19 (and_19_out, Bit24_Dividend[12], demultiplexer_2_out11);
  and and_20 (and_20_out, Bit24_Dividend[11], demultiplexer_2_out12);
  S_R_Flip_Flop s_r_ff_11 (
    .S(demultiplexer_1_out14), .R(and_6_out), .clk(and_2_out), .Q(Bit24_Quotient[10]), .reset(and_6_out));  // open: Qn, preset
  and and_21 (and_21_out, Bit24_Dividend[10], demultiplexer_2_out13);
  and and_22 (and_22_out, Bit24_Dividend[9], demultiplexer_2_out14);
  S_R_Flip_Flop s_r_ff_12 (
    .S(demultiplexer_1_out13), .R(and_6_out), .clk(and_2_out), .Q(Bit24_Quotient[11]), .reset(and_6_out));  // open: Qn, preset
  and and_23 (and_23_out, Bit24_Dividend[8], demultiplexer_2_out15);
  and and_24 (and_24_out, Bit24_Dividend[7], demultiplexer_2_out16);
  S_R_Flip_Flop s_r_ff_13 (
    .S(demultiplexer_1_out12), .R(and_6_out), .clk(and_2_out), .Q(Bit24_Quotient[12]), .reset(and_6_out));  // open: Qn, preset
  and and_25 (and_25_out, Bit24_Dividend[6], demultiplexer_2_out17);
  and and_26 (and_26_out, Bit24_Dividend[5], demultiplexer_2_out18);
  S_R_Flip_Flop s_r_ff_14 (
    .S(demultiplexer_1_out11), .R(and_6_out), .clk(and_2_out), .Q(Bit24_Quotient[13]), .reset(and_6_out));  // open: Qn, preset
  and and_27 (and_27_out, Bit24_Dividend[4], demultiplexer_2_out19);
  and and_28 (and_28_out, Bit24_Dividend[3], demultiplexer_2_out20);
  S_R_Flip_Flop s_r_ff_15 (
    .S(demultiplexer_1_out10), .R(and_6_out), .clk(and_2_out), .Q(Bit24_Quotient[14]), .reset(and_6_out));  // open: Qn, preset
  and and_29 (and_29_out, Bit24_Dividend[2], demultiplexer_2_out21);
  and and_30 (and_30_out, Bit24_Dividend[1], demultiplexer_2_out22);
  S_R_Flip_Flop s_r_ff_16 (
    .S(demultiplexer_1_out9), .R(and_6_out), .clk(and_2_out), .Q(Bit24_Quotient[15]), .reset(and_6_out));  // open: Qn, preset
  and and_31 (and_31_out, Bit24_Dividend[0], demultiplexer_2_out23);
  S_R_Flip_Flop s_r_ff_17 (
    .S(demultiplexer_1_out8), .R(and_6_out), .clk(and_2_out), .Q(Bit24_Quotient[16]), .reset(and_6_out));  // open: Qn, preset
  S_R_Flip_Flop s_r_ff_18 (
    .S(demultiplexer_1_out7), .R(and_6_out), .clk(and_2_out), .Q(Bit24_Quotient[17]), .reset(and_6_out));  // open: Qn, preset
  S_R_Flip_Flop s_r_ff_19 (
    .S(demultiplexer_1_out6), .R(and_6_out), .clk(and_2_out), .Q(Bit24_Quotient[18]), .reset(and_6_out));  // open: Qn, preset
  S_R_Flip_Flop s_r_ff_20 (
    .S(demultiplexer_1_out5), .R(and_6_out), .clk(and_2_out), .Q(Bit24_Quotient[19]), .reset(and_6_out));  // open: Qn, preset
  S_R_Flip_Flop s_r_ff_21 (
    .S(demultiplexer_1_out4), .R(and_6_out), .clk(and_2_out), .Q(Bit24_Quotient[20]), .reset(and_6_out));  // open: Qn, preset
  S_R_Flip_Flop s_r_ff_22 (
    .S(demultiplexer_1_out3), .R(and_6_out), .clk(and_2_out), .Q(Bit24_Quotient[21]), .reset(and_6_out));  // open: Qn, preset
  S_R_Flip_Flop s_r_ff_23 (
    .S(demultiplexer_1_out2), .R(and_6_out), .clk(and_2_out), .Q(Bit24_Quotient[22]), .reset(and_6_out));  // open: Qn, preset
  S_R_Flip_Flop s_r_ff_24 (
    .S(demultiplexer_1_out1), .R(and_6_out), .clk(and_2_out), .Q(Bit24_Quotient[23]), .reset(and_6_out));  // open: Qn, preset

  assign Bit24_Remainder = Bit24_Adder_A;

  // Notes on the sheet:
  //   the adder Cin needs to be active when dividing bc thats an inverter above here not a twscmpletner
  //   REMAINDER AND QUOTIENT ARE VALID AFTER RISING EDGE ON 17th cycle
  //   RESULTS ARE CLEARED ON RISING EDGE OF 19th
  //   DIVIDER IS READY TO USE AFTER falling edge of 19th
endmodule

module Bit16_To_Bit24_High_Byte (
  input  [15:0] Bit16,
  output [23:0] Bit24
);


  assign Bit24 = {Bit16, {8{1'b0}}};
endmodule

module Bit16_To_Bit24_Low_Byte (
  input  [15:0] Bit16,
  output [23:0] Bit24
);


  assign Bit24 = {{8{1'b0}}, Bit16};
endmodule

module Bit5_Controlled_Buffer (
  input  [4:0] Bit5_In,
  input  Enable,
  output [4:0] Bit5_Out
);

  and and_1 (Bit5_Out[0], Bit5_In[0], Enable);
  and and_2 (Bit5_Out[1], Bit5_In[1], Enable);
  and and_3 (Bit5_Out[2], Bit5_In[2], Enable);
  and and_4 (Bit5_Out[3], Bit5_In[3], Enable);
  and and_5 (Bit5_Out[4], Bit5_In[4], Enable);
endmodule

module Bit16_Float_Exponent_Unit (
  input  [23:0] Bit24_Right_Shift_Result,
  input  DIV,
  input  MUL,
  input  ADD_OR_SUB,
  input  [15:0] A16,
  input  [15:0] B16,
  output [15:0] Bit16_Right_Shift_Data,
  output [3:0] Bit4_Right_Shift,
  output [23:0] Mantissa_B_Div_And_Mul_Shifted,
  output [23:0] Mantissa_A_Mul_Shifted,
  output [23:0] Mantissa_A_Add_Shifted,
  output [23:0] Mantissa_A_Sub_Shifted,
  output [23:0] Mantissa_B_Add_Shifted,
  output [23:0] Mantissa_B_Sub_Shifted,
  output [4:0] Initial_Add_Sub_Exponent,
  output [4:0] Result_Exponent_A_Sub_B_DIV,
  output [4:0] Result_Exponent_A_Add_B_MUL,
  output Result_Sign,
  output Exponent_Overflow,
  output Exponent_Underflow,
  output A_Negative,
  output B_Negative
);

  wire and_1_out, and_2_out, and_3_out, and_4_out, and_5_out, and_6_out, and_7_out, and_8_out, and_9_out,
       and_10_out, and_11_out, bit5_adder_3_cout, bit5_adder_4_cout, bit5_adder_6_cout, nor_1_out, nor_2_out,
       not_1_out, not_2_out, not_3_out, not_4_out, or_6_out, or_7_out, or_8_out, xor_1_out;
  wire [3:0] bit4_controlled_buffer_1_bit4_out, bit4_controlled_buffer_2_bit4_out,
       bit4_twos_complementer_1_bit4_result;
  wire [4:0] bit5_adder_1_bit5_result, bit5_adder_2_bit5_result, bit5_adder_3_bit5_result,
       bit5_adder_4_bit5_result, bit5_adder_5_bit5_result, bit5_adder_6_bit5_result,
       bit5_adder_7_bit5_result, bit5_controlled_buffer_1_bit5_out, bit5_controlled_buffer_2_bit5_out,
       bit5_twos_complementer_1_bit5_result, bit5_twos_complementer_2_bit5_result;
  wire [10:10] or_1_out, or_2_out;
  wire [15:0] bit16_controlled_buffer_1_bit16_out, bit16_controlled_buffer_2_bit16_out;
  wire [23:0] bit16_to_bit24_high_byte_1_bit24, bit16_to_bit24_high_byte_2_bit24,
       bit16_to_bit24_low_byte_1_bit24, bit16_to_bit24_low_byte_2_bit24, bit24_controlled_buffer_3_bit24_out,
       bit24_controlled_buffer_4_bit24_out, bit24_controlled_buffer_5_bit24_out,
       bit24_controlled_buffer_6_bit24_out;
  wire [23:20] or_9_out, or_10_out;

  or or_1 (or_1_out[10], A16[10], A16[11], A16[12], A16[13], A16[14]);
  or or_2 (or_2_out[10], B16[10], B16[11], B16[12], B16[13], B16[14]);
  Bit5_Adder bit5_adder_1 (
    .Bit5_A(A16[14:10]), .Bit5_B(5'b10001), .Bit5_Result(bit5_adder_1_bit5_result));  // open: Cin, Cout
  Bit5_Adder bit5_adder_2 (
    .Bit5_A(B16[14:10]), .Bit5_B(5'b10001), .Bit5_Result(bit5_adder_2_bit5_result));  // open: Cin, Cout
  Bit5_Twos_Complementer bit5_twos_complementer_1 (
    .Bit5_In(bit5_adder_2_bit5_result), .Bit5_Result(bit5_twos_complementer_1_bit5_result));
  Bit5_Twos_Complementer bit5_twos_complementer_2 (
    .Bit5_In(B16[14:10]), .Bit5_Result(bit5_twos_complementer_2_bit5_result));
  Bit5_Controlled_Buffer bit5_controlled_buffer_1 (
    .Bit5_In(A16[14:10]), .Enable(and_2_out), .Bit5_Out(bit5_controlled_buffer_1_bit5_out));
  Bit5_Controlled_Buffer bit5_controlled_buffer_2 (
    .Bit5_In(B16[14:10]), .Enable(and_1_out), .Bit5_Out(bit5_controlled_buffer_2_bit5_out));
  assign Initial_Add_Sub_Exponent = bit5_controlled_buffer_1_bit5_out | bit5_controlled_buffer_2_bit5_out;  // OR_Gate or_3, 5 bits wide
  and and_1 (and_1_out, ADD_OR_SUB, ~bit5_adder_3_cout);  // AND_Gate
  and and_2 (and_2_out, ADD_OR_SUB, bit5_adder_3_cout);
  Bit5_Adder bit5_adder_3 (
    .Bit5_A(A16[14:10]), .Bit5_B(bit5_twos_complementer_2_bit5_result),
    .Bit5_Result(bit5_adder_3_bit5_result), .Cout(bit5_adder_3_cout));  // open: Cin
  Bit5_Adder bit5_adder_4 (
    .Bit5_A(bit5_adder_1_bit5_result), .Bit5_B(bit5_adder_2_bit5_result),
    .Bit5_Result(bit5_adder_4_bit5_result), .Cout(bit5_adder_4_cout));  // open: Cin
  Bit5_Adder bit5_adder_5 (
    .Bit5_A(bit5_adder_4_bit5_result), .Bit5_B(5'b01111), .Bit5_Result(bit5_adder_5_bit5_result));  // open: Cin, Cout
  Bit5_Adder bit5_adder_6 (
    .Bit5_A(bit5_adder_1_bit5_result), .Bit5_B(bit5_twos_complementer_1_bit5_result),
    .Bit5_Result(bit5_adder_6_bit5_result), .Cout(bit5_adder_6_cout));  // open: Cin
  not not_1 (not_1_out, bit5_adder_6_cout);
  Bit5_Adder bit5_adder_7 (
    .Bit5_A(bit5_adder_6_bit5_result), .Bit5_B(5'b01111), .Bit5_Result(bit5_adder_7_bit5_result));  // open: Cin, Cout
  Bit16_To_Bit24_Low_Byte bit16_to_bit24_low_byte_1 (
    .Bit16({{5{1'b0}}, or_2_out[10], B16[9:0]}), .Bit24(bit16_to_bit24_low_byte_1_bit24));
  Bit16_To_Bit24_Low_Byte bit16_to_bit24_low_byte_2 (
    .Bit16({{5{1'b0}}, or_1_out[10], A16[9:0]}), .Bit24(bit16_to_bit24_low_byte_2_bit24));
  Bit16_To_Bit24_High_Byte bit16_to_bit24_high_byte_1 (
    .Bit16({{5{1'b0}}, or_1_out[10], A16[9:0]}), .Bit24(bit16_to_bit24_high_byte_1_bit24));
  Bit16_To_Bit24_High_Byte bit16_to_bit24_high_byte_2 (
    .Bit16({{5{1'b0}}, or_2_out[10], B16[9:0]}), .Bit24(bit16_to_bit24_high_byte_2_bit24));
  Bit16_Controlled_Buffer bit16_controlled_buffer_1 (
    .Enable(and_1_out), .Bit16_In({{5{1'b0}}, or_1_out[10], A16[9:0]}),
    .Bit16_Out(bit16_controlled_buffer_1_bit16_out));
  Bit16_Controlled_Buffer bit16_controlled_buffer_2 (
    .Enable(and_2_out), .Bit16_In({{5{1'b0}}, or_2_out[10], B16[9:0]}),
    .Bit16_Out(bit16_controlled_buffer_2_bit16_out));
  assign Bit16_Right_Shift_Data = bit16_controlled_buffer_1_bit16_out | bit16_controlled_buffer_2_bit16_out;  // OR_Gate or_4, 16 bits wide
  Bit4_Twos_Complementer bit4_twos_complementer_1 (
    .Bit4_In(bit5_adder_3_bit5_result[3:0]), .Bit4_Result(bit4_twos_complementer_1_bit4_result));
  not not_2 (not_2_out, bit5_adder_3_bit5_result[4]);
  and and_3 (and_3_out, not_2_out, ADD_OR_SUB);
  Bit4_Controlled_Buffer bit4_controlled_buffer_1 (
    .Bit4_In(bit4_twos_complementer_1_bit4_result), .Enable(bit5_adder_3_bit5_result[4]),
    .Bit4_Out(bit4_controlled_buffer_1_bit4_out));
  Bit4_Controlled_Buffer bit4_controlled_buffer_2 (
    .Bit4_In(bit5_adder_3_bit5_result[3:0]), .Enable(and_3_out), .Bit4_Out(bit4_controlled_buffer_2_bit4_out));
  and and_4 (and_4_out, bit5_adder_3_cout, bit5_adder_3_bit5_result[4]);
  nor nor_1 (nor_1_out, bit5_adder_3_bit5_result[4], bit5_adder_3_cout);
  and and_5 (and_5_out, ~bit5_adder_3_bit5_result[0], ~bit5_adder_3_bit5_result[1], ~bit5_adder_3_bit5_result[2], ~bit5_adder_3_bit5_result[3], bit5_adder_3_bit5_result[4]);  // AND_Gate
  Bit5_Controlled_Buffer bit5_controlled_buffer_3 (
    .Bit5_In(bit5_adder_7_bit5_result), .Enable(DIV), .Bit5_Out(Result_Exponent_A_Sub_B_DIV));
  Bit5_Controlled_Buffer bit5_controlled_buffer_4 (
    .Bit5_In(bit5_adder_5_bit5_result), .Enable(MUL), .Bit5_Out(Result_Exponent_A_Add_B_MUL));
  assign Bit4_Right_Shift = bit4_controlled_buffer_1_bit4_out | bit4_controlled_buffer_2_bit4_out;  // OR_Gate or_5, 4 bits wide
  nor nor_2 (nor_2_out, and_4_out, nor_1_out, and_5_out);
  not not_3 (not_3_out, and_1_out);
  and and_6 (and_6_out, nor_2_out, and_1_out);
  and and_7 (and_7_out, ADD_OR_SUB, not_3_out);
  and and_8 (and_8_out, nor_2_out, and_2_out);
  not not_4 (not_4_out, and_2_out);
  or or_6 (or_6_out, DIV, MUL);
  or or_7 (or_7_out, DIV, and_7_out);
  and and_9 (and_9_out, ADD_OR_SUB, not_4_out);
  Bit24_Controlled_Buffer bit24_controlled_buffer_1 (
    .Enable(or_6_out), .Bit24_In(bit16_to_bit24_low_byte_1_bit24), .Bit24_Out(Mantissa_B_Div_And_Mul_Shifted));
  Bit24_Controlled_Buffer bit24_controlled_buffer_2 (
    .Enable(MUL), .Bit24_In(bit16_to_bit24_low_byte_2_bit24), .Bit24_Out(Mantissa_A_Mul_Shifted));
  Bit24_Controlled_Buffer bit24_controlled_buffer_3 (
    .Enable(and_6_out), .Bit24_In(Bit24_Right_Shift_Result), .Bit24_Out(bit24_controlled_buffer_3_bit24_out));
  Bit24_Controlled_Buffer bit24_controlled_buffer_4 (
    .Enable(or_7_out), .Bit24_In(bit16_to_bit24_high_byte_1_bit24),
    .Bit24_Out(bit24_controlled_buffer_4_bit24_out));
  Bit24_Controlled_Buffer bit24_controlled_buffer_5 (
    .Enable(and_8_out), .Bit24_In(Bit24_Right_Shift_Result), .Bit24_Out(bit24_controlled_buffer_5_bit24_out));
  Bit24_Controlled_Buffer bit24_controlled_buffer_6 (
    .Enable(and_9_out), .Bit24_In(bit16_to_bit24_high_byte_2_bit24),
    .Bit24_Out(bit24_controlled_buffer_6_bit24_out));
  xor xor_1 (xor_1_out, B16[15], A16[15]);
  or or_8 (or_8_out, A16[15], B16[15]);
  assign {or_9_out, Mantissa_A_Add_Shifted[23:4]} = bit24_controlled_buffer_3_bit24_out | bit24_controlled_buffer_4_bit24_out;  // OR_Gate or_9, 24 bits wide
  assign {or_10_out, Mantissa_B_Add_Shifted[23:4]} = bit24_controlled_buffer_5_bit24_out | bit24_controlled_buffer_6_bit24_out;  // OR_Gate or_10, 24 bits wide
  and and_10 (and_10_out, or_6_out, xor_1_out);
  and and_11 (and_11_out, ADD_OR_SUB, or_8_out);
  or or_11 (Result_Sign, and_10_out, and_11_out);
  and and_12 (Exponent_Overflow, bit5_adder_4_cout, DIV);
  and and_13 (Exponent_Underflow, not_1_out, MUL);

  assign A_Negative = A16[15];
  assign B_Negative = B16[15];
  assign Mantissa_A_Add_Shifted[3:0] = 4'b0000;
  assign Mantissa_A_Sub_Shifted = {Mantissa_A_Add_Shifted[22:4], {5{1'b0}}};
  assign Mantissa_B_Add_Shifted[3:0] = 4'b0000;
  assign Mantissa_B_Sub_Shifted = {Mantissa_B_Add_Shifted[22:4], {5{1'b0}}};
endmodule

module fpu2 (
  input  Add,
  input  Sub,
  input  Mul,
  input  Div,
  input  [15:0] in_5,
  input  [15:0] in_6,
  input  [15:0] in_7,
  input  [15:0] in_8,
  input  [31:0] in_9,
  input  [4:0] in_10,
  input  [4:0] in_11,
  input  [4:0] in_12,
  input  [15:0] in_13,
  output [4:0] out_14,
  output [4:0] out_15,
  output [4:0] out_16,
  output [4:0] out_17,
  output [15:0] out_18,
  output [15:0] out_19,
  output [15:0] out_20,
  output [4:0] out_21,
  output [4:0] out_22,
  output [15:0] out_23,
  output [4:0] out_24,
  output [4:0] out_25,
  output [4:0] out_26,
  output [4:0] out_27
);

  wire and_1_out, and_2_out, and_3_out, and_4_out, and_5_out, and_6_out, and_7_out, and_8_out, and_9_out,
       and_10_out, and_11_out, and_12_out, and_13_out, and_14_out, and_15_out, and_16_out, and_17_out,
       and_18_out, and_19_out, and_20_out, and_21_out, and_22_out, and_23_out, and_24_out, and_25_out,
       and_26_out, and_27_out, and_28_out, and_29_out, and_30_out, and_31_out, and_32_out, and_33_out,
       and_34_out, and_35_out, and_36_out, and_37_out, and_38_out, and_40_out, and_41_out, bit5_adder_2_cout,
       bit5_adder_4_cout, bit5_adder_6_cout, bit5_adder_7_cout, bit5_adder_8_cout, bit5_adder_10_cout,
       bit5_adder_11_cout, bit5_greater_than_1_a_greater_b, bit10_add_one_1_carry_out, bit24_adder_1_c_out,
       nand_1_out, nand_2_out, nand_5_out, nor_1_out, nor_2_out, nor_3_out, nor_4_out, nor_5_out, not_1_out,
       not_2_out, or_1_out, or_2_out, or_3_out, or_4_out, or_7_out, or_10_out, or_11_out, or_12_out,
       or_13_out, or_15_out, or_16_out, or_17_out, or_19_out, or_20_out, or_21_out, or_22_out, or_23_out,
       or_24_out, or_25_out, or_28_out, or_29_out, or_30_out, or_31_out, or_33_out, undriven_2, xnor_1_out,
       xor_1_out, xor_2_out, xor_3_out, xor_4_out, xor_5_out, xor_6_out, xor_7_out, xor_8_out;
  wire [4:0] bit5_add_one_2_bit5_out, bit5_add_one_3_bit5_out, bit5_adder_1_bit5_result,
       bit5_adder_2_bit5_result, bit5_adder_3_bit5_result, bit5_adder_4_bit5_result,
       bit5_adder_5_bit5_result, bit5_adder_6_bit5_result, bit5_adder_9_bit5_result,
       bit5_adder_10_bit5_result, bit5_adder_11_bit5_result, bit5_controlled_buffer_1_bit5_out,
       bit5_controlled_buffer_2_bit5_out, bit5_controlled_buffer_3_bit5_out,
       bit5_controlled_buffer_5_bit5_out, bit5_controlled_buffer_6_bit5_out,
       bit5_controlled_buffer_7_bit5_out, bit5_controlled_buffer_8_bit5_out,
       bit5_controlled_buffer_9_bit5_out, bit5_controlled_buffer_10_bit5_out,
       bit5_controlled_buffer_11_bit5_out, bit5_controlled_buffer_12_bit5_out, bit5_inverter_1_bit5_out,
       bit5_inverter_2_bit5_out, bit5_inverter_3_bit5_out, bit5_inverter_4_bit5_out,
       bit5_inverter_5_bit5_out, bit5_inverter_6_bit5_out, bit5_toggle_twscmplmtr_1_bit5_result,
       bit5_toggle_twscmplmtr_3_bit5_result, bit5_toggle_twscmplmtr_6_bit5_result,
       bit5_twos_complementer_1_bit5_result, bit5_twos_complementer_2_bit5_result, or_26_out, or_27_out,
       or_32_out, priority_encoder_1_out, undriven, undriven_3;
  wire [4:1] bit5_add_one_1_bit5_out;
  wire [4:4] bit5_add_one_1_bit5_out_2;
  wire [9:0] bit10_add_one_1_bit10_out, bit10_controlled_buffer_1_bit10_out;
  wire [10:0] bit11_controlled_buffer_1_bit11_out, bit11_controlled_buffer_2_bit11_out,
       bit11_controlled_buffer_3_bit11_out, bit11_controlled_buffer_4_bit11_out,
       bit11_controlled_buffer_5_bit11_out, bit11_controlled_buffer_6_bit11_out,
       bit11_controlled_buffer_7_bit11_out, bit11_controlled_buffer_8_bit11_out, or_8_out, or_9_out;
  wire [10:10] or_5_out, or_6_out;
  wire [15:0] bit11_to_bit16_high_3_bit16_out, bit11_to_bit16_high_4_bit16_out,
       bit11_to_bit16_low_1_bit16_out, bit11_to_bit16_low_2_bit16_out, bit11_to_bit16_low_3_bit16_out,
       bit16_controlled_buffer_1_bit16_out, bit16_controlled_buffer_2_bit16_out, bit16_multiplier_1_p1,
       bit16_multiplier_1_p2;
  wire [15:15] and_39_out;
  wire [23:0] bit16_to_bit24_high_byte_1_bit24, bit16_to_bit24_high_byte_2_bit24,
       bit16_to_bit24_low_byte_1_bit24, bit24_adder_1_bit24_result, bit24_controlled_buffer_1_bit24_out,
       bit24_controlled_buffer_2_bit24_out, bit24_controlled_buffer_3_bit24_out,
       bit24_controlled_buffer_4_bit24_out, bit24_toggle_twscmplmtr_1_bit24_out,
       bit24_toggle_twscmplmtr_2_bit24_out, bit24_toggle_twscmplmtr_3_bit24_out,
       bit32_to_bit24_high_1_bit24_out, divider_1_out, divider_1_rem;
  wire [31:0] bit11_to_bit32_high_1_bit32_out, bit32_left_shift_1_bit32_result,
       bit32_right_shift_1_bit32_result, or_18_out;

  // Probe on in_13
  // Probe on in_7
  // Probe on in_8
  // Probe on in_7
  // Probe on in_7
  // Probe on in_8
  FPAdder #(.fpwidth(16)) fpadder_1 (.a(in_8), .b(in_7), .out(out_18));
  FPSubtractor #(.fpwidth(16)) fpsubtractor_1 (.a(in_7), .b(in_8), .out(out_20));
  FPMultiplier #(.fpwidth(16)) fpmultiplier_1 (.a(in_8), .b(in_7), .out(out_19));
  FPDivider #(.fpwidth(16)) fpdivider_1 (.a(in_7), .b(in_8), .out(out_23));
  or or_1 (or_1_out, Add, Sub);
  or or_2 (or_2_out, Mul, Div);
  // Probe on out_18
  // Probe on out_20
  // Probe on out_20[14:10]
  // Probe on out_23
  or or_3 (or_3_out, in_7[0], in_7[1], in_7[2], in_7[3], in_7[4], in_7[5], in_7[6], in_7[7], in_7[8], in_7[9]);
  or or_4 (or_4_out, in_8[0], in_8[1], in_8[2], in_8[3], in_8[4], in_8[5], in_8[6], in_8[7], in_8[8], in_8[9]);
  or or_5 (or_5_out[10], in_7[10], in_7[11], in_7[12], in_7[13], in_7[14]);
  or or_6 (or_6_out[10], in_8[10], in_8[11], in_8[12], in_8[13], in_8[14]);
  // Probe on out_19
  // Probe on {and_39_out[15], bit5_add_one_3_bit5_out, bit10_controlled_buffer_1_bit10_out}
  // Probe on {and_39_out[15], bit5_add_one_3_bit5_out, bit10_controlled_buffer_1_bit10_out}
  and and_1 (and_1_out, in_7[9], or_3_out, in_7[10], in_7[11], in_7[12], in_7[13], in_7[14]);
  and and_2 (and_2_out, ~in_7[9], or_3_out, in_7[10], in_7[11], in_7[12], in_7[13], in_7[14]);  // AND_Gate
  and and_3 (and_3_out, ~in_7[9], in_7[10], in_7[11], in_7[12], in_7[13], in_7[14]);  // AND_Gate
  nor nor_1 (nor_1_out, in_7[0], in_7[1], in_7[2], in_7[3], in_7[4], in_7[5], in_7[6], in_7[7], in_7[8], in_7[9], in_7[10], in_7[11], in_7[12], in_7[13], in_7[14]);
  and and_4 (and_4_out, in_8[9], or_4_out, in_8[10], in_8[11], in_8[12], in_8[13], in_8[14]);
  and and_5 (and_5_out, ~in_8[9], or_4_out, in_8[10], in_8[11], in_8[12], in_8[13], in_8[14]);  // AND_Gate
  and and_6 (and_6_out, ~in_8[9], in_8[10], in_8[11], in_8[12], in_8[13], in_8[14]);  // AND_Gate
  nor nor_2 (nor_2_out, in_8[0], in_8[1], in_8[2], in_8[3], in_8[4], in_8[5], in_8[6], in_8[7], in_8[8], in_8[9], in_8[10], in_8[11], in_8[12], in_8[13], in_8[14]);
  Bit5_Inverter bit5_inverter_1 (.Bit5_In(out_23[14:10]), .Bit5_Out(bit5_inverter_1_bit5_out));
  Bit5_Inverter bit5_inverter_2 (.Bit5_In(in_8[14:10]), .Bit5_Out(bit5_inverter_2_bit5_out));
  and and_7 (and_7_out, or_1_out, ~not_1_out);  // AND_Gate
  and and_8 (and_8_out, or_1_out, not_1_out);
  // Probe on bit5_inverter_5_bit5_out
  // Probe on bit5_add_one_3_bit5_out
  Bit5_Inverter bit5_inverter_3 (.Bit5_In(out_20[14:10]), .Bit5_Out(bit5_inverter_3_bit5_out));
  and and_9 (and_9_out, and_3_out, and_6_out, Div);
  and and_10 (and_10_out, or_1_out, ~not_1_out);  // AND_Gate
  and and_11 (and_11_out, or_1_out, not_1_out);
  and and_12 (and_12_out, or_1_out, not_1_out);
  and and_13 (and_13_out, or_1_out, ~not_1_out);  // AND_Gate
  Bit5_Toggle_TwsCmplmtr bit5_toggle_twscmplmtr_1 (
    .Bit5_Input(in_8[14:10]), .Enable_Twos(Div), .Bit5_Result(bit5_toggle_twscmplmtr_1_bit5_result));
  Bit5_Inverter bit5_inverter_4 (.Bit5_In(out_19[14:10]), .Bit5_Out(bit5_inverter_4_bit5_out));
  // Probe on bit5_inverter_5_bit5_out
  Bit5_Adder bit5_adder_1 (
    .Cin(1'b1), .Bit5_A(bit5_add_one_3_bit5_out), .Bit5_B(bit5_inverter_1_bit5_out),
    .Bit5_Result(bit5_adder_1_bit5_result));  // open: Cout
  and and_14 (and_14_out, nor_1_out, nor_2_out, Div);
  and and_15 (and_15_out, and_3_out, nor_2_out, Mul);
  Bit5_Adder bit5_adder_2 (
    .Cin(1'b1), .Bit5_A(in_7[14:10]), .Bit5_B(bit5_inverter_2_bit5_out),
    .Bit5_Result(bit5_adder_2_bit5_result), .Cout(bit5_adder_2_cout));
  // Probe on bit5_adder_3_bit5_result
  // Probe on bit5_adder_1_bit5_result
  and and_16 (and_16_out, nor_1_out, and_6_out, Mul);
  Bit11_Controlled_Buffer bit11_controlled_buffer_1 (
    .Enable(Mul), .Bit11_In({or_5_out[10], in_7[9:0]}), .Bit11_Out(bit11_controlled_buffer_1_bit11_out));
  Bit11_Controlled_Buffer bit11_controlled_buffer_2 (
    .Enable(Mul), .Bit11_In({or_6_out[10], in_8[9:0]}), .Bit11_Out(bit11_controlled_buffer_2_bit11_out));
  Bit11_Controlled_Buffer bit11_controlled_buffer_3 (
    .Enable(Div), .Bit11_In({or_5_out[10], in_7[9:0]}), .Bit11_Out(bit11_controlled_buffer_3_bit11_out));
  Bit11_Controlled_Buffer bit11_controlled_buffer_4 (
    .Enable(Div), .Bit11_In({or_6_out[10], in_8[9:0]}), .Bit11_Out(bit11_controlled_buffer_4_bit11_out));
  Bit11_Controlled_Buffer bit11_controlled_buffer_5 (
    .Enable(and_10_out), .Bit11_In({or_5_out[10], in_7[9:0]}), .Bit11_Out(bit11_controlled_buffer_5_bit11_out));
  Bit11_Controlled_Buffer bit11_controlled_buffer_6 (
    .Enable(and_11_out), .Bit11_In({or_6_out[10], in_8[9:0]}), .Bit11_Out(bit11_controlled_buffer_6_bit11_out));
  Bit11_Controlled_Buffer bit11_controlled_buffer_7 (
    .Enable(and_12_out), .Bit11_In({or_5_out[10], in_7[9:0]}), .Bit11_Out(bit11_controlled_buffer_7_bit11_out));
  Bit11_Controlled_Buffer bit11_controlled_buffer_8 (
    .Enable(and_13_out), .Bit11_In({or_6_out[10], in_8[9:0]}), .Bit11_Out(bit11_controlled_buffer_8_bit11_out));
  not not_1 (not_1_out, bit5_adder_2_cout);
  Bit5_Controlled_Buffer bit5_controlled_buffer_1 (
    .Bit5_In(in_7[14:10]), .Enable(and_7_out), .Bit5_Out(bit5_controlled_buffer_1_bit5_out));
  Bit5_Controlled_Buffer bit5_controlled_buffer_2 (
    .Bit5_In(in_8[14:10]), .Enable(and_8_out), .Bit5_Out(bit5_controlled_buffer_2_bit5_out));
  Bit5_Adder bit5_adder_3 (
    .Cin(1'b1), .Bit5_A(bit5_add_one_3_bit5_out), .Bit5_B(bit5_inverter_3_bit5_out),
    .Bit5_Result(bit5_adder_3_bit5_result));  // open: Cout
  and and_17 (and_17_out, and_3_out, and_6_out, or_7_out, xor_2_out);
  or or_7 (or_7_out, Add, Sub);
  xor xor_1 (xor_1_out, in_7[15], Sub);
  assign or_8_out = bit11_controlled_buffer_5_bit11_out | bit11_controlled_buffer_6_bit11_out;  // OR_Gate or_8, 11 bits wide
  assign or_9_out = bit11_controlled_buffer_7_bit11_out | bit11_controlled_buffer_8_bit11_out;  // OR_Gate or_9, 11 bits wide
  Bit5_Adder bit5_adder_4 (
    .Bit5_A(in_7[14:10]), .Bit5_B(bit5_toggle_twscmplmtr_1_bit5_result),
    .Bit5_Result(bit5_adder_4_bit5_result), .Cout(bit5_adder_4_cout));  // open: Cin
  Bit5_Adder bit5_adder_5 (
    .Cin(1'b1), .Bit5_A(bit5_add_one_3_bit5_out), .Bit5_B(bit5_inverter_4_bit5_out),
    .Bit5_Result(bit5_adder_5_bit5_result));  // open: Cout
  and and_18 (and_18_out, ~xor_3_out, or_7_out, and_6_out, and_3_out);  // AND_Gate
  xor xor_2 (xor_2_out, xor_1_out, in_8[15]);
  xor xor_3 (xor_3_out, xor_1_out, in_8[15]);
  // Probe on bit5_adder_5_bit5_result
  and and_19 (and_19_out, ~or_10_out, nor_2_out);  // AND_Gate
  or or_10 (or_10_out, and_1_out, and_2_out, and_3_out, nor_1_out);
  Bit11_To_Bit16_High bit11_to_bit16_high_1 ();  // open: Bit11_In, Bit16_Out
  Bit11_To_Bit16_High bit11_to_bit16_high_2 ();  // open: Bit11_In, Bit16_Out
  Bit11_To_Bit16_Low bit11_to_bit16_low_1 (
    .Bit11_In(bit11_controlled_buffer_1_bit11_out), .Bit16_Out(bit11_to_bit16_low_1_bit16_out));
  Bit11_To_Bit16_Low bit11_to_bit16_low_2 (
    .Bit11_In(bit11_controlled_buffer_2_bit11_out), .Bit16_Out(bit11_to_bit16_low_2_bit16_out));
  Bit11_To_Bit16_High bit11_to_bit16_high_3 (
    .Bit11_In(bit11_controlled_buffer_3_bit11_out), .Bit16_Out(bit11_to_bit16_high_3_bit16_out));
  Bit11_To_Bit16_Low bit11_to_bit16_low_3 (
    .Bit11_In(bit11_controlled_buffer_4_bit11_out), .Bit16_Out(bit11_to_bit16_low_3_bit16_out));
  and and_20 (and_20_out, not_1_out, in_8[15]);
  and and_21 (and_21_out, ~not_1_out, in_8[15]);  // AND_Gate
  xor xor_4 (xor_4_out, or_10_out, or_11_out);
  or or_11 (or_11_out, and_4_out, and_5_out, and_6_out, nor_2_out);
  Bit11_To_Bit16_High bit11_to_bit16_high_4 (.Bit11_In(or_8_out), .Bit16_Out(bit11_to_bit16_high_4_bit16_out));
  Bit16_To_Bit24_High_Byte bit16_to_bit24_high_byte_1 (
    .Bit16(bit11_to_bit16_high_4_bit16_out), .Bit24(bit16_to_bit24_high_byte_1_bit24));
  and and_22 (and_22_out, ~not_1_out, in_7[15]);  // AND_Gate
  and and_23 (and_23_out, not_1_out, in_7[15]);
  Bit5_Toggle_TwsCmplmtr bit5_toggle_twscmplmtr_2 (.Bit5_Input(5'b10001), .Enable_Twos(Mul));  // open: Bit5_Result
  and and_24 (and_24_out, Mul, xor_4_out, xor_5_out);
  xor xor_5 (xor_5_out, and_3_out, and_6_out);
  or or_12 (or_12_out, and_20_out, and_22_out);
  or or_13 (or_13_out, and_21_out, and_23_out);
  Bit11_To_Bit32_High bit11_to_bit32_high_1 (.Bit11_In(or_9_out), .Bit32_Out(bit11_to_bit32_high_1_bit32_out));
  Bit5_Toggle_TwsCmplmtr bit5_toggle_twscmplmtr_3 (
    .Bit5_Input(bit5_adder_2_bit5_result), .Enable_Twos(not_1_out),
    .Bit5_Result(bit5_toggle_twscmplmtr_3_bit5_result));
  Bit5_Adder bit5_adder_6 (
    .Bit5_A(bit5_adder_4_bit5_result), .Bit5_B({1'b0, {4{Div}}}), .Bit5_Result(bit5_adder_6_bit5_result),
    .Cout(bit5_adder_6_cout));  // open: Cin
  Bit5_Toggle_TwsCmplmtr bit5_toggle_twscmplmtr_4 (.Bit5_Input(in_11), .Enable_Twos(1'b1), .Bit5_Result(out_21));
  Bit16_To_Bit24_High_Byte bit16_to_bit24_high_byte_2 (
    .Bit16(bit11_to_bit16_high_3_bit16_out), .Bit24(bit16_to_bit24_high_byte_2_bit24));
  Bit16_To_Bit24_Low_Byte bit16_to_bit24_low_byte_1 (
    .Bit16(bit11_to_bit16_low_3_bit16_out), .Bit24(bit16_to_bit24_low_byte_1_bit24));
  and and_25 (and_25_out, not_1_out, Sub);
  and and_26 (and_26_out, Sub, ~not_1_out);  // AND_Gate
  nor nor_3 (nor_3_out, bit5_adder_6_cout, bit5_adder_4_cout);
  xor xor_6 (xor_6_out, and_25_out, or_12_out);
  xor xor_7 (xor_7_out, and_26_out, or_13_out);
  Divider #(.width(24)) divider_1 (
    .a(bit16_to_bit24_high_byte_2_bit24), .b(bit16_to_bit24_low_byte_1_bit24), .out(divider_1_out),
    .rem(divider_1_rem));  // open: upper
  xor xor_8 (xor_8_out, xor_6_out, xor_7_out);
  xnor xnor_1 (xnor_1_out, xor_6_out, xor_7_out);
  and and_27 (and_27_out, xor_6_out, ~xor_7_out);  // AND_Gate
  and and_28 (and_28_out, xor_7_out, ~xor_6_out);  // AND_Gate
  Bit5_Controlled_Buffer bit5_controlled_buffer_3 (
    .Bit5_In(bit5_toggle_twscmplmtr_3_bit5_result), .Enable(or_1_out),
    .Bit5_Out(bit5_controlled_buffer_3_bit5_out));
  Bit5_Controlled_Buffer bit5_controlled_buffer_4 (
    .Bit5_In(bit5_adder_6_bit5_result), .Enable(or_2_out), .Bit5_Out(out_15));
  Bit5_Adder bit5_adder_7 (
    .Bit5_A(out_21), .Bit5_B(in_10), .Bit5_Result(out_22), .Cout(bit5_adder_7_cout));  // open: Cin
  // Probe on divider_1_out
  assign out_14 = bit5_controlled_buffer_1_bit5_out | bit5_controlled_buffer_2_bit5_out | out_15;  // OR_Gate or_14, 5 bits wide
  // Bit16_Multiplier bit16_multiplier_1: pin names not known; wires that end beside it: bit16_multiplier_1_p1, bit16_multiplier_1_p2
  and and_29 (and_29_out, xor_6_out, xor_8_out);
  and and_30 (and_30_out, xor_6_out, xnor_1_out);
  Bit24_Toggle_TwsCmplmtr bit24_toggle_twscmplmtr_1 (
    .Enable(and_27_out), .Bit24_In(bit16_to_bit24_high_byte_1_bit24),
    .Bit24_Out(bit24_toggle_twscmplmtr_1_bit24_out));
  Bit24_Toggle_TwsCmplmtr bit24_toggle_twscmplmtr_2 (
    .Enable(and_28_out), .Bit24_In(bit32_to_bit24_high_1_bit24_out),
    .Bit24_Out(bit24_toggle_twscmplmtr_2_bit24_out));
  Bit32_Right_Shift bit32_right_shift_1 (
    .Bit32_In(bit11_to_bit32_high_1_bit32_out), .Bit5_Shift(bit5_controlled_buffer_3_bit5_out),
    .Bit32_Result(bit32_right_shift_1_bit32_result));
  nor nor_4 (nor_4_out, out_15[0], out_15[1], out_15[2], out_15[3], out_15[4]);
  or or_15 (or_15_out, and_29_out, and_30_out);
  or or_16 (or_16_out, nor_3_out, nor_4_out);
  nor nor_5 (nor_5_out, bit5_adder_7_cout, bit5_adder_8_cout);
  Bit5_Adder bit5_adder_8 (
    .Bit5_A(out_22), .Bit5_B(in_12), .Bit5_Result(out_25), .Cout(bit5_adder_8_cout));  // open: Cin
  and and_31 (and_31_out, Div, or_16_out);
  Bit24_Controlled_Buffer bit24_controlled_buffer_1 (
    .Enable(or_1_out), .Bit24_In(bit24_toggle_twscmplmtr_1_bit24_out),
    .Bit24_Out(bit24_controlled_buffer_1_bit24_out));
  Bit24_Controlled_Buffer bit24_controlled_buffer_2 (
    .Enable(or_1_out), .Bit24_In(bit24_toggle_twscmplmtr_2_bit24_out),
    .Bit24_Out(bit24_controlled_buffer_2_bit24_out));
  Bit32_To_Bit24_High bit32_to_bit24_high_1 (
    .Bit32_In(bit32_right_shift_1_bit32_result), .Bit24_Out(bit32_to_bit24_high_1_bit24_out));
  Bit16_Controlled_Buffer bit16_controlled_buffer_1 (
    .Enable(Mul), .Bit16_In(bit16_multiplier_1_p1), .Bit16_Out(bit16_controlled_buffer_1_bit16_out));
  Bit16_Controlled_Buffer bit16_controlled_buffer_2 (
    .Enable(Mul), .Bit16_In(bit16_multiplier_1_p2), .Bit16_Out(bit16_controlled_buffer_2_bit16_out));
  Bit5_Toggle_TwsCmplmtr bit5_toggle_twscmplmtr_5 (
    .Bit5_Input(out_25), .Enable_Twos(bit5_adder_8_cout), .Bit5_Result(out_26));
  Bit24_Controlled_Buffer bit24_controlled_buffer_3 (
    .Enable(Div), .Bit24_In(divider_1_out), .Bit24_Out(bit24_controlled_buffer_3_bit24_out));
  Bit24_Controlled_Buffer bit24_controlled_buffer_4 (
    .Enable(or_1_out), .Bit24_In(bit24_toggle_twscmplmtr_3_bit24_out),
    .Bit24_Out(bit24_controlled_buffer_4_bit24_out));
  Bit24_Adder bit24_adder_1 (
    .Bit24_A(bit24_controlled_buffer_1_bit24_out), .Bit24_B(bit24_controlled_buffer_2_bit24_out),
    .Bit24_Result(bit24_adder_1_bit24_result), .C_OUT(bit24_adder_1_c_out));  // open: C_In, Bit16_C_OUT
  and and_32 (and_32_out, or_1_out, or_17_out);
  or or_17 (or_17_out, not_2_out, and_33_out);
  and and_33 (and_33_out, xnor_1_out, ~bit24_adder_1_c_out);  // AND_Gate
  not not_2 (not_2_out, xnor_1_out);
  assign or_18_out = {bit16_controlled_buffer_2_bit16_out, bit16_controlled_buffer_1_bit16_out} | {bit24_controlled_buffer_3_bit24_out, {8{1'b0}}} | {bit24_controlled_buffer_4_bit24_out, {8{1'b0}}};  // OR_Gate or_18, 32 bits wide
  and and_34 (and_34_out, or_18_out[31], Mul);
  or or_19 (or_19_out, Mul, Div, and_32_out);
  Priority_Encoder #(.select(5)) priority_encoder_1 (
    .in0(or_18_out[0]), .in1(or_18_out[1]), .in2(or_18_out[2]), .in3(or_18_out[3]), .in4(or_18_out[4]),
    .in5(or_18_out[5]), .in6(or_18_out[6]), .in7(or_18_out[7]), .in8(or_18_out[8]), .in9(or_18_out[9]),
    .in10(or_18_out[10]), .in11(or_18_out[11]), .in12(or_18_out[12]), .in13(or_18_out[13]),
    .in14(or_18_out[14]), .in15(or_18_out[15]), .in16(or_18_out[16]), .in17(or_18_out[17]),
    .in18(or_18_out[18]), .in19(or_18_out[19]), .in20(or_18_out[20]), .in21(or_18_out[21]),
    .in22(or_18_out[22]), .in23(or_18_out[23]), .in24(or_18_out[24]), .in25(or_18_out[25]),
    .in26(or_18_out[26]), .in27(or_18_out[27]), .in28(or_18_out[28]), .in29(or_18_out[29]),
    .in30(or_18_out[30]), .in31(or_18_out[31]), .out(priority_encoder_1_out), .en_in(or_23_out));  // open: gs, en_out
  or or_20 (or_20_out, and_34_out, and_32_out);
  // Probe on out_14
  // Probe on out_14
  or or_21 (or_21_out, Div, Add, Sub, Mul);
  // Probe on priority_encoder_1_out
  // Probe on priority_encoder_1_out
  or or_22 (or_22_out, bit24_adder_1_bit24_result[0], bit24_adder_1_bit24_result[1], bit24_adder_1_bit24_result[2], bit24_adder_1_bit24_result[3], bit24_adder_1_bit24_result[4], bit24_adder_1_bit24_result[5], bit24_adder_1_bit24_result[6], bit24_adder_1_bit24_result[7], bit24_adder_1_bit24_result[8], bit24_adder_1_bit24_result[9], bit24_adder_1_bit24_result[10], bit24_adder_1_bit24_result[11], bit24_adder_1_bit24_result[13], bit24_adder_1_bit24_result[14], bit24_adder_1_bit24_result[15], bit24_adder_1_bit24_result[16], bit24_adder_1_bit24_result[17], bit24_adder_1_bit24_result[18], bit24_adder_1_bit24_result[19], bit24_adder_1_bit24_result[20], bit24_adder_1_bit24_result[21], bit24_adder_1_bit24_result[22], bit24_adder_1_bit24_result[23], bit24_adder_1_bit24_result[12]);
  and and_35 (and_35_out, or_21_out, or_23_out);
  or or_23 (or_23_out, or_18_out[0], or_18_out[1], or_18_out[2], or_18_out[3], or_18_out[4], or_18_out[5], or_18_out[6], or_18_out[7], or_18_out[8], or_18_out[9], or_18_out[10], or_18_out[11], or_18_out[12], or_18_out[13], or_18_out[14], or_18_out[15], or_18_out[17], or_18_out[18], or_18_out[19], or_18_out[20], or_18_out[21], or_18_out[22], or_18_out[23], or_18_out[24], or_18_out[25], or_18_out[26], or_18_out[27], or_18_out[28], or_18_out[29], or_18_out[30], or_18_out[31], or_18_out[16]);
  nand nand_1 (nand_1_out, and_31_out, Div);
  Bit24_Toggle_TwsCmplmtr bit24_toggle_twscmplmtr_3 (
    .Enable(and_29_out), .Bit24_In(bit24_adder_1_bit24_result),
    .Bit24_Out(bit24_toggle_twscmplmtr_3_bit24_out));
  Bit5_Controlled_Buffer bit5_controlled_buffer_5 (
    .Bit5_In(bit5_adder_9_bit5_result), .Enable(Div), .Bit5_Out(bit5_controlled_buffer_5_bit5_out));
  Bit5_Controlled_Buffer bit5_controlled_buffer_6 (
    .Bit5_In(bit5_adder_9_bit5_result), .Enable(or_19_out), .Bit5_Out(bit5_controlled_buffer_6_bit5_out));
  Bit5_Controlled_Buffer bit5_controlled_buffer_7 (
    .Bit5_In(bit5_inverter_5_bit5_out), .Enable(or_20_out), .Bit5_Out(bit5_controlled_buffer_7_bit5_out));
  Bit5_Adder bit5_adder_9 (
    .Bit5_A(bit5_inverter_5_bit5_out), .Bit5_B(bit5_controlled_buffer_8_bit5_out),
    .Bit5_Result(bit5_adder_9_bit5_result));  // open: Cin, Cout
  Bit5_Controlled_Buffer bit5_controlled_buffer_8 (
    .Bit5_In(bit5_inverter_6_bit5_out), .Enable(and_31_out), .Bit5_Out(bit5_controlled_buffer_8_bit5_out));
  Bit5_Inverter bit5_inverter_5 (.Bit5_In(priority_encoder_1_out), .Bit5_Out(bit5_inverter_5_bit5_out));
  Bit5_Inverter bit5_inverter_6 (.Bit5_In({bit5_add_one_1_bit5_out, 1'b0}), .Bit5_Out(bit5_inverter_6_bit5_out));
  Bit5_Twos_Complementer bit5_twos_complementer_1 (
    .Bit5_In(out_14), .Bit5_Result(bit5_twos_complementer_1_bit5_result));
  Bit5_Add_One bit5_add_one_1 (
    .Add_One(and_31_out), .Bit5_In(bit5_twos_complementer_1_bit5_result),
    .Bit5_Out({bit5_add_one_1_bit5_out_2[4], bit5_add_one_1_bit5_out}));  // open: Carry_Out
  Bit5_Controlled_Buffer bit5_controlled_buffer_9 (
    .Bit5_In(out_14), .Enable(nand_1_out), .Bit5_Out(bit5_controlled_buffer_9_bit5_out));
  or or_24 (or_24_out, divider_1_rem[11], divider_1_rem[0], divider_1_rem[1], divider_1_rem[2], divider_1_rem[3], divider_1_rem[4], divider_1_rem[5], divider_1_rem[6], divider_1_rem[7], divider_1_rem[8], divider_1_rem[9], divider_1_rem[10], divider_1_rem[12], divider_1_rem[13], divider_1_rem[14], divider_1_rem[15], divider_1_rem[16], divider_1_rem[17], divider_1_rem[18], divider_1_rem[19], divider_1_rem[20], divider_1_rem[21], divider_1_rem[22], divider_1_rem[23]);
  and and_36 (and_36_out, or_24_out, Div);
  or or_25 (or_25_out, Sub, or_23_out);
  assign or_26_out = bit5_controlled_buffer_7_bit5_out | bit5_controlled_buffer_5_bit5_out;  // OR_Gate or_26, 5 bits wide
  assign or_27_out = bit5_twos_complementer_2_bit5_result | bit5_controlled_buffer_9_bit5_out;  // OR_Gate or_27, 5 bits wide
  // Probe on undriven_2
  // Probe on undriven_2
  or or_28 (or_28_out, and_37_out, and_34_out);
  and and_37 (and_37_out, ~xor_8_out, bit24_adder_1_c_out);  // AND_Gate
  // Probe on or_32_out
  // Probe on or_32_out
  Bit5_Add_One bit5_add_one_2 (
    .Add_One(and_35_out), .Bit5_In(bit5_controlled_buffer_6_bit5_out), .Bit5_Out(bit5_add_one_2_bit5_out));  // open: Carry_Out
  Bit5_Twos_Complementer bit5_twos_complementer_2 (
    .Bit5_In({bit5_add_one_1_bit5_out_2[4], bit5_add_one_1_bit5_out}),
    .Bit5_Result(bit5_twos_complementer_2_bit5_result));
  and and_38 (and_38_out, Div, bit5_greater_than_1_a_greater_b);
  nand nand_2 (nand_2_out, Div, bit5_greater_than_1_a_greater_b);
  Bit5_Greater_Than bit5_greater_than_1 (
    .Bit5_A(bit5_controlled_buffer_6_bit5_out), .Bit5_B(undriven),
    .A_Greater_B(bit5_greater_than_1_a_greater_b));
  Bit5_Adder bit5_adder_10 (
    .Cin(or_28_out), .Bit5_A(bit5_toggle_twscmplmtr_6_bit5_result), .Bit5_B(or_27_out),
    .Bit5_Result(bit5_adder_10_bit5_result), .Cout(bit5_adder_10_cout));
  or or_29 (or_29_out, or_22_out, Div, Mul);
  Bit5_Toggle_TwsCmplmtr bit5_toggle_twscmplmtr_6 (
    .Bit5_Input(or_26_out), .Enable_Twos(or_25_out), .Bit5_Result(bit5_toggle_twscmplmtr_6_bit5_result));
  or or_30 (or_30_out, Div, or_22_out);
  and and_39 (and_39_out[15], or_30_out, or_15_out);
  Bit5_Controlled_Buffer bit5_controlled_buffer_10 (
    .Bit5_In(undriven_3), .Enable(and_38_out), .Bit5_Out(bit5_controlled_buffer_10_bit5_out));
  Bit5_Controlled_Buffer bit5_controlled_buffer_11 (
    .Bit5_In(bit5_controlled_buffer_6_bit5_out), .Enable(nand_2_out),
    .Bit5_Out(bit5_controlled_buffer_11_bit5_out));
  // Probe on {Mul, Div, 1'b0, Div, Mul}
  // Probe on {Mul, Div, 1'b0, Div, Mul}
  Bit32_Left_Shift bit32_left_shift_1 (
    .Bit32_In(or_18_out), .Bit5_Shift(bit5_add_one_2_bit5_out), .Bit32_Result(bit32_left_shift_1_bit32_result));
  Bit5_Controlled_Buffer bit5_controlled_buffer_12 (
    .Bit5_In(bit5_adder_10_bit5_result), .Enable(or_29_out), .Bit5_Out(bit5_controlled_buffer_12_bit5_out));
  // Probe on bit5_controlled_buffer_12_bit5_out
  // Probe on bit5_controlled_buffer_12_bit5_out
  // NAND_Gate nand_3 is placed but not wired
  or or_31 (or_31_out, and_36_out, bit32_left_shift_1_bit32_result[0], bit32_left_shift_1_bit32_result[1], bit32_left_shift_1_bit32_result[2], bit32_left_shift_1_bit32_result[3], bit32_left_shift_1_bit32_result[4], bit32_left_shift_1_bit32_result[5], bit32_left_shift_1_bit32_result[6], bit32_left_shift_1_bit32_result[7], bit32_left_shift_1_bit32_result[8], bit32_left_shift_1_bit32_result[9], bit32_left_shift_1_bit32_result[10], bit32_left_shift_1_bit32_result[11], bit32_left_shift_1_bit32_result[12], bit32_left_shift_1_bit32_result[13], bit32_left_shift_1_bit32_result[14], bit32_left_shift_1_bit32_result[15], bit32_left_shift_1_bit32_result[16], bit32_left_shift_1_bit32_result[17], bit32_left_shift_1_bit32_result[18], bit32_left_shift_1_bit32_result[19]);
  // NAND_Gate nand_4 has open pins: in3=and_40_out, out=open
  // AND_Gate and_40 has open pins: out=and_40_out
  assign or_32_out = bit5_controlled_buffer_10_bit5_out | bit5_controlled_buffer_11_bit5_out;  // OR_Gate or_32, 5 bits wide
  and and_41 (and_41_out, bit32_left_shift_1_bit32_result[21], or_33_out);
  or or_33 (or_33_out, or_31_out, bit32_left_shift_1_bit32_result[20]);
  // Probe on bit5_adder_11_bit5_result
  // Probe on bit5_adder_11_bit5_result
  Bit5_Adder bit5_adder_11 (
    .Bit5_A(bit5_controlled_buffer_12_bit5_out), .Bit5_B({Mul, Div, 1'b0, Div, Mul}),
    .Bit5_Result(bit5_adder_11_bit5_result), .Cout(bit5_adder_11_cout));  // open: Cin
  Bit10_Add_One bit10_add_one_1 (
    .Add_One(and_41_out), .Bit10_In(bit32_left_shift_1_bit32_result[31:22]),
    .Bit10_Out(bit10_add_one_1_bit10_out), .Carry_Out(bit10_add_one_1_carry_out));
  Bit5_Add_One bit5_add_one_3 (
    .Add_One(bit10_add_one_1_carry_out), .Bit5_In(bit5_adder_11_bit5_result),
    .Bit5_Out(bit5_add_one_3_bit5_out));  // open: Carry_Out
  // Probe on bit5_add_one_3_bit5_out
  // Probe on bit5_add_one_3_bit5_out
  nand nand_5 (nand_5_out, bit5_add_one_3_bit5_out[0], bit5_add_one_3_bit5_out[1], bit5_add_one_3_bit5_out[2], bit5_add_one_3_bit5_out[3], bit5_add_one_3_bit5_out[4]);
  Bit10_Controlled_Buffer bit10_controlled_buffer_1 (
    .Enable(1'b1), .Bit10_In(bit10_add_one_1_bit10_out), .Bit10_Out(bit10_controlled_buffer_1_bit10_out));
  // Probe on {and_39_out[15], bit5_add_one_3_bit5_out, bit10_controlled_buffer_1_bit10_out}
  // Probe on {and_39_out[15], bit5_add_one_3_bit5_out, bit10_controlled_buffer_1_bit10_out}

  assign out_16 = in_7[14:10];
  assign out_17 = in_8[14:10];
  assign out_24 = in_11;
  assign out_27 = in_12;

  // Notes on the sheet:
  //   snan
  //   qnan
  //   infinity
  //   zero
  //   snan
  //   qnan
  //   infinity
  //   zero
  //   sorts of nan!
  //   infinities
endmodule

module Bit4_Toggle_TwsCmplmtr (
  input  [3:0] Bit4_Input,
  input  Enable_Twos,
  output [3:0] Bit4_Result
);

  wire and_1_out, and_2_out, and_3_out, or_1_out, or_2_out;

  or or_1 (or_1_out, Bit4_Input[0], Bit4_Result[1]);
  or or_2 (or_2_out, Bit4_Input[0], Bit4_Result[1], Bit4_Result[2]);
  xor xor_1 (Bit4_Result[1], Bit4_Input[1], and_1_out);
  and and_1 (and_1_out, Enable_Twos, Bit4_Input[0]);
  xor xor_2 (Bit4_Result[2], Bit4_Input[2], and_2_out);
  and and_2 (and_2_out, Enable_Twos, or_1_out);
  xor xor_3 (Bit4_Result[3], Bit4_Input[3], and_3_out);
  and and_3 (and_3_out, Enable_Twos, or_2_out);

  assign Bit4_Result[0] = Bit4_Input[0];
endmodule

module Bit5_Toggle_TwsCmplmtr (
  input  [4:0] Bit5_Input,
  input  Enable_Twos,
  output [4:0] Bit5_Result
);

  wire and_1_out, and_2_out, and_3_out, and_4_out, or_1_out, or_2_out, or_3_out;

  or or_1 (or_1_out, Bit5_Input[0], Bit5_Result[1]);
  or or_2 (or_2_out, Bit5_Input[0], Bit5_Result[1], Bit5_Result[2]);
  or or_3 (or_3_out, Bit5_Result[3], Bit5_Result[2], Bit5_Result[1], Bit5_Input[0]);
  xor xor_1 (Bit5_Result[1], Bit5_Input[1], and_1_out);
  and and_1 (and_1_out, Enable_Twos, Bit5_Input[0]);
  xor xor_2 (Bit5_Result[2], Bit5_Input[2], and_2_out);
  and and_2 (and_2_out, Enable_Twos, or_1_out);
  xor xor_3 (Bit5_Result[3], Bit5_Input[3], and_3_out);
  and and_3 (and_3_out, Enable_Twos, or_2_out);
  and and_4 (and_4_out, Enable_Twos, or_3_out);
  xor xor_4 (Bit5_Result[4], Bit5_Input[4], and_4_out);

  assign Bit5_Result[0] = Bit5_Input[0];
endmodule

module Bit24_Toggle_TwsCmplmtr (
  input  Enable,
  input  [23:0] Bit24_In,
  output [23:0] Bit24_Out
);

  wire and_1_out, and_2_out, and_3_out, and_4_out, and_5_out, and_6_out, and_7_out, and_8_out, and_9_out,
       and_10_out, and_11_out, and_12_out, and_13_out, and_14_out, and_15_out, and_16_out, and_17_out,
       and_18_out, and_19_out, and_20_out, and_21_out, and_22_out, and_23_out, or_1_out, or_2_out, or_3_out,
       or_4_out, or_5_out, or_6_out, or_7_out, or_8_out, or_9_out, or_10_out, or_11_out, or_12_out,
       or_13_out, or_14_out, or_15_out, or_16_out, or_17_out, or_18_out, or_19_out, or_20_out, or_21_out,
       or_22_out;

  or or_1 (or_1_out, Bit24_In[0], Bit24_Out[1]);
  or or_2 (or_2_out, Bit24_In[0], Bit24_Out[1], Bit24_Out[2]);
  or or_3 (or_3_out, Bit24_In[0], Bit24_Out[1], Bit24_Out[2], Bit24_Out[3]);
  or or_4 (or_4_out, Bit24_In[0], Bit24_Out[1], Bit24_Out[2], Bit24_Out[3], Bit24_Out[4]);
  or or_5 (or_5_out, Bit24_In[0], Bit24_Out[1], Bit24_Out[2], Bit24_Out[3], Bit24_Out[4], Bit24_Out[5]);
  or or_6 (or_6_out, Bit24_In[0], Bit24_Out[1], Bit24_Out[2], Bit24_Out[3], Bit24_Out[4], Bit24_Out[5], Bit24_Out[6]);
  or or_7 (or_7_out, Bit24_In[0], Bit24_Out[1], Bit24_Out[2], Bit24_Out[3], Bit24_Out[4], Bit24_Out[5], Bit24_Out[6], Bit24_Out[7]);
  or or_8 (or_8_out, Bit24_In[0], Bit24_Out[1], Bit24_Out[2], Bit24_Out[3], Bit24_Out[4], Bit24_Out[5], Bit24_Out[6], Bit24_Out[7], Bit24_Out[8]);
  or or_9 (or_9_out, Bit24_In[0], Bit24_Out[1], Bit24_Out[2], Bit24_Out[3], Bit24_Out[4], Bit24_Out[5], Bit24_Out[6], Bit24_Out[7], Bit24_Out[8], Bit24_Out[9]);
  or or_10 (or_10_out, Bit24_In[0], Bit24_Out[1], Bit24_Out[2], Bit24_Out[3], Bit24_Out[4], Bit24_Out[5], Bit24_Out[6], Bit24_Out[7], Bit24_Out[8], Bit24_Out[9], Bit24_Out[10]);
  or or_11 (or_11_out, Bit24_In[0], Bit24_Out[1], Bit24_Out[2], Bit24_Out[3], Bit24_Out[4], Bit24_Out[5], Bit24_Out[6], Bit24_Out[7], Bit24_Out[8], Bit24_Out[9], Bit24_Out[10], Bit24_Out[11]);
  or or_12 (or_12_out, Bit24_In[0], Bit24_Out[1], Bit24_Out[2], Bit24_Out[3], Bit24_Out[4], Bit24_Out[5], Bit24_Out[6], Bit24_Out[7], Bit24_Out[8], Bit24_Out[9], Bit24_Out[10], Bit24_Out[11], Bit24_Out[12]);
  or or_13 (or_13_out, Bit24_In[0], Bit24_Out[1], Bit24_Out[2], Bit24_Out[3], Bit24_Out[4], Bit24_Out[5], Bit24_Out[6], Bit24_Out[7], Bit24_Out[8], Bit24_Out[9], Bit24_Out[10], Bit24_Out[11], Bit24_Out[12], Bit24_Out[13]);
  or or_14 (or_14_out, Bit24_In[0], Bit24_Out[1], Bit24_Out[2], Bit24_Out[3], Bit24_Out[4], Bit24_Out[5], Bit24_Out[6], Bit24_Out[7], Bit24_Out[8], Bit24_Out[9], Bit24_Out[10], Bit24_Out[11], Bit24_Out[12], Bit24_Out[13], Bit24_Out[14]);
  or or_15 (or_15_out, Bit24_In[0], Bit24_Out[1], Bit24_Out[2], Bit24_Out[3], Bit24_Out[4], Bit24_Out[5], Bit24_Out[6], Bit24_Out[7], Bit24_Out[8], Bit24_Out[9], Bit24_Out[10], Bit24_Out[11], Bit24_Out[12], Bit24_Out[13], Bit24_Out[14], Bit24_Out[15]);
  or or_16 (or_16_out, Bit24_In[0], Bit24_Out[1], Bit24_Out[2], Bit24_Out[3], Bit24_Out[4], Bit24_Out[5], Bit24_Out[6], Bit24_Out[7], Bit24_Out[8], Bit24_Out[9], Bit24_Out[10], Bit24_Out[11], Bit24_Out[12], Bit24_Out[13], Bit24_Out[14], Bit24_Out[15], Bit24_Out[16]);
  or or_17 (or_17_out, Bit24_In[0], Bit24_Out[1], Bit24_Out[2], Bit24_Out[3], Bit24_Out[4], Bit24_Out[5], Bit24_Out[6], Bit24_Out[7], Bit24_Out[8], Bit24_Out[9], Bit24_Out[10], Bit24_Out[11], Bit24_Out[12], Bit24_Out[13], Bit24_Out[14], Bit24_Out[15], Bit24_Out[16], Bit24_Out[17]);
  or or_18 (or_18_out, Bit24_In[0], Bit24_Out[1], Bit24_Out[2], Bit24_Out[3], Bit24_Out[4], Bit24_Out[5], Bit24_Out[6], Bit24_Out[7], Bit24_Out[8], Bit24_Out[9], Bit24_Out[10], Bit24_Out[11], Bit24_Out[12], Bit24_Out[13], Bit24_Out[14], Bit24_Out[15], Bit24_Out[16], Bit24_Out[17], Bit24_Out[18]);
  or or_19 (or_19_out, Bit24_In[0], Bit24_Out[1], Bit24_Out[2], Bit24_Out[3], Bit24_Out[4], Bit24_Out[5], Bit24_Out[6], Bit24_Out[7], Bit24_Out[8], Bit24_Out[9], Bit24_Out[10], Bit24_Out[11], Bit24_Out[12], Bit24_Out[13], Bit24_Out[14], Bit24_Out[15], Bit24_Out[16], Bit24_Out[17], Bit24_Out[18], Bit24_Out[19]);
  or or_20 (or_20_out, Bit24_In[0], Bit24_Out[1], Bit24_Out[2], Bit24_Out[3], Bit24_Out[4], Bit24_Out[5], Bit24_Out[6], Bit24_Out[7], Bit24_Out[8], Bit24_Out[9], Bit24_Out[10], Bit24_Out[11], Bit24_Out[12], Bit24_Out[13], Bit24_Out[14], Bit24_Out[15], Bit24_Out[16], Bit24_Out[17], Bit24_Out[18], Bit24_Out[19], Bit24_Out[20]);
  or or_21 (or_21_out, Bit24_In[0], Bit24_Out[1], Bit24_Out[2], Bit24_Out[3], Bit24_Out[4], Bit24_Out[5], Bit24_Out[6], Bit24_Out[7], Bit24_Out[8], Bit24_Out[9], Bit24_Out[10], Bit24_Out[11], Bit24_Out[12], Bit24_Out[13], Bit24_Out[14], Bit24_Out[15], Bit24_Out[16], Bit24_Out[17], Bit24_Out[18], Bit24_Out[19], Bit24_Out[20], Bit24_Out[21]);
  or or_22 (or_22_out, Bit24_In[0], Bit24_Out[1], Bit24_Out[2], Bit24_Out[3], Bit24_Out[4], Bit24_Out[5], Bit24_Out[6], Bit24_Out[7], Bit24_Out[8], Bit24_Out[9], Bit24_Out[10], Bit24_Out[11], Bit24_Out[12], Bit24_Out[13], Bit24_Out[14], Bit24_Out[15], Bit24_Out[16], Bit24_Out[17], Bit24_Out[18], Bit24_Out[19], Bit24_Out[20], Bit24_Out[21], Bit24_Out[22]);
  xor xor_1 (Bit24_Out[1], Bit24_In[1], and_1_out);
  and and_1 (and_1_out, Bit24_In[0], Enable);
  xor xor_2 (Bit24_Out[2], Bit24_In[2], and_2_out);
  and and_2 (and_2_out, or_1_out, Enable);
  xor xor_3 (Bit24_Out[3], Bit24_In[3], and_3_out);
  and and_3 (and_3_out, or_2_out, Enable);
  xor xor_4 (Bit24_Out[4], Bit24_In[4], and_4_out);
  and and_4 (and_4_out, Enable, or_3_out);
  xor xor_5 (Bit24_Out[5], Bit24_In[5], and_5_out);
  and and_5 (and_5_out, Enable, or_4_out);
  xor xor_6 (Bit24_Out[6], Bit24_In[6], and_6_out);
  and and_6 (and_6_out, Enable, or_5_out);
  xor xor_7 (Bit24_Out[7], Bit24_In[7], and_7_out);
  and and_7 (and_7_out, Enable, or_6_out);
  xor xor_8 (Bit24_Out[8], Bit24_In[8], and_8_out);
  and and_8 (and_8_out, Enable, or_7_out);
  xor xor_9 (Bit24_Out[9], Bit24_In[9], and_9_out);
  and and_9 (and_9_out, Enable, or_8_out);
  xor xor_10 (Bit24_Out[10], Bit24_In[10], and_10_out);
  and and_10 (and_10_out, Enable, or_9_out);
  xor xor_11 (Bit24_Out[11], Bit24_In[11], and_11_out);
  and and_11 (and_11_out, Enable, or_10_out);
  xor xor_12 (Bit24_Out[12], Bit24_In[12], and_12_out);
  and and_12 (and_12_out, Enable, or_11_out);
  xor xor_13 (Bit24_Out[13], Bit24_In[13], and_13_out);
  and and_13 (and_13_out, Enable, or_12_out);
  xor xor_14 (Bit24_Out[14], Bit24_In[14], and_14_out);
  and and_14 (and_14_out, Enable, or_13_out);
  xor xor_15 (Bit24_Out[15], Bit24_In[15], and_15_out);
  and and_15 (and_15_out, Enable, or_14_out);
  xor xor_16 (Bit24_Out[16], Bit24_In[16], and_16_out);
  and and_16 (and_16_out, Enable, or_15_out);
  xor xor_17 (Bit24_Out[17], Bit24_In[17], and_17_out);
  and and_17 (and_17_out, Enable, or_16_out);
  xor xor_18 (Bit24_Out[18], Bit24_In[18], and_18_out);
  and and_18 (and_18_out, Enable, or_17_out);
  xor xor_19 (Bit24_Out[19], Bit24_In[19], and_19_out);
  and and_19 (and_19_out, Enable, or_18_out);
  xor xor_20 (Bit24_Out[20], Bit24_In[20], and_20_out);
  and and_20 (and_20_out, Enable, or_19_out);
  xor xor_21 (Bit24_Out[21], Bit24_In[21], and_21_out);
  and and_21 (and_21_out, Enable, or_20_out);
  xor xor_22 (Bit24_Out[22], Bit24_In[22], and_22_out);
  and and_22 (and_22_out, Enable, or_21_out);
  xor xor_23 (Bit24_Out[23], Bit24_In[23], and_23_out);
  and and_23 (and_23_out, Enable, or_22_out);

  assign Bit24_Out[0] = Bit24_In[0];
endmodule

module Bit24_Inverter (
  input  [23:0] Bit24_In,
  output [23:0] Bit24_Out
);

  not not_1 (Bit24_Out[0], Bit24_In[0]);
  not not_2 (Bit24_Out[1], Bit24_In[1]);
  not not_3 (Bit24_Out[2], Bit24_In[2]);
  not not_4 (Bit24_Out[3], Bit24_In[3]);
  not not_5 (Bit24_Out[4], Bit24_In[4]);
  not not_6 (Bit24_Out[5], Bit24_In[5]);
  not not_7 (Bit24_Out[6], Bit24_In[6]);
  not not_8 (Bit24_Out[7], Bit24_In[7]);
  not not_9 (Bit24_Out[8], Bit24_In[8]);
  not not_10 (Bit24_Out[9], Bit24_In[9]);
  not not_11 (Bit24_Out[10], Bit24_In[10]);
  not not_12 (Bit24_Out[11], Bit24_In[11]);
  not not_13 (Bit24_Out[12], Bit24_In[12]);
  not not_14 (Bit24_Out[13], Bit24_In[13]);
  not not_15 (Bit24_Out[14], Bit24_In[14]);
  not not_16 (Bit24_Out[15], Bit24_In[15]);
  not not_17 (Bit24_Out[16], Bit24_In[16]);
  not not_18 (Bit24_Out[17], Bit24_In[17]);
  not not_19 (Bit24_Out[18], Bit24_In[18]);
  not not_20 (Bit24_Out[19], Bit24_In[19]);
  not not_21 (Bit24_Out[20], Bit24_In[20]);
  not not_22 (Bit24_Out[21], Bit24_In[21]);
  not not_23 (Bit24_Out[22], Bit24_In[22]);
  not not_24 (Bit24_Out[23], Bit24_In[23]);
endmodule

module Bit4_Inverter (
  input  [3:0] Bit4_In,
  output [3:0] Bit4_Out
);

  not not_1 (Bit4_Out[0], Bit4_In[0]);
  not not_2 (Bit4_Out[1], Bit4_In[1]);
  not not_3 (Bit4_Out[2], Bit4_In[2]);
  not not_4 (Bit4_Out[3], Bit4_In[3]);
endmodule

module Bit5_Inverter (
  input  [4:0] Bit5_In,
  output [4:0] Bit5_Out
);

  not not_1 (Bit5_Out[0], Bit5_In[0]);
  not not_2 (Bit5_Out[1], Bit5_In[1]);
  not not_3 (Bit5_Out[2], Bit5_In[2]);
  not not_4 (Bit5_Out[3], Bit5_In[3]);
  not not_5 (Bit5_Out[4], Bit5_In[4]);
endmodule

module Bit11_To_Bit16_High (
  input  [10:0] Bit11_In,
  output [15:0] Bit16_Out
);


  assign Bit16_Out = {Bit11_In, {5{1'b0}}};
endmodule

module Bit11_Controlled_Buffer (
  input  Enable,
  input  [10:0] Bit11_In,
  output [10:0] Bit11_Out
);

  and and_1 (Bit11_Out[0], Bit11_In[0], Enable);
  and and_2 (Bit11_Out[1], Bit11_In[1], Enable);
  and and_3 (Bit11_Out[2], Bit11_In[2], Enable);
  and and_4 (Bit11_Out[3], Bit11_In[3], Enable);
  and and_5 (Bit11_Out[4], Bit11_In[4], Enable);
  and and_6 (Bit11_Out[5], Bit11_In[5], Enable);
  and and_7 (Bit11_Out[6], Bit11_In[6], Enable);
  and and_8 (Bit11_Out[7], Bit11_In[7], Enable);
  and and_9 (Bit11_Out[8], Bit11_In[8], Enable);
  and and_10 (Bit11_Out[9], Bit11_In[9], Enable);
  and and_11 (Bit11_Out[10], Bit11_In[10], Enable);
endmodule

module Bit32_Left_Shift (
  input  [31:0] Bit32_In,
  input  [4:0] Bit5_Shift,
  output [31:0] Bit32_Result
);

  wire and_2_out, and_3_out, and_4_out, and_5_out, and_6_out, and_7_out, and_8_out, and_9_out, and_10_out,
       and_11_out, and_12_out, and_13_out, and_14_out, and_15_out, and_16_out, and_17_out, and_18_out,
       and_19_out, and_20_out, and_21_out, and_22_out, and_23_out, and_24_out, and_25_out, and_26_out,
       and_27_out, and_28_out, and_29_out, and_30_out, and_31_out, and_32_out, and_33_out, and_34_out,
       and_35_out, and_36_out, and_37_out, and_38_out, and_39_out, and_40_out, and_41_out, and_42_out,
       and_43_out, and_44_out, and_45_out, and_46_out, and_47_out, and_48_out, and_49_out, and_50_out,
       and_51_out, and_52_out, and_53_out, and_54_out, and_55_out, and_56_out, and_57_out, and_58_out,
       and_59_out, and_60_out, and_61_out, and_62_out, and_63_out, and_64_out, and_65_out, and_66_out,
       and_67_out, and_68_out, and_69_out, and_70_out, and_71_out, and_72_out, and_73_out, and_74_out,
       and_75_out, and_76_out, and_77_out, and_78_out, and_79_out, and_80_out, and_81_out, and_82_out,
       and_83_out, and_84_out, and_85_out, and_86_out, and_87_out, and_88_out, and_89_out, and_90_out,
       and_91_out, and_92_out, and_93_out, and_94_out, and_95_out, and_96_out, and_97_out, and_98_out,
       and_99_out, and_100_out, and_101_out, and_102_out, and_103_out, and_104_out, and_105_out, and_106_out,
       and_107_out, and_108_out, and_109_out, and_110_out, and_111_out, and_112_out, and_113_out,
       and_114_out, and_115_out, and_116_out, and_117_out, and_118_out, and_119_out, and_120_out,
       and_121_out, and_122_out, and_123_out, and_124_out, and_125_out, and_126_out, and_127_out,
       and_128_out, and_129_out, and_130_out, and_131_out, and_132_out, and_133_out, and_134_out,
       and_135_out, and_136_out, and_137_out, and_138_out, and_139_out, and_140_out, and_141_out,
       and_143_out, and_144_out, and_145_out, and_146_out, and_147_out, and_148_out, and_149_out,
       and_150_out, and_152_out, and_153_out, and_154_out, and_155_out, and_156_out, and_157_out,
       and_158_out, and_159_out, and_161_out, and_162_out, and_163_out, and_164_out, and_165_out,
       and_166_out, and_167_out, and_168_out, and_169_out, and_171_out, and_172_out, and_173_out,
       and_174_out, and_175_out, and_176_out, and_177_out, and_178_out, and_180_out, and_181_out,
       and_182_out, and_183_out, and_184_out, and_185_out, and_186_out, and_187_out, and_189_out,
       and_190_out, and_191_out, and_192_out, and_193_out, and_194_out, and_195_out, and_196_out,
       and_198_out, and_199_out, and_200_out, and_201_out, and_202_out, and_203_out, and_204_out,
       and_205_out, and_207_out, and_208_out, and_209_out, and_210_out, and_211_out, and_212_out,
       and_213_out, and_214_out, and_215_out, and_216_out, and_217_out, and_218_out, and_219_out,
       and_220_out, and_221_out, and_223_out, and_224_out, and_225_out, and_226_out, and_227_out,
       and_228_out, and_229_out, and_230_out, and_232_out, and_233_out, and_234_out, and_235_out,
       and_236_out, and_237_out, and_238_out, and_239_out, and_241_out, and_242_out, and_243_out,
       and_244_out, and_245_out, and_246_out, and_247_out, and_248_out, and_249_out, and_251_out,
       and_252_out, and_253_out, and_254_out, and_255_out, and_256_out, and_257_out, and_258_out,
       and_260_out, and_261_out, and_262_out, and_263_out, and_264_out, and_265_out, and_266_out,
       and_267_out, and_269_out, and_270_out, and_271_out, and_272_out, and_273_out, and_274_out,
       and_275_out, and_276_out, and_278_out, and_279_out, and_280_out, and_281_out, and_282_out,
       and_283_out, and_284_out, and_285_out, and_287_out, and_288_out, and_289_out, and_290_out, or_1_out,
       or_2_out, or_3_out, or_4_out, or_6_out, or_7_out, or_8_out, or_9_out, or_11_out, or_12_out, or_13_out,
       or_14_out, or_16_out, or_17_out, or_18_out, or_20_out, or_21_out, or_22_out, or_24_out, or_25_out,
       or_26_out, or_28_out, or_29_out, or_30_out, or_32_out, or_33_out, or_34_out, or_35_out, or_36_out,
       or_37_out, or_38_out, or_39_out, or_41_out, or_42_out, or_43_out, or_44_out, or_46_out, or_47_out,
       or_48_out, or_49_out, or_51_out, or_52_out, or_53_out, or_54_out, or_56_out, or_57_out, or_58_out,
       or_60_out, or_61_out, or_62_out, or_64_out, or_65_out, or_66_out, or_68_out, or_69_out, or_70_out,
       or_72_out, or_73_out, or_74_out, or_75_out, or_76_out, or_77_out, or_78_out, or_79_out, or_81_out,
       or_82_out, or_83_out, or_84_out, or_85_out, or_86_out, or_87_out, or_88_out, or_89_out, or_90_out,
       or_91_out, or_92_out, or_93_out, or_94_out, or_95_out, or_96_out, or_97_out, or_98_out, or_99_out,
       or_100_out, or_101_out, or_102_out, or_103_out, or_104_out, or_105_out, or_106_out, or_107_out,
       or_108_out, or_109_out, or_110_out, or_111_out, or_112_out, or_113_out, or_114_out, or_115_out,
       or_116_out, or_117_out, or_118_out, or_119_out, or_120_out, or_121_out, or_122_out, or_123_out,
       or_124_out, or_125_out, or_126_out, or_127_out, or_128_out, or_129_out;

  // AND_Gate and_1 has open pins: in0=Bit5_Shift[0], in1=Bit32_In[31], out=open
  and and_2 (and_2_out, ~Bit5_Shift[0], Bit32_In[31]);  // AND_Gate
  or or_1 (or_1_out, and_2_out, and_7_out);
  and and_3 (and_3_out, ~Bit5_Shift[1], or_1_out);  // AND_Gate
  or or_2 (or_2_out, and_3_out, and_15_out);
  and and_4 (and_4_out, ~Bit5_Shift[2], or_2_out);  // AND_Gate
  or or_3 (or_3_out, and_4_out, and_30_out);
  and and_5 (and_5_out, ~Bit5_Shift[3], or_3_out);  // AND_Gate
  or or_4 (or_4_out, and_5_out, and_61_out);
  and and_6 (and_6_out, ~Bit5_Shift[4], or_4_out);  // AND_Gate
  or or_5 (Bit32_Result[31], and_6_out, and_134_out);
  and and_7 (and_7_out, Bit5_Shift[0], Bit32_In[30]);
  and and_8 (and_8_out, ~Bit5_Shift[0], Bit32_In[30]);  // AND_Gate
  or or_6 (or_6_out, and_8_out, and_13_out);
  and and_9 (and_9_out, ~Bit5_Shift[1], or_6_out);  // AND_Gate
  or or_7 (or_7_out, and_9_out, and_22_out);
  and and_10 (and_10_out, ~Bit5_Shift[2], or_7_out);  // AND_Gate
  or or_8 (or_8_out, and_10_out, and_37_out);
  and and_11 (and_11_out, ~Bit5_Shift[3], or_8_out);  // AND_Gate
  or or_9 (or_9_out, and_11_out, and_68_out);
  and and_12 (and_12_out, ~Bit5_Shift[4], or_9_out);  // AND_Gate
  or or_10 (Bit32_Result[30], and_12_out, and_143_out);
  and and_13 (and_13_out, Bit5_Shift[0], Bit32_In[29]);
  and and_14 (and_14_out, ~Bit5_Shift[0], Bit32_In[29]);  // AND_Gate
  or or_11 (or_11_out, and_14_out, and_20_out);
  and and_15 (and_15_out, Bit5_Shift[1], or_11_out);
  and and_16 (and_16_out, ~Bit5_Shift[1], or_11_out);  // AND_Gate
  or or_12 (or_12_out, and_16_out, and_28_out);
  and and_17 (and_17_out, ~Bit5_Shift[2], or_12_out);  // AND_Gate
  or or_13 (or_13_out, and_17_out, and_45_out);
  and and_18 (and_18_out, ~Bit5_Shift[3], or_13_out);  // AND_Gate
  or or_14 (or_14_out, and_18_out, and_76_out);
  and and_19 (and_19_out, ~Bit5_Shift[4], or_14_out);  // AND_Gate
  or or_15 (Bit32_Result[29], and_19_out, and_152_out);
  and and_20 (and_20_out, Bit5_Shift[0], Bit32_In[28]);
  and and_21 (and_21_out, ~Bit5_Shift[0], Bit32_In[28]);  // AND_Gate
  and and_22 (and_22_out, Bit5_Shift[1], or_20_out);
  and and_23 (and_23_out, ~Bit5_Shift[1], or_20_out);  // AND_Gate
  or or_16 (or_16_out, and_23_out, and_36_out);
  and and_24 (and_24_out, ~Bit5_Shift[2], or_16_out);  // AND_Gate
  or or_17 (or_17_out, and_24_out, and_52_out);
  and and_25 (and_25_out, ~Bit5_Shift[3], or_17_out);  // AND_Gate
  or or_18 (or_18_out, and_25_out, and_92_out);
  and and_26 (and_26_out, ~Bit5_Shift[4], or_18_out);  // AND_Gate
  or or_19 (Bit32_Result[28], and_26_out, and_161_out);
  and and_27 (and_27_out, Bit5_Shift[0], Bit32_In[27]);
  or or_20 (or_20_out, and_21_out, and_27_out);
  and and_28 (and_28_out, Bit5_Shift[1], or_24_out);
  and and_29 (and_29_out, ~Bit5_Shift[1], or_24_out);  // AND_Gate
  and and_30 (and_30_out, Bit5_Shift[2], or_25_out);
  and and_31 (and_31_out, ~Bit5_Shift[2], or_25_out);  // AND_Gate
  or or_21 (or_21_out, and_31_out, and_59_out);
  and and_32 (and_32_out, ~Bit5_Shift[3], or_21_out);  // AND_Gate
  or or_22 (or_22_out, and_32_out, and_100_out);
  and and_33 (and_33_out, ~Bit5_Shift[4], or_22_out);  // AND_Gate
  or or_23 (Bit32_Result[27], and_33_out, and_178_out);
  and and_34 (and_34_out, ~Bit5_Shift[0], Bit32_In[27]);  // AND_Gate
  and and_35 (and_35_out, Bit5_Shift[0], Bit32_In[26]);
  or or_24 (or_24_out, and_34_out, and_35_out);
  and and_36 (and_36_out, Bit5_Shift[1], or_28_out);
  or or_25 (or_25_out, and_29_out, and_44_out);
  and and_37 (and_37_out, Bit5_Shift[2], or_29_out);
  and and_38 (and_38_out, ~Bit5_Shift[2], or_29_out);  // AND_Gate
  and and_39 (and_39_out, ~Bit5_Shift[3], or_30_out);  // AND_Gate
  or or_26 (or_26_out, and_39_out, and_108_out);
  and and_40 (and_40_out, ~Bit5_Shift[4], or_26_out);  // AND_Gate
  or or_27 (Bit32_Result[26], and_40_out, and_187_out);
  and and_41 (and_41_out, ~Bit5_Shift[0], Bit32_In[26]);  // AND_Gate
  and and_42 (and_42_out, Bit5_Shift[0], Bit32_In[25]);
  or or_28 (or_28_out, and_41_out, and_42_out);
  and and_43 (and_43_out, ~Bit5_Shift[1], or_28_out);  // AND_Gate
  and and_44 (and_44_out, Bit5_Shift[1], or_32_out);
  or or_29 (or_29_out, and_43_out, and_50_out);
  and and_45 (and_45_out, Bit5_Shift[2], or_33_out);
  or or_30 (or_30_out, and_38_out, and_66_out);
  and and_46 (and_46_out, ~Bit5_Shift[3], or_34_out);  // AND_Gate
  and and_47 (and_47_out, ~Bit5_Shift[4], or_35_out);  // AND_Gate
  or or_31 (Bit32_Result[25], and_47_out, and_196_out);
  and and_48 (and_48_out, Bit5_Shift[0], Bit32_In[24]);
  and and_49 (and_49_out, ~Bit5_Shift[0], Bit32_In[25]);  // AND_Gate
  or or_32 (or_32_out, and_49_out, and_48_out);
  and and_50 (and_50_out, Bit5_Shift[1], or_36_out);
  and and_51 (and_51_out, ~Bit5_Shift[1], or_32_out);  // AND_Gate
  or or_33 (or_33_out, and_51_out, and_57_out);
  and and_52 (and_52_out, Bit5_Shift[2], or_37_out);
  and and_53 (and_53_out, ~Bit5_Shift[2], or_33_out);  // AND_Gate
  or or_34 (or_34_out, and_53_out, and_82_out);
  or or_35 (or_35_out, and_46_out, and_116_out);
  and and_54 (and_54_out, ~Bit5_Shift[4], or_39_out);  // AND_Gate
  and and_55 (and_55_out, ~Bit5_Shift[0], Bit32_In[24]);  // AND_Gate
  or or_36 (or_36_out, and_55_out, and_62_out);
  and and_56 (and_56_out, ~Bit5_Shift[1], or_36_out);  // AND_Gate
  and and_57 (and_57_out, Bit5_Shift[1], or_41_out);
  or or_37 (or_37_out, and_56_out, and_72_out);
  and and_58 (and_58_out, ~Bit5_Shift[2], or_37_out);  // AND_Gate
  and and_59 (and_59_out, Bit5_Shift[2], or_42_out);
  or or_38 (or_38_out, and_58_out, and_90_out);
  and and_60 (and_60_out, ~Bit5_Shift[3], or_38_out);  // AND_Gate
  and and_61 (and_61_out, Bit5_Shift[3], or_43_out);
  or or_39 (or_39_out, and_60_out, and_125_out);
  or or_40 (Bit32_Result[24], and_54_out, and_205_out);
  and and_62 (and_62_out, Bit5_Shift[0], Bit32_In[23]);
  and and_63 (and_63_out, ~Bit5_Shift[0], Bit32_In[23]);  // AND_Gate
  or or_41 (or_41_out, and_63_out, and_70_out);
  and and_64 (and_64_out, ~Bit5_Shift[1], or_41_out);  // AND_Gate
  or or_42 (or_42_out, and_64_out, and_80_out);
  and and_65 (and_65_out, ~Bit5_Shift[2], or_42_out);  // AND_Gate
  and and_66 (and_66_out, Bit5_Shift[2], or_47_out);
  or or_43 (or_43_out, and_65_out, and_98_out);
  and and_67 (and_67_out, ~Bit5_Shift[3], or_43_out);  // AND_Gate
  and and_68 (and_68_out, Bit5_Shift[3], or_48_out);
  or or_44 (or_44_out, and_67_out, and_133_out);
  and and_69 (and_69_out, ~Bit5_Shift[4], or_44_out);  // AND_Gate
  or or_45 (Bit32_Result[23], and_69_out, and_214_out);
  and and_70 (and_70_out, Bit5_Shift[0], Bit32_In[22]);
  and and_71 (and_71_out, ~Bit5_Shift[0], Bit32_In[22]);  // AND_Gate
  or or_46 (or_46_out, and_71_out, and_78_out);
  and and_72 (and_72_out, Bit5_Shift[1], or_46_out);
  and and_73 (and_73_out, ~Bit5_Shift[1], or_46_out);  // AND_Gate
  or or_47 (or_47_out, and_73_out, and_88_out);
  and and_74 (and_74_out, ~Bit5_Shift[2], or_47_out);  // AND_Gate
  or or_48 (or_48_out, and_74_out, and_106_out);
  and and_75 (and_75_out, ~Bit5_Shift[3], or_48_out);  // AND_Gate
  and and_76 (and_76_out, Bit5_Shift[3], or_53_out);
  or or_49 (or_49_out, and_75_out, and_141_out);
  and and_77 (and_77_out, ~Bit5_Shift[4], or_49_out);  // AND_Gate
  or or_50 (Bit32_Result[22], and_77_out, and_223_out);
  and and_78 (and_78_out, Bit5_Shift[0], Bit32_In[21]);
  and and_79 (and_79_out, ~Bit5_Shift[0], Bit32_In[21]);  // AND_Gate
  or or_51 (or_51_out, and_79_out, and_86_out);
  and and_80 (and_80_out, Bit5_Shift[1], or_51_out);
  and and_81 (and_81_out, ~Bit5_Shift[1], or_51_out);  // AND_Gate
  or or_52 (or_52_out, and_81_out, and_96_out);
  and and_82 (and_82_out, Bit5_Shift[2], or_52_out);
  and and_83 (and_83_out, ~Bit5_Shift[2], or_52_out);  // AND_Gate
  or or_53 (or_53_out, and_83_out, and_115_out);
  and and_84 (and_84_out, ~Bit5_Shift[3], or_53_out);  // AND_Gate
  or or_54 (or_54_out, and_84_out, and_150_out);
  and and_85 (and_85_out, ~Bit5_Shift[4], or_54_out);  // AND_Gate
  or or_55 (Bit32_Result[21], and_85_out, and_232_out);
  and and_86 (and_86_out, Bit5_Shift[0], Bit32_In[20]);
  and and_87 (and_87_out, ~Bit5_Shift[0], Bit32_In[20]);  // AND_Gate
  and and_88 (and_88_out, Bit5_Shift[1], or_60_out);
  and and_89 (and_89_out, ~Bit5_Shift[1], or_60_out);  // AND_Gate
  or or_56 (or_56_out, and_89_out, and_105_out);
  and and_90 (and_90_out, Bit5_Shift[2], or_56_out);
  and and_91 (and_91_out, ~Bit5_Shift[2], or_56_out);  // AND_Gate
  or or_57 (or_57_out, and_91_out, and_124_out);
  and and_92 (and_92_out, Bit5_Shift[3], or_57_out);
  and and_93 (and_93_out, ~Bit5_Shift[3], or_57_out);  // AND_Gate
  or or_58 (or_58_out, and_93_out, and_168_out);
  and and_94 (and_94_out, ~Bit5_Shift[4], or_58_out);  // AND_Gate
  or or_59 (Bit32_Result[20], and_94_out, and_241_out);
  and and_95 (and_95_out, Bit5_Shift[0], Bit32_In[19]);
  or or_60 (or_60_out, and_87_out, and_95_out);
  and and_96 (and_96_out, Bit5_Shift[1], or_64_out);
  and and_97 (and_97_out, ~Bit5_Shift[1], or_64_out);  // AND_Gate
  and and_98 (and_98_out, Bit5_Shift[2], or_65_out);
  and and_99 (and_99_out, ~Bit5_Shift[2], or_65_out);  // AND_Gate
  or or_61 (or_61_out, and_99_out, and_131_out);
  and and_100 (and_100_out, Bit5_Shift[3], or_61_out);
  and and_101 (and_101_out, ~Bit5_Shift[3], or_61_out);  // AND_Gate
  or or_62 (or_62_out, and_101_out, and_176_out);
  and and_102 (and_102_out, ~Bit5_Shift[4], or_62_out);  // AND_Gate
  or or_63 (Bit32_Result[19], and_102_out, and_258_out);
  and and_103 (and_103_out, ~Bit5_Shift[0], Bit32_In[19]);  // AND_Gate
  and and_104 (and_104_out, Bit5_Shift[0], Bit32_In[18]);
  or or_64 (or_64_out, and_103_out, and_104_out);
  and and_105 (and_105_out, Bit5_Shift[1], or_68_out);
  or or_65 (or_65_out, and_97_out, and_114_out);
  and and_106 (and_106_out, Bit5_Shift[2], or_69_out);
  and and_107 (and_107_out, ~Bit5_Shift[2], or_69_out);  // AND_Gate
  and and_108 (and_108_out, Bit5_Shift[3], or_70_out);
  and and_109 (and_109_out, ~Bit5_Shift[3], or_70_out);  // AND_Gate
  or or_66 (or_66_out, and_109_out, and_185_out);
  and and_110 (and_110_out, ~Bit5_Shift[4], or_66_out);  // AND_Gate
  or or_67 (Bit32_Result[18], and_110_out, and_267_out);
  and and_111 (and_111_out, ~Bit5_Shift[0], Bit32_In[18]);  // AND_Gate
  and and_112 (and_112_out, Bit5_Shift[0], Bit32_In[17]);
  or or_68 (or_68_out, and_111_out, and_112_out);
  and and_113 (and_113_out, ~Bit5_Shift[1], or_68_out);  // AND_Gate
  and and_114 (and_114_out, Bit5_Shift[1], or_72_out);
  or or_69 (or_69_out, and_113_out, and_122_out);
  and and_115 (and_115_out, Bit5_Shift[2], or_73_out);
  or or_70 (or_70_out, and_107_out, and_139_out);
  and and_116 (and_116_out, Bit5_Shift[3], or_74_out);
  and and_117 (and_117_out, ~Bit5_Shift[3], or_74_out);  // AND_Gate
  and and_118 (and_118_out, ~Bit5_Shift[4], or_75_out);  // AND_Gate
  or or_71 (Bit32_Result[17], and_118_out, and_276_out);
  and and_119 (and_119_out, ~Bit5_Shift[0], Bit32_In[17]);  // AND_Gate
  and and_120 (and_120_out, Bit5_Shift[0], Bit32_In[16]);
  or or_72 (or_72_out, and_119_out, and_120_out);
  and and_121 (and_121_out, ~Bit5_Shift[1], or_72_out);  // AND_Gate
  and and_122 (and_122_out, Bit5_Shift[1], or_76_out);
  or or_73 (or_73_out, and_121_out, and_129_out);
  and and_123 (and_123_out, ~Bit5_Shift[2], or_73_out);  // AND_Gate
  and and_124 (and_124_out, Bit5_Shift[2], or_77_out);
  or or_74 (or_74_out, and_123_out, and_157_out);
  and and_125 (and_125_out, Bit5_Shift[3], or_78_out);
  or or_75 (or_75_out, and_117_out, and_194_out);
  and and_126 (and_126_out, ~Bit5_Shift[4], or_79_out);  // AND_Gate
  and and_127 (and_127_out, ~Bit5_Shift[0], Bit32_In[16]);  // AND_Gate
  or or_76 (or_76_out, and_127_out, and_135_out);
  and and_128 (and_128_out, ~Bit5_Shift[1], or_76_out);  // AND_Gate
  and and_129 (and_129_out, Bit5_Shift[1], or_81_out);
  or or_77 (or_77_out, and_128_out, and_146_out);
  and and_130 (and_130_out, ~Bit5_Shift[2], or_77_out);  // AND_Gate
  and and_131 (and_131_out, Bit5_Shift[2], or_82_out);
  or or_78 (or_78_out, and_130_out, and_166_out);
  and and_132 (and_132_out, ~Bit5_Shift[3], or_78_out);  // AND_Gate
  and and_133 (and_133_out, Bit5_Shift[3], or_83_out);
  or or_79 (or_79_out, and_132_out, and_204_out);
  and and_134 (and_134_out, Bit5_Shift[4], or_84_out);
  or or_80 (Bit32_Result[16], and_126_out, and_285_out);
  and and_135 (and_135_out, Bit5_Shift[0], Bit32_In[15]);
  and and_136 (and_136_out, ~Bit5_Shift[0], Bit32_In[15]);  // AND_Gate
  or or_81 (or_81_out, and_136_out, and_144_out);
  and and_137 (and_137_out, ~Bit5_Shift[1], or_81_out);  // AND_Gate
  or or_82 (or_82_out, and_137_out, and_155_out);
  and and_138 (and_138_out, ~Bit5_Shift[2], or_82_out);  // AND_Gate
  and and_139 (and_139_out, Bit5_Shift[2], or_86_out);
  or or_83 (or_83_out, and_138_out, and_174_out);
  and and_140 (and_140_out, ~Bit5_Shift[3], or_83_out);  // AND_Gate
  and and_141 (and_141_out, Bit5_Shift[3], or_87_out);
  or or_84 (or_84_out, and_140_out, and_213_out);
  and and_142 (Bit32_Result[15], ~Bit5_Shift[4], or_84_out);  // AND_Gate
  and and_143 (and_143_out, Bit5_Shift[4], or_88_out);
  and and_144 (and_144_out, Bit5_Shift[0], Bit32_In[14]);
  and and_145 (and_145_out, ~Bit5_Shift[0], Bit32_In[14]);  // AND_Gate
  or or_85 (or_85_out, and_145_out, and_153_out);
  and and_146 (and_146_out, Bit5_Shift[1], or_85_out);
  and and_147 (and_147_out, ~Bit5_Shift[1], or_85_out);  // AND_Gate
  or or_86 (or_86_out, and_147_out, and_164_out);
  and and_148 (and_148_out, ~Bit5_Shift[2], or_86_out);  // AND_Gate
  or or_87 (or_87_out, and_148_out, and_183_out);
  and and_149 (and_149_out, ~Bit5_Shift[3], or_87_out);  // AND_Gate
  and and_150 (and_150_out, Bit5_Shift[3], or_91_out);
  or or_88 (or_88_out, and_149_out, and_221_out);
  and and_151 (Bit32_Result[14], ~Bit5_Shift[4], or_88_out);  // AND_Gate
  and and_152 (and_152_out, Bit5_Shift[4], or_92_out);
  and and_153 (and_153_out, Bit5_Shift[0], Bit32_In[13]);
  and and_154 (and_154_out, ~Bit5_Shift[0], Bit32_In[13]);  // AND_Gate
  or or_89 (or_89_out, and_154_out, and_162_out);
  and and_155 (and_155_out, Bit5_Shift[1], or_89_out);
  and and_156 (and_156_out, ~Bit5_Shift[1], or_89_out);  // AND_Gate
  or or_90 (or_90_out, and_156_out, and_172_out);
  and and_157 (and_157_out, Bit5_Shift[2], or_90_out);
  and and_158 (and_158_out, ~Bit5_Shift[2], or_90_out);  // AND_Gate
  or or_91 (or_91_out, and_158_out, and_193_out);
  and and_159 (and_159_out, ~Bit5_Shift[3], or_91_out);  // AND_Gate
  or or_92 (or_92_out, and_159_out, and_230_out);
  and and_160 (Bit32_Result[13], ~Bit5_Shift[4], or_92_out);  // AND_Gate
  and and_161 (and_161_out, Bit5_Shift[4], or_95_out);
  and and_162 (and_162_out, Bit5_Shift[0], Bit32_In[12]);
  and and_163 (and_163_out, ~Bit5_Shift[0], Bit32_In[12]);  // AND_Gate
  and and_164 (and_164_out, Bit5_Shift[1], or_96_out);
  and and_165 (and_165_out, ~Bit5_Shift[1], or_96_out);  // AND_Gate
  or or_93 (or_93_out, and_165_out, and_182_out);
  and and_166 (and_166_out, Bit5_Shift[2], or_93_out);
  and and_167 (and_167_out, ~Bit5_Shift[2], or_93_out);  // AND_Gate
  or or_94 (or_94_out, and_167_out, and_203_out);
  and and_168 (and_168_out, Bit5_Shift[3], or_94_out);
  and and_169 (and_169_out, ~Bit5_Shift[3], or_94_out);  // AND_Gate
  or or_95 (or_95_out, and_169_out, and_248_out);
  and and_170 (Bit32_Result[12], ~Bit5_Shift[4], or_95_out);  // AND_Gate
  and and_171 (and_171_out, Bit5_Shift[0], Bit32_In[11]);
  or or_96 (or_96_out, and_163_out, and_171_out);
  and and_172 (and_172_out, Bit5_Shift[1], or_99_out);
  and and_173 (and_173_out, ~Bit5_Shift[1], or_99_out);  // AND_Gate
  and and_174 (and_174_out, Bit5_Shift[2], or_100_out);
  and and_175 (and_175_out, ~Bit5_Shift[2], or_100_out);  // AND_Gate
  or or_97 (or_97_out, and_175_out, and_211_out);
  and and_176 (and_176_out, Bit5_Shift[3], or_97_out);
  and and_177 (and_177_out, ~Bit5_Shift[3], or_97_out);  // AND_Gate
  or or_98 (or_98_out, and_177_out, and_256_out);
  and and_178 (and_178_out, Bit5_Shift[4], or_98_out);
  and and_179 (Bit32_Result[11], ~Bit5_Shift[4], or_98_out);  // AND_Gate
  and and_180 (and_180_out, ~Bit5_Shift[0], Bit32_In[11]);  // AND_Gate
  and and_181 (and_181_out, Bit5_Shift[0], Bit32_In[10]);
  or or_99 (or_99_out, and_180_out, and_181_out);
  and and_182 (and_182_out, Bit5_Shift[1], or_102_out);
  or or_100 (or_100_out, and_173_out, and_192_out);
  and and_183 (and_183_out, Bit5_Shift[2], or_103_out);
  and and_184 (and_184_out, ~Bit5_Shift[2], or_103_out);  // AND_Gate
  and and_185 (and_185_out, Bit5_Shift[3], or_104_out);
  and and_186 (and_186_out, ~Bit5_Shift[3], or_104_out);  // AND_Gate
  or or_101 (or_101_out, and_186_out, and_265_out);
  and and_187 (and_187_out, Bit5_Shift[4], or_101_out);
  and and_188 (Bit32_Result[10], ~Bit5_Shift[4], or_101_out);  // AND_Gate
  and and_189 (and_189_out, ~Bit5_Shift[0], Bit32_In[10]);  // AND_Gate
  and and_190 (and_190_out, Bit5_Shift[0], Bit32_In[9]);
  or or_102 (or_102_out, and_189_out, and_190_out);
  and and_191 (and_191_out, ~Bit5_Shift[1], or_102_out);  // AND_Gate
  and and_192 (and_192_out, Bit5_Shift[1], or_105_out);
  or or_103 (or_103_out, and_191_out, and_201_out);
  and and_193 (and_193_out, Bit5_Shift[2], or_106_out);
  or or_104 (or_104_out, and_184_out, and_219_out);
  and and_194 (and_194_out, Bit5_Shift[3], or_107_out);
  and and_195 (and_195_out, ~Bit5_Shift[3], or_107_out);  // AND_Gate
  and and_196 (and_196_out, Bit5_Shift[4], or_108_out);
  and and_197 (Bit32_Result[9], ~Bit5_Shift[4], or_108_out);  // AND_Gate
  and and_198 (and_198_out, ~Bit5_Shift[0], Bit32_In[9]);  // AND_Gate
  and and_199 (and_199_out, Bit5_Shift[0], Bit32_In[8]);
  or or_105 (or_105_out, and_198_out, and_199_out);
  and and_200 (and_200_out, ~Bit5_Shift[1], or_105_out);  // AND_Gate
  and and_201 (and_201_out, Bit5_Shift[1], or_109_out);
  or or_106 (or_106_out, and_200_out, and_209_out);
  and and_202 (and_202_out, ~Bit5_Shift[2], or_106_out);  // AND_Gate
  and and_203 (and_203_out, Bit5_Shift[2], or_110_out);
  or or_107 (or_107_out, and_202_out, and_237_out);
  and and_204 (and_204_out, Bit5_Shift[3], or_111_out);
  or or_108 (or_108_out, and_195_out, and_274_out);
  and and_205 (and_205_out, Bit5_Shift[4], or_112_out);
  and and_206 (Bit32_Result[8], ~Bit5_Shift[4], or_112_out);  // AND_Gate
  and and_207 (and_207_out, ~Bit5_Shift[0], Bit32_In[8]);  // AND_Gate
  or or_109 (or_109_out, and_207_out, and_215_out);
  and and_208 (and_208_out, ~Bit5_Shift[1], or_109_out);  // AND_Gate
  and and_209 (and_209_out, Bit5_Shift[1], or_113_out);
  or or_110 (or_110_out, and_208_out, and_226_out);
  and and_210 (and_210_out, ~Bit5_Shift[2], or_110_out);  // AND_Gate
  and and_211 (and_211_out, Bit5_Shift[2], or_114_out);
  or or_111 (or_111_out, and_210_out, and_246_out);
  and and_212 (and_212_out, ~Bit5_Shift[3], or_111_out);  // AND_Gate
  and and_213 (and_213_out, Bit5_Shift[3], or_115_out);
  or or_112 (or_112_out, and_212_out, and_284_out);
  and and_214 (and_214_out, Bit5_Shift[4], and_220_out);
  and and_215 (and_215_out, Bit5_Shift[0], Bit32_In[7]);
  and and_216 (and_216_out, ~Bit5_Shift[0], Bit32_In[7]);  // AND_Gate
  or or_113 (or_113_out, and_216_out, and_224_out);
  and and_217 (and_217_out, ~Bit5_Shift[1], or_113_out);  // AND_Gate
  or or_114 (or_114_out, and_217_out, and_235_out);
  and and_218 (and_218_out, ~Bit5_Shift[2], or_114_out);  // AND_Gate
  and and_219 (and_219_out, Bit5_Shift[2], or_117_out);
  or or_115 (or_115_out, and_218_out, and_254_out);
  and and_220 (and_220_out, ~Bit5_Shift[3], or_115_out);  // AND_Gate
  and and_221 (and_221_out, Bit5_Shift[3], or_118_out);
  and and_222 (Bit32_Result[7], ~Bit5_Shift[4], and_220_out);  // AND_Gate
  and and_223 (and_223_out, Bit5_Shift[4], and_229_out);
  and and_224 (and_224_out, Bit5_Shift[0], Bit32_In[6]);
  and and_225 (and_225_out, ~Bit5_Shift[0], Bit32_In[6]);  // AND_Gate
  or or_116 (or_116_out, and_225_out, and_233_out);
  and and_226 (and_226_out, Bit5_Shift[1], or_116_out);
  and and_227 (and_227_out, ~Bit5_Shift[1], or_116_out);  // AND_Gate
  or or_117 (or_117_out, and_227_out, and_244_out);
  and and_228 (and_228_out, ~Bit5_Shift[2], or_117_out);  // AND_Gate
  or or_118 (or_118_out, and_228_out, and_263_out);
  and and_229 (and_229_out, ~Bit5_Shift[3], or_118_out);  // AND_Gate
  and and_230 (and_230_out, Bit5_Shift[3], or_121_out);
  and and_231 (Bit32_Result[6], ~Bit5_Shift[4], and_229_out);  // AND_Gate
  and and_232 (and_232_out, Bit5_Shift[4], and_239_out);
  and and_233 (and_233_out, Bit5_Shift[0], Bit32_In[5]);
  and and_234 (and_234_out, ~Bit5_Shift[0], Bit32_In[5]);  // AND_Gate
  or or_119 (or_119_out, and_234_out, and_242_out);
  and and_235 (and_235_out, Bit5_Shift[1], or_119_out);
  and and_236 (and_236_out, ~Bit5_Shift[1], or_119_out);  // AND_Gate
  or or_120 (or_120_out, and_236_out, and_252_out);
  and and_237 (and_237_out, Bit5_Shift[2], or_120_out);
  and and_238 (and_238_out, ~Bit5_Shift[2], or_120_out);  // AND_Gate
  or or_121 (or_121_out, and_238_out, and_273_out);
  and and_239 (and_239_out, ~Bit5_Shift[3], or_121_out);  // AND_Gate
  and and_240 (Bit32_Result[5], ~Bit5_Shift[4], and_239_out);  // AND_Gate
  and and_241 (and_241_out, Bit5_Shift[4], and_249_out);
  and and_242 (and_242_out, Bit5_Shift[0], Bit32_In[4]);
  and and_243 (and_243_out, ~Bit5_Shift[0], Bit32_In[4]);  // AND_Gate
  and and_244 (and_244_out, Bit5_Shift[1], or_124_out);
  and and_245 (and_245_out, ~Bit5_Shift[1], or_124_out);  // AND_Gate
  or or_122 (or_122_out, and_245_out, and_262_out);
  and and_246 (and_246_out, Bit5_Shift[2], or_122_out);
  and and_247 (and_247_out, ~Bit5_Shift[2], or_122_out);  // AND_Gate
  or or_123 (or_123_out, and_247_out, and_283_out);
  and and_248 (and_248_out, Bit5_Shift[3], or_123_out);
  and and_249 (and_249_out, ~Bit5_Shift[3], or_123_out);  // AND_Gate
  and and_250 (Bit32_Result[4], ~Bit5_Shift[4], and_249_out);  // AND_Gate
  and and_251 (and_251_out, Bit5_Shift[0], Bit32_In[3]);
  or or_124 (or_124_out, and_243_out, and_251_out);
  and and_252 (and_252_out, Bit5_Shift[1], or_125_out);
  and and_253 (and_253_out, ~Bit5_Shift[1], or_125_out);  // AND_Gate
  and and_254 (and_254_out, Bit5_Shift[2], or_126_out);
  and and_255 (and_255_out, ~Bit5_Shift[2], or_126_out);  // AND_Gate
  and and_256 (and_256_out, Bit5_Shift[3], and_255_out);
  and and_257 (and_257_out, ~Bit5_Shift[3], and_255_out);  // AND_Gate
  and and_258 (and_258_out, Bit5_Shift[4], and_257_out);
  and and_259 (Bit32_Result[3], ~Bit5_Shift[4], and_257_out);  // AND_Gate
  and and_260 (and_260_out, ~Bit5_Shift[0], Bit32_In[3]);  // AND_Gate
  and and_261 (and_261_out, Bit5_Shift[0], Bit32_In[2]);
  or or_125 (or_125_out, and_260_out, and_261_out);
  and and_262 (and_262_out, Bit5_Shift[1], or_127_out);
  or or_126 (or_126_out, and_253_out, and_272_out);
  and and_263 (and_263_out, Bit5_Shift[2], or_128_out);
  and and_264 (and_264_out, ~Bit5_Shift[2], or_128_out);  // AND_Gate
  and and_265 (and_265_out, Bit5_Shift[3], and_264_out);
  and and_266 (and_266_out, ~Bit5_Shift[3], and_264_out);  // AND_Gate
  and and_267 (and_267_out, Bit5_Shift[4], and_266_out);
  and and_268 (Bit32_Result[2], ~Bit5_Shift[4], and_266_out);  // AND_Gate
  and and_269 (and_269_out, ~Bit5_Shift[0], Bit32_In[2]);  // AND_Gate
  and and_270 (and_270_out, Bit5_Shift[0], Bit32_In[1]);
  or or_127 (or_127_out, and_269_out, and_270_out);
  and and_271 (and_271_out, ~Bit5_Shift[1], or_127_out);  // AND_Gate
  and and_272 (and_272_out, Bit5_Shift[1], or_129_out);
  or or_128 (or_128_out, and_271_out, and_281_out);
  and and_273 (and_273_out, Bit5_Shift[2], and_280_out);
  and and_274 (and_274_out, Bit5_Shift[3], and_282_out);
  and and_275 (and_275_out, ~Bit5_Shift[3], and_282_out);  // AND_Gate
  and and_276 (and_276_out, Bit5_Shift[4], and_275_out);
  and and_277 (Bit32_Result[1], ~Bit5_Shift[4], and_275_out);  // AND_Gate
  and and_278 (and_278_out, ~Bit5_Shift[0], Bit32_In[1]);  // AND_Gate
  and and_279 (and_279_out, Bit5_Shift[0], Bit32_In[0]);
  or or_129 (or_129_out, and_278_out, and_279_out);
  and and_280 (and_280_out, ~Bit5_Shift[1], or_129_out);  // AND_Gate
  and and_281 (and_281_out, Bit5_Shift[1], and_287_out);
  and and_282 (and_282_out, ~Bit5_Shift[2], and_280_out);  // AND_Gate
  and and_283 (and_283_out, Bit5_Shift[2], and_288_out);
  and and_284 (and_284_out, Bit5_Shift[3], and_289_out);
  and and_285 (and_285_out, Bit5_Shift[4], and_290_out);
  and and_286 (Bit32_Result[0], ~Bit5_Shift[4], and_290_out);  // AND_Gate
  and and_287 (and_287_out, ~Bit5_Shift[0], Bit32_In[0]);  // AND_Gate
  and and_288 (and_288_out, ~Bit5_Shift[1], and_287_out);  // AND_Gate
  and and_289 (and_289_out, ~Bit5_Shift[2], and_288_out);  // AND_Gate
  and and_290 (and_290_out, ~Bit5_Shift[3], and_289_out);  // AND_Gate
endmodule
module Bit32_Right_Shift (
  input  [31:0] Bit32_In,
  input  [4:0] Bit5_Shift,
  output [31:0] Bit32_Result
);

  wire and_2_out, and_3_out, and_4_out, and_5_out, and_6_out, and_7_out, and_8_out, and_9_out, and_10_out,
       and_11_out, and_12_out, and_13_out, and_14_out, and_15_out, and_16_out, and_17_out, and_18_out,
       and_19_out, and_20_out, and_21_out, and_22_out, and_23_out, and_24_out, and_25_out, and_26_out,
       and_27_out, and_28_out, and_29_out, and_30_out, and_31_out, and_32_out, and_33_out, and_34_out,
       and_35_out, and_36_out, and_37_out, and_38_out, and_39_out, and_40_out, and_41_out, and_42_out,
       and_43_out, and_44_out, and_45_out, and_46_out, and_47_out, and_48_out, and_49_out, and_50_out,
       and_51_out, and_52_out, and_53_out, and_54_out, and_55_out, and_56_out, and_57_out, and_58_out,
       and_59_out, and_60_out, and_61_out, and_62_out, and_63_out, and_64_out, and_65_out, and_66_out,
       and_67_out, and_68_out, and_69_out, and_70_out, and_71_out, and_72_out, and_73_out, and_74_out,
       and_75_out, and_76_out, and_77_out, and_78_out, and_79_out, and_80_out, and_81_out, and_82_out,
       and_83_out, and_84_out, and_85_out, and_86_out, and_87_out, and_88_out, and_89_out, and_90_out,
       and_91_out, and_92_out, and_93_out, and_94_out, and_95_out, and_96_out, and_97_out, and_98_out,
       and_99_out, and_100_out, and_101_out, and_102_out, and_103_out, and_104_out, and_105_out, and_106_out,
       and_107_out, and_108_out, and_109_out, and_110_out, and_111_out, and_112_out, and_113_out,
       and_114_out, and_115_out, and_116_out, and_117_out, and_118_out, and_119_out, and_120_out,
       and_121_out, and_122_out, and_123_out, and_124_out, and_125_out, and_126_out, and_127_out,
       and_128_out, and_129_out, and_130_out, and_131_out, and_132_out, and_133_out, and_134_out,
       and_135_out, and_136_out, and_137_out, and_138_out, and_139_out, and_140_out, and_141_out,
       and_143_out, and_144_out, and_145_out, and_146_out, and_147_out, and_148_out, and_149_out,
       and_150_out, and_152_out, and_153_out, and_154_out, and_155_out, and_156_out, and_157_out,
       and_158_out, and_159_out, and_161_out, and_162_out, and_163_out, and_164_out, and_165_out,
       and_166_out, and_167_out, and_168_out, and_169_out, and_171_out, and_172_out, and_173_out,
       and_174_out, and_175_out, and_176_out, and_177_out, and_178_out, and_180_out, and_181_out,
       and_182_out, and_183_out, and_184_out, and_185_out, and_186_out, and_187_out, and_189_out,
       and_190_out, and_191_out, and_192_out, and_193_out, and_194_out, and_195_out, and_196_out,
       and_198_out, and_199_out, and_200_out, and_201_out, and_202_out, and_203_out, and_204_out,
       and_205_out, and_207_out, and_208_out, and_209_out, and_210_out, and_211_out, and_212_out,
       and_213_out, and_214_out, and_215_out, and_216_out, and_217_out, and_218_out, and_219_out,
       and_220_out, and_221_out, and_223_out, and_224_out, and_225_out, and_226_out, and_227_out,
       and_228_out, and_229_out, and_230_out, and_232_out, and_233_out, and_234_out, and_235_out,
       and_236_out, and_237_out, and_238_out, and_239_out, and_241_out, and_242_out, and_243_out,
       and_244_out, and_245_out, and_246_out, and_247_out, and_248_out, and_249_out, and_251_out,
       and_252_out, and_253_out, and_254_out, and_255_out, and_256_out, and_257_out, and_258_out,
       and_260_out, and_261_out, and_262_out, and_263_out, and_264_out, and_265_out, and_266_out,
       and_267_out, and_269_out, and_270_out, and_271_out, and_272_out, and_273_out, and_274_out,
       and_275_out, and_276_out, and_278_out, and_279_out, and_280_out, and_281_out, and_282_out,
       and_283_out, and_284_out, and_285_out, and_287_out, and_288_out, and_289_out, and_290_out, or_1_out,
       or_2_out, or_3_out, or_4_out, or_6_out, or_7_out, or_8_out, or_9_out, or_11_out, or_12_out, or_13_out,
       or_14_out, or_16_out, or_17_out, or_18_out, or_20_out, or_21_out, or_22_out, or_24_out, or_25_out,
       or_26_out, or_28_out, or_29_out, or_30_out, or_32_out, or_33_out, or_34_out, or_35_out, or_36_out,
       or_37_out, or_38_out, or_39_out, or_41_out, or_42_out, or_43_out, or_44_out, or_46_out, or_47_out,
       or_48_out, or_49_out, or_51_out, or_52_out, or_53_out, or_54_out, or_56_out, or_57_out, or_58_out,
       or_60_out, or_61_out, or_62_out, or_64_out, or_65_out, or_66_out, or_68_out, or_69_out, or_70_out,
       or_72_out, or_73_out, or_74_out, or_75_out, or_76_out, or_77_out, or_78_out, or_79_out, or_81_out,
       or_82_out, or_83_out, or_84_out, or_85_out, or_86_out, or_87_out, or_88_out, or_89_out, or_90_out,
       or_91_out, or_92_out, or_93_out, or_94_out, or_95_out, or_96_out, or_97_out, or_98_out, or_99_out,
       or_100_out, or_101_out, or_102_out, or_103_out, or_104_out, or_105_out, or_106_out, or_107_out,
       or_108_out, or_109_out, or_110_out, or_111_out, or_112_out, or_113_out, or_114_out, or_115_out,
       or_116_out, or_117_out, or_118_out, or_119_out, or_120_out, or_121_out, or_122_out, or_123_out,
       or_124_out, or_125_out, or_126_out, or_127_out, or_128_out, or_129_out;

  // AND_Gate and_1 has open pins: in0=Bit5_Shift[0], in1=Bit32_In[0], out=open
  and and_2 (and_2_out, ~Bit5_Shift[0], Bit32_In[0]);  // AND_Gate
  or or_1 (or_1_out, and_2_out, and_7_out);
  and and_3 (and_3_out, ~Bit5_Shift[1], or_1_out);  // AND_Gate
  or or_2 (or_2_out, and_3_out, and_15_out);
  and and_4 (and_4_out, ~Bit5_Shift[2], or_2_out);  // AND_Gate
  or or_3 (or_3_out, and_4_out, and_30_out);
  and and_5 (and_5_out, ~Bit5_Shift[3], or_3_out);  // AND_Gate
  or or_4 (or_4_out, and_5_out, and_61_out);
  and and_6 (and_6_out, ~Bit5_Shift[4], or_4_out);  // AND_Gate
  or or_5 (Bit32_Result[0], and_6_out, and_134_out);
  and and_7 (and_7_out, Bit5_Shift[0], Bit32_In[1]);
  and and_8 (and_8_out, ~Bit5_Shift[0], Bit32_In[1]);  // AND_Gate
  or or_6 (or_6_out, and_8_out, and_13_out);
  and and_9 (and_9_out, ~Bit5_Shift[1], or_6_out);  // AND_Gate
  or or_7 (or_7_out, and_9_out, and_22_out);
  and and_10 (and_10_out, ~Bit5_Shift[2], or_7_out);  // AND_Gate
  or or_8 (or_8_out, and_10_out, and_37_out);
  and and_11 (and_11_out, ~Bit5_Shift[3], or_8_out);  // AND_Gate
  or or_9 (or_9_out, and_11_out, and_68_out);
  and and_12 (and_12_out, ~Bit5_Shift[4], or_9_out);  // AND_Gate
  or or_10 (Bit32_Result[1], and_12_out, and_143_out);
  and and_13 (and_13_out, Bit5_Shift[0], Bit32_In[2]);
  and and_14 (and_14_out, ~Bit5_Shift[0], Bit32_In[2]);  // AND_Gate
  or or_11 (or_11_out, and_14_out, and_20_out);
  and and_15 (and_15_out, Bit5_Shift[1], or_11_out);
  and and_16 (and_16_out, ~Bit5_Shift[1], or_11_out);  // AND_Gate
  or or_12 (or_12_out, and_16_out, and_28_out);
  and and_17 (and_17_out, ~Bit5_Shift[2], or_12_out);  // AND_Gate
  or or_13 (or_13_out, and_17_out, and_45_out);
  and and_18 (and_18_out, ~Bit5_Shift[3], or_13_out);  // AND_Gate
  or or_14 (or_14_out, and_18_out, and_76_out);
  and and_19 (and_19_out, ~Bit5_Shift[4], or_14_out);  // AND_Gate
  or or_15 (Bit32_Result[2], and_19_out, and_152_out);
  and and_20 (and_20_out, Bit5_Shift[0], Bit32_In[3]);
  and and_21 (and_21_out, ~Bit5_Shift[0], Bit32_In[3]);  // AND_Gate
  and and_22 (and_22_out, Bit5_Shift[1], or_20_out);
  and and_23 (and_23_out, ~Bit5_Shift[1], or_20_out);  // AND_Gate
  or or_16 (or_16_out, and_23_out, and_36_out);
  and and_24 (and_24_out, ~Bit5_Shift[2], or_16_out);  // AND_Gate
  or or_17 (or_17_out, and_24_out, and_52_out);
  and and_25 (and_25_out, ~Bit5_Shift[3], or_17_out);  // AND_Gate
  or or_18 (or_18_out, and_25_out, and_92_out);
  and and_26 (and_26_out, ~Bit5_Shift[4], or_18_out);  // AND_Gate
  or or_19 (Bit32_Result[3], and_26_out, and_161_out);
  and and_27 (and_27_out, Bit5_Shift[0], Bit32_In[4]);
  or or_20 (or_20_out, and_21_out, and_27_out);
  and and_28 (and_28_out, Bit5_Shift[1], or_24_out);
  and and_29 (and_29_out, ~Bit5_Shift[1], or_24_out);  // AND_Gate
  and and_30 (and_30_out, Bit5_Shift[2], or_25_out);
  and and_31 (and_31_out, ~Bit5_Shift[2], or_25_out);  // AND_Gate
  or or_21 (or_21_out, and_31_out, and_59_out);
  and and_32 (and_32_out, ~Bit5_Shift[3], or_21_out);  // AND_Gate
  or or_22 (or_22_out, and_32_out, and_100_out);
  and and_33 (and_33_out, ~Bit5_Shift[4], or_22_out);  // AND_Gate
  or or_23 (Bit32_Result[4], and_33_out, and_178_out);
  and and_34 (and_34_out, ~Bit5_Shift[0], Bit32_In[4]);  // AND_Gate
  and and_35 (and_35_out, Bit5_Shift[0], Bit32_In[5]);
  or or_24 (or_24_out, and_34_out, and_35_out);
  and and_36 (and_36_out, Bit5_Shift[1], or_28_out);
  or or_25 (or_25_out, and_29_out, and_44_out);
  and and_37 (and_37_out, Bit5_Shift[2], or_29_out);
  and and_38 (and_38_out, ~Bit5_Shift[2], or_29_out);  // AND_Gate
  and and_39 (and_39_out, ~Bit5_Shift[3], or_30_out);  // AND_Gate
  or or_26 (or_26_out, and_39_out, and_108_out);
  and and_40 (and_40_out, ~Bit5_Shift[4], or_26_out);  // AND_Gate
  or or_27 (Bit32_Result[5], and_40_out, and_187_out);
  and and_41 (and_41_out, ~Bit5_Shift[0], Bit32_In[5]);  // AND_Gate
  and and_42 (and_42_out, Bit5_Shift[0], Bit32_In[6]);
  or or_28 (or_28_out, and_41_out, and_42_out);
  and and_43 (and_43_out, ~Bit5_Shift[1], or_28_out);  // AND_Gate
  and and_44 (and_44_out, Bit5_Shift[1], or_32_out);
  or or_29 (or_29_out, and_43_out, and_50_out);
  and and_45 (and_45_out, Bit5_Shift[2], or_33_out);
  or or_30 (or_30_out, and_38_out, and_66_out);
  and and_46 (and_46_out, ~Bit5_Shift[3], or_34_out);  // AND_Gate
  and and_47 (and_47_out, ~Bit5_Shift[4], or_35_out);  // AND_Gate
  or or_31 (Bit32_Result[6], and_47_out, and_196_out);
  and and_48 (and_48_out, Bit5_Shift[0], Bit32_In[7]);
  and and_49 (and_49_out, ~Bit5_Shift[0], Bit32_In[6]);  // AND_Gate
  or or_32 (or_32_out, and_49_out, and_48_out);
  and and_50 (and_50_out, Bit5_Shift[1], or_36_out);
  and and_51 (and_51_out, ~Bit5_Shift[1], or_32_out);  // AND_Gate
  or or_33 (or_33_out, and_51_out, and_57_out);
  and and_52 (and_52_out, Bit5_Shift[2], or_37_out);
  and and_53 (and_53_out, ~Bit5_Shift[2], or_33_out);  // AND_Gate
  or or_34 (or_34_out, and_53_out, and_82_out);
  or or_35 (or_35_out, and_46_out, and_116_out);
  and and_54 (and_54_out, ~Bit5_Shift[4], or_39_out);  // AND_Gate
  and and_55 (and_55_out, ~Bit5_Shift[0], Bit32_In[7]);  // AND_Gate
  or or_36 (or_36_out, and_55_out, and_62_out);
  and and_56 (and_56_out, ~Bit5_Shift[1], or_36_out);  // AND_Gate
  and and_57 (and_57_out, Bit5_Shift[1], or_41_out);
  or or_37 (or_37_out, and_56_out, and_72_out);
  and and_58 (and_58_out, ~Bit5_Shift[2], or_37_out);  // AND_Gate
  and and_59 (and_59_out, Bit5_Shift[2], or_42_out);
  or or_38 (or_38_out, and_58_out, and_90_out);
  and and_60 (and_60_out, ~Bit5_Shift[3], or_38_out);  // AND_Gate
  and and_61 (and_61_out, Bit5_Shift[3], or_43_out);
  or or_39 (or_39_out, and_60_out, and_125_out);
  or or_40 (Bit32_Result[7], and_54_out, and_205_out);
  and and_62 (and_62_out, Bit5_Shift[0], Bit32_In[8]);
  and and_63 (and_63_out, ~Bit5_Shift[0], Bit32_In[8]);  // AND_Gate
  or or_41 (or_41_out, and_63_out, and_70_out);
  and and_64 (and_64_out, ~Bit5_Shift[1], or_41_out);  // AND_Gate
  or or_42 (or_42_out, and_64_out, and_80_out);
  and and_65 (and_65_out, ~Bit5_Shift[2], or_42_out);  // AND_Gate
  and and_66 (and_66_out, Bit5_Shift[2], or_47_out);
  or or_43 (or_43_out, and_65_out, and_98_out);
  and and_67 (and_67_out, ~Bit5_Shift[3], or_43_out);  // AND_Gate
  and and_68 (and_68_out, Bit5_Shift[3], or_48_out);
  or or_44 (or_44_out, and_67_out, and_133_out);
  and and_69 (and_69_out, ~Bit5_Shift[4], or_44_out);  // AND_Gate
  or or_45 (Bit32_Result[8], and_69_out, and_214_out);
  and and_70 (and_70_out, Bit5_Shift[0], Bit32_In[9]);
  and and_71 (and_71_out, ~Bit5_Shift[0], Bit32_In[9]);  // AND_Gate
  or or_46 (or_46_out, and_71_out, and_78_out);
  and and_72 (and_72_out, Bit5_Shift[1], or_46_out);
  and and_73 (and_73_out, ~Bit5_Shift[1], or_46_out);  // AND_Gate
  or or_47 (or_47_out, and_73_out, and_88_out);
  and and_74 (and_74_out, ~Bit5_Shift[2], or_47_out);  // AND_Gate
  or or_48 (or_48_out, and_74_out, and_106_out);
  and and_75 (and_75_out, ~Bit5_Shift[3], or_48_out);  // AND_Gate
  and and_76 (and_76_out, Bit5_Shift[3], or_53_out);
  or or_49 (or_49_out, and_75_out, and_141_out);
  and and_77 (and_77_out, ~Bit5_Shift[4], or_49_out);  // AND_Gate
  or or_50 (Bit32_Result[9], and_77_out, and_223_out);
  and and_78 (and_78_out, Bit5_Shift[0], Bit32_In[10]);
  and and_79 (and_79_out, ~Bit5_Shift[0], Bit32_In[10]);  // AND_Gate
  or or_51 (or_51_out, and_79_out, and_86_out);
  and and_80 (and_80_out, Bit5_Shift[1], or_51_out);
  and and_81 (and_81_out, ~Bit5_Shift[1], or_51_out);  // AND_Gate
  or or_52 (or_52_out, and_81_out, and_96_out);
  and and_82 (and_82_out, Bit5_Shift[2], or_52_out);
  and and_83 (and_83_out, ~Bit5_Shift[2], or_52_out);  // AND_Gate
  or or_53 (or_53_out, and_83_out, and_115_out);
  and and_84 (and_84_out, ~Bit5_Shift[3], or_53_out);  // AND_Gate
  or or_54 (or_54_out, and_84_out, and_150_out);
  and and_85 (and_85_out, ~Bit5_Shift[4], or_54_out);  // AND_Gate
  or or_55 (Bit32_Result[10], and_85_out, and_232_out);
  and and_86 (and_86_out, Bit5_Shift[0], Bit32_In[11]);
  and and_87 (and_87_out, ~Bit5_Shift[0], Bit32_In[11]);  // AND_Gate
  and and_88 (and_88_out, Bit5_Shift[1], or_60_out);
  and and_89 (and_89_out, ~Bit5_Shift[1], or_60_out);  // AND_Gate
  or or_56 (or_56_out, and_89_out, and_105_out);
  and and_90 (and_90_out, Bit5_Shift[2], or_56_out);
  and and_91 (and_91_out, ~Bit5_Shift[2], or_56_out);  // AND_Gate
  or or_57 (or_57_out, and_91_out, and_124_out);
  and and_92 (and_92_out, Bit5_Shift[3], or_57_out);
  and and_93 (and_93_out, ~Bit5_Shift[3], or_57_out);  // AND_Gate
  or or_58 (or_58_out, and_93_out, and_168_out);
  and and_94 (and_94_out, ~Bit5_Shift[4], or_58_out);  // AND_Gate
  or or_59 (Bit32_Result[11], and_94_out, and_241_out);
  and and_95 (and_95_out, Bit5_Shift[0], Bit32_In[12]);
  or or_60 (or_60_out, and_87_out, and_95_out);
  and and_96 (and_96_out, Bit5_Shift[1], or_64_out);
  and and_97 (and_97_out, ~Bit5_Shift[1], or_64_out);  // AND_Gate
  and and_98 (and_98_out, Bit5_Shift[2], or_65_out);
  and and_99 (and_99_out, ~Bit5_Shift[2], or_65_out);  // AND_Gate
  or or_61 (or_61_out, and_99_out, and_131_out);
  and and_100 (and_100_out, Bit5_Shift[3], or_61_out);
  and and_101 (and_101_out, ~Bit5_Shift[3], or_61_out);  // AND_Gate
  or or_62 (or_62_out, and_101_out, and_176_out);
  and and_102 (and_102_out, ~Bit5_Shift[4], or_62_out);  // AND_Gate
  or or_63 (Bit32_Result[12], and_102_out, and_258_out);
  and and_103 (and_103_out, ~Bit5_Shift[0], Bit32_In[12]);  // AND_Gate
  and and_104 (and_104_out, Bit5_Shift[0], Bit32_In[13]);
  or or_64 (or_64_out, and_103_out, and_104_out);
  and and_105 (and_105_out, Bit5_Shift[1], or_68_out);
  or or_65 (or_65_out, and_97_out, and_114_out);
  and and_106 (and_106_out, Bit5_Shift[2], or_69_out);
  and and_107 (and_107_out, ~Bit5_Shift[2], or_69_out);  // AND_Gate
  and and_108 (and_108_out, Bit5_Shift[3], or_70_out);
  and and_109 (and_109_out, ~Bit5_Shift[3], or_70_out);  // AND_Gate
  or or_66 (or_66_out, and_109_out, and_185_out);
  and and_110 (and_110_out, ~Bit5_Shift[4], or_66_out);  // AND_Gate
  or or_67 (Bit32_Result[13], and_110_out, and_267_out);
  and and_111 (and_111_out, ~Bit5_Shift[0], Bit32_In[13]);  // AND_Gate
  and and_112 (and_112_out, Bit5_Shift[0], Bit32_In[14]);
  or or_68 (or_68_out, and_111_out, and_112_out);
  and and_113 (and_113_out, ~Bit5_Shift[1], or_68_out);  // AND_Gate
  and and_114 (and_114_out, Bit5_Shift[1], or_72_out);
  or or_69 (or_69_out, and_113_out, and_122_out);
  and and_115 (and_115_out, Bit5_Shift[2], or_73_out);
  or or_70 (or_70_out, and_107_out, and_139_out);
  and and_116 (and_116_out, Bit5_Shift[3], or_74_out);
  and and_117 (and_117_out, ~Bit5_Shift[3], or_74_out);  // AND_Gate
  and and_118 (and_118_out, ~Bit5_Shift[4], or_75_out);  // AND_Gate
  or or_71 (Bit32_Result[14], and_118_out, and_276_out);
  and and_119 (and_119_out, ~Bit5_Shift[0], Bit32_In[14]);  // AND_Gate
  and and_120 (and_120_out, Bit5_Shift[0], Bit32_In[15]);
  or or_72 (or_72_out, and_119_out, and_120_out);
  and and_121 (and_121_out, ~Bit5_Shift[1], or_72_out);  // AND_Gate
  and and_122 (and_122_out, Bit5_Shift[1], or_76_out);
  or or_73 (or_73_out, and_121_out, and_129_out);
  and and_123 (and_123_out, ~Bit5_Shift[2], or_73_out);  // AND_Gate
  and and_124 (and_124_out, Bit5_Shift[2], or_77_out);
  or or_74 (or_74_out, and_123_out, and_157_out);
  and and_125 (and_125_out, Bit5_Shift[3], or_78_out);
  or or_75 (or_75_out, and_117_out, and_194_out);
  and and_126 (and_126_out, ~Bit5_Shift[4], or_79_out);  // AND_Gate
  and and_127 (and_127_out, ~Bit5_Shift[0], Bit32_In[15]);  // AND_Gate
  or or_76 (or_76_out, and_127_out, and_135_out);
  and and_128 (and_128_out, ~Bit5_Shift[1], or_76_out);  // AND_Gate
  and and_129 (and_129_out, Bit5_Shift[1], or_81_out);
  or or_77 (or_77_out, and_128_out, and_146_out);
  and and_130 (and_130_out, ~Bit5_Shift[2], or_77_out);  // AND_Gate
  and and_131 (and_131_out, Bit5_Shift[2], or_82_out);
  or or_78 (or_78_out, and_130_out, and_166_out);
  and and_132 (and_132_out, ~Bit5_Shift[3], or_78_out);  // AND_Gate
  and and_133 (and_133_out, Bit5_Shift[3], or_83_out);
  or or_79 (or_79_out, and_132_out, and_204_out);
  and and_134 (and_134_out, Bit5_Shift[4], or_84_out);
  or or_80 (Bit32_Result[15], and_126_out, and_285_out);
  and and_135 (and_135_out, Bit5_Shift[0], Bit32_In[16]);
  and and_136 (and_136_out, ~Bit5_Shift[0], Bit32_In[16]);  // AND_Gate
  or or_81 (or_81_out, and_136_out, and_144_out);
  and and_137 (and_137_out, ~Bit5_Shift[1], or_81_out);  // AND_Gate
  or or_82 (or_82_out, and_137_out, and_155_out);
  and and_138 (and_138_out, ~Bit5_Shift[2], or_82_out);  // AND_Gate
  and and_139 (and_139_out, Bit5_Shift[2], or_86_out);
  or or_83 (or_83_out, and_138_out, and_174_out);
  and and_140 (and_140_out, ~Bit5_Shift[3], or_83_out);  // AND_Gate
  and and_141 (and_141_out, Bit5_Shift[3], or_87_out);
  or or_84 (or_84_out, and_140_out, and_213_out);
  and and_142 (Bit32_Result[16], ~Bit5_Shift[4], or_84_out);  // AND_Gate
  and and_143 (and_143_out, Bit5_Shift[4], or_88_out);
  and and_144 (and_144_out, Bit5_Shift[0], Bit32_In[17]);
  and and_145 (and_145_out, ~Bit5_Shift[0], Bit32_In[17]);  // AND_Gate
  or or_85 (or_85_out, and_145_out, and_153_out);
  and and_146 (and_146_out, Bit5_Shift[1], or_85_out);
  and and_147 (and_147_out, ~Bit5_Shift[1], or_85_out);  // AND_Gate
  or or_86 (or_86_out, and_147_out, and_164_out);
  and and_148 (and_148_out, ~Bit5_Shift[2], or_86_out);  // AND_Gate
  or or_87 (or_87_out, and_148_out, and_183_out);
  and and_149 (and_149_out, ~Bit5_Shift[3], or_87_out);  // AND_Gate
  and and_150 (and_150_out, Bit5_Shift[3], or_91_out);
  or or_88 (or_88_out, and_149_out, and_221_out);
  and and_151 (Bit32_Result[17], ~Bit5_Shift[4], or_88_out);  // AND_Gate
  and and_152 (and_152_out, Bit5_Shift[4], or_92_out);
  and and_153 (and_153_out, Bit5_Shift[0], Bit32_In[18]);
  and and_154 (and_154_out, ~Bit5_Shift[0], Bit32_In[18]);  // AND_Gate
  or or_89 (or_89_out, and_154_out, and_162_out);
  and and_155 (and_155_out, Bit5_Shift[1], or_89_out);
  and and_156 (and_156_out, ~Bit5_Shift[1], or_89_out);  // AND_Gate
  or or_90 (or_90_out, and_156_out, and_172_out);
  and and_157 (and_157_out, Bit5_Shift[2], or_90_out);
  and and_158 (and_158_out, ~Bit5_Shift[2], or_90_out);  // AND_Gate
  or or_91 (or_91_out, and_158_out, and_193_out);
  and and_159 (and_159_out, ~Bit5_Shift[3], or_91_out);  // AND_Gate
  or or_92 (or_92_out, and_159_out, and_230_out);
  and and_160 (Bit32_Result[18], ~Bit5_Shift[4], or_92_out);  // AND_Gate
  and and_161 (and_161_out, Bit5_Shift[4], or_95_out);
  and and_162 (and_162_out, Bit5_Shift[0], Bit32_In[19]);
  and and_163 (and_163_out, ~Bit5_Shift[0], Bit32_In[19]);  // AND_Gate
  and and_164 (and_164_out, Bit5_Shift[1], or_96_out);
  and and_165 (and_165_out, ~Bit5_Shift[1], or_96_out);  // AND_Gate
  or or_93 (or_93_out, and_165_out, and_182_out);
  and and_166 (and_166_out, Bit5_Shift[2], or_93_out);
  and and_167 (and_167_out, ~Bit5_Shift[2], or_93_out);  // AND_Gate
  or or_94 (or_94_out, and_167_out, and_203_out);
  and and_168 (and_168_out, Bit5_Shift[3], or_94_out);
  and and_169 (and_169_out, ~Bit5_Shift[3], or_94_out);  // AND_Gate
  or or_95 (or_95_out, and_169_out, and_248_out);
  and and_170 (Bit32_Result[19], ~Bit5_Shift[4], or_95_out);  // AND_Gate
  and and_171 (and_171_out, Bit5_Shift[0], Bit32_In[20]);
  or or_96 (or_96_out, and_163_out, and_171_out);
  and and_172 (and_172_out, Bit5_Shift[1], or_99_out);
  and and_173 (and_173_out, ~Bit5_Shift[1], or_99_out);  // AND_Gate
  and and_174 (and_174_out, Bit5_Shift[2], or_100_out);
  and and_175 (and_175_out, ~Bit5_Shift[2], or_100_out);  // AND_Gate
  or or_97 (or_97_out, and_175_out, and_211_out);
  and and_176 (and_176_out, Bit5_Shift[3], or_97_out);
  and and_177 (and_177_out, ~Bit5_Shift[3], or_97_out);  // AND_Gate
  or or_98 (or_98_out, and_177_out, and_256_out);
  and and_178 (and_178_out, Bit5_Shift[4], or_98_out);
  and and_179 (Bit32_Result[20], ~Bit5_Shift[4], or_98_out);  // AND_Gate
  and and_180 (and_180_out, ~Bit5_Shift[0], Bit32_In[20]);  // AND_Gate
  and and_181 (and_181_out, Bit5_Shift[0], Bit32_In[21]);
  or or_99 (or_99_out, and_180_out, and_181_out);
  and and_182 (and_182_out, Bit5_Shift[1], or_102_out);
  or or_100 (or_100_out, and_173_out, and_192_out);
  and and_183 (and_183_out, Bit5_Shift[2], or_103_out);
  and and_184 (and_184_out, ~Bit5_Shift[2], or_103_out);  // AND_Gate
  and and_185 (and_185_out, Bit5_Shift[3], or_104_out);
  and and_186 (and_186_out, ~Bit5_Shift[3], or_104_out);  // AND_Gate
  or or_101 (or_101_out, and_186_out, and_265_out);
  and and_187 (and_187_out, Bit5_Shift[4], or_101_out);
  and and_188 (Bit32_Result[21], ~Bit5_Shift[4], or_101_out);  // AND_Gate
  and and_189 (and_189_out, ~Bit5_Shift[0], Bit32_In[21]);  // AND_Gate
  and and_190 (and_190_out, Bit5_Shift[0], Bit32_In[22]);
  or or_102 (or_102_out, and_189_out, and_190_out);
  and and_191 (and_191_out, ~Bit5_Shift[1], or_102_out);  // AND_Gate
  and and_192 (and_192_out, Bit5_Shift[1], or_105_out);
  or or_103 (or_103_out, and_191_out, and_201_out);
  and and_193 (and_193_out, Bit5_Shift[2], or_106_out);
  or or_104 (or_104_out, and_184_out, and_219_out);
  and and_194 (and_194_out, Bit5_Shift[3], or_107_out);
  and and_195 (and_195_out, ~Bit5_Shift[3], or_107_out);  // AND_Gate
  and and_196 (and_196_out, Bit5_Shift[4], or_108_out);
  and and_197 (Bit32_Result[22], ~Bit5_Shift[4], or_108_out);  // AND_Gate
  and and_198 (and_198_out, ~Bit5_Shift[0], Bit32_In[22]);  // AND_Gate
  and and_199 (and_199_out, Bit5_Shift[0], Bit32_In[23]);
  or or_105 (or_105_out, and_198_out, and_199_out);
  and and_200 (and_200_out, ~Bit5_Shift[1], or_105_out);  // AND_Gate
  and and_201 (and_201_out, Bit5_Shift[1], or_109_out);
  or or_106 (or_106_out, and_200_out, and_209_out);
  and and_202 (and_202_out, ~Bit5_Shift[2], or_106_out);  // AND_Gate
  and and_203 (and_203_out, Bit5_Shift[2], or_110_out);
  or or_107 (or_107_out, and_202_out, and_237_out);
  and and_204 (and_204_out, Bit5_Shift[3], or_111_out);
  or or_108 (or_108_out, and_195_out, and_274_out);
  and and_205 (and_205_out, Bit5_Shift[4], or_112_out);
  and and_206 (Bit32_Result[23], ~Bit5_Shift[4], or_112_out);  // AND_Gate
  and and_207 (and_207_out, ~Bit5_Shift[0], Bit32_In[23]);  // AND_Gate
  or or_109 (or_109_out, and_207_out, and_215_out);
  and and_208 (and_208_out, ~Bit5_Shift[1], or_109_out);  // AND_Gate
  and and_209 (and_209_out, Bit5_Shift[1], or_113_out);
  or or_110 (or_110_out, and_208_out, and_226_out);
  and and_210 (and_210_out, ~Bit5_Shift[2], or_110_out);  // AND_Gate
  and and_211 (and_211_out, Bit5_Shift[2], or_114_out);
  or or_111 (or_111_out, and_210_out, and_246_out);
  and and_212 (and_212_out, ~Bit5_Shift[3], or_111_out);  // AND_Gate
  and and_213 (and_213_out, Bit5_Shift[3], or_115_out);
  or or_112 (or_112_out, and_212_out, and_284_out);
  and and_214 (and_214_out, Bit5_Shift[4], and_220_out);
  and and_215 (and_215_out, Bit5_Shift[0], Bit32_In[24]);
  and and_216 (and_216_out, ~Bit5_Shift[0], Bit32_In[24]);  // AND_Gate
  or or_113 (or_113_out, and_216_out, and_224_out);
  and and_217 (and_217_out, ~Bit5_Shift[1], or_113_out);  // AND_Gate
  or or_114 (or_114_out, and_217_out, and_235_out);
  and and_218 (and_218_out, ~Bit5_Shift[2], or_114_out);  // AND_Gate
  and and_219 (and_219_out, Bit5_Shift[2], or_117_out);
  or or_115 (or_115_out, and_218_out, and_254_out);
  and and_220 (and_220_out, ~Bit5_Shift[3], or_115_out);  // AND_Gate
  and and_221 (and_221_out, Bit5_Shift[3], or_118_out);
  and and_222 (Bit32_Result[24], ~Bit5_Shift[4], and_220_out);  // AND_Gate
  and and_223 (and_223_out, Bit5_Shift[4], and_229_out);
  and and_224 (and_224_out, Bit5_Shift[0], Bit32_In[25]);
  and and_225 (and_225_out, ~Bit5_Shift[0], Bit32_In[25]);  // AND_Gate
  or or_116 (or_116_out, and_225_out, and_233_out);
  and and_226 (and_226_out, Bit5_Shift[1], or_116_out);
  and and_227 (and_227_out, ~Bit5_Shift[1], or_116_out);  // AND_Gate
  or or_117 (or_117_out, and_227_out, and_244_out);
  and and_228 (and_228_out, ~Bit5_Shift[2], or_117_out);  // AND_Gate
  or or_118 (or_118_out, and_228_out, and_263_out);
  and and_229 (and_229_out, ~Bit5_Shift[3], or_118_out);  // AND_Gate
  and and_230 (and_230_out, Bit5_Shift[3], or_121_out);
  and and_231 (Bit32_Result[25], ~Bit5_Shift[4], and_229_out);  // AND_Gate
  and and_232 (and_232_out, Bit5_Shift[4], and_239_out);
  and and_233 (and_233_out, Bit5_Shift[0], Bit32_In[26]);
  and and_234 (and_234_out, ~Bit5_Shift[0], Bit32_In[26]);  // AND_Gate
  or or_119 (or_119_out, and_234_out, and_242_out);
  and and_235 (and_235_out, Bit5_Shift[1], or_119_out);
  and and_236 (and_236_out, ~Bit5_Shift[1], or_119_out);  // AND_Gate
  or or_120 (or_120_out, and_236_out, and_252_out);
  and and_237 (and_237_out, Bit5_Shift[2], or_120_out);
  and and_238 (and_238_out, ~Bit5_Shift[2], or_120_out);  // AND_Gate
  or or_121 (or_121_out, and_238_out, and_273_out);
  and and_239 (and_239_out, ~Bit5_Shift[3], or_121_out);  // AND_Gate
  and and_240 (Bit32_Result[26], ~Bit5_Shift[4], and_239_out);  // AND_Gate
  and and_241 (and_241_out, Bit5_Shift[4], and_249_out);
  and and_242 (and_242_out, Bit5_Shift[0], Bit32_In[27]);
  and and_243 (and_243_out, ~Bit5_Shift[0], Bit32_In[27]);  // AND_Gate
  and and_244 (and_244_out, Bit5_Shift[1], or_124_out);
  and and_245 (and_245_out, ~Bit5_Shift[1], or_124_out);  // AND_Gate
  or or_122 (or_122_out, and_245_out, and_262_out);
  and and_246 (and_246_out, Bit5_Shift[2], or_122_out);
  and and_247 (and_247_out, ~Bit5_Shift[2], or_122_out);  // AND_Gate
  or or_123 (or_123_out, and_247_out, and_283_out);
  and and_248 (and_248_out, Bit5_Shift[3], or_123_out);
  and and_249 (and_249_out, ~Bit5_Shift[3], or_123_out);  // AND_Gate
  and and_250 (Bit32_Result[27], ~Bit5_Shift[4], and_249_out);  // AND_Gate
  and and_251 (and_251_out, Bit5_Shift[0], Bit32_In[28]);
  or or_124 (or_124_out, and_243_out, and_251_out);
  and and_252 (and_252_out, Bit5_Shift[1], or_125_out);
  and and_253 (and_253_out, ~Bit5_Shift[1], or_125_out);  // AND_Gate
  and and_254 (and_254_out, Bit5_Shift[2], or_126_out);
  and and_255 (and_255_out, ~Bit5_Shift[2], or_126_out);  // AND_Gate
  and and_256 (and_256_out, Bit5_Shift[3], and_255_out);
  and and_257 (and_257_out, ~Bit5_Shift[3], and_255_out);  // AND_Gate
  and and_258 (and_258_out, Bit5_Shift[4], and_257_out);
  and and_259 (Bit32_Result[28], ~Bit5_Shift[4], and_257_out);  // AND_Gate
  and and_260 (and_260_out, ~Bit5_Shift[0], Bit32_In[28]);  // AND_Gate
  and and_261 (and_261_out, Bit5_Shift[0], Bit32_In[29]);
  or or_125 (or_125_out, and_260_out, and_261_out);
  and and_262 (and_262_out, Bit5_Shift[1], or_127_out);
  or or_126 (or_126_out, and_253_out, and_272_out);
  and and_263 (and_263_out, Bit5_Shift[2], or_128_out);
  and and_264 (and_264_out, ~Bit5_Shift[2], or_128_out);  // AND_Gate
  and and_265 (and_265_out, Bit5_Shift[3], and_264_out);
  and and_266 (and_266_out, ~Bit5_Shift[3], and_264_out);  // AND_Gate
  and and_267 (and_267_out, Bit5_Shift[4], and_266_out);
  and and_268 (Bit32_Result[29], ~Bit5_Shift[4], and_266_out);  // AND_Gate
  and and_269 (and_269_out, ~Bit5_Shift[0], Bit32_In[29]);  // AND_Gate
  and and_270 (and_270_out, Bit5_Shift[0], Bit32_In[30]);
  or or_127 (or_127_out, and_269_out, and_270_out);
  and and_271 (and_271_out, ~Bit5_Shift[1], or_127_out);  // AND_Gate
  and and_272 (and_272_out, Bit5_Shift[1], or_129_out);
  or or_128 (or_128_out, and_271_out, and_281_out);
  and and_273 (and_273_out, Bit5_Shift[2], and_280_out);
  and and_274 (and_274_out, Bit5_Shift[3], and_282_out);
  and and_275 (and_275_out, ~Bit5_Shift[3], and_282_out);  // AND_Gate
  and and_276 (and_276_out, Bit5_Shift[4], and_275_out);
  and and_277 (Bit32_Result[30], ~Bit5_Shift[4], and_275_out);  // AND_Gate
  and and_278 (and_278_out, ~Bit5_Shift[0], Bit32_In[30]);  // AND_Gate
  and and_279 (and_279_out, Bit5_Shift[0], Bit32_In[31]);
  or or_129 (or_129_out, and_278_out, and_279_out);
  and and_280 (and_280_out, ~Bit5_Shift[1], or_129_out);  // AND_Gate
  and and_281 (and_281_out, Bit5_Shift[1], and_287_out);
  and and_282 (and_282_out, ~Bit5_Shift[2], and_280_out);  // AND_Gate
  and and_283 (and_283_out, Bit5_Shift[2], and_288_out);
  and and_284 (and_284_out, Bit5_Shift[3], and_289_out);
  and and_285 (and_285_out, Bit5_Shift[4], and_290_out);
  and and_286 (Bit32_Result[31], ~Bit5_Shift[4], and_290_out);  // AND_Gate
  and and_287 (and_287_out, ~Bit5_Shift[0], Bit32_In[31]);  // AND_Gate
  and and_288 (and_288_out, ~Bit5_Shift[1], and_287_out);  // AND_Gate
  and and_289 (and_289_out, ~Bit5_Shift[2], and_288_out);  // AND_Gate
  and and_290 (and_290_out, ~Bit5_Shift[3], and_289_out);  // AND_Gate
endmodule

module Bit11_To_Bit32_High (
  input  [10:0] Bit11_In,
  output [31:0] Bit32_Out
);


  assign Bit32_Out = {Bit11_In, {21{1'b0}}};
endmodule

module Bit32_To_Bit24_High (
  input  [31:0] Bit32_In,
  output [23:0] Bit24_Out
);


  assign Bit24_Out = Bit32_In[31:8];
endmodule

module Bit10_Add_One (
  input  Add_One,
  input  [9:0] Bit10_In,
  output [9:0] Bit10_Out,
  output Carry_Out
);

  wire and_1_out, and_2_out, and_3_out, and_4_out, and_5_out, and_6_out, and_7_out, and_8_out, and_9_out;

  and and_1 (and_1_out, Add_One, Bit10_In[0]);
  and and_2 (and_2_out, Add_One, Bit10_In[0], Bit10_In[1]);
  and and_3 (and_3_out, Add_One, Bit10_In[0], Bit10_In[1], Bit10_In[2]);
  and and_4 (and_4_out, Add_One, Bit10_In[0], Bit10_In[1], Bit10_In[2], Bit10_In[3]);
  and and_5 (and_5_out, Add_One, Bit10_In[0], Bit10_In[1], Bit10_In[2], Bit10_In[3], Bit10_In[4]);
  and and_6 (and_6_out, Add_One, Bit10_In[0], Bit10_In[1], Bit10_In[2], Bit10_In[3], Bit10_In[4], Bit10_In[5]);
  and and_7 (and_7_out, Add_One, Bit10_In[0], Bit10_In[1], Bit10_In[2], Bit10_In[3], Bit10_In[4], Bit10_In[5], Bit10_In[6]);
  and and_8 (and_8_out, Add_One, Bit10_In[0], Bit10_In[1], Bit10_In[2], Bit10_In[3], Bit10_In[4], Bit10_In[5], Bit10_In[6], Bit10_In[7]);
  and and_9 (and_9_out, Add_One, Bit10_In[0], Bit10_In[1], Bit10_In[2], Bit10_In[3], Bit10_In[4], Bit10_In[5], Bit10_In[6], Bit10_In[7], Bit10_In[8]);
  and and_10 (Carry_Out, Add_One, Bit10_In[0], Bit10_In[1], Bit10_In[2], Bit10_In[3], Bit10_In[4], Bit10_In[5], Bit10_In[6], Bit10_In[7], Bit10_In[8], Bit10_In[9]);
  xor xor_1 (Bit10_Out[0], Bit10_In[0], Add_One);
  xor xor_2 (Bit10_Out[1], Bit10_In[1], and_1_out);
  xor xor_3 (Bit10_Out[2], Bit10_In[2], and_2_out);
  xor xor_4 (Bit10_Out[3], Bit10_In[3], and_3_out);
  xor xor_5 (Bit10_Out[4], Bit10_In[4], and_4_out);
  xor xor_6 (Bit10_Out[5], Bit10_In[5], and_5_out);
  xor xor_7 (Bit10_Out[6], Bit10_In[6], and_6_out);
  xor xor_8 (Bit10_Out[7], Bit10_In[7], and_7_out);
  xor xor_9 (Bit10_Out[8], Bit10_In[8], and_8_out);
  xor xor_10 (Bit10_Out[9], Bit10_In[9], and_9_out);
endmodule

module Bit5_Add_One (
  input  Add_One,
  input  [4:0] Bit5_In,
  output [4:0] Bit5_Out,
  output Carry_Out
);

  wire and_1_out, and_2_out, and_3_out, and_4_out;

  and and_1 (and_1_out, Add_One, Bit5_In[0]);
  and and_2 (and_2_out, Add_One, Bit5_In[0], Bit5_In[1]);
  and and_3 (and_3_out, Add_One, Bit5_In[0], Bit5_In[1], Bit5_In[2]);
  and and_4 (and_4_out, Add_One, Bit5_In[0], Bit5_In[1], Bit5_In[2], Bit5_In[3]);
  and and_5 (Carry_Out, Add_One, Bit5_In[0], Bit5_In[1], Bit5_In[2], Bit5_In[3], Bit5_In[4]);
  xor xor_1 (Bit5_Out[0], Bit5_In[0], Add_One);
  xor xor_2 (Bit5_Out[1], Bit5_In[1], and_1_out);
  xor xor_3 (Bit5_Out[2], Bit5_In[2], and_2_out);
  xor xor_4 (Bit5_Out[3], Bit5_In[3], and_3_out);
  xor xor_5 (Bit5_Out[4], Bit5_In[4], and_4_out);
endmodule

module Bit11_To_Bit16_Low (
  input  [10:0] Bit11_In,
  output [15:0] Bit16_Out
);


  assign Bit16_Out = {{5{1'b0}}, Bit11_In};
endmodule

module Bit10_Controlled_Buffer (
  input  Enable,
  input  [9:0] Bit10_In,
  output [9:0] Bit10_Out
);

  and and_1 (Bit10_Out[0], Bit10_In[0], Enable);
  and and_2 (Bit10_Out[1], Bit10_In[1], Enable);
  and and_3 (Bit10_Out[2], Bit10_In[2], Enable);
  and and_4 (Bit10_Out[3], Bit10_In[3], Enable);
  and and_5 (Bit10_Out[4], Bit10_In[4], Enable);
  and and_6 (Bit10_Out[5], Bit10_In[5], Enable);
  and and_7 (Bit10_Out[6], Bit10_In[6], Enable);
  and and_8 (Bit10_Out[7], Bit10_In[7], Enable);
  and and_9 (Bit10_Out[8], Bit10_In[8], Enable);
  and and_10 (Bit10_Out[9], Bit10_In[9], Enable);
endmodule

module Bit5_Greater_Than (
  input  [4:0] Bit5_A,
  input  [4:0] Bit5_B,
  output A_Greater_B
);

  wire and_1_out, and_2_out, and_3_out, and_4_out, and_5_out, and_6_out, and_7_out, and_8_out, and_9_out,
       and_10_out, and_11_out, and_12_out, and_13_out, nor_1_out, nor_2_out, nor_3_out, nor_4_out;

  and and_1 (and_1_out, Bit5_B[4], ~Bit5_A[4]);  // AND_Gate
  and and_2 (and_2_out, Bit5_A[4], ~Bit5_B[4]);  // AND_Gate
  and and_3 (and_3_out, Bit5_B[3], ~Bit5_A[3]);  // AND_Gate
  and and_4 (and_4_out, Bit5_A[3], ~Bit5_B[3]);  // AND_Gate
  and and_5 (and_5_out, Bit5_B[2], ~Bit5_A[2]);  // AND_Gate
  and and_6 (and_6_out, Bit5_A[2], ~Bit5_B[2]);  // AND_Gate
  and and_7 (and_7_out, Bit5_B[1], ~Bit5_A[1]);  // AND_Gate
  and and_8 (and_8_out, Bit5_A[1], ~Bit5_B[1]);  // AND_Gate
  and and_9 (and_9_out, Bit5_A[0], ~Bit5_B[0]);  // AND_Gate
  nor nor_1 (nor_1_out, and_1_out, and_2_out);
  nor nor_2 (nor_2_out, and_3_out, and_4_out);
  nor nor_3 (nor_3_out, and_5_out, and_6_out);
  nor nor_4 (nor_4_out, and_7_out, and_8_out);
  and and_10 (and_10_out, nor_1_out, and_4_out);
  and and_11 (and_11_out, nor_1_out, nor_2_out, and_6_out);
  and and_12 (and_12_out, nor_1_out, nor_2_out, nor_3_out, and_8_out);
  and and_13 (and_13_out, nor_1_out, nor_2_out, nor_3_out, nor_4_out, and_9_out);
  or or_1 (A_Greater_B, and_2_out, and_10_out, and_11_out, and_12_out, and_13_out);
endmodule

module Bit5_Toggle_Inverter (
  input  Invert,
  input  [4:0] Bit5_In,
  output [4:0] Bit5_out
);

  xor xor_1 (Bit5_out[0], Invert, Bit5_In[0]);
  xor xor_2 (Bit5_out[1], Invert, Bit5_In[1]);
  xor xor_3 (Bit5_out[2], Invert, Bit5_In[2]);
  xor xor_4 (Bit5_out[3], Invert, Bit5_In[3]);
  xor xor_5 (Bit5_out[4], Invert, Bit5_In[4]);
endmodule

module fpu3 (
  input  ADD,
  input  SUB,
  input  MUL,
  input  DIV,
  input  [15:0] INPUT_A,
  input  [15:0] INPUT_B,
  input  [23:0] Bit24_Adder_Result_In,
  input  Bit24_Adder_C_OUT,
  input  [31:0] Bit32_Right_Shift_Result_In,
  input  [15:0] Bit16_Multiplier_Lower_Word,
  input  [15:0] Bit16_Multiplier_Upper_Word,
  input  [23:0] Bit24_Division_Result,
  input  [31:0] Bit32_Left_Shift_Result,
  output [15:0] Result,
  output Inexact,
  output Overflow,
  output Underflow,
  output Divide_By_Zero,
  output Invalid_Operation,
  output [23:0] Bit24_Adder_A_In,
  output [23:0] Bit24_Adder_B_In,
  output [31:0] Bit32_Right_Shift_In,
  output [4:0] Bit5_Right_Shift_In,
  output [15:0] Bit16_Multiplier_A,
  output [15:0] Bit16_Multiplier_B,
  output [23:0] Bit24_Dividend,
  output [23:0] Bit24_Divisor,
  output [31:0] Bit32_Left_Shift_In,
  output [4:0] Bit5_Left_Shift_In
);

  wire and_1_out, and_2_out, and_3_out, and_4_out, and_5_out, and_6_out, and_7_out, and_8_out, and_9_out,
       and_10_out, and_11_out, and_12_out, and_13_out, and_14_out, and_15_out, and_16_out, and_17_out,
       and_18_out, and_19_out, and_20_out, and_21_out, and_22_out, and_23_out, and_25_out, and_26_out,
       and_28_out, and_31_out, and_32_out, and_33_out, and_34_out, and_35_out, and_36_out, and_37_out,
       and_38_out, and_39_out, and_40_out, and_41_out, and_43_out, and_44_out, and_45_out, and_46_out,
       bit5_adder_1_cout, bit6_adder_2_cout, bit6_greater_than_1_a_greater_than_b, nor_1_out, nor_2_out,
       not_1_out, or_1_out, or_2_out, or_5_out, or_6_out, or_7_out, or_9_out, or_10_out, or_11_out,
       or_12_out, or_17_out, or_19_out, or_20_out, or_21_out, or_23_out, or_28_out, xor_1_out, xor_2_out,
       xor_3_out, xor_5_out, xor_6_out;
  wire [1:1] and_24_out, xor_4_out;
  wire [4:0] bit5_adder_1_bit5_result, bit5_controlled_buffer_1_bit5_out, bit5_controlled_buffer_2_bit5_out,
       bit5_inverter_1_bit5_out, or_15_out, plsbnormal_1_exponent;
  wire [5:0] bit5_to_6_low_1_bit6_out, bit5_to_6_low_2_bit6_out, bit5_to_6_low_3_bit6_out,
       bit6_adder_1_bit6_result, bit6_adder_2_bit6_result, bit6_controlled_buffer_1_bit6_output,
       bit6_toggle_twscmplmtr_1_bit6_result, or_24_out, or_25_out, or_26_out;
  wire [9:0] plsbnormal_1_mantissa;
  wire [10:0] bit11_controlled_buffer_1_bit11_out, bit11_controlled_buffer_2_bit11_out,
       bit11_controlled_buffer_3_bit11_out, bit11_controlled_buffer_4_bit11_out,
       bit11_controlled_buffer_5_bit11_out, bit11_controlled_buffer_6_bit11_out,
       bit11_controlled_buffer_7_bit11_out, bit11_controlled_buffer_8_bit11_out, or_13_out, or_14_out;
  wire [10:10] or_3_out, or_4_out;
  wire [15:0] bit11_to_bit16_high_1_bit16_out, bit11_to_bit16_high_2_bit16_out,
       bit11_to_bit16_low_3_bit16_out, bit16_controlled_buffer_1_bit16_out,
       bit16_controlled_buffer_2_bit16_out;
  wire [15:8] or_8_out;
  wire [15:15] or_22_out;
  wire [23:0] bit16_to_bit24_high_byte_1_bit24, bit24_controlled_buffer_1_bit24_out,
       bit24_controlled_buffer_2_bit24_out, bit24_toggle_twscmplmtr_3_bit24_out,
       bit32_to_bit24_high_1_bit24_out;
  wire [31:0] or_27_out;
  wire [31:31] and_42_out;

  // Probe on INPUT_A
  // Probe on INPUT_B
  or or_1 (or_1_out, ADD, SUB);
  or or_2 (or_2_out, ADD, SUB, MUL, DIV);
  or or_3 (or_3_out[10], INPUT_A[10], INPUT_A[11], INPUT_A[12], INPUT_A[13], INPUT_A[14]);
  or or_4 (or_4_out[10], INPUT_B[10], INPUT_B[11], INPUT_B[12], INPUT_B[13], INPUT_B[14]);
  Bit5_Inverter bit5_inverter_1 (.Bit5_In(INPUT_B[14:10]), .Bit5_Out(bit5_inverter_1_bit5_out));
  or or_5 (or_5_out, INPUT_A[0], INPUT_A[1], INPUT_A[2], INPUT_A[3], INPUT_A[4], INPUT_A[5], INPUT_A[6], INPUT_A[7], INPUT_A[8]);
  or or_6 (or_6_out, INPUT_B[0], INPUT_B[1], INPUT_B[2], INPUT_B[3], INPUT_B[4], INPUT_B[5], INPUT_B[6], INPUT_B[7], INPUT_B[8]);
  or or_7 (or_7_out, ADD, SUB);
  and and_1 (and_1_out, or_2_out, or_12_out);
  and and_2 (and_2_out, or_2_out, ~or_12_out);  // AND_Gate
  and and_3 (and_3_out, INPUT_A[10], INPUT_A[11], INPUT_A[12], INPUT_A[13], INPUT_A[14], ~INPUT_A[9], or_5_out);  // AND_Gate
  and and_4 (and_4_out, ~or_5_out, INPUT_A[9], INPUT_A[10], INPUT_A[11], INPUT_A[12], INPUT_A[13], INPUT_A[14]);  // AND_Gate
  and and_5 (and_5_out, ~INPUT_A[9], INPUT_A[10], INPUT_A[11], INPUT_A[12], INPUT_A[13], INPUT_A[14]);  // AND_Gate
  nor nor_1 (nor_1_out, INPUT_A[0], INPUT_A[1], INPUT_A[2], INPUT_A[3], INPUT_A[4], INPUT_A[5], INPUT_A[6], INPUT_A[7], INPUT_A[8], INPUT_A[9], INPUT_A[10], INPUT_A[11], INPUT_A[12], INPUT_A[13], INPUT_A[14]);
  and and_6 (and_6_out, INPUT_B[10], INPUT_B[11], INPUT_B[12], INPUT_B[13], INPUT_B[14], ~INPUT_B[9], or_6_out);  // AND_Gate
  and and_7 (and_7_out, ~or_6_out, INPUT_B[9], INPUT_B[10], INPUT_B[11], INPUT_B[12], INPUT_B[13], INPUT_B[14]);  // AND_Gate
  and and_8 (and_8_out, ~INPUT_B[9], INPUT_B[10], INPUT_B[11], INPUT_B[12], INPUT_B[13], INPUT_B[14]);  // AND_Gate
  nor nor_2 (nor_2_out, INPUT_B[0], INPUT_B[1], INPUT_B[2], INPUT_B[3], INPUT_B[4], INPUT_B[5], INPUT_B[6], INPUT_B[7], INPUT_B[8], INPUT_B[9], INPUT_B[10], INPUT_B[11], INPUT_B[12], INPUT_B[13], INPUT_B[14]);
  Bit5_Adder bit5_adder_1 (
    .Cin(1'b1), .Bit5_A(INPUT_A[14:10]), .Bit5_B(bit5_inverter_1_bit5_out),
    .Bit5_Result(bit5_adder_1_bit5_result), .Cout(bit5_adder_1_cout));
  or or_8 (or_8_out[8], and_3_out, and_6_out);
  and and_9 (and_9_out, nor_1_out, MUL, and_8_out);
  xor xor_1 (xor_1_out, SUB, INPUT_B[15]);
  or or_9 (or_9_out, MUL, DIV);
  xor xor_2 (xor_2_out, INPUT_A[15], INPUT_B[15]);
  and and_10 (and_10_out, ~SUB, INPUT_B[15], INPUT_A[15]);  // AND_Gate
  and and_11 (and_11_out, SUB, ~INPUT_B[15], INPUT_A[15]);  // AND_Gate
  xor xor_3 (xor_3_out, SUB, INPUT_A[15]);
  and and_12 (and_12_out, or_7_out, ~bit5_adder_1_cout);  // AND_Gate
  and and_13 (and_13_out, or_7_out, bit5_adder_1_cout);
  and and_14 (and_14_out, or_7_out, ~bit5_adder_1_cout);  // AND_Gate
  and and_15 (and_15_out, or_7_out, bit5_adder_1_cout);
  not not_1 (not_1_out, bit5_adder_1_cout);
  and and_16 (and_16_out, bit5_adder_1_cout, or_7_out);
  and and_17 (and_17_out, or_7_out, ~bit5_adder_1_cout);  // AND_Gate
  and and_18 (and_18_out, and_5_out, MUL, nor_2_out);
  and and_19 (and_19_out, or_9_out, xor_2_out);
  or or_10 (or_10_out, and_10_out, and_11_out);
  xor xor_4 (xor_4_out[1], xor_3_out, INPUT_B[15]);
  and and_20 (and_20_out, or_2_out, or_11_out);
  or or_11 (or_11_out, and_3_out, and_4_out, and_6_out, and_7_out);
  and and_21 (and_21_out, xor_4_out[1], Bit24_Adder_C_OUT);
  or or_12 (or_12_out, or_17_out, and_28_out, Invalid_Operation);
  and and_22 (and_22_out, xor_4_out[1], or_1_out, and_5_out, and_8_out);
  and and_23 (and_23_out, DIV, and_5_out, and_8_out);
  xor xor_5 (xor_5_out, or_10_out, and_21_out);
  and and_24 (and_24_out[1], ~xor_4_out[1], or_7_out);  // AND_Gate
  Bit11_Controlled_Buffer bit11_controlled_buffer_1 (
    .Enable(and_12_out), .Bit11_In({or_4_out[10], INPUT_B[9:0]}),
    .Bit11_Out(bit11_controlled_buffer_1_bit11_out));
  assign or_13_out = bit11_controlled_buffer_1_bit11_out | bit11_controlled_buffer_2_bit11_out;  // OR_Gate or_13, 11 bits wide
  Bit11_Controlled_Buffer bit11_controlled_buffer_2 (
    .Enable(and_13_out), .Bit11_In({or_3_out[10], INPUT_A[9:0]}),
    .Bit11_Out(bit11_controlled_buffer_2_bit11_out));
  Bit11_Controlled_Buffer bit11_controlled_buffer_3 (
    .Enable(and_14_out), .Bit11_In({or_3_out[10], INPUT_A[9:0]}),
    .Bit11_Out(bit11_controlled_buffer_3_bit11_out));
  assign or_14_out = bit11_controlled_buffer_3_bit11_out | bit11_controlled_buffer_4_bit11_out;  // OR_Gate or_14, 11 bits wide
  Bit11_Controlled_Buffer bit11_controlled_buffer_4 (
    .Enable(and_15_out), .Bit11_In({or_4_out[10], INPUT_B[9:0]}),
    .Bit11_Out(bit11_controlled_buffer_4_bit11_out));
  Bit5_Toggle_TwsCmplmtr bit5_toggle_twscmplmtr_1 (
    .Bit5_Input(bit5_adder_1_bit5_result), .Enable_Twos(not_1_out), .Bit5_Result(Bit5_Right_Shift_In));
  Bit5_Controlled_Buffer bit5_controlled_buffer_1 (
    .Bit5_In(INPUT_A[14:10]), .Enable(and_16_out), .Bit5_Out(bit5_controlled_buffer_1_bit5_out));
  assign or_15_out = bit5_controlled_buffer_1_bit5_out | bit5_controlled_buffer_2_bit5_out;  // OR_Gate or_15, 5 bits wide
  Bit5_Controlled_Buffer bit5_controlled_buffer_2 (
    .Bit5_In(INPUT_B[14:10]), .Enable(and_17_out), .Bit5_Out(bit5_controlled_buffer_2_bit5_out));
  or or_16 (Invalid_Operation, and_9_out, and_18_out, and_22_out, and_23_out, and_25_out);
  and and_25 (and_25_out, DIV, nor_1_out, nor_2_out);
  BIT5_To_6_LOW bit5_to_6_low_1 (.Bit5_In(or_15_out), .Bit6_Out(bit5_to_6_low_1_bit6_out));
  and and_26 (and_26_out, ~Invalid_Operation, or_17_out);  // AND_Gate
  or or_17 (or_17_out, Divide_By_Zero, and_32_out, and_36_out, and_37_out, and_38_out);
  and and_27 (Divide_By_Zero, DIV, nor_2_out, ~and_5_out, ~nor_1_out);  // AND_Gate
  or or_18 (or_8_out[14], Invalid_Operation, and_26_out);
  and and_28 (and_28_out, DIV, and_8_out, ~and_5_out, ~nor_1_out);  // AND_Gate
  Bit11_To_Bit16_High bit11_to_bit16_high_1 (.Bit11_In(or_13_out), .Bit16_Out(bit11_to_bit16_high_1_bit16_out));
  Bit11_To_Bit32_High bit11_to_bit32_high_1 (.Bit11_In(or_14_out), .Bit32_Out(Bit32_Right_Shift_In));
  and and_29 (or_8_out[9], ~or_8_out[8], and_20_out);  // AND_Gate
  and and_30 (or_8_out[15], ~Invalid_Operation, or_19_out);  // AND_Gate
  or or_19 (or_19_out, and_31_out, and_33_out);
  and and_31 (and_31_out, or_17_out, xor_2_out);
  and and_32 (and_32_out, or_20_out, or_1_out);
  or or_20 (or_20_out, and_5_out, and_8_out);
  and and_33 (and_33_out, or_1_out, or_21_out);
  or or_21 (or_21_out, and_34_out, and_35_out);
  and and_34 (and_34_out, and_5_out, INPUT_A[15]);
  and and_35 (and_35_out, xor_1_out, and_8_out);
  and and_36 (and_36_out, MUL, and_8_out, ~and_5_out, ~nor_1_out);  // AND_Gate
  Bit16_To_Bit24_High_Byte bit16_to_bit24_high_byte_1 (
    .Bit16(bit11_to_bit16_high_1_bit16_out), .Bit24(bit16_to_bit24_high_byte_1_bit24));
  and and_37 (and_37_out, and_5_out, MUL, ~and_8_out, ~nor_2_out);  // AND_Gate
  and and_38 (and_38_out, MUL, and_5_out, and_8_out);
  and and_39 (and_39_out, xor_4_out[1], ~bit5_adder_1_cout);  // AND_Gate
  and and_40 (and_40_out, xor_4_out[1], bit5_adder_1_cout);
  Bit32_To_Bit24_High bit32_to_bit24_high_1 (
    .Bit32_In(Bit32_Right_Shift_Result_In), .Bit24_Out(bit32_to_bit24_high_1_bit24_out));
  Bit24_Toggle_TwsCmplmtr bit24_toggle_twscmplmtr_1 (
    .Enable(and_39_out), .Bit24_In(bit16_to_bit24_high_byte_1_bit24), .Bit24_Out(Bit24_Adder_A_In));
  Bit24_Controlled_Buffer bit24_controlled_buffer_1 (
    .Enable(or_7_out), .Bit24_In(bit32_to_bit24_high_1_bit24_out),
    .Bit24_Out(bit24_controlled_buffer_1_bit24_out));
  Bit24_Toggle_TwsCmplmtr bit24_toggle_twscmplmtr_2 (
    .Enable(and_40_out), .Bit24_In(bit24_controlled_buffer_1_bit24_out), .Bit24_Out(Bit24_Adder_B_In));
  and and_41 (and_41_out, xor_4_out[1], ~Bit24_Adder_C_OUT);  // AND_Gate
  and and_42 (and_42_out[31], Bit24_Adder_C_OUT, ~xor_5_out);  // AND_Gate
  and and_43 (and_43_out, ~xor_4_out[1], Bit24_Adder_C_OUT);  // AND_Gate
  xor xor_6 (xor_6_out, xor_5_out, xor_4_out[1]);
  and and_44 (and_44_out, xor_6_out, or_7_out);
  or or_22 (or_22_out[15], and_19_out, and_44_out);
  Bit24_Toggle_TwsCmplmtr bit24_toggle_twscmplmtr_3 (
    .Enable(and_41_out), .Bit24_In(Bit24_Adder_Result_In), .Bit24_Out(bit24_toggle_twscmplmtr_3_bit24_out));
  BIT5_To_6_LOW bit5_to_6_low_2 (.Bit5_In(INPUT_B[14:10]), .Bit6_Out(bit5_to_6_low_2_bit6_out));
  or or_23 (or_23_out, MUL, DIV);
  assign or_24_out = {4'b0000, and_24_out[1], 1'b0} | {4'b0000, xor_4_out[1], 1'b0} | {2'b00, MUL, 1'b0, {2{MUL}}} | {{5{1'b0}}, DIV};  // OR_Gate or_24, 6 bits wide
  Bit6_Toggle_TwsCmplmtr bit6_toggle_twscmplmtr_1 (
    .Bit6_Input(bit5_to_6_low_2_bit6_out), .Enable_Twos(DIV),
    .Bit6_Result(bit6_toggle_twscmplmtr_1_bit6_result));
  Bit11_Controlled_Buffer bit11_controlled_buffer_5 (
    .Enable(MUL), .Bit11_In({or_3_out[10], INPUT_A[9:0]}), .Bit11_Out(bit11_controlled_buffer_5_bit11_out));
  Bit11_Controlled_Buffer bit11_controlled_buffer_6 (
    .Enable(MUL), .Bit11_In({or_4_out[10], INPUT_B[9:0]}), .Bit11_Out(bit11_controlled_buffer_6_bit11_out));
  Bit11_Controlled_Buffer bit11_controlled_buffer_7 (
    .Enable(DIV), .Bit11_In({or_3_out[10], INPUT_A[9:0]}), .Bit11_Out(bit11_controlled_buffer_7_bit11_out));
  Bit11_Controlled_Buffer bit11_controlled_buffer_8 (
    .Enable(DIV), .Bit11_In({or_4_out[10], INPUT_B[9:0]}), .Bit11_Out(bit11_controlled_buffer_8_bit11_out));
  assign or_25_out = bit5_to_6_low_1_bit6_out | bit6_controlled_buffer_1_bit6_output;  // OR_Gate or_25, 6 bits wide
  Bit6_Controlled_Buffer bit6_controlled_buffer_1 (
    .Enable(or_23_out), .Bit6_Input(bit6_adder_2_bit6_result),
    .Bit6_Output(bit6_controlled_buffer_1_bit6_output));
  BIT5_To_6_LOW bit5_to_6_low_3 (.Bit5_In(INPUT_A[14:10]), .Bit6_Out(bit5_to_6_low_3_bit6_out));
  Bit11_To_Bit16_Low bit11_to_bit16_low_1 (
    .Bit11_In(bit11_controlled_buffer_5_bit11_out), .Bit16_Out(Bit16_Multiplier_A));
  Bit11_To_Bit16_Low bit11_to_bit16_low_2 (
    .Bit11_In(bit11_controlled_buffer_6_bit11_out), .Bit16_Out(Bit16_Multiplier_B));
  Bit11_To_Bit16_High bit11_to_bit16_high_2 (
    .Bit11_In(bit11_controlled_buffer_7_bit11_out), .Bit16_Out(bit11_to_bit16_high_2_bit16_out));
  Bit11_To_Bit16_Low bit11_to_bit16_low_3 (
    .Bit11_In(bit11_controlled_buffer_8_bit11_out), .Bit16_Out(bit11_to_bit16_low_3_bit16_out));
  Bit6_Greater_Than bit6_greater_than_1 (
    .Bit6_A(bit6_controlled_buffer_1_bit6_output), .Bit6_B(6'b010010),
    .A_Greater_Than_B(bit6_greater_than_1_a_greater_than_b));
  Bit6_Adder bit6_adder_1 (
    .Bit6_A(bit5_to_6_low_3_bit6_out), .Bit6_B(bit6_toggle_twscmplmtr_1_bit6_result),
    .Bit6_Result(bit6_adder_1_bit6_result));  // open: Cin, Cout
  assign or_26_out = {DIV, {5{1'b0}}} | {{2{MUL}}, 3'b000, MUL};  // OR_Gate or_26, 6 bits wide
  and and_45 (and_45_out, bit6_greater_than_1_a_greater_than_b, DIV);
  Bit16_To_Bit24_High_Byte bit16_to_bit24_high_byte_2 (.Bit16(bit11_to_bit16_high_2_bit16_out), .Bit24(Bit24_Dividend));
  Bit16_To_Bit24_Low_Byte bit16_to_bit24_low_byte_1 (.Bit16(bit11_to_bit16_low_3_bit16_out), .Bit24(Bit24_Divisor));
  Bit6_Adder bit6_adder_2 (
    .Bit6_A(bit6_adder_1_bit6_result), .Bit6_B(or_26_out), .Bit6_Result(bit6_adder_2_bit6_result),
    .Cout(bit6_adder_2_cout));  // open: Cin
  and and_46 (and_46_out, MUL, bit6_adder_2_cout);
  Bit16_Controlled_Buffer bit16_controlled_buffer_1 (
    .Enable(MUL), .Bit16_In(Bit16_Multiplier_Lower_Word), .Bit16_Out(bit16_controlled_buffer_1_bit16_out));
  Bit16_Controlled_Buffer bit16_controlled_buffer_2 (
    .Enable(MUL), .Bit16_In(Bit16_Multiplier_Upper_Word), .Bit16_Out(bit16_controlled_buffer_2_bit16_out));
  assign or_27_out = {and_42_out[31], bit24_toggle_twscmplmtr_3_bit24_out, {7{1'b0}}} | {bit16_controlled_buffer_2_bit16_out, bit16_controlled_buffer_1_bit16_out} | {{8{1'b0}}, bit24_controlled_buffer_2_bit24_out};  // OR_Gate or_27, 32 bits wide
  Bit24_Controlled_Buffer bit24_controlled_buffer_2 (
    .Enable(DIV), .Bit24_In(Bit24_Division_Result), .Bit24_Out(bit24_controlled_buffer_2_bit24_out));
  or or_28 (or_28_out, and_46_out, and_45_out);
  plsbnormal plsbnormal_1 (
    .INPT(or_27_out), .CURRENT_EXP(or_25_out), .OFFSET_EXP(or_24_out), .Cin(or_28_out), .Multiplication(MUL),
    .Division(DIV), .Addition(and_24_out[1]), .Subtraction_Negative_Infinity(and_43_out),
    .Bit32_Left_Shift_Result(Bit32_Left_Shift_Result), .Mantissa(plsbnormal_1_mantissa),
    .Exponent(plsbnormal_1_exponent), .Inexact(Inexact), .Overflow(Overflow), .Underflow(Underflow),
    .Bit32_Left_Shift_In(Bit32_Left_Shift_In), .Bit5_Left_Shift_In(Bit5_Left_Shift_In));
  Pull_Resistor pull_resistor_1 (.node(Result));
  assign Result = and_2_out ? {or_22_out[15], plsbnormal_1_exponent, plsbnormal_1_mantissa} : 16'bz;  // Controlled_Buffer controlled_buffer_1
  assign Result = and_1_out ? {or_8_out[15:14], {4{or_8_out[14]}}, or_8_out[9:8], {8{or_8_out[8]}}} : 16'bz;  // Controlled_Buffer controlled_buffer_2
  // Probe on Result

  // Notes on the sheet:
  //   snan
  //   qnan
  //   infinity
  //   zero
  //   snan
  //   qnan
  //   infinity
  //   zero
  //   qnan
  //   prop nan pri snan
  //   qnazn
  //   qnazn
  //   inf w/ xor sign
  //   d by 0
  //   xor sign
  //   0
  //   inf
  //   neg
  //   infs w/ xor sign
  //   mul
  //   div
  //   mant
  //   exp
endmodule

module normaliser (
  input  [31:0] Inpt,
  input  [4:0] Current_Exponent,
  input  [4:0] Final_Offset_Exponent_ADD_SUB,
  input  MUL,
  input  DIV,
  output [9:0] Mantissa,
  output [4:0] Exponent
);

  wire and_1_out, and_2_out, and_3_out, and_4_out, bit5_adder_1_cout, bit5_adder_2_cout, bit5_adder_5_cout,
       nand_1_out, nor_1_out, not_1_out, not_2_out, or_1_out, or_3_out, or_4_out, priority_encoder_1_gs;
  wire [4:0] bit5_adder_1_bit5_result, bit5_adder_2_bit5_result, bit5_adder_3_bit5_result,
       bit5_adder_4_bit5_result, bit5_adder_5_bit5_result, bit5_adder_6_bit5_result,
       bit5_controlled_buffer_1_bit5_out, bit5_controlled_buffer_2_bit5_out,
       bit5_controlled_buffer_3_bit5_out, bit5_twos_complementer_1_bit5_result,
       bit5_twos_complementer_2_bit5_result, or_2_out, priority_encoder_1_out, undriven;
  wire [4:4] and_5_out;
  wire [31:0] bit32_left_shift_1_bit32_result;

  Priority_Encoder #(.select(5)) priority_encoder_1 (
    .in0(Inpt[0]), .in1(Inpt[1]), .in2(Inpt[2]), .in3(Inpt[3]), .in4(Inpt[4]), .in5(Inpt[5]), .in6(Inpt[6]),
    .in7(Inpt[7]), .in8(Inpt[8]), .in9(Inpt[9]), .in10(Inpt[10]), .in11(Inpt[11]), .in12(Inpt[12]),
    .in13(Inpt[13]), .in14(Inpt[14]), .in15(Inpt[15]), .in16(Inpt[16]), .in17(Inpt[17]), .in18(Inpt[18]),
    .in19(Inpt[19]), .in20(Inpt[20]), .in21(Inpt[21]), .in22(Inpt[22]), .in23(Inpt[23]), .in24(Inpt[24]),
    .in25(Inpt[25]), .in26(Inpt[26]), .in27(Inpt[27]), .in28(Inpt[28]), .in29(Inpt[29]), .in30(Inpt[30]),
    .in31(Inpt[31]), .out(priority_encoder_1_out), .gs(priority_encoder_1_gs));  // open: en_out, en_in
  Bit5_Adder bit5_adder_1 (
    .Bit5_A(Current_Exponent), .Bit5_B(Final_Offset_Exponent_ADD_SUB),
    .Bit5_Result(bit5_adder_1_bit5_result), .Cout(bit5_adder_1_cout));  // open: Cin
  // Probe on bit5_adder_1_bit5_result
  // Probe on priority_encoder_1_out
  // Probe on bit5_twos_complementer_1_bit5_result
  Bit5_Twos_Complementer bit5_twos_complementer_1 (
    .Bit5_In(priority_encoder_1_out), .Bit5_Result(bit5_twos_complementer_1_bit5_result));
  Bit5_Adder bit5_adder_2 (
    .Bit5_A(priority_encoder_1_out), .Bit5_B(bit5_adder_1_bit5_result),
    .Bit5_Result(bit5_adder_2_bit5_result), .Cout(bit5_adder_2_cout));  // open: Cin
  // Probe on bit5_adder_2_bit5_result
  or or_1 (or_1_out, bit5_adder_2_cout, bit5_adder_1_cout);
  and and_1 (and_1_out, priority_encoder_1_gs, or_1_out);
  not not_1 (not_1_out, or_1_out);
  not not_2 (not_2_out, bit5_adder_2_cout);
  Bit5_Controlled_Buffer bit5_controlled_buffer_1 (
    .Bit5_In(bit5_twos_complementer_1_bit5_result), .Enable(and_1_out),
    .Bit5_Out(bit5_controlled_buffer_1_bit5_out));
  Bit5_Controlled_Buffer bit5_controlled_buffer_2 (
    .Bit5_In(bit5_adder_1_bit5_result), .Enable(not_1_out), .Bit5_Out(bit5_controlled_buffer_2_bit5_out));
  and and_2 (and_2_out, not_2_out, MUL);
  and and_3 (and_3_out, bit5_adder_1_cout, MUL);
  assign or_2_out = bit5_controlled_buffer_1_bit5_out | bit5_controlled_buffer_2_bit5_out;  // OR_Gate or_2, 5 bits wide
  Bit5_Twos_Complementer bit5_twos_complementer_2 (
    .Bit5_In(or_2_out), .Bit5_Result(bit5_twos_complementer_2_bit5_result));
  Bit5_Controlled_Buffer bit5_controlled_buffer_3 (
    .Bit5_In({bit5_adder_2_bit5_result[3:0], 1'b0}), .Enable(and_2_out),
    .Bit5_Out(bit5_controlled_buffer_3_bit5_out));
  Bit5_Adder bit5_adder_3 (
    .Bit5_A(or_2_out), .Bit5_B(bit5_controlled_buffer_3_bit5_out), .Bit5_Result(bit5_adder_3_bit5_result));  // open: Cin, Cout
  Bit32_Left_Shift bit32_left_shift_1 (
    .Bit32_In(Inpt), .Bit5_Shift(bit5_adder_3_bit5_result), .Bit32_Result(bit32_left_shift_1_bit32_result));
  Bit5_Adder bit5_adder_4 (
    .Bit5_A(bit5_twos_complementer_2_bit5_result), .Bit5_B(Current_Exponent),
    .Bit5_Result(bit5_adder_4_bit5_result));  // open: Cin, Cout
  or or_3 (or_3_out, bit32_left_shift_1_bit32_result[9], bit32_left_shift_1_bit32_result[0], bit32_left_shift_1_bit32_result[1], bit32_left_shift_1_bit32_result[2], bit32_left_shift_1_bit32_result[3], bit32_left_shift_1_bit32_result[4], bit32_left_shift_1_bit32_result[5], bit32_left_shift_1_bit32_result[6], bit32_left_shift_1_bit32_result[7], bit32_left_shift_1_bit32_result[8], bit32_left_shift_1_bit32_result[10], bit32_left_shift_1_bit32_result[11], bit32_left_shift_1_bit32_result[12], bit32_left_shift_1_bit32_result[13], bit32_left_shift_1_bit32_result[14], bit32_left_shift_1_bit32_result[15], bit32_left_shift_1_bit32_result[16], bit32_left_shift_1_bit32_result[17], bit32_left_shift_1_bit32_result[18], bit32_left_shift_1_bit32_result[19]);
  and and_4 (and_4_out, bit32_left_shift_1_bit32_result[21], or_4_out);
  or or_4 (or_4_out, or_3_out, bit32_left_shift_1_bit32_result[20]);
  Bit5_Adder bit5_adder_5 (
    .Cin(and_3_out), .Bit5_A(bit5_adder_4_bit5_result), .Bit5_B(Final_Offset_Exponent_ADD_SUB),
    .Bit5_Result(bit5_adder_5_bit5_result), .Cout(bit5_adder_5_cout));
  and and_5 (and_5_out[4], DIV, bit5_adder_5_cout, ~nor_1_out);  // AND_Gate
  nor nor_1 (nor_1_out, bit5_adder_5_bit5_result[0], bit5_adder_5_bit5_result[1], bit5_adder_5_bit5_result[2], bit5_adder_5_bit5_result[3], bit5_adder_5_bit5_result[4]);
  nand nand_1 (nand_1_out, nor_1_out, ~bit5_adder_5_cout, DIV);  // NAND_Gate
  Bit5_Adder bit5_adder_6 (
    .Bit5_A(bit5_adder_5_bit5_result), .Bit5_B({and_5_out[4], 1'b0, {2{and_5_out[4]}}, 1'b0}),
    .Bit5_Result(bit5_adder_6_bit5_result));  // open: Cin, Cout
  Bit10_Controlled_Buffer bit10_controlled_buffer_1 (
    .Enable(nand_1_out), .Bit10_In(bit32_left_shift_1_bit32_result[31:22]), .Bit10_Out(Mantissa));
  Bit5_Adder bit5_adder_7 (
    .Bit5_A(bit5_adder_6_bit5_result), .Bit5_B(undriven), .Bit5_Result(Exponent));  // open: Cin, Cout
  // Probe on Exponent
endmodule

module Bit5_GT_EQ (
  input  [4:0] Bit5_A,
  input  [4:0] Bit5_B,
  output A_Greater_EQ_B
);

  wire and_1_out, and_2_out, and_3_out, and_4_out, and_5_out, and_6_out, and_7_out, and_8_out, and_9_out,
       and_10_out, and_11_out, and_12_out, and_13_out, nor_1_out, nor_2_out, nor_3_out, nor_4_out, nor_5_out,
       xor_1_out, xor_2_out, xor_3_out, xor_4_out, xor_5_out;

  and and_1 (and_1_out, Bit5_B[4], ~Bit5_A[4]);  // AND_Gate
  and and_2 (and_2_out, Bit5_A[4], ~Bit5_B[4]);  // AND_Gate
  and and_3 (and_3_out, Bit5_B[3], ~Bit5_A[3]);  // AND_Gate
  and and_4 (and_4_out, Bit5_A[3], ~Bit5_B[3]);  // AND_Gate
  and and_5 (and_5_out, Bit5_B[2], ~Bit5_A[2]);  // AND_Gate
  and and_6 (and_6_out, Bit5_A[2], ~Bit5_B[2]);  // AND_Gate
  and and_7 (and_7_out, Bit5_B[1], ~Bit5_A[1]);  // AND_Gate
  and and_8 (and_8_out, Bit5_A[1], ~Bit5_B[1]);  // AND_Gate
  and and_9 (and_9_out, Bit5_A[0], ~Bit5_B[0]);  // AND_Gate
  xor xor_1 (xor_1_out, Bit5_A[0], Bit5_B[0]);
  xor xor_2 (xor_2_out, Bit5_B[1], Bit5_A[1]);
  xor xor_3 (xor_3_out, Bit5_B[2], Bit5_A[2]);
  xor xor_4 (xor_4_out, Bit5_B[3], Bit5_A[3]);
  xor xor_5 (xor_5_out, Bit5_A[4], Bit5_B[4]);
  nor nor_1 (nor_1_out, and_1_out, and_2_out);
  nor nor_2 (nor_2_out, and_3_out, and_4_out);
  nor nor_3 (nor_3_out, and_5_out, and_6_out);
  nor nor_4 (nor_4_out, and_7_out, and_8_out);
  nor nor_5 (nor_5_out, xor_1_out, xor_2_out, xor_3_out, xor_4_out, xor_5_out);
  and and_10 (and_10_out, nor_1_out, and_4_out);
  and and_11 (and_11_out, nor_1_out, nor_2_out, and_6_out);
  and and_12 (and_12_out, nor_1_out, nor_2_out, nor_3_out, and_8_out);
  and and_13 (and_13_out, nor_1_out, nor_2_out, nor_3_out, nor_4_out, and_9_out);
  or or_1 (A_Greater_EQ_B, and_2_out, and_10_out, and_11_out, and_12_out, and_13_out, nor_5_out);
endmodule

module BIT5_EQ (
  input  [4:0] Bit5_A,
  input  [4:0] Bit5_B,
  output A_EQ_B
);

  wire xor_1_out, xor_2_out, xor_3_out, xor_4_out, xor_5_out;

  xor xor_1 (xor_1_out, Bit5_A[0], Bit5_B[0]);
  xor xor_2 (xor_2_out, Bit5_A[1], Bit5_B[1]);
  xor xor_3 (xor_3_out, Bit5_A[2], Bit5_B[2]);
  xor xor_4 (xor_4_out, Bit5_A[3], Bit5_B[3]);
  xor xor_5 (xor_5_out, Bit5_A[4], Bit5_B[4]);
  nor nor_1 (A_EQ_B, xor_1_out, xor_2_out, xor_3_out, xor_4_out, xor_5_out);
endmodule

module plsbnormal (
  input  [31:0] INPT,
  input  [5:0] CURRENT_EXP,
  input  [5:0] OFFSET_EXP,
  input  Cin,
  input  Multiplication,
  input  Division,
  input  Addition,
  input  Subtraction_Negative_Infinity,
  input  [31:0] Bit32_Left_Shift_Result,
  output [9:0] Mantissa,
  output [4:0] Exponent,
  output Inexact,
  output Overflow,
  output Underflow,
  output [31:0] Bit32_Left_Shift_In,
  output [4:0] Bit5_Left_Shift_In
);

  wire and_1_out, and_2_out, and_4_out, and_5_out, and_6_out, bit6_adder_1_cout, bit6_gt_eq_1_a_greater_eq_b,
       bit10_add_one_1_carry_out, nor_1_out, nor_2_out, nor_3_out, not_1_out, not_2_out, or_1_out, or_3_out,
       or_4_out, or_5_out, or_6_out, priority_encoder_1_gs, xor_1_out, xor_2_out;
  wire [4:0] bit5_add_one_1_bit5_out, bit5_controlled_buffer_1_bit5_out, bit5_controlled_buffer_3_bit5_out,
       bit5_twos_complementer_1_bit5_result, bit6_to_5_exmsb_1_bit5_out, bit6_to_5_exmsb_2_bit5_out,
       priority_encoder_1_out;
  wire [4:4] not_3_out;
  wire [5:0] bit5_to_6_low_1_bit6_out, bit5_to_6_low_2_bit6_out, bit6_adder_1_bit6_result,
       bit6_adder_2_bit6_result, bit6_adder_3_bit6_result, bit6_controlled_buffer_1_bit6_output,
       bit6_twos_complementer_1_bit6_result, or_2_out;
  wire [9:0] bit10_add_one_1_bit10_out;

  Priority_Encoder #(.select(5)) priority_encoder_1 (
    .in0(INPT[0]), .in1(INPT[1]), .in2(INPT[2]), .in3(INPT[3]), .in4(INPT[4]), .in5(INPT[5]), .in6(INPT[6]),
    .in7(INPT[7]), .in8(INPT[8]), .in9(INPT[9]), .in10(INPT[10]), .in11(INPT[11]), .in12(INPT[12]),
    .in13(INPT[13]), .in14(INPT[14]), .in15(INPT[15]), .in16(INPT[16]), .in17(INPT[17]), .in18(INPT[18]),
    .in19(INPT[19]), .in20(INPT[20]), .in21(INPT[21]), .in22(INPT[22]), .in23(INPT[23]), .in24(INPT[24]),
    .in25(INPT[25]), .in26(INPT[26]), .in27(INPT[27]), .in28(INPT[28]), .in29(INPT[29]), .in30(INPT[30]),
    .in31(INPT[31]), .out(priority_encoder_1_out), .gs(priority_encoder_1_gs));  // open: en_out, en_in
  and and_1 (and_1_out, CURRENT_EXP[5], Multiplication);
  Bit6_Adder bit6_adder_1 (
    .Cin(Cin), .Bit6_A(CURRENT_EXP), .Bit6_B(OFFSET_EXP), .Bit6_Result(bit6_adder_1_bit6_result),
    .Cout(bit6_adder_1_cout));
  Bit5_Twos_Complementer bit5_twos_complementer_1 (
    .Bit5_In(priority_encoder_1_out), .Bit5_Result(bit5_twos_complementer_1_bit5_result));
  BIT5_To_6_LOW bit5_to_6_low_1 (.Bit5_In(bit5_twos_complementer_1_bit5_result), .Bit6_Out(bit5_to_6_low_1_bit6_out));
  xor xor_1 (xor_1_out, OFFSET_EXP[5], bit6_adder_1_cout);
  or or_1 (or_1_out, xor_1_out, bit6_gt_eq_1_a_greater_eq_b);
  Bit6_GT_EQ bit6_gt_eq_1 (
    .Bit6_A(bit6_adder_1_bit6_result), .Bit6_B(bit5_to_6_low_1_bit6_out),
    .A_Greater_EQ_B(bit6_gt_eq_1_a_greater_eq_b));
  not not_1 (not_1_out, xor_2_out);
  xor xor_2 (xor_2_out, or_1_out, and_1_out);
  Bit5_Controlled_Buffer bit5_controlled_buffer_1 (
    .Bit5_In(bit5_twos_complementer_1_bit5_result), .Enable(xor_2_out),
    .Bit5_Out(bit5_controlled_buffer_1_bit5_out));
  BIT5_To_6_LOW bit5_to_6_low_2 (.Bit5_In(bit5_controlled_buffer_1_bit5_out), .Bit6_Out(bit5_to_6_low_2_bit6_out));
  Bit6_Controlled_Buffer bit6_controlled_buffer_1 (
    .Enable(not_1_out), .Bit6_Input(bit6_adder_1_bit6_result),
    .Bit6_Output(bit6_controlled_buffer_1_bit6_output));
  assign or_2_out = bit5_to_6_low_2_bit6_out | bit6_controlled_buffer_1_bit6_output;  // OR_Gate or_2, 6 bits wide
  not not_2 (not_2_out, or_2_out[5]);
  Bit6_To_5_EXMSB bit6_to_5_exmsb_1 (.Bit6_In(or_2_out), .Bit5_Out(bit6_to_5_exmsb_1_bit5_out));
  Bit6_Twos_Complementer bit6_twos_complementer_1 (
    .Bit6_In(or_2_out), .Bit6_Result(bit6_twos_complementer_1_bit6_result));
  Bit5_Controlled_Buffer bit5_controlled_buffer_2 (
    .Bit5_In(bit6_to_5_exmsb_1_bit5_out), .Enable(not_2_out), .Bit5_Out(Bit5_Left_Shift_In));
  and and_2 (and_2_out, or_2_out[5], Cin);
  Bit6_Adder bit6_adder_2 (
    .Bit6_A(bit6_twos_complementer_1_bit6_result), .Bit6_B(CURRENT_EXP),
    .Bit6_Result(bit6_adder_2_bit6_result));  // open: Cin, Cout
  or or_3 (or_3_out, Bit32_Left_Shift_Result[9], Bit32_Left_Shift_Result[0], Bit32_Left_Shift_Result[1], Bit32_Left_Shift_Result[2], Bit32_Left_Shift_Result[3], Bit32_Left_Shift_Result[4], Bit32_Left_Shift_Result[5], Bit32_Left_Shift_Result[6], Bit32_Left_Shift_Result[7], Bit32_Left_Shift_Result[8], Bit32_Left_Shift_Result[10], Bit32_Left_Shift_Result[11], Bit32_Left_Shift_Result[12], Bit32_Left_Shift_Result[13], Bit32_Left_Shift_Result[14], Bit32_Left_Shift_Result[15], Bit32_Left_Shift_Result[16], Bit32_Left_Shift_Result[17], Bit32_Left_Shift_Result[18], Bit32_Left_Shift_Result[19]);
  nor nor_1 (nor_1_out, Bit32_Left_Shift_Result[31], Bit32_Left_Shift_Result[30], Bit32_Left_Shift_Result[29], Bit32_Left_Shift_Result[28], Bit32_Left_Shift_Result[27], Bit32_Left_Shift_Result[26], Bit32_Left_Shift_Result[25], Bit32_Left_Shift_Result[24], Bit32_Left_Shift_Result[23], Bit32_Left_Shift_Result[22]);
  and and_3 (Inexact, Bit32_Left_Shift_Result[21], or_4_out);
  or or_4 (or_4_out, or_3_out, Bit32_Left_Shift_Result[20]);
  Bit6_Adder bit6_adder_3 (
    .Cin(Cin), .Bit6_A(bit6_adder_2_bit6_result), .Bit6_B(OFFSET_EXP), .Bit6_Result(bit6_adder_3_bit6_result));  // open: Cout
  nor nor_2 (nor_2_out, bit6_adder_3_bit6_result[2], bit6_adder_3_bit6_result[0], bit6_adder_3_bit6_result[1], bit6_adder_3_bit6_result[3], bit6_adder_3_bit6_result[4], bit6_adder_3_bit6_result[5]);
  or or_5 (or_5_out, Multiplication, Division);
  and and_4 (and_4_out, bit6_adder_3_bit6_result[0], bit6_adder_3_bit6_result[1], bit6_adder_3_bit6_result[2], bit6_adder_3_bit6_result[3], bit6_adder_3_bit6_result[4]);
  or or_6 (or_6_out, bit6_adder_3_bit6_result[5], and_2_out, and_4_out);
  and and_5 (and_5_out, and_4_out, Addition);
  Bit10_Add_One bit10_add_one_1 (
    .Add_One(Inexact), .Bit10_In(Bit32_Left_Shift_Result[31:22]), .Bit10_Out(bit10_add_one_1_bit10_out),
    .Carry_Out(bit10_add_one_1_carry_out));
  Bit5_Add_One bit5_add_one_1 (
    .Add_One(bit10_add_one_1_carry_out), .Bit5_In(bit6_to_5_exmsb_2_bit5_out),
    .Bit5_Out(bit5_add_one_1_bit5_out), .Carry_Out(Overflow));
  Bit6_To_5_EXMSB bit6_to_5_exmsb_2 (.Bit6_In(bit6_adder_3_bit6_result), .Bit5_Out(bit6_to_5_exmsb_2_bit5_out));
  and and_6 (and_6_out, or_6_out, or_5_out);
  nor nor_3 (nor_3_out, and_6_out, and_5_out, Subtraction_Negative_Infinity);
  and and_7 (Underflow, Inexact, nor_1_out, nor_2_out);
  not not_3 (not_3_out[4], nor_3_out);
  Bit10_Controlled_Buffer bit10_controlled_buffer_1 (
    .Enable(nor_3_out), .Bit10_In(bit10_add_one_1_bit10_out), .Bit10_Out(Mantissa));
  Bit5_Controlled_Buffer bit5_controlled_buffer_3 (
    .Bit5_In(bit5_add_one_1_bit5_out), .Enable(priority_encoder_1_gs),
    .Bit5_Out(bit5_controlled_buffer_3_bit5_out));
  assign Exponent = bit5_controlled_buffer_3_bit5_out | {5{not_3_out[4]}};  // OR_Gate or_7, 5 bits wide

  assign Bit32_Left_Shift_In = INPT;
endmodule

module Bit6_Adder (
  input  Cin,
  input  [5:0] Bit6_A,
  input  [5:0] Bit6_B,
  output [5:0] Bit6_Result,
  output Cout
);

  wire and_1_out, and_2_out, and_3_out, and_4_out, and_5_out, and_6_out, and_7_out, and_8_out, and_9_out,
       and_10_out, and_11_out, and_12_out, and_13_out, and_14_out, and_15_out, and_16_out, and_17_out,
       and_18_out, and_19_out, and_20_out, and_21_out, and_22_out, and_23_out, and_24_out, and_25_out,
       and_26_out, and_27_out, or_1_out, or_2_out, or_3_out, or_4_out, or_5_out, xor_1_out, xor_2_out,
       xor_3_out, xor_4_out, xor_5_out, xor_6_out;

  xor xor_1 (xor_1_out, Bit6_B[3], Bit6_A[3]);
  and and_1 (and_1_out, Bit6_A[3], Bit6_B[3]);
  xor xor_2 (xor_2_out, Bit6_B[4], Bit6_A[4]);
  and and_2 (and_2_out, Bit6_A[4], Bit6_B[4]);
  xor xor_3 (xor_3_out, Bit6_B[5], Bit6_A[5]);
  and and_3 (and_3_out, Bit6_A[5], Bit6_B[5]);
  xor xor_4 (xor_4_out, Bit6_B[0], Bit6_A[0]);
  and and_4 (and_4_out, Bit6_A[0], Bit6_B[0]);
  xor xor_5 (xor_5_out, Bit6_B[1], Bit6_A[1]);
  and and_5 (and_5_out, Bit6_A[1], Bit6_B[1]);
  xor xor_6 (xor_6_out, Bit6_B[2], Bit6_A[2]);
  and and_6 (and_6_out, Bit6_A[2], Bit6_B[2]);
  xor xor_7 (Bit6_Result[3], or_3_out, xor_1_out);
  xor xor_8 (Bit6_Result[4], or_4_out, xor_2_out);
  xor xor_9 (Bit6_Result[5], or_5_out, xor_3_out);
  xor xor_10 (Bit6_Result[2], or_2_out, xor_6_out);
  xor xor_11 (Bit6_Result[0], Cin, xor_4_out);
  or or_1 (or_1_out, and_4_out, and_7_out);
  xor xor_12 (Bit6_Result[1], or_1_out, xor_5_out);
  or or_2 (or_2_out, and_5_out, and_8_out, and_9_out);
  or or_3 (or_3_out, and_6_out, and_10_out, and_11_out, and_12_out);
  or or_4 (or_4_out, and_1_out, and_13_out, and_14_out, and_15_out, and_16_out);
  or or_5 (or_5_out, and_2_out, and_17_out, and_18_out, and_19_out, and_20_out, and_21_out);
  or or_6 (Cout, and_3_out, and_22_out, and_23_out, and_24_out, and_25_out, and_26_out, and_27_out);
  and and_7 (and_7_out, xor_4_out, Cin);
  and and_8 (and_8_out, xor_5_out, and_4_out);
  and and_9 (and_9_out, xor_5_out, xor_4_out, Cin);
  and and_10 (and_10_out, and_5_out, xor_6_out);
  and and_11 (and_11_out, xor_6_out, xor_5_out, and_4_out);
  and and_12 (and_12_out, xor_6_out, xor_5_out, Cin, xor_4_out);
  and and_13 (and_13_out, and_6_out, xor_1_out);
  and and_14 (and_14_out, xor_1_out, xor_6_out, and_5_out);
  and and_15 (and_15_out, xor_1_out, xor_6_out, xor_5_out, and_4_out);
  and and_16 (and_16_out, xor_1_out, xor_6_out, xor_5_out, xor_4_out, Cin);
  and and_17 (and_17_out, xor_2_out, and_1_out);
  and and_18 (and_18_out, xor_2_out, xor_1_out, and_6_out);
  and and_19 (and_19_out, xor_2_out, xor_1_out, xor_6_out, and_5_out);
  and and_20 (and_20_out, xor_2_out, xor_1_out, xor_6_out, xor_5_out, and_4_out);
  and and_21 (and_21_out, xor_2_out, xor_1_out, xor_6_out, xor_5_out, xor_4_out, Cin);
  and and_22 (and_22_out, xor_3_out, and_2_out);
  and and_23 (and_23_out, xor_3_out, xor_2_out, and_1_out);
  and and_24 (and_24_out, xor_3_out, xor_2_out, and_6_out, xor_1_out);
  and and_25 (and_25_out, xor_3_out, xor_2_out, and_5_out, xor_1_out, xor_6_out);
  and and_26 (and_26_out, xor_3_out, xor_2_out, and_4_out, xor_1_out, xor_6_out, xor_5_out);
  and and_27 (and_27_out, xor_3_out, xor_2_out, xor_1_out, xor_6_out, xor_5_out, xor_4_out, Cin);

  // Notes on the sheet:
  //   0
endmodule

module BIT5_To_6_LOW (
  input  [4:0] Bit5_In,
  output [5:0] Bit6_Out
);


  assign Bit6_Out = {1'b0, Bit5_In};
endmodule

module Bit6_Controlled_Buffer (
  input  Enable,
  input  [5:0] Bit6_Input,
  output [5:0] Bit6_Output
);

  and and_1 (Bit6_Output[0], Bit6_Input[0], Enable);
  and and_2 (Bit6_Output[1], Bit6_Input[1], Enable);
  and and_3 (Bit6_Output[2], Bit6_Input[2], Enable);
  and and_4 (Bit6_Output[3], Bit6_Input[3], Enable);
  and and_5 (Bit6_Output[4], Bit6_Input[4], Enable);
  and and_6 (Bit6_Output[5], Bit6_Input[5], Enable);
endmodule

module Bit6_To_5_EXMSB (
  input  [5:0] Bit6_In,
  output [4:0] Bit5_Out
);


  assign Bit5_Out = Bit6_In[4:0];
endmodule

module Bit6_Twos_Complementer (
  input  [5:0] Bit6_In,
  output [5:0] Bit6_Result
);

  wire or_1_out, or_2_out, or_3_out, or_4_out;

  or or_1 (or_1_out, Bit6_In[0], Bit6_Result[1]);
  or or_2 (or_2_out, Bit6_In[0], Bit6_Result[1], Bit6_Result[2]);
  or or_3 (or_3_out, Bit6_Result[3], Bit6_Result[1], Bit6_Result[2], Bit6_In[0]);
  or or_4 (or_4_out, Bit6_Result[4], Bit6_Result[3], Bit6_Result[1], Bit6_Result[2], Bit6_In[0]);
  xor xor_1 (Bit6_Result[1], Bit6_In[1], Bit6_In[0]);
  xor xor_2 (Bit6_Result[2], Bit6_In[2], or_1_out);
  xor xor_3 (Bit6_Result[3], Bit6_In[3], or_2_out);
  xor xor_4 (Bit6_Result[4], or_3_out, Bit6_In[4]);
  xor xor_5 (Bit6_Result[5], or_4_out, Bit6_In[5]);

  assign Bit6_Result[0] = Bit6_In[0];
endmodule

module Bit6_GT_EQ (
  input  [5:0] Bit6_A,
  input  [5:0] Bit6_B,
  output A_Greater_EQ_B
);

  wire and_1_out, and_2_out, and_3_out, and_4_out, and_5_out, and_6_out, and_7_out, and_8_out, and_9_out,
       and_10_out, and_11_out, and_12_out, and_13_out, and_14_out, and_15_out, and_16_out, nor_1_out,
       nor_2_out, nor_3_out, nor_4_out, nor_5_out, nor_6_out, xor_1_out, xor_2_out, xor_3_out, xor_4_out,
       xor_5_out, xor_6_out;

  and and_1 (and_1_out, Bit6_B[5], ~Bit6_A[5]);  // AND_Gate
  and and_2 (and_2_out, Bit6_A[5], ~Bit6_B[5]);  // AND_Gate
  and and_3 (and_3_out, Bit6_B[4], ~Bit6_A[4]);  // AND_Gate
  and and_4 (and_4_out, Bit6_A[4], ~Bit6_B[4]);  // AND_Gate
  and and_5 (and_5_out, Bit6_B[3], ~Bit6_A[3]);  // AND_Gate
  and and_6 (and_6_out, Bit6_A[3], ~Bit6_B[3]);  // AND_Gate
  and and_7 (and_7_out, Bit6_B[2], ~Bit6_A[2]);  // AND_Gate
  and and_8 (and_8_out, Bit6_A[2], ~Bit6_B[2]);  // AND_Gate
  and and_9 (and_9_out, Bit6_B[1], ~Bit6_A[1]);  // AND_Gate
  and and_10 (and_10_out, Bit6_A[1], ~Bit6_B[1]);  // AND_Gate
  and and_11 (and_11_out, Bit6_A[0], ~Bit6_B[0]);  // AND_Gate
  nor nor_1 (nor_1_out, and_1_out, and_2_out);
  nor nor_2 (nor_2_out, and_3_out, and_4_out);
  nor nor_3 (nor_3_out, and_5_out, and_6_out);
  nor nor_4 (nor_4_out, and_7_out, and_8_out);
  nor nor_5 (nor_5_out, and_9_out, and_10_out);
  xor xor_1 (xor_1_out, Bit6_A[1], Bit6_B[1]);
  xor xor_2 (xor_2_out, Bit6_B[2], Bit6_A[2]);
  xor xor_3 (xor_3_out, Bit6_B[3], Bit6_A[3]);
  xor xor_4 (xor_4_out, Bit6_B[4], Bit6_A[4]);
  xor xor_5 (xor_5_out, Bit6_A[5], Bit6_B[5]);
  xor xor_6 (xor_6_out, Bit6_A[0], Bit6_B[0]);
  nor nor_6 (nor_6_out, xor_1_out, xor_2_out, xor_3_out, xor_4_out, xor_5_out, xor_6_out);
  and and_12 (and_12_out, nor_1_out, and_4_out);
  and and_13 (and_13_out, nor_1_out, nor_2_out, and_6_out);
  and and_14 (and_14_out, nor_1_out, nor_2_out, nor_3_out, and_8_out);
  and and_15 (and_15_out, nor_1_out, nor_2_out, nor_3_out, nor_4_out, and_10_out);
  and and_16 (and_16_out, nor_1_out, nor_2_out, nor_3_out, nor_4_out, nor_5_out, and_11_out);
  or or_1 (A_Greater_EQ_B, and_2_out, and_12_out, and_13_out, and_16_out, and_14_out, and_15_out, nor_6_out);
endmodule

module Bit6_Toggle_TwsCmplmtr (
  input  [5:0] Bit6_Input,
  input  Enable_Twos,
  output [5:0] Bit6_Result
);

  wire and_1_out, and_2_out, and_3_out, and_4_out, and_5_out, or_1_out, or_2_out, or_3_out, or_4_out;

  or or_1 (or_1_out, Bit6_Input[0], Bit6_Result[1]);
  or or_2 (or_2_out, Bit6_Input[0], Bit6_Result[1], Bit6_Result[2]);
  or or_3 (or_3_out, Bit6_Result[3], Bit6_Result[2], Bit6_Result[1], Bit6_Input[0]);
  xor xor_1 (Bit6_Result[1], Bit6_Input[1], and_1_out);
  and and_1 (and_1_out, Enable_Twos, Bit6_Input[0]);
  xor xor_2 (Bit6_Result[2], Bit6_Input[2], and_2_out);
  and and_2 (and_2_out, Enable_Twos, or_1_out);
  xor xor_3 (Bit6_Result[3], Bit6_Input[3], and_3_out);
  and and_3 (and_3_out, Enable_Twos, or_2_out);
  and and_4 (and_4_out, Enable_Twos, or_3_out);
  and and_5 (and_5_out, Enable_Twos, or_4_out);
  or or_4 (or_4_out, Bit6_Result[4], Bit6_Result[3], Bit6_Result[2], Bit6_Result[1], Bit6_Input[0]);
  xor xor_4 (Bit6_Result[4], Bit6_Input[4], and_4_out);
  xor xor_5 (Bit6_Result[5], Bit6_Input[5], and_5_out);

  assign Bit6_Result[0] = Bit6_Input[0];
endmodule

module Bit6_Greater_Than (
  input  [5:0] Bit6_A,
  input  [5:0] Bit6_B,
  output A_Greater_Than_B
);

  wire and_1_out, and_2_out, and_3_out, and_4_out, and_5_out, and_6_out, and_7_out, and_8_out, and_9_out,
       and_10_out, and_11_out, and_12_out, and_13_out, and_14_out, and_15_out, and_16_out, nor_1_out,
       nor_2_out, nor_3_out, nor_4_out, nor_5_out;

  and and_1 (and_1_out, Bit6_B[5], ~Bit6_A[5]);  // AND_Gate
  and and_2 (and_2_out, Bit6_A[5], ~Bit6_B[5]);  // AND_Gate
  and and_3 (and_3_out, Bit6_B[4], ~Bit6_A[4]);  // AND_Gate
  and and_4 (and_4_out, Bit6_A[4], ~Bit6_B[4]);  // AND_Gate
  and and_5 (and_5_out, Bit6_B[3], ~Bit6_A[3]);  // AND_Gate
  and and_6 (and_6_out, Bit6_A[3], ~Bit6_B[3]);  // AND_Gate
  and and_7 (and_7_out, Bit6_B[2], ~Bit6_A[2]);  // AND_Gate
  and and_8 (and_8_out, Bit6_A[2], ~Bit6_B[2]);  // AND_Gate
  and and_9 (and_9_out, Bit6_B[1], ~Bit6_A[1]);  // AND_Gate
  and and_10 (and_10_out, Bit6_A[1], ~Bit6_B[1]);  // AND_Gate
  and and_11 (and_11_out, Bit6_A[0], ~Bit6_B[0]);  // AND_Gate
  nor nor_1 (nor_1_out, and_1_out, and_2_out);
  nor nor_2 (nor_2_out, and_3_out, and_4_out);
  nor nor_3 (nor_3_out, and_5_out, and_6_out);
  nor nor_4 (nor_4_out, and_7_out, and_8_out);
  nor nor_5 (nor_5_out, and_9_out, and_10_out);
  and and_12 (and_12_out, nor_1_out, and_4_out);
  and and_13 (and_13_out, nor_1_out, nor_2_out, and_6_out);
  and and_14 (and_14_out, nor_1_out, nor_2_out, nor_3_out, and_8_out);
  and and_15 (and_15_out, nor_1_out, nor_2_out, nor_3_out, nor_4_out, and_10_out);
  and and_16 (and_16_out, nor_1_out, nor_2_out, nor_3_out, nor_4_out, nor_5_out, and_11_out);
  or or_1 (A_Greater_Than_B, and_2_out, and_12_out, and_13_out, and_14_out, and_15_out, and_16_out);
endmodule

module ALU3 (
  input  ALU_Enable,
  input  [3:0] Bit4_Operation,
  input  [15:0] Bit16_A,
  input  [15:0] Bit16_B,
  output Zero,
  output Overflow,
  output Carry,
  output Negative,
  output [15:0] Bit16_Result
);

  wire and_1_out, and_2_out, and_3_out, bit16_add_1_carry_out, bit16_left_shift_1_p4, bit16_right_shift_1_p4,
       not_1_out, or_1_out, xor_1_out, xor_2_out;
  wire [3:0] bit_extender_1_out;
  wire [15:0] bit16_add_1_bit16_result, bit16_and_1_bit16_result, bit16_left_shift_1_p3,
       bit16_multiplier_1_lower_word, bit16_multiplier_1_upper_word, bit16_not_1_bit16_result,
       bit16_or_1_bit16_result, bit16_right_shift_1_p3, bit16_toggle_xor_1_bit16_result,
       bit16_xor_1_bit16_result, demultiplexer_1_out15;

  Bit16_Toggle_Xor bit16_toggle_xor_1 (
    .Bit16_A(Bit16_B), .Toggle(demultiplexer_1_out15[14]), .Bit16_Result(bit16_toggle_xor_1_bit16_result));
  Bit_Extender #(.in_width(16), .out_width(4), .\type ("zero")) bit_extender_1 (.in(Bit16_B), .out(bit_extender_1_out));
  xor xor_1 (xor_1_out, Bit16_A[15], Bit16_B[15]);
  xor xor_2 (xor_2_out, Bit16_A[15], Bit16_Result[15]);
  and and_1 (and_1_out, xor_1_out, xor_2_out);
  Bit16_Add bit16_add_1 (
    .Carry_In(demultiplexer_1_out15[14]), .Bit16_A(Bit16_A), .Bit16_B(bit16_toggle_xor_1_bit16_result),
    .Bit16_Result(bit16_add_1_bit16_result), .Carry_Out(bit16_add_1_carry_out));
  Bit16_Multiplier bit16_multiplier_1 (
    .Bit16_B(Bit16_B), .Bit16_A(Bit16_A), .Lower_Word(bit16_multiplier_1_lower_word),
    .Upper_Word(bit16_multiplier_1_upper_word));
  Bit16_Not bit16_not_1 (.Bit16_In(Bit16_A), .Bit16_Result(bit16_not_1_bit16_result));
  Bit16_And bit16_and_1 (.Bit16_A(Bit16_A), .Bit16_B(Bit16_B), .Bit16_Result(bit16_and_1_bit16_result));
  Bit16_Or bit16_or_1 (.Bit16_A(Bit16_A), .Bit16_Result(bit16_or_1_bit16_result));  // open: Bit16_B
  Bit16_Xor bit16_xor_1 (.Bit16_A(Bit16_A), .Bit16_Result(bit16_xor_1_bit16_result));  // open: Bit16_B
  // Bit16_Left_Shift bit16_left_shift_1: pin names not known; wires that end beside it: Bit16_A, bit_extender_1_out, bit16_left_shift_1_p3, bit16_left_shift_1_p4
  // Bit16_Right_Shift bit16_right_shift_1: pin names not known; wires that end beside it: Bit16_A, bit_extender_1_out, bit16_right_shift_1_p3, bit16_right_shift_1_p4
  assign Bit16_Result = or_1_out ? bit16_add_1_bit16_result : 16'bz;  // Controlled_Buffer controlled_buffer_1
  assign Bit16_Result = demultiplexer_1_out15[13] ? bit16_multiplier_1_lower_word : 16'bz;  // Controlled_Buffer controlled_buffer_2
  assign Bit16_Result = demultiplexer_1_out15[12] ? bit16_multiplier_1_upper_word : 16'bz;  // Controlled_Buffer controlled_buffer_3
  assign Bit16_Result = demultiplexer_1_out15[11] ? bit16_left_shift_1_p3 : 16'bz;  // Controlled_Buffer controlled_buffer_4
  assign Bit16_Result = demultiplexer_1_out15[10] ? bit16_right_shift_1_p3 : 16'bz;  // Controlled_Buffer controlled_buffer_5
  assign Bit16_Result = demultiplexer_1_out15[9] ? bit16_not_1_bit16_result : 16'bz;  // Controlled_Buffer controlled_buffer_6
  assign Bit16_Result = demultiplexer_1_out15[8] ? bit16_and_1_bit16_result : 16'bz;  // Controlled_Buffer controlled_buffer_7
  assign Bit16_Result = demultiplexer_1_out15[7] ? bit16_or_1_bit16_result : 16'bz;  // Controlled_Buffer controlled_buffer_8
  assign Bit16_Result = demultiplexer_1_out15[6] ? bit16_xor_1_bit16_result : 16'bz;  // Controlled_Buffer controlled_buffer_9
  Demultiplexer #(.select(4)) demultiplexer_1 (
    .out0(demultiplexer_1_out15[15]), .out1(demultiplexer_1_out15[14]), .out2(demultiplexer_1_out15[13]),
    .out3(demultiplexer_1_out15[12]), .out4(demultiplexer_1_out15[11]), .out5(demultiplexer_1_out15[10]),
    .out6(demultiplexer_1_out15[9]), .out7(demultiplexer_1_out15[8]), .out8(demultiplexer_1_out15[7]),
    .out9(demultiplexer_1_out15[6]), .out10(demultiplexer_1_out15[5]), .out11(demultiplexer_1_out15[4]),
    .out12(demultiplexer_1_out15[3]), .out13(demultiplexer_1_out15[2]), .out14(demultiplexer_1_out15[1]),
    .out15(demultiplexer_1_out15[0]), .in(ALU_Enable), .sel(Bit4_Operation));
  or or_1 (or_1_out, demultiplexer_1_out15[15], demultiplexer_1_out15[14]);
  Pull_Resistor pull_resistor_1 (.node(Bit16_Result));
  not not_1 (not_1_out, bit16_add_1_carry_out);
  nor nor_1 (Zero, Bit16_Result[0], Bit16_Result[1], Bit16_Result[2], Bit16_Result[3], Bit16_Result[4], Bit16_Result[5], Bit16_Result[6], Bit16_Result[7], Bit16_Result[9], Bit16_Result[10], Bit16_Result[11], Bit16_Result[12], Bit16_Result[13], Bit16_Result[14], Bit16_Result[15], Bit16_Result[8]);
  and and_2 (and_2_out, bit16_add_1_carry_out, demultiplexer_1_out15[15]);
  and and_3 (and_3_out, not_1_out, demultiplexer_1_out15[14]);
  or or_2 (Overflow, and_1_out, and_2_out);
  or or_3 (Carry, and_3_out, bit16_left_shift_1_p4, bit16_right_shift_1_p4);

  assign Negative = Bit16_Result[15];
endmodule

module Bit16_Not (
  input  [15:0] Bit16_In,
  output [15:0] Bit16_Result
);

  not not_1 (Bit16_Result[0], Bit16_In[0]);
  not not_2 (Bit16_Result[1], Bit16_In[1]);
  not not_3 (Bit16_Result[2], Bit16_In[2]);
  not not_4 (Bit16_Result[3], Bit16_In[3]);
  not not_5 (Bit16_Result[4], Bit16_In[4]);
  not not_6 (Bit16_Result[5], Bit16_In[5]);
  not not_7 (Bit16_Result[6], Bit16_In[6]);
  not not_8 (Bit16_Result[7], Bit16_In[7]);
  not not_9 (Bit16_Result[8], Bit16_In[8]);
  not not_10 (Bit16_Result[9], Bit16_In[9]);
  not not_11 (Bit16_Result[10], Bit16_In[10]);
  not not_12 (Bit16_Result[11], Bit16_In[11]);
  not not_13 (Bit16_Result[12], Bit16_In[12]);
  not not_14 (Bit16_Result[13], Bit16_In[13]);
  not not_15 (Bit16_Result[14], Bit16_In[14]);
  not not_16 (Bit16_Result[15], Bit16_In[15]);
endmodule

module Bit16_And (
  input  [15:0] Bit16_A,
  input  [15:0] Bit16_B,
  output [15:0] Bit16_Result
);

  and and_1 (Bit16_Result[0], Bit16_A[0], Bit16_B[0]);
  and and_2 (Bit16_Result[1], Bit16_A[1], Bit16_B[1]);
  and and_3 (Bit16_Result[2], Bit16_A[2], Bit16_B[2]);
  and and_4 (Bit16_Result[3], Bit16_A[3], Bit16_B[3]);
  and and_5 (Bit16_Result[4], Bit16_A[4], Bit16_B[4]);
  and and_6 (Bit16_Result[5], Bit16_A[5], Bit16_B[5]);
  and and_7 (Bit16_Result[6], Bit16_A[6], Bit16_B[6]);
  and and_8 (Bit16_Result[7], Bit16_A[7], Bit16_B[7]);
  and and_9 (Bit16_Result[8], Bit16_A[8], Bit16_B[8]);
  and and_10 (Bit16_Result[9], Bit16_A[9], Bit16_B[9]);
  and and_11 (Bit16_Result[10], Bit16_A[10], Bit16_B[10]);
  and and_12 (Bit16_Result[11], Bit16_A[11], Bit16_B[11]);
  and and_13 (Bit16_Result[12], Bit16_A[12], Bit16_B[12]);
  and and_14 (Bit16_Result[13], Bit16_A[13], Bit16_B[13]);
  and and_15 (Bit16_Result[14], Bit16_A[14], Bit16_B[14]);
  and and_16 (Bit16_Result[15], Bit16_A[15], Bit16_B[15]);
endmodule

module Bit16_Or (
  input  [15:0] Bit16_A,
  input  [15:0] Bit16_B,
  output [15:0] Bit16_Result
);

  or or_1 (Bit16_Result[0], Bit16_A[0], Bit16_B[0]);
  or or_2 (Bit16_Result[1], Bit16_A[1], Bit16_B[1]);
  or or_3 (Bit16_Result[2], Bit16_A[2], Bit16_B[2]);
  or or_4 (Bit16_Result[3], Bit16_A[3], Bit16_B[3]);
  or or_5 (Bit16_Result[4], Bit16_A[4], Bit16_B[4]);
  or or_6 (Bit16_Result[5], Bit16_A[5], Bit16_B[5]);
  or or_7 (Bit16_Result[6], Bit16_A[6], Bit16_B[6]);
  or or_8 (Bit16_Result[7], Bit16_A[7], Bit16_B[7]);
  or or_9 (Bit16_Result[8], Bit16_A[8], Bit16_B[8]);
  or or_10 (Bit16_Result[9], Bit16_A[9], Bit16_B[9]);
  or or_11 (Bit16_Result[10], Bit16_A[10], Bit16_B[10]);
  or or_12 (Bit16_Result[11], Bit16_A[11], Bit16_B[11]);
  or or_13 (Bit16_Result[12], Bit16_A[12], Bit16_B[12]);
  or or_14 (Bit16_Result[13], Bit16_A[13], Bit16_B[13]);
  or or_15 (Bit16_Result[14], Bit16_A[14], Bit16_B[14]);
  or or_16 (Bit16_Result[15], Bit16_A[15], Bit16_B[15]);
endmodule

module Bit16_To_Bit5 (
  input  [15:0] Bit16_In,
  output [4:0] Bit5_Out
);


  assign Bit5_Out = Bit16_In[4:0];
endmodule

module Bit16_To_Bit32 (
  input  [15:0] Bit16_In,
  output [31:0] Bit32_Out
);


  assign Bit32_Out = {{16{1'b0}}, Bit16_In};
endmodule

module Bit32_To_Bit16 (
  input  [31:0] Bit32_In,
  output [15:0] Bit16_Out
);


  assign Bit16_Out = Bit32_In[15:0];
endmodule

module Bit16_Toggle_TwsCmplmtr (
  input  Enable,
  input  [15:0] Bit16_In,
  output [15:0] Bit16_Out
);

  wire and_1_out, and_2_out, and_3_out, and_4_out, and_5_out, and_6_out, and_7_out, and_8_out, and_9_out,
       and_10_out, and_11_out, and_12_out, and_13_out, and_14_out, and_15_out, or_1_out, or_2_out, or_3_out,
       or_4_out, or_5_out, or_6_out, or_7_out, or_8_out, or_9_out, or_10_out, or_11_out, or_12_out,
       or_13_out, or_14_out;

  or or_1 (or_1_out, Bit16_In[0], Bit16_Out[14]);
  or or_2 (or_2_out, Bit16_In[0], Bit16_Out[14], Bit16_Out[13]);
  or or_3 (or_3_out, Bit16_In[0], Bit16_Out[14], Bit16_Out[13], Bit16_Out[12]);
  or or_4 (or_4_out, Bit16_In[0], Bit16_Out[14], Bit16_Out[13], Bit16_Out[12], Bit16_Out[11]);
  or or_5 (or_5_out, Bit16_In[0], Bit16_Out[14], Bit16_Out[13], Bit16_Out[12], Bit16_Out[11], Bit16_Out[10]);
  or or_6 (or_6_out, Bit16_In[0], Bit16_Out[14], Bit16_Out[13], Bit16_Out[12], Bit16_Out[11], Bit16_Out[10], Bit16_Out[9]);
  or or_7 (or_7_out, Bit16_In[0], Bit16_Out[14], Bit16_Out[13], Bit16_Out[12], Bit16_Out[11], Bit16_Out[10], Bit16_Out[9], Bit16_Out[8]);
  or or_8 (or_8_out, Bit16_In[0], Bit16_Out[14], Bit16_Out[13], Bit16_Out[12], Bit16_Out[11], Bit16_Out[10], Bit16_Out[9], Bit16_Out[8], Bit16_Out[7]);
  or or_9 (or_9_out, Bit16_In[0], Bit16_Out[14], Bit16_Out[13], Bit16_Out[12], Bit16_Out[11], Bit16_Out[10], Bit16_Out[9], Bit16_Out[8], Bit16_Out[7], Bit16_Out[6]);
  or or_10 (or_10_out, Bit16_In[0], Bit16_Out[14], Bit16_Out[13], Bit16_Out[12], Bit16_Out[11], Bit16_Out[10], Bit16_Out[9], Bit16_Out[8], Bit16_Out[7], Bit16_Out[6], Bit16_Out[5]);
  or or_11 (or_11_out, Bit16_In[0], Bit16_Out[14], Bit16_Out[13], Bit16_Out[12], Bit16_Out[11], Bit16_Out[10], Bit16_Out[9], Bit16_Out[8], Bit16_Out[7], Bit16_Out[6], Bit16_Out[5], Bit16_Out[4]);
  or or_12 (or_12_out, Bit16_In[0], Bit16_Out[14], Bit16_Out[13], Bit16_Out[12], Bit16_Out[11], Bit16_Out[10], Bit16_Out[9], Bit16_Out[8], Bit16_Out[7], Bit16_Out[6], Bit16_Out[5], Bit16_Out[4], Bit16_Out[3]);
  or or_13 (or_13_out, Bit16_In[0], Bit16_Out[14], Bit16_Out[13], Bit16_Out[12], Bit16_Out[11], Bit16_Out[10], Bit16_Out[9], Bit16_Out[8], Bit16_Out[7], Bit16_Out[6], Bit16_Out[5], Bit16_Out[4], Bit16_Out[3], Bit16_Out[2]);
  or or_14 (or_14_out, Bit16_In[0], Bit16_Out[14], Bit16_Out[13], Bit16_Out[12], Bit16_Out[11], Bit16_Out[10], Bit16_Out[9], Bit16_Out[8], Bit16_Out[7], Bit16_Out[6], Bit16_Out[5], Bit16_Out[4], Bit16_Out[3], Bit16_Out[2], Bit16_Out[1]);
  xor xor_1 (Bit16_Out[14], Bit16_In[1], and_1_out);
  and and_1 (and_1_out, Bit16_In[0], Enable);
  xor xor_2 (Bit16_Out[13], Bit16_In[2], and_2_out);
  and and_2 (and_2_out, or_1_out, Enable);
  xor xor_3 (Bit16_Out[12], Bit16_In[3], and_3_out);
  and and_3 (and_3_out, or_2_out, Enable);
  xor xor_4 (Bit16_Out[11], Bit16_In[4], and_4_out);
  and and_4 (and_4_out, Enable, or_3_out);
  xor xor_5 (Bit16_Out[10], Bit16_In[5], and_5_out);
  and and_5 (and_5_out, Enable, or_4_out);
  xor xor_6 (Bit16_Out[9], Bit16_In[6], and_6_out);
  and and_6 (and_6_out, Enable, or_5_out);
  xor xor_7 (Bit16_Out[8], Bit16_In[7], and_7_out);
  and and_7 (and_7_out, Enable, or_6_out);
  xor xor_8 (Bit16_Out[7], Bit16_In[8], and_8_out);
  and and_8 (and_8_out, Enable, or_7_out);
  xor xor_9 (Bit16_Out[6], Bit16_In[9], and_9_out);
  and and_9 (and_9_out, Enable, or_8_out);
  xor xor_10 (Bit16_Out[5], Bit16_In[10], and_10_out);
  and and_10 (and_10_out, Enable, or_9_out);
  xor xor_11 (Bit16_Out[4], Bit16_In[11], and_11_out);
  and and_11 (and_11_out, Enable, or_10_out);
  xor xor_12 (Bit16_Out[3], Bit16_In[12], and_12_out);
  and and_12 (and_12_out, Enable, or_11_out);
  xor xor_13 (Bit16_Out[2], Bit16_In[13], and_13_out);
  and and_13 (and_13_out, Enable, or_12_out);
  xor xor_14 (Bit16_Out[1], Bit16_In[14], and_14_out);
  and and_14 (and_14_out, Enable, or_13_out);
  xor xor_15 (Bit16_Out[0], Bit16_In[15], and_15_out);
  and and_15 (and_15_out, Enable, or_14_out);

  assign Bit16_Out[15] = Bit16_In[0];
endmodule
module FPURIGGED (
  input  ADD,
  input  SUB,
  input  MUL,
  input  DIV,
  input  [15:0] INPUT_A,
  input  [15:0] INPUT_B,
  output [15:0] Result
);

  wire and_1_out, and_2_out, and_3_out, and_4_out, and_5_out, and_6_out, and_7_out, and_8_out, and_9_out,
       and_10_out, and_11_out, and_12_out, and_13_out, and_14_out, and_15_out, and_16_out, and_17_out,
       and_18_out, and_19_out, and_20_out, and_21_out, and_22_out, and_23_out, and_25_out, and_26_out,
       and_27_out, and_28_out, and_31_out, and_32_out, and_33_out, and_34_out, and_35_out, and_36_out,
       and_37_out, and_38_out, and_39_out, and_40_out, and_41_out, and_43_out, and_44_out, and_45_out,
       and_46_out, bit5_adder_1_cout, bit6_adder_2_cout, bit6_greater_than_1_a_greater_than_b,
       bit24_adder_1_c_out, nor_1_out, nor_2_out, not_1_out, or_1_out, or_2_out, or_5_out, or_6_out,
       or_7_out, or_9_out, or_10_out, or_11_out, or_12_out, or_16_out, or_17_out, or_19_out, or_20_out,
       or_21_out, or_23_out, or_28_out, plsbnormal_1_p9, plsbnormal_1_p12, plsbnormal_1_p13,
       plsbnormal_1_p14, xor_1_out, xor_2_out, xor_3_out, xor_5_out, xor_6_out;
  wire [1:1] and_24_out, xor_4_out;
  wire [4:0] bit5_adder_1_bit5_result, bit5_controlled_buffer_1_bit5_out, bit5_controlled_buffer_2_bit5_out,
       bit5_inverter_1_bit5_out, bit5_toggle_twscmplmtr_1_bit5_result, or_15_out, plsbnormal_1_p11;
  wire [5:0] bit5_to_6_low_1_bit6_out, bit5_to_6_low_2_bit6_out, bit5_to_6_low_3_bit6_out,
       bit6_adder_1_bit6_result, bit6_adder_2_bit6_result, bit6_controlled_buffer_1_bit6_output,
       bit6_toggle_twscmplmtr_1_bit6_result, or_24_out, or_25_out, or_26_out;
  wire [9:0] plsbnormal_1_p10;
  wire [10:0] bit11_controlled_buffer_1_bit11_out, bit11_controlled_buffer_2_bit11_out,
       bit11_controlled_buffer_3_bit11_out, bit11_controlled_buffer_4_bit11_out,
       bit11_controlled_buffer_5_bit11_out, bit11_controlled_buffer_6_bit11_out,
       bit11_controlled_buffer_7_bit11_out, bit11_controlled_buffer_8_bit11_out, or_13_out, or_14_out;
  wire [10:10] or_3_out, or_4_out;
  wire [15:0] bit11_to_bit16_high_1_bit16_out, bit11_to_bit16_high_2_bit16_out,
       bit11_to_bit16_low_1_bit16_out, bit11_to_bit16_low_2_bit16_out, bit11_to_bit16_low_3_bit16_out,
       bit16_controlled_buffer_1_bit16_out, bit16_controlled_buffer_2_bit16_out, bit16_multiplier_1_p1,
       bit16_multiplier_1_p2, fpsubtractor_1_out;
  wire [15:8] or_8_out;
  wire [15:15] or_22_out;
  wire [23:0] bit16_to_bit24_high_byte_1_bit24, bit16_to_bit24_high_byte_2_bit24,
       bit16_to_bit24_low_byte_1_bit24, bit24_adder_1_bit24_result, bit24_controlled_buffer_1_bit24_out,
       bit24_controlled_buffer_2_bit24_out, bit24_toggle_twscmplmtr_1_bit24_out,
       bit24_toggle_twscmplmtr_2_bit24_out, bit24_toggle_twscmplmtr_3_bit24_out,
       bit32_to_bit24_high_1_bit24_out, divider_1_out;
  wire [31:0] bit11_to_bit32_high_1_bit32_out, bit32_right_shift_1_bit32_result, or_27_out;
  wire [31:31] and_42_out;

  // Probe on INPUT_A
  // Probe on INPUT_B
  FPSubtractor #(.fpwidth(16)) fpsubtractor_1 (.a(INPUT_A), .b(INPUT_B), .out(fpsubtractor_1_out));
  // Probe on fpsubtractor_1_out
  // Probe on fpsubtractor_1_out
  or or_1 (or_1_out, ADD, SUB);
  or or_2 (or_2_out, ADD, SUB, MUL, DIV);
  or or_3 (or_3_out[10], INPUT_A[10], INPUT_A[11], INPUT_A[12], INPUT_A[13], INPUT_A[14]);
  or or_4 (or_4_out[10], INPUT_B[10], INPUT_B[11], INPUT_B[12], INPUT_B[13], INPUT_B[14]);
  Bit5_Inverter bit5_inverter_1 (.Bit5_In(INPUT_B[14:10]), .Bit5_Out(bit5_inverter_1_bit5_out));
  or or_5 (or_5_out, INPUT_A[0], INPUT_A[1], INPUT_A[2], INPUT_A[3], INPUT_A[4], INPUT_A[5], INPUT_A[6], INPUT_A[7], INPUT_A[8]);
  or or_6 (or_6_out, INPUT_B[0], INPUT_B[1], INPUT_B[2], INPUT_B[3], INPUT_B[4], INPUT_B[5], INPUT_B[6], INPUT_B[7], INPUT_B[8]);
  or or_7 (or_7_out, ADD, SUB);
  and and_1 (and_1_out, or_2_out, or_12_out);
  and and_2 (and_2_out, or_2_out, ~or_12_out);  // AND_Gate
  and and_3 (and_3_out, INPUT_A[10], INPUT_A[11], INPUT_A[12], INPUT_A[13], INPUT_A[14], ~INPUT_A[9], or_5_out);  // AND_Gate
  and and_4 (and_4_out, ~or_5_out, INPUT_A[9], INPUT_A[10], INPUT_A[11], INPUT_A[12], INPUT_A[13], INPUT_A[14]);  // AND_Gate
  and and_5 (and_5_out, ~INPUT_A[9], INPUT_A[10], INPUT_A[11], INPUT_A[12], INPUT_A[13], INPUT_A[14]);  // AND_Gate
  nor nor_1 (nor_1_out, INPUT_A[0], INPUT_A[1], INPUT_A[2], INPUT_A[3], INPUT_A[4], INPUT_A[5], INPUT_A[6], INPUT_A[7], INPUT_A[8], INPUT_A[9], INPUT_A[10], INPUT_A[11], INPUT_A[12], INPUT_A[13], INPUT_A[14]);
  and and_6 (and_6_out, INPUT_B[10], INPUT_B[11], INPUT_B[12], INPUT_B[13], INPUT_B[14], ~INPUT_B[9], or_6_out);  // AND_Gate
  and and_7 (and_7_out, ~or_6_out, INPUT_B[9], INPUT_B[10], INPUT_B[11], INPUT_B[12], INPUT_B[13], INPUT_B[14]);  // AND_Gate
  and and_8 (and_8_out, ~INPUT_B[9], INPUT_B[10], INPUT_B[11], INPUT_B[12], INPUT_B[13], INPUT_B[14]);  // AND_Gate
  nor nor_2 (nor_2_out, INPUT_B[0], INPUT_B[1], INPUT_B[2], INPUT_B[3], INPUT_B[4], INPUT_B[5], INPUT_B[6], INPUT_B[7], INPUT_B[8], INPUT_B[9], INPUT_B[10], INPUT_B[11], INPUT_B[12], INPUT_B[13], INPUT_B[14]);
  Bit5_Adder bit5_adder_1 (
    .Cin(1'b1), .Bit5_A(INPUT_A[14:10]), .Bit5_B(bit5_inverter_1_bit5_out),
    .Bit5_Result(bit5_adder_1_bit5_result), .Cout(bit5_adder_1_cout));
  or or_8 (or_8_out[8], and_3_out, and_6_out);
  and and_9 (and_9_out, nor_1_out, MUL, and_8_out);
  xor xor_1 (xor_1_out, SUB, INPUT_B[15]);
  or or_9 (or_9_out, MUL, DIV);
  xor xor_2 (xor_2_out, INPUT_A[15], INPUT_B[15]);
  and and_10 (and_10_out, ~SUB, INPUT_B[15], INPUT_A[15]);  // AND_Gate
  and and_11 (and_11_out, SUB, ~INPUT_B[15], INPUT_A[15]);  // AND_Gate
  xor xor_3 (xor_3_out, SUB, INPUT_A[15]);
  and and_12 (and_12_out, or_7_out, ~bit5_adder_1_cout);  // AND_Gate
  and and_13 (and_13_out, or_7_out, bit5_adder_1_cout);
  and and_14 (and_14_out, or_7_out, ~bit5_adder_1_cout);  // AND_Gate
  and and_15 (and_15_out, or_7_out, bit5_adder_1_cout);
  not not_1 (not_1_out, bit5_adder_1_cout);
  and and_16 (and_16_out, bit5_adder_1_cout, or_7_out);
  and and_17 (and_17_out, or_7_out, ~bit5_adder_1_cout);  // AND_Gate
  and and_18 (and_18_out, and_5_out, MUL, nor_2_out);
  and and_19 (and_19_out, or_9_out, xor_2_out);
  or or_10 (or_10_out, and_10_out, and_11_out);
  xor xor_4 (xor_4_out[1], xor_3_out, INPUT_B[15]);
  and and_20 (and_20_out, or_2_out, or_11_out);
  or or_11 (or_11_out, and_3_out, and_4_out, and_6_out, and_7_out);
  and and_21 (and_21_out, xor_4_out[1], bit24_adder_1_c_out);
  or or_12 (or_12_out, or_17_out, and_28_out, or_16_out);
  and and_22 (and_22_out, xor_4_out[1], or_1_out, and_5_out, and_8_out);
  and and_23 (and_23_out, DIV, and_5_out, and_8_out);
  xor xor_5 (xor_5_out, or_10_out, and_21_out);
  and and_24 (and_24_out[1], ~xor_4_out[1], or_7_out);  // AND_Gate
  Bit11_Controlled_Buffer bit11_controlled_buffer_1 (
    .Enable(and_12_out), .Bit11_In({or_4_out[10], INPUT_B[9:0]}),
    .Bit11_Out(bit11_controlled_buffer_1_bit11_out));
  assign or_13_out = bit11_controlled_buffer_1_bit11_out | bit11_controlled_buffer_2_bit11_out;  // OR_Gate or_13, 11 bits wide
  Bit11_Controlled_Buffer bit11_controlled_buffer_2 (
    .Enable(and_13_out), .Bit11_In({or_3_out[10], INPUT_A[9:0]}),
    .Bit11_Out(bit11_controlled_buffer_2_bit11_out));
  Bit11_Controlled_Buffer bit11_controlled_buffer_3 (
    .Enable(and_14_out), .Bit11_In({or_3_out[10], INPUT_A[9:0]}),
    .Bit11_Out(bit11_controlled_buffer_3_bit11_out));
  assign or_14_out = bit11_controlled_buffer_3_bit11_out | bit11_controlled_buffer_4_bit11_out;  // OR_Gate or_14, 11 bits wide
  Bit11_Controlled_Buffer bit11_controlled_buffer_4 (
    .Enable(and_15_out), .Bit11_In({or_4_out[10], INPUT_B[9:0]}),
    .Bit11_Out(bit11_controlled_buffer_4_bit11_out));
  Bit5_Toggle_TwsCmplmtr bit5_toggle_twscmplmtr_1 (
    .Bit5_Input(bit5_adder_1_bit5_result), .Enable_Twos(not_1_out),
    .Bit5_Result(bit5_toggle_twscmplmtr_1_bit5_result));
  Bit5_Controlled_Buffer bit5_controlled_buffer_1 (
    .Bit5_In(INPUT_A[14:10]), .Enable(and_16_out), .Bit5_Out(bit5_controlled_buffer_1_bit5_out));
  assign or_15_out = bit5_controlled_buffer_1_bit5_out | bit5_controlled_buffer_2_bit5_out;  // OR_Gate or_15, 5 bits wide
  Bit5_Controlled_Buffer bit5_controlled_buffer_2 (
    .Bit5_In(INPUT_B[14:10]), .Enable(and_17_out), .Bit5_Out(bit5_controlled_buffer_2_bit5_out));
  or or_16 (or_16_out, and_9_out, and_18_out, and_22_out, and_23_out, and_25_out);
  and and_25 (and_25_out, DIV, nor_1_out, nor_2_out);
  BIT5_To_6_LOW bit5_to_6_low_1 (.Bit5_In(or_15_out), .Bit6_Out(bit5_to_6_low_1_bit6_out));
  and and_26 (and_26_out, ~or_16_out, or_17_out);  // AND_Gate
  or or_17 (or_17_out, and_27_out, and_32_out, and_36_out, and_37_out, and_38_out);
  and and_27 (and_27_out, DIV, nor_2_out, ~and_5_out, ~nor_1_out);  // AND_Gate
  or or_18 (or_8_out[14], or_16_out, and_26_out);
  and and_28 (and_28_out, DIV, and_8_out, ~and_5_out, ~nor_1_out);  // AND_Gate
  Bit11_To_Bit16_High bit11_to_bit16_high_1 (.Bit11_In(or_13_out), .Bit16_Out(bit11_to_bit16_high_1_bit16_out));
  Bit11_To_Bit32_High bit11_to_bit32_high_1 (.Bit11_In(or_14_out), .Bit32_Out(bit11_to_bit32_high_1_bit32_out));
  and and_29 (or_8_out[9], ~or_8_out[8], and_20_out);  // AND_Gate
  and and_30 (or_8_out[15], ~or_16_out, or_19_out);  // AND_Gate
  or or_19 (or_19_out, and_31_out, and_33_out);
  and and_31 (and_31_out, or_17_out, xor_2_out);
  and and_32 (and_32_out, or_20_out, or_1_out);
  or or_20 (or_20_out, and_5_out, and_8_out);
  and and_33 (and_33_out, or_1_out, or_21_out);
  or or_21 (or_21_out, and_34_out, and_35_out);
  and and_34 (and_34_out, and_5_out, INPUT_A[15]);
  and and_35 (and_35_out, xor_1_out, and_8_out);
  and and_36 (and_36_out, MUL, and_8_out, ~and_5_out, ~nor_1_out);  // AND_Gate
  Bit16_To_Bit24_High_Byte bit16_to_bit24_high_byte_1 (
    .Bit16(bit11_to_bit16_high_1_bit16_out), .Bit24(bit16_to_bit24_high_byte_1_bit24));
  Bit32_Right_Shift bit32_right_shift_1 (
    .Bit32_In(bit11_to_bit32_high_1_bit32_out), .Bit5_Shift(bit5_toggle_twscmplmtr_1_bit5_result),
    .Bit32_Result(bit32_right_shift_1_bit32_result));
  and and_37 (and_37_out, and_5_out, MUL, ~and_8_out, ~nor_2_out);  // AND_Gate
  and and_38 (and_38_out, MUL, and_5_out, and_8_out);
  and and_39 (and_39_out, xor_4_out[1], ~bit5_adder_1_cout);  // AND_Gate
  and and_40 (and_40_out, xor_4_out[1], bit5_adder_1_cout);
  Bit32_To_Bit24_High bit32_to_bit24_high_1 (
    .Bit32_In(bit32_right_shift_1_bit32_result), .Bit24_Out(bit32_to_bit24_high_1_bit24_out));
  Bit24_Toggle_TwsCmplmtr bit24_toggle_twscmplmtr_1 (
    .Enable(and_39_out), .Bit24_In(bit16_to_bit24_high_byte_1_bit24),
    .Bit24_Out(bit24_toggle_twscmplmtr_1_bit24_out));
  Bit24_Controlled_Buffer bit24_controlled_buffer_1 (
    .Enable(or_7_out), .Bit24_In(bit32_to_bit24_high_1_bit24_out),
    .Bit24_Out(bit24_controlled_buffer_1_bit24_out));
  Bit24_Toggle_TwsCmplmtr bit24_toggle_twscmplmtr_2 (
    .Enable(and_40_out), .Bit24_In(bit24_controlled_buffer_1_bit24_out),
    .Bit24_Out(bit24_toggle_twscmplmtr_2_bit24_out));
  Bit24_Adder bit24_adder_1 (
    .Bit24_A(bit24_toggle_twscmplmtr_1_bit24_out), .Bit24_B(bit24_toggle_twscmplmtr_2_bit24_out),
    .Bit24_Result(bit24_adder_1_bit24_result), .C_OUT(bit24_adder_1_c_out));  // open: C_In, Bit16_C_OUT
  and and_41 (and_41_out, xor_4_out[1], ~bit24_adder_1_c_out);  // AND_Gate
  and and_42 (and_42_out[31], bit24_adder_1_c_out, ~xor_5_out);  // AND_Gate
  and and_43 (and_43_out, ~xor_4_out[1], bit24_adder_1_c_out);  // AND_Gate
  xor xor_6 (xor_6_out, xor_5_out, xor_4_out[1]);
  and and_44 (and_44_out, xor_6_out, or_7_out);
  or or_22 (or_22_out[15], and_19_out, and_44_out);
  Bit24_Toggle_TwsCmplmtr bit24_toggle_twscmplmtr_3 (
    .Enable(and_41_out), .Bit24_In(bit24_adder_1_bit24_result),
    .Bit24_Out(bit24_toggle_twscmplmtr_3_bit24_out));
  BIT5_To_6_LOW bit5_to_6_low_2 (.Bit5_In(INPUT_B[14:10]), .Bit6_Out(bit5_to_6_low_2_bit6_out));
  or or_23 (or_23_out, MUL, DIV);
  assign or_24_out = {4'b0000, and_24_out[1], 1'b0} | {4'b0000, xor_4_out[1], 1'b0} | {2'b00, MUL, 1'b0, {2{MUL}}} | {{5{1'b0}}, DIV};  // OR_Gate or_24, 6 bits wide
  Bit6_Toggle_TwsCmplmtr bit6_toggle_twscmplmtr_1 (
    .Bit6_Input(bit5_to_6_low_2_bit6_out), .Enable_Twos(DIV),
    .Bit6_Result(bit6_toggle_twscmplmtr_1_bit6_result));
  Bit11_Controlled_Buffer bit11_controlled_buffer_5 (
    .Enable(MUL), .Bit11_In({or_3_out[10], INPUT_A[9:0]}), .Bit11_Out(bit11_controlled_buffer_5_bit11_out));
  Bit11_Controlled_Buffer bit11_controlled_buffer_6 (
    .Enable(MUL), .Bit11_In({or_4_out[10], INPUT_B[9:0]}), .Bit11_Out(bit11_controlled_buffer_6_bit11_out));
  Bit11_Controlled_Buffer bit11_controlled_buffer_7 (
    .Enable(DIV), .Bit11_In({or_3_out[10], INPUT_A[9:0]}), .Bit11_Out(bit11_controlled_buffer_7_bit11_out));
  Bit11_Controlled_Buffer bit11_controlled_buffer_8 (
    .Enable(DIV), .Bit11_In({or_4_out[10], INPUT_B[9:0]}), .Bit11_Out(bit11_controlled_buffer_8_bit11_out));
  assign or_25_out = bit5_to_6_low_1_bit6_out | bit6_controlled_buffer_1_bit6_output;  // OR_Gate or_25, 6 bits wide
  Bit6_Controlled_Buffer bit6_controlled_buffer_1 (
    .Enable(or_23_out), .Bit6_Input(bit6_adder_2_bit6_result),
    .Bit6_Output(bit6_controlled_buffer_1_bit6_output));
  BIT5_To_6_LOW bit5_to_6_low_3 (.Bit5_In(INPUT_A[14:10]), .Bit6_Out(bit5_to_6_low_3_bit6_out));
  Bit11_To_Bit16_Low bit11_to_bit16_low_1 (
    .Bit11_In(bit11_controlled_buffer_5_bit11_out), .Bit16_Out(bit11_to_bit16_low_1_bit16_out));
  Bit11_To_Bit16_Low bit11_to_bit16_low_2 (
    .Bit11_In(bit11_controlled_buffer_6_bit11_out), .Bit16_Out(bit11_to_bit16_low_2_bit16_out));
  Bit11_To_Bit16_High bit11_to_bit16_high_2 (
    .Bit11_In(bit11_controlled_buffer_7_bit11_out), .Bit16_Out(bit11_to_bit16_high_2_bit16_out));
  Bit11_To_Bit16_Low bit11_to_bit16_low_3 (
    .Bit11_In(bit11_controlled_buffer_8_bit11_out), .Bit16_Out(bit11_to_bit16_low_3_bit16_out));
  Bit6_Greater_Than bit6_greater_than_1 (
    .Bit6_A(bit6_controlled_buffer_1_bit6_output), .Bit6_B(6'b010010),
    .A_Greater_Than_B(bit6_greater_than_1_a_greater_than_b));
  Bit6_Adder bit6_adder_1 (
    .Bit6_A(bit5_to_6_low_3_bit6_out), .Bit6_B(bit6_toggle_twscmplmtr_1_bit6_result),
    .Bit6_Result(bit6_adder_1_bit6_result));  // open: Cin, Cout
  assign or_26_out = {DIV, {5{1'b0}}} | {{2{MUL}}, 3'b000, MUL};  // OR_Gate or_26, 6 bits wide
  and and_45 (and_45_out, bit6_greater_than_1_a_greater_than_b, DIV);
  // Bit16_Multiplier bit16_multiplier_1: pin names not known; wires that end beside it: bit16_multiplier_1_p1, bit16_multiplier_1_p2
  Bit16_To_Bit24_High_Byte bit16_to_bit24_high_byte_2 (
    .Bit16(bit11_to_bit16_high_2_bit16_out), .Bit24(bit16_to_bit24_high_byte_2_bit24));
  Bit16_To_Bit24_Low_Byte bit16_to_bit24_low_byte_1 (
    .Bit16(bit11_to_bit16_low_3_bit16_out), .Bit24(bit16_to_bit24_low_byte_1_bit24));
  Bit6_Adder bit6_adder_2 (
    .Bit6_A(bit6_adder_1_bit6_result), .Bit6_B(or_26_out), .Bit6_Result(bit6_adder_2_bit6_result),
    .Cout(bit6_adder_2_cout));  // open: Cin
  Divider #(.width(24)) divider_1 (
    .a(bit16_to_bit24_high_byte_2_bit24), .b(bit16_to_bit24_low_byte_1_bit24), .out(divider_1_out));  // open: upper, rem
  and and_46 (and_46_out, MUL, bit6_adder_2_cout);
  Bit16_Controlled_Buffer bit16_controlled_buffer_1 (
    .Enable(MUL), .Bit16_In(bit16_multiplier_1_p1), .Bit16_Out(bit16_controlled_buffer_1_bit16_out));
  Bit16_Controlled_Buffer bit16_controlled_buffer_2 (
    .Enable(MUL), .Bit16_In(bit16_multiplier_1_p2), .Bit16_Out(bit16_controlled_buffer_2_bit16_out));
  assign or_27_out = {and_42_out[31], bit24_toggle_twscmplmtr_3_bit24_out, {7{1'b0}}} | {bit16_controlled_buffer_2_bit16_out, bit16_controlled_buffer_1_bit16_out} | {{8{1'b0}}, bit24_controlled_buffer_2_bit24_out};  // OR_Gate or_27, 32 bits wide
  Bit24_Controlled_Buffer bit24_controlled_buffer_2 (
    .Enable(DIV), .Bit24_In(divider_1_out), .Bit24_Out(bit24_controlled_buffer_2_bit24_out));
  or or_28 (or_28_out, and_46_out, and_45_out);
  // plsbnormal plsbnormal_1: pin names not known; wires that end beside it: or_27_out, or_25_out, or_24_out, or_28_out, MUL, DIV, and_24_out[1], and_43_out, plsbnormal_1_p9, plsbnormal_1_p10, plsbnormal_1_p11, plsbnormal_1_p12, plsbnormal_1_p13, plsbnormal_1_p14
  // Bit32_Left_Shift bit32_left_shift_1: pin names not known; wires that end beside it: plsbnormal_1_p13, plsbnormal_1_p14, plsbnormal_1_p9
  Pull_Resistor pull_resistor_1 (.node(Result));
  assign Result = and_2_out ? {or_22_out[15], plsbnormal_1_p11, plsbnormal_1_p10} : 16'bz;  // Controlled_Buffer controlled_buffer_1
  assign Result = and_1_out ? {or_8_out[15:14], {4{or_8_out[14]}}, or_8_out[9:8], {8{or_8_out[8]}}} : 16'bz;  // Controlled_Buffer controlled_buffer_2
  // Probe on Result

  // Notes on the sheet:
  //   snan
  //   qnan
  //   infinity
  //   zero
  //   snan
  //   qnan
  //   infinity
  //   zero
  //   qnan
  //   prop nan pri snan
  //   qnazn
  //   qnazn
  //   inf w/ xor sign
  //   d by 0
  //   xor sign
  //   0
  //   inf
  //   neg
  //   infs w/ xor sign
  //   mul
  //   div
  //   mant
  //   exp
endmodule

module Register_File (
  input  [15:0] Write_Data,
  input  [3:0] Read_Address_B,
  input  Read_B_Enable,
  input  [3:0] Read_Address_A,
  input  Read_A_Enable,
  input  [3:0] Write_Address,
  input  Write_Enable,
  input  Clock,
  input  Clear_All_Registers,
  output [15:0] ReadLine_A,
  output [15:0] ReadLine_B
);

  wire demultiplexer_1_out1, demultiplexer_1_out2, demultiplexer_1_out3, demultiplexer_1_out4,
       demultiplexer_1_out5, demultiplexer_1_out6, demultiplexer_1_out7, demultiplexer_1_out8,
       demultiplexer_1_out9, demultiplexer_1_out10, demultiplexer_1_out11, demultiplexer_1_out12,
       demultiplexer_1_out13, demultiplexer_1_out14, demultiplexer_1_out15, demultiplexer_2_out0,
       demultiplexer_2_out1, demultiplexer_2_out2, demultiplexer_2_out3, demultiplexer_2_out4,
       demultiplexer_2_out5, demultiplexer_2_out6, demultiplexer_2_out7, demultiplexer_2_out8,
       demultiplexer_2_out9, demultiplexer_2_out10, demultiplexer_2_out11, demultiplexer_2_out12,
       demultiplexer_2_out13, demultiplexer_2_out14, demultiplexer_2_out15, demultiplexer_3_out0,
       demultiplexer_3_out1, demultiplexer_3_out2, demultiplexer_3_out3, demultiplexer_3_out4,
       demultiplexer_3_out5, demultiplexer_3_out6, demultiplexer_3_out7, demultiplexer_3_out8,
       demultiplexer_3_out9, demultiplexer_3_out10, demultiplexer_3_out11, demultiplexer_3_out12,
       demultiplexer_3_out13, demultiplexer_3_out14, demultiplexer_3_out15;
  wire [15:0] register_1_q, register_2_q, register_3_q, register_4_q, register_5_q, register_6_q,
       register_7_q, register_8_q, register_9_q, register_10_q, register_11_q, register_12_q, register_13_q,
       register_14_q, register_15_q;

  Demultiplexer #(.select(4)) demultiplexer_1 (
    .out1(demultiplexer_1_out1), .out2(demultiplexer_1_out2), .out3(demultiplexer_1_out3),
    .out4(demultiplexer_1_out4), .out5(demultiplexer_1_out5), .out6(demultiplexer_1_out6),
    .out7(demultiplexer_1_out7), .out8(demultiplexer_1_out8), .out9(demultiplexer_1_out9),
    .out10(demultiplexer_1_out10), .out11(demultiplexer_1_out11), .out12(demultiplexer_1_out12),
    .out13(demultiplexer_1_out13), .out14(demultiplexer_1_out14), .out15(demultiplexer_1_out15),
    .in(Write_Enable), .sel(Write_Address));  // open: out0
  Register #(.trigger("falling"), .width(16)) register_1 (
    .D(Write_Data), .en(demultiplexer_1_out1), .clk(Clock), .Q(register_1_q), .clr(Clear_All_Registers));
  Register #(.trigger("falling"), .width(16)) register_2 (
    .D(Write_Data), .en(demultiplexer_1_out2), .clk(Clock), .Q(register_2_q), .clr(Clear_All_Registers));
  Register #(.trigger("falling"), .width(16)) register_3 (
    .D(Write_Data), .en(demultiplexer_1_out3), .clk(Clock), .Q(register_3_q), .clr(Clear_All_Registers));
  Register #(.trigger("falling"), .width(16)) register_4 (
    .D(Write_Data), .en(demultiplexer_1_out4), .clk(Clock), .Q(register_4_q), .clr(Clear_All_Registers));
  Register #(.trigger("falling"), .width(16)) register_5 (
    .D(Write_Data), .en(demultiplexer_1_out5), .clk(Clock), .Q(register_5_q), .clr(Clear_All_Registers));
  Register #(.trigger("falling"), .width(16)) register_6 (
    .D(Write_Data), .en(demultiplexer_1_out6), .clk(Clock), .Q(register_6_q), .clr(Clear_All_Registers));
  Register #(.trigger("falling"), .width(16)) register_7 (
    .D(Write_Data), .en(demultiplexer_1_out7), .clk(Clock), .Q(register_7_q), .clr(Clear_All_Registers));
  Register #(.trigger("falling"), .width(16)) register_8 (
    .D(Write_Data), .en(demultiplexer_1_out8), .clk(Clock), .Q(register_8_q), .clr(Clear_All_Registers));
  Register #(.trigger("falling"), .width(16)) register_9 (
    .D(Write_Data), .en(demultiplexer_1_out9), .clk(Clock), .Q(register_9_q), .clr(Clear_All_Registers));
  Register #(.trigger("falling"), .width(16)) register_10 (
    .D(Write_Data), .en(demultiplexer_1_out10), .clk(Clock), .Q(register_10_q), .clr(Clear_All_Registers));
  Register #(.trigger("falling"), .width(16)) register_11 (
    .D(Write_Data), .en(demultiplexer_1_out11), .clk(Clock), .Q(register_11_q), .clr(Clear_All_Registers));
  Register #(.trigger("falling"), .width(16)) register_12 (
    .D(Write_Data), .en(demultiplexer_1_out12), .clk(Clock), .Q(register_12_q), .clr(Clear_All_Registers));
  Register #(.trigger("falling"), .width(16)) register_13 (
    .D(Write_Data), .en(demultiplexer_1_out13), .clk(Clock), .Q(register_13_q), .clr(Clear_All_Registers));
  Register #(.trigger("falling"), .width(16)) register_14 (
    .D(Write_Data), .en(demultiplexer_1_out14), .clk(Clock), .Q(register_14_q), .clr(Clear_All_Registers));
  Register #(.trigger("falling"), .width(16)) register_15 (
    .D(Write_Data), .en(demultiplexer_1_out15), .clk(Clock), .Q(register_15_q), .clr(Clear_All_Registers));
  assign ReadLine_A = demultiplexer_2_out0 ? {16{1'b0}} : 16'bz;  // Controlled_Buffer controlled_buffer_1
  assign ReadLine_B = demultiplexer_3_out0 ? {16{1'b0}} : 16'bz;  // Controlled_Buffer controlled_buffer_2
  assign ReadLine_A = demultiplexer_2_out1 ? register_1_q : 16'bz;  // Controlled_Buffer controlled_buffer_3
  assign ReadLine_B = demultiplexer_3_out1 ? register_1_q : 16'bz;  // Controlled_Buffer controlled_buffer_4
  assign ReadLine_A = demultiplexer_2_out2 ? register_2_q : 16'bz;  // Controlled_Buffer controlled_buffer_5
  assign ReadLine_B = demultiplexer_3_out2 ? register_2_q : 16'bz;  // Controlled_Buffer controlled_buffer_6
  assign ReadLine_A = demultiplexer_2_out3 ? register_3_q : 16'bz;  // Controlled_Buffer controlled_buffer_7
  assign ReadLine_B = demultiplexer_3_out3 ? register_3_q : 16'bz;  // Controlled_Buffer controlled_buffer_8
  assign ReadLine_A = demultiplexer_2_out4 ? register_4_q : 16'bz;  // Controlled_Buffer controlled_buffer_9
  assign ReadLine_B = demultiplexer_3_out4 ? register_4_q : 16'bz;  // Controlled_Buffer controlled_buffer_10
  assign ReadLine_A = demultiplexer_2_out5 ? register_5_q : 16'bz;  // Controlled_Buffer controlled_buffer_11
  assign ReadLine_B = demultiplexer_3_out5 ? register_5_q : 16'bz;  // Controlled_Buffer controlled_buffer_12
  assign ReadLine_A = demultiplexer_2_out6 ? register_6_q : 16'bz;  // Controlled_Buffer controlled_buffer_13
  assign ReadLine_B = demultiplexer_3_out6 ? register_6_q : 16'bz;  // Controlled_Buffer controlled_buffer_14
  assign ReadLine_A = demultiplexer_2_out7 ? register_7_q : 16'bz;  // Controlled_Buffer controlled_buffer_15
  assign ReadLine_B = demultiplexer_3_out7 ? register_7_q : 16'bz;  // Controlled_Buffer controlled_buffer_16
  assign ReadLine_A = demultiplexer_2_out8 ? register_8_q : 16'bz;  // Controlled_Buffer controlled_buffer_17
  assign ReadLine_B = demultiplexer_3_out8 ? register_8_q : 16'bz;  // Controlled_Buffer controlled_buffer_18
  assign ReadLine_A = demultiplexer_2_out9 ? register_9_q : 16'bz;  // Controlled_Buffer controlled_buffer_19
  assign ReadLine_B = demultiplexer_3_out9 ? register_9_q : 16'bz;  // Controlled_Buffer controlled_buffer_20
  assign ReadLine_A = demultiplexer_2_out10 ? register_10_q : 16'bz;  // Controlled_Buffer controlled_buffer_21
  assign ReadLine_B = demultiplexer_3_out10 ? register_10_q : 16'bz;  // Controlled_Buffer controlled_buffer_22
  assign ReadLine_A = demultiplexer_2_out11 ? register_11_q : 16'bz;  // Controlled_Buffer controlled_buffer_23
  assign ReadLine_B = demultiplexer_3_out11 ? register_11_q : 16'bz;  // Controlled_Buffer controlled_buffer_24
  assign ReadLine_A = demultiplexer_2_out12 ? register_12_q : 16'bz;  // Controlled_Buffer controlled_buffer_25
  assign ReadLine_B = demultiplexer_3_out12 ? register_12_q : 16'bz;  // Controlled_Buffer controlled_buffer_26
  assign ReadLine_A = demultiplexer_2_out13 ? register_13_q : 16'bz;  // Controlled_Buffer controlled_buffer_27
  assign ReadLine_B = demultiplexer_3_out13 ? register_13_q : 16'bz;  // Controlled_Buffer controlled_buffer_28
  assign ReadLine_A = demultiplexer_2_out14 ? register_14_q : 16'bz;  // Controlled_Buffer controlled_buffer_29
  assign ReadLine_B = demultiplexer_3_out14 ? register_14_q : 16'bz;  // Controlled_Buffer controlled_buffer_30
  assign ReadLine_A = demultiplexer_2_out15 ? register_15_q : 16'bz;  // Controlled_Buffer controlled_buffer_31
  assign ReadLine_B = demultiplexer_3_out15 ? register_15_q : 16'bz;  // Controlled_Buffer controlled_buffer_32
  Demultiplexer #(.select(4)) demultiplexer_2 (
    .out0(demultiplexer_2_out0), .out1(demultiplexer_2_out1), .out2(demultiplexer_2_out2),
    .out3(demultiplexer_2_out3), .out4(demultiplexer_2_out4), .out5(demultiplexer_2_out5),
    .out6(demultiplexer_2_out6), .out7(demultiplexer_2_out7), .out8(demultiplexer_2_out8),
    .out9(demultiplexer_2_out9), .out10(demultiplexer_2_out10), .out11(demultiplexer_2_out11),
    .out12(demultiplexer_2_out12), .out13(demultiplexer_2_out13), .out14(demultiplexer_2_out14),
    .out15(demultiplexer_2_out15), .in(Read_A_Enable), .sel(Read_Address_A));
  Demultiplexer #(.select(4)) demultiplexer_3 (
    .out0(demultiplexer_3_out0), .out1(demultiplexer_3_out1), .out2(demultiplexer_3_out2),
    .out3(demultiplexer_3_out3), .out4(demultiplexer_3_out4), .out5(demultiplexer_3_out5),
    .out6(demultiplexer_3_out6), .out7(demultiplexer_3_out7), .out8(demultiplexer_3_out8),
    .out9(demultiplexer_3_out9), .out10(demultiplexer_3_out10), .out11(demultiplexer_3_out11),
    .out12(demultiplexer_3_out12), .out13(demultiplexer_3_out13), .out14(demultiplexer_3_out14),
    .out15(demultiplexer_3_out15), .in(Read_B_Enable), .sel(Read_Address_B));
endmodule

module Instruction_Pointer (
  input  [26:0] Bit27_Address_In,
  input  Set_Counter,
  input  [5:0] Bit6_Stall_Cycles,
  input  Clock,
  input  Enable,
  input  Reset_To_0,
  output [26:0] Bit27_Address_Out
);

  wire and_1_out, nor_1_out, or_1_out, or_2_out;
  wire [5:0] counter_1_q;

  or or_1 (or_1_out, Bit6_Stall_Cycles[2], Bit6_Stall_Cycles[0], Bit6_Stall_Cycles[1], Bit6_Stall_Cycles[3], Bit6_Stall_Cycles[4], Bit6_Stall_Cycles[5]);
  Counter #(.max('h3f), .width(6)) counter_1 (
    .clr(Reset_To_0), .load(or_1_out), .up(1'b0), .count(or_2_out), .clk(Clock), .D(Bit6_Stall_Cycles),
    .Q(counter_1_q));  // open: carry
  and and_1 (and_1_out, Enable, nor_1_out);
  or or_2 (or_2_out, counter_1_q[2], counter_1_q[0], counter_1_q[1], counter_1_q[3], counter_1_q[4], counter_1_q[5]);
  nor nor_1 (nor_1_out, counter_1_q[2], counter_1_q[0], counter_1_q[1], counter_1_q[3], counter_1_q[4], counter_1_q[5]);
  Counter #(.max('h3ffffff), .width(26)) counter_2 (
    .clr(Reset_To_0), .load(Set_Counter), .up(Enable), .count(and_1_out), .clk(Clock),
    .D(Bit27_Address_In[26:1]), .Q(Bit27_Address_Out[26:1]));  // open: carry
  D_Flip_Flop d_ff_1 (
    .D(Bit27_Address_In[0]), .clk(Clock), .Q(Bit27_Address_Out[0]), .preset(Set_Counter), .reset(Reset_To_0));  // open: Qn
endmodule

module Memory_Controller (
  input  [15:0] Bit16_Data_In,
  input  [26:0] Bit27_Address,
  input  Read_Enable,
  input  Write_Enable,
  input  Two_Byte_Operation,
  input  Clock,
  input  Reset,
  output Out_Of_Bounds,
  output [15:0] Bit16_Output
);

  wire and_1_out, and_2_out, and_3_out, and_4_out, and_5_out, and_6_out, and_7_out, and_8_out, and_9_out,
       and_10_out, and_11_out, and_12_out, and_13_out, bit24_add_one_1_c_out, demultiplexer_1_out0,
       demultiplexer_1_out1, demultiplexer_1_out2, demultiplexer_1_out3, demultiplexer_2_out0,
       demultiplexer_2_out1, demultiplexer_2_out2, demultiplexer_2_out3, demultiplexer_3_out0,
       demultiplexer_3_out1, demultiplexer_3_out2, demultiplexer_3_out3, demultiplexer_4_out0,
       demultiplexer_4_out1, demultiplexer_4_out2, demultiplexer_4_out3, not_1_out, or_1_out, or_2_out,
       or_3_out, or_4_out, or_5_out;
  wire [1:0] bit2_add_one_1_bit2_out;
  wire [7:0] controlled_buffer_1_out, controlled_buffer_3_out, pull_resistor_4_node, pull_resistor_5_node,
       ram_1_dout, ram_2_dout, ram_3_dout, ram_4_dout, ram_5_dout, ram_6_dout, ram_7_dout, ram_8_dout;
  wire [23:0] bit24_add_one_1_bit24_out, pull_resistor_3_node;

  and and_1 (and_1_out, Write_Enable, ~Bit27_Address[0]);  // AND_Gate
  and and_2 (and_2_out, Write_Enable, Bit27_Address[0]);
  and and_3 (and_3_out, Write_Enable, Two_Byte_Operation, Bit27_Address[0]);
  and and_4 (and_4_out, ~Bit27_Address[0], Two_Byte_Operation, Write_Enable);  // AND_Gate
  assign controlled_buffer_1_out = and_1_out ? Bit16_Data_In[7:0] : 8'bz;  // Controlled_Buffer controlled_buffer_1
  Pull_Resistor pull_resistor_1 (.node(controlled_buffer_1_out));
  assign controlled_buffer_1_out = and_2_out ? Bit16_Data_In[15:8] : 8'bz;  // Controlled_Buffer controlled_buffer_2
  assign controlled_buffer_3_out = and_3_out ? Bit16_Data_In[7:0] : 8'bz;  // Controlled_Buffer controlled_buffer_3
  Pull_Resistor pull_resistor_2 (.node(controlled_buffer_3_out));
  assign controlled_buffer_3_out = and_4_out ? Bit16_Data_In[15:8] : 8'bz;  // Controlled_Buffer controlled_buffer_4
  or or_1 (or_1_out, Write_Enable, Read_Enable);
  Bit2_Add_One bit2_add_one_1 (
    .Add_One(bit24_add_one_1_c_out), .Bit2_In(Bit27_Address[26:25]), .Bit2_Out(bit2_add_one_1_bit2_out),
    .Carry_Out(Out_Of_Bounds));
  Register #(.width(16)) Last_Write_Data (.D(Bit16_Data_In), .en(Write_Enable), .clk(Clock), .clr(Reset));  // open: Q
  Register #(.width(27)) Last_Access_Address (.D(Bit27_Address), .en(or_1_out), .clk(Clock), .clr(Reset));  // open: Q
  and and_5 (and_5_out, Two_Byte_Operation, Bit27_Address[0]);
  or or_2 (or_2_out, Bit27_Address[0], Two_Byte_Operation);
  and and_6 (and_6_out, Read_Enable, or_2_out);
  and and_7 (and_7_out, Read_Enable, or_3_out);
  Demultiplexer #(.select(2)) demultiplexer_1 (
    .out0(demultiplexer_1_out0), .out1(demultiplexer_1_out1), .out2(demultiplexer_1_out2),
    .out3(demultiplexer_1_out3), .in(and_6_out), .sel(Bit27_Address[26:25]));
  or or_3 (or_3_out, ~Bit27_Address[0], Two_Byte_Operation);  // OR_Gate
  or or_4 (or_4_out, Bit27_Address[0], Two_Byte_Operation);
  and and_8 (and_8_out, Write_Enable, or_4_out);
  Demultiplexer #(.select(2)) demultiplexer_2 (
    .out0(demultiplexer_2_out0), .out1(demultiplexer_2_out1), .out2(demultiplexer_2_out2),
    .out3(demultiplexer_2_out3), .in(and_7_out), .sel(bit2_add_one_1_bit2_out));
  Demultiplexer #(.select(2)) demultiplexer_3 (
    .out0(demultiplexer_3_out0), .out1(demultiplexer_3_out1), .out2(demultiplexer_3_out2),
    .out3(demultiplexer_3_out3), .in(and_8_out), .sel(Bit27_Address[26:25]));
  or or_5 (or_5_out, ~Bit27_Address[0], Two_Byte_Operation);  // OR_Gate
  and and_9 (and_9_out, Write_Enable, or_5_out);
  Demultiplexer #(.select(2)) demultiplexer_4 (
    .out0(demultiplexer_4_out0), .out1(demultiplexer_4_out1), .out2(demultiplexer_4_out2),
    .out3(demultiplexer_4_out3), .in(and_9_out), .sel(bit2_add_one_1_bit2_out));
  RAM #(.addrWidth(24), .asyncread("true"), .clearpin("true")) ram_1 (
    .addr(pull_resistor_3_node), .we(demultiplexer_4_out0), .oe(demultiplexer_2_out0), .clk(Clock),
    .din(controlled_buffer_1_out), .dout(ram_1_dout), .clr(Reset));
  RAM #(.addrWidth(24), .asyncread("true"), .clearpin("true")) ram_2 (
    .addr(Bit27_Address[24:1]), .we(demultiplexer_3_out0), .oe(demultiplexer_1_out0), .clk(Clock),
    .din(controlled_buffer_3_out), .dout(ram_2_dout), .clr(Reset));
  RAM #(.addrWidth(24), .asyncread("true"), .clearpin("true")) ram_3 (
    .addr(pull_resistor_3_node), .we(demultiplexer_4_out1), .oe(demultiplexer_2_out1), .clk(Clock),
    .din(controlled_buffer_1_out), .dout(ram_3_dout), .clr(Reset));
  RAM #(.addrWidth(24), .asyncread("true"), .clearpin("true")) ram_4 (
    .addr(Bit27_Address[24:1]), .we(demultiplexer_3_out1), .oe(demultiplexer_1_out1), .clk(Clock),
    .din(controlled_buffer_3_out), .dout(ram_4_dout), .clr(Reset));
  RAM #(.addrWidth(24), .asyncread("true"), .clearpin("true")) ram_5 (
    .addr(pull_resistor_3_node), .we(demultiplexer_4_out2), .oe(demultiplexer_2_out2), .clk(Clock),
    .din(controlled_buffer_1_out), .dout(ram_5_dout), .clr(Reset));
  RAM #(.addrWidth(24), .asyncread("true"), .clearpin("true")) ram_6 (
    .addr(Bit27_Address[24:1]), .we(demultiplexer_3_out2), .oe(demultiplexer_1_out2), .clk(Clock),
    .din(controlled_buffer_3_out), .dout(ram_6_dout), .clr(Reset));
  RAM #(.addrWidth(24), .asyncread("true"), .clearpin("true")) ram_7 (
    .addr(pull_resistor_3_node), .we(demultiplexer_4_out3), .oe(demultiplexer_2_out3), .clk(Clock),
    .din(controlled_buffer_1_out), .dout(ram_7_dout), .clr(Reset));
  RAM #(.addrWidth(24), .asyncread("true"), .clearpin("true")) ram_8 (
    .addr(Bit27_Address[24:1]), .we(demultiplexer_3_out3), .oe(demultiplexer_1_out3), .clk(Clock),
    .din(controlled_buffer_3_out), .dout(ram_8_dout), .clr(Reset));
  Bit24_Add_One bit24_add_one_1 (
    .Add_One(and_5_out), .Bit24_In(Bit27_Address[24:1]), .Bit24_Out(bit24_add_one_1_bit24_out),
    .C_Out(bit24_add_one_1_c_out));
  Pull_Resistor pull_resistor_3 (.node(pull_resistor_3_node));
  assign pull_resistor_3_node = and_5_out ? bit24_add_one_1_bit24_out : 24'bz;  // Controlled_Buffer controlled_buffer_5
  not not_1 (not_1_out, and_5_out);
  assign pull_resistor_3_node = not_1_out ? Bit27_Address[24:1] : 24'bz;  // Controlled_Buffer controlled_buffer_6
  Pull_Resistor pull_resistor_4 (.node(pull_resistor_4_node));
  Pull_Resistor pull_resistor_5 (.node(pull_resistor_5_node));
  assign pull_resistor_4_node = demultiplexer_2_out0 ? ram_1_dout : 8'bz;  // Controlled_Buffer controlled_buffer_7
  assign pull_resistor_5_node = demultiplexer_1_out0 ? ram_2_dout : 8'bz;  // Controlled_Buffer controlled_buffer_8
  assign pull_resistor_4_node = demultiplexer_2_out1 ? ram_3_dout : 8'bz;  // Controlled_Buffer controlled_buffer_9
  assign pull_resistor_5_node = demultiplexer_1_out1 ? ram_4_dout : 8'bz;  // Controlled_Buffer controlled_buffer_10
  assign pull_resistor_4_node = demultiplexer_2_out2 ? ram_5_dout : 8'bz;  // Controlled_Buffer controlled_buffer_11
  assign pull_resistor_5_node = demultiplexer_1_out2 ? ram_6_dout : 8'bz;  // Controlled_Buffer controlled_buffer_12
  assign pull_resistor_4_node = demultiplexer_2_out3 ? ram_7_dout : 8'bz;  // Controlled_Buffer controlled_buffer_13
  assign pull_resistor_5_node = demultiplexer_1_out3 ? ram_8_dout : 8'bz;  // Controlled_Buffer controlled_buffer_14
  and and_10 (and_10_out, Read_Enable, ~Bit27_Address[0]);  // AND_Gate
  and and_11 (and_11_out, Read_Enable, Bit27_Address[0]);
  and and_12 (and_12_out, Read_Enable, Two_Byte_Operation, Bit27_Address[0]);
  and and_13 (and_13_out, ~Bit27_Address[0], Two_Byte_Operation, Read_Enable);  // AND_Gate
  assign Bit16_Output[7:0] = and_10_out ? pull_resistor_4_node : 8'bz;  // Controlled_Buffer controlled_buffer_15
  assign Bit16_Output[7:0] = and_11_out ? pull_resistor_5_node : 8'bz;  // Controlled_Buffer controlled_buffer_16
  assign Bit16_Output[15:8] = and_12_out ? pull_resistor_4_node : 8'bz;  // Controlled_Buffer controlled_buffer_17
  assign Bit16_Output[15:8] = and_13_out ? pull_resistor_5_node : 8'bz;  // Controlled_Buffer controlled_buffer_18
  Pull_Resistor pull_resistor_6 (.node(Bit16_Output[7:0]));
  Pull_Resistor pull_resistor_7 (.node(Bit16_Output[15:8]));
  Register #(.width(16)) Last_Read_Value (.D(Bit16_Output), .en(Read_Enable), .clk(Clock), .clr(Reset));  // open: Q

  // Notes on the sheet:
  //   address requested will be in the lower byte of the word
  //   if 2 byte, the addr will be lower, and addr+1 will be in the upper
  //   these reg and state for dbugging
endmodule

module Bit24_Add_One (
  input  Add_One,
  input  [23:0] Bit24_In,
  output [23:0] Bit24_Out,
  output C_Out
);

  wire and_1_out, and_2_out, and_3_out, and_4_out, and_5_out, and_6_out, and_7_out, and_8_out, and_9_out,
       and_10_out, and_11_out, and_12_out, and_13_out, and_14_out, and_15_out, and_16_out, and_17_out,
       and_18_out, and_19_out, and_20_out, and_21_out, and_22_out, and_23_out;

  and and_1 (and_1_out, Add_One, Bit24_In[0]);
  and and_2 (and_2_out, Add_One, Bit24_In[0], Bit24_In[1]);
  and and_3 (and_3_out, Add_One, Bit24_In[0], Bit24_In[1], Bit24_In[2]);
  and and_4 (and_4_out, Add_One, Bit24_In[0], Bit24_In[1], Bit24_In[2], Bit24_In[3]);
  and and_5 (and_5_out, Add_One, Bit24_In[0], Bit24_In[1], Bit24_In[2], Bit24_In[3], Bit24_In[4]);
  and and_6 (and_6_out, Add_One, Bit24_In[0], Bit24_In[1], Bit24_In[2], Bit24_In[3], Bit24_In[4], Bit24_In[5]);
  and and_7 (and_7_out, Add_One, Bit24_In[0], Bit24_In[1], Bit24_In[2], Bit24_In[3], Bit24_In[4], Bit24_In[5], Bit24_In[6]);
  and and_8 (and_8_out, Add_One, Bit24_In[0], Bit24_In[1], Bit24_In[2], Bit24_In[3], Bit24_In[4], Bit24_In[5], Bit24_In[6], Bit24_In[7]);
  and and_9 (and_9_out, Add_One, Bit24_In[0], Bit24_In[1], Bit24_In[2], Bit24_In[3], Bit24_In[4], Bit24_In[5], Bit24_In[6], Bit24_In[7], Bit24_In[8]);
  and and_10 (and_10_out, Add_One, Bit24_In[0], Bit24_In[1], Bit24_In[2], Bit24_In[3], Bit24_In[4], Bit24_In[5], Bit24_In[6], Bit24_In[7], Bit24_In[8], Bit24_In[9]);
  and and_11 (and_11_out, Add_One, Bit24_In[0], Bit24_In[1], Bit24_In[2], Bit24_In[3], Bit24_In[4], Bit24_In[5], Bit24_In[6], Bit24_In[7], Bit24_In[8], Bit24_In[9], Bit24_In[10]);
  and and_12 (and_12_out, Add_One, Bit24_In[0], Bit24_In[1], Bit24_In[2], Bit24_In[3], Bit24_In[4], Bit24_In[5], Bit24_In[6], Bit24_In[7], Bit24_In[8], Bit24_In[9], Bit24_In[10], Bit24_In[11]);
  and and_13 (and_13_out, Add_One, Bit24_In[0], Bit24_In[1], Bit24_In[2], Bit24_In[3], Bit24_In[4], Bit24_In[5], Bit24_In[6], Bit24_In[7], Bit24_In[8], Bit24_In[9], Bit24_In[10], Bit24_In[11], Bit24_In[12]);
  and and_14 (and_14_out, Add_One, Bit24_In[0], Bit24_In[1], Bit24_In[2], Bit24_In[3], Bit24_In[4], Bit24_In[5], Bit24_In[6], Bit24_In[7], Bit24_In[8], Bit24_In[9], Bit24_In[10], Bit24_In[11], Bit24_In[12], Bit24_In[13]);
  and and_15 (and_15_out, Add_One, Bit24_In[0], Bit24_In[1], Bit24_In[2], Bit24_In[3], Bit24_In[4], Bit24_In[5], Bit24_In[6], Bit24_In[7], Bit24_In[8], Bit24_In[9], Bit24_In[10], Bit24_In[11], Bit24_In[12], Bit24_In[13], Bit24_In[14]);
  and and_16 (and_16_out, Add_One, Bit24_In[0], Bit24_In[1], Bit24_In[2], Bit24_In[3], Bit24_In[4], Bit24_In[5], Bit24_In[6], Bit24_In[7], Bit24_In[8], Bit24_In[9], Bit24_In[10], Bit24_In[11], Bit24_In[12], Bit24_In[13], Bit24_In[14], Bit24_In[15]);
  and and_17 (and_17_out, Add_One, Bit24_In[0], Bit24_In[1], Bit24_In[2], Bit24_In[3], Bit24_In[4], Bit24_In[5], Bit24_In[6], Bit24_In[7], Bit24_In[8], Bit24_In[9], Bit24_In[10], Bit24_In[11], Bit24_In[12], Bit24_In[13], Bit24_In[14], Bit24_In[15], Bit24_In[16]);
  and and_18 (and_18_out, Add_One, Bit24_In[0], Bit24_In[1], Bit24_In[2], Bit24_In[3], Bit24_In[4], Bit24_In[5], Bit24_In[6], Bit24_In[7], Bit24_In[8], Bit24_In[9], Bit24_In[10], Bit24_In[11], Bit24_In[12], Bit24_In[13], Bit24_In[14], Bit24_In[15], Bit24_In[16], Bit24_In[17]);
  and and_19 (and_19_out, Add_One, Bit24_In[0], Bit24_In[1], Bit24_In[2], Bit24_In[3], Bit24_In[4], Bit24_In[5], Bit24_In[6], Bit24_In[7], Bit24_In[8], Bit24_In[9], Bit24_In[10], Bit24_In[11], Bit24_In[12], Bit24_In[13], Bit24_In[14], Bit24_In[15], Bit24_In[16], Bit24_In[17], Bit24_In[18]);
  and and_20 (and_20_out, Add_One, Bit24_In[0], Bit24_In[1], Bit24_In[2], Bit24_In[3], Bit24_In[4], Bit24_In[5], Bit24_In[6], Bit24_In[7], Bit24_In[8], Bit24_In[9], Bit24_In[10], Bit24_In[11], Bit24_In[12], Bit24_In[13], Bit24_In[14], Bit24_In[15], Bit24_In[16], Bit24_In[17], Bit24_In[18], Bit24_In[19]);
  and and_21 (and_21_out, Add_One, Bit24_In[0], Bit24_In[1], Bit24_In[2], Bit24_In[3], Bit24_In[4], Bit24_In[5], Bit24_In[6], Bit24_In[7], Bit24_In[8], Bit24_In[9], Bit24_In[10], Bit24_In[11], Bit24_In[12], Bit24_In[13], Bit24_In[14], Bit24_In[15], Bit24_In[16], Bit24_In[17], Bit24_In[18], Bit24_In[19], Bit24_In[20]);
  and and_22 (and_22_out, Add_One, Bit24_In[0], Bit24_In[1], Bit24_In[2], Bit24_In[3], Bit24_In[4], Bit24_In[5], Bit24_In[6], Bit24_In[7], Bit24_In[8], Bit24_In[9], Bit24_In[10], Bit24_In[11], Bit24_In[12], Bit24_In[13], Bit24_In[14], Bit24_In[15], Bit24_In[16], Bit24_In[17], Bit24_In[18], Bit24_In[19], Bit24_In[20], Bit24_In[21]);
  and and_23 (and_23_out, Add_One, Bit24_In[0], Bit24_In[1], Bit24_In[2], Bit24_In[3], Bit24_In[4], Bit24_In[5], Bit24_In[6], Bit24_In[7], Bit24_In[8], Bit24_In[9], Bit24_In[10], Bit24_In[11], Bit24_In[12], Bit24_In[13], Bit24_In[14], Bit24_In[15], Bit24_In[16], Bit24_In[17], Bit24_In[18], Bit24_In[19], Bit24_In[20], Bit24_In[21], Bit24_In[22]);
  and and_24 (C_Out, Add_One, Bit24_In[0], Bit24_In[1], Bit24_In[2], Bit24_In[3], Bit24_In[4], Bit24_In[5], Bit24_In[6], Bit24_In[7], Bit24_In[8], Bit24_In[9], Bit24_In[10], Bit24_In[11], Bit24_In[12], Bit24_In[13], Bit24_In[14], Bit24_In[15], Bit24_In[16], Bit24_In[17], Bit24_In[18], Bit24_In[19], Bit24_In[20], Bit24_In[21], Bit24_In[22], Bit24_In[23]);
  xor xor_1 (Bit24_Out[0], Bit24_In[0], Add_One);
  xor xor_2 (Bit24_Out[1], Bit24_In[1], and_1_out);
  xor xor_3 (Bit24_Out[2], Bit24_In[2], and_2_out);
  xor xor_4 (Bit24_Out[3], Bit24_In[3], and_3_out);
  xor xor_5 (Bit24_Out[4], Bit24_In[4], and_4_out);
  xor xor_6 (Bit24_Out[5], Bit24_In[5], and_5_out);
  xor xor_7 (Bit24_Out[6], Bit24_In[6], and_6_out);
  xor xor_8 (Bit24_Out[7], Bit24_In[7], and_7_out);
  xor xor_9 (Bit24_Out[8], Bit24_In[8], and_8_out);
  xor xor_10 (Bit24_Out[9], Bit24_In[9], and_9_out);
  xor xor_11 (Bit24_Out[10], Bit24_In[10], and_10_out);
  xor xor_12 (Bit24_Out[11], Bit24_In[11], and_11_out);
  xor xor_13 (Bit24_Out[12], Bit24_In[12], and_12_out);
  xor xor_14 (Bit24_Out[13], Bit24_In[13], and_13_out);
  xor xor_15 (Bit24_Out[14], Bit24_In[14], and_14_out);
  xor xor_16 (Bit24_Out[15], Bit24_In[15], and_15_out);
  xor xor_17 (Bit24_Out[16], Bit24_In[16], and_16_out);
  xor xor_18 (Bit24_Out[17], Bit24_In[17], and_17_out);
  xor xor_19 (Bit24_Out[18], Bit24_In[18], and_18_out);
  xor xor_20 (Bit24_Out[19], Bit24_In[19], and_19_out);
  xor xor_21 (Bit24_Out[20], Bit24_In[20], and_20_out);
  xor xor_22 (Bit24_Out[21], Bit24_In[21], and_21_out);
  xor xor_23 (Bit24_Out[22], Bit24_In[22], and_22_out);
  xor xor_24 (Bit24_Out[23], Bit24_In[23], and_23_out);
endmodule

module Bit4_Add_One (
  input  Add_One,
  input  [3:0] Bit4_In,
  output [3:0] Bit4_Out,
  output Carry_Out
);

  wire and_1_out, and_2_out, and_3_out;

  and and_1 (and_1_out, Add_One, Bit4_In[0]);
  and and_2 (and_2_out, Add_One, Bit4_In[0], Bit4_In[1]);
  and and_3 (and_3_out, Add_One, Bit4_In[0], Bit4_In[1], Bit4_In[2]);
  and and_4 (Carry_Out, Add_One, Bit4_In[0], Bit4_In[1], Bit4_In[2], Bit4_In[3]);
  xor xor_1 (Bit4_Out[0], Bit4_In[0], Add_One);
  xor xor_2 (Bit4_Out[1], Bit4_In[1], and_1_out);
  xor xor_3 (Bit4_Out[2], Bit4_In[2], and_2_out);
  xor xor_4 (Bit4_Out[3], Bit4_In[3], and_3_out);
endmodule

module Bit2_Add_One (
  input  Add_One,
  input  [1:0] Bit2_In,
  output [1:0] Bit2_Out,
  output Carry_Out
);

  wire and_1_out;

  and and_1 (and_1_out, Add_One, Bit2_In[0]);
  and and_2 (Carry_Out, Add_One, Bit2_In[0], Bit2_In[1]);
  xor xor_1 (Bit2_Out[0], Bit2_In[0], Add_One);
  xor xor_2 (Bit2_Out[1], Bit2_In[1], and_1_out);
endmodule

module Instruction_Decoder (
  input  [15:0] Bit16_Instruction,
  input  [1:0] Privilege_Level,
  output Register_Read_A_Enable,
  output [3:0] Register_Read_A_Address,
  output Register_Read_B_Enable,
  output [3:0] Register_Read_B_Address,
  output Register_Write_Enable,
  output [3:0] Register_Write_Address,
  output Immediate_Register_Write,
  output [15:0] Bit16_Register_Write_Data,
  output ALU_Immediate,
  output Bit11_Immediate,
  output ALU_Writeback,
  output Register_Writeback,
  output Set_Memory_Offset,
  output Bit11_Memory_Offset,
  output Memory_Read,
  output Memory_Write,
  output Interrupt_Disable,
  output Interrupt_Enable,
  output System_Call,
  output Set_Privilege_Mode,
  output [1:0] Bit2_Privilege_Mode,
  output Assign_Page,
  output Deassign_Page,
  output [5:0] Bit6_Stall_Count
);


  // Notes on the sheet:
  //   BELOW IS ALWAYS INPUT B.
  //   below is only for when loading immediates
  //   11 since thats the max immediate loaded ot the alu
endmodule

module Page_Mapper (
  input  [26:0] Bit27_Address,
  input  Translate_Operation,
  input  [7:0] Bit8_Context_Id,
  input  Assign_Page,
  input  Deallocate_Page,
  input  [1:0] Privilege_Level,
  input  Clock,
  input  Enable,
  input  Reset,
  output [26:0] Translated_Address,
  output Address_Not_Allocated
);

  wire and_1_out, and_2_out, and_4_out, and_5_out, Deallocated_Page_Available,
       Deallocating_Or_Page_Available_To_Allocate, nor_1_out, not_1_out, not_2_out, or_3_out,
       Page_Index_Changing, Privilege_Level_Zero;
  wire [14:0] bit_extender_1_out;
  wire [15:0] adder_1_out, Bit16_Virtual_Page_Index, controlled_buffer_1_out, controlled_buffer_5_out,
       controlled_buffer_7_out, controlled_buffer_8_out, controlled_buffer_12_out,
       Highest_Current_Context_Allocated, Highest_Unassigned_Page, Last_Freed_Page, Next_Free_Page,
       Page_Address, ram_1_dout, ram_3_dout;
  wire [22:0] Bit23_Translation_Lookup;

  assign controlled_buffer_1_out = Deallocate_Page ? Highest_Current_Context_Allocated : 16'bz;  // Controlled_Buffer controlled_buffer_1
  not not_1 (not_1_out, Deallocate_Page);
  assign controlled_buffer_1_out = not_1_out ? Bit16_Virtual_Page_Index : 16'bz;  // Controlled_Buffer controlled_buffer_2
  Pull_Resistor pull_resistor_1 (.node(Bit23_Translation_Lookup));
  assign Bit23_Translation_Lookup = Translate_Operation ? {Bit8_Context_Id, Bit27_Address[26:12]} : 23'bz;  // Controlled_Buffer controlled_buffer_3
  and and_1 (and_1_out, Deallocated_Page_Available, Assign_Page);
  or or_1 (Deallocating_Or_Page_Available_To_Allocate, and_1_out, Deallocate_Page);
  Pull_Resistor pull_resistor_2 (.node(Bit23_Translation_Lookup));
  assign Bit23_Translation_Lookup = Page_Index_Changing ? {Bit8_Context_Id, controlled_buffer_1_out[14:0]} : 23'bz;  // Controlled_Buffer controlled_buffer_4
  assign controlled_buffer_5_out = Assign_Page ? Last_Freed_Page : 16'bz;  // Controlled_Buffer controlled_buffer_5
  assign controlled_buffer_5_out = Deallocate_Page ? Highest_Current_Context_Allocated : 16'bz;  // Controlled_Buffer controlled_buffer_6
  or or_2 (Page_Index_Changing, Assign_Page, Deallocate_Page);
  or or_3 (or_3_out, Deallocate_Page, Translate_Operation);
  assign controlled_buffer_7_out = Assign_Page ? Next_Free_Page : 16'bz;  // Controlled_Buffer controlled_buffer_7
  Pull_Resistor pull_resistor_3 (.node(controlled_buffer_5_out));
  and and_2 (and_2_out, Assign_Page, ~Deallocated_Page_Available);  // AND_Gate
  Pull_Resistor pull_resistor_4 (.node(controlled_buffer_7_out));
  Bit_Extender #(.in_width(16), .out_width(15), .\type ("zero")) bit_extender_1 (
    .in(controlled_buffer_5_out), .out(bit_extender_1_out));
  RAM #(.asyncread("true"), .dataWidth(16), .trigger("falling")) ram_1 (
    .addr(Bit8_Context_Id), .we(Page_Index_Changing), .oe(Page_Index_Changing), .clk(Clock),
    .din(controlled_buffer_12_out), .dout(ram_1_dout));
  RAM #(.addrWidth(23), .asyncread("true"), .dataWidth(16)) ram_2 (
    .addr(Bit23_Translation_Lookup), .we(Page_Index_Changing), .oe(or_3_out), .clk(Clock),
    .din(controlled_buffer_7_out), .dout(Page_Address));
  RAM #(.addrWidth(15), .asyncread("true"), .dataWidth(16)) ram_3 (
    .addr(bit_extender_1_out), .we(Deallocating_Or_Page_Available_To_Allocate), .oe(Page_Index_Changing),
    .clk(Clock), .din(Last_Freed_Page), .dout(ram_3_dout));
  assign controlled_buffer_8_out = Deallocate_Page ? Page_Address : 16'bz;  // Controlled_Buffer controlled_buffer_8
  assign controlled_buffer_8_out = Assign_Page ? ram_3_dout : 16'bz;  // Controlled_Buffer controlled_buffer_9
  RAM #(.addrWidth(7), .asyncread("true")) ram_4 ();  // open: addr, we, oe, clk, din, dout
  Counter #(.max('hffff), .width(16)) counter_1 (
    .up(Enable), .count(and_2_out), .clk(Clock), .Q(Highest_Unassigned_Page));  // open: clr, load, D, carry
  Register #(.width(16)) register_1 (
    .D(controlled_buffer_8_out), .en(Deallocating_Or_Page_Available_To_Allocate), .clk(Clock),
    .Q(Last_Freed_Page));  // open: clr
  assign Bit16_Virtual_Page_Index = Deallocate_Page ? controlled_buffer_12_out : 16'bz;  // Controlled_Buffer controlled_buffer_10
  Pull_Resistor pull_resistor_5 (.node(Bit16_Virtual_Page_Index));
  assign Bit16_Virtual_Page_Index = Assign_Page ? ram_1_dout : 16'bz;  // Controlled_Buffer controlled_buffer_11
  or or_4 (Privilege_Level_Zero, Privilege_Level[0], Privilege_Level[1]);
  and and_3 (Address_Not_Allocated, Privilege_Level_Zero, nor_1_out);
  nor nor_1 (nor_1_out, Page_Address[7], Page_Address[0], Page_Address[1], Page_Address[2], Page_Address[3], Page_Address[4], Page_Address[5], Page_Address[6], Page_Address[8], Page_Address[9], Page_Address[10], Page_Address[11], Page_Address[12], Page_Address[13], Page_Address[14], Page_Address[15]);
  Subtractor #(.width(16)) subtractor_1 (
    .a(ram_1_dout), .b(16'h1), .out(Highest_Current_Context_Allocated));  // open: bin, bout
  Adder #(.width(16)) adder_1 (.a(ram_1_dout), .b(16'h1), .out(adder_1_out));  // open: cin, cout
  assign controlled_buffer_12_out = Deallocate_Page ? Highest_Current_Context_Allocated : 16'bz;  // Controlled_Buffer controlled_buffer_12
  assign controlled_buffer_12_out = Assign_Page ? adder_1_out : 16'bz;  // Controlled_Buffer controlled_buffer_13
  or or_5 (Deallocated_Page_Available, Last_Freed_Page[7], Last_Freed_Page[0], Last_Freed_Page[1], Last_Freed_Page[2], Last_Freed_Page[3], Last_Freed_Page[4], Last_Freed_Page[5], Last_Freed_Page[6], Last_Freed_Page[8], Last_Freed_Page[9], Last_Freed_Page[10], Last_Freed_Page[11], Last_Freed_Page[12], Last_Freed_Page[13], Last_Freed_Page[14], Last_Freed_Page[15]);
  Pull_Resistor pull_resistor_6 (.node(Translated_Address));
  assign Translated_Address = and_4_out ? {Page_Address, Bit27_Address[10:0]} : 27'bz;  // Controlled_Buffer controlled_buffer_14
  and and_4 (and_4_out, ~Address_Not_Allocated, Translate_Operation);  // AND_Gate
  assign Translated_Address = and_5_out ? Bit27_Address : 27'bz;  // Controlled_Buffer controlled_buffer_15
  and and_5 (and_5_out, ~Translate_Operation, Privilege_Level_Zero);  // AND_Gate
  not not_2 (not_2_out, Deallocated_Page_Available);
  assign Next_Free_Page = not_2_out ? Highest_Unassigned_Page : 16'bz;  // Controlled_Buffer controlled_buffer_16
  assign Next_Free_Page = Deallocated_Page_Available ? Last_Freed_Page : 16'bz;  // Controlled_Buffer controlled_buffer_17

  // Notes on the sheet:
  //   highest+1 index allocated by context id
  //   translation table
  //   indexed by page, stores last deallocated page index
  //   last freed
  //   page assigned (addr is top 7, byte is lower 8, bit per)
  //   highest assigned
  //   it is truly tragic that this is not a viable solution :(
endmodule

module Bit16_Cache_Cell (
  input  [15:0] Bit16_Key_Data,
  input  [15:0] Bit16_Value_Data,
  input  [15:0] Bit16_Search_Key,
  input  NOT_Search_Enable,
  input  Set_Cell,
  input  Reset_Cell,
  input  Clock,
  input  Force_Reset,
  output [15:0] Bit16_Value_Bus,
  output Search_Match,
  output Search_Match_Non_Buffered
);

  wire and_1_out, or_1_out;
  wire [15:0] Current_Key, Val_Reg_q, xor_1_out;

  and and_1 (and_1_out, Search_Match_Non_Buffered, Reset_Cell);
  Register #(.width(16)) Key_Reg (.D(Bit16_Key_Data), .en(or_1_out), .clk(Clock), .Q(Current_Key));  // open: clr
  Register #(.width(16)) Val_Reg (.D(Bit16_Value_Data), .en(or_1_out), .clk(Clock), .Q(Val_Reg_q));  // open: clr
  or or_1 (or_1_out, Set_Cell, Force_Reset, and_1_out);
  assign Bit16_Value_Bus = Search_Match_Non_Buffered ? Val_Reg_q : 16'bz;  // Controlled_Buffer controlled_buffer_1
  xor xor_1 (xor_1_out[0], Current_Key[0], Bit16_Search_Key[0]);
  xor xor_2 (xor_1_out[1], Current_Key[1], Bit16_Search_Key[1]);
  xor xor_3 (xor_1_out[2], Current_Key[2], Bit16_Search_Key[2]);
  xor xor_4 (xor_1_out[3], Current_Key[3], Bit16_Search_Key[3]);
  xor xor_5 (xor_1_out[4], Current_Key[4], Bit16_Search_Key[4]);
  xor xor_6 (xor_1_out[5], Current_Key[5], Bit16_Search_Key[5]);
  xor xor_7 (xor_1_out[6], Current_Key[6], Bit16_Search_Key[6]);
  xor xor_8 (xor_1_out[7], Current_Key[7], Bit16_Search_Key[7]);
  xor xor_9 (xor_1_out[8], Current_Key[8], Bit16_Search_Key[8]);
  xor xor_10 (xor_1_out[9], Current_Key[9], Bit16_Search_Key[9]);
  xor xor_11 (xor_1_out[10], Current_Key[10], Bit16_Search_Key[10]);
  xor xor_12 (xor_1_out[11], Current_Key[11], Bit16_Search_Key[11]);
  xor xor_13 (xor_1_out[12], Current_Key[12], Bit16_Search_Key[12]);
  xor xor_14 (xor_1_out[13], Current_Key[13], Bit16_Search_Key[13]);
  xor xor_15 (xor_1_out[14], Current_Key[14], Bit16_Search_Key[14]);
  xor xor_16 (xor_1_out[15], Current_Key[15], Bit16_Search_Key[15]);
  nor nor_1 (Search_Match_Non_Buffered, NOT_Search_Enable, xor_1_out[0], xor_1_out[1], xor_1_out[2], xor_1_out[3], xor_1_out[4], xor_1_out[5], xor_1_out[6], xor_1_out[7], xor_1_out[8], xor_1_out[9], xor_1_out[10], xor_1_out[11], xor_1_out[12], xor_1_out[13], xor_1_out[14], xor_1_out[15]);
  // XOR_Gate xor_17 is placed but not wired
  assign Search_Match = Search_Match_Non_Buffered ? Search_Match_Non_Buffered : 1'bz;  // Controlled_Buffer controlled_buffer_2

  // Other names for the same wires on the sheet: Key_Match = Search_Match_Non_Buffered;
  //   Search_Enable = NOT_Search_Enable; Search_Key[15:0] = Bit16_Search_Key
endmodule

module Translation_Lookaside_Buffer (
  input  [15:0] Bit16_Key_Data,
  input  [15:0] Bit16_Value_Data,
  input  [15:0] Bit16_Search_Key,
  input  Search_Enable,
  input  Set_Cell,
  input  Reset_Cell,
  input  [2:0] Bit3_Cell_Index,
  input  Clock,
  input  Enable,
  input  Reset_Buffer,
  output [2:0] Bit3_Least_Recently_Used_Cell,
  output Key_In_Cache,
  output [15:0] Bit16_Value,
  output Cache_Miss
);

  wire and_1_out, and_2_out, and_3_out, and_4_out, and_5_out, and_6_out, and_7_out, and_8_out, and_9_out,
       and_10_out, and_11_out, and_12_out, and_13_out, and_14_out, and_15_out, and_16_out, and_18_out,
       and_19_out, and_20_out, and_21_out, and_22_out, and_23_out, and_24_out,
       bit16_cache_cell_1_search_match_non_buffered, bit16_cache_cell_2_search_match_non_buffered,
       bit16_cache_cell_3_search_match_non_buffered, bit16_cache_cell_4_search_match_non_buffered,
       bit16_cache_cell_5_search_match_non_buffered, bit16_cache_cell_6_search_match_non_buffered,
       bit16_cache_cell_7_search_match_non_buffered, bit16_cache_cell_8_search_match_non_buffered,
       Bumping_Index, comparator_1_eq, comparator_2_eq, comparator_3_eq, comparator_4_eq, comparator_5_eq,
       comparator_6_eq, comparator_7_eq, decoder_1_out0, decoder_1_out1, decoder_1_out2, decoder_1_out3,
       decoder_1_out4, decoder_1_out5, decoder_1_out6, decoder_1_out7, nor_1_out, not_1_out, not_2_out,
       or_1_out, or_3_out, or_4_out, or_5_out, or_6_out, or_7_out, or_8_out, or_9_out;
  wire [2:0] Index_To_Bump;
  wire [3:0] Bit4_Least_Recently_Used_Cell, bit_extender_1_out, controlled_buffer_3_out,
       controlled_buffer_4_out, controlled_buffer_5_out, controlled_buffer_6_out, controlled_buffer_7_out,
       controlled_buffer_8_out, controlled_buffer_9_out, register_1_q, register_2_q, register_3_q,
       register_4_q, register_5_q, register_6_q, register_7_q;
  wire [15:0] controlled_buffer_1_out;
  wire [15:15] or_2_out;

  or or_1 (or_1_out, Reset_Cell, Set_Cell);
  assign controlled_buffer_1_out = or_2_out[15] ? {or_2_out[15], {15{1'b0}}} : 16'bz;  // Controlled_Buffer controlled_buffer_1
  not not_1 (not_1_out, or_2_out[15]);
  or or_2 (or_2_out[15], Reset_Cell, Reset_Buffer);
  assign controlled_buffer_1_out = not_1_out ? Bit16_Key_Data : 16'bz;  // Controlled_Buffer controlled_buffer_2
  Decoder #(.select(3)) decoder_1 (
    .out0(decoder_1_out0), .out1(decoder_1_out1), .out2(decoder_1_out2), .out3(decoder_1_out3),
    .out4(decoder_1_out4), .out5(decoder_1_out5), .out6(decoder_1_out6), .out7(decoder_1_out7),
    .sel(Bit3_Cell_Index), .en(or_1_out));
  nor nor_1 (nor_1_out, Search_Enable, Reset_Cell);
  and and_1 (and_1_out, Set_Cell, decoder_1_out7);
  and and_2 (and_2_out, decoder_1_out7, Reset_Cell);
  and and_3 (and_3_out, Set_Cell, decoder_1_out6);
  and and_4 (and_4_out, decoder_1_out6, Reset_Cell);
  and and_5 (and_5_out, Set_Cell, decoder_1_out5);
  and and_6 (and_6_out, decoder_1_out5, Reset_Cell);
  and and_7 (and_7_out, Set_Cell, decoder_1_out4);
  and and_8 (and_8_out, decoder_1_out4, Reset_Cell);
  and and_9 (and_9_out, Set_Cell, decoder_1_out3);
  and and_10 (and_10_out, decoder_1_out3, Reset_Cell);
  and and_11 (and_11_out, Set_Cell, decoder_1_out2);
  and and_12 (and_12_out, decoder_1_out2, Reset_Cell);
  and and_13 (and_13_out, Set_Cell, decoder_1_out1);
  and and_14 (and_14_out, decoder_1_out1, Reset_Cell);
  and and_15 (and_15_out, Set_Cell, decoder_1_out0);
  and and_16 (and_16_out, decoder_1_out0, Reset_Cell);
  Pull_Resistor pull_resistor_1 (.node(controlled_buffer_1_out));
  Bit16_Cache_Cell bit16_cache_cell_1 (
    .Bit16_Key_Data(controlled_buffer_1_out), .Bit16_Value_Data(Bit16_Value_Data),
    .Bit16_Search_Key(Bit16_Search_Key), .NOT_Search_Enable(nor_1_out), .Set_Cell(and_1_out),
    .Reset_Cell(and_2_out), .Clock(Clock), .Force_Reset(Reset_Buffer), .Bit16_Value_Bus(Bit16_Value),
    .Search_Match(Key_In_Cache), .Search_Match_Non_Buffered(bit16_cache_cell_1_search_match_non_buffered));
  Bit16_Cache_Cell bit16_cache_cell_2 (
    .Bit16_Key_Data(controlled_buffer_1_out), .Bit16_Value_Data(Bit16_Value_Data),
    .Bit16_Search_Key(Bit16_Search_Key), .NOT_Search_Enable(nor_1_out), .Set_Cell(and_3_out),
    .Reset_Cell(and_4_out), .Clock(Clock), .Force_Reset(Reset_Buffer), .Bit16_Value_Bus(Bit16_Value),
    .Search_Match(Key_In_Cache), .Search_Match_Non_Buffered(bit16_cache_cell_2_search_match_non_buffered));
  Bit16_Cache_Cell bit16_cache_cell_3 (
    .Bit16_Key_Data(controlled_buffer_1_out), .Bit16_Value_Data(Bit16_Value_Data),
    .Bit16_Search_Key(Bit16_Search_Key), .NOT_Search_Enable(nor_1_out), .Set_Cell(and_5_out),
    .Reset_Cell(and_6_out), .Clock(Clock), .Force_Reset(Reset_Buffer), .Bit16_Value_Bus(Bit16_Value),
    .Search_Match(Key_In_Cache), .Search_Match_Non_Buffered(bit16_cache_cell_3_search_match_non_buffered));
  Bit16_Cache_Cell bit16_cache_cell_4 (
    .Bit16_Key_Data(controlled_buffer_1_out), .Bit16_Value_Data(Bit16_Value_Data),
    .Bit16_Search_Key(Bit16_Search_Key), .NOT_Search_Enable(nor_1_out), .Set_Cell(and_7_out),
    .Reset_Cell(and_8_out), .Clock(Clock), .Force_Reset(Reset_Buffer), .Bit16_Value_Bus(Bit16_Value),
    .Search_Match(Key_In_Cache), .Search_Match_Non_Buffered(bit16_cache_cell_4_search_match_non_buffered));
  Bit16_Cache_Cell bit16_cache_cell_5 (
    .Bit16_Key_Data(controlled_buffer_1_out), .Bit16_Value_Data(Bit16_Value_Data),
    .Bit16_Search_Key(Bit16_Search_Key), .NOT_Search_Enable(nor_1_out), .Set_Cell(and_9_out),
    .Reset_Cell(and_10_out), .Clock(Clock), .Force_Reset(Reset_Buffer), .Bit16_Value_Bus(Bit16_Value),
    .Search_Match(Key_In_Cache), .Search_Match_Non_Buffered(bit16_cache_cell_5_search_match_non_buffered));
  Bit16_Cache_Cell bit16_cache_cell_6 (
    .Bit16_Key_Data(controlled_buffer_1_out), .Bit16_Value_Data(Bit16_Value_Data),
    .Bit16_Search_Key(Bit16_Search_Key), .NOT_Search_Enable(nor_1_out), .Set_Cell(and_11_out),
    .Reset_Cell(and_12_out), .Clock(Clock), .Force_Reset(Reset_Buffer), .Bit16_Value_Bus(Bit16_Value),
    .Search_Match(Key_In_Cache), .Search_Match_Non_Buffered(bit16_cache_cell_6_search_match_non_buffered));
  Bit16_Cache_Cell bit16_cache_cell_7 (
    .Bit16_Key_Data(controlled_buffer_1_out), .Bit16_Value_Data(Bit16_Value_Data),
    .Bit16_Search_Key(Bit16_Search_Key), .NOT_Search_Enable(nor_1_out), .Set_Cell(and_13_out),
    .Reset_Cell(and_14_out), .Clock(Clock), .Force_Reset(Reset_Buffer), .Bit16_Value_Bus(Bit16_Value),
    .Search_Match(Key_In_Cache), .Search_Match_Non_Buffered(bit16_cache_cell_7_search_match_non_buffered));
  Bit16_Cache_Cell bit16_cache_cell_8 (
    .Bit16_Key_Data(controlled_buffer_1_out), .Bit16_Value_Data(Bit16_Value_Data),
    .Bit16_Search_Key(Bit16_Search_Key), .NOT_Search_Enable(nor_1_out), .Set_Cell(and_15_out),
    .Reset_Cell(and_16_out), .Clock(Clock), .Force_Reset(Reset_Buffer), .Bit16_Value_Bus(Bit16_Value),
    .Search_Match(Key_In_Cache), .Search_Match_Non_Buffered(bit16_cache_cell_8_search_match_non_buffered));
  Pull_Resistor pull_resistor_2 (.node(Bit16_Value));
  Pull_Resistor pull_resistor_3 (.node(Key_In_Cache));
  and and_17 (Cache_Miss, ~Key_In_Cache, Search_Enable);  // AND_Gate
  Pull_Resistor pull_resistor_4 (.node(Index_To_Bump));
  Priority_Encoder priority_encoder_1 (
    .in0(bit16_cache_cell_8_search_match_non_buffered), .in1(bit16_cache_cell_7_search_match_non_buffered),
    .in2(bit16_cache_cell_6_search_match_non_buffered), .in3(bit16_cache_cell_5_search_match_non_buffered),
    .in4(bit16_cache_cell_4_search_match_non_buffered), .in5(bit16_cache_cell_3_search_match_non_buffered),
    .in6(bit16_cache_cell_2_search_match_non_buffered), .in7(bit16_cache_cell_1_search_match_non_buffered),
    .out(Index_To_Bump), .en_in(Enable));
  assign controlled_buffer_3_out = Reset_Buffer ? {3'b000, Reset_Buffer} : 4'bz;  // Controlled_Buffer controlled_buffer_3
  assign controlled_buffer_4_out = Reset_Buffer ? {2'b00, Reset_Buffer, 1'b0} : 4'bz;  // Controlled_Buffer controlled_buffer_4
  assign controlled_buffer_5_out = Reset_Buffer ? {2'b00, {2{Reset_Buffer}}} : 4'bz;  // Controlled_Buffer controlled_buffer_5
  assign controlled_buffer_6_out = Reset_Buffer ? {1'b0, Reset_Buffer, 2'b00} : 4'bz;  // Controlled_Buffer controlled_buffer_6
  assign controlled_buffer_7_out = Reset_Buffer ? {1'b0, Reset_Buffer, 1'b0, Reset_Buffer} : 4'bz;  // Controlled_Buffer controlled_buffer_7
  assign controlled_buffer_8_out = Reset_Buffer ? {1'b0, {2{Reset_Buffer}}, 1'b0} : 4'bz;  // Controlled_Buffer controlled_buffer_8
  assign controlled_buffer_9_out = Reset_Buffer ? {1'b0, {3{Reset_Buffer}}} : 4'bz;  // Controlled_Buffer controlled_buffer_9
  assign bit_extender_1_out = {{1{1'b0}}, Index_To_Bump};  // Bit_Extender bit_extender_1
  or or_3 (or_3_out, Reset_Buffer, Bumping_Index);
  or or_4 (or_4_out, comparator_7_eq, comparator_6_eq, comparator_5_eq, comparator_1_eq, comparator_4_eq, comparator_3_eq, comparator_2_eq);
  and and_18 (and_18_out, or_4_out, or_3_out);
  or or_5 (or_5_out, comparator_2_eq, comparator_3_eq, comparator_4_eq, comparator_6_eq, comparator_7_eq, comparator_5_eq);
  and and_19 (and_19_out, or_5_out, or_3_out);
  or or_6 (or_6_out, comparator_4_eq, comparator_5_eq, comparator_3_eq, comparator_6_eq, comparator_7_eq);
  and and_20 (and_20_out, or_6_out, or_3_out);
  or or_7 (or_7_out, comparator_6_eq, comparator_5_eq, comparator_7_eq, comparator_4_eq);
  and and_21 (and_21_out, or_7_out, or_3_out);
  or or_8 (or_8_out, comparator_6_eq, comparator_5_eq, comparator_7_eq);
  and and_22 (and_22_out, or_8_out, or_3_out);
  or or_9 (or_9_out, comparator_6_eq, comparator_7_eq);
  and and_23 (and_23_out, or_9_out, or_3_out);
  and and_24 (and_24_out, comparator_7_eq, or_3_out);
  not not_2 (not_2_out, Reset_Buffer);
  Register #(.width(4)) register_1 (.D(bit_extender_1_out), .en(or_3_out), .clk(Clock), .Q(register_1_q));  // open: clr
  Register #(.width(4)) register_2 (
    .D(controlled_buffer_3_out), .en(and_18_out), .clk(Clock), .Q(register_2_q));  // open: clr
  Register #(.width(4)) register_3 (
    .D(controlled_buffer_4_out), .en(and_19_out), .clk(Clock), .Q(register_3_q));  // open: clr
  Register #(.width(4)) register_4 (
    .D(controlled_buffer_5_out), .en(and_20_out), .clk(Clock), .Q(register_4_q));  // open: clr
  Register #(.width(4)) register_5 (
    .D(controlled_buffer_6_out), .en(and_21_out), .clk(Clock), .Q(register_5_q));  // open: clr
  Register #(.width(4)) register_6 (
    .D(controlled_buffer_7_out), .en(and_22_out), .clk(Clock), .Q(register_6_q));  // open: clr
  Register #(.width(4)) register_7 (
    .D(controlled_buffer_8_out), .en(and_23_out), .clk(Clock), .Q(register_7_q));  // open: clr
  Register #(.width(4)) register_8 (
    .D(controlled_buffer_9_out), .en(and_24_out), .clk(Clock), .Q(Bit4_Least_Recently_Used_Cell));  // open: clr
  assign controlled_buffer_3_out = not_2_out ? register_1_q : 4'bz;  // Controlled_Buffer controlled_buffer_10
  assign controlled_buffer_4_out = not_2_out ? register_2_q : 4'bz;  // Controlled_Buffer controlled_buffer_11
  assign controlled_buffer_5_out = not_2_out ? register_3_q : 4'bz;  // Controlled_Buffer controlled_buffer_12
  assign controlled_buffer_6_out = not_2_out ? register_4_q : 4'bz;  // Controlled_Buffer controlled_buffer_13
  assign controlled_buffer_7_out = not_2_out ? register_5_q : 4'bz;  // Controlled_Buffer controlled_buffer_14
  assign controlled_buffer_8_out = not_2_out ? register_6_q : 4'bz;  // Controlled_Buffer controlled_buffer_15
  assign controlled_buffer_9_out = not_2_out ? register_7_q : 4'bz;  // Controlled_Buffer controlled_buffer_16
  Comparator #(.mode("unsigned"), .width(4)) comparator_1 (
    .a(bit_extender_1_out), .b(register_2_q), .eq(comparator_1_eq));  // open: gt, lt
  Comparator #(.mode("unsigned"), .width(4)) comparator_2 (
    .a(bit_extender_1_out), .b(register_3_q), .eq(comparator_2_eq));  // open: gt, lt
  Comparator #(.mode("unsigned"), .width(4)) comparator_3 (
    .a(bit_extender_1_out), .b(register_4_q), .eq(comparator_3_eq));  // open: gt, lt
  Comparator #(.mode("unsigned"), .width(4)) comparator_4 (
    .a(bit_extender_1_out), .b(register_5_q), .eq(comparator_4_eq));  // open: gt, lt
  Comparator #(.mode("unsigned"), .width(4)) comparator_5 (
    .a(bit_extender_1_out), .b(register_6_q), .eq(comparator_5_eq));  // open: gt, lt
  Comparator #(.mode("unsigned"), .width(4)) comparator_6 (
    .a(bit_extender_1_out), .b(register_7_q), .eq(comparator_6_eq));  // open: gt, lt
  Comparator #(.mode("unsigned"), .width(4)) comparator_7 (
    .a(bit_extender_1_out), .b(Bit4_Least_Recently_Used_Cell), .eq(comparator_7_eq));  // open: gt, lt
  Bit_Extender #(.in_width(4), .out_width(3), .\type ("zero")) bit_extender_2 (
    .in(Bit4_Least_Recently_Used_Cell), .out(Bit3_Least_Recently_Used_Cell));

  // Other names for the same wires on the sheet: Reset = Reset_Buffer

  // Notes on the sheet:
  //   write by search enable and set  cell high
  //   reset by search and reset cell
endmodule

module MMU (
  input  Two_Byte_Operation_In,
  input  [26:0] Bit27_Virtual_Address,
  input  [7:0] Bit8_Context_Id,
  input  [15:0] Bit16_From_Memory,
  input  Deallocate_Page,
  input  Allocate_Page,
  input  Translate_Operation,
  input  Clock,
  input  Enable,
  input  Reset,
  output Automated_Read_Enable,
  output Automated_Write_Enable,
  output [26:0] Bit27_Memory_Address,
  output Two_Byte_Operation,
  output Stall_Core,
  output [15:0] Bit16_Memory_Write_Bus
);

  wire A_STG_1, A_STG_2, A_STG_3, A_STG_4, adder_1_cout, adder_2_cout, and_1_out, and_2_out, and_4_out,
       Cache_Hit, Cache_Miss, comparator_1_eq, comparator_1_lt, Current_Context_Number_Pages_Allocated_carry,
       D_STG_1, D_STG_2, D_STG_3, D_STG_4, Deallocated_Page_Available, demultiplexer_1_out0,
       demultiplexer_1_out1, demultiplexer_1_out2, demultiplexer_1_out3, NO_Deallocated_Page_Available,
       not_1_out, not_2_out, not_3_out, or_1_out, or_2_out, or_3_out, or_4_out, or_5_out, or_6_out, or_7_out,
       or_8_out, or_9_out, or_11_out, or_14_out, or_15_out, or_16_out, or_17_out, Out_Of_Bounds_Access,
       Out_Of_Bounds_Page_Index_q, Resolving_Cache_Miss, T_STG_1, T_STG_2, T_STG_3, T_STG_4;
  wire [1:0] Internal_Operation_Stage_q;
  wire [2:0] translation_lookaside_buffer_1_bit3_least_recently_used_cell;
  wire [3:0] controlled_buffer_3_out;
  wire [11:1] Virtual_Page_Translation_Address;
  wire [11:11] bit12_add_one_1_bit12_out;
  wire [14:14] bit15_add_one_2_bit15_out;
  wire [15:0] controlled_buffer_1_out, Current_Context_Number_Pages_Allocated, Highest_Unassigned_Page,
       Last_Freed_Page, Next_Free_Page, Page_Holding_Translation, Physical_Page_To_Be_Freed, Translated_Page;
  wire [26:0] Deallocated_Page_Table_Base_Address, Page_Index_Table_Base_Offset, Page_Translation_Table_Index;
  wire [26:1] Deallocated_Page_Table_Write_Address;
  wire [26:13] Context_Id_Max_Page_Address;

  Comparator #(.mode("unsigned"), .width(16)) comparator_1 (
    .a(Current_Context_Number_Pages_Allocated), .b({1'b0, Bit27_Virtual_Address[26:12]}),
    .eq(comparator_1_eq), .lt(comparator_1_lt));  // open: gt
  or or_1 (or_1_out, T_STG_2, D_STG_2, A_STG_1);
  Register #(.width(1)) Out_Of_Bounds_Page_Index (
    .D(or_2_out), .en(T_STG_1), .clk(Clock), .Q(Out_Of_Bounds_Page_Index_q), .clr(Reset));
  or or_2 (or_2_out, comparator_1_eq, comparator_1_lt);
  Register #(.width(16)) u_Page_Holding_Translation (
    .D(Bit16_From_Memory), .en(or_1_out), .clk(Clock), .Q(Page_Holding_Translation), .clr(Reset));
  Register #(.width(16)) u_Physical_Page_To_Be_Freed (
    .D(Bit16_From_Memory), .en(D_STG_3), .clk(Clock), .Q(Physical_Page_To_Be_Freed), .clr(Reset));
  or or_3 (or_3_out, Translate_Operation, Deallocate_Page);
  or or_4 (or_4_out, A_STG_3, D_STG_1);
  and and_1 (and_1_out, NO_Deallocated_Page_Available, A_STG_4);
  and and_2 (and_2_out, Deallocated_Page_Available, A_STG_4);
  and and_3 (Out_Of_Bounds_Access, Out_Of_Bounds_Page_Index_q, Cache_Miss);
  Counter #(.max('hffff), .width(16)) u_Current_Context_Number_Pages_Allocated (
    .clr(Reset), .up(Allocate_Page), .count(or_4_out), .clk(Clock), .D(Bit16_From_Memory),
    .carry(Current_Context_Number_Pages_Allocated_carry), .Q(Current_Context_Number_Pages_Allocated));  // open: load
  Counter #(.max('hffff), .width(16)) u_Highest_Unassigned_Page (
    .load(Reset), .up(and_1_out), .count(and_1_out), .clk(Clock), .D(16'h13), .Q(Highest_Unassigned_Page));  // open: clr, carry
  assign controlled_buffer_1_out = A_STG_4 ? Bit16_From_Memory : 16'bz;  // Controlled_Buffer controlled_buffer_1
  assign controlled_buffer_1_out = D_STG_4 ? Physical_Page_To_Be_Freed : 16'bz;  // Controlled_Buffer controlled_buffer_2
  or or_5 (or_5_out, D_STG_4, and_2_out);
  Register #(.width(27)) register_1 (
    .D({27{1'b0}}), .en(Reset), .clk(Clock), .Q(Page_Index_Table_Base_Offset), .clr(not_1_out));
  not not_1 (not_1_out, Enable);
  Register #(.width(27)) u_Deallocated_Page_Table_Base_Address (
    .D(27'h2200), .en(Reset), .clk(Clock), .Q(Deallocated_Page_Table_Base_Address), .clr(not_2_out));
  not not_2 (not_2_out, Enable);
  Register #(.width(16)) u_Last_Freed_Page (
    .D(controlled_buffer_1_out), .en(or_5_out), .clk(Clock), .Q(Last_Freed_Page), .clr(Reset));
  Translation_Lookaside_Buffer translation_lookaside_buffer_1 (
    .Bit16_Key_Data({1'b0, Bit27_Virtual_Address[26:12]}), .Bit16_Value_Data(Bit16_From_Memory),
    .Bit16_Search_Key({1'b0, Bit27_Virtual_Address[26:12]}), .Search_Enable(or_3_out), .Set_Cell(T_STG_3),
    .Reset_Cell(Deallocate_Page),
    .Bit3_Cell_Index(translation_lookaside_buffer_1_bit3_least_recently_used_cell), .Clock(Clock),
    .Enable(Enable), .Reset_Buffer(Reset),
    .Bit3_Least_Recently_Used_Cell(translation_lookaside_buffer_1_bit3_least_recently_used_cell),
    .Key_In_Cache(Cache_Hit), .Bit16_Value(Translated_Page), .Cache_Miss(Cache_Miss));
  not not_3 (not_3_out, Resolving_Cache_Miss);
  and and_4 (and_4_out, not_3_out, Translate_Operation);
  // Probe on Cache_Hit
  Register #(.width(1)) register_2 (.D(Cache_Miss), .en(or_6_out), .clk(Clock), .Q(Resolving_Cache_Miss), .clr(Reset));
  or or_6 (or_6_out, not_3_out, T_STG_4);
  Counter #(.max('h3), .trigger("falling"), .width(2)) Internal_Operation_Stage (
    .clr(or_7_out), .up(or_8_out), .count(or_8_out), .clk(Clock), .Q(Internal_Operation_Stage_q));  // open: load, D, carry
  or or_7 (or_7_out, and_4_out, Reset);
  or or_8 (or_8_out, Allocate_Page, Deallocate_Page, Resolving_Cache_Miss, Cache_Miss);
  Demultiplexer #(.select(2)) demultiplexer_1 (
    .out0(demultiplexer_1_out0), .out1(demultiplexer_1_out1), .out2(demultiplexer_1_out2),
    .out3(demultiplexer_1_out3), .in(or_8_out), .sel(Internal_Operation_Stage_q));
  RAM #(.addrWidth(4), .dataWidth(16)) Page_Translation_Table (.addr(Bit27_Virtual_Address[26:23]));  // open: we, oe, clk, din, dout
  and and_5 (T_STG_1, demultiplexer_1_out0, Translate_Operation);
  and and_6 (T_STG_2, demultiplexer_1_out1, Translate_Operation);
  and and_7 (T_STG_3, demultiplexer_1_out2, Translate_Operation);
  and and_8 (T_STG_4, demultiplexer_1_out3, Translate_Operation);
  and and_9 (D_STG_1, demultiplexer_1_out0, Deallocate_Page);
  and and_10 (D_STG_2, demultiplexer_1_out1, Deallocate_Page);
  and and_11 (D_STG_3, demultiplexer_1_out2, Deallocate_Page);
  and and_12 (D_STG_4, demultiplexer_1_out3, Deallocate_Page);
  assign controlled_buffer_3_out = T_STG_1 ? Bit27_Virtual_Address[26:23] : 4'bz;  // Controlled_Buffer controlled_buffer_3
  assign controlled_buffer_3_out = or_9_out ? Current_Context_Number_Pages_Allocated[14:11] : 4'bz;  // Controlled_Buffer controlled_buffer_4
  or or_9 (or_9_out, D_STG_2, A_STG_1);
  and and_13 (A_STG_1, demultiplexer_1_out0, Allocate_Page);
  Pull_Resistor pull_resistor_1 (.node(controlled_buffer_3_out));
  and and_14 (A_STG_2, demultiplexer_1_out1, Allocate_Page);
  and and_15 (A_STG_3, demultiplexer_1_out2, Allocate_Page);
  Adder #(.width(15)) adder_1 (
    .a(Last_Freed_Page[14:0]), .b(Deallocated_Page_Table_Base_Address[14:0]),
    .out(Deallocated_Page_Table_Write_Address[15:1]), .cout(adder_1_cout));  // open: cin
  and and_16 (A_STG_4, demultiplexer_1_out3, Allocate_Page);
  Adder #(.width(12)) adder_2 (
    .a({Bit8_Context_Id, controlled_buffer_3_out}), .b(Page_Index_Table_Base_Offset[11:0]),
    .out(Page_Translation_Table_Index[11:0]), .cout(adder_2_cout));  // open: cin
  or or_10 (Deallocated_Page_Available, Last_Freed_Page[7], Last_Freed_Page[0], Last_Freed_Page[1], Last_Freed_Page[2], Last_Freed_Page[3], Last_Freed_Page[4], Last_Freed_Page[5], Last_Freed_Page[6], Last_Freed_Page[8], Last_Freed_Page[9], Last_Freed_Page[10], Last_Freed_Page[11], Last_Freed_Page[12], Last_Freed_Page[13], Last_Freed_Page[14], Last_Freed_Page[15]);
  Bit15_Add_One bit15_add_one_1 (
    .Add_One(adder_2_cout), .Bit15_In(Page_Index_Table_Base_Offset[26:12]),
    .Bit15_Out(Page_Translation_Table_Index[26:12]));  // open: Carry_Out
  assign Virtual_Page_Translation_Address = T_STG_3 ? Bit27_Virtual_Address[22:12] : 11'bz;  // Controlled_Buffer controlled_buffer_5
  assign Virtual_Page_Translation_Address = or_11_out ? Current_Context_Number_Pages_Allocated[10:0] : 11'bz;  // Controlled_Buffer controlled_buffer_6
  or or_11 (or_11_out, D_STG_3, A_STG_2);
  Bit12_Add_One bit12_add_one_1 (
    .Add_One(adder_1_cout), .Bit12_In(Deallocated_Page_Table_Base_Address[26:15]),
    .Bit12_Out({bit12_add_one_1_bit12_out[11], Deallocated_Page_Table_Write_Address[26:16]}));  // open: Carry_Out
  Pull_Resistor pull_resistor_2 (.node(Virtual_Page_Translation_Address));
  buf or_12 (Stall_Core, Resolving_Cache_Miss);  // OR_Gate
  Bit15_Add_One bit15_add_one_2 (
    .Add_One(Enable), .Bit15_In(Page_Translation_Table_Index[26:12]),
    .Bit15_Out({bit15_add_one_2_bit15_out[14], Context_Id_Max_Page_Address}));  // open: Carry_Out
  not not_4 (NO_Deallocated_Page_Available, Deallocated_Page_Available);
  assign Next_Free_Page = NO_Deallocated_Page_Available ? Highest_Unassigned_Page : 16'bz;  // Controlled_Buffer controlled_buffer_7
  assign Next_Free_Page = Deallocated_Page_Available ? Last_Freed_Page : 16'bz;  // Controlled_Buffer controlled_buffer_8
  or or_13 (Two_Byte_Operation, Cache_Miss, Two_Byte_Operation_In);
  // Probe on {Context_Id_Max_Page_Address, {5{1'b0}}, Bit8_Context_Id}
  // Probe on {Context_Id_Max_Page_Address, {5{1'b0}}, Bit8_Context_Id}
  assign Bit27_Memory_Address = Cache_Hit ? {Translated_Page[14:0], Bit27_Virtual_Address[11:0]} : 27'bz;  // Controlled_Buffer controlled_buffer_9
  or or_14 (or_14_out, D_STG_1, T_STG_1);
  assign Bit27_Memory_Address = or_14_out ? {Context_Id_Max_Page_Address, {5{1'b0}}, Bit8_Context_Id} : 27'bz;  // Controlled_Buffer controlled_buffer_10
  or or_15 (or_15_out, A_STG_1, D_STG_2, T_STG_2);
  assign Bit27_Memory_Address = or_15_out ? Page_Translation_Table_Index : 27'bz;  // Controlled_Buffer controlled_buffer_11
  or or_16 (or_16_out, A_STG_2, T_STG_3);
  assign Bit27_Memory_Address = or_16_out ? {Page_Holding_Translation[14:0], Virtual_Page_Translation_Address, 1'b0} : 27'bz;  // Controlled_Buffer controlled_buffer_12
  assign Bit27_Memory_Address = or_17_out ? {Deallocated_Page_Table_Write_Address, 1'b0} : 27'bz;  // Controlled_Buffer controlled_buffer_13
  or or_17 (or_17_out, D_STG_4, A_STG_4);
  assign Bit16_Memory_Write_Bus = D_STG_4 ? Last_Freed_Page : 16'bz;  // Controlled_Buffer controlled_buffer_14
  assign Bit16_Memory_Write_Bus = A_STG_2 ? Next_Free_Page : 16'bz;  // Controlled_Buffer controlled_buffer_15
  Pull_Resistor pull_resistor_3 (.node(Bit27_Memory_Address));
  Pull_Resistor pull_resistor_4 (.node(Bit16_Memory_Write_Bus));
  or or_18 (Automated_Read_Enable, or_14_out, or_15_out, T_STG_3);
  or or_19 (Automated_Write_Enable, A_STG_2, D_STG_4);

  // Other names for the same wires on the sheet: Context_Id[7:0] = Bit8_Context_Id;
  //   Context_Id_Max_Page_Address[7:0] = Bit8_Context_Id; From_Memory[15:0] = Bit16_From_Memory;
  //   Virtual_Page_Translation_Address[26:12] = Page_Holding_Translation[14:0];
  //   Page_Offset[11:0] = Bit27_Virtual_Address[11:0]; Virtual_Page_Index[14:0] = Bit27_Virtual_Address[26:12]

  // Notes on the sheet:
  //   Mem pull max page alloc
  //   page index table base address
  //   only 15 bit of page adr
  //   only 15 bit of page adr
endmodule

module Bit15_Add_One (
  input  Add_One,
  input  [14:0] Bit15_In,
  output [14:0] Bit15_Out,
  output Carry_Out
);

  wire and_1_out, and_2_out, and_3_out, and_4_out, and_5_out, and_6_out, and_7_out, and_8_out, and_9_out,
       and_10_out, and_11_out, and_12_out, and_13_out, and_14_out;

  and and_1 (and_1_out, Add_One, Bit15_In[0]);
  and and_2 (and_2_out, Add_One, Bit15_In[0], Bit15_In[1]);
  and and_3 (and_3_out, Add_One, Bit15_In[0], Bit15_In[1], Bit15_In[2]);
  and and_4 (and_4_out, Add_One, Bit15_In[0], Bit15_In[1], Bit15_In[2], Bit15_In[3]);
  and and_5 (and_5_out, Add_One, Bit15_In[0], Bit15_In[1], Bit15_In[2], Bit15_In[3], Bit15_In[4]);
  and and_6 (and_6_out, Add_One, Bit15_In[0], Bit15_In[1], Bit15_In[2], Bit15_In[3], Bit15_In[4], Bit15_In[5]);
  and and_7 (and_7_out, Add_One, Bit15_In[0], Bit15_In[1], Bit15_In[2], Bit15_In[3], Bit15_In[4], Bit15_In[5], Bit15_In[6]);
  and and_8 (and_8_out, Add_One, Bit15_In[0], Bit15_In[1], Bit15_In[2], Bit15_In[3], Bit15_In[4], Bit15_In[5], Bit15_In[6], Bit15_In[7]);
  and and_9 (and_9_out, Add_One, Bit15_In[0], Bit15_In[1], Bit15_In[2], Bit15_In[3], Bit15_In[4], Bit15_In[5], Bit15_In[6], Bit15_In[7], Bit15_In[8]);
  and and_10 (and_10_out, Add_One, Bit15_In[0], Bit15_In[1], Bit15_In[2], Bit15_In[3], Bit15_In[4], Bit15_In[5], Bit15_In[6], Bit15_In[7], Bit15_In[8], Bit15_In[9]);
  and and_11 (and_11_out, Add_One, Bit15_In[0], Bit15_In[1], Bit15_In[2], Bit15_In[3], Bit15_In[4], Bit15_In[5], Bit15_In[6], Bit15_In[7], Bit15_In[8], Bit15_In[9], Bit15_In[10]);
  and and_12 (and_12_out, Add_One, Bit15_In[0], Bit15_In[1], Bit15_In[2], Bit15_In[3], Bit15_In[4], Bit15_In[5], Bit15_In[6], Bit15_In[7], Bit15_In[8], Bit15_In[9], Bit15_In[10], Bit15_In[11]);
  and and_13 (and_13_out, Add_One, Bit15_In[0], Bit15_In[1], Bit15_In[2], Bit15_In[3], Bit15_In[4], Bit15_In[5], Bit15_In[6], Bit15_In[7], Bit15_In[8], Bit15_In[9], Bit15_In[10], Bit15_In[11], Bit15_In[12]);
  and and_14 (and_14_out, Add_One, Bit15_In[0], Bit15_In[1], Bit15_In[2], Bit15_In[3], Bit15_In[4], Bit15_In[5], Bit15_In[6], Bit15_In[7], Bit15_In[8], Bit15_In[9], Bit15_In[10], Bit15_In[11], Bit15_In[12], Bit15_In[13]);
  and and_15 (Carry_Out, Add_One, Bit15_In[0], Bit15_In[1], Bit15_In[2], Bit15_In[3], Bit15_In[4], Bit15_In[5], Bit15_In[6], Bit15_In[7], Bit15_In[8], Bit15_In[9], Bit15_In[10], Bit15_In[11], Bit15_In[12], Bit15_In[13], Bit15_In[14]);
  xor xor_1 (Bit15_Out[0], Bit15_In[0], Add_One);
  xor xor_2 (Bit15_Out[1], Bit15_In[1], and_1_out);
  xor xor_3 (Bit15_Out[2], Bit15_In[2], and_2_out);
  xor xor_4 (Bit15_Out[3], Bit15_In[3], and_3_out);
  xor xor_5 (Bit15_Out[4], Bit15_In[4], and_4_out);
  xor xor_6 (Bit15_Out[5], Bit15_In[5], and_5_out);
  xor xor_7 (Bit15_Out[6], Bit15_In[6], and_6_out);
  xor xor_8 (Bit15_Out[7], Bit15_In[7], and_7_out);
  xor xor_9 (Bit15_Out[8], Bit15_In[8], and_8_out);
  xor xor_10 (Bit15_Out[9], Bit15_In[9], and_9_out);
  xor xor_11 (Bit15_Out[10], Bit15_In[10], and_10_out);
  xor xor_12 (Bit15_Out[11], Bit15_In[11], and_11_out);
  xor xor_13 (Bit15_Out[12], Bit15_In[12], and_12_out);
  xor xor_14 (Bit15_Out[13], Bit15_In[13], and_13_out);
  xor xor_15 (Bit15_Out[14], Bit15_In[14], and_14_out);
endmodule

module Bit12_Add_One (
  input  Add_One,
  input  [11:0] Bit12_In,
  output [11:0] Bit12_Out,
  output Carry_Out
);

  wire and_1_out, and_2_out, and_3_out, and_4_out, and_5_out, and_6_out, and_7_out, and_8_out, and_9_out,
       and_10_out, and_11_out;

  and and_1 (and_1_out, Add_One, Bit12_In[0]);
  and and_2 (and_2_out, Add_One, Bit12_In[0], Bit12_In[1]);
  and and_3 (and_3_out, Add_One, Bit12_In[0], Bit12_In[1], Bit12_In[2]);
  and and_4 (and_4_out, Add_One, Bit12_In[0], Bit12_In[1], Bit12_In[2], Bit12_In[3]);
  and and_5 (and_5_out, Add_One, Bit12_In[0], Bit12_In[1], Bit12_In[2], Bit12_In[3], Bit12_In[4]);
  and and_6 (and_6_out, Add_One, Bit12_In[0], Bit12_In[1], Bit12_In[2], Bit12_In[3], Bit12_In[4], Bit12_In[5]);
  and and_7 (and_7_out, Add_One, Bit12_In[0], Bit12_In[1], Bit12_In[2], Bit12_In[3], Bit12_In[4], Bit12_In[5], Bit12_In[6]);
  and and_8 (and_8_out, Add_One, Bit12_In[0], Bit12_In[1], Bit12_In[2], Bit12_In[3], Bit12_In[4], Bit12_In[5], Bit12_In[6], Bit12_In[7]);
  and and_9 (and_9_out, Add_One, Bit12_In[0], Bit12_In[1], Bit12_In[2], Bit12_In[3], Bit12_In[4], Bit12_In[5], Bit12_In[6], Bit12_In[7], Bit12_In[8]);
  and and_10 (and_10_out, Add_One, Bit12_In[0], Bit12_In[1], Bit12_In[2], Bit12_In[3], Bit12_In[4], Bit12_In[5], Bit12_In[6], Bit12_In[7], Bit12_In[8], Bit12_In[9]);
  and and_11 (and_11_out, Add_One, Bit12_In[0], Bit12_In[1], Bit12_In[2], Bit12_In[3], Bit12_In[4], Bit12_In[5], Bit12_In[6], Bit12_In[7], Bit12_In[8], Bit12_In[9], Bit12_In[10]);
  and and_12 (Carry_Out, Add_One, Bit12_In[0], Bit12_In[1], Bit12_In[2], Bit12_In[3], Bit12_In[4], Bit12_In[5], Bit12_In[6], Bit12_In[7], Bit12_In[8], Bit12_In[9], Bit12_In[10], Bit12_In[11]);
  xor xor_1 (Bit12_Out[0], Bit12_In[0], Add_One);
  xor xor_2 (Bit12_Out[1], Bit12_In[1], and_1_out);
  xor xor_3 (Bit12_Out[2], Bit12_In[2], and_2_out);
  xor xor_4 (Bit12_Out[3], Bit12_In[3], and_3_out);
  xor xor_5 (Bit12_Out[4], Bit12_In[4], and_4_out);
  xor xor_6 (Bit12_Out[5], Bit12_In[5], and_5_out);
  xor xor_7 (Bit12_Out[6], Bit12_In[6], and_6_out);
  xor xor_8 (Bit12_Out[7], Bit12_In[7], and_7_out);
  xor xor_9 (Bit12_Out[8], Bit12_In[8], and_8_out);
  xor xor_10 (Bit12_Out[9], Bit12_In[9], and_9_out);
  xor xor_11 (Bit12_Out[10], Bit12_In[10], and_10_out);
  xor xor_12 (Bit12_Out[11], Bit12_In[11], and_11_out);
endmodule
module MMU2 (
  input  Passthrough_Instruction,
  input  Passthrough_Data,
  input  Instruction_Read,
  input  Translate_Instruction,
  input  [26:0] Bit27_Instruction_Address_In,
  input  [14:0] Bit15_Target_Page,
  input  Specific_Page_Management,
  input  Data_Write,
  input  Data_Read,
  input  Enable,
  input  Reset,
  input  Clock,
  input  Allocate,
  input  Deallocate,
  input  Translate_Data,
  input  Context_Switch,
  input  Two_Byte_Operation,
  input  [26:0] Bit27_Virtual_Memory_Address,
  input  [7:0] Bit8_Context_Id,
  input  [15:0] Bit16_From_Memory,
  input  [4:0] Bit5_Lower_Flag_Mask,
  input  Lower_Flag_Mask_Enable,
  output [26:0] Bit27_Data_Memory_Address,
  output [15:0] Bit16_Memory_Out,
  output [26:0] Bit27_Instruction_Memory_Address,
  output Auto_Memory_Read_Data,
  output Auto_Memory_Write_Data,
  output Two_Byte_Op,
  output Stall_Core,
  output Memory_Read_Instruction,
  output Out_Of_Pages,
  output Context_Max_Pages_Allocated,
  output Multipage_Virtual_Page_Overflow,
  output Page_Not_Allocated,
  output Translation_Page_Not_Allocated,
  output Fault
);

  wire A1, A_Translation_Page_Table_Was_Cached, AFETCH, AMAIN1, AMAIN2, AMAIN2_3, and_1_out, and_2_out,
       and_3_out, and_4_out, and_5_out, and_7_out, and_9_out, and_10_out, and_11_out, and_12_out, and_13_out,
       and_14_out, and_16_out, and_18_out, and_19_out, and_21_out, and_22_out, and_23_out, and_24_out,
       and_25_out, and_28_out, and_29_out, and_30_out, and_31_out, and_32_out, and_33_out, and_34_out,
       and_35_out, and_36_out, and_37_out, and_38_out, and_41_out, and_42_out, and_43_out, and_44_out,
       and_46_out, and_47_out, and_48_out, and_49_out, and_50_out, and_52_out, and_53_out, and_54_out,
       and_55_out, and_56_out, and_57_out, and_58_out, and_59_out, Context_Max_Pages_Allocated_t,
       Context_Switch_Or_Reset, CT1, CT2, Current_Context_Number_Of_Pages_Lower_10_Are_0,
       Current_Context_Number_Of_Pages_Lower_10_Are_1, D1, d_ff_1_q, d_ff_2_q, d_ff_4_qn, d_ff_6_q, d_ff_7_q,
       d_ff_8_q, d_ff_9_q, d_ff_10_q, d_ff_11_q, Data_Cache_Miss, Data_Key_In_Cache,
       Data_Translate_And_Cache_Miss, Deallocated_Page_Available, demultiplexer_1_out1, demultiplexer_1_out2,
       demultiplexer_1_out3, demultiplexer_1_out4, demultiplexer_2_out0, demultiplexer_2_out1,
       demultiplexer_2_out2, demultiplexer_3_out1, demultiplexer_3_out2, demultiplexer_3_out3,
       demultiplexer_3_out4, demultiplexer_3_out5, demultiplexer_4_out0, demultiplexer_4_out1,
       demultiplexer_4_out2, demultiplexer_4_out3, DMAIN1, DMAIN2, DMAIN3, DSIM1_2ND, DT1, DT2, DT3,
       FE_Internal_Reset, Highest_Allocated_Page_Index_carry, Instruction_Cache_Miss,
       Instruction_Key_In_Cache, Instruction_Translate_And_Cache_Miss, Internal_Reset, IT1, IT2, IT3,
       Last_Freed_Page_Write_Enable, Multi_Page_Translation, Multipage_Virtual_Page_Overflow_t, nand_1_out,
       nand_2_out, No_Deallocated_Page_Available, nor_1_out, nor_2_out, not_1_out, not_2_out, not_3_out,
       not_4_out, not_5_out, or_1_out, or_3_out, or_4_out, or_5_out, or_6_out, or_7_out, or_8_out, or_9_out,
       or_10_out, or_11_out, or_12_out, or_13_out, or_16_out, or_17_out, or_18_out, or_19_out, or_20_out,
       or_22_out, or_24_out, or_25_out, or_26_out, or_29_out, or_32_out, or_36_out, or_37_out, or_38_out,
       or_42_out, OUT_OF_PAGES_t, Page_Not_Allocated_t, T2_Not_Cached, t_ff_1_q,
       T_Translation_Page_Table_Was_Cached, Translation_Page_Not_Allocated_t,
       Virtual_Page_Table_Index_Is_Cached;
  wire [1:0] priority_encoder_1_out, priority_encoder_2_out;
  wire [2:0] bit3_fe_counter_sync_reset_1_value, Instruction_TLB_bit3_least_recently_used_cell,
       priority_encoder_3_out, TLB_LRU;
  wire [3:0] Translation_Page_Index_Table_Address, Virtual_Page_Table_Index;
  wire [7:0] Context_Id;
  wire [12:12] pull_resistor_5_node;
  wire [14:0] bit15_x16_cache_1_bit15_result, bit_extender_1_out, bit_extender_4_out, bit_extender_5_out,
       bit_extender_6_out, bit_extender_11_out, Cached_Virtual_Page_Table_Index, controlled_buffer_4_out,
       controlled_buffer_10_out, Current_Context_Number_Of_Pages, Data_Virtual_Page,
       Highest_Allocated_Page_Index, Virtual_Page;
  wire [15:0] bit_extender_2_out, bit_extender_3_out, bit_extender_7_out, bit_extender_13_out,
       Data_Cache_Value, Deallocation_Internal_Register, Instruction_Cache_Value, Last_Freed_Page,
       multiplexer_3_out, multiplexer_4_out, Next_Free_Id, pull_resistor_3_node, register_2_q,
       Temp_Register_2;
  wire [16:0] Deallocated_Page_Pointer;
  wire [26:0] bit_extender_12_out, bit_extender_14_out, controlled_buffer_13_out, controlled_buffer_15_out,
       controlled_buffer_16_out, Data_Translated_Address;
  wire [26:1] Translation_Address;
  wire [26:12] Instruction_Translated_Address;

  D_Flip_Flop d_ff_1 (.D(CT1), .clk(Clock), .Q(d_ff_1_q));  // open: Qn, preset, reset
  and and_1 (and_1_out, or_1_out, ~Specific_Page_Management);  // AND_Gate
  and and_2 (and_2_out, Specific_Page_Management, or_1_out);
  Multiplexer #(.select(2), .width(4)) multiplexer_1 (
    .in0(Data_Virtual_Page[14:11]), .in1(Bit27_Instruction_Address_In[26:23]),
    .in2(Current_Context_Number_Of_Pages[14:11]), .in3(Bit15_Target_Page[14:11]),
    .out(Translation_Page_Index_Table_Address), .sel(priority_encoder_1_out));
  Priority_Encoder #(.select(2)) priority_encoder_1 (
    .in0(not_1_out), .in1(Instruction_Translate_And_Cache_Miss), .in2(and_1_out), .in3(and_2_out),
    .out(priority_encoder_1_out));
  Register #(.trigger("falling")) register_1 (
    .D(Bit8_Context_Id), .en(d_ff_1_q), .clk(Clock), .Q(Context_Id), .clr(Reset));
  or or_1 (or_1_out, AFETCH, A1, D1);
  not not_1 (not_1_out, or_1_out);
  D_Flip_Flop d_ff_2 (.D(AMAIN2_3), .clk(Clock), .Q(d_ff_2_q), .reset(Context_Switch_Or_Reset));  // open: Qn, preset
  or or_2 (Context_Switch_Or_Reset, Reset, Context_Switch);
  Bit_Extender #(.in_width(16), .out_width(15), .\type ("zero")) bit_extender_1 (
    .in(Temp_Register_2), .out(bit_extender_1_out));
  assign Translation_Address[26:12] = not_2_out ? Cached_Virtual_Page_Table_Index : 15'bz;  // Controlled_Buffer controlled_buffer_1
  not not_2 (not_2_out, DMAIN3);
  assign Translation_Address[26:12] = DMAIN3 ? bit_extender_1_out : 15'bz;  // Controlled_Buffer controlled_buffer_2
  and and_3 (and_3_out, or_3_out, Specific_Page_Management);
  and and_4 (and_4_out, or_3_out, ~Specific_Page_Management);  // AND_Gate
  nor nor_1 (nor_1_out, AMAIN1, DMAIN3);
  or or_3 (or_3_out, AMAIN1, DMAIN3);
  or or_4 (or_4_out, Current_Context_Number_Of_Pages[9], Current_Context_Number_Of_Pages[8], Current_Context_Number_Of_Pages[7], Current_Context_Number_Of_Pages[6], Current_Context_Number_Of_Pages[5], Current_Context_Number_Of_Pages[4], Current_Context_Number_Of_Pages[3], Current_Context_Number_Of_Pages[2], Current_Context_Number_Of_Pages[1], Current_Context_Number_Of_Pages[0]);
  D_Flip_Flop #(.trigger("falling")) d_ff_3 (
    .D(or_4_out), .clk(and_5_out), .Qn(Current_Context_Number_Of_Pages_Lower_10_Are_0),
    .reset(Context_Switch_Or_Reset));  // open: Q, preset
  and and_5 (and_5_out, d_ff_2_q, Clock);
  and and_6 (Multi_Page_Translation, Bit27_Virtual_Memory_Address[0], Bit27_Virtual_Memory_Address[1], Bit27_Virtual_Memory_Address[2], Bit27_Virtual_Memory_Address[3], Bit27_Virtual_Memory_Address[4], Bit27_Virtual_Memory_Address[5], Bit27_Virtual_Memory_Address[6], Bit27_Virtual_Memory_Address[7], Bit27_Virtual_Memory_Address[8], Bit27_Virtual_Memory_Address[9], Bit27_Virtual_Memory_Address[10], Bit27_Virtual_Memory_Address[11], Two_Byte_Operation);
  Adder #(.width(15)) adder_1 (
    .a({15{1'b0}}), .b(Bit27_Virtual_Memory_Address[26:12]), .out(Data_Virtual_Page), .cin(t_ff_1_q),
    .cout(Multipage_Virtual_Page_Overflow_t));
  Multiplexer #(.select(2), .width(11)) multiplexer_2 (
    .in0(Data_Virtual_Page[10:0]), .in1(Bit27_Instruction_Address_In[22:12]),
    .in2(Current_Context_Number_Of_Pages[10:0]), .in3(Bit15_Target_Page[10:0]),
    .out(Translation_Address[11:1]), .sel(priority_encoder_2_out));
  Priority_Encoder #(.select(2)) priority_encoder_2 (
    .in0(nor_1_out), .in1(Instruction_Translate_And_Cache_Miss), .in2(and_4_out), .in3(and_3_out),
    .out(priority_encoder_2_out));
  nor nor_2 (nor_2_out, Current_Context_Number_Of_Pages[9], Current_Context_Number_Of_Pages[8], Current_Context_Number_Of_Pages[7], Current_Context_Number_Of_Pages[6], Current_Context_Number_Of_Pages[5], Current_Context_Number_Of_Pages[4], Current_Context_Number_Of_Pages[3], Current_Context_Number_Of_Pages[2], Current_Context_Number_Of_Pages[1]);
  and and_7 (and_7_out, Internal_Reset, Multi_Page_Translation);
  and and_8 (Current_Context_Number_Of_Pages_Lower_10_Are_1, nor_2_out, Current_Context_Number_Of_Pages[0]);
  T_Flip_Flop #(.trigger("falling")) t_ff_1 (
    .T(and_7_out), .clk(Clock), .Q(t_ff_1_q), .reset(Reset));  // open: Qn, preset
  not not_3 (not_3_out, t_ff_1_q);
  Pull_Resistor pull_resistor_1 (.node(Data_Translated_Address[11:0]));
  assign Data_Translated_Address[11:0] = not_3_out ? Bit27_Virtual_Memory_Address[11:0] : 12'bz;  // Controlled_Buffer controlled_buffer_3
  assign bit_extender_2_out = {{1{1'b0}}, Virtual_Page};  // Bit_Extender bit_extender_2
  assign bit_extender_3_out = {{1{1'b0}}, Bit27_Instruction_Address_In[26:12]};  // Bit_Extender bit_extender_3
  and and_9 (and_9_out, AMAIN1, Last_Freed_Page_Write_Enable);
  Bit_Extender #(.in_width(16), .out_width(15), .\type ("zero")) bit_extender_4 (
    .in({Last_Freed_Page[15:2], Last_Freed_Page[7], Last_Freed_Page[0]}), .out(bit_extender_4_out));
  assign controlled_buffer_4_out = and_9_out ? bit_extender_4_out : 15'bz;  // Controlled_Buffer controlled_buffer_4
  Bit_Extender #(.in_width(16), .out_width(15), .\type ("zero")) bit_extender_5 (
    .in(Bit16_From_Memory), .out(bit_extender_5_out));
  assign controlled_buffer_4_out = not_4_out ? bit_extender_5_out : 15'bz;  // Controlled_Buffer controlled_buffer_5
  not not_4 (not_4_out, and_9_out);
  and and_10 (and_10_out, T_Translation_Page_Table_Was_Cached, IT2);
  and and_11 (and_11_out, ~T_Translation_Page_Table_Was_Cached, IT3);  // AND_Gate
  and and_12 (and_12_out, T_Translation_Page_Table_Was_Cached, DT2);
  and and_13 (and_13_out, ~T_Translation_Page_Table_Was_Cached, DT3);  // AND_Gate
  or or_5 (or_5_out, and_14_out, and_9_out);
  nand nand_1 (nand_1_out, controlled_buffer_4_out[0], controlled_buffer_4_out[1], controlled_buffer_4_out[2], controlled_buffer_4_out[3], controlled_buffer_4_out[4], controlled_buffer_4_out[5], controlled_buffer_4_out[6], controlled_buffer_4_out[7], controlled_buffer_4_out[8], controlled_buffer_4_out[9], controlled_buffer_4_out[10], controlled_buffer_4_out[11], controlled_buffer_4_out[12], controlled_buffer_4_out[13], controlled_buffer_4_out[14]);
  or or_6 (or_6_out, and_10_out, and_11_out);
  or or_7 (or_7_out, and_12_out, and_13_out);
  and and_14 (and_14_out, ~nand_1_out, T2_Not_Cached);  // AND_Gate
  and and_15 (Translation_Page_Not_Allocated_t, nand_1_out, T2_Not_Cached);
  and and_16 (and_16_out, ~and_25_out, AMAIN2_3);  // AND_Gate
  nand nand_2 (nand_2_out, Bit16_From_Memory[0], Bit16_From_Memory[1], Bit16_From_Memory[2], Bit16_From_Memory[3], Bit16_From_Memory[4], Bit16_From_Memory[5], Bit16_From_Memory[6], Bit16_From_Memory[7], Bit16_From_Memory[8], Bit16_From_Memory[9], Bit16_From_Memory[10], Bit16_From_Memory[11], Bit16_From_Memory[12], Bit16_From_Memory[13], Bit16_From_Memory[14]);
  or or_8 (or_8_out, Translate_Instruction, Deallocate);
  or or_9 (or_9_out, and_16_out, DMAIN2);
  and and_17 (Page_Not_Allocated_t, nand_2_out, or_10_out);
  or or_10 (or_10_out, or_6_out, or_7_out);
  and and_18 (and_18_out, ~nand_2_out, or_6_out);  // AND_Gate
  and and_19 (and_19_out, ~nand_2_out, or_7_out);  // AND_Gate
  or or_11 (or_11_out, Deallocate, Translate_Data);
  Multiplexer #(.width(16)) multiplexer_3 (
    .in0(bit_extender_3_out), .in1(Deallocation_Internal_Register), .out(multiplexer_3_out),
    .sel(Translate_Instruction));
  and and_20 (OUT_OF_PAGES_t, Allocate, Highest_Allocated_Page_Index_carry, No_Deallocated_Page_Available);
  and and_21 (and_21_out, AMAIN2, ~No_Deallocated_Page_Available);  // AND_Gate
  and and_22 (and_22_out, or_9_out, ~Specific_Page_Management);  // AND_Gate
  Multiplexer #(.width(16)) multiplexer_4 (
    .in0(bit_extender_7_out), .in1(Deallocation_Internal_Register), .out(multiplexer_4_out), .sel(DSIM1_2ND));
  D_Flip_Flop d_ff_4 (.D(AFETCH), .clk(and_23_out), .Qn(d_ff_4_qn));  // open: Q, preset, reset
  or or_12 (or_12_out, AFETCH, Internal_Reset);
  and and_23 (and_23_out, or_12_out, Clock);
  Counter #(.max('h7fff), .width(15)) u_Highest_Allocated_Page_Index (
    .load(Reset), .up(AMAIN2), .count(and_21_out), .clk(Clock), .D(15'h13),
    .carry(Highest_Allocated_Page_Index_carry), .Q(Highest_Allocated_Page_Index));  // open: clr
  Counter #(.max('h7fff), .width(15)) Current_Context_Number_Pages_Allocated (
    .clr(Reset), .load(Context_Switch), .up(AMAIN2_3), .count(and_22_out), .clk(Clock),
    .D(bit_extender_6_out), .Q(Current_Context_Number_Of_Pages));  // open: carry
  Bit_Extender #(.in_width(16), .out_width(15), .\type ("zero")) bit_extender_6 (
    .in(Bit16_From_Memory), .out(bit_extender_6_out));
  assign bit_extender_7_out = {{1{1'b0}}, Virtual_Page};  // Bit_Extender bit_extender_7
  assign Cached_Virtual_Page_Table_Index = not_5_out ? bit15_x16_cache_1_bit15_result : 15'bz;  // Controlled_Buffer controlled_buffer_6
  Bit15_x16_Cache bit15_x16_cache_1 (
    .Bit4_Query(Virtual_Page_Table_Index), .Bit15_Write_Value(controlled_buffer_4_out),
    .Write_Enable(or_5_out), .Reset_Enable(Clock), .Clock(1'b1), .Query(Context_Switch_Or_Reset),
    .Bit15_Result(bit15_x16_cache_1_bit15_result), .Value_Cached(Virtual_Page_Table_Index_Is_Cached));  // open: Clear
  or or_13 (or_13_out, DT1, IT1);
  and and_24 (and_24_out, or_13_out, Clock);
  Translation_Lookaside_Buffer Data_TLB (
    .Bit16_Key_Data(bit_extender_2_out), .Bit16_Value_Data(Bit16_From_Memory),
    .Bit16_Search_Key(multiplexer_4_out), .Search_Enable(or_11_out), .Set_Cell(and_19_out),
    .Reset_Cell(DSIM1_2ND), .Bit3_Cell_Index(TLB_LRU), .Clock(Clock), .Enable(Enable),
    .Reset_Buffer(Context_Switch_Or_Reset), .Bit3_Least_Recently_Used_Cell(TLB_LRU),
    .Key_In_Cache(Data_Key_In_Cache), .Bit16_Value(Data_Cache_Value), .Cache_Miss(Data_Cache_Miss));
  Translation_Lookaside_Buffer Instruction_TLB (
    .Bit16_Key_Data(bit_extender_3_out), .Bit16_Value_Data(Bit16_From_Memory),
    .Bit16_Search_Key(multiplexer_3_out), .Search_Enable(or_8_out), .Set_Cell(and_18_out),
    .Reset_Cell(DSIM1_2ND), .Bit3_Cell_Index(Instruction_TLB_bit3_least_recently_used_cell), .Clock(Clock),
    .Enable(Enable), .Reset_Buffer(Context_Switch_Or_Reset),
    .Bit3_Least_Recently_Used_Cell(Instruction_TLB_bit3_least_recently_used_cell),
    .Key_In_Cache(Instruction_Key_In_Cache), .Bit16_Value(Instruction_Cache_Value),
    .Cache_Miss(Instruction_Cache_Miss));
  not not_5 (not_5_out, Last_Freed_Page_Write_Enable);
  Pull_Resistor pull_resistor_2 (.node(Cached_Virtual_Page_Table_Index));
  D_Flip_Flop #(.trigger("falling")) d_ff_5 (
    .D(Virtual_Page_Table_Index_Is_Cached), .clk(and_24_out), .Q(T_Translation_Page_Table_Was_Cached),
    .reset(Internal_Reset));  // open: Qn, preset
  and and_25 (and_25_out, Current_Context_Number_Of_Pages[0], Current_Context_Number_Of_Pages[1], Current_Context_Number_Of_Pages[2], Current_Context_Number_Of_Pages[3], Current_Context_Number_Of_Pages[4], Current_Context_Number_Of_Pages[5], Current_Context_Number_Of_Pages[6], Current_Context_Number_Of_Pages[7], Current_Context_Number_Of_Pages[8], Current_Context_Number_Of_Pages[9], Current_Context_Number_Of_Pages[10], Current_Context_Number_Of_Pages[11], Current_Context_Number_Of_Pages[12], Current_Context_Number_Of_Pages[13], Current_Context_Number_Of_Pages[14]);
  and and_26 (A_Translation_Page_Table_Was_Cached, Virtual_Page_Table_Index_Is_Cached, d_ff_4_qn);
  and and_27 (Context_Max_Pages_Allocated_t, and_25_out, Allocate);
  Pull_Resistor pull_resistor_3 (.node(pull_resistor_3_node));
  assign pull_resistor_3_node = AMAIN2 ? {Last_Freed_Page[15:2], Last_Freed_Page[7], Last_Freed_Page[0]} : 16'bz;  // Controlled_Buffer controlled_buffer_7
  assign pull_resistor_3_node = DMAIN1 ? Deallocation_Internal_Register : 16'bz;  // Controlled_Buffer controlled_buffer_8
  or or_14 (Instruction_Translate_And_Cache_Miss, d_ff_6_q, and_28_out);
  and and_28 (and_28_out, Translate_Instruction, ~d_ff_7_q, Instruction_Cache_Miss);  // AND_Gate
  or or_15 (Data_Translate_And_Cache_Miss, d_ff_7_q, and_29_out);
  and and_29 (and_29_out, Translate_Data, ~Instruction_Translate_And_Cache_Miss, Data_Cache_Miss);  // AND_Gate
  Adder #(.width(16)) adder_2 (
    .a(pull_resistor_3_node), .b(16'h2200), .out(Deallocated_Page_Pointer[15:0]),
    .cout(Deallocated_Page_Pointer[16]));  // open: cin
  D_Flip_Flop d_ff_6 (
    .D(Instruction_Translate_And_Cache_Miss), .clk(Clock), .Q(d_ff_6_q), .reset(or_16_out));  // open: Qn, preset
  D_Flip_Flop d_ff_7 (
    .D(Data_Translate_And_Cache_Miss), .clk(Clock), .Q(d_ff_7_q), .reset(or_19_out));  // open: Qn, preset
  and and_30 (and_30_out, T_Translation_Page_Table_Was_Cached, DT2);
  and and_31 (and_31_out, ~T_Translation_Page_Table_Was_Cached, DT3);  // AND_Gate
  and and_32 (and_32_out, T_Translation_Page_Table_Was_Cached, IT2);
  or or_16 (or_16_out, and_32_out, Reset, and_33_out);
  and and_33 (and_33_out, ~T_Translation_Page_Table_Was_Cached, IT3);  // AND_Gate
  or or_17 (or_17_out, AMAIN2, AFETCH, D1, DMAIN3);
  or or_18 (or_18_out, DMAIN1, AMAIN2);
  or or_19 (or_19_out, and_30_out, Reset, and_31_out);
  D_Flip_Flop d_ff_8 (.D(DMAIN2), .clk(Clock), .Q(d_ff_8_q), .reset(Reset));  // open: Qn, preset
  D_Flip_Flop d_ff_9 (.D(or_18_out), .clk(Clock), .Q(d_ff_9_q), .reset(Reset));  // open: Qn, preset
  Register #(.width(16)) Temp_Register_1 (
    .D(Bit16_From_Memory), .en(or_17_out), .clk(Clock), .Q(Deallocation_Internal_Register), .clr(Reset));
  D_Flip_Flop d_ff_10 (.D(AFETCH), .clk(Clock), .Q(d_ff_10_q), .reset(Reset));  // open: Qn, preset
  assign Next_Free_Id = Deallocated_Page_Available ? {Last_Freed_Page[15:2], Last_Freed_Page[7], Last_Freed_Page[0]} : 16'bz;  // Controlled_Buffer controlled_buffer_9
  assign controlled_buffer_10_out = No_Deallocated_Page_Available ? Highest_Allocated_Page_Index : 15'bz;  // Controlled_Buffer controlled_buffer_10
  not not_6 (No_Deallocated_Page_Available, Deallocated_Page_Available);
  assign Next_Free_Id = {{1{1'b0}}, controlled_buffer_10_out};  // Bit_Extender bit_extender_8
  Pull_Resistor pull_resistor_4 (.node(Next_Free_Id));
  Register #(.trigger("falling"), .width(16)) u_Temp_Register_2 (
    .D(Bit16_From_Memory), .en(d_ff_8_q), .clk(Clock), .Q(Temp_Register_2), .clr(Reset));
  Register #(.trigger("falling"), .width(16)) u_Last_Freed_Page (
    .D(Deallocation_Internal_Register), .en(d_ff_9_q), .clk(Clock),
    .Q({Last_Freed_Page[15:2], Last_Freed_Page[7], Last_Freed_Page[0]}), .clr(Reset));
  J_K_Flip_Flop #(.trigger("falling")) j_k_ff_1 (
    .J(d_ff_10_q), .K(d_ff_10_q), .clk(Clock), .Q(Last_Freed_Page_Write_Enable), .reset(Internal_Reset));  // open: Qn, preset
  Register #(.trigger("falling"), .width(16)) register_2 (
    .D(Deallocation_Internal_Register), .en(d_ff_10_q), .clk(Clock), .Q(register_2_q), .clr(Reset));
  Bit_Extender #(.in_width(16), .out_width(15), .\type ("zero")) bit_extender_9 (
    .in(Data_Cache_Value), .out(Data_Translated_Address[26:12]));
  Bit_Extender #(.in_width(16), .out_width(15), .\type ("zero")) bit_extender_10 (
    .in(Instruction_Cache_Value), .out(Instruction_Translated_Address));
  or or_20 (or_20_out, Allocate, Deallocate, Data_Translate_And_Cache_Miss, Instruction_Translate_And_Cache_Miss, Context_Switch);
  or or_21 (Deallocated_Page_Available, Last_Freed_Page[15], Last_Freed_Page[14], Last_Freed_Page[13], Last_Freed_Page[12], Last_Freed_Page[11], Last_Freed_Page[10], Last_Freed_Page[9], Last_Freed_Page[8], Last_Freed_Page[6], Last_Freed_Page[5], Last_Freed_Page[4], Last_Freed_Page[3], Last_Freed_Page[2], Last_Freed_Page[7], Last_Freed_Page[0], Last_Freed_Page[7]);
  Bit_Extender #(.in_width(16), .out_width(15), .\type ("zero")) bit_extender_11 (
    .in(register_2_q), .out(bit_extender_11_out));
  assign Cached_Virtual_Page_Table_Index = Last_Freed_Page_Write_Enable ? bit_extender_11_out : 15'bz;  // Controlled_Buffer controlled_buffer_11
  D_Flip_Flop d_ff_11 (.D(or_22_out), .clk(Clock), .Q(d_ff_11_q), .reset(Reset));  // open: Qn, preset
  or or_22 (or_22_out, IT3, CT2, DSIM1_2ND, AMAIN2_3, DT3, T_Translation_Page_Table_Was_Cached);
  Register #(.trigger("falling"), .width(16)) DEBUG_REG_NEXT_FREE (
    .D(Next_Free_Id), .en(Enable), .clk(Clock), .clr(Reset));  // open: Q
  or or_23 (Internal_Reset, d_ff_11_q, Reset);
  D_Flip_Flop #(.trigger("falling")) d_ff_12 (
    .D(Internal_Reset), .clk(Clock), .Q(FE_Internal_Reset), .reset(Reset));  // open: Qn, preset
  // Probe on bit3_fe_counter_sync_reset_1_value
  Bit3_FE_Counter_Sync_Reset bit3_fe_counter_sync_reset_1 (
    .Reset(Internal_Reset), .Count(or_20_out), .Clock(Clock), .Value(bit3_fe_counter_sync_reset_1_value));
  and and_34 (and_34_out, Allocate, Current_Context_Number_Of_Pages_Lower_10_Are_0);
  Demultiplexer #(.select(3)) demultiplexer_1 (
    .out0(A1), .out1(demultiplexer_1_out1), .out2(demultiplexer_1_out2), .out3(demultiplexer_1_out3),
    .out4(demultiplexer_1_out4), .in(and_34_out), .sel(bit3_fe_counter_sync_reset_1_value));  // open: out5, out6, out7
  and and_35 (and_35_out, ~Current_Context_Number_Of_Pages_Lower_10_Are_0, Allocate);  // AND_Gate
  Demultiplexer #(.select(3)) demultiplexer_2 (
    .out0(demultiplexer_2_out0), .out1(demultiplexer_2_out1), .out2(demultiplexer_2_out2), .in(and_35_out),
    .sel(bit3_fe_counter_sync_reset_1_value));  // open: out3, out4, out5, out6, out7
  and and_36 (and_36_out, Deallocate, Current_Context_Number_Of_Pages_Lower_10_Are_1);
  Demultiplexer #(.select(3)) demultiplexer_3 (
    .out0(D1), .out1(demultiplexer_3_out1), .out2(demultiplexer_3_out2), .out3(demultiplexer_3_out3),
    .out4(demultiplexer_3_out4), .out5(demultiplexer_3_out5), .in(and_36_out),
    .sel(bit3_fe_counter_sync_reset_1_value));  // open: out6, out7
  and and_37 (and_37_out, ~Current_Context_Number_Of_Pages_Lower_10_Are_1, Deallocate);  // AND_Gate
  Demultiplexer #(.select(3)) demultiplexer_4 (
    .out0(demultiplexer_4_out0), .out1(demultiplexer_4_out1), .out2(demultiplexer_4_out2),
    .out3(demultiplexer_4_out3), .in(and_37_out), .sel(bit3_fe_counter_sync_reset_1_value));  // open: out4, out5, out6, out7
  Demultiplexer #(.select(3)) demultiplexer_5 (
    .out0(CT1), .out1(CT2), .in(Context_Switch), .sel(bit3_fe_counter_sync_reset_1_value));  // open: out2, out3, out4, out5, out6, out7
  Pull_Resistor pull_resistor_5 (.node(pull_resistor_5_node[12]));
  assign bit_extender_12_out = {{13{1'b0}}, {Enable, {4{pull_resistor_5_node[12]}}, Context_Id, pull_resistor_5_node[12]}};  // Bit_Extender bit_extender_12
  assign bit_extender_13_out = {{1{1'b0}}, Current_Context_Number_Of_Pages};  // Bit_Extender bit_extender_13
  assign Bit16_Memory_Out = CT1 ? bit_extender_13_out : 16'bz;  // Controlled_Buffer controlled_buffer_12
  and and_38 (and_38_out, Data_Key_In_Cache, Translate_Data);
  and and_39 (Memory_Read_Instruction, Instruction_Key_In_Cache, Translate_Instruction);
  Demultiplexer #(.select(3)) demultiplexer_6 (
    .out0(DT1), .out1(DT2), .out2(DT3), .in(Translate_Data), .sel(bit3_fe_counter_sync_reset_1_value));  // open: out3, out4, out5, out6, out7
  Demultiplexer #(.select(3)) demultiplexer_7 (
    .out0(IT1), .out1(IT2), .out2(IT3), .in(Translate_Instruction), .sel(bit3_fe_counter_sync_reset_1_value));  // open: out3, out4, out5, out6, out7
  or or_24 (or_24_out, demultiplexer_1_out2, demultiplexer_2_out0);
  or or_25 (or_25_out, demultiplexer_1_out3, demultiplexer_2_out1);
  or or_26 (or_26_out, demultiplexer_1_out4, demultiplexer_2_out2);
  or or_27 (DMAIN2, demultiplexer_3_out2, demultiplexer_4_out0);
  or or_28 (DMAIN3, demultiplexer_3_out3, demultiplexer_4_out1);
  or or_29 (or_29_out, demultiplexer_3_out4, demultiplexer_4_out2);
  or or_30 (DSIM1_2ND, demultiplexer_3_out5, demultiplexer_4_out3);
  and and_40 (AFETCH, ~A_Translation_Page_Table_Was_Cached, or_24_out);  // AND_Gate
  and and_41 (and_41_out, A_Translation_Page_Table_Was_Cached, or_24_out);
  and and_42 (and_42_out, ~A_Translation_Page_Table_Was_Cached, or_25_out);  // AND_Gate
  and and_43 (and_43_out, A_Translation_Page_Table_Was_Cached, or_25_out);
  and and_44 (and_44_out, ~A_Translation_Page_Table_Was_Cached, or_26_out);  // AND_Gate
  // AND_Gate and_45 has open pins: in0=A_Translation_Page_Table_Was_Cached, in1=or_26_out, out=open
  or or_31 (DMAIN1, demultiplexer_3_out1, or_29_out);
  and and_46 (and_46_out, DMAIN1, Deallocated_Page_Available);
  and and_47 (and_47_out, AMAIN2, Deallocated_Page_Available);
  or or_32 (or_32_out, DMAIN1, and_47_out);
  assign controlled_buffer_13_out = or_32_out ? bit_extender_14_out : 27'bz;  // Controlled_Buffer controlled_buffer_13
  assign Bit16_Memory_Out = or_36_out ? Next_Free_Id : 16'bz;  // Controlled_Buffer controlled_buffer_14
  and and_48 (and_48_out, and_38_out, Memory_Read_Instruction);
  or or_33 (AMAIN1, and_41_out, and_42_out);
  or or_34 (AMAIN2, and_43_out, and_44_out, demultiplexer_1_out1);
  or or_35 (AMAIN2_3, and_44_out, and_43_out);
  assign bit_extender_14_out = {{10{1'b0}}, Deallocated_Page_Pointer};  // Bit_Extender bit_extender_14
  assign controlled_buffer_15_out = or_37_out ? {{15{1'b0}}, Context_Id, Translation_Page_Index_Table_Address} : 27'bz;  // Controlled_Buffer controlled_buffer_15
  or or_36 (or_36_out, A1, and_46_out, AMAIN1);
  and and_49 (and_49_out, and_48_out, Data_Write);
  and and_50 (and_50_out, and_48_out, Data_Read);
  or or_37 (or_37_out, T2_Not_Cached, A1, D1, AFETCH);
  and and_51 (T2_Not_Cached, or_42_out, ~Virtual_Page_Table_Index_Is_Cached);  // AND_Gate
  or or_38 (or_38_out, and_52_out, DMAIN3, AMAIN1);
  assign controlled_buffer_16_out = or_38_out ? {Translation_Address, 1'b0} : 27'bz;  // Controlled_Buffer controlled_buffer_16
  and and_52 (and_52_out, or_42_out, Virtual_Page_Table_Index_Is_Cached);
  Priority_Encoder priority_encoder_3 (
    .in1(and_53_out), .in2(or_38_out), .in3(or_37_out), .in4(or_32_out), .in5(CT1),
    .out(priority_encoder_3_out));  // open: in0, in6, in7, en_in
  or or_39 (Auto_Memory_Read_Data, AFETCH, DMAIN3, or_42_out, D1, CT2, and_50_out);
  or or_40 (Auto_Memory_Write_Data, A1, DMAIN1, and_49_out, CT1, AMAIN1);
  or or_41 (Two_Byte_Op, AFETCH, or_42_out, AMAIN1, DMAIN3, D1, A1, DMAIN1, Context_Switch);
  Multiplexer #(.select(3), .width(27)) multiplexer_5 (
    .in0(Bit27_Virtual_Memory_Address), .in1(Data_Translated_Address), .in2(controlled_buffer_16_out),
    .in3(controlled_buffer_15_out), .in4(controlled_buffer_13_out), .in5(bit_extender_12_out),
    .out(Bit27_Data_Memory_Address), .sel(priority_encoder_3_out));  // open: in6, in7
  Pull_Resistor pull_resistor_6 (.node(Bit27_Data_Memory_Address));
  Pull_Resistor pull_resistor_7 (.node(Bit16_Memory_Out));
  // Probe on 16'h2000
  or or_42 (or_42_out, DT2, IT2);
  and and_53 (and_53_out, Data_Key_In_Cache, DT1);
  and and_54 (and_54_out, Instruction_Key_In_Cache, IT1);
  assign Bit27_Instruction_Memory_Address = and_54_out ? {Instruction_Translated_Address, Bit27_Instruction_Address_In[11:0]} : 27'bz;  // Controlled_Buffer controlled_buffer_17
  Pull_Resistor pull_resistor_8 (.node(Bit27_Instruction_Memory_Address));
  and and_55 (and_55_out, Bit5_Lower_Flag_Mask[0], Lower_Flag_Mask_Enable);
  and and_56 (and_56_out, Bit5_Lower_Flag_Mask[1], Lower_Flag_Mask_Enable);
  and and_57 (and_57_out, Bit5_Lower_Flag_Mask[2], Lower_Flag_Mask_Enable);
  and and_58 (and_58_out, Bit5_Lower_Flag_Mask[3], Lower_Flag_Mask_Enable);
  and and_59 (and_59_out, Bit5_Lower_Flag_Mask[4], Lower_Flag_Mask_Enable);
  S_R_Flip_Flop s_r_ff_1 (
    .S(OUT_OF_PAGES_t), .R(and_55_out), .clk(Clock), .Q(Out_Of_Pages), .reset(Reset));  // open: Qn, preset
  S_R_Flip_Flop s_r_ff_2 (
    .S(Context_Max_Pages_Allocated_t), .R(and_56_out), .clk(Clock), .Q(Context_Max_Pages_Allocated),
    .reset(Reset));  // open: Qn, preset
  S_R_Flip_Flop s_r_ff_3 (
    .S(Multipage_Virtual_Page_Overflow_t), .R(and_57_out), .clk(Clock), .Q(Multipage_Virtual_Page_Overflow),
    .reset(Reset));  // open: Qn, preset
  S_R_Flip_Flop s_r_ff_4 (
    .S(Page_Not_Allocated_t), .R(and_58_out), .clk(Clock), .Q(Page_Not_Allocated), .reset(Reset));  // open: Qn, preset
  S_R_Flip_Flop s_r_ff_5 (
    .S(Translation_Page_Not_Allocated_t), .R(and_59_out), .clk(Clock), .Q(Translation_Page_Not_Allocated),
    .reset(Reset));  // open: Qn, preset
  or or_43 (Fault, Translation_Page_Not_Allocated, Page_Not_Allocated, Multipage_Virtual_Page_Overflow, Context_Max_Pages_Allocated, Out_Of_Pages);

  // Other names for the same wires on the sheet: Bit27_Instruction_Address[26:0] = Bit27_Instruction_Address_In;
  //   Instruction_Virtual_Page[14:0] = Bit27_Instruction_Address_In[26:12];
  //   Bit27_Data_Address[26:0] = Bit27_Virtual_Memory_Address;
  //   Translation_Page_Index_Table_Address[11:4] = Context_Id; DATA_OP_READ = Data_Read; DATA_OP_WRITE = Data_Write;
  //   Data_Virtual_Page_Offset[11:0] = Data_Translated_Address[11:0];
  //   Data_Virtual_Page_Table_Index[3:0] = Data_Virtual_Page[14:11];
  //   Instruction_Translated_Address[11:0] = Bit27_Instruction_Address_In[11:0];
  //   Instruction_Virtual_Page_Offset[11:0] = Bit27_Instruction_Address_In[11:0];
  //   Instruction_Virtual_Page_Table_Index[3:0] = Bit27_Instruction_Address_In[26:23];
  //   Last_Freed_Page[1] = Last_Freed_Page[7]; Lower_Flag_Mask[4:0] = Bit5_Lower_Flag_Mask;
  //   Stalling_Core = Stall_Core

  // Notes on the sheet:
  //   lowest pg number + 1 not allocated to hardware
  //   Deallocated_Page_Table_Base_Address
  //   this lowest priority
endmodule

module Bit15_x16_Cache (
  input  [3:0] Bit4_Query,
  input  [14:0] Bit15_Write_Value,
  input  Write_Enable,
  input  Reset_Enable,
  input  Clock,
  input  Query,
  input  Clear,
  output [14:0] Bit15_Result,
  output Value_Cached
);

  wire and_1_out, and_2_out, and_3_out, and_4_out, and_5_out, and_6_out, and_7_out, and_8_out, and_9_out,
       and_10_out, and_11_out, and_12_out, and_13_out, and_14_out, and_15_out, and_16_out,
       demultiplexer_1_out0, demultiplexer_1_out1, demultiplexer_1_out2, demultiplexer_1_out3,
       demultiplexer_1_out4, demultiplexer_1_out5, demultiplexer_1_out6, demultiplexer_1_out7,
       demultiplexer_1_out8, demultiplexer_1_out9, demultiplexer_1_out10, demultiplexer_1_out11,
       demultiplexer_1_out12, demultiplexer_1_out13, demultiplexer_1_out14, demultiplexer_1_out15, or_1_out,
       or_2_out;
  wire [14:0] bit_extender_1_out, controlled_buffer_1_out;
  wire [15:0] register_1_q, register_2_q, register_3_q, register_4_q, register_5_q, register_6_q,
       register_7_q, register_8_q, register_9_q, register_10_q, register_11_q, register_12_q, register_13_q,
       register_14_q, register_15_q, register_16_q;

  or or_1 (or_1_out, Write_Enable, Reset_Enable);
  Register #(.width(16)) register_1 (
    .D({Write_Enable, Bit15_Write_Value}), .en(and_1_out), .clk(Clock), .Q(register_1_q), .clr(Clear));
  and and_1 (and_1_out, demultiplexer_1_out0, or_1_out);
  Register #(.width(16)) register_2 (
    .D({Write_Enable, Bit15_Write_Value}), .en(and_2_out), .clk(Clock), .Q(register_2_q), .clr(Clear));
  and and_2 (and_2_out, demultiplexer_1_out1, or_1_out);
  Register #(.width(16)) register_3 (
    .D({Write_Enable, Bit15_Write_Value}), .en(and_3_out), .clk(Clock), .Q(register_3_q), .clr(Clear));
  and and_3 (and_3_out, demultiplexer_1_out2, or_1_out);
  Register #(.width(16)) register_4 (
    .D({Write_Enable, Bit15_Write_Value}), .en(and_4_out), .clk(Clock), .Q(register_4_q), .clr(Clear));
  and and_4 (and_4_out, demultiplexer_1_out3, or_1_out);
  Register #(.width(16)) register_5 (
    .D({Write_Enable, Bit15_Write_Value}), .en(and_5_out), .clk(Clock), .Q(register_5_q), .clr(Clear));
  and and_5 (and_5_out, demultiplexer_1_out4, or_1_out);
  Register #(.width(16)) register_6 (
    .D({Write_Enable, Bit15_Write_Value}), .en(and_6_out), .clk(Clock), .Q(register_6_q), .clr(Clear));
  and and_6 (and_6_out, demultiplexer_1_out5, or_1_out);
  Register #(.width(16)) register_7 (
    .D({Write_Enable, Bit15_Write_Value}), .en(and_7_out), .clk(Clock), .Q(register_7_q), .clr(Clear));
  and and_7 (and_7_out, demultiplexer_1_out6, or_1_out);
  Register #(.width(16)) register_8 (
    .D({Write_Enable, Bit15_Write_Value}), .en(and_8_out), .clk(Clock), .Q(register_8_q), .clr(Clear));
  and and_8 (and_8_out, demultiplexer_1_out7, or_1_out);
  Register #(.width(16)) register_9 (
    .D({Write_Enable, Bit15_Write_Value}), .en(and_9_out), .clk(Clock), .Q(register_9_q), .clr(Clear));
  and and_9 (and_9_out, demultiplexer_1_out8, or_1_out);
  Register #(.width(16)) register_10 (
    .D({Write_Enable, Bit15_Write_Value}), .en(and_10_out), .clk(Clock), .Q(register_10_q), .clr(Clear));
  and and_10 (and_10_out, demultiplexer_1_out9, or_1_out);
  Register #(.width(16)) register_11 (
    .D({Write_Enable, Bit15_Write_Value}), .en(and_11_out), .clk(Clock), .Q(register_11_q), .clr(Clear));
  and and_11 (and_11_out, demultiplexer_1_out10, or_1_out);
  Register #(.width(16)) register_12 (
    .D({Write_Enable, Bit15_Write_Value}), .en(and_12_out), .clk(Clock), .Q(register_12_q), .clr(Clear));
  and and_12 (and_12_out, demultiplexer_1_out11, or_1_out);
  Register #(.width(16)) register_13 (
    .D({Write_Enable, Bit15_Write_Value}), .en(and_13_out), .clk(Clock), .Q(register_13_q), .clr(Clear));
  and and_13 (and_13_out, demultiplexer_1_out12, or_1_out);
  Register #(.width(16)) register_14 (
    .D({Write_Enable, Bit15_Write_Value}), .en(and_14_out), .clk(Clock), .Q(register_14_q), .clr(Clear));
  and and_14 (and_14_out, demultiplexer_1_out13, or_1_out);
  Register #(.width(16)) register_15 (
    .D({Write_Enable, Bit15_Write_Value}), .en(and_15_out), .clk(Clock), .Q(register_15_q), .clr(Clear));
  and and_15 (and_15_out, demultiplexer_1_out14, or_1_out);
  Register #(.width(16)) register_16 (
    .D({Write_Enable, Bit15_Write_Value}), .en(and_16_out), .clk(Clock), .Q(register_16_q), .clr(Clear));
  and and_16 (and_16_out, demultiplexer_1_out15, or_1_out);
  assign {Value_Cached, controlled_buffer_1_out} = demultiplexer_1_out0 ? register_1_q : 16'bz;  // Controlled_Buffer controlled_buffer_1
  assign {Value_Cached, controlled_buffer_1_out} = demultiplexer_1_out1 ? register_2_q : 16'bz;  // Controlled_Buffer controlled_buffer_2
  assign {Value_Cached, controlled_buffer_1_out} = demultiplexer_1_out2 ? register_3_q : 16'bz;  // Controlled_Buffer controlled_buffer_3
  assign {Value_Cached, controlled_buffer_1_out} = demultiplexer_1_out3 ? register_4_q : 16'bz;  // Controlled_Buffer controlled_buffer_4
  assign {Value_Cached, controlled_buffer_1_out} = demultiplexer_1_out4 ? register_5_q : 16'bz;  // Controlled_Buffer controlled_buffer_5
  assign {Value_Cached, controlled_buffer_1_out} = demultiplexer_1_out5 ? register_6_q : 16'bz;  // Controlled_Buffer controlled_buffer_6
  assign {Value_Cached, controlled_buffer_1_out} = demultiplexer_1_out6 ? register_7_q : 16'bz;  // Controlled_Buffer controlled_buffer_7
  assign {Value_Cached, controlled_buffer_1_out} = demultiplexer_1_out7 ? register_8_q : 16'bz;  // Controlled_Buffer controlled_buffer_8
  assign {Value_Cached, controlled_buffer_1_out} = demultiplexer_1_out8 ? register_9_q : 16'bz;  // Controlled_Buffer controlled_buffer_9
  assign {Value_Cached, controlled_buffer_1_out} = demultiplexer_1_out9 ? register_10_q : 16'bz;  // Controlled_Buffer controlled_buffer_10
  assign {Value_Cached, controlled_buffer_1_out} = demultiplexer_1_out10 ? register_11_q : 16'bz;  // Controlled_Buffer controlled_buffer_11
  assign {Value_Cached, controlled_buffer_1_out} = demultiplexer_1_out11 ? register_12_q : 16'bz;  // Controlled_Buffer controlled_buffer_12
  assign {Value_Cached, controlled_buffer_1_out} = demultiplexer_1_out12 ? register_13_q : 16'bz;  // Controlled_Buffer controlled_buffer_13
  assign {Value_Cached, controlled_buffer_1_out} = demultiplexer_1_out13 ? register_14_q : 16'bz;  // Controlled_Buffer controlled_buffer_14
  assign {Value_Cached, controlled_buffer_1_out} = demultiplexer_1_out14 ? register_15_q : 16'bz;  // Controlled_Buffer controlled_buffer_15
  assign {Value_Cached, controlled_buffer_1_out} = demultiplexer_1_out15 ? register_16_q : 16'bz;  // Controlled_Buffer controlled_buffer_16
  or or_2 (or_2_out, or_1_out, Query);
  Demultiplexer #(.select(4)) demultiplexer_1 (
    .out0(demultiplexer_1_out0), .out1(demultiplexer_1_out1), .out2(demultiplexer_1_out2),
    .out3(demultiplexer_1_out3), .out4(demultiplexer_1_out4), .out5(demultiplexer_1_out5),
    .out6(demultiplexer_1_out6), .out7(demultiplexer_1_out7), .out8(demultiplexer_1_out8),
    .out9(demultiplexer_1_out9), .out10(demultiplexer_1_out10), .out11(demultiplexer_1_out11),
    .out12(demultiplexer_1_out12), .out13(demultiplexer_1_out13), .out14(demultiplexer_1_out14),
    .out15(demultiplexer_1_out15), .in(or_2_out), .sel(Bit4_Query));
  Pull_Resistor pull_resistor_1 (.node({Value_Cached, controlled_buffer_1_out}));
  Bit_Extender #(.in_width(16), .out_width(15), .\type ("zero")) bit_extender_1 (
    .in({Value_Cached, controlled_buffer_1_out}), .out(bit_extender_1_out));
  assign Bit15_Result = Value_Cached ? bit_extender_1_out : 15'bz;  // Controlled_Buffer controlled_buffer_17

  // Notes on the sheet:
  //   just redo this bruh
endmodule

module Bit3_FE_Counter_Sync_Reset (
  input  Count,
  input  Clock,
  input  Reset,
  output [2:0] Value
);

  wire and_1_out, and_2_out, and_3_out, and_4_out, not_1_out, or_1_out, or_2_out, or_3_out;
  wire [2:0] adder_1_out, pull_resistor_1_node, VL_q;

  not not_1 (not_1_out, Reset);
  or or_1 (or_1_out, Count, Reset);
  J_K_Flip_Flop #(.trigger("falling")) j_k_ff_1 (
    .J(and_1_out), .K(or_1_out), .clk(Clock), .Q(Value[0]));  // open: Qn, preset, reset
  and and_1 (and_1_out, Count, not_1_out);
  and and_2 (and_2_out, Value[0], not_1_out);
  J_K_Flip_Flop #(.trigger("falling")) j_k_ff_2 (
    .J(and_2_out), .K(or_2_out), .clk(Clock), .Q(Value[1]));  // open: Qn, preset, reset
  or or_2 (or_2_out, Value[0], Reset);
  and and_3 (and_3_out, Value[0], Value[1]);
  J_K_Flip_Flop #(.trigger("falling")) j_k_ff_3 (
    .J(and_4_out), .K(or_3_out), .clk(Clock), .Q(Value[2]));  // open: Qn, preset, reset
  and and_4 (and_4_out, and_3_out, not_1_out);
  or or_3 (or_3_out, and_3_out, Reset);
  Adder #(.width(3)) adder_1 (.a(3'b001), .b(Value), .out(adder_1_out));  // open: cin, cout
  Register #(.trigger("falling"), .width(3)) VL (
    .D(pull_resistor_1_node), .en(or_1_out), .clk(Clock), .Q(VL_q));  // open: clr
  Pull_Resistor pull_resistor_1 (.node(pull_resistor_1_node));
  assign pull_resistor_1_node = not_1_out ? adder_1_out : 3'bz;  // Controlled_Buffer controlled_buffer_1
  // Probe on VL_q
endmodule

module Instruction_Pointer_2 (
  input  Offset_Mode,
  input  [26:0] Bit27_Offset,
  input  [26:0] Bit27_Address,
  input  Set_Address,
  input  Offset,
  input  Enable,
  input  Clock,
  input  Reset,
  output [26:0] Bit27_Instruction_Address,
  output Instruction_Offset_Out_Of_Bounds
);

  wire and_2_out, and_33_out, and_34_out, bit32_adder_1_c_out, nor_1_out, xor_1_out, xor_2_out, xor_3_out,
       xor_4_out, xor_5_out, xor_6_out, xor_7_out, xor_8_out, xor_9_out, xor_10_out, xor_11_out, xor_12_out,
       xor_13_out, xor_14_out, xor_15_out, xor_16_out, xor_17_out, xor_18_out, xor_19_out, xor_20_out,
       xor_21_out, xor_22_out, xor_23_out, xor_24_out, xor_25_out, xor_26_out, xor_27_out;
  wire [26:0] bit_extender_2_out, multiplexer_1_out;
  wire [31:0] and_1_out, bit32_adder_1_bit32_result, bit_extender_1_out;

  nor nor_1 (nor_1_out, Set_Address, Offset);
  Multiplexer #(.width(27)) multiplexer_1 (
    .in0(Bit27_Instruction_Address), .in1(Bit27_Address), .out(multiplexer_1_out), .sel(Set_Address));
  assign bit_extender_1_out = {{5{1'b0}}, multiplexer_1_out};  // Bit_Extender bit_extender_1
  xor xor_1 (xor_1_out, Bit27_Offset[0], Offset_Mode);
  and and_1 (and_1_out[0], xor_1_out, Offset);
  xor xor_2 (xor_2_out, Bit27_Offset[1], Offset_Mode);
  and and_2 (and_2_out, xor_2_out, Offset);
  xor xor_3 (xor_3_out, Bit27_Offset[2], Offset_Mode);
  and and_3 (and_1_out[2], xor_3_out, Offset);
  xor xor_4 (xor_4_out, Bit27_Offset[3], Offset_Mode);
  and and_4 (and_1_out[3], xor_4_out, Offset);
  xor xor_5 (xor_5_out, Bit27_Offset[4], Offset_Mode);
  and and_5 (and_1_out[4], xor_5_out, Offset);
  xor xor_6 (xor_6_out, Bit27_Offset[5], Offset_Mode);
  and and_6 (and_1_out[5], xor_6_out, Offset);
  xor xor_7 (xor_7_out, Bit27_Offset[6], Offset_Mode);
  and and_7 (and_1_out[6], xor_7_out, Offset);
  xor xor_8 (xor_8_out, Bit27_Offset[7], Offset_Mode);
  and and_8 (and_1_out[7], xor_8_out, Offset);
  xor xor_9 (xor_9_out, Bit27_Offset[8], Offset_Mode);
  and and_9 (and_1_out[8], xor_9_out, Offset);
  xor xor_10 (xor_10_out, Bit27_Offset[9], Offset_Mode);
  and and_10 (and_1_out[9], xor_10_out, Offset);
  xor xor_11 (xor_11_out, Bit27_Offset[10], Offset_Mode);
  and and_11 (and_1_out[10], xor_11_out, Offset);
  xor xor_12 (xor_12_out, Bit27_Offset[11], Offset_Mode);
  and and_12 (and_1_out[11], xor_12_out, Offset);
  xor xor_13 (xor_13_out, Bit27_Offset[12], Offset_Mode);
  and and_13 (and_1_out[12], xor_13_out, Offset);
  xor xor_14 (xor_14_out, Bit27_Offset[13], Offset_Mode);
  and and_14 (and_1_out[13], xor_14_out, Offset);
  xor xor_15 (xor_15_out, Bit27_Offset[14], Offset_Mode);
  and and_15 (and_1_out[14], xor_15_out, Offset);
  xor xor_16 (xor_16_out, Bit27_Offset[15], Offset_Mode);
  and and_16 (and_1_out[15], xor_16_out, Offset);
  xor xor_17 (xor_17_out, Bit27_Offset[16], Offset_Mode);
  and and_17 (and_1_out[16], xor_17_out, Offset);
  xor xor_18 (xor_18_out, Bit27_Offset[17], Offset_Mode);
  and and_18 (and_1_out[17], xor_18_out, Offset);
  xor xor_19 (xor_19_out, Bit27_Offset[18], Offset_Mode);
  and and_19 (and_1_out[18], xor_19_out, Offset);
  xor xor_20 (xor_20_out, Bit27_Offset[19], Offset_Mode);
  and and_20 (and_1_out[19], xor_20_out, Offset);
  xor xor_21 (xor_21_out, Bit27_Offset[20], Offset_Mode);
  and and_21 (and_1_out[20], xor_21_out, Offset);
  xor xor_22 (xor_22_out, Bit27_Offset[21], Offset_Mode);
  and and_22 (and_1_out[21], xor_22_out, Offset);
  xor xor_23 (xor_23_out, Bit27_Offset[22], Offset_Mode);
  and and_23 (and_1_out[22], xor_23_out, Offset);
  xor xor_24 (xor_24_out, Bit27_Offset[23], Offset_Mode);
  and and_24 (and_1_out[23], xor_24_out, Offset);
  xor xor_25 (xor_25_out, Bit27_Offset[24], Offset_Mode);
  and and_25 (and_1_out[24], xor_25_out, Offset);
  xor xor_26 (xor_26_out, Bit27_Offset[25], Offset_Mode);
  and and_26 (and_1_out[25], xor_26_out, Offset);
  xor xor_27 (xor_27_out, Bit27_Offset[26], Offset_Mode);
  and and_27 (and_1_out[26], xor_27_out, Offset);
  and and_28 (and_1_out[27], Offset_Mode, Offset);
  and and_29 (and_1_out[28], Offset_Mode, Offset);
  and and_30 (and_1_out[29], Offset_Mode, Offset);
  and and_31 (and_1_out[30], Offset_Mode, Offset);
  and and_32 (and_1_out[31], Offset_Mode, Offset);
  or or_1 (and_1_out[1], nor_1_out, and_2_out);
  Bit32_Adder bit32_adder_1 (
    .C_In(Offset_Mode), .Bit32_A(bit_extender_1_out), .Bit32_B(and_1_out),
    .Bit32_Result(bit32_adder_1_bit32_result), .C_OUT(bit32_adder_1_c_out));
  Bit_Extender #(.in_width(32), .out_width(27), .\type ("zero")) bit_extender_2 (
    .in(bit32_adder_1_bit32_result), .out(bit_extender_2_out));
  Register #(.width(27)) register_1 (
    .D(bit_extender_2_out), .en(Enable), .clk(Clock), .Q(Bit27_Instruction_Address), .clr(Reset));
  and and_33 (and_33_out, ~bit32_adder_1_c_out, Offset_Mode, Set_Address);  // AND_Gate
  and and_34 (and_34_out, bit32_adder_1_c_out, Offset_Mode, Set_Address);
  or or_2 (Instruction_Offset_Out_Of_Bounds, and_33_out, and_34_out);

  // Notes on the sheet:
  //   0 = add, 1 = sub
endmodule

module Stack_Pointer (
  input  [26:0] Bit27_Address,
  input  Set,
  input  Push,
  input  Pop,
  input  Clock,
  input  Reset,
  output [26:0] Bit27_Stack_Address
);

  wire and_1_out, or_1_out;

  Counter #(.max('h3ffffff), .width(26)) counter_1 (
    .clr(Reset), .load(Set), .up(Pop), .count(or_1_out), .clk(Clock), .D(Bit27_Address[26:1]),
    .Q(Bit27_Stack_Address[26:1]));  // open: carry
  or or_1 (or_1_out, Push, Pop);
  D_Flip_Flop d_ff_1 (
    .D(Bit27_Address[0]), .clk(and_1_out), .Q(Bit27_Stack_Address[0]), .reset(Reset));  // open: Qn, preset
  and and_1 (and_1_out, Set, Clock);
endmodule

module Bit32_Adder (
  input  C_In,
  input  [31:0] Bit32_A,
  input  [31:0] Bit32_B,
  output [31:0] Bit32_Result,
  output C_OUT
);

  wire and_1_out, and_2_out, and_3_out, and_4_out, and_5_out, and_6_out, and_7_out, and_8_out, and_9_out,
       and_10_out, and_11_out, and_12_out, and_13_out, and_14_out, and_15_out, and_16_out, and_17_out,
       and_18_out, and_19_out, and_20_out, and_21_out, and_22_out, and_23_out, and_24_out, and_25_out,
       and_26_out, and_27_out, and_28_out, and_29_out, and_30_out, and_31_out, and_32_out,
       bit4_cla_logic_1_c2, bit4_cla_logic_1_c3, bit4_cla_logic_1_c4, bit8_cla_logic_1_c1,
       bit8_cla_logic_1_c2, bit8_cla_logic_1_c3, bit8_cla_logic_1_c4, bit8_cla_logic_1_c5,
       bit8_cla_logic_1_c6, bit8_cla_logic_1_c7, bit8_cla_logic_1_c_out, bit8_cla_logic_1_pg,
       bit8_cla_logic_2_c1, bit8_cla_logic_2_c2, bit8_cla_logic_2_c3, bit8_cla_logic_2_c4,
       bit8_cla_logic_2_c5, bit8_cla_logic_2_c6, bit8_cla_logic_2_c7, bit8_cla_logic_2_c_out,
       bit8_cla_logic_2_pg, bit8_cla_logic_3_c1, bit8_cla_logic_3_c2, bit8_cla_logic_3_c3,
       bit8_cla_logic_3_c4, bit8_cla_logic_3_c5, bit8_cla_logic_3_c6, bit8_cla_logic_3_c7,
       bit8_cla_logic_3_c_out, bit8_cla_logic_3_pg, bit8_cla_logic_4_c1, bit8_cla_logic_4_c2,
       bit8_cla_logic_4_c3, bit8_cla_logic_4_c4, bit8_cla_logic_4_c5, bit8_cla_logic_4_c6,
       bit8_cla_logic_4_c7, bit8_cla_logic_4_c_out, bit8_cla_logic_4_pg, xor_1_out, xor_2_out, xor_3_out,
       xor_4_out, xor_5_out, xor_6_out, xor_7_out, xor_8_out, xor_9_out, xor_10_out, xor_11_out, xor_12_out,
       xor_13_out, xor_14_out, xor_15_out, xor_16_out, xor_17_out, xor_18_out, xor_19_out, xor_20_out,
       xor_21_out, xor_22_out, xor_23_out, xor_24_out, xor_25_out, xor_26_out, xor_27_out, xor_28_out,
       xor_29_out, xor_30_out, xor_31_out, xor_32_out;

  xor xor_1 (xor_1_out, Bit32_A[0], Bit32_B[0]);
  and and_1 (and_1_out, Bit32_B[0], Bit32_A[0]);
  xor xor_2 (xor_2_out, Bit32_A[1], Bit32_B[1]);
  and and_2 (and_2_out, Bit32_B[1], Bit32_A[1]);
  xor xor_3 (xor_3_out, Bit32_A[2], Bit32_B[2]);
  and and_3 (and_3_out, Bit32_B[2], Bit32_A[2]);
  xor xor_4 (xor_4_out, Bit32_A[3], Bit32_B[3]);
  and and_4 (and_4_out, Bit32_B[3], Bit32_A[3]);
  xor xor_5 (xor_5_out, Bit32_A[4], Bit32_B[4]);
  and and_5 (and_5_out, Bit32_B[4], Bit32_A[4]);
  xor xor_6 (xor_6_out, Bit32_A[5], Bit32_B[5]);
  and and_6 (and_6_out, Bit32_B[5], Bit32_A[5]);
  xor xor_7 (xor_7_out, Bit32_A[6], Bit32_B[6]);
  and and_7 (and_7_out, Bit32_B[6], Bit32_A[6]);
  xor xor_8 (xor_8_out, Bit32_A[7], Bit32_B[7]);
  and and_8 (and_8_out, Bit32_B[7], Bit32_A[7]);
  xor xor_9 (xor_9_out, Bit32_A[8], Bit32_B[8]);
  and and_9 (and_9_out, Bit32_B[8], Bit32_A[8]);
  xor xor_10 (xor_10_out, Bit32_A[9], Bit32_B[9]);
  and and_10 (and_10_out, Bit32_B[9], Bit32_A[9]);
  xor xor_11 (xor_11_out, Bit32_A[10], Bit32_B[10]);
  and and_11 (and_11_out, Bit32_B[10], Bit32_A[10]);
  xor xor_12 (xor_12_out, Bit32_A[11], Bit32_B[11]);
  and and_12 (and_12_out, Bit32_B[11], Bit32_A[11]);
  xor xor_13 (xor_13_out, Bit32_A[12], Bit32_B[12]);
  and and_13 (and_13_out, Bit32_B[12], Bit32_A[12]);
  xor xor_14 (xor_14_out, Bit32_A[13], Bit32_B[13]);
  and and_14 (and_14_out, Bit32_B[13], Bit32_A[13]);
  xor xor_15 (xor_15_out, Bit32_A[14], Bit32_B[14]);
  and and_15 (and_15_out, Bit32_B[14], Bit32_A[14]);
  xor xor_16 (xor_16_out, Bit32_A[15], Bit32_B[15]);
  and and_16 (and_16_out, Bit32_B[15], Bit32_A[15]);
  xor xor_17 (xor_17_out, Bit32_A[16], Bit32_B[16]);
  and and_17 (and_17_out, Bit32_B[16], Bit32_A[16]);
  xor xor_18 (xor_18_out, Bit32_A[17], Bit32_B[17]);
  and and_18 (and_18_out, Bit32_B[17], Bit32_A[17]);
  xor xor_19 (xor_19_out, Bit32_A[18], Bit32_B[18]);
  and and_19 (and_19_out, Bit32_B[18], Bit32_A[18]);
  xor xor_20 (xor_20_out, Bit32_A[19], Bit32_B[19]);
  and and_20 (and_20_out, Bit32_B[19], Bit32_A[19]);
  xor xor_21 (xor_21_out, Bit32_A[20], Bit32_B[20]);
  and and_21 (and_21_out, Bit32_B[20], Bit32_A[20]);
  xor xor_22 (xor_22_out, Bit32_A[21], Bit32_B[21]);
  and and_22 (and_22_out, Bit32_B[21], Bit32_A[21]);
  xor xor_23 (xor_23_out, Bit32_A[22], Bit32_B[22]);
  and and_23 (and_23_out, Bit32_B[22], Bit32_A[22]);
  xor xor_24 (xor_24_out, Bit32_A[23], Bit32_B[23]);
  and and_24 (and_24_out, Bit32_B[23], Bit32_A[23]);
  xor xor_25 (xor_25_out, Bit32_A[24], Bit32_B[24]);
  and and_25 (and_25_out, Bit32_B[24], Bit32_A[24]);
  xor xor_26 (xor_26_out, Bit32_A[25], Bit32_B[25]);
  and and_26 (and_26_out, Bit32_B[25], Bit32_A[25]);
  xor xor_27 (xor_27_out, Bit32_A[26], Bit32_B[26]);
  and and_27 (and_27_out, Bit32_B[26], Bit32_A[26]);
  xor xor_28 (xor_28_out, Bit32_A[27], Bit32_B[27]);
  and and_28 (and_28_out, Bit32_B[27], Bit32_A[27]);
  xor xor_29 (xor_29_out, Bit32_A[28], Bit32_B[28]);
  and and_29 (and_29_out, Bit32_B[28], Bit32_A[28]);
  xor xor_30 (xor_30_out, Bit32_A[29], Bit32_B[29]);
  and and_30 (and_30_out, Bit32_B[29], Bit32_A[29]);
  xor xor_31 (xor_31_out, Bit32_A[30], Bit32_B[30]);
  and and_31 (and_31_out, Bit32_B[30], Bit32_A[30]);
  xor xor_32 (xor_32_out, Bit32_A[31], Bit32_B[31]);
  and and_32 (and_32_out, Bit32_B[31], Bit32_A[31]);
  xor xor_33 (Bit32_Result[0], C_In, xor_1_out);
  xor xor_34 (Bit32_Result[1], bit8_cla_logic_1_c1, xor_2_out);
  xor xor_35 (Bit32_Result[2], bit8_cla_logic_1_c2, xor_3_out);
  xor xor_36 (Bit32_Result[3], bit8_cla_logic_1_c3, xor_4_out);
  xor xor_37 (Bit32_Result[4], bit8_cla_logic_1_c4, xor_5_out);
  xor xor_38 (Bit32_Result[5], bit8_cla_logic_1_c5, xor_6_out);
  xor xor_39 (Bit32_Result[6], bit8_cla_logic_1_c6, xor_7_out);
  xor xor_40 (Bit32_Result[7], bit8_cla_logic_1_c7, xor_8_out);
  xor xor_41 (Bit32_Result[8], bit4_cla_logic_1_c2, xor_9_out);
  xor xor_42 (Bit32_Result[9], bit8_cla_logic_2_c1, xor_10_out);
  xor xor_43 (Bit32_Result[10], bit8_cla_logic_2_c2, xor_11_out);
  xor xor_44 (Bit32_Result[11], bit8_cla_logic_2_c3, xor_12_out);
  xor xor_45 (Bit32_Result[12], bit8_cla_logic_2_c4, xor_13_out);
  xor xor_46 (Bit32_Result[13], bit8_cla_logic_2_c5, xor_14_out);
  xor xor_47 (Bit32_Result[14], bit8_cla_logic_2_c6, xor_15_out);
  xor xor_48 (Bit32_Result[15], bit8_cla_logic_2_c7, xor_16_out);
  xor xor_49 (Bit32_Result[16], bit4_cla_logic_1_c3, xor_17_out);
  xor xor_50 (Bit32_Result[17], bit8_cla_logic_3_c1, xor_18_out);
  xor xor_51 (Bit32_Result[18], bit8_cla_logic_3_c2, xor_19_out);
  xor xor_52 (Bit32_Result[19], bit8_cla_logic_3_c3, xor_20_out);
  xor xor_53 (Bit32_Result[20], bit8_cla_logic_3_c4, xor_21_out);
  xor xor_54 (Bit32_Result[21], bit8_cla_logic_3_c5, xor_22_out);
  xor xor_55 (Bit32_Result[22], bit8_cla_logic_3_c6, xor_23_out);
  xor xor_56 (Bit32_Result[23], bit8_cla_logic_3_c7, xor_24_out);
  xor xor_57 (Bit32_Result[24], bit4_cla_logic_1_c4, xor_25_out);
  xor xor_58 (Bit32_Result[25], bit8_cla_logic_4_c1, xor_26_out);
  xor xor_59 (Bit32_Result[26], bit8_cla_logic_4_c2, xor_27_out);
  xor xor_60 (Bit32_Result[27], bit8_cla_logic_4_c3, xor_28_out);
  xor xor_61 (Bit32_Result[28], bit8_cla_logic_4_c4, xor_29_out);
  xor xor_62 (Bit32_Result[29], bit8_cla_logic_4_c5, xor_30_out);
  xor xor_63 (Bit32_Result[30], bit8_cla_logic_4_c6, xor_31_out);
  xor xor_64 (Bit32_Result[31], bit8_cla_logic_4_c7, xor_32_out);
  Bit8_CLA_Logic bit8_cla_logic_1 (
    .C_In(C_In), .P0(xor_1_out), .G0(and_1_out), .P1(xor_2_out), .G1(and_2_out), .P2(xor_3_out),
    .G2(and_3_out), .P3(xor_4_out), .G3(and_4_out), .P4(xor_5_out), .G4(and_5_out), .P5(xor_6_out),
    .G5(and_6_out), .P6(xor_7_out), .G6(and_7_out), .P7(xor_8_out), .G7(and_8_out), .C1(bit8_cla_logic_1_c1),
    .C2(bit8_cla_logic_1_c2), .C3(bit8_cla_logic_1_c3), .C4(bit8_cla_logic_1_c4), .C5(bit8_cla_logic_1_c5),
    .C6(bit8_cla_logic_1_c6), .C7(bit8_cla_logic_1_c7), .C_OUT(bit8_cla_logic_1_c_out),
    .PG(bit8_cla_logic_1_pg));
  Bit8_CLA_Logic bit8_cla_logic_2 (
    .C_In(bit4_cla_logic_1_c2), .P0(xor_9_out), .G0(and_9_out), .P1(xor_10_out), .G1(and_10_out),
    .P2(xor_11_out), .G2(and_11_out), .P3(xor_12_out), .G3(and_12_out), .P4(xor_13_out), .G4(and_13_out),
    .P5(xor_14_out), .G5(and_14_out), .P6(xor_15_out), .G6(and_15_out), .P7(xor_16_out), .G7(and_16_out),
    .C1(bit8_cla_logic_2_c1), .C2(bit8_cla_logic_2_c2), .C3(bit8_cla_logic_2_c3), .C4(bit8_cla_logic_2_c4),
    .C5(bit8_cla_logic_2_c5), .C6(bit8_cla_logic_2_c6), .C7(bit8_cla_logic_2_c7),
    .C_OUT(bit8_cla_logic_2_c_out), .PG(bit8_cla_logic_2_pg));
  Bit8_CLA_Logic bit8_cla_logic_3 (
    .C_In(bit4_cla_logic_1_c3), .P0(xor_17_out), .G0(and_17_out), .P1(xor_18_out), .G1(and_18_out),
    .P2(xor_19_out), .G2(and_19_out), .P3(xor_20_out), .G3(and_20_out), .P4(xor_21_out), .G4(and_21_out),
    .P5(xor_22_out), .G5(and_22_out), .P6(xor_23_out), .G6(and_23_out), .P7(xor_24_out), .G7(and_24_out),
    .C1(bit8_cla_logic_3_c1), .C2(bit8_cla_logic_3_c2), .C3(bit8_cla_logic_3_c3), .C4(bit8_cla_logic_3_c4),
    .C5(bit8_cla_logic_3_c5), .C6(bit8_cla_logic_3_c6), .C7(bit8_cla_logic_3_c7),
    .C_OUT(bit8_cla_logic_3_c_out), .PG(bit8_cla_logic_3_pg));
  Bit8_CLA_Logic bit8_cla_logic_4 (
    .C_In(bit4_cla_logic_1_c4), .P0(xor_25_out), .G0(and_25_out), .P1(xor_26_out), .G1(and_26_out),
    .P2(xor_27_out), .G2(and_27_out), .P3(xor_28_out), .G3(and_28_out), .P4(xor_29_out), .G4(and_29_out),
    .P5(xor_30_out), .G5(and_30_out), .P6(xor_31_out), .G6(and_31_out), .P7(xor_32_out), .G7(and_32_out),
    .C1(bit8_cla_logic_4_c1), .C2(bit8_cla_logic_4_c2), .C3(bit8_cla_logic_4_c3), .C4(bit8_cla_logic_4_c4),
    .C5(bit8_cla_logic_4_c5), .C6(bit8_cla_logic_4_c6), .C7(bit8_cla_logic_4_c7),
    .C_OUT(bit8_cla_logic_4_c_out), .PG(bit8_cla_logic_4_pg));
  Bit4_CLA_Logic bit4_cla_logic_1 (
    .Cin(C_In), .P1(bit8_cla_logic_1_pg), .G1(bit8_cla_logic_1_c_out), .P2(bit8_cla_logic_2_pg),
    .G2(bit8_cla_logic_2_c_out), .P3(bit8_cla_logic_3_pg), .G3(bit8_cla_logic_3_c_out),
    .P4(bit8_cla_logic_4_pg), .G4(bit8_cla_logic_4_c_out), .C2(bit4_cla_logic_1_c2),
    .C3(bit4_cla_logic_1_c3), .C4(bit4_cla_logic_1_c4), .COUT(C_OUT));  // open: PG
endmodule

module Bit32_X_Bit3_Right_Shift (
  input  [31:0] Bit32_In,
  input  [2:0] Bit3_Shift,
  output [31:0] Bit32_Result
);

  wire and_2_out, and_3_out, and_4_out, and_5_out, and_6_out, and_7_out, and_8_out, and_9_out, and_10_out,
       and_11_out, and_12_out, and_13_out, and_14_out, and_15_out, and_16_out, and_17_out, and_18_out,
       and_19_out, and_20_out, and_21_out, and_22_out, and_23_out, and_24_out, and_25_out, and_26_out,
       and_27_out, and_28_out, and_29_out, and_30_out, and_31_out, and_32_out, and_33_out, and_34_out,
       and_35_out, and_36_out, and_37_out, and_38_out, and_39_out, and_40_out, and_41_out, and_42_out,
       and_43_out, and_44_out, and_45_out, and_46_out, and_47_out, and_48_out, and_49_out, and_50_out,
       and_51_out, and_52_out, and_53_out, and_54_out, and_55_out, and_56_out, and_57_out, and_58_out,
       and_59_out, and_60_out, and_61_out, and_62_out, and_63_out, and_64_out, and_65_out, and_66_out,
       and_67_out, and_68_out, and_69_out, and_70_out, and_71_out, and_72_out, and_73_out, and_74_out,
       and_75_out, and_76_out, and_77_out, and_78_out, and_79_out, and_80_out, and_81_out, and_82_out,
       and_83_out, and_84_out, and_85_out, and_86_out, and_87_out, and_88_out, and_89_out, and_90_out,
       and_91_out, and_92_out, and_93_out, and_94_out, and_95_out, and_96_out, and_97_out, and_98_out,
       and_99_out, and_100_out, and_101_out, and_102_out, and_103_out, and_104_out, and_105_out, and_106_out,
       and_107_out, and_108_out, and_109_out, and_110_out, and_111_out, and_112_out, and_113_out,
       and_114_out, and_115_out, and_116_out, and_117_out, and_118_out, and_119_out, and_120_out,
       and_121_out, and_122_out, and_123_out, and_124_out, and_125_out, and_126_out, and_127_out,
       and_128_out, and_129_out, and_130_out, and_131_out, and_132_out, and_133_out, and_134_out,
       and_135_out, and_136_out, and_137_out, and_138_out, and_139_out, and_140_out, and_141_out,
       and_142_out, and_143_out, and_144_out, and_145_out, and_146_out, and_147_out, and_148_out,
       and_149_out, and_150_out, and_151_out, and_152_out, and_153_out, and_154_out, and_155_out,
       and_156_out, and_157_out, and_158_out, and_159_out, and_160_out, and_161_out, and_162_out,
       and_163_out, and_164_out, and_165_out, and_166_out, and_168_out, and_169_out, and_170_out,
       and_171_out, and_173_out, and_174_out, and_175_out, and_176_out, and_177_out, and_178_out,
       and_179_out, and_180_out, and_181_out, and_183_out, and_184_out, and_185_out, or_1_out, or_2_out,
       or_4_out, or_5_out, or_7_out, or_8_out, or_10_out, or_12_out, or_14_out, or_15_out, or_16_out,
       or_17_out, or_19_out, or_20_out, or_22_out, or_23_out, or_25_out, or_26_out, or_28_out, or_29_out,
       or_31_out, or_32_out, or_34_out, or_36_out, or_38_out, or_39_out, or_40_out, or_41_out, or_43_out,
       or_44_out, or_46_out, or_47_out, or_49_out, or_50_out, or_52_out, or_53_out, or_55_out, or_56_out,
       or_58_out, or_60_out, or_62_out, or_63_out, or_64_out, or_65_out, or_67_out, or_68_out, or_70_out,
       or_71_out, or_73_out, or_74_out, or_76_out, or_77_out, or_79_out, or_80_out, or_82_out, or_84_out,
       or_85_out, or_86_out, or_87_out, or_88_out, or_89_out;

  // AND_Gate and_1 has open pins: in0=Bit3_Shift[0], in1=Bit32_In[0], out=open
  and and_2 (and_2_out, ~Bit3_Shift[0], Bit32_In[0]);  // AND_Gate
  or or_1 (or_1_out, and_2_out, and_5_out);
  and and_3 (and_3_out, ~Bit3_Shift[1], or_1_out);  // AND_Gate
  or or_2 (or_2_out, and_3_out, and_11_out);
  and and_4 (and_4_out, ~Bit3_Shift[2], or_2_out);  // AND_Gate
  or or_3 (Bit32_Result[0], and_4_out, and_22_out);
  and and_5 (and_5_out, Bit3_Shift[0], Bit32_In[1]);
  and and_6 (and_6_out, ~Bit3_Shift[0], Bit32_In[1]);  // AND_Gate
  or or_4 (or_4_out, and_6_out, and_9_out);
  and and_7 (and_7_out, ~Bit3_Shift[1], or_4_out);  // AND_Gate
  or or_5 (or_5_out, and_7_out, and_16_out);
  and and_8 (and_8_out, ~Bit3_Shift[2], or_5_out);  // AND_Gate
  or or_6 (Bit32_Result[1], and_8_out, and_27_out);
  and and_9 (and_9_out, Bit3_Shift[0], Bit32_In[2]);
  and and_10 (and_10_out, ~Bit3_Shift[0], Bit32_In[2]);  // AND_Gate
  or or_7 (or_7_out, and_10_out, and_14_out);
  and and_11 (and_11_out, Bit3_Shift[1], or_7_out);
  and and_12 (and_12_out, ~Bit3_Shift[1], or_7_out);  // AND_Gate
  or or_8 (or_8_out, and_12_out, and_20_out);
  and and_13 (and_13_out, ~Bit3_Shift[2], or_8_out);  // AND_Gate
  or or_9 (Bit32_Result[2], and_13_out, and_33_out);
  and and_14 (and_14_out, Bit3_Shift[0], Bit32_In[3]);
  and and_15 (and_15_out, ~Bit3_Shift[0], Bit32_In[3]);  // AND_Gate
  and and_16 (and_16_out, Bit3_Shift[1], or_12_out);
  and and_17 (and_17_out, ~Bit3_Shift[1], or_12_out);  // AND_Gate
  or or_10 (or_10_out, and_17_out, and_26_out);
  and and_18 (and_18_out, ~Bit3_Shift[2], or_10_out);  // AND_Gate
  or or_11 (Bit32_Result[3], and_18_out, and_38_out);
  and and_19 (and_19_out, Bit3_Shift[0], Bit32_In[4]);
  or or_12 (or_12_out, and_15_out, and_19_out);
  and and_20 (and_20_out, Bit3_Shift[1], or_14_out);
  and and_21 (and_21_out, ~Bit3_Shift[1], or_14_out);  // AND_Gate
  and and_22 (and_22_out, Bit3_Shift[2], or_15_out);
  and and_23 (and_23_out, ~Bit3_Shift[2], or_15_out);  // AND_Gate
  or or_13 (Bit32_Result[4], and_23_out, and_44_out);
  and and_24 (and_24_out, ~Bit3_Shift[0], Bit32_In[4]);  // AND_Gate
  and and_25 (and_25_out, Bit3_Shift[0], Bit32_In[5]);
  or or_14 (or_14_out, and_24_out, and_25_out);
  and and_26 (and_26_out, Bit3_Shift[1], or_16_out);
  or or_15 (or_15_out, and_21_out, and_32_out);
  and and_27 (and_27_out, Bit3_Shift[2], or_17_out);
  and and_28 (and_28_out, ~Bit3_Shift[2], or_17_out);  // AND_Gate
  and and_29 (and_29_out, ~Bit3_Shift[0], Bit32_In[5]);  // AND_Gate
  and and_30 (and_30_out, Bit3_Shift[0], Bit32_In[6]);
  or or_16 (or_16_out, and_29_out, and_30_out);
  and and_31 (and_31_out, ~Bit3_Shift[1], or_16_out);  // AND_Gate
  and and_32 (and_32_out, Bit3_Shift[1], or_19_out);
  or or_17 (or_17_out, and_31_out, and_36_out);
  and and_33 (and_33_out, Bit3_Shift[2], or_20_out);
  or or_18 (Bit32_Result[5], and_28_out, and_49_out);
  and and_34 (and_34_out, Bit3_Shift[0], Bit32_In[7]);
  and and_35 (and_35_out, ~Bit3_Shift[0], Bit32_In[6]);  // AND_Gate
  or or_19 (or_19_out, and_35_out, and_34_out);
  and and_36 (and_36_out, Bit3_Shift[1], or_22_out);
  and and_37 (and_37_out, ~Bit3_Shift[1], or_19_out);  // AND_Gate
  or or_20 (or_20_out, and_37_out, and_42_out);
  and and_38 (and_38_out, Bit3_Shift[2], or_23_out);
  and and_39 (and_39_out, ~Bit3_Shift[2], or_20_out);  // AND_Gate
  or or_21 (Bit32_Result[6], and_39_out, and_59_out);
  and and_40 (and_40_out, ~Bit3_Shift[0], Bit32_In[7]);  // AND_Gate
  or or_22 (or_22_out, and_40_out, and_45_out);
  and and_41 (and_41_out, ~Bit3_Shift[1], or_22_out);  // AND_Gate
  and and_42 (and_42_out, Bit3_Shift[1], or_25_out);
  or or_23 (or_23_out, and_41_out, and_52_out);
  and and_43 (and_43_out, ~Bit3_Shift[2], or_23_out);  // AND_Gate
  and and_44 (and_44_out, Bit3_Shift[2], or_26_out);
  or or_24 (Bit32_Result[7], and_43_out, and_65_out);
  and and_45 (and_45_out, Bit3_Shift[0], Bit32_In[8]);
  and and_46 (and_46_out, ~Bit3_Shift[0], Bit32_In[8]);  // AND_Gate
  or or_25 (or_25_out, and_46_out, and_50_out);
  and and_47 (and_47_out, ~Bit3_Shift[1], or_25_out);  // AND_Gate
  or or_26 (or_26_out, and_47_out, and_57_out);
  and and_48 (and_48_out, ~Bit3_Shift[2], or_26_out);  // AND_Gate
  and and_49 (and_49_out, Bit3_Shift[2], or_29_out);
  or or_27 (Bit32_Result[8], and_48_out, and_70_out);
  and and_50 (and_50_out, Bit3_Shift[0], Bit32_In[9]);
  and and_51 (and_51_out, ~Bit3_Shift[0], Bit32_In[9]);  // AND_Gate
  or or_28 (or_28_out, and_51_out, and_55_out);
  and and_52 (and_52_out, Bit3_Shift[1], or_28_out);
  and and_53 (and_53_out, ~Bit3_Shift[1], or_28_out);  // AND_Gate
  or or_29 (or_29_out, and_53_out, and_63_out);
  and and_54 (and_54_out, ~Bit3_Shift[2], or_29_out);  // AND_Gate
  or or_30 (Bit32_Result[9], and_54_out, and_75_out);
  and and_55 (and_55_out, Bit3_Shift[0], Bit32_In[10]);
  and and_56 (and_56_out, ~Bit3_Shift[0], Bit32_In[10]);  // AND_Gate
  or or_31 (or_31_out, and_56_out, and_61_out);
  and and_57 (and_57_out, Bit3_Shift[1], or_31_out);
  and and_58 (and_58_out, ~Bit3_Shift[1], or_31_out);  // AND_Gate
  or or_32 (or_32_out, and_58_out, and_68_out);
  and and_59 (and_59_out, Bit3_Shift[2], or_32_out);
  and and_60 (and_60_out, ~Bit3_Shift[2], or_32_out);  // AND_Gate
  or or_33 (Bit32_Result[10], and_60_out, and_81_out);
  and and_61 (and_61_out, Bit3_Shift[0], Bit32_In[11]);
  and and_62 (and_62_out, ~Bit3_Shift[0], Bit32_In[11]);  // AND_Gate
  and and_63 (and_63_out, Bit3_Shift[1], or_36_out);
  and and_64 (and_64_out, ~Bit3_Shift[1], or_36_out);  // AND_Gate
  or or_34 (or_34_out, and_64_out, and_74_out);
  and and_65 (and_65_out, Bit3_Shift[2], or_34_out);
  and and_66 (and_66_out, ~Bit3_Shift[2], or_34_out);  // AND_Gate
  or or_35 (Bit32_Result[11], and_66_out, and_87_out);
  and and_67 (and_67_out, Bit3_Shift[0], Bit32_In[12]);
  or or_36 (or_36_out, and_62_out, and_67_out);
  and and_68 (and_68_out, Bit3_Shift[1], or_38_out);
  and and_69 (and_69_out, ~Bit3_Shift[1], or_38_out);  // AND_Gate
  and and_70 (and_70_out, Bit3_Shift[2], or_39_out);
  and and_71 (and_71_out, ~Bit3_Shift[2], or_39_out);  // AND_Gate
  or or_37 (Bit32_Result[12], and_71_out, and_92_out);
  and and_72 (and_72_out, ~Bit3_Shift[0], Bit32_In[12]);  // AND_Gate
  and and_73 (and_73_out, Bit3_Shift[0], Bit32_In[13]);
  or or_38 (or_38_out, and_72_out, and_73_out);
  and and_74 (and_74_out, Bit3_Shift[1], or_40_out);
  or or_39 (or_39_out, and_69_out, and_80_out);
  and and_75 (and_75_out, Bit3_Shift[2], or_41_out);
  and and_76 (and_76_out, ~Bit3_Shift[2], or_41_out);  // AND_Gate
  and and_77 (and_77_out, ~Bit3_Shift[0], Bit32_In[13]);  // AND_Gate
  and and_78 (and_78_out, Bit3_Shift[0], Bit32_In[14]);
  or or_40 (or_40_out, and_77_out, and_78_out);
  and and_79 (and_79_out, ~Bit3_Shift[1], or_40_out);  // AND_Gate
  and and_80 (and_80_out, Bit3_Shift[1], or_43_out);
  or or_41 (or_41_out, and_79_out, and_85_out);
  and and_81 (and_81_out, Bit3_Shift[2], or_44_out);
  or or_42 (Bit32_Result[13], and_76_out, and_97_out);
  and and_82 (and_82_out, ~Bit3_Shift[0], Bit32_In[14]);  // AND_Gate
  and and_83 (and_83_out, Bit3_Shift[0], Bit32_In[15]);
  or or_43 (or_43_out, and_82_out, and_83_out);
  and and_84 (and_84_out, ~Bit3_Shift[1], or_43_out);  // AND_Gate
  and and_85 (and_85_out, Bit3_Shift[1], or_46_out);
  or or_44 (or_44_out, and_84_out, and_90_out);
  and and_86 (and_86_out, ~Bit3_Shift[2], or_44_out);  // AND_Gate
  and and_87 (and_87_out, Bit3_Shift[2], or_47_out);
  or or_45 (Bit32_Result[14], and_86_out, and_107_out);
  and and_88 (and_88_out, ~Bit3_Shift[0], Bit32_In[15]);  // AND_Gate
  or or_46 (or_46_out, and_88_out, and_93_out);
  and and_89 (and_89_out, ~Bit3_Shift[1], or_46_out);  // AND_Gate
  and and_90 (and_90_out, Bit3_Shift[1], or_49_out);
  or or_47 (or_47_out, and_89_out, and_100_out);
  and and_91 (and_91_out, ~Bit3_Shift[2], or_47_out);  // AND_Gate
  and and_92 (and_92_out, Bit3_Shift[2], or_50_out);
  or or_48 (Bit32_Result[15], and_91_out, and_113_out);
  and and_93 (and_93_out, Bit3_Shift[0], Bit32_In[16]);
  and and_94 (and_94_out, ~Bit3_Shift[0], Bit32_In[16]);  // AND_Gate
  or or_49 (or_49_out, and_94_out, and_98_out);
  and and_95 (and_95_out, ~Bit3_Shift[1], or_49_out);  // AND_Gate
  or or_50 (or_50_out, and_95_out, and_105_out);
  and and_96 (and_96_out, ~Bit3_Shift[2], or_50_out);  // AND_Gate
  and and_97 (and_97_out, Bit3_Shift[2], or_53_out);
  or or_51 (Bit32_Result[16], and_96_out, and_118_out);
  and and_98 (and_98_out, Bit3_Shift[0], Bit32_In[17]);
  and and_99 (and_99_out, ~Bit3_Shift[0], Bit32_In[17]);  // AND_Gate
  or or_52 (or_52_out, and_99_out, and_103_out);
  and and_100 (and_100_out, Bit3_Shift[1], or_52_out);
  and and_101 (and_101_out, ~Bit3_Shift[1], or_52_out);  // AND_Gate
  or or_53 (or_53_out, and_101_out, and_111_out);
  and and_102 (and_102_out, ~Bit3_Shift[2], or_53_out);  // AND_Gate
  or or_54 (Bit32_Result[17], and_102_out, and_123_out);
  and and_103 (and_103_out, Bit3_Shift[0], Bit32_In[18]);
  and and_104 (and_104_out, ~Bit3_Shift[0], Bit32_In[18]);  // AND_Gate
  or or_55 (or_55_out, and_104_out, and_109_out);
  and and_105 (and_105_out, Bit3_Shift[1], or_55_out);
  and and_106 (and_106_out, ~Bit3_Shift[1], or_55_out);  // AND_Gate
  or or_56 (or_56_out, and_106_out, and_116_out);
  and and_107 (and_107_out, Bit3_Shift[2], or_56_out);
  and and_108 (and_108_out, ~Bit3_Shift[2], or_56_out);  // AND_Gate
  or or_57 (Bit32_Result[18], and_108_out, and_129_out);
  and and_109 (and_109_out, Bit3_Shift[0], Bit32_In[19]);
  and and_110 (and_110_out, ~Bit3_Shift[0], Bit32_In[19]);  // AND_Gate
  and and_111 (and_111_out, Bit3_Shift[1], or_60_out);
  and and_112 (and_112_out, ~Bit3_Shift[1], or_60_out);  // AND_Gate
  or or_58 (or_58_out, and_112_out, and_122_out);
  and and_113 (and_113_out, Bit3_Shift[2], or_58_out);
  and and_114 (and_114_out, ~Bit3_Shift[2], or_58_out);  // AND_Gate
  or or_59 (Bit32_Result[19], and_114_out, and_135_out);
  and and_115 (and_115_out, Bit3_Shift[0], Bit32_In[20]);
  or or_60 (or_60_out, and_110_out, and_115_out);
  and and_116 (and_116_out, Bit3_Shift[1], or_62_out);
  and and_117 (and_117_out, ~Bit3_Shift[1], or_62_out);  // AND_Gate
  and and_118 (and_118_out, Bit3_Shift[2], or_63_out);
  and and_119 (and_119_out, ~Bit3_Shift[2], or_63_out);  // AND_Gate
  or or_61 (Bit32_Result[20], and_119_out, and_140_out);
  and and_120 (and_120_out, ~Bit3_Shift[0], Bit32_In[20]);  // AND_Gate
  and and_121 (and_121_out, Bit3_Shift[0], Bit32_In[21]);
  or or_62 (or_62_out, and_120_out, and_121_out);
  and and_122 (and_122_out, Bit3_Shift[1], or_64_out);
  or or_63 (or_63_out, and_117_out, and_128_out);
  and and_123 (and_123_out, Bit3_Shift[2], or_65_out);
  and and_124 (and_124_out, ~Bit3_Shift[2], or_65_out);  // AND_Gate
  and and_125 (and_125_out, ~Bit3_Shift[0], Bit32_In[21]);  // AND_Gate
  and and_126 (and_126_out, Bit3_Shift[0], Bit32_In[22]);
  or or_64 (or_64_out, and_125_out, and_126_out);
  and and_127 (and_127_out, ~Bit3_Shift[1], or_64_out);  // AND_Gate
  and and_128 (and_128_out, Bit3_Shift[1], or_67_out);
  or or_65 (or_65_out, and_127_out, and_133_out);
  and and_129 (and_129_out, Bit3_Shift[2], or_68_out);
  or or_66 (Bit32_Result[21], and_124_out, and_145_out);
  and and_130 (and_130_out, ~Bit3_Shift[0], Bit32_In[22]);  // AND_Gate
  and and_131 (and_131_out, Bit3_Shift[0], Bit32_In[23]);
  or or_67 (or_67_out, and_130_out, and_131_out);
  and and_132 (and_132_out, ~Bit3_Shift[1], or_67_out);  // AND_Gate
  and and_133 (and_133_out, Bit3_Shift[1], or_70_out);
  or or_68 (or_68_out, and_132_out, and_138_out);
  and and_134 (and_134_out, ~Bit3_Shift[2], or_68_out);  // AND_Gate
  and and_135 (and_135_out, Bit3_Shift[2], or_71_out);
  or or_69 (Bit32_Result[22], and_134_out, and_155_out);
  and and_136 (and_136_out, ~Bit3_Shift[0], Bit32_In[23]);  // AND_Gate
  or or_70 (or_70_out, and_136_out, and_141_out);
  and and_137 (and_137_out, ~Bit3_Shift[1], or_70_out);  // AND_Gate
  and and_138 (and_138_out, Bit3_Shift[1], or_73_out);
  or or_71 (or_71_out, and_137_out, and_148_out);
  and and_139 (and_139_out, ~Bit3_Shift[2], or_71_out);  // AND_Gate
  and and_140 (and_140_out, Bit3_Shift[2], or_74_out);
  or or_72 (Bit32_Result[23], and_139_out, and_161_out);
  and and_141 (and_141_out, Bit3_Shift[0], Bit32_In[24]);
  and and_142 (and_142_out, ~Bit3_Shift[0], Bit32_In[24]);  // AND_Gate
  or or_73 (or_73_out, and_142_out, and_146_out);
  and and_143 (and_143_out, ~Bit3_Shift[1], or_73_out);  // AND_Gate
  or or_74 (or_74_out, and_143_out, and_153_out);
  and and_144 (and_144_out, ~Bit3_Shift[2], or_74_out);  // AND_Gate
  and and_145 (and_145_out, Bit3_Shift[2], or_77_out);
  or or_75 (Bit32_Result[24], and_144_out, and_166_out);
  and and_146 (and_146_out, Bit3_Shift[0], Bit32_In[25]);
  and and_147 (and_147_out, ~Bit3_Shift[0], Bit32_In[25]);  // AND_Gate
  or or_76 (or_76_out, and_147_out, and_151_out);
  and and_148 (and_148_out, Bit3_Shift[1], or_76_out);
  and and_149 (and_149_out, ~Bit3_Shift[1], or_76_out);  // AND_Gate
  or or_77 (or_77_out, and_149_out, and_159_out);
  and and_150 (and_150_out, ~Bit3_Shift[2], or_77_out);  // AND_Gate
  or or_78 (Bit32_Result[25], and_150_out, and_171_out);
  and and_151 (and_151_out, Bit3_Shift[0], Bit32_In[26]);
  and and_152 (and_152_out, ~Bit3_Shift[0], Bit32_In[26]);  // AND_Gate
  or or_79 (or_79_out, and_152_out, and_157_out);
  and and_153 (and_153_out, Bit3_Shift[1], or_79_out);
  and and_154 (and_154_out, ~Bit3_Shift[1], or_79_out);  // AND_Gate
  or or_80 (or_80_out, and_154_out, and_164_out);
  and and_155 (and_155_out, Bit3_Shift[2], or_80_out);
  and and_156 (and_156_out, ~Bit3_Shift[2], or_80_out);  // AND_Gate
  or or_81 (Bit32_Result[26], and_156_out, and_177_out);
  and and_157 (and_157_out, Bit3_Shift[0], Bit32_In[27]);
  and and_158 (and_158_out, ~Bit3_Shift[0], Bit32_In[27]);  // AND_Gate
  and and_159 (and_159_out, Bit3_Shift[1], or_84_out);
  and and_160 (and_160_out, ~Bit3_Shift[1], or_84_out);  // AND_Gate
  or or_82 (or_82_out, and_160_out, and_170_out);
  and and_161 (and_161_out, Bit3_Shift[2], or_82_out);
  and and_162 (and_162_out, ~Bit3_Shift[2], or_82_out);  // AND_Gate
  or or_83 (Bit32_Result[27], and_162_out, and_183_out);
  and and_163 (and_163_out, Bit3_Shift[0], Bit32_In[28]);
  or or_84 (or_84_out, and_158_out, and_163_out);
  and and_164 (and_164_out, Bit3_Shift[1], or_85_out);
  and and_165 (and_165_out, ~Bit3_Shift[1], or_85_out);  // AND_Gate
  and and_166 (and_166_out, Bit3_Shift[2], or_86_out);
  and and_167 (Bit32_Result[28], ~Bit3_Shift[2], or_86_out);  // AND_Gate
  and and_168 (and_168_out, ~Bit3_Shift[0], Bit32_In[28]);  // AND_Gate
  and and_169 (and_169_out, Bit3_Shift[0], Bit32_In[29]);
  or or_85 (or_85_out, and_168_out, and_169_out);
  and and_170 (and_170_out, Bit3_Shift[1], or_87_out);
  or or_86 (or_86_out, and_165_out, and_176_out);
  and and_171 (and_171_out, Bit3_Shift[2], or_88_out);
  and and_172 (Bit32_Result[29], ~Bit3_Shift[2], or_88_out);  // AND_Gate
  and and_173 (and_173_out, ~Bit3_Shift[0], Bit32_In[29]);  // AND_Gate
  and and_174 (and_174_out, Bit3_Shift[0], Bit32_In[30]);
  or or_87 (or_87_out, and_173_out, and_174_out);
  and and_175 (and_175_out, ~Bit3_Shift[1], or_87_out);  // AND_Gate
  and and_176 (and_176_out, Bit3_Shift[1], or_89_out);
  or or_88 (or_88_out, and_175_out, and_181_out);
  and and_177 (and_177_out, Bit3_Shift[2], and_180_out);
  and and_178 (and_178_out, ~Bit3_Shift[0], Bit32_In[30]);  // AND_Gate
  and and_179 (and_179_out, Bit3_Shift[0], Bit32_In[31]);
  or or_89 (or_89_out, and_178_out, and_179_out);
  and and_180 (and_180_out, ~Bit3_Shift[1], or_89_out);  // AND_Gate
  and and_181 (and_181_out, Bit3_Shift[1], and_184_out);
  and and_182 (Bit32_Result[30], ~Bit3_Shift[2], and_180_out);  // AND_Gate
  and and_183 (and_183_out, Bit3_Shift[2], and_185_out);
  and and_184 (and_184_out, ~Bit3_Shift[0], Bit32_In[31]);  // AND_Gate
  and and_185 (and_185_out, ~Bit3_Shift[1], and_184_out);  // AND_Gate
  and and_186 (Bit32_Result[31], ~Bit3_Shift[2], and_185_out);  // AND_Gate
endmodule

module Address_Generation_Unit (
  input  [2:0] Scale,
  input  [31:0] Bit32_Base,
  input  [31:0] Bit32_Immediate,
  input  [31:0] Bit32_Index,
  output [26:0] Bit27_Address
);

  wire [31:0] bit32_adder_1_bit32_result, bit32_adder_2_bit32_result, bit32_x_bit3_right_shift_1_bit32_result;

  Bit32_X_Bit3_Right_Shift bit32_x_bit3_right_shift_1 (
    .Bit32_In(Bit32_Index), .Bit3_Shift(Scale), .Bit32_Result(bit32_x_bit3_right_shift_1_bit32_result));
  Bit32_Adder bit32_adder_1 (
    .Bit32_A(Bit32_Base), .Bit32_B(Bit32_Immediate), .Bit32_Result(bit32_adder_1_bit32_result));  // open: C_In, C_OUT
  Bit32_Adder bit32_adder_2 (
    .Bit32_A(bit32_x_bit3_right_shift_1_bit32_result), .Bit32_B(bit32_adder_1_bit32_result),
    .Bit32_Result(bit32_adder_2_bit32_result));  // open: C_In, C_OUT
  Bit_Extender #(.in_width(32), .out_width(27), .\type ("zero")) bit_extender_1 (
    .in(bit32_adder_2_bit32_result), .out(Bit27_Address));
endmodule

module Wide_Register_File (
  input  [31:0] Bit32_Write_Data,
  input  Write_Enable,
  input  [1:0] Write_Address,
  input  Read_A_Enable,
  input  [1:0] Read_A_Address,
  input  Read_B_Enable,
  input  [1:0] Read_B_Address,
  input  Read_C_Enable,
  input  [1:0] Read_C_Address,
  input  Clock,
  input  Reset,
  output [31:0] Bit32_Read_Line_C,
  output [31:0] Bit32_Read_Line_B,
  output [31:0] Bit32_Read_Line_A
);

  wire demultiplexer_1_out0, demultiplexer_1_out1, demultiplexer_1_out2, demultiplexer_1_out3,
       demultiplexer_2_out0, demultiplexer_2_out1, demultiplexer_2_out2, demultiplexer_2_out3,
       demultiplexer_3_out0, demultiplexer_3_out1, demultiplexer_3_out2, demultiplexer_3_out3,
       demultiplexer_4_out0, demultiplexer_4_out1, demultiplexer_4_out2, demultiplexer_4_out3;
  wire [31:0] Bit32_Register_1_q, Bit32_Register_2_q, Bit32_Register_3_q, Bit32_Register_4_q;

  Demultiplexer #(.select(2)) demultiplexer_1 (
    .out0(demultiplexer_1_out0), .out1(demultiplexer_1_out1), .out2(demultiplexer_1_out2),
    .out3(demultiplexer_1_out3), .in(Write_Enable), .sel(Write_Address));
  Register #(.width(32)) Bit32_Register_1 (
    .D(Bit32_Write_Data), .en(demultiplexer_1_out0), .clk(Clock), .Q(Bit32_Register_1_q), .clr(Reset));
  Register #(.width(32)) Bit32_Register_2 (
    .D(Bit32_Write_Data), .en(demultiplexer_1_out1), .clk(Clock), .Q(Bit32_Register_2_q), .clr(Reset));
  Register #(.width(32)) Bit32_Register_3 (
    .D(Bit32_Write_Data), .en(demultiplexer_1_out2), .clk(Clock), .Q(Bit32_Register_3_q), .clr(Reset));
  Register #(.width(32)) Bit32_Register_4 (
    .D(Bit32_Write_Data), .en(demultiplexer_1_out3), .clk(Clock), .Q(Bit32_Register_4_q), .clr(Reset));
  assign Bit32_Read_Line_A = demultiplexer_2_out0 ? Bit32_Register_1_q : 32'bz;  // Controlled_Buffer controlled_buffer_1
  assign Bit32_Read_Line_A = demultiplexer_2_out1 ? Bit32_Register_2_q : 32'bz;  // Controlled_Buffer controlled_buffer_2
  assign Bit32_Read_Line_A = demultiplexer_2_out2 ? Bit32_Register_3_q : 32'bz;  // Controlled_Buffer controlled_buffer_3
  assign Bit32_Read_Line_A = demultiplexer_2_out3 ? Bit32_Register_4_q : 32'bz;  // Controlled_Buffer controlled_buffer_4
  Demultiplexer #(.select(2)) demultiplexer_2 (
    .out0(demultiplexer_2_out0), .out1(demultiplexer_2_out1), .out2(demultiplexer_2_out2),
    .out3(demultiplexer_2_out3), .in(Read_A_Enable), .sel(Read_A_Address));
  Pull_Resistor pull_resistor_1 (.node(Bit32_Read_Line_A));
  assign Bit32_Read_Line_B = demultiplexer_3_out0 ? Bit32_Register_1_q : 32'bz;  // Controlled_Buffer controlled_buffer_5
  assign Bit32_Read_Line_B = demultiplexer_3_out1 ? Bit32_Register_2_q : 32'bz;  // Controlled_Buffer controlled_buffer_6
  assign Bit32_Read_Line_B = demultiplexer_3_out2 ? Bit32_Register_3_q : 32'bz;  // Controlled_Buffer controlled_buffer_7
  assign Bit32_Read_Line_B = demultiplexer_3_out3 ? Bit32_Register_4_q : 32'bz;  // Controlled_Buffer controlled_buffer_8
  Demultiplexer #(.select(2)) demultiplexer_3 (
    .out0(demultiplexer_3_out0), .out1(demultiplexer_3_out1), .out2(demultiplexer_3_out2),
    .out3(demultiplexer_3_out3), .in(Read_B_Enable), .sel(Read_B_Address));
  Pull_Resistor pull_resistor_2 (.node(Bit32_Read_Line_B));
  Demultiplexer #(.select(2)) demultiplexer_4 (
    .out0(demultiplexer_4_out0), .out1(demultiplexer_4_out1), .out2(demultiplexer_4_out2),
    .out3(demultiplexer_4_out3), .in(Read_C_Enable), .sel(Read_C_Address));
  assign Bit32_Read_Line_C = demultiplexer_4_out0 ? Bit32_Register_1_q : 32'bz;  // Controlled_Buffer controlled_buffer_9
  assign Bit32_Read_Line_C = demultiplexer_4_out1 ? Bit32_Register_2_q : 32'bz;  // Controlled_Buffer controlled_buffer_10
  assign Bit32_Read_Line_C = demultiplexer_4_out2 ? Bit32_Register_3_q : 32'bz;  // Controlled_Buffer controlled_buffer_11
  assign Bit32_Read_Line_C = demultiplexer_4_out3 ? Bit32_Register_4_q : 32'bz;  // Controlled_Buffer controlled_buffer_12
  Pull_Resistor pull_resistor_3 (.node(Bit32_Read_Line_C));

  // Other names for the same wires on the sheet: RAAD[1:0] = Read_A_Address; RAEN = Read_A_Enable;
  //   RBAD[1:0] = Read_B_Address; RBEN = Read_B_Enable; RCAD[1:0] = Read_C_Address; RCEN = Read_C_Enable

  // Notes on the sheet:
  //   0 = low 16, 1 = high 16
endmodule

module MMU_DEMO (
  input  ALC,
  input  DLC,
  input  TRA,
  input  CTSWTCH,
  input  B2OI,
  input  [26:0] VADD,
  input  [7:0] CID,
  input  ENB,
  input  CLK,
  input  RST
);

  wire mmu2_1_p7, mmu2_1_p11, mmu2_1_p12, mmu2_1_p13, mmu2_1_p14, mmu2_1_p15;

  // MMU2 mmu2_1: pin names not known; wires that end beside it: ALC, DLC, TRA, CTSWTCH, B2OI, VADD, mmu2_1_p7, CID, RST, ENB, mmu2_1_p11, mmu2_1_p12, mmu2_1_p13, mmu2_1_p14, mmu2_1_p15, CLK
  // Memory_Controller memory_controller_1: pin names not known; wires that end beside it: mmu2_1_p12, mmu2_1_p11, mmu2_1_p13, mmu2_1_p14, mmu2_1_p15, CLK, RST, mmu2_1_p7
endmodule

module ALU_Flag_Register_File (
  input  [4:0] Bit5_Float_Flag_Mask,
  input  Float_Flag_Raise,
  input  Float_Flag_Lower,
  input  Reset_Int_Div_By_Zero,
  input  FLT_Inexact,
  input  FLT_Overflow,
  input  FLT_Underflow,
  input  FLT_DBZ,
  input  FLT_INVALOP,
  input  Int_DBZ,
  input  Carry,
  input  INT_OVFLW,
  input  Zero,
  input  Negative,
  input  Alu_Flag_Setting_Operation,
  input  Clock,
  input  Reset,
  output STATE_FLT_Inexact,
  output STATE_FLT_Overflow,
  output STATE_FLT_Underflow,
  output STATE_FLT_Divide_By_Zero,
  output STATE_FLT_Invalid_Operation,
  output STATE_Int_Divide_By_Zero,
  output STATE_Int_Carry,
  output STATE_Int_Overflow,
  output STATE_Zero,
  output STATE_Negative
);

  wire and_1_out, and_2_out, and_3_out, and_4_out, and_5_out, and_6_out, and_7_out, and_8_out, and_9_out,
       and_10_out, and_11_out, and_12_out, and_13_out, and_14_out, and_15_out, and_16_out, and_17_out,
       and_18_out, or_1_out, or_2_out, or_3_out, or_4_out, or_5_out, or_6_out, or_7_out, or_8_out, or_9_out,
       or_10_out, or_11_out;

  J_K_Flip_Flop j_k_ff_1 ();  // open: J, K, clk, Q, Qn, preset, reset
  // ALU3 alu3_1: pin names not known
  and and_1 (and_1_out, Bit5_Float_Flag_Mask[0], Float_Flag_Raise);
  or or_1 (or_1_out, and_1_out, FLT_INVALOP);
  and and_2 (and_2_out, Bit5_Float_Flag_Mask[0], Float_Flag_Lower);
  or or_2 (or_2_out, and_2_out, Reset);
  and and_3 (and_3_out, Bit5_Float_Flag_Mask[1], Float_Flag_Raise);
  or or_3 (or_3_out, and_3_out, FLT_DBZ);
  and and_4 (and_4_out, Bit5_Float_Flag_Mask[1], Float_Flag_Lower);
  or or_4 (or_4_out, and_4_out, Reset);
  and and_5 (and_5_out, Bit5_Float_Flag_Mask[2], Float_Flag_Raise);
  or or_5 (or_5_out, and_5_out, FLT_Underflow);
  and and_6 (and_6_out, Bit5_Float_Flag_Mask[2], Float_Flag_Lower);
  or or_6 (or_6_out, and_6_out, Reset);
  and and_7 (and_7_out, Bit5_Float_Flag_Mask[3], Float_Flag_Raise);
  or or_7 (or_7_out, and_7_out, FLT_Overflow);
  and and_8 (and_8_out, Bit5_Float_Flag_Mask[3], Float_Flag_Lower);
  or or_8 (or_8_out, and_8_out, Reset);
  and and_9 (and_9_out, Bit5_Float_Flag_Mask[4], Float_Flag_Raise);
  or or_9 (or_9_out, and_9_out, FLT_Inexact);
  and and_10 (and_10_out, Bit5_Float_Flag_Mask[4], Float_Flag_Lower);
  or or_10 (or_10_out, and_10_out, Reset);
  S_R_Flip_Flop Float_Invalid (
    .S(or_1_out), .R(or_2_out), .clk(Clock), .Q(STATE_FLT_Invalid_Operation));  // open: reset, Qn, preset
  S_R_Flip_Flop Float_Divide_By_0 (
    .S(or_3_out), .R(or_4_out), .clk(Clock), .Q(STATE_FLT_Divide_By_Zero));  // open: reset, Qn, preset
  S_R_Flip_Flop Float_Underflow (
    .S(or_5_out), .R(or_6_out), .clk(Clock), .Q(STATE_FLT_Underflow));  // open: reset, Qn, preset
  S_R_Flip_Flop Float_Overflow (
    .S(or_7_out), .R(or_8_out), .clk(Clock), .Q(STATE_FLT_Overflow));  // open: reset, Qn, preset
  S_R_Flip_Flop Float_Inexact (
    .S(or_9_out), .R(or_10_out), .clk(Clock), .Q(STATE_FLT_Inexact));  // open: reset, Qn, preset
  S_R_Flip_Flop Int_Divide_By_Zero (
    .S(Int_DBZ), .R(or_11_out), .clk(Clock), .Q(STATE_Int_Divide_By_Zero));  // open: reset, Qn, preset
  or or_11 (or_11_out, Reset, Reset_Int_Div_By_Zero);
  and and_11 (and_11_out, Carry, Alu_Flag_Setting_Operation);
  S_R_Flip_Flop Int_Carry (
    .S(and_11_out), .R(and_12_out), .clk(Clock), .Q(STATE_Int_Carry), .reset(Reset));  // open: Qn, preset
  and and_12 (and_12_out, Alu_Flag_Setting_Operation, ~Carry);  // AND_Gate
  and and_13 (and_13_out, INT_OVFLW, Alu_Flag_Setting_Operation);
  S_R_Flip_Flop Int_Overflow (
    .S(and_13_out), .R(and_14_out), .clk(Clock), .Q(STATE_Int_Overflow), .reset(Reset));  // open: Qn, preset
  and and_14 (and_14_out, Alu_Flag_Setting_Operation, ~INT_OVFLW);  // AND_Gate
  and and_15 (and_15_out, Zero, Alu_Flag_Setting_Operation);
  S_R_Flip_Flop Z (.S(and_15_out), .R(and_16_out), .clk(Clock), .Q(STATE_Zero), .reset(Reset));  // open: Qn, preset
  and and_16 (and_16_out, Alu_Flag_Setting_Operation, ~Zero);  // AND_Gate
  and and_17 (and_17_out, Negative, Alu_Flag_Setting_Operation);
  S_R_Flip_Flop Neg (
    .S(and_17_out), .R(and_18_out), .clk(Clock), .Q(STATE_Negative), .reset(Reset));  // open: Qn, preset
  and and_18 (and_18_out, Alu_Flag_Setting_Operation, ~Negative);  // AND_Gate

  // Notes on the sheet:
  //   includes alu and flag setting
endmodule

module Instruction_Cache_2_Way (
  input  Read,
  input  Two_Byte_Operation,
  input  Invalidate_Address,
  input  Invalidate_Line,
  input  Set,
  input  [25:0] Bit26_Address,
  input  [7:0] Bit8_From_Memory,
  input  Ram_Data_Moving,
  input  Clock,
  input  Reset,
  output [15:0] Bit16_To_Core,
  output Ram_Read,
  output Requesting_Ram,
  output RWDS
);

  wire A_Change, A_Dirty, A_Evict, A_Hit, A_Miss, A_Valid, and_1_out, and_2_out, and_3_out, and_4_out,
       and_5_out, and_6_out, and_7_out, and_8_out, and_9_out, and_10_out, and_11_out, and_12_out, and_13_out,
       and_14_out, and_15_out, and_16_out, and_17_out, and_18_out, and_19_out, and_21_out, and_25_out,
       and_26_out, and_27_out, and_29_out, B_Change, B_Dirty, B_Evict, B_Hit, B_LRU, B_Miss, B_Valid,
       comparator_1_eq, comparator_2_eq, d_ff_1_q, d_ff_2_q, d_ff_3_q, d_ff_4_q, d_ff_5_q, d_ff_6_q,
       d_ff_7_q, d_ff_8_q, d_ff_9_q, FE_Clock, Hit, Invalid_Operation, nand_1_out, nand_2_out, not_1_out,
       Operation, or_3_out, or_4_out, or_6_out, or_9_out, or_10_out, PSRAM_Clock, RE_Clock, Tag_Write_Enable;
  wire [2:0] adder_1_out, Burst_Stage, multiplexer_1_out;
  wire [3:0] Address_Line_Offset;
  wire [7:0] ram_1_dout, ram_2_dout, ram_3_dout, ram_4_dout, register_1_q, register_2_q;
  wire [9:0] Address_Tag;
  wire [11:0] Address_Index;
  wire [12:0] Old_Tag_A, Old_Tag_B;
  wire [13:13] Tag_A;
  wire [14:0] bit_extender_1_out;
  wire [15:0] multiplexer_2_out, multiplexer_3_out, register_3_q, register_4_q;
  wire [15:15] New_Tag;

  or or_1 (Operation, Read, Invalidate_Address, Invalidate_Line);
  nor nor_1 (New_Tag[15], Invalidate_Address, Invalidate_Line);
  or or_2 (Invalid_Operation, Invalidate_Line, Invalidate_Address);
  Memory_Clock memory_clock_1 (
    .Clock(Clock), .Reset(Reset), .RE_Clock(RE_Clock), .PSRAM_Clock(PSRAM_Clock), .FE_Clock(FE_Clock));  // open: CPU_Clock
  or or_3 (or_3_out, Reset, ~Ram_Data_Moving);  // OR_Gate
  Counter #(.max('h7), .trigger("falling"), .width(3)) counter_1 (
    .clr(or_3_out), .up(d_ff_1_q), .count(d_ff_1_q), .clk(FE_Clock), .Q(Burst_Stage));  // open: load, D, carry
  // Probe on Bit8_From_Memory
  // Probe on Bit8_From_Memory
  D_Flip_Flop d_ff_1 (.D(and_1_out), .clk(RE_Clock), .Q(d_ff_1_q), .reset(not_1_out));  // open: Qn, preset
  and and_1 (and_1_out, Ram_Data_Moving, or_4_out);
  or or_4 (or_4_out, d_ff_1_q, Ram_Read);
  not not_1 (not_1_out, Ram_Data_Moving);
  and and_2 (and_2_out, ~FE_Clock, Ram_Data_Moving, Ram_Read);  // AND_Gate
  and and_3 (and_3_out, FE_Clock, Ram_Data_Moving, Ram_Read);
  and and_4 (and_4_out, Ram_Data_Moving, Ram_Read, RE_Clock, A_Evict);
  Register #(.trigger("falling")) register_1 (
    .D(Bit8_From_Memory), .en(and_2_out), .clk(PSRAM_Clock), .Q(register_1_q), .clr(Reset));
  Register register_2 (.D(Bit8_From_Memory), .en(and_3_out), .clk(PSRAM_Clock), .Q(register_2_q), .clr(Reset));
  and and_5 (and_5_out, Two_Byte_Operation, Address_Line_Offset[0]);
  Adder #(.width(3)) adder_1 (.a(multiplexer_1_out), .b(3'b000), .out(adder_1_out), .cin(and_5_out));  // open: cout
  Multiplexer #(.width(3)) multiplexer_1 (
    .in0(Burst_Stage), .in1(Address_Line_Offset[3:1]), .out(multiplexer_1_out), .sel(and_6_out));
  RAM #(.addrWidth(15), .trigger("high")) ram_1 (
    .addr({Address_Index, multiplexer_1_out}), .we(and_4_out), .oe(Read), .din(register_1_q),
    .dout(ram_1_dout));
  RAM #(.addrWidth(15), .trigger("high")) ram_2 (
    .addr({Address_Index, adder_1_out}), .we(and_4_out), .oe(Read), .din(register_2_q), .dout(ram_2_dout));
  assign Bit16_To_Core[7:0] = d_ff_5_q ? ram_1_dout : 8'bz;  // Controlled_Buffer controlled_buffer_1
  assign Bit16_To_Core[15:8] = d_ff_4_q ? ram_1_dout : 8'bz;  // Controlled_Buffer controlled_buffer_2
  assign Bit16_To_Core[7:0] = d_ff_3_q ? ram_2_dout : 8'bz;  // Controlled_Buffer controlled_buffer_3
  assign Bit16_To_Core[15:8] = d_ff_2_q ? ram_2_dout : 8'bz;  // Controlled_Buffer controlled_buffer_4
  and and_6 (and_6_out, Operation, Hit);
  and and_7 (and_7_out, A_Hit, ~Address_Line_Offset[0]);  // AND_Gate
  D_Flip_Flop d_ff_2 (.D(and_7_out), .clk(Clock), .Q(d_ff_2_q), .reset(Reset));  // open: Qn, preset
  and and_8 (and_8_out, A_Hit, Address_Line_Offset[0]);
  D_Flip_Flop d_ff_3 (.D(and_8_out), .clk(Clock), .Q(d_ff_3_q), .reset(Reset));  // open: Qn, preset
  and and_9 (and_9_out, A_Hit, Address_Line_Offset[0]);
  D_Flip_Flop d_ff_4 (.D(and_9_out), .clk(Clock), .Q(d_ff_4_q), .reset(Reset));  // open: Qn, preset
  D_Flip_Flop d_ff_5 (.D(and_10_out), .clk(Clock), .Q(d_ff_5_q), .reset(Reset));  // open: Qn, preset
  and and_10 (and_10_out, A_Hit, ~Address_Line_Offset[0]);  // AND_Gate
  and and_11 (and_11_out, Ram_Data_Moving, Ram_Read, RE_Clock, B_Change);
  RAM #(.addrWidth(15), .trigger("high")) ram_3 (
    .addr({Address_Index, multiplexer_1_out}), .we(and_11_out), .oe(Read), .din(register_1_q),
    .dout(ram_3_dout));
  RAM #(.addrWidth(15), .trigger("high")) ram_4 (
    .addr({Address_Index, adder_1_out}), .we(and_11_out), .oe(Read), .din(register_2_q), .dout(ram_4_dout));
  nor nor_2 (Tag_Write_Enable, Burst_Stage[0], Burst_Stage[1], Burst_Stage[2]);
  or or_5 (A_Change, A_Evict, A_Hit);
  and and_12 (and_12_out, Burst_Stage[0], Burst_Stage[1], Burst_Stage[2], RE_Clock, A_Change);
  assign Bit16_To_Core[7:0] = d_ff_9_q ? ram_3_dout : 8'bz;  // Controlled_Buffer controlled_buffer_5
  assign Bit16_To_Core[15:8] = d_ff_8_q ? ram_3_dout : 8'bz;  // Controlled_Buffer controlled_buffer_6
  assign Bit16_To_Core[7:0] = d_ff_7_q ? ram_4_dout : 8'bz;  // Controlled_Buffer controlled_buffer_7
  assign Bit16_To_Core[15:8] = d_ff_6_q ? ram_4_dout : 8'bz;  // Controlled_Buffer controlled_buffer_8
  and and_13 (and_13_out, B_Hit, ~Address_Line_Offset[0]);  // AND_Gate
  and and_14 (and_14_out, ~and_26_out, Operation, A_Hit);  // AND_Gate
  D_Flip_Flop d_ff_6 (.D(and_13_out), .clk(Clock), .Q(d_ff_6_q), .reset(Reset));  // open: Qn, preset
  and and_15 (and_15_out, B_Hit, Address_Line_Offset[0]);
  or or_6 (or_6_out, and_14_out, and_12_out);
  Register #(.width(16)) register_3 (
    .D(multiplexer_2_out), .en(Tag_Write_Enable), .clk(PSRAM_Clock), .Q(register_3_q), .clr(Reset));
  Multiplexer #(.width(16)) multiplexer_2 (
    .in0({A_Valid, A_Dirty, 1'b0, Old_Tag_A}), .in1({New_Tag[15], 1'b0, Read, 3'b000, Address_Tag}),
    .out(multiplexer_2_out), .sel(A_Change));
  D_Flip_Flop d_ff_7 (.D(and_15_out), .clk(Clock), .Q(d_ff_7_q), .reset(Reset));  // open: Qn, preset
  and and_16 (and_16_out, B_Hit, Address_Line_Offset[0]);
  assign bit_extender_1_out = {{3{1'b0}}, Address_Index};  // Bit_Extender bit_extender_1
  Pull_Resistor pull_resistor_1 (.node(or_6_out));
  D_Flip_Flop d_ff_8 (.D(and_16_out), .clk(Clock), .Q(d_ff_8_q), .reset(Reset));  // open: Qn, preset
  RAM #(.addrWidth(15), .clearpin("true"), .dataWidth(16), .trigger("high")) ram_5 (
    .addr(bit_extender_1_out), .we(or_6_out), .oe(Operation), .din(register_3_q),
    .dout({A_Valid, A_Dirty, Tag_A[13], Old_Tag_A}));  // open: clr
  D_Flip_Flop d_ff_9 (.D(and_17_out), .clk(Clock), .Q(d_ff_9_q), .reset(Reset));  // open: Qn, preset
  and and_17 (and_17_out, B_Hit, ~Address_Line_Offset[0]);  // AND_Gate
  Pull_Resistor pull_resistor_2 (.node(Operation));
  Comparator #(.mode("unsigned"), .width(10)) comparator_1 (
    .a(Old_Tag_A[9:0]), .b(Address_Tag), .eq(comparator_1_eq));  // open: gt, lt
  Pull_Resistor pull_resistor_3 (.node({A_Valid, A_Dirty, Tag_A[13], Old_Tag_A}));
  nand nand_1 (nand_1_out, comparator_1_eq, A_Valid);
  and and_18 (and_18_out, Invalidate_Line, ~Set);  // AND_Gate
  and and_19 (and_19_out, Operation, ~Invalidate_Line, comparator_1_eq, A_Valid);  // AND_Gate
  and and_20 (A_Miss, Operation, nand_1_out);
  or or_7 (A_Hit, and_18_out, and_19_out);
  and and_21 (and_21_out, Burst_Stage[0], Burst_Stage[1], Burst_Stage[2], RE_Clock, B_Change);
  or or_8 (B_Change, B_Evict, B_Hit);
  and and_22 (Ram_Read, A_Miss, New_Tag[15], B_Miss);
  or or_9 (or_9_out, and_25_out, and_21_out);
  Multiplexer #(.width(16)) multiplexer_3 (
    .in0({B_Valid, B_Dirty, 1'b0, Old_Tag_B}), .in1({New_Tag[15], 1'b0, Read, 3'b000, Address_Tag}),
    .out(multiplexer_3_out), .sel(B_Change));
  and and_23 (A_Evict, A_Miss, B_Miss, ~1'b0);  // AND_Gate
  Register #(.width(16)) register_4 (
    .D(multiplexer_3_out), .en(Tag_Write_Enable), .clk(PSRAM_Clock), .Q(register_4_q), .clr(Reset));
  and and_24 (B_Evict, A_Miss, B_Miss, 1'b0);
  and and_25 (and_25_out, ~and_26_out, Operation, B_Hit);  // AND_Gate
  RAM #(.addrWidth(15), .clearpin("true"), .dataWidth(16), .trigger("high")) ram_6 (
    .addr(bit_extender_1_out), .we(or_9_out), .oe(Operation), .din(register_4_q),
    .dout({B_Valid, B_Dirty, B_LRU, Old_Tag_B}));  // open: clr
  and and_26 (and_26_out, ~or_10_out, Ram_Read);  // AND_Gate
  or or_10 (or_10_out, Invalidate_Line, Invalidate_Address);
  or or_11 (Hit, A_Hit, B_Hit);
  Pull_Resistor pull_resistor_4 (.node({B_Valid, B_Dirty, B_LRU, Old_Tag_B}));
  Comparator #(.mode("unsigned"), .width(10)) comparator_2 (
    .a(Old_Tag_B[9:0]), .b(Address_Tag), .eq(comparator_2_eq));  // open: gt, lt
  and and_27 (and_27_out, Operation, ~Invalidate_Line, comparator_2_eq, B_Valid);  // AND_Gate
  and and_28 (B_Miss, Operation, nand_2_out);
  nand nand_2 (nand_2_out, comparator_2_eq, B_Valid);
  and and_29 (and_29_out, Invalidate_Line, Set);
  or or_12 (B_Hit, and_29_out, and_27_out);

  assign Requesting_Ram = Ram_Read;
  assign RWDS = Ram_Data_Moving;

  // Other names for the same wires on the sheet: Tag_A (some bits) = {A_Valid, A_Dirty, Old_Tag_A};
  //   Address[25:0] = Bit26_Address; Invalidate_Addr = Invalidate_Address; Memory_Data[7:0] = Bit8_From_Memory;
  //   New_Tag (some bits) = {Read, Address_Tag}; Valid_Operation = Read; Not_inValid_Operation = New_Tag[15];
  //   Old_Tag_A[15:14] = {A_Valid, A_Dirty}; Tag_B[15:0] = {B_Valid, B_Dirty, B_LRU, Old_Tag_B};
  //   Old_Tag_B[15:14] = {B_Valid, B_Dirty}

  // Notes on the sheet:
  //   data moving starts on psram LOW
  //   1st data comes on the following FE high edge after data moving
  //   ODD
  //   EVEN
  //   ODD
  //   EVEN
  //   can prob latch these on like
  //   burst stage 0 or smth
endmodule
module PSRAM_Controller (
  input  Clock,
  input  Reset,
  input  RWDS_In,
  input  [7:0] Bit8_Data_In,
  input  [26:0] Bit27_Address,
  input  Read,
  input  Write,
  output reclocktemp,
  output psramclocktemp,
  output feclocktemp,
  output Operationtemp,
  output RWDS_Out,
  output Data_Moving,
  output [7:0] Bit8_Data_Out
);

  wire and_1_out, and_2_out, and_3_out, and_4_out, and_5_out, and_6_out, and_7_out, and_8_out, and_9_out,
       and_10_out, and_11_out, and_12_out, and_16_out, and_17_out, and_18_out, and_19_out, and_20_out,
       and_21_out, and_22_out, and_23_out, and_24_out, and_25_out, and_26_out, and_27_out, and_28_out,
       and_29_out, and_30_out, and_31_out, and_32_out, and_33_out, and_34_out, d_ff_2_q, d_ff_3_q, d_ff_4_q,
       d_ff_5_qn, demultiplexer_1_out0, demultiplexer_1_out1, demultiplexer_1_out2, demultiplexer_1_out3,
       demultiplexer_1_out4, demultiplexer_1_out5, demultiplexer_1_out6, demultiplexer_1_out7, Is_Setup,
       Isnt_Setup, not_1_out, not_2_out, not_4_out, not_5_out, not_6_out, not_7_out, not_8_out, not_9_out,
       not_10_out, not_11_out, or_1_out, or_3_out, or_4_out, or_5_out, or_7_out, or_8_out, Reg_Loaded,
       Reg_Loaded_Sub_1, Reset_Setup, Single_Chip_Setup_Complete;
  wire [0:0] Latency_x2_Latch_q;
  wire [2:0] Chip_Setup, multiplexer_2_out, not_3_out;
  wire [4:0] adder_1_out, Setup_Counter_q, shifter_1_out;
  wire [6:0] pull_resistor_1_node_2;
  wire [7:0] multiplexer_1_out, or_6_out, pull_resistor_1_node_3;
  wire [7:7] d_ff_1_q;
  wire [8:8] pull_resistor_1_node;

  or or_1 (or_1_out, Is_Setup, and_1_out);
  and and_1 (and_1_out, Chip_Setup[1], Chip_Setup[0], Chip_Setup[2], Reg_Loaded_Sub_1);
  Counter #(.max('h7), .width(3)) Chip_Setup_Counter (
    .clr(Reset), .up(Reg_Loaded), .count(Reg_Loaded), .clk(feclocktemp), .Q(Chip_Setup));  // open: load, D, carry
  D_Flip_Flop #(.trigger("falling")) u_Is_Setup (
    .D(or_1_out), .clk(psramclocktemp), .Q(Is_Setup), .Qn(Isnt_Setup), .reset(Reset));  // open: preset
  D_Flip_Flop d_ff_1 (.D(Read), .clk(feclocktemp), .Q(d_ff_1_q[7]), .reset(Reset));  // open: Qn, preset
  D_Flip_Flop d_ff_2 (.D(Write), .clk(feclocktemp), .Q(d_ff_2_q), .reset(Reset));  // open: Qn, preset
  D_Flip_Flop #(.trigger("falling")) d_ff_3 (
    .D(Is_Setup), .clk(psramclocktemp), .Q(d_ff_3_q), .reset(Reset));  // open: Qn, preset
  and and_2 (and_2_out, Is_Setup, ~d_ff_3_q);  // AND_Gate
  or or_2 (Operationtemp, d_ff_2_q, and_4_out, d_ff_1_q[7]);
  and and_3 (and_3_out, Is_Setup, not_1_out);
  not not_1 (not_1_out, Operationtemp);
  and and_4 (and_4_out, ~Single_Chip_Setup_Complete, Isnt_Setup);  // AND_Gate
  or or_3 (or_3_out, Reg_Loaded, and_3_out, Reset);
  or or_4 (or_4_out, not_1_out, Reset);
  and and_5 (and_5_out, ~Operationtemp, Is_Setup);  // AND_Gate
  Memory_Clock memory_clock_1 (
    .Clock(Clock), .Reset(Reset), .RE_Clock(reclocktemp), .PSRAM_Clock(psramclocktemp), .FE_Clock(feclocktemp));  // open: CPU_Clock
  and and_6 (and_6_out, Is_Setup, Data_Moving);
  Counter #(.max('h3), .width(2)) counter_1 (
    .clr(or_3_out), .up(d_ff_5_qn), .count(d_ff_5_qn), .clk(feclocktemp), .Q(not_3_out[2:1]));  // open: load, D, carry
  and and_7 (and_7_out, d_ff_5_qn, psramclocktemp);
  and and_8 (and_8_out, Reset_Setup, Isnt_Setup);
  and and_9 (and_9_out, ~Data_Moving, Operationtemp, Is_Setup);  // AND_Gate
  D_Flip_Flop #(.trigger("falling")) d_ff_4 (
    .D(Reg_Loaded_Sub_1), .clk(psramclocktemp), .Q(d_ff_4_q), .reset(Reset));  // open: Qn, preset
  not not_2 (not_2_out, and_6_out);
  not not_3 (not_3_out[0], feclocktemp);
  D_Flip_Flop #(.trigger("falling")) d_ff_5 (
    .D(or_7_out), .clk(and_7_out), .Qn(d_ff_5_qn), .reset(or_4_out));  // open: Q, preset
  or or_5 (or_5_out, Isnt_Setup, and_9_out);
  Pull_Resistor pull_resistor_1 (.node({pull_resistor_1_node_2, or_6_out[7:1], pull_resistor_1_node[8], pull_resistor_1_node_3}));
  assign {pull_resistor_1_node_2, or_6_out[7:1], pull_resistor_1_node[8], pull_resistor_1_node_3} = Is_Setup ? Bit27_Address[23:1] : 23'bz;  // Controlled_Buffer controlled_buffer_1
  or or_6 (or_6_out[0], Isnt_Setup, pull_resistor_1_node[8]);
  and and_10 (and_10_out, and_12_out, Is_Setup);
  or or_7 (or_7_out, and_10_out, and_11_out);
  and and_11 (and_11_out, and_17_out, Isnt_Setup);
  or or_8 (or_8_out, Reset, and_2_out, and_8_out, and_5_out);
  Counter #(.max('h1f), .width(5)) Setup_Counter (
    .clr(or_8_out), .up(or_5_out), .count(or_5_out), .clk(psramclocktemp), .Q(Setup_Counter_q));  // open: load, D, carry
  or or_9 (Single_Chip_Setup_Complete, d_ff_4_q, d_ff_4_q);
  Multiplexer #(.select(3), .width(8)) multiplexer_1 (
    .in0({d_ff_1_q[7], {2{Isnt_Setup}}, {5{1'b0}}}), .in1({1'b0, pull_resistor_1_node_2}), .in2(or_6_out),
    .in3(pull_resistor_1_node_3), .in4({8{1'b0}}), .in5({8{1'b0}}), .in6(8'h8f), .in7(8'he6),
    .out(multiplexer_1_out), .sel(not_3_out));
  and and_12 (and_12_out, not_3_out[2], ~not_3_out[1], not_3_out[0]);  // AND_Gate
  and and_13 (Reset_Setup, ~Setup_Counter_q[0], Setup_Counter_q[1], Setup_Counter_q[2], ~Setup_Counter_q[3], ~Setup_Counter_q[4]);  // AND_Gate
  and and_14 (Reg_Loaded_Sub_1, ~Setup_Counter_q[0], ~Setup_Counter_q[1], Setup_Counter_q[2], ~Setup_Counter_q[3], ~Setup_Counter_q[4]);  // AND_Gate
  and and_15 (Reg_Loaded, Setup_Counter_q[0], ~Setup_Counter_q[1], Setup_Counter_q[2], ~Setup_Counter_q[3], ~Setup_Counter_q[4]);  // AND_Gate
  and and_16 (and_16_out, ~Setup_Counter_q[0], Setup_Counter_q[1], ~Setup_Counter_q[2], ~Setup_Counter_q[3], ~Setup_Counter_q[4]);  // AND_Gate
  Shifter #(.width(5)) shifter_1 (.in(5'b00011), .\dist ({2'b00, Latency_x2_Latch_q[0]}), .out(shifter_1_out));
  Adder #(.width(5)) adder_1 (.a(5'b00010), .b(shifter_1_out), .out(adder_1_out));  // open: cin, cout
  Multiplexer #(.width(3)) multiplexer_2 (
    .in0(Chip_Setup), .in1(Bit27_Address[26:24]), .out(multiplexer_2_out), .sel(Is_Setup));
  // Probe on multiplexer_2_out
  Multiplexer #(.width(8)) multiplexer_3 (
    .in0(multiplexer_1_out), .in1(Bit8_Data_In), .out(Bit8_Data_Out), .sel(Data_Moving));
  and and_17 (and_17_out, not_3_out[2], not_3_out[1], not_3_out[0]);
  D_Flip_Flop Latency_x2_Latch (.D(RWDS_In), .clk(and_18_out), .Q(Latency_x2_Latch_q[0]));  // open: Qn, preset, reset
  and and_18 (and_18_out, ~feclocktemp, and_16_out);  // AND_Gate
  Comparator #(.width(5)) comparator_1 (.a(Setup_Counter_q), .b(adder_1_out), .eq(Data_Moving));  // open: gt, lt
  Demultiplexer #(.select(3)) demultiplexer_1 (
    .out0(demultiplexer_1_out0), .out1(demultiplexer_1_out1), .out2(demultiplexer_1_out2),
    .out3(demultiplexer_1_out3), .out4(demultiplexer_1_out4), .out5(demultiplexer_1_out5),
    .out6(demultiplexer_1_out6), .out7(demultiplexer_1_out7), .in(Operationtemp), .sel(multiplexer_2_out));
  not not_4 (not_4_out, demultiplexer_1_out0);
  not not_5 (not_5_out, demultiplexer_1_out1);
  not not_6 (not_6_out, demultiplexer_1_out2);
  not not_7 (not_7_out, demultiplexer_1_out3);
  not not_8 (not_8_out, demultiplexer_1_out4);
  not not_9 (not_9_out, demultiplexer_1_out5);
  not not_10 (not_10_out, demultiplexer_1_out6);
  not not_11 (not_11_out, demultiplexer_1_out7);
  and and_19 (and_19_out, psramclocktemp, demultiplexer_1_out0);
  and and_20 (and_20_out, feclocktemp, demultiplexer_1_out0);
  and and_21 (and_21_out, psramclocktemp, demultiplexer_1_out1);
  and and_22 (and_22_out, feclocktemp, demultiplexer_1_out1);
  and and_23 (and_23_out, psramclocktemp, demultiplexer_1_out2);
  and and_24 (and_24_out, feclocktemp, demultiplexer_1_out2);
  and and_25 (and_25_out, psramclocktemp, demultiplexer_1_out3);
  and and_26 (and_26_out, feclocktemp, demultiplexer_1_out3);
  and and_27 (and_27_out, psramclocktemp, demultiplexer_1_out4);
  and and_28 (and_28_out, feclocktemp, demultiplexer_1_out4);
  and and_29 (and_29_out, psramclocktemp, demultiplexer_1_out5);
  and and_30 (and_30_out, feclocktemp, demultiplexer_1_out5);
  and and_31 (and_31_out, psramclocktemp, demultiplexer_1_out6);
  and and_32 (and_32_out, feclocktemp, demultiplexer_1_out6);
  and and_33 (and_33_out, psramclocktemp, demultiplexer_1_out7);
  and and_34 (and_34_out, feclocktemp, demultiplexer_1_out7);
  PSRAM_SIM psram_sim_1 (
    .NOT_CS(not_4_out), .RWDS(RWDS_In), .DQ(Bit8_Data_Out), .reset(Reset), .PSRAMCLOCK(and_19_out),
    .FECLOCK(and_20_out), .RWDS_OUT(RWDS_In), .DATA_OUT(Bit8_Data_Out));
  PSRAM_SIM psram_sim_2 (
    .NOT_CS(not_5_out), .RWDS(RWDS_In), .DQ(Bit8_Data_Out), .reset(Reset), .PSRAMCLOCK(and_21_out),
    .FECLOCK(and_22_out), .RWDS_OUT(RWDS_In), .DATA_OUT(Bit8_Data_Out));
  PSRAM_SIM psram_sim_3 (
    .NOT_CS(not_6_out), .RWDS(RWDS_In), .DQ(Bit8_Data_Out), .reset(Reset), .PSRAMCLOCK(and_23_out),
    .FECLOCK(and_24_out), .RWDS_OUT(RWDS_In), .DATA_OUT(Bit8_Data_Out));
  PSRAM_SIM psram_sim_4 (
    .NOT_CS(not_7_out), .RWDS(RWDS_In), .DQ(Bit8_Data_Out), .reset(Reset), .PSRAMCLOCK(and_25_out),
    .FECLOCK(and_26_out), .RWDS_OUT(RWDS_In), .DATA_OUT(Bit8_Data_Out));
  PSRAM_SIM psram_sim_5 (
    .NOT_CS(not_8_out), .RWDS(RWDS_In), .DQ(Bit8_Data_Out), .reset(Reset), .PSRAMCLOCK(and_27_out),
    .FECLOCK(and_28_out), .RWDS_OUT(RWDS_In), .DATA_OUT(Bit8_Data_Out));
  PSRAM_SIM psram_sim_6 (
    .NOT_CS(not_9_out), .RWDS(RWDS_In), .DQ(Bit8_Data_Out), .reset(Reset), .PSRAMCLOCK(and_29_out),
    .FECLOCK(and_30_out), .RWDS_OUT(RWDS_In), .DATA_OUT(Bit8_Data_Out));
  PSRAM_SIM psram_sim_7 (
    .NOT_CS(not_10_out), .RWDS(RWDS_In), .DQ(Bit8_Data_Out), .reset(Reset), .PSRAMCLOCK(and_31_out),
    .FECLOCK(and_32_out), .RWDS_OUT(RWDS_In), .DATA_OUT(Bit8_Data_Out));
  PSRAM_SIM psram_sim_8 (
    .NOT_CS(not_11_out), .RWDS(RWDS_In), .DQ(Bit8_Data_Out), .reset(Reset), .PSRAMCLOCK(and_33_out),
    .FECLOCK(and_34_out), .RWDS_OUT(RWDS_In), .DATA_OUT(Bit8_Data_Out));

  assign RWDS_Out = RWDS_In;

  // Other names for the same wires on the sheet: Chip_Select[2:0] = Bit27_Address[26:24]; FE_Clock = feclocktemp;
  //   Operation = Operationtemp; PSRAM_Clock = psramclocktemp; RE_Clock = reclocktemp; RWDS = RWDS_In;
  //   Sub_Clock = Clock

  // Notes on the sheet:
  //   latch input on rising
  //   lock is setup until reset
  //   number of cycle of latency
  //   PSRAM BINARY SELECT OF CLOCK CYCLES
  //   6
  //   8
  //   when assembling, pick a latency to operate at and hard code and gates to identify the numbers
  //   (both latency + 2 and 2*latency + 2)
  //   maybe edge latch operation so no flickering
  //   PSRAM = CK
endmodule

module Memory_Clock (
  input  Clock,
  input  Reset,
  output CPU_Clock,
  output RE_Clock,
  output PSRAM_Clock,
  output FE_Clock
);

  wire d_ff_2_q, d_ff_3_qn;

  D_Flip_Flop d_ff_1 (.D(RE_Clock), .clk(Clock), .Q(PSRAM_Clock), .Qn(RE_Clock), .reset(Reset));  // open: preset
  D_Flip_Flop #(.trigger("falling")) d_ff_2 (
    .D(FE_Clock), .clk(Clock), .Q(d_ff_2_q), .Qn(FE_Clock), .reset(Reset));  // open: preset
  D_Flip_Flop d_ff_3 (.D(d_ff_3_qn), .clk(RE_Clock), .Qn(d_ff_3_qn), .reset(Reset));  // open: Q, preset
  D_Flip_Flop d_ff_4 (.D(CPU_Clock), .clk(d_ff_3_qn), .Qn(CPU_Clock), .reset(Reset));  // open: Q, preset

  // Notes on the sheet:
  //   PSRAM CLOCK (NOT RE_CLOCK)
endmodule

module Data_Cache_2_Way (
  input  Read,
  input  Write,
  input  Two_Byte_Operation,
  input  Flush_Address,
  input  Invalidate_Address,
  input  Flush_Line,
  input  Invalidate_Line,
  input  Set,
  input  [25:0] Bit26_Address,
  input  [15:0] Bit16_Data,
  input  [7:0] Bit8_From_Memory,
  input  Ram_Data_Moving,
  input  Clock,
  input  Reset,
  output [15:0] Bit16_To_Core,
  output Ram_Write,
  output Ram_Read,
  output Requesting_Ram,
  output [7:0] Memory_Byte,
  output RWDS
);

  wire A_Change, A_Dirty, A_Evict, A_Hit, A_Line_Flush, A_Miss, A_Valid, and_2_out, and_3_out, and_4_out,
       and_5_out, and_6_out, and_7_out, and_8_out, and_9_out, and_10_out, and_11_out, and_12_out, and_13_out,
       and_14_out, and_15_out, and_16_out, and_17_out, and_18_out, and_19_out, and_20_out, and_21_out,
       and_22_out, and_23_out, and_24_out, and_25_out, and_26_out, and_27_out, and_28_out, and_29_out,
       and_30_out, and_31_out, and_32_out, and_33_out, and_35_out, and_36_out, and_37_out, and_38_out,
       and_44_out, and_45_out, and_46_out, and_48_out, B_Change, B_Dirty, B_Evict, B_Hit, B_Line_Flush,
       B_LRU, B_Miss, B_Valid, comparator_1_eq, comparator_2_eq, d_ff_1_q, d_ff_3_q, d_ff_4_q, d_ff_5_q,
       d_ff_6_q, d_ff_7_q, d_ff_8_q, d_ff_9_q, d_ff_10_q, d_ff_11_q, d_ff_12_q, d_ff_13_q, d_ff_14_q,
       d_ff_15_q, d_ff_16_q, d_ff_17_q, d_ff_18_q, FE_Clock, Hit, Line_Operation, nand_1_out, nand_2_out,
       nand_3_out, nand_4_out, nor_2_out, not_1_out, not_2_out, not_3_out, Operation, or_3_out, or_4_out,
       or_5_out, or_6_out, or_7_out, or_8_out, or_9_out, or_10_out, or_11_out, or_12_out, or_13_out,
       or_15_out, or_20_out, or_22_out, PSRAM_Clock, RE_Clock, Tag_Write_Enable, Writing;
  wire [2:0] adder_1_out, Burst_Stage, multiplexer_3_out;
  wire [3:0] Address_Line_Offset;
  wire [7:0] multiplexer_1_out, multiplexer_2_out, ram_1_dout, ram_2_dout, ram_3_dout, ram_4_dout,
       register_1_q, register_2_q;
  wire [9:0] Address_Tag;
  wire [11:0] Address_Index;
  wire [12:0] Old_Tag_A, Old_Tag_B;
  wire [13:13] Tag_A;
  wire [14:0] bit_extender_1_out;
  wire [15:0] multiplexer_4_out, multiplexer_5_out, register_3_q, register_4_q;
  wire [15:13] New_Tag;

  nor nor_1 (New_Tag[15], Invalidate_Address, Invalidate_Line);
  or or_1 (New_Tag[13], Write, Read);
  or or_2 (Operation, Write, Read, Invalidate_Address, Invalidate_Line, Flush_Line, Flush_Address);
  Memory_Clock memory_clock_1 (
    .Clock(Clock), .Reset(Reset), .RE_Clock(RE_Clock), .PSRAM_Clock(PSRAM_Clock), .FE_Clock(FE_Clock));  // open: CPU_Clock
  and and_1 (Writing, Write, ~Requesting_Ram);  // AND_Gate
  nor nor_2 (nor_2_out, Ram_Data_Moving, Writing);
  or or_3 (or_3_out, Writing, d_ff_1_q);
  or or_4 (or_4_out, Reset, nor_2_out);
  Multiplexer #(.select(2), .width(8)) multiplexer_1 (
    .in0(Bit8_From_Memory), .in2(Bit16_Data[15:8]), .in3(Bit16_Data[7:0]), .out(multiplexer_1_out),
    .sel({Hit, Address_Line_Offset[0]}));  // open: in1
  Multiplexer #(.select(2), .width(8)) multiplexer_2 (
    .in0(Bit8_From_Memory), .in2(Bit16_Data[7:0]), .in3(Bit16_Data[15:8]), .out(multiplexer_2_out),
    .sel({Hit, Address_Line_Offset[0]}));  // open: in1
  Counter #(.max('h7), .trigger("falling"), .width(3)) counter_1 (
    .clr(or_4_out), .up(or_3_out), .count(or_3_out), .clk(FE_Clock), .Q(Burst_Stage));  // open: load, D, carry
  // Probe on multiplexer_1_out
  // Probe on multiplexer_1_out
  // Probe on multiplexer_2_out
  // Probe on multiplexer_2_out
  D_Flip_Flop d_ff_1 (.D(and_2_out), .clk(RE_Clock), .Q(d_ff_1_q), .reset(not_1_out));  // open: Qn, preset
  and and_2 (and_2_out, Ram_Data_Moving, or_5_out);
  or or_5 (or_5_out, d_ff_1_q, Requesting_Ram);
  not not_1 (not_1_out, Ram_Data_Moving);
  and and_3 (and_3_out, Write, Hit, Address_Line_Offset[0]);
  and and_4 (and_4_out, Write, Hit, Two_Byte_Operation);
  and and_5 (and_5_out, Write, Hit, ~Address_Line_Offset[0]);  // AND_Gate
  and and_6 (and_6_out, ~FE_Clock, Ram_Data_Moving, Ram_Read);  // AND_Gate
  and and_7 (and_7_out, FE_Clock, Ram_Data_Moving, Ram_Read);
  and and_8 (and_8_out, Ram_Data_Moving, Ram_Read, RE_Clock, A_Evict);
  Register #(.trigger("falling")) register_1 (
    .D(multiplexer_1_out), .en(or_6_out), .clk(RE_Clock), .Q(register_1_q), .clr(Reset));
  or or_6 (or_6_out, and_6_out, and_4_out, and_3_out);
  Register #(.trigger("falling")) register_2 (
    .D(multiplexer_2_out), .en(or_7_out), .clk(RE_Clock), .Q(register_2_q), .clr(Reset));
  or or_7 (or_7_out, and_5_out, and_4_out, and_7_out);
  D_Flip_Flop d_ff_2 ();  // open: D, clk, Q, Qn, preset, reset
  and and_9 (and_9_out, A_Hit, Writing);
  and and_10 (and_10_out, or_8_out, or_6_out);
  and and_11 (and_11_out, or_11_out, or_6_out);
  and and_12 (and_12_out, or_11_out, or_7_out);
  and and_13 (and_13_out, or_8_out, or_7_out);
  or or_8 (or_8_out, and_8_out, and_9_out);
  D_Flip_Flop d_ff_3 (.D(and_10_out), .clk(PSRAM_Clock), .Q(d_ff_3_q), .reset(RE_Clock));  // open: Qn, preset
  D_Flip_Flop d_ff_4 (.D(and_11_out), .clk(PSRAM_Clock), .Q(d_ff_4_q), .reset(RE_Clock));  // open: Qn, preset
  D_Flip_Flop d_ff_5 (.D(and_12_out), .clk(PSRAM_Clock), .Q(d_ff_5_q), .reset(RE_Clock));  // open: Qn, preset
  D_Flip_Flop d_ff_6 (.D(and_13_out), .clk(PSRAM_Clock), .Q(d_ff_6_q), .reset(RE_Clock));  // open: Qn, preset
  or or_9 (or_9_out, Read, Ram_Write);
  nand nand_1 (nand_1_out, Ram_Write, Ram_Data_Moving);
  and and_14 (and_14_out, Two_Byte_Operation, Address_Line_Offset[0]);
  Adder #(.width(3)) adder_1 (.a(multiplexer_3_out), .b(3'b000), .out(adder_1_out), .cin(and_14_out));  // open: cout
  Multiplexer #(.width(3)) multiplexer_3 (
    .in0(Burst_Stage), .in1(Address_Line_Offset[3:1]), .out(multiplexer_3_out), .sel(and_17_out));
  RAM #(.addrWidth(15), .trigger("high")) ram_1 (
    .addr({Address_Index, multiplexer_3_out}), .we(d_ff_3_q), .oe(or_9_out), .din(register_1_q),
    .dout(ram_1_dout));
  RAM #(.addrWidth(15), .trigger("high")) ram_2 (
    .addr({Address_Index, adder_1_out}), .we(d_ff_6_q), .oe(or_9_out), .din(register_2_q), .dout(ram_2_dout));
  not not_2 (not_2_out, FE_Clock);
  or or_10 (or_10_out, nand_1_out, Reset);
  D_Flip_Flop #(.trigger("falling")) d_ff_7 (
    .D(and_15_out), .clk(Clock), .Q(d_ff_7_q), .reset(or_10_out));  // open: Qn, preset
  and and_15 (and_15_out, Ram_Data_Moving, FE_Clock, Ram_Write, A_Hit);
  D_Flip_Flop #(.trigger("falling")) d_ff_8 (
    .D(and_16_out), .clk(Clock), .Q(d_ff_8_q), .reset(or_10_out));  // open: Qn, preset
  and and_16 (and_16_out, Ram_Data_Moving, not_2_out, Ram_Write, A_Hit);
  assign Bit16_To_Core[15:8] = d_ff_12_q ? ram_1_dout : 8'bz;  // Controlled_Buffer controlled_buffer_1
  assign Bit16_To_Core[7:0] = d_ff_11_q ? ram_1_dout : 8'bz;  // Controlled_Buffer controlled_buffer_2
  assign Memory_Byte = d_ff_8_q ? ram_1_dout : 8'bz;  // Controlled_Buffer controlled_buffer_3
  assign Bit16_To_Core[15:8] = d_ff_10_q ? ram_2_dout : 8'bz;  // Controlled_Buffer controlled_buffer_4
  assign Bit16_To_Core[7:0] = d_ff_9_q ? ram_2_dout : 8'bz;  // Controlled_Buffer controlled_buffer_5
  assign Memory_Byte = d_ff_7_q ? ram_2_dout : 8'bz;  // Controlled_Buffer controlled_buffer_6
  and and_17 (and_17_out, Operation, Hit);
  and and_18 (and_18_out, A_Hit, ~Address_Line_Offset[0]);  // AND_Gate
  D_Flip_Flop d_ff_9 (.D(and_18_out), .clk(Clock), .Q(d_ff_9_q), .reset(Reset));  // open: Qn, preset
  and and_19 (and_19_out, A_Hit, Address_Line_Offset[0]);
  D_Flip_Flop d_ff_10 (.D(and_19_out), .clk(Clock), .Q(d_ff_10_q), .reset(Reset));  // open: Qn, preset
  and and_20 (and_20_out, A_Hit, Address_Line_Offset[0]);
  D_Flip_Flop d_ff_11 (.D(and_20_out), .clk(Clock), .Q(d_ff_11_q), .reset(Reset));  // open: Qn, preset
  D_Flip_Flop d_ff_12 (.D(and_21_out), .clk(Clock), .Q(d_ff_12_q), .reset(Reset));  // open: Qn, preset
  and and_21 (and_21_out, A_Hit, ~Address_Line_Offset[0]);  // AND_Gate
  and and_22 (and_22_out, Ram_Data_Moving, Ram_Read, RE_Clock, B_Change);
  and and_23 (and_23_out, B_Hit, Writing);
  or or_11 (or_11_out, and_22_out, and_23_out);
  nand nand_2 (nand_2_out, Ram_Write, Ram_Data_Moving);
  or or_12 (or_12_out, Read, Ram_Write);
  RAM #(.addrWidth(15), .trigger("high")) ram_3 (
    .addr({Address_Index, multiplexer_3_out}), .we(d_ff_4_q), .oe(or_12_out), .din(register_1_q),
    .dout(ram_3_dout));
  RAM #(.addrWidth(15), .trigger("high")) ram_4 (
    .addr({Address_Index, adder_1_out}), .we(d_ff_5_q), .oe(or_12_out), .din(register_2_q), .dout(ram_4_dout));
  not not_3 (not_3_out, FE_Clock);
  or or_13 (or_13_out, nand_2_out, Reset);
  nor nor_3 (Tag_Write_Enable, Burst_Stage[0], Burst_Stage[1], Burst_Stage[2]);
  or or_14 (A_Change, A_Evict, A_Hit);
  D_Flip_Flop #(.trigger("falling")) d_ff_13 (
    .D(and_24_out), .clk(Clock), .Q(d_ff_13_q), .reset(or_13_out));  // open: Qn, preset
  and and_24 (and_24_out, Ram_Data_Moving, FE_Clock, Ram_Write, B_Hit);
  D_Flip_Flop #(.trigger("falling")) d_ff_14 (
    .D(and_25_out), .clk(Clock), .Q(d_ff_14_q), .reset(or_13_out));  // open: Qn, preset
  and and_25 (and_25_out, Ram_Data_Moving, not_3_out, Ram_Write, B_Hit);
  and and_26 (and_26_out, Burst_Stage[0], Burst_Stage[1], Burst_Stage[2], RE_Clock, A_Change);
  assign Bit16_To_Core[15:8] = d_ff_18_q ? ram_3_dout : 8'bz;  // Controlled_Buffer controlled_buffer_7
  assign Bit16_To_Core[7:0] = d_ff_17_q ? ram_3_dout : 8'bz;  // Controlled_Buffer controlled_buffer_8
  assign Memory_Byte = d_ff_14_q ? ram_3_dout : 8'bz;  // Controlled_Buffer controlled_buffer_9
  assign Bit16_To_Core[15:8] = d_ff_16_q ? ram_4_dout : 8'bz;  // Controlled_Buffer controlled_buffer_10
  assign Bit16_To_Core[7:0] = d_ff_15_q ? ram_4_dout : 8'bz;  // Controlled_Buffer controlled_buffer_11
  assign Memory_Byte = d_ff_13_q ? ram_4_dout : 8'bz;  // Controlled_Buffer controlled_buffer_12
  and and_27 (and_27_out, B_Hit, ~Address_Line_Offset[0]);  // AND_Gate
  and and_28 (and_28_out, ~and_45_out, Operation, A_Hit);  // AND_Gate
  D_Flip_Flop d_ff_15 (.D(and_27_out), .clk(Clock), .Q(d_ff_15_q), .reset(Reset));  // open: Qn, preset
  and and_29 (and_29_out, B_Hit, Address_Line_Offset[0]);
  or or_15 (or_15_out, and_28_out, and_26_out);
  Register #(.width(16)) register_3 (
    .D(multiplexer_4_out), .en(Tag_Write_Enable), .clk(PSRAM_Clock), .Q(register_3_q), .clr(Reset));
  Multiplexer #(.width(16)) multiplexer_4 (
    .in0({A_Valid, A_Dirty, 1'b0, Old_Tag_A}), .in1({New_Tag[15], Write, New_Tag[13], 3'b000, Address_Tag}),
    .out(multiplexer_4_out), .sel(A_Change));
  D_Flip_Flop d_ff_16 (.D(and_29_out), .clk(Clock), .Q(d_ff_16_q), .reset(Reset));  // open: Qn, preset
  and and_30 (and_30_out, B_Hit, Address_Line_Offset[0]);
  assign bit_extender_1_out = {{3{1'b0}}, Address_Index};  // Bit_Extender bit_extender_1
  D_Flip_Flop d_ff_17 (.D(and_30_out), .clk(Clock), .Q(d_ff_17_q), .reset(Reset));  // open: Qn, preset
  RAM #(.addrWidth(15), .dataWidth(16), .trigger("high")) ram_5 (
    .addr(bit_extender_1_out), .we(or_15_out), .oe(Operation), .din(register_3_q),
    .dout({A_Valid, A_Dirty, Tag_A[13], Old_Tag_A}));
  D_Flip_Flop d_ff_18 (.D(and_31_out), .clk(Clock), .Q(d_ff_18_q), .reset(Reset));  // open: Qn, preset
  and and_31 (and_31_out, B_Hit, ~Address_Line_Offset[0]);  // AND_Gate
  Comparator #(.mode("unsigned"), .width(10)) comparator_1 (
    .a(Old_Tag_A[9:0]), .b(Address_Tag), .eq(comparator_1_eq));  // open: gt, lt
  Pull_Resistor pull_resistor_1 (.node({A_Valid, A_Dirty, Tag_A[13], Old_Tag_A}));
  nand nand_3 (nand_3_out, comparator_1_eq, A_Valid);
  and and_32 (and_32_out, Invalidate_Line, ~Set);  // AND_Gate
  and and_33 (and_33_out, Operation, ~Line_Operation, comparator_1_eq, A_Valid);  // AND_Gate
  and and_34 (A_Miss, Operation, nand_3_out);
  and and_35 (and_35_out, A_Miss, New_Tag[15], B_Miss);
  or or_16 (A_Hit, A_Line_Flush, and_32_out, and_33_out);
  and and_36 (and_36_out, A_Miss, B_Miss, ~1'b0, A_Valid, A_Dirty, New_Tag[15]);  // AND_Gate
  and and_37 (and_37_out, Burst_Stage[0], Burst_Stage[1], Burst_Stage[2], RE_Clock, B_Change);
  or or_17 (B_Change, B_Evict, B_Hit);
  or or_18 (Line_Operation, Flush_Line, Invalidate_Line);
  and and_38 (and_38_out, A_Miss, B_Miss, 1'b0, B_Valid, B_Dirty, New_Tag[15]);
  or or_19 (Ram_Write, and_38_out, and_36_out);
  xor xor_1 (Ram_Read, Ram_Write, and_35_out);
  Multiplexer #(.width(16)) multiplexer_5 (
    .in0({B_Valid, B_Dirty, 1'b0, Old_Tag_B}), .in1({New_Tag[15], Write, New_Tag[13], 3'b000, Address_Tag}),
    .out(multiplexer_5_out), .sel(B_Change));
  and and_39 (B_Line_Flush, Line_Operation, B_Dirty, Set);
  and and_40 (A_Line_Flush, ~Set, A_Dirty, Line_Operation);  // AND_Gate
  and and_41 (A_Evict, A_Miss, B_Miss, ~1'b0);  // AND_Gate
  or or_20 (or_20_out, and_44_out, and_37_out);
  Register #(.width(16)) register_4 (
    .D(multiplexer_5_out), .en(Tag_Write_Enable), .clk(PSRAM_Clock), .Q(register_4_q), .clr(Reset));
  and and_42 (B_Evict, A_Miss, B_Miss, 1'b0);
  or or_21 (Requesting_Ram, Ram_Write, Ram_Read);
  and and_43 (RWDS, Ram_Write, Ram_Data_Moving);
  and and_44 (and_44_out, ~and_45_out, Operation, B_Hit);  // AND_Gate
  RAM #(.addrWidth(15), .clearpin("true"), .dataWidth(16), .trigger("high")) ram_6 (
    .addr(bit_extender_1_out), .we(or_20_out), .oe(Operation), .din(register_4_q),
    .dout({B_Valid, B_Dirty, B_LRU, Old_Tag_B}));  // open: clr
  and and_45 (and_45_out, ~or_22_out, Requesting_Ram);  // AND_Gate
  or or_22 (or_22_out, Invalidate_Line, Invalidate_Address);
  or or_23 (Hit, A_Hit, B_Hit);
  Pull_Resistor pull_resistor_2 (.node({B_Valid, B_Dirty, B_LRU, Old_Tag_B}));
  Comparator #(.mode("unsigned"), .width(10)) comparator_2 (
    .a(Old_Tag_B[9:0]), .b(Address_Tag), .eq(comparator_2_eq));  // open: gt, lt
  and and_46 (and_46_out, Operation, ~Line_Operation, comparator_2_eq, B_Valid);  // AND_Gate
  and and_47 (B_Miss, Operation, nand_4_out);
  nand nand_4 (nand_4_out, comparator_2_eq, B_Valid);
  and and_48 (and_48_out, Invalidate_Line, Set);
  or or_24 (B_Hit, B_Line_Flush, and_48_out, and_46_out);

  // Other names for the same wires on the sheet: Tag_A (some bits) = {A_Valid, A_Dirty, Old_Tag_A};
  //   Address[25:0] = Bit26_Address; Data[15:0] = Bit16_Data; Flush_Addr = Flush_Address;
  //   Invalidate_Addr = Invalidate_Address; Memory_Data[7:0] = Bit8_From_Memory;
  //   New_Tag (some bits) = {Write, Address_Tag}; Valid_Operation = New_Tag[13]; Not_Invalid_Operation = New_Tag[15];
  //   Old_Tag_A[15:14] = {A_Valid, A_Dirty}; Tag_B[15:0] = {B_Valid, B_Dirty, B_LRU, Old_Tag_B};
  //   Old_Tag_B[15:14] = {B_Valid, B_Dirty}; To_Memory[7:0] = Memory_Byte

  // Notes on the sheet:
  //   data moving starts on psram LOW
  //   1st data comes on the following FE high edge after data moving
  //   ODD
  //   EVEN
  //   ODD
  //   EVEN
  //   can prob latch these on like
  //   burst stage 0 or smth
endmodule

module PSRAM_SIM (
  input  NOT_CS,
  input  RWDS,
  input  [7:0] DQ,
  input  reset,
  input  PSRAMCLOCK,
  input  FECLOCK,
  output RWDS_OUT,
  output [7:0] DATA_OUT
);

  wire and_1_out, and_2_out, and_3_out, and_4_out, and_5_out, and_6_out, and_7_out, and_8_out, and_9_out,
       and_10_out, and_11_out, comparator_1_eq, d_ff_1_q, d_ff_1_qn, d_ff_2_q, d_ff_3_q, d_ff_3_qn,
       DATA_MOVING, demultiplexer_1_out0, demultiplexer_1_out1, demultiplexer_2_out0, demultiplexer_2_out1,
       demultiplexer_3_out0, demultiplexer_3_out1, demultiplexer_3_out2, demultiplexer_5_out0,
       demultiplexer_5_out1, LATENCYx2, memory_clock_1_p3, not_1_out, not_2_out, not_3_out, not_4_out,
       not_6_out, or_1_out, or_2_out, or_3_out, or_4_out, or_5_out, or_6_out, or_7_out, READOP, undriven,
       WRITEOP;
  wire [1:0] counter_1_q;
  wire [3:0] rom_1_data;
  wire [4:0] adder_2_out, bit_extender_2_out, counter_2_q, shifter_1_out;
  wire [5:0] counter_3_q;
  wire [6:0] register_1_q;
  wire [7:0] e_dout, ram_1_dout, register_2_q, register_4_q, register_6_q, register_7_q, register_8_q;
  wire [7:4] register_3_q_2;
  wire [22:0] Bit23_Address, bit_extender_1_out;
  wire [22:11] register_3_q;

  LED led_1 (.in(PSRAMCLOCK));
  not not_1 (not_1_out, NOT_CS);
  not not_2 (not_2_out, undriven);
  Random #(.width(1)) random_1 (.next(not_1_out), .clk(not_1_out), .out(LATENCYx2));  // open: clr
  not not_3 (not_3_out, NOT_CS);
  or or_1 (or_1_out, d_ff_1_q, reset);
  not not_4 (not_4_out, not_3_out);
  Register register_1 (.D(DQ), .en(demultiplexer_1_out0), .clk(PSRAMCLOCK), .Q({READOP, register_1_q}), .clr(reset));
  Counter #(.max('h3), .trigger("falling"), .width(2)) counter_1 (
    .clr(or_1_out), .up(not_3_out), .count(not_3_out), .clk(PSRAMCLOCK), .Q(counter_1_q));  // open: load, D, carry
  or or_2 (or_2_out, and_2_out, not_4_out);
  Register register_2 (.D(DQ), .en(and_3_out), .clk(PSRAMCLOCK), .Q(register_2_q), .clr(reset));
  // Memory_Clock memory_clock_1: pin names not known; wires that end beside it: not_2_out, reset, memory_clock_1_p3, FECLOCK
  not not_5 (WRITEOP, READOP);
  Register #(.trigger("falling")) register_3 (
    .D(DQ), .en(demultiplexer_1_out1), .clk(PSRAMCLOCK), .Q({register_3_q_2, register_3_q[22:19]}),
    .clr(reset));
  Demultiplexer demultiplexer_1 (
    .out0(demultiplexer_1_out0), .out1(demultiplexer_1_out1), .in(demultiplexer_3_out0), .sel(PSRAMCLOCK));
  D_Flip_Flop d_ff_1 (.D(and_2_out), .clk(and_1_out), .Q(d_ff_1_q), .Qn(d_ff_1_qn), .reset(or_3_out));  // open: preset
  and and_1 (and_1_out, or_2_out, PSRAMCLOCK);
  or or_3 (or_3_out, reset, NOT_CS);
  Register #(.trigger("falling")) register_4 (.D(DQ), .en(and_3_out), .clk(PSRAMCLOCK), .Q(register_4_q), .clr(reset));
  or or_4 (or_4_out, and_2_out, d_ff_1_q);
  Adder #(.width(23)) adder_1 (
    .a({register_3_q, register_6_q, 3'b000}), .b(bit_extender_1_out), .out(Bit23_Address));  // open: cin, cout
  Register register_5 (.D(DQ), .en(demultiplexer_2_out0), .clk(PSRAMCLOCK), .Q(register_3_q[18:11]), .clr(reset));
  and and_2 (and_2_out, counter_1_q[0], counter_1_q[1]);
  and and_3 (and_3_out, or_4_out, ~d_ff_2_q, register_1_q[6]);  // AND_Gate
  and and_4 (and_4_out, or_4_out, register_1_q[6]);
  and and_5 (and_5_out, ~DATA_MOVING, PSRAMCLOCK);  // AND_Gate
  Register #(.trigger("falling")) register_6 (
    .D(DQ), .en(demultiplexer_2_out1), .clk(PSRAMCLOCK), .Q(register_6_q), .clr(reset));
  Demultiplexer demultiplexer_2 (
    .out0(demultiplexer_2_out0), .out1(demultiplexer_2_out1), .in(demultiplexer_3_out1), .sel(PSRAMCLOCK));
  Demultiplexer #(.select(2)) demultiplexer_3 (
    .out0(demultiplexer_3_out0), .out1(demultiplexer_3_out1), .out2(demultiplexer_3_out2), .in(d_ff_1_qn),
    .sel(counter_1_q));  // open: out3
  D_Flip_Flop #(.trigger("falling")) d_ff_2 (
    .D(and_4_out), .clk(PSRAMCLOCK), .Q(d_ff_2_q), .reset(NOT_CS));  // open: Qn, preset
  ROM #(.addrWidth(4), .dataWidth(4)) rom_1 (.addr(register_4_q[7:4]), .data(rom_1_data));
  Counter #(.max('h1f), .width(5)) counter_2 (
    .clr(or_5_out), .up(1'b1), .count(not_1_out), .clk(and_5_out), .Q(counter_2_q));  // open: load, D, carry
  or or_5 (or_5_out, reset, NOT_CS);
  Counter #(.max('h3f), .width(6)) counter_3 (
    .clr(or_6_out), .up(1'b1), .count(DATA_MOVING), .clk(FECLOCK), .Q(counter_3_q));  // open: load, D, carry
  or or_6 (or_6_out, reset, NOT_CS);
  Demultiplexer #(.select(2)) demultiplexer_4 (.in(1'b1), .sel(register_4_q[1:0]));  // open: out0, out1, out2, out3
  assign bit_extender_1_out = {{17{1'b0}}, counter_3_q};  // Bit_Extender bit_extender_1
  Register register_7 (.D(DQ), .en(demultiplexer_5_out0), .clk(PSRAMCLOCK), .Q(register_7_q), .clr(reset));
  Demultiplexer demultiplexer_5 (
    .out0(demultiplexer_5_out0), .out1(demultiplexer_5_out1), .in(demultiplexer_3_out2), .sel(PSRAMCLOCK));
  Register #(.trigger("falling")) register_8 (
    .D(DQ), .en(demultiplexer_5_out1), .clk(PSRAMCLOCK), .Q(register_8_q), .clr(reset));
  Comparator #(.mode("unsigned"), .width(5)) comparator_1 (
    .a(5'b00011), .b(counter_2_q), .eq(comparator_1_eq));  // open: gt, lt
  assign bit_extender_2_out = {{1{1'b0}}, rom_1_data};  // Bit_Extender bit_extender_2
  Comparator #(.mode("unsigned"), .width(5)) comparator_2 (
    .a(counter_2_q), .b(adder_2_out), .eq(DATA_MOVING));  // open: gt, lt
  Adder #(.width(5)) adder_2 (.a(5'b00010), .b(shifter_1_out), .out(adder_2_out));  // open: cin, cout
  Shifter #(.width(5)) shifter_1 (.in(bit_extender_2_out), .\dist ({2'b00, LATENCYx2}), .out(shifter_1_out));
  D_Flip_Flop d_ff_3 (.D(d_ff_3_qn), .clk(not_1_out), .Q(d_ff_3_q), .Qn(d_ff_3_qn), .reset(or_7_out));  // open: preset
  or or_7 (or_7_out, comparator_1_eq, reset);
  and and_6 (and_6_out, RWDS, WRITEOP);
  and and_7 (and_7_out, PSRAMCLOCK, DATA_MOVING);
  and and_8 (and_8_out, PSRAMCLOCK, DATA_MOVING);
  RAM #(.addrWidth(23), .clearpin("true")) e (
    .addr(Bit23_Address), .we(and_6_out), .oe(READOP), .clk(and_7_out), .din(DQ), .dout(e_dout), .clr(reset));
  RAM #(.addrWidth(23), .clearpin("true"), .trigger("falling")) ram_1 (
    .addr(Bit23_Address), .we(and_6_out), .oe(READOP), .clk(and_8_out), .din(DQ), .dout(ram_1_dout),
    .clr(reset));
  and and_9 (and_9_out, READOP, DATA_MOVING);
  assign RWDS_OUT = d_ff_3_q ? LATENCYx2 : 1'bz;  // Controlled_Buffer controlled_buffer_1
  assign RWDS_OUT = and_9_out ? FECLOCK : 1'bz;  // Controlled_Buffer controlled_buffer_2
  and and_10 (and_10_out, READOP, FECLOCK);
  assign DATA_OUT = and_10_out ? e_dout : 8'bz;  // Controlled_Buffer controlled_buffer_3
  not not_6 (not_6_out, FECLOCK);
  and and_11 (and_11_out, READOP, not_6_out);
  assign DATA_OUT = and_11_out ? ram_1_dout : 8'bz;  // Controlled_Buffer controlled_buffer_4

  // Other names for the same wires on the sheet: PSCLOCK = PSRAMCLOCK; RWDSIN = RWDS

  // Notes on the sheet:
  //   contents of rom_1 (hex, n*v repeats v):
  //   5 6 7 8 10*0 3 4
  //   ensure driving device handles the number of cycles for burst ops gracefully
endmodule

module AGU_Helper (
  input  [31:0] Bit32_In,
  input  Scale_WE,
  input  Base_WE,
  input  Imm_WE,
  input  Index_WE,
  input  Clock,
  input  Reset,
  output [2:0] Scale,
  output [31:0] Base,
  output [31:0] Immediate,
  output [31:0] Index
);

  wire [2:0] bit_extender_1_out;

  Register #(.width(3)) ScaleR (.D(bit_extender_1_out), .en(Scale_WE), .clk(Clock), .Q(Scale), .clr(Reset));
  Bit_Extender #(.in_width(32), .out_width(3)) bit_extender_1 (.in(Bit32_In), .out(bit_extender_1_out));
  Register #(.width(32)) BaseR (.D(Bit32_In), .en(Base_WE), .clk(Clock), .Q(Base), .clr(Reset));
  Register #(.width(32)) ImmR (.D(Bit32_In), .en(Imm_WE), .clk(Clock), .Q(Immediate), .clr(Reset));
  Register #(.width(32)) IndexR (.D(Bit32_In), .en(Index_WE), .clk(Clock), .Q(Index), .clr(Reset));
endmodule

module Data_Buffer_R0 (
  input  [7:0] Bit8,
  input  [31:0] Bit32,
  input  [15:0] Bit16_A,
  input  [15:0] Bit16_B,
  input  Write_Enable,
  input  Clock,
  input  Reset,
  output [7:0] Special_8,
  output [31:0] Wide_32,
  output [15:0] Regular_A,
  output [15:0] Regular_B
);

  Register Special_R (.D(Bit8), .en(Write_Enable), .clk(Clock), .Q(Special_8), .clr(Reset));
  Register #(.width(32)) Wide_R (.D(Bit32), .en(Write_Enable), .clk(Clock), .Q(Wide_32), .clr(Reset));
  Register #(.width(16)) REG_RA (.D(Bit16_A), .en(Write_Enable), .clk(Clock), .Q(Regular_A), .clr(Reset));
  Register #(.width(16)) REG_RB (.D(Bit16_B), .en(Write_Enable), .clk(Clock), .Q(Regular_B), .clr(Reset));
endmodule

module Data_Buffer_R1 (
  input  [7:0] Bit8,
  input  [31:0] Bit32,
  input  [15:0] Bit16_A,
  input  [15:0] Bit16_B,
  input  Write_Enable,
  input  Clock,
  input  Reset,
  output [7:0] Special_8,
  output [31:0] Wide_32,
  output [15:0] Regular_A,
  output [15:0] Regular_B
);

  Register Special_R (.D(Bit8), .en(Write_Enable), .clk(Clock), .Q(Special_8), .clr(Reset));
  Register #(.width(32)) Wide_R (.D(Bit32), .en(Write_Enable), .clk(Clock), .Q(Wide_32), .clr(Reset));
  Register #(.width(16)) REG_RA (.D(Bit16_A), .en(Write_Enable), .clk(Clock), .Q(Regular_A), .clr(Reset));
  Register #(.width(16)) REG_RB (.D(Bit16_B), .en(Write_Enable), .clk(Clock), .Q(Regular_B), .clr(Reset));
endmodule

module Data_Buffer_R2 (
  input  [7:0] Bit8,
  input  [31:0] Bit32,
  input  [15:0] Bit16_A,
  input  Write_Enable,
  input  Clock,
  input  Reset,
  output [7:0] Special_8,
  output [31:0] Wide_32,
  output [15:0] Regular_A
);

  Register Special_R (.D(Bit8), .en(Write_Enable), .clk(Clock), .Q(Special_8), .clr(Reset));
  Register #(.width(32)) Wide_R (.D(Bit32), .en(Write_Enable), .clk(Clock), .Q(Wide_32), .clr(Reset));
  Register #(.width(16)) REG_RA (.D(Bit16_A), .en(Write_Enable), .clk(Clock), .Q(Regular_A), .clr(Reset));
endmodule

module Forwarding_Latch (
  input  [31:0] Bit32,
  input  [15:0] Bit16,
  input  Write_Enable,
  input  Clock,
  input  Reset,
  output [31:0] Bit32_Held,
  output [15:0] Bit16_Held
);

  Register #(.width(32)) register_1 (.D(Bit32), .en(Write_Enable), .clk(Clock), .Q(Bit32_Held), .clr(Reset));
  Register #(.width(16)) register_2 (.D(Bit16), .en(Write_Enable), .clk(Clock), .Q(Bit16_Held), .clr(Reset));
endmodule

module Bit3_Arbiter (
  input  RA,
  input  RB,
  input  RC,
  output GA,
  output GB,
  output GC
);

  wire and_2_out, and_3_out, nor_1_out, nor_2_out, nor_3_out;

  nor nor_1 (nor_1_out, GC, GB);
  nor nor_2 (nor_2_out, GA, GC);
  nor nor_3 (nor_3_out, GA, GB);
  and and_1 (GA, RA, nor_1_out);
  and and_2 (and_2_out, RB, nor_2_out);
  and and_3 (and_3_out, RC, nor_3_out);
  and and_4 (GB, ~GA, and_2_out);  // AND_Gate
  and and_5 (GC, ~GA, ~and_2_out, and_3_out);  // AND_Gate
endmodule

module Bit3_Latching_Arbiter (
  input  Reset,
  input  Clock,
  input  RA,
  input  RB,
  input  RC,
  output GA,
  output GB,
  output GC
);

  wire bit3_arbiter_1_ga, bit3_arbiter_1_gb, bit3_arbiter_1_gc;

  Bit3_Arbiter bit3_arbiter_1 (
    .RA(RA), .RB(RB), .RC(RC), .GA(bit3_arbiter_1_ga), .GB(bit3_arbiter_1_gb), .GC(bit3_arbiter_1_gc));
  D_Flip_Flop d_ff_1 (.D(bit3_arbiter_1_ga), .clk(Clock), .Q(GA), .reset(Reset));  // open: Qn, preset
  D_Flip_Flop d_ff_2 (.D(bit3_arbiter_1_gb), .clk(Clock), .Q(GB), .reset(Reset));  // open: Qn, preset
  D_Flip_Flop d_ff_3 (.D(bit3_arbiter_1_gc), .clk(Clock), .Q(GC), .reset(Reset));  // open: Qn, preset
endmodule

module PSRAM_Controller_2 (
  input  Clock,
  input  Reset,
  input  Read,
  input  Write,
  input  [7:0] Bit8_Data,
  input  [25:0] Bit26_Address,
  input  RWDS_In,
  output RWDS_Out,
  output [7:0] Bit8_Out,
  output Setup,
  output Data_Moving
);

  wire and_1_out, and_2_out, and_3_out, and_4_out, and_5_out, CS_Live, d_ff_1_q, demultiplexer_1_out0,
       demultiplexer_1_out1, demultiplexer_1_out2, demultiplexer_1_out3, FE_Clock, Isnt_Setup,
       Max_Setup_Stage, nand_1_out, nor_1_out, not_1_out, not_2_out, not_3_out, not_4_out, not_5_out,
       not_6_out, not_7_out, not_8_out, or_2_out, or_3_out, or_4_out, PSRAM_Clock, RE_Clock,
       RWDS_Latency_X2_q, undriven, undriven_2, undriven_3, undriven_4;
  wire [1:0] Chip_Setup_Select, multiplexer_3_out;
  wire [2:0] bit_extender_1_out, Setup_Stage;
  wire [4:0] adder_1_out, counter_1_q, shifter_1_out;
  wire [6:0] pull_resistor_1_node_2;
  wire [7:0] multiplexer_1_out, multiplexer_2_out, or_1_out, pull_resistor_1_node_3;
  wire [8:8] pull_resistor_1_node;

  D_Flip_Flop Is_Setup (.D(and_3_out), .clk(and_1_out), .Q(Setup), .Qn(Isnt_Setup), .reset(Reset));  // open: preset
  and and_1 (and_1_out, Isnt_Setup, Clock);
  Memory_Clock memory_clock_1 (
    .Clock(Clock), .Reset(Reset), .RE_Clock(RE_Clock), .PSRAM_Clock(PSRAM_Clock), .FE_Clock(FE_Clock));  // open: CPU_Clock
  Pull_Resistor pull_resistor_1 (.node({pull_resistor_1_node_2, or_1_out[7:1], pull_resistor_1_node[8], pull_resistor_1_node_3}));
  assign {pull_resistor_1_node_2, or_1_out[7:1], pull_resistor_1_node[8], pull_resistor_1_node_3} = Setup ? Bit26_Address[23:1] : 23'bz;  // Controlled_Buffer controlled_buffer_1
  or or_1 (or_1_out[0], Isnt_Setup, pull_resistor_1_node[8]);
  Counter #(.max('h3), .trigger("falling"), .width(2)) Chip_Setup (
    .clr(Reset), .up(Max_Setup_Stage), .count(Max_Setup_Stage), .clk(Clock), .Q(Chip_Setup_Select));  // open: load, D, carry
  D_Flip_Flop d_ff_1 (.D(Read), .clk(FE_Clock), .Q(d_ff_1_q), .reset(Reset));  // open: Qn, preset
  // Probe on multiplexer_1_out
  // Probe on Setup_Stage
  Multiplexer #(.select(3), .width(8)) multiplexer_1 (
    .in0({Read, {2{Isnt_Setup}}, {5{1'b0}}}), .in1({1'b0, pull_resistor_1_node_2}), .in2(or_1_out),
    .in3(pull_resistor_1_node_3), .in4({8{1'b0}}), .in5({8{1'b0}}), .in6(8'h8f), .in7(8'he6),
    .out(multiplexer_1_out), .sel(Setup_Stage));
  nand nand_1 (nand_1_out, Data_Moving, d_ff_1_q);
  assign Bit8_Out = nand_1_out ? multiplexer_2_out : 8'bz;  // Controlled_Buffer controlled_buffer_2
  Multiplexer #(.width(8)) multiplexer_2 (
    .in0(multiplexer_1_out), .in1(Bit8_Data), .out(multiplexer_2_out), .sel(Data_Moving));
  and and_2 (and_2_out, Chip_Setup_Select[0], Chip_Setup_Select[1]);
  and and_3 (and_3_out, and_2_out, Max_Setup_Stage);
  Multiplexer #(.width(2)) multiplexer_3 (
    .in0(Bit26_Address[25:24]), .in1(Chip_Setup_Select), .out(multiplexer_3_out), .sel(Isnt_Setup));
  or or_2 (or_2_out, Read, Write, Isnt_Setup);
  D_Flip_Flop d_ff_2 (.D(or_2_out), .clk(FE_Clock), .Q(CS_Live), .reset(Reset));  // open: Qn, preset
  Demultiplexer #(.select(2)) demultiplexer_1 (
    .out0(demultiplexer_1_out0), .out1(demultiplexer_1_out1), .out2(demultiplexer_1_out2),
    .out3(demultiplexer_1_out3), .in(CS_Live), .sel(multiplexer_3_out));
  and and_4 (and_4_out, Data_Moving, Write);
  assign RWDS_Out = and_4_out ? 1'b0 : 1'bz;  // Controlled_Buffer controlled_buffer_3
  Counter #(.max('h7), .trigger("falling"), .width(3)) u_Setup_Stage (
    .clr(or_3_out), .up(CS_Live), .count(CS_Live), .clk(Clock), .Q(Setup_Stage));  // open: load, D, carry
  or or_3 (or_3_out, ~CS_Live, Reset);  // OR_Gate
  not not_1 (not_1_out, demultiplexer_1_out0);
  not not_2 (not_2_out, demultiplexer_1_out1);
  not not_3 (not_3_out, demultiplexer_1_out2);
  not not_4 (not_4_out, demultiplexer_1_out3);
  not not_5 (not_5_out, undriven);
  not not_6 (not_6_out, undriven_2);
  not not_7 (not_7_out, undriven_3);
  not not_8 (not_8_out, undriven_4);
  and and_5 (and_5_out, CS_Live, ~Data_Moving, Setup);  // AND_Gate
  PSRAM_SIM_2 psram_sim_2_1 (
    .Bit8_Data(Bit8_Out), .RWDS(RWDS_Out), .NOT_CS(not_1_out), .Sub_Clock(Clock), .PSRAM_Clock(PSRAM_Clock),
    .FE_Clock(FE_Clock), .reset(Reset), .RWDS_Out(RWDS_Out), .Bit8_Data_Out(Bit8_Out));
  PSRAM_SIM_2 psram_sim_2_2 (
    .Bit8_Data(Bit8_Out), .RWDS(RWDS_Out), .NOT_CS(not_2_out), .Sub_Clock(Clock), .PSRAM_Clock(PSRAM_Clock),
    .FE_Clock(FE_Clock), .reset(Reset), .RWDS_Out(RWDS_Out), .Bit8_Data_Out(Bit8_Out));
  PSRAM_SIM_2 psram_sim_2_3 (
    .Bit8_Data(Bit8_Out), .RWDS(RWDS_Out), .NOT_CS(not_3_out), .Sub_Clock(Clock), .PSRAM_Clock(PSRAM_Clock),
    .FE_Clock(FE_Clock), .reset(Reset), .RWDS_Out(RWDS_Out), .Bit8_Data_Out(Bit8_Out));
  PSRAM_SIM_2 psram_sim_2_4 (
    .Bit8_Data(Bit8_Out), .RWDS(RWDS_Out), .NOT_CS(not_4_out), .Sub_Clock(Clock), .PSRAM_Clock(PSRAM_Clock),
    .FE_Clock(FE_Clock), .reset(Reset), .RWDS_Out(RWDS_Out), .Bit8_Data_Out(Bit8_Out));
  PSRAM_SIM_2 psram_sim_2_5 (
    .Bit8_Data(Bit8_Out), .RWDS(RWDS_Out), .NOT_CS(not_5_out), .Sub_Clock(Clock), .PSRAM_Clock(PSRAM_Clock),
    .FE_Clock(FE_Clock), .reset(Reset), .RWDS_Out(RWDS_Out), .Bit8_Data_Out(Bit8_Out));
  PSRAM_SIM_2 psram_sim_2_6 (
    .Bit8_Data(Bit8_Out), .RWDS(RWDS_Out), .NOT_CS(not_6_out), .Sub_Clock(Clock), .PSRAM_Clock(PSRAM_Clock),
    .FE_Clock(FE_Clock), .reset(Reset), .RWDS_Out(RWDS_Out), .Bit8_Data_Out(Bit8_Out));
  PSRAM_SIM_2 psram_sim_2_7 (
    .Bit8_Data(Bit8_Out), .RWDS(RWDS_Out), .NOT_CS(not_7_out), .Sub_Clock(Clock), .PSRAM_Clock(PSRAM_Clock),
    .FE_Clock(FE_Clock), .reset(Reset), .RWDS_Out(RWDS_Out), .Bit8_Data_Out(Bit8_Out));
  PSRAM_SIM_2 psram_sim_2_8 (
    .Bit8_Data(Bit8_Out), .RWDS(RWDS_Out), .NOT_CS(not_8_out), .Sub_Clock(Clock), .PSRAM_Clock(PSRAM_Clock),
    .FE_Clock(FE_Clock), .reset(Reset), .RWDS_Out(RWDS_Out), .Bit8_Data_Out(Bit8_Out));
  Counter #(.max('h1f), .trigger("falling"), .width(5)) counter_1 (
    .clr(or_4_out), .up(and_5_out), .count(and_5_out), .clk(PSRAM_Clock), .Q(counter_1_q));  // open: load, D, carry
  or or_4 (or_4_out, ~CS_Live, Reset);  // OR_Gate
  and and_6 (Max_Setup_Stage, Setup_Stage[0], Setup_Stage[1], Setup_Stage[2]);
  nor nor_1 (nor_1_out, counter_1_q[0], counter_1_q[1], counter_1_q[2], counter_1_q[3], counter_1_q[4]);
  D_Flip_Flop #(.trigger("falling")) RWDS_Latency_X2 (
    .D(RWDS_Out), .clk(nor_1_out), .Q(RWDS_Latency_X2_q), .reset(Reset));  // open: Qn, preset
  assign bit_extender_1_out = {{2{1'b0}}, RWDS_Latency_X2_q};  // Bit_Extender bit_extender_1
  Shifter #(.width(5)) shifter_1 (.in(5'b00011), .\dist (bit_extender_1_out), .out(shifter_1_out));
  Adder #(.width(5)) adder_1 (.a(5'b00010), .b(shifter_1_out), .out(adder_1_out));  // open: cin, cout
  Comparator #(.mode("unsigned"), .width(5)) comparator_1 (
    .a(adder_1_out), .b(counter_1_q), .eq(Data_Moving));  // open: gt, lt

  // Other names for the same wires on the sheet: Address[25:0] = Bit26_Address;
  //   Chip_Select[1:0] = Bit26_Address[25:24]; Data[7:0] = Bit8_Data; Is_Setup = Setup; RWDS = RWDS_In

  // Notes on the sheet:
  //   number of cycle of latency
  //   PSRAM BINARY SELECT OF CLOCK CYCLES
  //   when assembling, pick a latency to operate at and hard code and gates to identify the numbers
  //   (both latency + 2 and 2*latency + 2)
  //   there are still enough here for 27 bits, but as you can see, they are not connected!, they are ready for removal, just left here for clarity just in case or som ethiing
  //   data moving starts on psram LOW
  //   1st data comes on the following FE high edge after data moving
endmodule

module PSRAM_SIM_2 (
  input  [7:0] Bit8_Data,
  input  RWDS,
  input  NOT_CS,
  input  Sub_Clock,
  input  PSRAM_Clock,
  input  FE_Clock,
  input  reset,
  output RWDS_Out,
  output [7:0] Bit8_Data_Out
);

  wire and_1_out, and_2_out, and_3_out, and_4_out, and_5_out, and_8_out, and_9_out, and_10_out, and_11_out,
       and_12_out, buffer_1_out, buffer_2_out, buffer_3_out, buffer_4_out, comparator_1_eq, comparator_1_lt,
       d_ff_1_q, d_ff_2_q, Data_Moving, decoder_1_out0, decoder_1_out1, decoder_1_out2, decoder_1_out3,
       decoder_1_out4, decoder_1_out5, decoder_1_out6, decoder_1_out7, Effective_Reset,
       memory_clock_1_fe_clock, memory_clock_1_psram_clock, nor_1_out, not_1_out, not_2_out, not_3_out,
       or_2_out, random_1_out, Read, Write;
  wire [1:0] bit_extender_1_out;
  wire [2:0] counter_1_q;
  wire [3:0] adder_1_out, Latency_Waiter_q, rom_2_data, shifter_1_out;
  wire [7:0] counter_2_q, divider_1_out, e_dout, ram_1_dout, register_1_q, register_4_q, register_5_q,
       register_6_q, register_7_q, register_8_q, rom_1_data;
  wire [7:4] register_2_q_2;
  wire [22:0] adder_2_out, bit_extender_2_out;
  wire [22:19] register_2_q;

  nor nor_1 (nor_1_out, and_4_out, and_5_out);
  not not_1 (not_1_out, NOT_CS);
  or or_1 (Effective_Reset, reset, NOT_CS);
  and and_1 (and_1_out, not_1_out, nor_1_out);
  Counter #(.max('h7), .trigger("falling"), .width(3)) counter_1 (
    .clr(Effective_Reset), .up(not_1_out), .count(and_1_out), .clk(Sub_Clock), .Q(counter_1_q));  // open: load, D, carry
  Random #(.width(1)) random_1 (.next(not_1_out), .clk(not_1_out), .out(random_1_out));  // open: clr
  buf buffer_1 (buffer_1_out, not_1_out);
  buf buffer_2 (buffer_2_out, buffer_1_out);
  and and_2 (and_2_out, not_1_out, or_2_out);
  Memory_Clock memory_clock_1 (
    .Clock(Sub_Clock), .Reset(reset), .PSRAM_Clock(memory_clock_1_psram_clock),
    .FE_Clock(memory_clock_1_fe_clock));  // open: CPU_Clock, RE_Clock
  D_Flip_Flop d_ff_1 (.D(random_1_out), .clk(buffer_4_out), .Q(d_ff_1_q));  // open: Qn, preset, reset
  buf buffer_3 (buffer_3_out, buffer_2_out);
  buf buffer_4 (buffer_4_out, buffer_3_out);
  Decoder #(.select(3)) decoder_1 (
    .out0(decoder_1_out0), .out1(decoder_1_out1), .out2(decoder_1_out2), .out3(decoder_1_out3),
    .out4(decoder_1_out4), .out5(decoder_1_out5), .out6(decoder_1_out6), .out7(decoder_1_out7),
    .sel(counter_1_q), .en(not_1_out));
  Register register_1 (.D(Bit8_Data), .en(decoder_1_out0), .clk(Sub_Clock), .Q(register_1_q), .clr(Effective_Reset));
  assign RWDS_Out = and_2_out ? d_ff_1_q : 1'bz;  // Controlled_Buffer controlled_buffer_1
  or or_2 (or_2_out, decoder_1_out4, decoder_1_out3, decoder_1_out2, decoder_1_out1, decoder_1_out0);
  and and_3 (and_3_out, decoder_1_out6, register_1_q[6]);
  Register register_2 (
    .D(Bit8_Data), .en(decoder_1_out1), .clk(Sub_Clock), .Q({register_2_q_2, register_2_q}),
    .clr(Effective_Reset));
  and and_4 (and_4_out, decoder_1_out6, ~register_1_q[6]);  // AND_Gate
  and and_5 (and_5_out, decoder_1_out7, register_1_q[6]);
  Register register_3 (.D(Bit8_Data), .en(and_3_out), .clk(Sub_Clock), .clr(reset));  // open: Q
  and and_6 (Read, register_1_q[7], ~register_1_q[6]);  // AND_Gate
  and and_7 (Write, ~register_1_q[7], ~register_1_q[6]);  // AND_Gate
  and and_8 (and_8_out, decoder_1_out7, register_1_q[6]);
  Register register_4 (.D(Bit8_Data), .en(decoder_1_out2), .clk(Sub_Clock), .Q(register_4_q), .clr(Effective_Reset));
  Register register_5 (.D(Bit8_Data), .en(and_8_out), .clk(Sub_Clock), .Q(register_5_q), .clr(reset));
  not not_2 (not_2_out, Data_Moving);
  Counter #(.max('hf), .trigger("falling"), .width(4)) Latency_Waiter (
    .clr(Effective_Reset), .up(not_2_out), .count(not_2_out), .clk(PSRAM_Clock), .Q(Latency_Waiter_q));  // open: load, D, carry
  Register register_6 (.D(Bit8_Data), .en(decoder_1_out3), .clk(Sub_Clock), .Q(register_6_q), .clr(Effective_Reset));
  ROM #(.addrWidth(2)) rom_1 (.addr(register_5_q[1:0]), .data(rom_1_data));
  ROM #(.addrWidth(4), .dataWidth(4)) rom_2 (.addr(register_5_q[7:4]), .data(rom_2_data));
  Register register_7 (.D(Bit8_Data), .en(decoder_1_out4), .clk(Sub_Clock), .Q(register_7_q), .clr(Effective_Reset));
  assign bit_extender_1_out = {{1{1'b0}}, d_ff_1_q};  // Bit_Extender bit_extender_1
  Register register_8 (.D(Bit8_Data), .en(decoder_1_out5), .clk(Sub_Clock), .Q(register_8_q), .clr(Effective_Reset));
  Shifter #(.width(4)) shifter_1 (.in(rom_2_data), .\dist (bit_extender_1_out), .out(shifter_1_out));
  Adder #(.width(4)) adder_1 (.a(4'b0010), .b(shifter_1_out), .out(adder_1_out));  // open: cin, cout
  // Probe on rom_1_data
  Comparator #(.mode("unsigned"), .width(4)) comparator_1 (
    .a(adder_1_out), .b(Latency_Waiter_q), .eq(comparator_1_eq), .lt(comparator_1_lt));  // open: gt
  D_Flip_Flop d_ff_2 (.D(Data_Moving), .clk(PSRAM_Clock), .Q(d_ff_2_q), .reset(Effective_Reset));  // open: Qn, preset
  Counter counter_2 (
    .clr(Effective_Reset), .up(d_ff_2_q), .count(d_ff_2_q), .clk(FE_Clock), .Q(counter_2_q));  // open: load, D, carry
  or or_3 (Data_Moving, comparator_1_eq, comparator_1_lt);
  Divider divider_1 (.a(rom_1_data), .b(8'h2), .out(divider_1_out));  // open: upper, rem
  and and_9 (and_9_out, Read, Data_Moving);
  and and_10 (and_10_out, Write, ~RWDS, Data_Moving);  // AND_Gate
  RAM #(.addrWidth(23), .asyncread("true"), .clearpin("true")) e (
    .addr(adder_2_out), .we(and_10_out), .oe(and_9_out), .clk(PSRAM_Clock), .din(Bit8_Data), .dout(e_dout),
    .clr(reset));
  RAM #(.addrWidth(23), .asyncread("true"), .clearpin("true"), .trigger("falling")) ram_1 (
    .addr(adder_2_out), .we(and_10_out), .oe(and_9_out), .clk(PSRAM_Clock), .din(Bit8_Data),
    .dout(ram_1_dout), .clr(reset));
  assign bit_extender_2_out = {{15{1'b0}}, counter_2_q};  // Bit_Extender bit_extender_2
  Adder #(.width(23)) adder_2 (
    .a({register_2_q, register_4_q, register_6_q, register_8_q[2:0]}), .b(bit_extender_2_out),
    .out(adder_2_out));  // open: cin, cout
  Comparator comparator_2 (.a(counter_2_q), .b(divider_1_out));  // open: gt, eq, lt
  assign RWDS_Out = and_9_out ? FE_Clock : 1'bz;  // Controlled_Buffer controlled_buffer_2
  assign Bit8_Data_Out = and_11_out ? e_dout : 8'bz;  // Controlled_Buffer controlled_buffer_3
  assign Bit8_Data_Out = and_12_out ? ram_1_dout : 8'bz;  // Controlled_Buffer controlled_buffer_4
  and and_11 (and_11_out, FE_Clock, and_9_out);
  not not_3 (not_3_out, FE_Clock);
  and and_12 (and_12_out, not_3_out, and_9_out);

  // Notes on the sheet:
  //   contents of rom_1 (hex, n*v repeats v):
  //   80 40 10 20
  //   contents of rom_2 (hex, n*v repeats v):
  //   5 6 7 8 10*0 3 4
  //   rwds should be low sometimes btw
  //   i did it
  //   top 2 signals mmeans the bursdt is over
endmodule

module Memory_Demo (
  input  Clock,
  input  [7:0] in_2,
  input  in_3,
  input  in_4,
  input  in_5,
  input  [26:0] Address,
  input  [15:0] Data,
  input  Two_Byte_Operation,
  input  Read,
  input  Write,
  input  Reset,
  input  Safe_Reset
);

  wire bit3_latching_arbiter_1_ga, bit3_latching_arbiter_1_gb, controlled_buffer_1_out,
       controlled_buffer_2_out, controlled_buffer_3_out, data_cache_2_way_1_p6, data_cache_2_way_1_p7,
       data_cache_2_way_1_p10, data_cache_2_way_1_p11, data_cache_2_way_1_p12, data_cache_2_way_1_p14,
       psram_controller_2_1_p1;
  wire [7:0] data_cache_2_way_1_p13;
  wire [26:0] controlled_buffer_7_out, instruction_cache_2_way_1_p1;

  // Probe on data_cache_2_way_1_p13
  // Probe on data_cache_2_way_1_p13
  // Probe on data_cache_2_way_1_p13
  // Probe on data_cache_2_way_1_p13
  // Data_Cache_2_Way data_cache_2_way_1: pin names not known; wires that end beside it: Read, Write, Two_Byte_Operation, Address, Data, data_cache_2_way_1_p6, data_cache_2_way_1_p7, Clock, Safe_Reset, data_cache_2_way_1_p10, data_cache_2_way_1_p11, data_cache_2_way_1_p12, data_cache_2_way_1_p13, data_cache_2_way_1_p14
  // Instruction_Cache_2_Way instruction_cache_2_way_1: pin names not known; wires that end beside it: instruction_cache_2_way_1_p1
  assign controlled_buffer_1_out = data_cache_2_way_1_p14 ? data_cache_2_way_1_p14 : 1'bz;  // Controlled_Buffer controlled_buffer_1
  assign controlled_buffer_2_out = bit3_latching_arbiter_1_ga ? in_3 : 1'bz;  // Controlled_Buffer controlled_buffer_2
  assign controlled_buffer_3_out = bit3_latching_arbiter_1_ga ? in_4 : 1'bz;  // Controlled_Buffer controlled_buffer_3
  assign controlled_buffer_2_out = bit3_latching_arbiter_1_gb ? data_cache_2_way_1_p11 : 1'bz;  // Controlled_Buffer controlled_buffer_4
  assign controlled_buffer_3_out = bit3_latching_arbiter_1_gb ? data_cache_2_way_1_p10 : 1'bz;  // Controlled_Buffer controlled_buffer_5
  assign in_2 = bit3_latching_arbiter_1_gb ? data_cache_2_way_1_p13 : 8'bz;  // Controlled_Buffer controlled_buffer_6
  Bit3_Latching_Arbiter bit3_latching_arbiter_1 (
    .Reset(Reset), .Clock(Clock), .RA(in_5), .RB(data_cache_2_way_1_p12), .GA(bit3_latching_arbiter_1_ga),
    .GB(bit3_latching_arbiter_1_gb));  // open: RC, GC
  assign controlled_buffer_7_out = bit3_latching_arbiter_1_ga ? instruction_cache_2_way_1_p1 : 27'bz;  // Controlled_Buffer controlled_buffer_7
  assign controlled_buffer_7_out = bit3_latching_arbiter_1_gb ? Address : 27'bz;  // Controlled_Buffer controlled_buffer_8
  // PSRAM_Controller_2 psram_controller_2_1: pin names not known; wires that end beside it: psram_controller_2_1_p1, Clock, Reset, controlled_buffer_2_out, controlled_buffer_3_out, in_2, controlled_buffer_7_out, controlled_buffer_1_out, controlled_buffer_1_out, data_cache_2_way_1_p6, data_cache_2_way_1_p7
  // Probe on data_cache_2_way_1_p6
  // Probe on data_cache_2_way_1_p6
  // Probe on data_cache_2_way_1_p6
endmodule

module Bits (
);

  // DMX_3_8 dmx_3_8_1: pin names not known
  // DMX_3_8 dmx_3_8_2: pin names not known
  // DMX_3_8 dmx_3_8_3: pin names not known
endmodule

module DMX_3_8 (
  input  [2:0] Switch,
  input  Enable,
  output A,
  output B,
  output C,
  output D,
  output E,
  output F,
  output G,
  output H
);

  wire and_1_out, and_2_out, and_3_out, and_4_out, and_5_out, and_6_out, and_7_out, and_8_out, and_9_out,
       and_11_out, and_13_out, and_15_out, and_17_out, and_19_out, and_21_out, and_23_out;

  and and_1 (and_1_out, ~Switch[0], ~Switch[1]);  // AND_Gate
  and and_2 (and_2_out, Switch[0], ~Switch[1]);  // AND_Gate
  and and_3 (and_3_out, ~Switch[0], Switch[1]);  // AND_Gate
  and and_4 (and_4_out, Switch[0], Switch[1]);
  and and_5 (and_5_out, ~Switch[0], ~Switch[1]);  // AND_Gate
  and and_6 (and_6_out, Switch[0], ~Switch[1]);  // AND_Gate
  and and_7 (and_7_out, ~Switch[0], Switch[1]);  // AND_Gate
  and and_8 (and_8_out, Switch[0], Switch[1]);
  and and_9 (and_9_out, and_1_out, ~Switch[2]);  // AND_Gate
  and and_10 (A, and_9_out, Enable);
  and and_11 (and_11_out, and_2_out, ~Switch[2]);  // AND_Gate
  and and_12 (B, and_11_out, Enable);
  and and_13 (and_13_out, and_3_out, ~Switch[2]);  // AND_Gate
  and and_14 (C, and_13_out, Enable);
  and and_15 (and_15_out, and_4_out, ~Switch[2]);  // AND_Gate
  and and_16 (D, and_15_out, Enable);
  and and_17 (and_17_out, and_5_out, Switch[2]);
  and and_18 (E, and_17_out, Enable);
  and and_19 (and_19_out, and_6_out, Switch[2]);
  and and_20 (F, and_19_out, Enable);
  and and_21 (and_21_out, and_7_out, Switch[2]);
  and and_22 (G, and_21_out, Enable);
  and and_23 (and_23_out, and_8_out, Switch[2]);
  and and_24 (H, and_23_out, Enable);
endmodule

module Bit2_CLA_Logic (
  input  C_In,
  input  P0,
  input  G0,
  input  P1,
  input  G1,
  output C1,
  output C_OUT,
  output PG
);

  wire and_1_out, and_2_out, and_3_out;

  and and_1 (and_1_out, C_In, P0);
  and and_2 (and_2_out, P1, G0);
  and and_3 (and_3_out, P1, P0, C_In);
  and and_4 (PG, P0, P1);
  or or_1 (C1, and_1_out, G0);
  or or_2 (C_OUT, G1, and_2_out, and_3_out);
endmodule

module Bit16_Xor (
  input  [15:0] Bit16_A,
  input  [15:0] Bit16_B,
  output [15:0] Bit16_Result
);

  xor xor_1 (Bit16_Result[0], Bit16_A[0], Bit16_B[0]);
  xor xor_2 (Bit16_Result[1], Bit16_A[1], Bit16_B[1]);
  xor xor_3 (Bit16_Result[2], Bit16_A[2], Bit16_B[2]);
  xor xor_4 (Bit16_Result[3], Bit16_A[3], Bit16_B[3]);
  xor xor_5 (Bit16_Result[4], Bit16_A[4], Bit16_B[4]);
  xor xor_6 (Bit16_Result[5], Bit16_A[5], Bit16_B[5]);
  xor xor_7 (Bit16_Result[6], Bit16_A[6], Bit16_B[6]);
  xor xor_8 (Bit16_Result[7], Bit16_A[7], Bit16_B[7]);
  xor xor_9 (Bit16_Result[8], Bit16_A[8], Bit16_B[8]);
  xor xor_10 (Bit16_Result[9], Bit16_A[9], Bit16_B[9]);
  xor xor_11 (Bit16_Result[10], Bit16_A[10], Bit16_B[10]);
  xor xor_12 (Bit16_Result[11], Bit16_A[11], Bit16_B[11]);
  xor xor_13 (Bit16_Result[12], Bit16_A[12], Bit16_B[12]);
  xor xor_14 (Bit16_Result[13], Bit16_A[13], Bit16_B[13]);
  xor xor_15 (Bit16_Result[14], Bit16_A[14], Bit16_B[14]);
  xor xor_16 (Bit16_Result[15], Bit16_A[15], Bit16_B[15]);
endmodule

module Bit16_Toggle_Xor (
  input  [15:0] Bit16_A,
  input  Toggle,
  output [15:0] Bit16_Result
);

  xor xor_1 (Bit16_Result[0], Bit16_A[0], Toggle);
  xor xor_2 (Bit16_Result[1], Bit16_A[1], Toggle);
  xor xor_3 (Bit16_Result[2], Bit16_A[2], Toggle);
  xor xor_4 (Bit16_Result[3], Bit16_A[3], Toggle);
  xor xor_5 (Bit16_Result[4], Bit16_A[4], Toggle);
  xor xor_6 (Bit16_Result[5], Bit16_A[5], Toggle);
  xor xor_7 (Bit16_Result[6], Bit16_A[6], Toggle);
  xor xor_8 (Bit16_Result[7], Bit16_A[7], Toggle);
  xor xor_9 (Bit16_Result[8], Bit16_A[8], Toggle);
  xor xor_10 (Bit16_Result[9], Bit16_A[9], Toggle);
  xor xor_11 (Bit16_Result[10], Bit16_A[10], Toggle);
  xor xor_12 (Bit16_Result[11], Bit16_A[11], Toggle);
  xor xor_13 (Bit16_Result[12], Bit16_A[12], Toggle);
  xor xor_14 (Bit16_Result[13], Bit16_A[13], Toggle);
  xor xor_15 (Bit16_Result[14], Bit16_A[14], Toggle);
  xor xor_16 (Bit16_Result[15], Bit16_A[15], Toggle);
endmodule

module Condition_Evaluator (
  input  [3:0] Bit4_Condition_Selector,
  input  [3:0] Bit4_Flags,
  output Condition_State
);

  wire and_1_out, and_2_out, not_1_out, not_2_out, not_3_out, not_4_out, not_5_out, or_1_out, or_2_out,
       xor_1_out;

  not not_1 (not_1_out, Bit4_Flags[1]);
  not not_2 (not_2_out, Bit4_Flags[3]);
  not not_3 (not_3_out, Bit4_Flags[2]);
  not not_4 (not_4_out, Bit4_Flags[0]);
  not not_5 (not_5_out, xor_1_out);
  and and_1 (and_1_out, not_5_out, not_4_out);
  xor xor_1 (xor_1_out, Bit4_Flags[3], Bit4_Flags[2]);
  or or_1 (or_1_out, xor_1_out, Bit4_Flags[0]);
  and and_2 (and_2_out, not_4_out, Bit4_Flags[1]);
  or or_2 (or_2_out, Bit4_Flags[0], Bit4_Flags[1]);
  Multiplexer #(.select(4)) multiplexer_1 (
    .in0(Bit4_Flags[0]), .in1(not_4_out), .in2(and_1_out), .in3(xor_1_out), .in4(not_5_out), .in5(or_1_out),
    .in6(Bit4_Flags[1]), .in7(not_1_out), .in8(Bit4_Flags[3]), .in9(not_2_out), .in10(1'b1), .in11(1'b0),
    .in12(Bit4_Flags[2]), .in13(not_3_out), .in14(and_2_out), .in15(or_2_out), .out(Condition_State),
    .sel(Bit4_Condition_Selector));

  // Other names for the same wires on the sheet: Zero = Bit4_Flags[0]; Carry = Bit4_Flags[1];
  //   Overflow = Bit4_Flags[2]; Negative = Bit4_Flags[3]
endmodule

module core (
);

  wire and_7_out, bit3_latching_arbiter_1_ga, bit3_latching_arbiter_1_gb, bit4_equal_1_equal,
       bit4_equal_2_equal, bit4_equal_3_equal, bit4_equal_4_equal, bit4_equal_5_equal, bit4_equal_6_equal,
       controlled_buffer_3_out, controlled_buffer_4_out, controlled_buffer_5_out, CPU_Clock, d_ff_1_q,
       data_cache_2_way_1_ram_read, data_cache_2_way_1_ram_write, data_cache_2_way_1_rwds, DCache_Stall,
       DEC_Read_A_Enable, DEC_Read_B_Enable, DEC_Write_Enable, EXE_Bit16_Reg_Write_Enable_q, Exe_Enable,
       Forward_EXE_A, Forward_EXE_B, Forward_MEM_A, Forward_MEM_B, Forward_WB_A, Forward_WB_B, ICache_Stall,
       instruction_cache_2_way_1_ram_read, instruction_cache_2_way_1_rwds, MEM_Bit16_Reg_Write_Enable_q,
       Mem_Enable, Memory_Instruction_Enable, mmu3_1_p19, mmu3_1_p22, mmu3_1_p24, mmu3_1_p25, mmu3_1_p26,
       MMU_Stall, not_2_out, not_3_out, or_1_out, or_2_out, psram_controller_2_1_data_moving, Read_A_Enable,
       Read_B_Enable, READ_Bit16_Reg_Write_Enable_q, Read_Enable, Reg_16_Write_Enable, undriven, undriven_3,
       undriven_4, undriven_5, undriven_6, undriven_7, undriven_8, undriven_9, undriven_10, undriven_11,
       undriven_12, undriven_13, undriven_14, undriven_18, undriven_21, undriven_24, undriven_25,
       undriven_26, Virtual_Instructions_Register_q;
  wire [1:0] bit2_W_Write, undriven_15, undriven_19;
  wire [2:0] EXE_BIT16_MMU_Flag_Mask_q, MMU_Flag_Mask, priority_encoder_1_out, priority_encoder_2_out,
       READ_BIT16_MMU_Flag_Mask_q, undriven_20;
  wire [3:0] alu3_1_zero, ALU_Operation, bit_extender_1_out, bit_extender_2_out, bit_extender_3_out,
       bit_extender_4_out, bit_extender_11_out, bit_extender_17_out, Condition, DEC_ALU_Operation,
       DEC_Condition, DEC_Reg16_Read_A_Select, DEC_Reg16_Read_B_Select, DEC_Reg16_Write_Select,
       EXE_Bit16_Reg_Write_Line_q, Flags_Register_q, MEM_Bit16_Reg_Write_Line_q, MEM_XXX_q,
       multiplexer_12_out, READ_Bit4_ALU_Operation_q, READ_Bit4_Condition_q, READ_Bit16_Reg_Write_Line_q,
       Reg_16_Write_Line, undriven_16, undriven_17;
  wire [4:0] ALU_Config, DEC_ALU_Config, READ_Bit5_ALU_Config_q;
  wire [7:0] bit_extender_14_out, Context_Register_q, controlled_buffer_7_out, data_buffer_r0_1_special_8,
       data_buffer_r1_1_special_8, data_buffer_r2_1_special_8, data_cache_2_way_1_memory_byte,
       IO_MEMORY_REGISTER_q, multiplexer_5_out, multiplexer_9_out, Privillege_Register_q,
       psram_controller_2_1_bit8_out;
  wire [9:0] Bit16_Instruction, Memory_Stage_Control_out, Writeback_Stage_Control_out;
  wire [9:3] Read_Stage_Control_out;
  wire [9:9] Execute_Stage_Control_out;
  wire [11:0] bit_extender_18_out;
  wire [14:0] bit_extender_16_out;
  wire [15:0] alu3_1_bit16_result, Current_Instruction, data_buffer_r0_1_regular_a,
       data_buffer_r0_1_regular_b, data_buffer_r1_1_regular_b, data_buffer_r2_1_regular_a, Data_To_DCache,
       EXE_BIT16_MEM_Config_q, From_DCache, instruction_cache_2_way_1_bit16_to_core, Memory_Config,
       multiplexer_6_out, multiplexer_7_out, multiplexer_11_out, multiplexer_13_out, multiplexer_14_out,
       READ_BIT16_MEM_Config_q, register_file_1_readline_a, rom_1_data, undriven_22, undriven_23;
  wire [26:0] adder_1_out, Address_To_DCache, bit_extender_5_out, bit_extender_6_out, bit_extender_12_out,
       bit_extender_13_out, controlled_buffer_1_out, counter_1_q, Frame_Pointer_q,
       instruction_pointer_2_1_bit27_instruction_address, mmu3_1_p21, mmu3_1_p23,
       stack_pointer_1_bit27_stack_address, undriven_2;
  wire [31:0] bit_extender_7_out, bit_extender_8_out, bit_extender_9_out, bit_extender_15_out,
       data_buffer_r0_1_wide_32, data_buffer_r1_1_wide_32, data_buffer_r2_1_wide_32, multiplexer_8_out,
       multiplexer_10_out, wide_register_file_1_bit32_read_line_a;

  PLA #(.in_width(6), .out_width(10), .\table ("000000 0000000000 # ad\n000001 0000000000 # adc\n000010 0000000001 # adi\n000011 0000000010 # adli\n000100 0000000000 # sub\n000101 0000000000 # sbc\n000110 0000000001 # sbi\n000111 0000000010 # sbli\n001000 0000000000 # mull\n001001 0000000000 # mulh\n001010 0000000000 # and\n001011 0000000000 # andi\n001100 0000000000 # or\n001101 0000000000 # ori")) Execute_Stage_Control (
    .in(Current_Instruction[15:10]), .out({Execute_Stage_Control_out[9], DEC_ALU_Operation, DEC_ALU_Config}));
  PLA #(.in_width(6), .out_width(10), .\table ("000000 0000000000 # ad\n000001 0000000000 # adc\n000010 0000000001 # adi\n000011 0000000010 # adli\n000100 0000000000 # sub\n000101 0000000000 # sbc\n000110 0000000001 # sbi\n000111 0000000010 # sbli\n001000 0000000000 # mull\n001001 0000000000 # mulh\n001010 0000000000 # and\n001011 0000000000 # andi\n001100 0000000000 # or\n001101 0000000000 # ori")) Memory_Stage_Control (
    .in(Current_Instruction[15:10]), .out(Memory_Stage_Control_out));
  PLA #(.in_width(6), .out_width(10), .\table ("000000 0000000000 # ad\n000001 0000000000 # adc\n000010 0000000001 # adi\n000011 0000000010 # adli\n000100 0000000000 # sub\n000101 0000000000 # sbc\n000110 0000000001 # sbi\n000111 0000000010 # sbli\n001000 0000000000 # mull\n001001 0000000000 # mulh\n001010 0000000000 # and\n001011 0000000000 # andi\n001100 0000000000 # or\n001101 0000000000 # ori")) Read_Stage_Control (
    .in(Current_Instruction[15:10]),
    .out({Read_Stage_Control_out, DEC_Write_Enable, DEC_Read_B_Enable, DEC_Read_A_Enable}));
  PLA #(.in_width(6), .out_width(10), .\table ("000000 0000000000 # ad\n000001 0000000000 # adc\n000010 0000000001 # adi\n000011 0000000010 # adli\n000100 0000000000 # sub\n000101 0000000000 # sbc\n000110 0000000001 # sbi\n000111 0000000010 # sbli\n001000 0000000000 # mull\n001001 0000000000 # mulh\n001010 0000000000 # and\n001011 0000000000 # andi\n001100 0000000000 # or\n001101 0000000000 # ori")) Writeback_Stage_Control (
    .in(Current_Instruction[15:10]), .out(Writeback_Stage_Control_out));
  PLA #(.in_width(6), .out_width(3), .\table ("000000 000 # ad\n000001 000 # adc\n000010 001 # adi\n000011 010 # adli\n000100 000 # sub\n000101 000 # sbc\n000110 001 # sbi\n000111 010 # sbli\n001000 000 # mull\n001001 000 # mulh\n001010 000 # and\n001011 000 # andi\n001100 000 # or\n001101 000 # ori")) Format (.in(Current_Instruction[15:10]));  // open: out
  assign bit_extender_1_out = {{1{1'b0}}, Bit16_Instruction[2:0]};  // Bit_Extender bit_extender_1
  assign bit_extender_2_out = {{1{1'b0}}, Bit16_Instruction[5:3]};  // Bit_Extender bit_extender_2
  Multiplexer #(.select(2), .width(4)) multiplexer_1 (
    .in0(Bit16_Instruction[9:6]), .in1(bit_extender_2_out), .in2(Bit16_Instruction[9:6]),
    .in3(bit_extender_3_out), .out(DEC_Reg16_Write_Select));  // open: sel
  Bit_Extender #(.in_width(5), .out_width(4), .\type ("zero")) bit_extender_3 (
    .in(Bit16_Instruction[9:5]), .out(bit_extender_3_out));
  Multiplexer #(.select(2), .width(4)) multiplexer_2 (
    .in0(bit_extender_2_out), .in1(bit_extender_1_out), .in2(bit_extender_3_out), .in3(bit_extender_4_out),
    .out(DEC_Reg16_Read_A_Select));  // open: sel
  Bit_Extender #(.in_width(5), .out_width(4), .\type ("zero")) bit_extender_4 (
    .in(Bit16_Instruction[4:0]), .out(bit_extender_4_out));
  Multiplexer #(.select(2), .width(4)) multiplexer_3 (
    .in0(bit_extender_1_out), .in1(bit_extender_2_out), .out(DEC_Reg16_Read_B_Select));  // open: in2, in3, sel
  Multiplexer #(.select(2), .width(4)) multiplexer_4 (
    .in0(Bit16_Instruction[9:6]), .in1(bit_extender_3_out), .in2(Bit16_Instruction[9:6]), .out(DEC_Condition));  // open: in3, sel
  nor nor_1 (Read_Enable, 1'b0, MMU_Stall, DCache_Stall);
  Register #(.width(4)) READ_Bit16_Reg_Write_Line (
    .D(DEC_Reg16_Write_Select), .en(Read_Enable), .clk(undriven), .Q(READ_Bit16_Reg_Write_Line_q), .clr(1'b0));
  Register #(.width(1)) READ_Bit16_Reg_Write_Enable (
    .en(Read_Enable), .clk(undriven), .Q(READ_Bit16_Reg_Write_Enable_q), .clr(1'b0));  // open: D
  Register #(.width(1)) READ_Bit16_Reg_Read_A_Enable (
    .D(DEC_Read_A_Enable), .en(Read_Enable), .clk(undriven), .Q(Read_A_Enable), .clr(1'b0));
  Register #(.width(1)) READ_Bit16_Reg_Read_B_Enable (
    .D(DEC_Read_B_Enable), .en(Read_Enable), .clk(undriven), .Q(Read_B_Enable), .clr(1'b0));
  Register #(.width(4)) READ_Bit4_ALU_Operation (
    .D(DEC_ALU_Operation), .en(Read_Enable), .clk(undriven), .Q(READ_Bit4_ALU_Operation_q), .clr(1'b0));
  Register #(.width(4)) READ_Bit4_Condition (
    .D(DEC_Condition), .en(Read_Enable), .clk(undriven), .Q(READ_Bit4_Condition_q), .clr(1'b0));
  Register #(.width(5)) READ_Bit5_ALU_Config (
    .D(DEC_ALU_Config), .en(Read_Enable), .clk(undriven), .Q(READ_Bit5_ALU_Config_q), .clr(1'b0));
  Register #(.width(16)) READ_BIT16_MEM_Config (
    .en(Read_Enable), .clk(undriven), .Q(READ_BIT16_MEM_Config_q), .clr(1'b0));  // open: D
  Register #(.width(3)) READ_BIT16_MMU_Flag_Mask (
    .en(Read_Enable), .clk(undriven), .Q(READ_BIT16_MMU_Flag_Mask_q), .clr(1'b0));  // open: D
  or or_1 (or_1_out, 1'b0, 1'b0);
  nor nor_2 (Exe_Enable, MMU_Stall, DCache_Stall);
  Register #(.width(4)) EXE_Bit16_Reg_Write_Line (
    .D(READ_Bit16_Reg_Write_Line_q), .en(Exe_Enable), .clk(undriven), .Q(EXE_Bit16_Reg_Write_Line_q),
    .clr(or_1_out));
  Register #(.width(1)) EXE_Bit16_Reg_Write_Enable (
    .D(READ_Bit16_Reg_Write_Enable_q), .en(Exe_Enable), .clk(undriven), .Q(EXE_Bit16_Reg_Write_Enable_q),
    .clr(or_1_out));
  Register #(.width(4)) EXE_Bit4_ALU_Operation (
    .D(READ_Bit4_ALU_Operation_q), .en(Exe_Enable), .clk(undriven), .Q(ALU_Operation), .clr(or_1_out));
  Register #(.width(4)) EXE_Bit4_Condition (
    .D(READ_Bit4_Condition_q), .en(Exe_Enable), .clk(undriven), .Q(Condition), .clr(or_1_out));
  Register #(.width(5)) EXE_Bit5_ALU_Config (
    .D(READ_Bit5_ALU_Config_q), .en(Exe_Enable), .clk(undriven), .Q(ALU_Config), .clr(or_1_out));
  Register #(.width(16)) EXE_BIT16_MEM_Config (
    .D(READ_BIT16_MEM_Config_q), .en(or_1_out), .clk(undriven), .Q(EXE_BIT16_MEM_Config_q), .clr(or_1_out));
  Register #(.width(3)) EXE_BIT16_MMU_Flag_Mask (
    .D(READ_BIT16_MMU_Flag_Mask_q), .en(Exe_Enable), .clk(undriven), .Q(EXE_BIT16_MMU_Flag_Mask_q),
    .clr(or_1_out));
  Bit4_Equal bit4_equal_1 (
    .Bit4_B(EXE_Bit16_Reg_Write_Line_q), .Bit4_A(DEC_Reg16_Read_A_Select), .Equal(bit4_equal_1_equal));
  Bit4_Equal bit4_equal_2 (
    .Bit4_B(EXE_Bit16_Reg_Write_Line_q), .Bit4_A(DEC_Reg16_Read_B_Select), .Equal(bit4_equal_2_equal));
  or or_2 (or_2_out, 1'b0, 1'b0, 1'b0);
  not not_1 (Mem_Enable, DCache_Stall);
  and and_1 (Forward_EXE_A, EXE_Bit16_Reg_Write_Enable_q, Read_A_Enable, bit4_equal_1_equal);
  and and_2 (Forward_EXE_B, EXE_Bit16_Reg_Write_Enable_q, Read_B_Enable, bit4_equal_2_equal);
  Register #(.width(4)) MEM_Bit16_Reg_Write_Line (
    .D(EXE_Bit16_Reg_Write_Line_q), .en(Mem_Enable), .clk(undriven), .Q(MEM_Bit16_Reg_Write_Line_q),
    .clr(or_2_out));
  Register #(.width(1)) MEM_Bit16_Reg_Write_Enable (
    .D(EXE_Bit16_Reg_Write_Enable_q), .en(Mem_Enable), .clk(undriven), .Q(MEM_Bit16_Reg_Write_Enable_q),
    .clr(or_2_out));
  Register #(.width(4)) MEM_XXX (.D(ALU_Operation), .en(Mem_Enable), .Q(MEM_XXX_q), .clr(or_2_out));  // open: clk
  Register #(.width(16)) MEM_BIT16_MEM_Config (
    .D(EXE_BIT16_MEM_Config_q), .en(Mem_Enable), .clk(undriven), .Q(Memory_Config), .clr(or_2_out));
  Register #(.width(3)) MEM_BIT16_MMU_Flag_Mask (
    .D(EXE_BIT16_MMU_Flag_Mask_q), .en(Mem_Enable), .clk(undriven), .Q(MMU_Flag_Mask), .clr(or_2_out));
  Bit4_Equal bit4_equal_3 (
    .Bit4_B(MEM_Bit16_Reg_Write_Line_q), .Bit4_A(DEC_Reg16_Read_A_Select), .Equal(bit4_equal_3_equal));
  Bit4_Equal bit4_equal_4 (
    .Bit4_B(MEM_Bit16_Reg_Write_Line_q), .Bit4_A(DEC_Reg16_Read_B_Select), .Equal(bit4_equal_4_equal));
  or or_3 (Forward_MEM_B, 1'b0, 1'b0, 1'b0, 1'b0);
  Register #(.width(4)) WB_Bit16_Reg_Write_Line (
    .D(MEM_Bit16_Reg_Write_Line_q), .en(1'b1), .clk(undriven), .Q(Reg_16_Write_Line), .clr(Forward_MEM_B));
  Register #(.width(1)) WB_Bit16_Reg_Write_Enable (
    .D(MEM_Bit16_Reg_Write_Enable_q), .en(1'b1), .clk(undriven), .Q(Reg_16_Write_Enable), .clr(Forward_MEM_B));
  and and_3 (Forward_MEM_A, MEM_Bit16_Reg_Write_Enable_q, Read_A_Enable, bit4_equal_3_equal);
  and and_4 (Forward_MEM_B, MEM_Bit16_Reg_Write_Enable_q, Read_B_Enable, bit4_equal_4_equal);
  Register #(.width(4)) WB_XXX (.D(MEM_XXX_q), .clr(Forward_MEM_B));  // open: en, clk, Q
  Bit4_Equal bit4_equal_5 (.Bit4_B(Reg_16_Write_Line), .Bit4_A(DEC_Reg16_Read_A_Select), .Equal(bit4_equal_5_equal));
  Bit4_Equal bit4_equal_6 (.Bit4_B(Reg_16_Write_Line), .Bit4_A(DEC_Reg16_Read_B_Select), .Equal(bit4_equal_6_equal));
  and and_5 (Forward_WB_A, Reg_16_Write_Enable, Read_A_Enable, bit4_equal_5_equal);
  and and_6 (Forward_WB_B, Reg_16_Write_Enable, Read_B_Enable, bit4_equal_6_equal);
  Bit_Extender #(.in_width(32), .out_width(27), .\type ("zero")) bit_extender_5 (
    .in(data_buffer_r2_1_wide_32), .out(bit_extender_5_out));
  Bit_Extender #(.in_width(32), .out_width(27), .\type ("zero")) bit_extender_6 (
    .in(data_buffer_r2_1_wide_32), .out(bit_extender_6_out));
  Register IO_MEMORY_REGISTER (
    .D(data_buffer_r2_1_special_8), .en(undriven_8), .clk(undriven_18), .Q(IO_MEMORY_REGISTER_q),
    .clr(undriven_21));
  Register Context_Register (
    .D(data_buffer_r2_1_special_8), .en(undriven_7), .clk(undriven_18), .Q(Context_Register_q),
    .clr(undriven_21));
  Register #(.width(27)) Frame_Pointer (
    .D(bit_extender_6_out), .en(undriven_6), .clk(undriven_18), .Q(Frame_Pointer_q), .clr(undriven_21));
  Register Privillege_Register (
    .D(data_buffer_r2_1_special_8), .en(undriven_5), .clk(undriven_18), .Q(Privillege_Register_q),
    .clr(undriven_21));
  Register #(.width(1)) Virtual_Instructions_Register (
    .en(undriven_12), .clk(undriven_18), .Q(Virtual_Instructions_Register_q), .clr(undriven_21));  // open: D
  Register #(.width(1)) Startup_Rom (.Q(Memory_Instruction_Enable));  // open: D, en, clk, clr
  Register_File register_file_1 (
    .Write_Data(data_buffer_r2_1_regular_a), .Read_Address_B(undriven_17), .Read_B_Enable(Read_B_Enable),
    .Read_Address_A(undriven_16), .Read_A_Enable(Read_A_Enable), .Write_Address(Reg_16_Write_Line),
    .Write_Enable(Reg_16_Write_Enable), .Clock(undriven_18), .Clear_All_Registers(undriven_21),
    .ReadLine_A(register_file_1_readline_a));  // open: ReadLine_B
  Wide_Register_File wide_register_file_1 (
    .Bit32_Write_Data(data_buffer_r2_1_wide_32), .Write_Enable(undriven_3), .Write_Address(bit2_W_Write),
    .Read_A_Address(undriven_15), .Clock(undriven_18), .Reset(undriven_21),
    .Bit32_Read_Line_A(wide_register_file_1_bit32_read_line_a));  // open: Read_A_Enable, Read_B_Enable, Read_B_Address, Read_C_Enable, Read_C_Address, Bit32_Read_Line_C, Bit32_Read_Line_B
  Instruction_Pointer_2 instruction_pointer_2_1 (
    .Offset_Mode(undriven_9), .Bit27_Offset(undriven_2), .Bit27_Address(bit_extender_5_out),
    .Set_Address(undriven_10), .Offset(undriven_11), .Clock(undriven_18), .Reset(undriven_21),
    .Bit27_Instruction_Address(instruction_pointer_2_1_bit27_instruction_address));  // open: Enable, Instruction_Offset_Out_Of_Bounds
  Stack_Pointer stack_pointer_1 (
    .Bit27_Address(bit_extender_5_out), .Set(undriven_4), .Push(undriven_14), .Pop(undriven_13),
    .Clock(undriven_18), .Reset(undriven_21), .Bit27_Stack_Address(stack_pointer_1_bit27_stack_address));
  Priority_Encoder priority_encoder_1 (
    .in0(Read_B_Enable), .in2(Forward_EXE_B), .in3(Forward_MEM_B), .in4(Forward_WB_B),
    .out(priority_encoder_1_out));  // open: in1, in5, in6, in7, en_in, gs, en_out
  Priority_Encoder priority_encoder_2 (
    .in0(Read_A_Enable), .in2(Forward_EXE_A), .in3(Forward_MEM_A), .in4(Forward_WB_A),
    .out(priority_encoder_2_out));  // open: in1, in5, in6, in7, en_in, gs, en_out
  Data_Buffer_R1 data_buffer_r1_1 (
    .Bit8(multiplexer_5_out), .Bit32(multiplexer_8_out), .Bit16_A(multiplexer_6_out),
    .Bit16_B(data_buffer_r0_1_regular_b), .Special_8(data_buffer_r1_1_special_8),
    .Wide_32(data_buffer_r1_1_wide_32), .Regular_A(Data_To_DCache), .Regular_B(data_buffer_r1_1_regular_b));  // open: Write_Enable, Clock, Reset
  Multiplexer #(.width(8)) multiplexer_5 (
    .in0(data_buffer_r0_1_special_8), .in1(bit_extender_14_out), .out(multiplexer_5_out), .sel(ALU_Config[0]));
  Multiplexer #(.width(16)) multiplexer_6 (
    .in0(data_buffer_r0_1_regular_a), .in1(alu3_1_bit16_result), .out(multiplexer_6_out), .sel(ALU_Config[1]));
  Data_Buffer_R2 data_buffer_r2_1 (
    .Bit8(data_buffer_r1_1_special_8), .Bit32(data_buffer_r1_1_wide_32), .Bit16_A(multiplexer_7_out),
    .Special_8(data_buffer_r2_1_special_8), .Wide_32(data_buffer_r2_1_wide_32),
    .Regular_A(data_buffer_r2_1_regular_a));  // open: Write_Enable, Clock, Reset
  Multiplexer #(.select(2), .width(16)) multiplexer_7 (
    .in0(Data_To_DCache), .in1(data_buffer_r1_1_regular_b), .in2(From_DCache), .out(multiplexer_7_out));  // open: in3, sel
  Multiplexer #(.width(32)) multiplexer_8 (
    .in0(data_buffer_r0_1_wide_32), .in1(bit_extender_15_out), .out(multiplexer_8_out), .sel(ALU_Config[2]));
  Data_Buffer_R0 data_buffer_r0_1 (
    .Bit8(multiplexer_9_out), .Bit32(multiplexer_10_out), .Bit16_A(multiplexer_11_out),
    .Bit16_B(multiplexer_13_out), .Special_8(data_buffer_r0_1_special_8), .Wide_32(data_buffer_r0_1_wide_32),
    .Regular_A(data_buffer_r0_1_regular_a), .Regular_B(data_buffer_r0_1_regular_b));  // open: Write_Enable, Clock, Reset
  assign bit_extender_7_out = {{5{1'b0}}, instruction_pointer_2_1_bit27_instruction_address};  // Bit_Extender bit_extender_7
  assign bit_extender_8_out = {{5{1'b0}}, stack_pointer_1_bit27_stack_address};  // Bit_Extender bit_extender_8
  Multiplexer #(.select(2), .width(8)) multiplexer_9 (
    .in0(IO_MEMORY_REGISTER_q), .in1(Context_Register_q), .in2(Privillege_Register_q),
    .out(multiplexer_9_out), .sel(undriven_19));  // open: in3
  assign bit_extender_9_out = {{5{1'b0}}, Frame_Pointer_q};  // Bit_Extender bit_extender_9
  Bit_Extender #(.in_width(32), .out_width(27), .\type ("zero")) bit_extender_10 (
    .in(data_buffer_r1_1_wide_32), .out(Address_To_DCache));
  Bit_Extender #(.in_width(16), .out_width(4), .\type ("zero")) bit_extender_11 (
    .in(data_buffer_r0_1_regular_a), .out(bit_extender_11_out));
  Multiplexer #(.select(3), .width(32)) multiplexer_10 (
    .in0(wide_register_file_1_bit32_read_line_a), .in1(bit_extender_7_out), .in2(bit_extender_8_out),
    .in3(bit_extender_9_out), .in4(bit_extender_15_out), .in5(data_buffer_r1_1_wide_32),
    .in6(data_buffer_r2_1_wide_32), .out(multiplexer_10_out), .sel(undriven_20));  // open: in7
  Multiplexer #(.select(3), .width(16)) multiplexer_11 (
    .in0(register_file_1_readline_a), .in1(undriven_23), .in2(multiplexer_7_out), .in3(alu3_1_bit16_result),
    .in4(data_buffer_r2_1_regular_a), .out(multiplexer_11_out), .sel(priority_encoder_2_out));  // open: in5, in6, in7
  Bit_Extender #(.in_width(32), .out_width(27), .\type ("zero")) bit_extender_12 (
    .in(data_buffer_r0_1_wide_32), .out(bit_extender_12_out));
  assign bit_extender_13_out = {{11{data_buffer_r0_1_regular_a[15]}}, data_buffer_r0_1_regular_a};  // Bit_Extender bit_extender_13
  Counter #(.max('h7ffffff), .width(27)) counter_1 (
    .clk(CPU_Clock), .Q(counter_1_q));  // open: clr, load, up, count, D, carry
  Register #(.width(4)) Flags_Register (
    .D(multiplexer_12_out), .en(ALU_Config[4]), .clk(undriven_24), .Q(Flags_Register_q), .clr(undriven_25));
  Multiplexer #(.width(4)) multiplexer_12 (
    .in0(alu3_1_zero), .in1(bit_extender_11_out), .out(multiplexer_12_out), .sel(ALU_Config[3]));
  ALU3 alu3_1 (
    .ALU_Enable(1'b1), .Bit4_Operation(ALU_Operation), .Bit16_A(data_buffer_r0_1_regular_a),
    .Bit16_B(data_buffer_r0_1_regular_b), .Zero(alu3_1_zero[0]), .Overflow(alu3_1_zero[1]),
    .Carry(alu3_1_zero[2]), .Negative(alu3_1_zero[3]), .Bit16_Result(alu3_1_bit16_result));
  Adder #(.width(27)) adder_1 (.a(bit_extender_12_out), .b(bit_extender_13_out), .out(adder_1_out));  // open: cin, cout
  Multiplexer #(.select(3), .width(16)) multiplexer_13 (
    .in0(undriven_22), .in1(undriven_23), .in2(multiplexer_7_out), .in3(alu3_1_bit16_result),
    .in4(data_buffer_r2_1_regular_a), .out(multiplexer_13_out), .sel(priority_encoder_1_out));  // open: in5, in6, in7
  assign bit_extender_14_out = {{4{1'b0}}, Flags_Register_q};  // Bit_Extender bit_extender_14
  assign bit_extender_15_out = {{5{1'b0}}, adder_1_out};  // Bit_Extender bit_extender_15
  Condition_Evaluator condition_evaluator_1 (
    .Bit4_Condition_Selector(Condition), .Bit4_Flags(Flags_Register_q));  // open: Condition_State
  Bit_Extender #(.in_width(16), .out_width(15), .\type ("zero")) bit_extender_16 (
    .in(data_buffer_r0_1_regular_a), .out(bit_extender_16_out));
  Bit_Extender #(.in_width(16), .out_width(4), .\type ("zero")) bit_extender_17 (
    .in(data_buffer_r0_1_regular_a), .out(bit_extender_17_out));
  Memory_Clock memory_clock_1 (
    .Clock(undriven_26), .Reset(mmu3_1_p19), .CPU_Clock(CPU_Clock));  // open: RE_Clock, PSRAM_Clock, FE_Clock
  Multiplexer #(.width(16)) multiplexer_14 (
    .in0(rom_1_data), .in1(instruction_cache_2_way_1_bit16_to_core), .out(multiplexer_14_out),
    .sel(Memory_Instruction_Enable));
  not not_2 (not_2_out, Virtual_Instructions_Register_q);
  D_Flip_Flop #(.trigger("low")) d_ff_1 (
    .D(not_3_out), .clk(CPU_Clock), .Q(d_ff_1_q), .reset(mmu3_1_p19));  // open: Qn, preset
  not not_3 (not_3_out, DCache_Stall);
  Register #(.width(16)) Instruction_Register (.D(multiplexer_14_out), .Q(Current_Instruction));  // open: en, clk, clr
  and and_7 (and_7_out, d_ff_1_q, CPU_Clock);
  ROM #(.addrWidth(12), .dataWidth(16)) rom_1 (.addr(bit_extender_18_out), .data(rom_1_data));
  Bit_Extender #(.in_width(27), .out_width(12), .\type ("zero")) bit_extender_18 (
    .in(counter_1_q), .out(bit_extender_18_out));
  // MMU3 mmu3_1: pin names not known; wires that end beside it: counter_1_q, Virtual_Instructions_Register_q, not_2_out, Address_To_DCache, Memory_Config[8], Memory_Config[9], Memory_Config[10], Memory_Config[11], From_DCache, Context_Register_q, Memory_Config[12], MMU_Flag_Mask, Memory_Config[13], bit_extender_16_out, Memory_Config[14], bit_extender_17_out, Memory_Config[15], 1'b1, mmu3_1_p19, and_7_out, mmu3_1_p21, mmu3_1_p22, mmu3_1_p23, mmu3_1_p24, mmu3_1_p25, mmu3_1_p26, MMU_Stall
  Instruction_Cache_2_Way instruction_cache_2_way_1 (
    .Read(mmu3_1_p22), .Two_Byte_Operation(mmu3_1_p22), .Invalidate_Address(Memory_Config[0]),
    .Invalidate_Line(Memory_Config[1]), .Set(Memory_Config[2]), .Bit26_Address(mmu3_1_p21[25:0]),
    .Bit8_From_Memory(psram_controller_2_1_bit8_out), .Ram_Data_Moving(psram_controller_2_1_data_moving),
    .Clock(undriven_26), .Reset(mmu3_1_p19), .Bit16_To_Core(instruction_cache_2_way_1_bit16_to_core),
    .Ram_Read(instruction_cache_2_way_1_ram_read), .Requesting_Ram(ICache_Stall),
    .RWDS(instruction_cache_2_way_1_rwds));
  Data_Cache_2_Way data_cache_2_way_1 (
    .Read(mmu3_1_p24), .Write(mmu3_1_p25), .Two_Byte_Operation(mmu3_1_p26), .Flush_Address(Memory_Config[3]),
    .Invalidate_Address(Memory_Config[4]), .Flush_Line(Memory_Config[5]), .Invalidate_Line(Memory_Config[6]),
    .Set(Memory_Config[7]), .Bit26_Address(mmu3_1_p23[25:0]), .Bit16_Data(Data_To_DCache),
    .Bit8_From_Memory(psram_controller_2_1_bit8_out), .Ram_Data_Moving(psram_controller_2_1_data_moving),
    .Clock(undriven_26), .Reset(mmu3_1_p19), .Bit16_To_Core(From_DCache),
    .Ram_Write(data_cache_2_way_1_ram_write), .Ram_Read(data_cache_2_way_1_ram_read),
    .Requesting_Ram(DCache_Stall), .Memory_Byte(data_cache_2_way_1_memory_byte),
    .RWDS(data_cache_2_way_1_rwds));
  assign controlled_buffer_1_out = bit3_latching_arbiter_1_gb ? mmu3_1_p23 : 27'bz;  // Controlled_Buffer controlled_buffer_1
  assign controlled_buffer_1_out = bit3_latching_arbiter_1_ga ? mmu3_1_p21 : 27'bz;  // Controlled_Buffer controlled_buffer_2
  assign controlled_buffer_3_out = bit3_latching_arbiter_1_ga ? instruction_cache_2_way_1_ram_read : 1'bz;  // Controlled_Buffer controlled_buffer_3
  assign controlled_buffer_4_out = bit3_latching_arbiter_1_gb ? instruction_cache_2_way_1_rwds : 1'bz;  // Controlled_Buffer controlled_buffer_4
  assign controlled_buffer_5_out = bit3_latching_arbiter_1_gb ? data_cache_2_way_1_ram_write : 1'bz;  // Controlled_Buffer controlled_buffer_5
  assign controlled_buffer_3_out = bit3_latching_arbiter_1_gb ? data_cache_2_way_1_ram_read : 1'bz;  // Controlled_Buffer controlled_buffer_6
  assign controlled_buffer_7_out = bit3_latching_arbiter_1_gb ? data_cache_2_way_1_memory_byte : 8'bz;  // Controlled_Buffer controlled_buffer_7
  assign controlled_buffer_4_out = bit3_latching_arbiter_1_gb ? data_cache_2_way_1_rwds : 1'bz;  // Controlled_Buffer controlled_buffer_8
  Bit3_Latching_Arbiter bit3_latching_arbiter_1 (
    .Reset(mmu3_1_p19), .Clock(undriven_26), .RA(ICache_Stall), .RB(DCache_Stall),
    .GA(bit3_latching_arbiter_1_ga), .GB(bit3_latching_arbiter_1_gb));  // open: RC, GC
  PSRAM_Controller_2 psram_controller_2_1 (
    .Clock(undriven_26), .Reset(mmu3_1_p19), .Read(controlled_buffer_3_out), .Write(controlled_buffer_5_out),
    .Bit8_Data(controlled_buffer_7_out), .Bit26_Address(controlled_buffer_1_out[25:0]),
    .RWDS_In(controlled_buffer_4_out), .Bit8_Out(psram_controller_2_1_bit8_out),
    .Data_Moving(psram_controller_2_1_data_moving));  // open: RWDS_Out, Setup
  // Pins of 26 and 27 bits meet at mmu3_1_p23
  // Pins of 26 and 27 bits meet at controlled_buffer_1_out
  // Pins of 26 and 27 bits meet at mmu3_1_p21

  // Other names for the same wires on the sheet: Opcode[5:0] = Current_Instruction[15:10];
  //   Stall_Before_Mem = MMU_Stall; Stall_Before_Wb = DCache_Stall

  // Notes on the sheet:
  //   normal
  //   two
  //   immediate
  //   READ
  //   EXECUTE
  //   MEMORY
  //   WRITEBACK
  //   8bit special wb
  //   16 wb
  //   32 wb
  //   alu alredy buffers this line
  //   simplyfy control and consider fpu vs simd vs none
  //   handle flags
  //   IP increment on opposite side to IR?
  //   data cache cross-cacheline request splitting
  //   maybe do in mmu bc mmu has similar logic for page width?
endmodule

module Bit32_Toggle_Xor (
  input  [31:0] Bit32_In,
  input  Toggle,
  output [31:0] Bit32_Out
);

  xor xor_1 (Bit32_Out[0], Bit32_In[0], Toggle);
  xor xor_2 (Bit32_Out[1], Bit32_In[1], Toggle);
  xor xor_3 (Bit32_Out[2], Bit32_In[2], Toggle);
  xor xor_4 (Bit32_Out[3], Bit32_In[3], Toggle);
  xor xor_5 (Bit32_Out[4], Bit32_In[4], Toggle);
  xor xor_6 (Bit32_Out[5], Bit32_In[5], Toggle);
  xor xor_7 (Bit32_Out[6], Bit32_In[6], Toggle);
  xor xor_8 (Bit32_Out[7], Bit32_In[7], Toggle);
  xor xor_9 (Bit32_Out[8], Bit32_In[8], Toggle);
  xor xor_10 (Bit32_Out[9], Bit32_In[9], Toggle);
  xor xor_11 (Bit32_Out[10], Bit32_In[10], Toggle);
  xor xor_12 (Bit32_Out[11], Bit32_In[11], Toggle);
  xor xor_13 (Bit32_Out[12], Bit32_In[12], Toggle);
  xor xor_14 (Bit32_Out[13], Bit32_In[13], Toggle);
  xor xor_15 (Bit32_Out[14], Bit32_In[14], Toggle);
  xor xor_16 (Bit32_Out[15], Bit32_In[15], Toggle);
  xor xor_17 (Bit32_Out[16], Bit32_In[16], Toggle);
  xor xor_18 (Bit32_Out[17], Bit32_In[17], Toggle);
  xor xor_19 (Bit32_Out[18], Bit32_In[18], Toggle);
  xor xor_20 (Bit32_Out[19], Bit32_In[19], Toggle);
  xor xor_21 (Bit32_Out[20], Bit32_In[20], Toggle);
  xor xor_22 (Bit32_Out[21], Bit32_In[21], Toggle);
  xor xor_23 (Bit32_Out[22], Bit32_In[22], Toggle);
  xor xor_24 (Bit32_Out[23], Bit32_In[23], Toggle);
  xor xor_25 (Bit32_Out[24], Bit32_In[24], Toggle);
  xor xor_26 (Bit32_Out[25], Bit32_In[25], Toggle);
  xor xor_27 (Bit32_Out[26], Bit32_In[26], Toggle);
  xor xor_28 (Bit32_Out[27], Bit32_In[27], Toggle);
  xor xor_29 (Bit32_Out[28], Bit32_In[28], Toggle);
  xor xor_30 (Bit32_Out[29], Bit32_In[29], Toggle);
  xor xor_31 (Bit32_Out[30], Bit32_In[30], Toggle);
  xor xor_32 (Bit32_Out[31], Bit32_In[31], Toggle);
endmodule
module MMU3 (
  input  [25:0] Bit27_Instruction_Address,
  input  Instruction_Translate,
  input  Instruction_Passthrough,
  input  [25:0] Bit27_Data_Address,
  input  Data_Translate,
  input  Data_Passthrough,
  input  Two_Byte_Operation,
  input  Data_Direction,
  input  [15:0] Bit16_From_Data_Cache,
  input  [7:0] Bit8_Context_Id,
  input  [3:0] Bit4_Lower_Flag_Mask,
  input  Lower_Flag_Mask_Enable,
  input  [13:0] Bit14_Target_Page,
  input  Invalidate_Target_Page,
  input  [2:0] Bit3_Target_Translation_Page,
  input  Invalidate_Translation_Page,
  input  Invalidate_All,
  input  Enable,
  input  Reset,
  input  Clock,
  output [25:0] Bit26_Data_Address_Out,
  output Data_Read,
  output Data_Write,
  output Data_Two_Byte,
  output [25:0] Bit26_Instruction_Address_Out,
  output Instruction_Read,
  output [3:0] Bit4_Faults,
  output Is_Fault,
  output Stall
);

  wire adder_1_cout, and_5_out, and_6_out, and_8_out, and_21_out, and_22_out, and_23_out, and_25_out,
       and_26_out, and_27_out, and_29_out, and_30_out, and_31_out, and_32_out, and_33_out, and_34_out, Clear,
       d_ff_1_q, d_ff_1_qn, d_ff_2_qn, d_ff_4_q, D_Miss, D_Resolving_q, D_Resolving_qn, D_TLB_Hit,
       D_TLB_Miss, I_Miss, I_Resolving_q, I_Resolving_qn, I_TLB_Hit, I_TLB_Miss,
       Lower_Translation_Page_Not_Allocated, Lower_Two_Byte_Out_Of_Page_Space,
       Lower_Virtual_Page_Not_Allocated, Lower_Write_Protection_Violation, Miss, nor_1_out, not_1_out,
       not_2_out, or_2_out, or_3_out, or_4_out, or_5_out, or_6_out, or_7_out, or_8_out, or_9_out, or_10_out,
       or_11_out, or_16_out, or_17_out, Translation_Page_Hit, Translation_Page_Rewrite_Miss,
       Two_Byte_Operation_t;
  wire [1:0] priority_encoder_1_p3;
  wire [1:1] and_24_out;
  wire [2:0] D_Cont_Trans_PGTB_Index, multiplexer_5_out, pull_resistor_1_node,
       translation_lookaside_buffer_1_bit3_least_recently_used_cell,
       translation_lookaside_buffer_2_bit3_least_recently_used_cell;
  wire [3:1] Translation_Page_Table_Address;
  wire [10:0] D_Trans_Page_Index;
  wire [11:0] D_Page_Offset;
  wire [11:1] Translation_Page_Address;
  wire [13:0] multiplexer_3_out, multiplexer_4_out, Translation_Page;
  wire [14:0] bit_extender_3_out, pull_resistor_2_node;
  wire [15:0] bit_extender_1_out, bit_extender_2_out, D_TLB_Result, I_TLB_Result;
  wire [25:0] Data_Instruction_Address, Translated_Instruction_Address;

  and and_1 (Lower_Translation_Page_Not_Allocated, Bit4_Lower_Flag_Mask[0], Lower_Flag_Mask_Enable);
  and and_2 (Lower_Virtual_Page_Not_Allocated, Bit4_Lower_Flag_Mask[1], Lower_Flag_Mask_Enable);
  and and_3 (Lower_Two_Byte_Out_Of_Page_Space, Lower_Flag_Mask_Enable, Bit4_Lower_Flag_Mask[2]);
  and and_4 (Lower_Write_Protection_Violation, Lower_Flag_Mask_Enable, Bit4_Lower_Flag_Mask[3]);
  or or_1 (Clear, Invalidate_All, Reset);
  and and_5 (and_5_out, Data_Translate, Bit27_Data_Address[0], Bit27_Data_Address[1], Bit27_Data_Address[2], Bit27_Data_Address[3], Bit27_Data_Address[4], Bit27_Data_Address[5], Bit27_Data_Address[6], Bit27_Data_Address[7], Bit27_Data_Address[8], Bit27_Data_Address[9], Bit27_Data_Address[10], Bit27_Data_Address[11]);
  and and_6 (and_6_out, Bit27_Data_Address[0], Bit27_Data_Address[1], Bit27_Data_Address[3], Bit27_Data_Address[2]);
  or or_2 (or_2_out, and_5_out, and_6_out);
  Multiplexer #(.width(3)) multiplexer_1 (
    .in0(D_Cont_Trans_PGTB_Index), .in1(Bit27_Instruction_Address[25:23]),
    .out(Translation_Page_Table_Address), .sel(I_Miss));
  and and_7 (Two_Byte_Operation_t, Two_Byte_Operation, ~or_2_out);  // AND_Gate
  and and_8 (and_8_out, or_2_out, Two_Byte_Operation, D_TLB_Hit, d_ff_2_qn);
  and and_9 (D_Page_Offset[0], Bit27_Data_Address[0], d_ff_1_qn);
  and and_10 (D_Page_Offset[1], Bit27_Data_Address[1], d_ff_1_qn);
  and and_11 (D_Page_Offset[2], Bit27_Data_Address[2], d_ff_1_qn);
  and and_12 (D_Page_Offset[3], Bit27_Data_Address[3], d_ff_1_qn);
  and and_13 (D_Page_Offset[4], Bit27_Data_Address[4], d_ff_1_qn);
  and and_14 (D_Page_Offset[5], Bit27_Data_Address[5], d_ff_1_qn);
  and and_15 (D_Page_Offset[6], Bit27_Data_Address[6], d_ff_1_qn);
  and and_16 (D_Page_Offset[7], Bit27_Data_Address[7], d_ff_1_qn);
  and and_17 (D_Page_Offset[8], Bit27_Data_Address[8], d_ff_1_qn);
  and and_18 (D_Page_Offset[9], Bit27_Data_Address[9], d_ff_1_qn);
  and and_19 (D_Page_Offset[10], Bit27_Data_Address[10], d_ff_1_qn);
  and and_20 (D_Page_Offset[11], Bit27_Data_Address[11], d_ff_1_qn);
  Multiplexer #(.width(11)) multiplexer_2 (
    .in0(D_Trans_Page_Index), .in1(Bit27_Instruction_Address[22:12]), .out(Translation_Page_Address),
    .sel(I_Miss));
  D_Flip_Flop d_ff_1 (.D(and_8_out), .clk(Clock), .Q(d_ff_1_q), .Qn(d_ff_1_qn), .reset(Reset));  // open: preset
  D_Flip_Flop #(.trigger("falling")) d_ff_2 (
    .D(d_ff_1_q), .clk(Clock), .Qn(d_ff_2_qn), .reset(Reset));  // open: Q, preset
  Multiplexer #(.width(14)) multiplexer_3 (
    .in0(Bit27_Instruction_Address[25:12]), .in1(Bit14_Target_Page), .out(multiplexer_3_out), .sel(and_21_out));
  Multiplexer #(.width(14)) multiplexer_4 (
    .in0({D_Cont_Trans_PGTB_Index, D_Trans_Page_Index}), .in1(Bit14_Target_Page), .out(multiplexer_4_out),
    .sel(and_21_out));
  D_Flip_Flop #(.trigger("falling")) d_ff_3 (
    .D(or_3_out), .clk(Clock), .Q(Bit4_Faults[2]), .reset(or_4_out));  // open: Qn, preset
  or or_3 (or_3_out, adder_1_cout, Bit4_Faults[2]);
  Adder #(.width(14)) adder_1 (
    .a({14{1'b0}}), .b(Bit27_Data_Address[25:12]), .out({D_Cont_Trans_PGTB_Index, D_Trans_Page_Index}),
    .cin(d_ff_1_q), .cout(adder_1_cout));
  or or_4 (or_4_out, Reset, Lower_Two_Byte_Out_Of_Page_Space);
  and and_21 (and_21_out, ~Miss, Invalidate_Target_Page);  // AND_Gate
  assign bit_extender_1_out = {{2{1'b0}}, multiplexer_3_out};  // Bit_Extender bit_extender_1
  and and_22 (and_22_out, I_Miss, Translation_Page_Hit);
  assign bit_extender_2_out = {{2{1'b0}}, multiplexer_4_out};  // Bit_Extender bit_extender_2
  and and_23 (and_23_out, D_Miss, Translation_Page_Hit);
  and and_24 (and_24_out[1], Invalidate_Translation_Page, ~Miss);  // AND_Gate
  and and_25 (and_25_out, Translation_Page_Hit, Miss);
  Pull_Resistor pull_resistor_1 (.node(pull_resistor_1_node));
  Bit_Extender #(.in_width(16), .out_width(15), .\type ("zero")) bit_extender_3 (
    .in(Bit16_From_Data_Cache), .out(bit_extender_3_out));
  D_Flip_Flop d_ff_4 (.D(Miss), .clk(Clock), .Q(d_ff_4_q), .reset(or_8_out));  // open: Qn, preset
  and and_26 (and_26_out, and_25_out, Bit16_From_Data_Cache[15]);
  Multiplexer #(.select(2), .width(3)) multiplexer_5 (
    .in0(D_Cont_Trans_PGTB_Index), .in1(Bit27_Instruction_Address[25:23]),
    .in2(Bit3_Target_Translation_Page), .in3(pull_resistor_1_node), .out(multiplexer_5_out),
    .sel({and_24_out[1], I_Miss}));
  D_Flip_Flop #(.trigger("falling")) d_ff_5 (
    .D(or_5_out), .clk(Clock), .Q(Bit4_Faults[1]), .reset(or_6_out));  // open: Qn, preset
  or or_5 (or_5_out, and_26_out, Bit4_Faults[1]);
  and and_27 (and_27_out, Bit16_From_Data_Cache[15], d_ff_4_q, not_2_out);
  or or_6 (or_6_out, Reset, Lower_Virtual_Page_Not_Allocated);
  Translation_Lookaside_Buffer translation_lookaside_buffer_1 (
    .Bit16_Key_Data(bit_extender_1_out), .Bit16_Value_Data(Bit16_From_Data_Cache),
    .Bit16_Search_Key(bit_extender_1_out), .Search_Enable(Instruction_Translate), .Set_Cell(and_22_out),
    .Reset_Cell(and_21_out), .Bit3_Cell_Index(translation_lookaside_buffer_1_bit3_least_recently_used_cell),
    .Clock(Clock), .Enable(Enable), .Reset_Buffer(Clear),
    .Bit3_Least_Recently_Used_Cell(translation_lookaside_buffer_1_bit3_least_recently_used_cell),
    .Key_In_Cache(I_TLB_Hit), .Bit16_Value(I_TLB_Result), .Cache_Miss(I_TLB_Miss));
  Translation_Lookaside_Buffer translation_lookaside_buffer_2 (
    .Bit16_Key_Data(bit_extender_2_out), .Bit16_Value_Data(Bit16_From_Data_Cache),
    .Bit16_Search_Key(bit_extender_2_out), .Search_Enable(Data_Translate), .Set_Cell(and_23_out),
    .Reset_Cell(and_21_out), .Bit3_Cell_Index(translation_lookaside_buffer_2_bit3_least_recently_used_cell),
    .Clock(Clock), .Enable(Enable), .Reset_Buffer(Clear),
    .Bit3_Least_Recently_Used_Cell(translation_lookaside_buffer_2_bit3_least_recently_used_cell),
    .Key_In_Cache(D_TLB_Hit), .Bit16_Value(D_TLB_Result), .Cache_Miss(D_TLB_Miss));
  and and_28 (Translation_Page_Rewrite_Miss, not_2_out, Miss);
  D_Flip_Flop #(.trigger("falling")) d_ff_6 (
    .D(or_7_out), .clk(Clock), .Q(Bit4_Faults[0]), .reset(or_9_out));  // open: Qn, preset
  or or_7 (or_7_out, Bit4_Faults[0], and_27_out);
  not not_1 (not_1_out, Miss);
  or or_8 (or_8_out, not_1_out, Clear);
  not not_2 (not_2_out, Translation_Page_Hit);
  or or_9 (or_9_out, Reset, Lower_Translation_Page_Not_Allocated);
  Pull_Resistor pull_resistor_2 (.node(pull_resistor_2_node));
  Bit15x8Cache bit15x8cache_1 (
    .Bit3_Query(multiplexer_5_out), .Bit15_Write_Value(bit_extender_3_out),
    .Write_Enable(Translation_Page_Rewrite_Miss), .Reset_Enable(and_24_out[1]), .Clock(Clock), .Query(Miss),
    .Clear(Clear), .Bit15_Result(pull_resistor_2_node), .Value_Cached(Translation_Page_Hit));
  Bit_Extender #(.in_width(15), .out_width(14), .\type ("zero")) bit_extender_4 (
    .in(pull_resistor_2_node), .out(Translation_Page));
  and and_29 (and_29_out, D_Resolving_qn, I_TLB_Miss);
  D_Flip_Flop #(.trigger("falling")) d_ff_7 (
    .D(or_10_out), .clk(Clock), .Q(Bit4_Faults[3]), .reset(or_11_out));  // open: Qn, preset
  or or_10 (or_10_out, and_30_out, Bit4_Faults[3]);
  D_Flip_Flop I_Resolving (
    .D(and_29_out), .clk(Clock), .Q(I_Resolving_q), .Qn(I_Resolving_qn), .reset(Reset));  // open: preset
  or or_11 (or_11_out, Reset, Lower_Write_Protection_Violation);
  or or_12 (Stall, Invalidate_Target_Page, I_Miss, D_Miss);
  or or_13 (I_Miss, and_29_out, I_Resolving_q);
  and and_30 (and_30_out, Data_Translate, pull_resistor_2_node[14], Translation_Page_Hit, Data_Direction);
  or or_14 (Miss, I_Miss, D_Miss);
  and and_31 (and_31_out, D_TLB_Miss, ~and_29_out, I_Resolving_qn);  // AND_Gate
  or or_15 (D_Miss, and_31_out, D_Resolving_q);
  D_Flip_Flop D_Resolving (
    .D(and_31_out), .clk(Clock), .Q(D_Resolving_q), .Qn(D_Resolving_qn), .reset(Reset));  // open: preset
  and and_32 (and_32_out, Translation_Page_Hit, D_TLB_Miss);
  // Priority_Encoder #(.select(2)) priority_encoder_1: pin names not known; wires that end beside it: Translation_Page_Rewrite_Miss, and_32_out, priority_encoder_1_p3, D_TLB_Hit, Data_Passthrough
  or or_16 (or_16_out, Data_Passthrough, Data_Translate);
  nor nor_1 (nor_1_out, Translation_Page_Rewrite_Miss, and_32_out);
  and and_33 (and_33_out, nor_1_out, Two_Byte_Operation_t);
  or or_17 (or_17_out, Translation_Page_Rewrite_Miss, and_32_out);
  and and_34 (and_34_out, nor_1_out, ~Data_Direction, or_16_out);  // AND_Gate
  and and_35 (Data_Write, nor_1_out, Data_Direction, or_16_out);
  Multiplexer #(.width(26)) multiplexer_6 (
    .in0(Bit27_Instruction_Address), .in1(Translated_Instruction_Address),
    .out(Bit26_Instruction_Address_Out), .sel(I_TLB_Hit));
  or or_18 (Instruction_Read, I_TLB_Hit, Instruction_Passthrough);
  Multiplexer #(.select(2), .width(26)) multiplexer_7 (
    .in0({{14{1'b0}}, Bit8_Context_Id, Translation_Page_Table_Address, 1'b0}),
    .in1({Translation_Page, Translation_Page_Address, 1'b0}), .in2(Data_Instruction_Address),
    .in3(Bit27_Data_Address), .out(Bit26_Data_Address_Out), .sel(priority_encoder_1_p3));
  or or_19 (Data_Two_Byte, and_33_out, or_17_out);
  or or_20 (Is_Fault, Bit4_Faults[0], Bit4_Faults[1], Bit4_Faults[2]);
  or or_21 (Data_Read, or_17_out, and_34_out);

  // Other names for the same wires on the sheet: Data_Address_In[25:0] = Bit27_Data_Address;
  //   U_D_Virtual_Page[13:0] = Bit27_Data_Address[25:12]; Translation_Page_Not_Allocated_Fault = Bit4_Faults[0];
  //   Virtual_Page_Not_Allocated_Fault = Bit4_Faults[1]; Two_Byte_Out_Of_Page_Space_Fault = Bit4_Faults[2];
  //   Write_Protection_Violation = Bit4_Faults[3];
  //   D_Virtual_Page[13:0] = {D_Cont_Trans_PGTB_Index, D_Trans_Page_Index};
  //   D_Trans_Page_Table_Address[10:0] = {Bit8_Context_Id, D_Cont_Trans_PGTB_Index};
  //   Data_Two_Byte_Operation = Two_Byte_Operation; I_Page_Offset[11:0] = Bit27_Instruction_Address[11:0];
  //   Instruction_Address_In[25:0] = Bit27_Instruction_Address;
  //   I_Trans_Page_Index[10:0] = Bit27_Instruction_Address[22:12];
  //   I_Virtual_Page[13:0] = Bit27_Instruction_Address[25:12];
  //   I_Cont_Trans_PGTB_Index[2:0] = Bit27_Instruction_Address[25:23];
  //   I_Trans_Page_Table_Address[10:0] = {Bit8_Context_Id, Bit27_Instruction_Address[25:23]};
  //   Invalidate = Invalidate_All; Lower_Flag_Mask[3:0] = Bit4_Lower_Flag_Mask;
  //   Memory_Data_In[15:0] = Bit16_From_Data_Cache; Target_Page[13:0] = Bit14_Target_Page;
  //   Target_Translation_Page[2:0] = Bit3_Target_Translation_Page; Translation_Page_Address[25:12] = Translation_Page;
  //   Context_Id[7:0] = Bit8_Context_Id; Translation_Page_Table_Address[11:4] = Bit8_Context_Id;
  //   U_D_Page_Offset[11:0] = Bit27_Data_Address[11:0]

  // Notes on the sheet:
  //   0 = read, 1 = write
  //   memory addressing (26 bits, not the extended io inclusive part)
  //   0bPWII IIII IIII IIII OOOO OOOO OOOO
  //   P = present ( 1 = present)
  //   w = write protected (1 = protected)
  //   I = page index
  //   O = page offset
  //   should add similar circuitery to deal with
  //   the 2 byte over 2 cache line
  //   HERE IS MY ATTEMPT IDK IF IT WORKS SO PLS THINK ABT IT TMRW
  //   since D cache cannot handle that
  //   and I cache is only 2 byte aligned
  //   0b00XX XXXX XXXX XXXX
  //   so thus validity is ensured
  //   for act last,
  //   the reset on these buffers sets to:
  //   0b1000 0000 0000 0000
  //   but any translation page is
  //   via these 0 extenders...
  //   where two page last
  //   with two page again,
  //   where HIT immediately
  //   FAAAUULTTTT
  //   OUT OF PAGE SPACE
  //   If I and D, I
  //   if I already, NOT D
  //   if D already, NOT I
endmodule

module Bit4_2_Mux (
  input  [3:0] Bit4_A,
  input  [3:0] Bit4_B,
  input  Sel,
  output [3:0] Bit4_Result
);

  wire and_1_out, and_2_out, and_3_out, and_4_out, and_5_out, and_6_out, and_7_out, and_8_out, not_1_out;

  and and_1 (and_1_out, not_1_out, Bit4_A[0]);
  and and_2 (and_2_out, not_1_out, Bit4_A[1]);
  and and_3 (and_3_out, not_1_out, Bit4_A[2]);
  and and_4 (and_4_out, not_1_out, Bit4_A[3]);
  not not_1 (not_1_out, Sel);
  and and_5 (and_5_out, Sel, Bit4_B[0]);
  and and_6 (and_6_out, Sel, Bit4_B[1]);
  and and_7 (and_7_out, Sel, Bit4_B[2]);
  and and_8 (and_8_out, Sel, Bit4_B[3]);
  or or_1 (Bit4_Result[3], and_8_out, and_4_out);
  or or_2 (Bit4_Result[2], and_7_out, and_3_out);
  or or_3 (Bit4_Result[1], and_6_out, and_2_out);
  or or_4 (Bit4_Result[0], and_5_out, and_1_out);
endmodule

module Bit4_3_Mux (
  input  [3:0] Bit4_A,
  input  [3:0] Bit4_B,
  input  [3:0] Bit4_C,
  input  [1:0] Sel,
  output [3:0] Bit4_Result
);

  wire and_1_out, and_2_out, and_3_out, and_4_out, and_5_out, and_6_out, and_7_out, and_8_out, and_9_out,
       and_10_out, and_11_out, and_12_out, and_13_out, and_14_out, not_1_out;

  not not_1 (not_1_out, Sel[1]);
  and and_1 (and_1_out, and_5_out, Bit4_A[0]);
  and and_2 (and_2_out, and_5_out, Bit4_A[1]);
  and and_3 (and_3_out, and_5_out, Bit4_A[2]);
  and and_4 (and_4_out, and_5_out, Bit4_A[3]);
  and and_5 (and_5_out, Sel[0], not_1_out);
  and and_6 (and_6_out, and_10_out, Bit4_B[0]);
  and and_7 (and_7_out, and_10_out, Bit4_B[1]);
  and and_8 (and_8_out, and_10_out, Bit4_B[2]);
  and and_9 (and_9_out, and_10_out, Bit4_B[3]);
  and and_10 (and_10_out, Sel[0], not_1_out);
  and and_11 (and_11_out, Bit4_C[0], Sel[1]);
  and and_12 (and_12_out, Bit4_C[1], Sel[1]);
  and and_13 (and_13_out, Bit4_C[2], Sel[1]);
  and and_14 (and_14_out, Bit4_C[3], Sel[1]);
  or or_1 (Bit4_Result[3], and_9_out, and_14_out, and_4_out);
  or or_2 (Bit4_Result[2], and_8_out, and_13_out, and_3_out);
  or or_3 (Bit4_Result[1], and_7_out, and_12_out, and_2_out);
  or or_4 (Bit4_Result[0], and_6_out, and_11_out, and_1_out);
endmodule

module Bit4_Equal (
  input  [3:0] Bit4_B,
  input  [3:0] Bit4_A,
  output Equal
);

  wire xor_1_out, xor_2_out, xor_3_out, xor_4_out;

  xor xor_1 (xor_1_out, Bit4_B[0], Bit4_A[0]);
  xor xor_2 (xor_2_out, Bit4_B[1], Bit4_A[1]);
  xor xor_3 (xor_3_out, Bit4_B[2], Bit4_A[2]);
  xor xor_4 (xor_4_out, Bit4_B[3], Bit4_A[3]);
  nor nor_1 (Equal, xor_1_out, xor_2_out, xor_3_out, xor_4_out);
endmodule

module core2 (
);

  wire and_1_out, and_2_out, and_15_out, and_16_out, and_17_out, and_18_out, and_19_out, and_20_out,
       and_21_out, and_22_out, and_23_out, and_24_out, and_25_out, bit2_equal_1_equal, bit2_equal_2_equal,
       bit2_equal_3_equal, bit2_equal_4_equal, bit3_equal_1_equal, bit3_equal_2_equal, bit3_equal_3_equal,
       bit3_equal_4_equal, bit3_latching_arbiter_1_ga, bit3_latching_arbiter_1_gb, bit4_equal_1_equal,
       bit4_equal_2_equal, bit4_equal_3_equal, bit4_equal_4_equal, bit4_equal_5_equal, bit4_equal_6_equal,
       controlled_buffer_1_out, controlled_buffer_3_out, controlled_buffer_5_out, d_ff_1_q,
       data_cache_2_way_1_ram_read, data_cache_2_way_1_ram_write, data_cache_2_way_1_rwds, DCache_Stall,
       DEC_Read_A_Enable, DEC_Read_B_Enable, DEC_Write_Enable, decoder_1_out0, decoder_1_out1,
       decoder_1_out2, decoder_1_out3, decoder_1_out4, decoder_2_out0, decoder_2_out1, decoder_2_out2,
       decoder_2_out3, decoder_3_out0, decoder_3_out1, decoder_3_out2, decoder_3_out3, decoder_3_out4,
       EXE_Bit16_Reg_Write_Enable_q, Exe_Enable, Fetch_Unit_Absolute_Jump, Fetch_Unit_Stepping,
       Fetch_Unit_Subtract, Fetch_Unit_Target, Forward_EXE_32, Forward_EXE_A, Forward_EXE_B,
       Forward_EXE_Special, Forward_MEM_32, Forward_MEM_A, Forward_MEM_B, Forward_MEM_Special, Forward_WB_32,
       Forward_WB_A, Forward_WB_B, Forward_WB_Special, ICache_Stall, instruction_cache_2_way_1_ram_read,
       instruction_cache_2_way_1_rwds, MEM_Bit16_Reg_Write_Enable_q, Mem_Enable, memory_clock_1_cpu_clock,
       mmu3_1_p18, mmu3_1_p21, mmu3_1_p23, mmu3_1_p24, mmu3_1_p25, MMU_Stall, nor_3_out, nor_4_out,
       not_2_out, not_3_out, not_4_out, or_1_out, or_2_out, or_4_out, or_5_out, or_6_out, or_7_out, or_8_out,
       or_9_out, or_10_out, or_11_out, or_12_out, or_13_out, psram_controller_2_1_data_moving, Read_A_Enable,
       Read_B_Enable, READ_Bit16_Reg_Write_Enable_q, Read_Enable, READ_Write_32_Registers_Enable_q,
       READ_Write_Special_Registers_Enable_q, Reg_16_Write_Enable, register_3_q, register_5_q, register_7_q,
       register_9_q, undriven, undriven_2, undriven_3, undriven_4, undriven_5, undriven_7, undriven_9,
       undriven_10, undriven_11, undriven_12, undriven_13, undriven_14, undriven_15, undriven_16,
       undriven_17, undriven_18, undriven_19, undriven_20, undriven_21, undriven_22, Write_32_Registers,
       Write_Special_Registers;
  wire [1:0] Bit2_Write_32_Registers, bit_extender_5_out, bit_extender_9_out, multiplexer_6_out,
       Privillege_Register_q, READ_Write_32_Registers_q, register_4_q, register_8_q, register_19_q,
       register_21_q, register_28_q, undriven_6, Virtual_Mode_q;
  wire [2:0] Bit3_Read_Special_Registers, Bit3_Write_Special_Registers, EXE_BIT3_MMU_Flag_Mask_q,
       MMU_Flag_Mask, priority_encoder_1_out, priority_encoder_2_out, priority_encoder_3_out,
       READ_BIT3_MMU_Flag_Mask_q, READ_Write_Special_Registers_q, register_2_q, register_6_q;
  wire [3:0] alu4_1_p5, ALU_Operation, bit_extender_1_out, bit_extender_2_out, bit_extender_3_out,
       bit_extender_4_out, bit_extender_19_out, bit_extender_23_out, Condition, DEC_ALU_Operation,
       DEC_Condition, DEC_Reg16_Read_A_Select, DEC_Reg16_Read_B_Select, EXE_Bit16_Reg_Write_Line_q,
       MEM_Bit16_Reg_Write_Line_q, MEM_XXX_q, multiplexer_1_out, multiplexer_2_out, multiplexer_3_out,
       multiplexer_11_out, READ_Bit4_ALU_Operation_q, READ_Bit4_Condition_q, READ_Bit16_Reg_Write_Line_q,
       Reg_16_Write_Line, register_22_q;
  wire [4:0] ALU_Config, DEC_ALU_Config, READ_Bit5_ALU_Config_q;
  wire [5:0] Opcode;
  wire [7:0] bit_extender_7_out, bit_extender_8_out, Context_Register_q, controlled_buffer_6_out,
       data_cache_2_way_1_memory_byte, Memory_Region_Register_q, psram_controller_2_1_bit8_out,
       register_18_q, register_20_q, register_25_q;
  wire [9:0] Bit16_Instruction, Memory_Stage_Control_out, Writeback_Stage_Control_out;
  wire [9:3] Read_Stage_Control_out;
  wire [9:9] Execute_Stage_Control_out;
  wire [10:0] bit_extender_6_out, MemoryOffset_q;
  wire [11:0] Read_Config;
  wire [13:6] undriven_8;
  wire [14:0] bit_extender_22_out, EXE_BIT15_MEM_Config_q, Memory_Config, READ_BIT15_MEM_Config_q;
  wire [15:0] alu4_1_p4, bit_extender_11_out, bit_extender_12_out, bit_extender_13_out, bit_extender_14_out,
       bit_extender_15_out, bit_extender_20_out, ICache_Result, mmu3_1_p9, multiplexer_8_out,
       multiplexer_9_out, multiplexer_12_out, multiplexer_14_out, register_16_q, register_17_q,
       register_24_q, register_30_q, register_file_1_readline_a, register_file_1_readline_b;
  wire [25:0] adder_1_out, adder_3_out, Bit26_To_Fetch_Unit, bit_extender_16_out, bit_extender_18_out,
       controlled_inverter_1_out, controlled_inverter_3_out, multiplexer_13_out;
  wire [26:0] bit_extender_21_out, controlled_buffer_7_out, mmu3_1_p20, mmu3_1_p22;
  wire [26:1] Next_Instruction_Address;
  wire [31:0] adder_2_out, Bit32_Architectural_Instruction_Pointer, Bit32_Register_q, bit_extender_10_out,
       bit_extender_17_out, controlled_inverter_2_out, demultiplexer_1_out1, framepointer_q,
       multiplexer_5_out, multiplexer_7_out, register_15_q, register_23_q, register_29_q, stackpointer_q;

  PLA #(.in_width(6), .out_width(10), .\table ("000000 0000000000 # ad\n000001 0000000000 # adc\n000010 0000000001 # adi\n000011 0000000010 # adli\n000100 0000000000 # sub\n000101 0000000000 # sbc\n000110 0000000001 # sbi\n000111 0000000010 # sbli\n001000 0000000000 # mull\n001001 0000000000 # mulh\n001010 0000000000 # and\n001011 0000000000 # andi\n001100 0000000000 # or\n001101 0000000000 # ori")) Execute_Stage_Control (
    .in(Opcode), .out({Execute_Stage_Control_out[9], DEC_ALU_Operation, DEC_ALU_Config}));
  PLA #(.in_width(6), .out_width(10), .\table ("000000 0000000000 # ad\n000001 0000000000 # adc\n000010 0000000001 # adi\n000011 0000000010 # adli\n000100 0000000000 # sub\n000101 0000000000 # sbc\n000110 0000000001 # sbi\n000111 0000000010 # sbli\n001000 0000000000 # mull\n001001 0000000000 # mulh\n001010 0000000000 # and\n001011 0000000000 # andi\n001100 0000000000 # or\n001101 0000000000 # ori")) Memory_Stage_Control (
    .in(Opcode), .out(Memory_Stage_Control_out));
  PLA #(.in_width(6), .out_width(10), .\table ("000000 0000000000 # ad\n000001 0000000000 # adc\n000010 0000000001 # adi\n000011 0000000010 # adli\n000100 0000000000 # sub\n000101 0000000000 # sbc\n000110 0000000001 # sbi\n000111 0000000010 # sbli\n001000 0000000000 # mull\n001001 0000000000 # mulh\n001010 0000000000 # and\n001011 0000000000 # andi\n001100 0000000000 # or\n001101 0000000000 # ori")) Read_Stage_Control (
    .in(Opcode), .out({Read_Stage_Control_out, DEC_Write_Enable, DEC_Read_B_Enable, DEC_Read_A_Enable}));
  PLA #(.in_width(6), .out_width(10), .\table ("000000 0000000000 # ad\n000001 0000000000 # adc\n000010 0000000001 # adi\n000011 0000000010 # adli\n000100 0000000000 # sub\n000101 0000000000 # sbc\n000110 0000000001 # sbi\n000111 0000000010 # sbli\n001000 0000000000 # mull\n001001 0000000000 # mulh\n001010 0000000000 # and\n001011 0000000000 # andi\n001100 0000000000 # or\n001101 0000000000 # ori")) Writeback_Stage_Control (
    .in(Opcode), .out(Writeback_Stage_Control_out));
  PLA #(.in_width(6), .out_width(3), .\table ("000000 000 # ad\n000001 000 # adc\n000010 001 # adi\n000011 010 # adli\n000100 000 # sub\n000101 000 # sbc\n000110 001 # sbi\n000111 010 # sbli\n001000 000 # mull\n001001 000 # mulh\n001010 000 # and\n001011 000 # andi\n001100 000 # or\n001101 000 # ori")) Format (.in(Opcode));  // open: out
  assign bit_extender_1_out = {{1{1'b0}}, Bit16_Instruction[2:0]};  // Bit_Extender bit_extender_1
  assign bit_extender_2_out = {{1{1'b0}}, Bit16_Instruction[5:3]};  // Bit_Extender bit_extender_2
  Multiplexer #(.select(2), .width(4)) multiplexer_1 (
    .in0(Bit16_Instruction[9:6]), .in1(bit_extender_2_out), .in2(Bit16_Instruction[9:6]),
    .in3(bit_extender_3_out), .out(multiplexer_1_out));  // open: sel
  Bit_Extender #(.in_width(5), .out_width(4), .\type ("zero")) bit_extender_3 (
    .in(Bit16_Instruction[9:5]), .out(bit_extender_3_out));
  Multiplexer #(.select(2), .width(4)) multiplexer_2 (
    .in0(bit_extender_2_out), .in1(bit_extender_1_out), .in2(bit_extender_3_out), .in3(bit_extender_4_out),
    .out(multiplexer_2_out));  // open: sel
  Bit_Extender #(.in_width(5), .out_width(4), .\type ("zero")) bit_extender_4 (
    .in(Bit16_Instruction[4:0]), .out(bit_extender_4_out));
  Multiplexer #(.select(2), .width(4)) multiplexer_3 (
    .in0(bit_extender_1_out), .in1(bit_extender_2_out), .out(multiplexer_3_out));  // open: in2, in3, sel
  Multiplexer #(.select(2), .width(4)) multiplexer_4 (
    .in0(Bit16_Instruction[9:6]), .in1(bit_extender_3_out), .in2(Bit16_Instruction[9:6]), .out(DEC_Condition));  // open: in3, sel
  nor nor_1 (Read_Enable, 1'b0, MMU_Stall, DCache_Stall);
  Register #(.width(4)) READ_Bit16_Reg_Write_Line (
    .D(multiplexer_1_out), .en(Read_Enable), .clk(undriven_4), .Q(READ_Bit16_Reg_Write_Line_q), .clr(1'b0));
  Register #(.width(1)) READ_Bit16_Reg_Write_Enable (
    .en(Read_Enable), .clk(undriven_4), .Q(READ_Bit16_Reg_Write_Enable_q), .clr(1'b0));  // open: D
  Register #(.width(1)) READ_Bit16_Reg_Read_A_Enable (
    .D(DEC_Read_A_Enable), .en(Read_Enable), .clk(undriven_4), .Q(Read_A_Enable), .clr(1'b0));
  Register #(.width(1)) READ_Bit16_Reg_Read_B_Enable (
    .D(DEC_Read_B_Enable), .en(Read_Enable), .clk(undriven_4), .Q(Read_B_Enable), .clr(1'b0));
  Register #(.width(4)) READ_Bit4_ALU_Operation (
    .D(DEC_ALU_Operation), .en(Read_Enable), .clk(undriven_4), .Q(READ_Bit4_ALU_Operation_q), .clr(1'b0));
  Register #(.width(4)) READ_Bit4_Condition (
    .D(DEC_Condition), .en(Read_Enable), .clk(undriven_4), .Q(READ_Bit4_Condition_q), .clr(1'b0));
  Register #(.width(5)) READ_Bit5_ALU_Config (
    .D(DEC_ALU_Config), .en(Read_Enable), .clk(undriven_4), .Q(READ_Bit5_ALU_Config_q), .clr(1'b0));
  Register #(.width(15)) READ_BIT15_MEM_Config (
    .en(Read_Enable), .clk(undriven_4), .Q(READ_BIT15_MEM_Config_q), .clr(1'b0));  // open: D
  Register #(.width(3)) READ_BIT3_MMU_Flag_Mask (
    .en(Read_Enable), .clk(undriven_4), .Q(READ_BIT3_MMU_Flag_Mask_q), .clr(1'b0));  // open: D
  Register #(.width(12)) register_1 (.en(Read_Enable), .clk(undriven_4), .Q(Read_Config), .clr(1'b0));  // open: D
  Register #(.width(3)) READ_Special_Registers (
    .en(Read_Enable), .clk(undriven_4), .Q(Bit3_Read_Special_Registers), .clr(1'b0));  // open: D
  Register #(.width(3)) READ_Write_Special_Registers (
    .en(Read_Enable), .clk(undriven_4), .Q(READ_Write_Special_Registers_q), .clr(1'b0));  // open: D
  Register #(.width(1)) READ_Write_Special_Registers_Enable (
    .en(Read_Enable), .clk(undriven_4), .Q(READ_Write_Special_Registers_Enable_q), .clr(1'b0));  // open: D
  Register #(.width(2)) READ_Write_32_Registers (
    .en(Read_Enable), .clk(undriven_5), .Q(READ_Write_32_Registers_q), .clr(1'b0));  // open: D
  Register #(.width(1)) READ_Write_32_Registers_Enable (
    .en(Read_Enable), .clk(undriven_5), .Q(READ_Write_32_Registers_Enable_q), .clr(1'b0));  // open: D
  Bit3_Equal bit3_equal_1 (
    .Bit3_B(READ_Write_Special_Registers_q), .Bit3_A(Bit3_Read_Special_Registers), .Equal(bit3_equal_1_equal));
  Bit2_Equal bit2_equal_1 (.Bit3_B(READ_Write_32_Registers_q), .Bit3_A(undriven_6), .Equal(bit2_equal_1_equal));
  or or_1 (or_1_out, 1'b0, 1'b0);
  nor nor_2 (Exe_Enable, MMU_Stall, DCache_Stall);
  Register #(.width(4)) EXE_Bit16_Reg_Write_Line (
    .D(READ_Bit16_Reg_Write_Line_q), .en(Exe_Enable), .clk(undriven_4), .Q(EXE_Bit16_Reg_Write_Line_q),
    .clr(or_1_out));
  Register #(.width(1)) EXE_Bit16_Reg_Write_Enable (
    .D(READ_Bit16_Reg_Write_Enable_q), .en(Exe_Enable), .clk(undriven_4), .Q(EXE_Bit16_Reg_Write_Enable_q),
    .clr(or_1_out));
  Register #(.width(4)) EXE_Bit4_ALU_Operation (
    .D(READ_Bit4_ALU_Operation_q), .en(Exe_Enable), .clk(undriven_4), .Q(ALU_Operation), .clr(or_1_out));
  Register #(.width(4)) EXE_Bit4_Condition (
    .D(READ_Bit4_Condition_q), .en(Exe_Enable), .clk(undriven_4), .Q(Condition), .clr(or_1_out));
  Register #(.width(5)) EXE_Bit5_ALU_Config (
    .D(READ_Bit5_ALU_Config_q), .en(Exe_Enable), .clk(undriven_4), .Q(ALU_Config), .clr(or_1_out));
  Register #(.width(15)) EXE_BIT15_MEM_Config (
    .D(READ_BIT15_MEM_Config_q), .en(or_1_out), .clk(undriven_4), .Q(EXE_BIT15_MEM_Config_q), .clr(or_1_out));
  Register #(.width(3)) EXE_BIT3_MMU_Flag_Mask (
    .D(READ_BIT3_MMU_Flag_Mask_q), .en(Exe_Enable), .clk(undriven_4), .Q(EXE_BIT3_MMU_Flag_Mask_q),
    .clr(or_1_out));
  Register #(.width(3)) register_2 (
    .D(READ_Write_Special_Registers_q), .en(Exe_Enable), .clk(undriven_4), .Q(register_2_q), .clr(or_1_out));
  and and_1 (and_1_out, bit3_equal_1_equal, READ_Write_Special_Registers_Enable_q);
  Register #(.width(1)) register_3 (
    .D(READ_Write_Special_Registers_Enable_q), .en(Exe_Enable), .clk(undriven_4), .Q(register_3_q),
    .clr(or_1_out));
  Register #(.width(2)) register_4 (
    .D(READ_Write_32_Registers_q), .en(Exe_Enable), .clk(undriven_5), .Q(register_4_q), .clr(undriven));
  and and_2 (and_2_out, bit2_equal_1_equal, READ_Write_32_Registers_Enable_q);
  Register #(.width(1)) register_5 (
    .D(READ_Write_32_Registers_Enable_q), .en(Exe_Enable), .clk(undriven_5), .Q(register_5_q), .clr(undriven));
  Bit4_Equal bit4_equal_1 (
    .Bit4_B(EXE_Bit16_Reg_Write_Line_q), .Bit4_A(DEC_Reg16_Read_A_Select), .Equal(bit4_equal_1_equal));
  Bit4_Equal bit4_equal_2 (
    .Bit4_B(EXE_Bit16_Reg_Write_Line_q), .Bit4_A(DEC_Reg16_Read_B_Select), .Equal(bit4_equal_2_equal));
  or or_2 (or_2_out, 1'b0, 1'b0, 1'b0);
  not not_1 (Mem_Enable, DCache_Stall);
  and and_3 (Forward_EXE_A, EXE_Bit16_Reg_Write_Enable_q, Read_A_Enable, bit4_equal_1_equal);
  and and_4 (Forward_EXE_B, EXE_Bit16_Reg_Write_Enable_q, Read_B_Enable, bit4_equal_2_equal);
  Bit3_Equal bit3_equal_2 (.Bit3_B(register_2_q), .Bit3_A(Bit3_Read_Special_Registers), .Equal(bit3_equal_2_equal));
  Bit2_Equal bit2_equal_2 (.Bit3_B(register_4_q), .Bit3_A(undriven_6), .Equal(bit2_equal_2_equal));
  Register #(.width(4)) MEM_Bit16_Reg_Write_Line (
    .D(EXE_Bit16_Reg_Write_Line_q), .en(Mem_Enable), .clk(undriven_4), .Q(MEM_Bit16_Reg_Write_Line_q),
    .clr(or_2_out));
  Register #(.width(1)) MEM_Bit16_Reg_Write_Enable (
    .D(EXE_Bit16_Reg_Write_Enable_q), .en(Mem_Enable), .clk(undriven_4), .Q(MEM_Bit16_Reg_Write_Enable_q),
    .clr(or_2_out));
  Register #(.width(4)) MEM_XXX (.D(ALU_Operation), .en(Mem_Enable), .Q(MEM_XXX_q), .clr(or_2_out));  // open: clk
  Register #(.width(15)) MEM_BIT15_MEM_Config (
    .D(EXE_BIT15_MEM_Config_q), .en(Mem_Enable), .clk(undriven_4), .Q(Memory_Config), .clr(or_2_out));
  Register #(.width(3)) MEM_BIT3_MMU_Flag_Mask (
    .D(EXE_BIT3_MMU_Flag_Mask_q), .en(Mem_Enable), .clk(undriven_4), .Q(MMU_Flag_Mask), .clr(or_2_out));
  Register #(.width(3)) register_6 (
    .D(register_2_q), .en(Mem_Enable), .clk(undriven_4), .Q(register_6_q), .clr(or_2_out));
  and and_5 (Forward_EXE_Special, bit3_equal_2_equal, register_3_q);
  Register #(.width(1)) register_7 (
    .D(register_3_q), .en(Mem_Enable), .clk(undriven_4), .Q(register_7_q), .clr(or_2_out));
  Register #(.width(2)) register_8 (
    .D(register_4_q), .en(Mem_Enable), .clk(undriven_5), .Q(register_8_q), .clr(undriven_2));
  and and_6 (Forward_EXE_32, bit2_equal_2_equal, register_5_q);
  Register #(.width(1)) register_9 (
    .D(register_5_q), .en(Mem_Enable), .clk(undriven_5), .Q(register_9_q), .clr(undriven_2));
  Bit4_Equal bit4_equal_3 (
    .Bit4_B(MEM_Bit16_Reg_Write_Line_q), .Bit4_A(DEC_Reg16_Read_A_Select), .Equal(bit4_equal_3_equal));
  Bit4_Equal bit4_equal_4 (
    .Bit4_B(MEM_Bit16_Reg_Write_Line_q), .Bit4_A(DEC_Reg16_Read_B_Select), .Equal(bit4_equal_4_equal));
  or or_3 (Forward_MEM_B, 1'b0, 1'b0, 1'b0, 1'b0);
  Register #(.width(4)) WB_Bit16_Reg_Write_Line (
    .D(MEM_Bit16_Reg_Write_Line_q), .en(1'b1), .clk(undriven_4), .Q(Reg_16_Write_Line), .clr(Forward_MEM_B));
  Register #(.width(1)) WB_Bit16_Reg_Write_Enable (
    .D(MEM_Bit16_Reg_Write_Enable_q), .en(1'b1), .clk(undriven_4), .Q(Reg_16_Write_Enable),
    .clr(Forward_MEM_B));
  and and_7 (Forward_MEM_A, MEM_Bit16_Reg_Write_Enable_q, Read_A_Enable, bit4_equal_3_equal);
  and and_8 (Forward_MEM_B, MEM_Bit16_Reg_Write_Enable_q, Read_B_Enable, bit4_equal_4_equal);
  Register #(.width(4)) WB_XXX (.D(MEM_XXX_q), .clr(Forward_MEM_B));  // open: en, clk, Q
  Bit3_Equal bit3_equal_3 (.Bit3_B(register_6_q), .Bit3_A(Bit3_Read_Special_Registers), .Equal(bit3_equal_3_equal));
  Bit2_Equal bit2_equal_3 (.Bit3_B(register_8_q), .Bit3_A(undriven_6), .Equal(bit2_equal_3_equal));
  Register #(.width(3)) register_10 (
    .D(register_6_q), .en(1'b1), .clk(undriven_4), .Q(Bit3_Write_Special_Registers));  // open: clr
  and and_9 (Forward_MEM_Special, bit3_equal_3_equal, register_7_q);
  Register #(.width(1)) register_11 (
    .D(register_7_q), .en(1'b1), .clk(undriven_4), .Q(Write_Special_Registers));  // open: clr
  Register #(.width(2)) register_12 (
    .D(register_8_q), .en(undriven_3), .clk(undriven_5), .Q(Bit2_Write_32_Registers));  // open: clr
  and and_10 (Forward_MEM_32, bit2_equal_3_equal, register_9_q);
  Register #(.width(1)) register_13 (
    .D(register_9_q), .en(undriven_3), .clk(undriven_5), .Q(Write_32_Registers));  // open: clr
  Bit4_Equal bit4_equal_5 (.Bit4_B(Reg_16_Write_Line), .Bit4_A(DEC_Reg16_Read_A_Select), .Equal(bit4_equal_5_equal));
  Bit4_Equal bit4_equal_6 (.Bit4_B(Reg_16_Write_Line), .Bit4_A(DEC_Reg16_Read_B_Select), .Equal(bit4_equal_6_equal));
  Bit3_Equal bit3_equal_4 (
    .Bit3_B(Bit3_Write_Special_Registers), .Bit3_A(Bit3_Read_Special_Registers), .Equal(bit3_equal_4_equal));
  Bit2_Equal bit2_equal_4 (.Bit3_B(Bit2_Write_32_Registers), .Bit3_A(undriven_6), .Equal(bit2_equal_4_equal));
  and and_11 (Forward_WB_A, Reg_16_Write_Enable, Read_A_Enable, bit4_equal_5_equal);
  and and_12 (Forward_WB_B, Reg_16_Write_Enable, Read_B_Enable, bit4_equal_6_equal);
  and and_13 (Forward_WB_Special, bit3_equal_4_equal, Write_Special_Registers);
  and and_14 (Forward_WB_32, bit2_equal_4_equal, Write_32_Registers);
  Decoder #(.select(3)) decoder_1 (
    .out0(decoder_1_out0), .out1(decoder_1_out1), .out2(decoder_1_out2), .out3(decoder_1_out3),
    .out4(decoder_1_out4), .sel(Bit3_Write_Special_Registers), .en(Write_Special_Registers));  // open: out5, out6, out7
  Decoder #(.select(2)) decoder_2 (
    .out0(decoder_2_out0), .out1(decoder_2_out1), .out2(decoder_2_out2), .out3(decoder_2_out3),
    .sel(Bit2_Write_32_Registers), .en(undriven_7));
  Bit_Extender #(.in_width(16), .out_width(2), .\type ("zero")) bit_extender_5 (
    .in(register_30_q), .out(bit_extender_5_out));
  Multiplexer #(.width(32)) multiplexer_5 (
    .in0(register_29_q), .in1(demultiplexer_1_out1), .out(multiplexer_5_out), .sel(undriven_8[12]));
  Bit_Extender #(.in_width(16), .out_width(11), .\type ("zero")) bit_extender_6 (
    .in(register_30_q), .out(bit_extender_6_out));
  Bit_Extender #(.in_width(16), .out_width(8), .\type ("zero")) bit_extender_7 (
    .in(register_30_q), .out(bit_extender_7_out));
  Multiplexer #(.width(2)) multiplexer_6 (
    .in0(bit_extender_5_out), .in1(undriven_8[9:8]), .out(multiplexer_6_out), .sel(undriven_8[6]));
  and and_15 (and_15_out, ~undriven_8[6], decoder_1_out2, nor_4_out);  // AND_Gate
  Bit_Extender #(.in_width(16), .out_width(8), .\type ("zero")) bit_extender_8 (
    .in(register_30_q), .out(bit_extender_8_out));
  Bit_Extender #(.in_width(16), .out_width(2), .\type ("zero")) bit_extender_9 (
    .in(register_30_q), .out(bit_extender_9_out));
  Register #(.width(11)) MemoryOffset (
    .D(bit_extender_6_out), .en(decoder_1_out0), .clk(memory_clock_1_cpu_clock), .Q(MemoryOffset_q),
    .clr(mmu3_1_p18));
  Register #(.width(32)) stackpointer (
    .D(multiplexer_5_out), .en(decoder_2_out3), .clk(memory_clock_1_cpu_clock), .Q(stackpointer_q),
    .clr(mmu3_1_p18));
  Register #(.width(32)) framepointer (
    .D(multiplexer_5_out), .en(decoder_2_out2), .clk(memory_clock_1_cpu_clock), .Q(framepointer_q),
    .clr(mmu3_1_p18));
  Register #(.width(32)) Bit32_Register (
    .D(multiplexer_5_out), .en(decoder_2_out1), .clk(memory_clock_1_cpu_clock), .Q(Bit32_Register_q),
    .clr(mmu3_1_p18));
  Register #(.width(32)) Instruction_Pointer (
    .en(decoder_2_out0), .clk(memory_clock_1_cpu_clock), .Q(Bit32_Architectural_Instruction_Pointer),
    .clr(mmu3_1_p18));  // open: D
  Register Context_Register (
    .D(bit_extender_7_out), .en(and_16_out), .clk(memory_clock_1_cpu_clock), .Q(Context_Register_q),
    .clr(mmu3_1_p18));
  and and_16 (and_16_out, nor_4_out, decoder_1_out1);
  Register #(.width(2)) Privillege_Register (
    .D(multiplexer_6_out), .en(or_4_out), .clk(memory_clock_1_cpu_clock), .Q(Privillege_Register_q),
    .clr(mmu3_1_p18));
  or or_4 (or_4_out, and_15_out, undriven_8[6]);
  Register Memory_Region_Register (
    .D(bit_extender_8_out), .en(and_17_out), .clk(memory_clock_1_cpu_clock), .Q(Memory_Region_Register_q),
    .clr(mmu3_1_p18));
  and and_17 (and_17_out, nor_4_out, decoder_1_out3);
  Register #(.width(2)) Virtual_Mode (
    .D(bit_extender_9_out), .en(and_18_out), .clk(memory_clock_1_cpu_clock), .Q(Virtual_Mode_q),
    .clr(mmu3_1_p18));
  and and_18 (and_18_out, nor_4_out, decoder_1_out4);
  Register_File register_file_1 (
    .Write_Data(register_30_q), .Read_B_Enable(Read_B_Enable), .Read_A_Enable(Read_A_Enable),
    .Write_Address(Reg_16_Write_Line), .Write_Enable(Reg_16_Write_Enable), .Clock(memory_clock_1_cpu_clock),
    .Clear_All_Registers(mmu3_1_p18), .ReadLine_A(register_file_1_readline_a),
    .ReadLine_B(register_file_1_readline_b));  // open: Read_Address_B, Read_Address_A
  assign bit_extender_10_out = {{21{1'b0}}, MemoryOffset_q};  // Bit_Extender bit_extender_10
  assign bit_extender_11_out = {{5{1'b0}}, MemoryOffset_q};  // Bit_Extender bit_extender_11
  not nor_3 (nor_3_out, ICache_Stall);  // NOR_Gate
  nor nor_4 (nor_4_out, Privillege_Register_q[0], Privillege_Register_q[1]);
  Demultiplexer #(.width(16)) demultiplexer_1 (
    .out0(demultiplexer_1_out1[15:0]), .out1(demultiplexer_1_out1[31:16]), .in(register_30_q),
    .sel(undriven_8[13]));
  Counter #(.max('h3ffffff), .width(26)) counter_1 (
    .clr(undriven_10), .load(Fetch_Unit_Target), .up(1'b1), .count(nor_3_out), .clk(undriven_9),
    .D(Bit26_To_Fetch_Unit), .Q(Next_Instruction_Address));  // open: carry
  Decoder #(.select(3)) decoder_3 (
    .out0(decoder_3_out0), .out1(decoder_3_out1), .out2(decoder_3_out2), .out3(decoder_3_out3),
    .out4(decoder_3_out4), .sel(Bit3_Write_Special_Registers), .en(Write_Special_Registers));  // open: out5, out6, out7
  assign bit_extender_12_out = {{8{1'b0}}, Context_Register_q};  // Bit_Extender bit_extender_12
  assign bit_extender_13_out = {{14{1'b0}}, Privillege_Register_q};  // Bit_Extender bit_extender_13
  assign bit_extender_14_out = {{8{1'b0}}, Memory_Region_Register_q};  // Bit_Extender bit_extender_14
  assign bit_extender_15_out = {{14{1'b0}}, Virtual_Mode_q};  // Bit_Extender bit_extender_15
  Register #(.width(16)) register_14 (
    .D(ICache_Result), .en(nor_3_out), .clk(undriven_9), .clr(undriven_10));  // open: Q
  or or_5 (or_5_out, decoder_3_out4, decoder_3_out3);
  or or_6 (or_6_out, decoder_3_out2, decoder_3_out1, decoder_3_out0);
  Priority_Encoder priority_encoder_1 (
    .in0(Read_B_Enable), .in1(decoder_3_out3), .in2(decoder_3_out4), .in4(or_7_out), .in5(or_8_out),
    .in6(or_9_out), .out(priority_encoder_1_out));  // open: in3, in7, en_in, gs, en_out
  Priority_Encoder priority_encoder_2 (
    .in0(Read_A_Enable), .in1(decoder_3_out0), .in2(decoder_3_out1), .in3(decoder_3_out2), .in4(or_10_out),
    .in5(or_11_out), .in6(or_12_out), .out(priority_encoder_2_out));  // open: in7, en_in, gs, en_out
  Priority_Encoder priority_encoder_3 (
    .in0(undriven_15), .in1(undriven_14), .in2(undriven_13), .in3(undriven_12), .in4(undriven_11),
    .in5(undriven_16), .in6(undriven_17), .in7(undriven_18), .out(priority_encoder_3_out));  // open: en_in, gs, en_out
  Multiplexer #(.select(3), .width(32)) multiplexer_7 (
    .in0(bit_extender_10_out), .in1(stackpointer_q), .in2(framepointer_q), .in3(Bit32_Register_q),
    .in4(Bit32_Architectural_Instruction_Pointer), .in5(adder_2_out), .in6(register_23_q),
    .in7(multiplexer_5_out), .out(multiplexer_7_out), .sel(priority_encoder_3_out));
  Multiplexer #(.select(3), .width(16)) multiplexer_8 (
    .in0(register_file_1_readline_a), .in1(bit_extender_11_out), .in2(bit_extender_12_out),
    .in3(bit_extender_13_out), .in4(multiplexer_12_out), .in5(multiplexer_14_out), .in6(register_30_q),
    .out(multiplexer_8_out), .sel(priority_encoder_2_out));  // open: in7
  Multiplexer #(.select(3), .width(16)) multiplexer_9 (
    .in0(register_file_1_readline_b), .in1(bit_extender_14_out), .in2(bit_extender_15_out),
    .in4(multiplexer_12_out), .in5(multiplexer_14_out), .in6(register_30_q), .out(multiplexer_9_out),
    .sel(priority_encoder_1_out));  // open: in3, in7
  Register #(.width(32)) register_15 (
    .D(multiplexer_7_out), .en(undriven_19), .clk(memory_clock_1_cpu_clock), .Q(register_15_q),
    .clr(mmu3_1_p18));
  Register #(.width(16)) register_16 (
    .D(multiplexer_8_out), .en(undriven_19), .clk(memory_clock_1_cpu_clock), .Q(register_16_q),
    .clr(mmu3_1_p18));
  Register #(.width(16)) register_17 (
    .D(multiplexer_9_out), .en(undriven_19), .clk(memory_clock_1_cpu_clock), .Q(register_17_q),
    .clr(mmu3_1_p18));
  and and_19 (and_19_out, or_5_out, Forward_EXE_Special);
  or or_7 (or_7_out, Forward_EXE_A, and_19_out);
  Register register_18 (
    .D(Context_Register_q), .en(undriven_19), .clk(memory_clock_1_cpu_clock), .Q(register_18_q),
    .clr(mmu3_1_p18));
  Register #(.width(2)) register_19 (
    .D(Privillege_Register_q), .en(undriven_19), .clk(memory_clock_1_cpu_clock), .Q(register_19_q),
    .clr(mmu3_1_p18));
  Register register_20 (
    .D(Memory_Region_Register_q), .en(undriven_19), .clk(memory_clock_1_cpu_clock), .Q(register_20_q),
    .clr(mmu3_1_p18));
  Register #(.width(2)) register_21 (
    .D(Virtual_Mode_q), .en(undriven_19), .clk(memory_clock_1_cpu_clock), .Q(register_21_q), .clr(mmu3_1_p18));
  Bit_Extender #(.in_width(32), .out_width(26), .\type ("zero")) bit_extender_16 (
    .in(multiplexer_7_out), .out(bit_extender_16_out));
  and and_20 (and_20_out, or_5_out, Forward_MEM_Special);
  and and_21 (and_21_out, or_5_out, Forward_WB_Special);
  or or_8 (or_8_out, Forward_MEM_A, and_20_out);
  or or_9 (or_9_out, Forward_WB_A, and_21_out);
  assign bit_extender_17_out = {{16{1'b0}}, register_16_q};  // Bit_Extender bit_extender_17
  and and_22 (and_22_out, or_6_out, Forward_EXE_Special);
  and and_23 (and_23_out, or_6_out, Forward_MEM_Special);
  or or_10 (or_10_out, Forward_EXE_B, and_22_out);
  or or_11 (or_11_out, Forward_MEM_B, and_23_out);
  Bit_Extender #(.in_width(32), .out_width(26), .\type ("zero")) bit_extender_18 (
    .in(Bit32_Architectural_Instruction_Pointer), .out(bit_extender_18_out));
  assign controlled_inverter_1_out = Fetch_Unit_Subtract ? ~bit_extender_16_out : 26'bz;  // Controlled_Inverter controlled_inverter_1
  Bit_Extender #(.in_width(16), .out_width(4), .\type ("zero")) bit_extender_19 (
    .in(register_16_q), .out(bit_extender_19_out));
  and and_24 (and_24_out, or_6_out, Forward_WB_Special);
  or or_12 (or_12_out, Forward_WB_B, and_24_out);
  Adder #(.width(26)) adder_1 (
    .a(bit_extender_18_out), .b(controlled_inverter_1_out), .out(adder_1_out), .cin(Fetch_Unit_Subtract));  // open: cout
  assign controlled_inverter_2_out = ALU_Config[0] ? ~bit_extender_17_out : 32'bz;  // Controlled_Inverter controlled_inverter_2
  Multiplexer #(.width(26)) multiplexer_10 (
    .in0(adder_1_out), .in1(bit_extender_16_out), .out(Bit26_To_Fetch_Unit), .sel(Fetch_Unit_Absolute_Jump));
  Adder #(.width(32)) adder_2 (
    .a(register_15_q), .b(controlled_inverter_2_out), .out(adder_2_out), .cin(ALU_Config[0]));  // open: cout
  // ALU4 alu4_1: pin names not known; wires that end beside it: register_16_q, register_17_q, ALU_Operation, alu4_1_p4, alu4_1_p5[0], alu4_1_p5[1], alu4_1_p5[2], alu4_1_p5[3]
  Multiplexer #(.width(4)) multiplexer_11 (
    .in0(alu4_1_p5), .in1(bit_extender_19_out), .out(multiplexer_11_out), .sel(ALU_Config[1]));
  Register #(.width(4)) register_22 (
    .D(multiplexer_11_out), .en(ALU_Config[2]), .clk(memory_clock_1_cpu_clock), .Q(register_22_q),
    .clr(mmu3_1_p18));
  assign bit_extender_20_out = {{12{1'b0}}, register_22_q};  // Bit_Extender bit_extender_20
  Multiplexer #(.select(2), .width(16)) multiplexer_12 (
    .in0(register_16_q), .in1(register_17_q), .in2(alu4_1_p4), .in3(bit_extender_20_out),
    .out(multiplexer_12_out), .sel(ALU_Config[4:3]));
  Register #(.width(32)) register_23 (
    .D(adder_2_out), .en(undriven_20), .clk(memory_clock_1_cpu_clock), .Q(register_23_q), .clr(mmu3_1_p18));
  Register #(.width(16)) register_24 (
    .D(multiplexer_12_out), .en(undriven_20), .clk(memory_clock_1_cpu_clock), .Q(register_24_q),
    .clr(mmu3_1_p18));
  Register register_25 (
    .D(register_18_q), .en(undriven_20), .clk(memory_clock_1_cpu_clock), .Q(register_25_q), .clr(mmu3_1_p18));
  Register #(.width(2)) register_26 (
    .D(register_19_q), .en(undriven_20), .clk(memory_clock_1_cpu_clock), .clr(mmu3_1_p18));  // open: Q
  Register register_27 (
    .D(register_20_q), .en(undriven_20), .clk(memory_clock_1_cpu_clock), .clr(mmu3_1_p18));  // open: Q
  Register #(.width(2)) register_28 (
    .D(register_21_q), .en(undriven_20), .clk(memory_clock_1_cpu_clock), .Q(register_28_q), .clr(mmu3_1_p18));
  or or_13 (or_13_out, Fetch_Unit_Subtract, Fetch_Unit_Stepping);
  assign controlled_inverter_3_out = Fetch_Unit_Subtract ? ~Bit26_To_Fetch_Unit : 26'bz;  // Controlled_Inverter controlled_inverter_3
  Adder #(.width(26)) adder_3 (
    .a(Next_Instruction_Address), .b(controlled_inverter_3_out), .out(adder_3_out), .cin(or_13_out));  // open: cout
  Multiplexer #(.width(26)) multiplexer_13 (
    .in0(adder_3_out), .in1(Bit26_To_Fetch_Unit), .out(multiplexer_13_out), .sel(Fetch_Unit_Absolute_Jump));
  Bit_Extender #(.in_width(32), .out_width(27), .\type ("zero")) bit_extender_21 (
    .in(register_23_q), .out(bit_extender_21_out));
  Bit_Extender #(.in_width(16), .out_width(15), .\type ("zero")) bit_extender_22 (
    .in(register_24_q), .out(bit_extender_22_out));
  Bit_Extender #(.in_width(16), .out_width(4), .\type ("zero")) bit_extender_23 (
    .in(register_24_q), .out(bit_extender_23_out));
  Multiplexer #(.width(16)) multiplexer_14 (
    .in0(register_24_q), .in1(mmu3_1_p9), .out(multiplexer_14_out), .sel(Memory_Config[14]));
  Register #(.width(32)) register_29 (
    .D(register_23_q), .en(undriven_21), .clk(memory_clock_1_cpu_clock), .Q(register_29_q), .clr(mmu3_1_p18));
  Register #(.width(16)) register_30 (
    .D(multiplexer_14_out), .en(undriven_21), .clk(memory_clock_1_cpu_clock), .Q(register_30_q),
    .clr(mmu3_1_p18));
  not not_2 (not_2_out, register_28_q[0]);
  not not_3 (not_3_out, register_28_q[1]);
  D_Flip_Flop #(.trigger("low")) d_ff_1 (
    .D(not_4_out), .clk(memory_clock_1_cpu_clock), .Q(d_ff_1_q), .reset(mmu3_1_p18));  // open: Qn, preset
  and and_25 (and_25_out, d_ff_1_q, memory_clock_1_cpu_clock);
  // MMU3 mmu3_1: pin names not known; wires that end beside it: {Next_Instruction_Address, 1'b0}, register_28_q[0], not_2_out, bit_extender_21_out, register_28_q[1], not_3_out, Memory_Config[8], Memory_Config[9], mmu3_1_p9, register_25_q, Memory_Config[10], MMU_Flag_Mask, Memory_Config[12], bit_extender_22_out, Memory_Config[13], bit_extender_23_out, Memory_Config[11], mmu3_1_p18, and_25_out, mmu3_1_p20, mmu3_1_p21, mmu3_1_p22, mmu3_1_p23, mmu3_1_p24, mmu3_1_p25, MMU_Stall
  not not_4 (not_4_out, DCache_Stall);
  Memory_Clock memory_clock_1 (
    .Clock(undriven_22), .Reset(mmu3_1_p18), .CPU_Clock(memory_clock_1_cpu_clock));  // open: RE_Clock, PSRAM_Clock, FE_Clock
  Instruction_Cache_2_Way instruction_cache_2_way_1 (
    .Read(mmu3_1_p21), .Two_Byte_Operation(mmu3_1_p21), .Invalidate_Address(Memory_Config[0]),
    .Invalidate_Line(Memory_Config[1]), .Set(Memory_Config[2]), .Bit26_Address(mmu3_1_p20[25:0]),
    .Bit8_From_Memory(psram_controller_2_1_bit8_out), .Ram_Data_Moving(psram_controller_2_1_data_moving),
    .Clock(undriven_22), .Reset(mmu3_1_p18), .Bit16_To_Core(ICache_Result),
    .Ram_Read(instruction_cache_2_way_1_ram_read), .Requesting_Ram(ICache_Stall),
    .RWDS(instruction_cache_2_way_1_rwds));
  Data_Cache_2_Way data_cache_2_way_1 (
    .Read(mmu3_1_p23), .Write(mmu3_1_p24), .Two_Byte_Operation(mmu3_1_p25), .Flush_Address(Memory_Config[3]),
    .Invalidate_Address(Memory_Config[4]), .Flush_Line(Memory_Config[5]), .Invalidate_Line(Memory_Config[6]),
    .Set(Memory_Config[7]), .Bit26_Address(mmu3_1_p22[25:0]), .Bit16_Data(register_24_q),
    .Bit8_From_Memory(psram_controller_2_1_bit8_out), .Ram_Data_Moving(psram_controller_2_1_data_moving),
    .Clock(undriven_22), .Reset(mmu3_1_p18), .Bit16_To_Core(mmu3_1_p9),
    .Ram_Write(data_cache_2_way_1_ram_write), .Ram_Read(data_cache_2_way_1_ram_read),
    .Requesting_Ram(DCache_Stall), .Memory_Byte(data_cache_2_way_1_memory_byte),
    .RWDS(data_cache_2_way_1_rwds));
  assign controlled_buffer_1_out = bit3_latching_arbiter_1_gb ? data_cache_2_way_1_ram_read : 1'bz;  // Controlled_Buffer controlled_buffer_1
  assign controlled_buffer_1_out = bit3_latching_arbiter_1_ga ? instruction_cache_2_way_1_ram_read : 1'bz;  // Controlled_Buffer controlled_buffer_2
  assign controlled_buffer_3_out = bit3_latching_arbiter_1_ga ? instruction_cache_2_way_1_rwds : 1'bz;  // Controlled_Buffer controlled_buffer_3
  assign controlled_buffer_3_out = bit3_latching_arbiter_1_gb ? data_cache_2_way_1_rwds : 1'bz;  // Controlled_Buffer controlled_buffer_4
  assign controlled_buffer_5_out = bit3_latching_arbiter_1_gb ? data_cache_2_way_1_ram_write : 1'bz;  // Controlled_Buffer controlled_buffer_5
  assign controlled_buffer_6_out = bit3_latching_arbiter_1_gb ? data_cache_2_way_1_memory_byte : 8'bz;  // Controlled_Buffer controlled_buffer_6
  assign controlled_buffer_7_out = bit3_latching_arbiter_1_ga ? mmu3_1_p20 : 27'bz;  // Controlled_Buffer controlled_buffer_7
  assign controlled_buffer_7_out = bit3_latching_arbiter_1_gb ? mmu3_1_p22 : 27'bz;  // Controlled_Buffer controlled_buffer_8
  Bit3_Latching_Arbiter bit3_latching_arbiter_1 (
    .Reset(mmu3_1_p18), .Clock(undriven_22), .RA(ICache_Stall), .RB(DCache_Stall),
    .GA(bit3_latching_arbiter_1_ga), .GB(bit3_latching_arbiter_1_gb));  // open: RC, GC
  PSRAM_Controller_2 psram_controller_2_1 (
    .Clock(undriven_22), .Reset(mmu3_1_p18), .Read(controlled_buffer_1_out), .Write(controlled_buffer_5_out),
    .Bit8_Data(controlled_buffer_6_out), .Bit26_Address(controlled_buffer_7_out[25:0]),
    .RWDS_In(controlled_buffer_3_out), .RWDS_Out(controlled_buffer_3_out),
    .Bit8_Out(psram_controller_2_1_bit8_out), .Data_Moving(psram_controller_2_1_data_moving));  // open: Setup
  // Pins of 26 and 27 bits meet at mmu3_1_p20
  // Pins of 26 and 27 bits meet at controlled_buffer_7_out
  // Pins of 26 and 27 bits meet at mmu3_1_p22

  // Other names for the same wires on the sheet: Read_Fetch_Config[2:1] = {Fetch_Unit_Absolute_Jump, Fetch_Unit_Subtract};
  //   Stall_Before_Mem = MMU_Stall; Stall_Before_Wb = DCache_Stall

  // Notes on the sheet:
  //   normal
  //   two
  //   immediate
  //   READ
  //   EXECUTE
  //   unsued
  //   unsued
  //   MEMORY
  //   WRITEBACK
  //   15 wb
  //   9 read
  //   points to the NEXT instruction
  //   bit 0 instr, bit 1 data
  //   holds the current instruction the decoder is decoding
  //   fetch unit calculator
  //   ALU
  //   bit9 exe control
  //   AGU
  //   these get set by the read stage,
  //   13mem
endmodule

module ALU4 (
  input  [3:0] Bit4_ALU_Control,
  input  CIN,
  input  [15:0] Bit16_A,
  input  [15:0] Bit16_B,
  output [15:0] result,
  output zero,
  output carry,
  output overflow,
  output negative
);

  wire and_1_out, and_2_out, bit16_add_1_carry_out, bit16_left_shift_1_shift_overflow, decoder_1_out0,
       decoder_1_out1, decoder_1_out2, decoder_2_out0, decoder_2_out1, decoder_2_out2, decoder_2_out3,
       decoder_2_out4, multiplexer_1_out, multiplexer_2_out, not_1_out, or_1_out, or_2_out, xor_1_out,
       xor_2_out, xor_3_out;
  wire [1:0] pla_1_out_2, pla_1_out_4, pla_1_out_5;
  wire [2:0] pla_1_out_3;
  wire [15:0] bit16_add_1_bit16_result, bit16_and_1_bit16_result, bit16_left_shift_1_bit16_result,
       bit16_multiplier_1_lower_word, bit16_multiplier_1_upper_word, bit16_or_1_bit16_result,
       bit16_toggle_xor_1_bit16_result, bit16_toggle_xor_2_bit16_result, bit16_xor_1_bit16_result,
       pull_resistor_1_node;
  wire [19:0] pla_1_out;

  PLA #(.in_width(4), .out_width(20), .\table ("0000 00000000000101110000\n0001 00000000000101110010\n0010 00000011000101110000\n0011 00000010000101110010\n0100 00000000100111100000\n0101 00000000101001000000\n0110 00000000111001011100\n0111 00000000001001011000\n1000 00000000111001011101\n1001 00000000001001011001\n1010 00000000011001000000\n1011 00000000010001000000\n1100 00000000110001000000\n1101 00000010000001000000")) pla_1 (
    .in(Bit4_ALU_Control),
    .out({pla_1_out[19:15], pla_1_out_4, pla_1_out_5, pla_1_out[10], pla_1_out_3, pla_1_out[6], pla_1_out_2, pla_1_out[3:0]}));
  and and_1 (and_1_out, CIN, pla_1_out[0]);
  or or_1 (or_1_out, and_1_out, pla_1_out[1]);
  Bit16_Toggle_Xor bit16_toggle_xor_1 (
    .Bit16_A(Bit16_B), .Toggle(pla_1_out[2]), .Bit16_Result(bit16_toggle_xor_1_bit16_result));
  Bit16_Or bit16_or_1 (.Bit16_A(Bit16_A), .Bit16_B(Bit16_B), .Bit16_Result(bit16_or_1_bit16_result));
  Bit16_And bit16_and_1 (.Bit16_A(Bit16_A), .Bit16_B(Bit16_B), .Bit16_Result(bit16_and_1_bit16_result));
  Bit16_Xor bit16_xor_1 (.Bit16_A(Bit16_B), .Bit16_B(Bit16_A), .Bit16_Result(bit16_xor_1_bit16_result));
  xor xor_1 (xor_1_out, Bit16_A[15], Bit16_B[15]);
  and and_2 (and_2_out, ~xor_1_out, xor_2_out);  // AND_Gate
  xor xor_2 (xor_2_out, Bit16_A[15], result[15]);
  Decoder #(.select(2)) decoder_1 (
    .out0(decoder_1_out0), .out1(decoder_1_out1), .out2(decoder_1_out2), .sel(pla_1_out_2), .en(1'b1));  // open: out3
  Bit16_Add bit16_add_1 (
    .Carry_In(or_1_out), .Bit16_A(Bit16_A), .Bit16_B(bit16_toggle_xor_1_bit16_result),
    .Bit16_Result(bit16_add_1_bit16_result), .Carry_Out(bit16_add_1_carry_out));
  Bit16_Left_Shift bit16_left_shift_1 (
    .Arithmetic_Mode(pla_1_out[19]), .Rotate_Mode(pla_1_out[3]), .Right_Shift_Mode(pla_1_out[18]),
    .Bit4_Shift(Bit16_B[3:0]), .Bit16_Data(Bit16_A), .Bit16_Result(bit16_left_shift_1_bit16_result),
    .Shift_Overflow(bit16_left_shift_1_shift_overflow));
  Pull_Resistor pull_resistor_1 (.node(pull_resistor_1_node));
  assign pull_resistor_1_node = decoder_1_out0 ? bit16_or_1_bit16_result : 16'bz;  // Controlled_Buffer controlled_buffer_1
  assign pull_resistor_1_node = decoder_1_out1 ? bit16_and_1_bit16_result : 16'bz;  // Controlled_Buffer controlled_buffer_2
  Bit16_Multiplier bit16_multiplier_1 (
    .Bit16_B(Bit16_A), .Bit16_A(Bit16_B), .Lower_Word(bit16_multiplier_1_lower_word),
    .Upper_Word(bit16_multiplier_1_upper_word));
  assign pull_resistor_1_node = decoder_1_out2 ? bit16_xor_1_bit16_result : 16'bz;  // Controlled_Buffer controlled_buffer_3
  assign result = decoder_2_out4 ? bit16_add_1_bit16_result : 16'bz;  // Controlled_Buffer controlled_buffer_4
  assign result = decoder_2_out3 ? bit16_left_shift_1_bit16_result : 16'bz;  // Controlled_Buffer controlled_buffer_5
  assign result = decoder_2_out2 ? bit16_toggle_xor_2_bit16_result : 16'bz;  // Controlled_Buffer controlled_buffer_6
  Bit16_Toggle_Xor bit16_toggle_xor_2 (
    .Bit16_A(pull_resistor_1_node), .Toggle(pla_1_out[6]), .Bit16_Result(bit16_toggle_xor_2_bit16_result));
  assign result = decoder_2_out1 ? bit16_multiplier_1_lower_word : 16'bz;  // Controlled_Buffer controlled_buffer_7
  assign result = decoder_2_out0 ? bit16_multiplier_1_upper_word : 16'bz;  // Controlled_Buffer controlled_buffer_8
  Pull_Resistor pull_resistor_2 (.node(result));
  Decoder #(.select(3)) decoder_2 (
    .out0(decoder_2_out0), .out1(decoder_2_out1), .out2(decoder_2_out2), .out3(decoder_2_out3),
    .out4(decoder_2_out4), .sel(pla_1_out_3), .en(pla_1_out[10]));  // open: out5, out6, out7
  nor nor_1 (zero, result[0], result[1], result[2], result[3], result[4], result[5], result[6], result[7], result[9], result[10], result[11], result[12], result[13], result[14], result[15], result[8]);
  and and_3 (negative, result[15], pla_1_out[15]);
  or or_2 (or_2_out, bit16_multiplier_1_upper_word[0], bit16_multiplier_1_upper_word[1], bit16_multiplier_1_upper_word[2], bit16_multiplier_1_upper_word[3], bit16_multiplier_1_upper_word[4], bit16_multiplier_1_upper_word[5], bit16_multiplier_1_upper_word[6], bit16_multiplier_1_upper_word[7], bit16_multiplier_1_upper_word[9], bit16_multiplier_1_upper_word[10], bit16_multiplier_1_upper_word[11], bit16_multiplier_1_upper_word[12], bit16_multiplier_1_upper_word[13], bit16_multiplier_1_upper_word[14], bit16_multiplier_1_upper_word[15], bit16_multiplier_1_upper_word[8]);
  xor xor_3 (xor_3_out, bit16_add_1_bit16_result[15], bit16_add_1_carry_out);
  Multiplexer #(.select(2)) multiplexer_1 (
    .in0(bit16_add_1_carry_out), .in1(xor_3_out), .in2(and_2_out), .in3(or_2_out), .out(multiplexer_1_out),
    .sel(pla_1_out_4));
  and and_4 (overflow, pla_1_out[17], multiplexer_1_out);
  not not_1 (not_1_out, bit16_add_1_carry_out);
  Multiplexer #(.select(2)) multiplexer_2 (
    .in0(bit16_add_1_carry_out), .in1(not_1_out), .in2(bit16_left_shift_1_shift_overflow),
    .out(multiplexer_2_out), .sel(pla_1_out_5));  // open: in3
  and and_5 (carry, pla_1_out[16], multiplexer_2_out);
endmodule

module Bit16_Register_File_2R_2W (
  input  Read_A_Enable,
  input  [3:0] Read_A_Select,
  input  Read_B_Enable,
  input  [3:0] Read_B_Select,
  input  Write_A_Enable,
  input  [3:0] Write_A_Select,
  input  Write_B_Enable,
  input  [3:0] Write_B_Select,
  input  [15:0] Write_Data_A,
  input  [15:0] Write_Data_B,
  input  Clock,
  input  Reset,
  output [15:0] Read_A,
  output [15:0] Read_B
);

  wire decoder_1_out0, decoder_1_out1, decoder_1_out2, decoder_1_out3, decoder_1_out4, decoder_1_out5,
       decoder_1_out6, decoder_1_out7, decoder_1_out8, decoder_1_out9, decoder_1_out10, decoder_1_out11,
       decoder_1_out12, decoder_1_out13, decoder_1_out14, decoder_1_out15, decoder_2_out0, decoder_2_out1,
       decoder_2_out2, decoder_2_out3, decoder_2_out4, decoder_2_out5, decoder_2_out6, decoder_2_out7,
       decoder_2_out8, decoder_2_out9, decoder_2_out10, decoder_2_out11, decoder_2_out12, decoder_2_out13,
       decoder_2_out14, decoder_2_out15, decoder_3_out0, decoder_3_out1, decoder_3_out2, decoder_3_out3,
       decoder_3_out4, decoder_3_out5, decoder_3_out6, decoder_3_out7, decoder_3_out8, decoder_3_out9,
       decoder_3_out10, decoder_3_out11, decoder_3_out12, decoder_3_out13, decoder_3_out14, decoder_3_out15,
       decoder_4_out0, decoder_4_out1, decoder_4_out2, decoder_4_out3, decoder_4_out4, decoder_4_out5,
       decoder_4_out6, decoder_4_out7, decoder_4_out8, decoder_4_out9, decoder_4_out10, decoder_4_out11,
       decoder_4_out12, decoder_4_out13, decoder_4_out14, decoder_4_out15, or_1_out, or_2_out, or_3_out,
       or_4_out, or_5_out, or_6_out, or_7_out, or_8_out, or_9_out, or_10_out, or_11_out, or_12_out,
       or_13_out, or_14_out, or_15_out, or_16_out;
  wire [15:0] multiplexer_1_out, multiplexer_2_out, multiplexer_3_out, multiplexer_4_out, multiplexer_5_out,
       multiplexer_6_out, multiplexer_7_out, multiplexer_8_out, multiplexer_9_out, multiplexer_10_out,
       multiplexer_11_out, multiplexer_12_out, multiplexer_13_out, multiplexer_14_out, multiplexer_15_out,
       multiplexer_16_out, pull_resistor_1_node, register_1_q, register_2_q, register_3_q, register_4_q,
       register_5_q, register_6_q, register_7_q, register_8_q, register_9_q, register_10_q, register_11_q,
       register_12_q, register_13_q, register_14_q, register_15_q;

  Decoder #(.select(4)) decoder_1 (
    .out0(decoder_1_out0), .out1(decoder_1_out1), .out2(decoder_1_out2), .out3(decoder_1_out3),
    .out4(decoder_1_out4), .out5(decoder_1_out5), .out6(decoder_1_out6), .out7(decoder_1_out7),
    .out8(decoder_1_out8), .out9(decoder_1_out9), .out10(decoder_1_out10), .out11(decoder_1_out11),
    .out12(decoder_1_out12), .out13(decoder_1_out13), .out14(decoder_1_out14), .out15(decoder_1_out15),
    .sel(Write_B_Select), .en(Write_B_Enable));
  Decoder #(.select(4)) decoder_2 (
    .out0(decoder_2_out0), .out1(decoder_2_out1), .out2(decoder_2_out2), .out3(decoder_2_out3),
    .out4(decoder_2_out4), .out5(decoder_2_out5), .out6(decoder_2_out6), .out7(decoder_2_out7),
    .out8(decoder_2_out8), .out9(decoder_2_out9), .out10(decoder_2_out10), .out11(decoder_2_out11),
    .out12(decoder_2_out12), .out13(decoder_2_out13), .out14(decoder_2_out14), .out15(decoder_2_out15),
    .sel(Write_A_Select), .en(Write_A_Enable));
  Multiplexer #(.width(16)) multiplexer_1 (
    .in0(Write_Data_B), .in1(Write_Data_A), .out(multiplexer_1_out), .sel(decoder_2_out0));
  or or_1 (or_1_out, decoder_1_out0, decoder_2_out0);
  Multiplexer #(.width(16)) multiplexer_2 (
    .in0(Write_Data_B), .in1(Write_Data_A), .out(multiplexer_2_out), .sel(decoder_2_out1));
  or or_2 (or_2_out, decoder_1_out1, decoder_2_out1);
  Multiplexer #(.width(16)) multiplexer_3 (
    .in0(Write_Data_B), .in1(Write_Data_A), .out(multiplexer_3_out), .sel(decoder_2_out2));
  or or_3 (or_3_out, decoder_1_out2, decoder_2_out2);
  Multiplexer #(.width(16)) multiplexer_4 (
    .in0(Write_Data_B), .in1(Write_Data_A), .out(multiplexer_4_out), .sel(decoder_2_out3));
  or or_4 (or_4_out, decoder_1_out3, decoder_2_out3);
  Multiplexer #(.width(16)) multiplexer_5 (
    .in0(Write_Data_B), .in1(Write_Data_A), .out(multiplexer_5_out), .sel(decoder_2_out4));
  or or_5 (or_5_out, decoder_1_out4, decoder_2_out4);
  Multiplexer #(.width(16)) multiplexer_6 (
    .in0(Write_Data_B), .in1(Write_Data_A), .out(multiplexer_6_out), .sel(decoder_2_out5));
  or or_6 (or_6_out, decoder_1_out5, decoder_2_out5);
  Multiplexer #(.width(16)) multiplexer_7 (
    .in0(Write_Data_B), .in1(Write_Data_A), .out(multiplexer_7_out), .sel(decoder_2_out6));
  or or_7 (or_7_out, decoder_1_out6, decoder_2_out6);
  Multiplexer #(.width(16)) multiplexer_8 (
    .in0(Write_Data_B), .in1(Write_Data_A), .out(multiplexer_8_out), .sel(decoder_2_out7));
  or or_8 (or_8_out, decoder_1_out7, decoder_2_out7);
  Multiplexer #(.width(16)) multiplexer_9 (
    .in0(Write_Data_B), .in1(Write_Data_A), .out(multiplexer_9_out), .sel(decoder_2_out8));
  or or_9 (or_9_out, decoder_1_out8, decoder_2_out8);
  Multiplexer #(.width(16)) multiplexer_10 (
    .in0(Write_Data_B), .in1(Write_Data_A), .out(multiplexer_10_out), .sel(decoder_2_out9));
  or or_10 (or_10_out, decoder_1_out9, decoder_2_out9);
  Multiplexer #(.width(16)) multiplexer_11 (
    .in0(Write_Data_B), .in1(Write_Data_A), .out(multiplexer_11_out), .sel(decoder_2_out10));
  or or_11 (or_11_out, decoder_1_out10, decoder_2_out10);
  Multiplexer #(.width(16)) multiplexer_12 (
    .in0(Write_Data_B), .in1(Write_Data_A), .out(multiplexer_12_out), .sel(decoder_2_out11));
  or or_12 (or_12_out, decoder_1_out11, decoder_2_out11);
  Multiplexer #(.width(16)) multiplexer_13 (
    .in0(Write_Data_B), .in1(Write_Data_A), .out(multiplexer_13_out), .sel(decoder_2_out12));
  or or_13 (or_13_out, decoder_1_out12, decoder_2_out12);
  Multiplexer #(.width(16)) multiplexer_14 (
    .in0(Write_Data_B), .in1(Write_Data_A), .out(multiplexer_14_out), .sel(decoder_2_out13));
  or or_14 (or_14_out, decoder_1_out13, decoder_2_out13);
  Multiplexer #(.width(16)) multiplexer_15 (
    .in0(Write_Data_B), .in1(Write_Data_A), .out(multiplexer_15_out), .sel(decoder_2_out14));
  or or_15 (or_15_out, decoder_1_out14, decoder_2_out14);
  Multiplexer #(.width(16)) multiplexer_16 (
    .in0(Write_Data_B), .in1(Write_Data_A), .out(multiplexer_16_out), .sel(decoder_2_out15));
  or or_16 (or_16_out, decoder_1_out15, decoder_2_out15);
  Register #(.width(16)) register_1 (.D(multiplexer_2_out), .en(or_2_out), .clk(Clock), .Q(register_1_q), .clr(Reset));
  Register #(.width(16)) register_2 (.D(multiplexer_3_out), .en(or_3_out), .clk(Clock), .Q(register_2_q), .clr(Reset));
  Register #(.width(16)) register_3 (.D(multiplexer_4_out), .en(or_4_out), .clk(Clock), .Q(register_3_q), .clr(Reset));
  Register #(.width(16)) register_4 (.D(multiplexer_5_out), .en(or_5_out), .clk(Clock), .Q(register_4_q), .clr(Reset));
  Register #(.width(16)) register_5 (.D(multiplexer_6_out), .en(or_6_out), .clk(Clock), .Q(register_5_q), .clr(Reset));
  Register #(.width(16)) register_6 (.D(multiplexer_7_out), .en(or_7_out), .clk(Clock), .Q(register_6_q), .clr(Reset));
  Register #(.width(16)) register_7 (.D(multiplexer_8_out), .en(or_8_out), .clk(Clock), .Q(register_7_q), .clr(Reset));
  Register #(.width(16)) register_8 (.D(multiplexer_9_out), .en(or_9_out), .clk(Clock), .Q(register_8_q), .clr(Reset));
  Register #(.width(16)) register_9 (
    .D(multiplexer_10_out), .en(or_10_out), .clk(Clock), .Q(register_9_q), .clr(Reset));
  Register #(.width(16)) register_10 (
    .D(multiplexer_11_out), .en(or_11_out), .clk(Clock), .Q(register_10_q), .clr(Reset));
  Register #(.width(16)) register_11 (
    .D(multiplexer_12_out), .en(or_12_out), .clk(Clock), .Q(register_11_q), .clr(Reset));
  Register #(.width(16)) register_12 (
    .D(multiplexer_13_out), .en(or_13_out), .clk(Clock), .Q(register_12_q), .clr(Reset));
  Register #(.width(16)) register_13 (
    .D(multiplexer_14_out), .en(or_14_out), .clk(Clock), .Q(register_13_q), .clr(Reset));
  Register #(.width(16)) register_14 (
    .D(multiplexer_15_out), .en(or_15_out), .clk(Clock), .Q(register_14_q), .clr(Reset));
  Register #(.width(16)) register_15 (
    .D(multiplexer_16_out), .en(or_16_out), .clk(Clock), .Q(register_15_q), .clr(Reset));
  Pull_Resistor pull_resistor_1 (.node(pull_resistor_1_node));
  assign Read_B = decoder_3_out0 ? pull_resistor_1_node : 16'bz;  // Controlled_Buffer controlled_buffer_1
  assign Read_A = decoder_4_out0 ? pull_resistor_1_node : 16'bz;  // Controlled_Buffer controlled_buffer_2
  assign Read_B = decoder_3_out1 ? register_1_q : 16'bz;  // Controlled_Buffer controlled_buffer_3
  assign Read_A = decoder_4_out1 ? register_1_q : 16'bz;  // Controlled_Buffer controlled_buffer_4
  assign Read_B = decoder_3_out2 ? register_2_q : 16'bz;  // Controlled_Buffer controlled_buffer_5
  assign Read_A = decoder_4_out2 ? register_2_q : 16'bz;  // Controlled_Buffer controlled_buffer_6
  assign Read_B = decoder_3_out3 ? register_3_q : 16'bz;  // Controlled_Buffer controlled_buffer_7
  assign Read_A = decoder_4_out3 ? register_3_q : 16'bz;  // Controlled_Buffer controlled_buffer_8
  assign Read_B = decoder_3_out4 ? register_4_q : 16'bz;  // Controlled_Buffer controlled_buffer_9
  assign Read_A = decoder_4_out4 ? register_4_q : 16'bz;  // Controlled_Buffer controlled_buffer_10
  assign Read_B = decoder_3_out5 ? register_5_q : 16'bz;  // Controlled_Buffer controlled_buffer_11
  assign Read_A = decoder_4_out5 ? register_5_q : 16'bz;  // Controlled_Buffer controlled_buffer_12
  assign Read_B = decoder_3_out6 ? register_6_q : 16'bz;  // Controlled_Buffer controlled_buffer_13
  assign Read_A = decoder_4_out6 ? register_6_q : 16'bz;  // Controlled_Buffer controlled_buffer_14
  assign Read_B = decoder_3_out7 ? register_7_q : 16'bz;  // Controlled_Buffer controlled_buffer_15
  assign Read_A = decoder_4_out7 ? register_7_q : 16'bz;  // Controlled_Buffer controlled_buffer_16
  assign Read_B = decoder_3_out8 ? register_8_q : 16'bz;  // Controlled_Buffer controlled_buffer_17
  assign Read_A = decoder_4_out8 ? register_8_q : 16'bz;  // Controlled_Buffer controlled_buffer_18
  assign Read_B = decoder_3_out9 ? register_9_q : 16'bz;  // Controlled_Buffer controlled_buffer_19
  assign Read_A = decoder_4_out9 ? register_9_q : 16'bz;  // Controlled_Buffer controlled_buffer_20
  assign Read_B = decoder_3_out10 ? register_10_q : 16'bz;  // Controlled_Buffer controlled_buffer_21
  assign Read_A = decoder_4_out10 ? register_10_q : 16'bz;  // Controlled_Buffer controlled_buffer_22
  assign Read_B = decoder_3_out11 ? register_11_q : 16'bz;  // Controlled_Buffer controlled_buffer_23
  assign Read_A = decoder_4_out11 ? register_11_q : 16'bz;  // Controlled_Buffer controlled_buffer_24
  assign Read_B = decoder_3_out12 ? register_12_q : 16'bz;  // Controlled_Buffer controlled_buffer_25
  assign Read_A = decoder_4_out12 ? register_12_q : 16'bz;  // Controlled_Buffer controlled_buffer_26
  assign Read_B = decoder_3_out13 ? register_13_q : 16'bz;  // Controlled_Buffer controlled_buffer_27
  assign Read_A = decoder_4_out13 ? register_13_q : 16'bz;  // Controlled_Buffer controlled_buffer_28
  assign Read_B = decoder_3_out14 ? register_14_q : 16'bz;  // Controlled_Buffer controlled_buffer_29
  assign Read_A = decoder_4_out14 ? register_14_q : 16'bz;  // Controlled_Buffer controlled_buffer_30
  assign Read_B = decoder_3_out15 ? register_15_q : 16'bz;  // Controlled_Buffer controlled_buffer_31
  assign Read_A = decoder_4_out15 ? register_15_q : 16'bz;  // Controlled_Buffer controlled_buffer_32
  Decoder #(.select(4)) decoder_3 (
    .out0(decoder_3_out0), .out1(decoder_3_out1), .out2(decoder_3_out2), .out3(decoder_3_out3),
    .out4(decoder_3_out4), .out5(decoder_3_out5), .out6(decoder_3_out6), .out7(decoder_3_out7),
    .out8(decoder_3_out8), .out9(decoder_3_out9), .out10(decoder_3_out10), .out11(decoder_3_out11),
    .out12(decoder_3_out12), .out13(decoder_3_out13), .out14(decoder_3_out14), .out15(decoder_3_out15),
    .sel(Read_B_Select), .en(Read_B_Enable));
  Decoder #(.select(4)) decoder_4 (
    .out0(decoder_4_out0), .out1(decoder_4_out1), .out2(decoder_4_out2), .out3(decoder_4_out3),
    .out4(decoder_4_out4), .out5(decoder_4_out5), .out6(decoder_4_out6), .out7(decoder_4_out7),
    .out8(decoder_4_out8), .out9(decoder_4_out9), .out10(decoder_4_out10), .out11(decoder_4_out11),
    .out12(decoder_4_out12), .out13(decoder_4_out13), .out14(decoder_4_out14), .out15(decoder_4_out15),
    .sel(Read_A_Select), .en(Read_A_Enable));
endmodule

module Bit5_Equal (
  input  [4:0] Bit5_B,
  input  [4:0] Bit5_A,
  output Equal
);

  wire xor_1_out, xor_2_out, xor_3_out, xor_4_out, xor_5_out;

  xor xor_1 (xor_1_out, Bit5_B[0], Bit5_A[0]);
  xor xor_2 (xor_2_out, Bit5_B[1], Bit5_A[1]);
  xor xor_3 (xor_3_out, Bit5_B[2], Bit5_A[2]);
  xor xor_4 (xor_4_out, Bit5_B[3], Bit5_A[3]);
  xor xor_5 (xor_5_out, Bit5_B[4], Bit5_A[4]);
  nor nor_1 (Equal, xor_2_out, xor_3_out, xor_1_out, xor_4_out, xor_5_out);
endmodule

module Bit3_Equal (
  input  [2:0] Bit3_B,
  input  [2:0] Bit3_A,
  output Equal
);

  wire xor_1_out, xor_2_out, xor_3_out;

  xor xor_1 (xor_1_out, Bit3_B[0], Bit3_A[0]);
  xor xor_2 (xor_2_out, Bit3_B[1], Bit3_A[1]);
  xor xor_3 (xor_3_out, Bit3_B[2], Bit3_A[2]);
  nor nor_1 (Equal, xor_1_out, xor_2_out, xor_3_out);
endmodule

module Bit2_Equal (
  input  [1:0] Bit3_B,
  input  [1:0] Bit3_A,
  output Equal
);

  wire xor_1_out, xor_2_out;

  xor xor_1 (xor_1_out, Bit3_B[0], Bit3_A[0]);
  xor xor_2 (xor_2_out, Bit3_B[1], Bit3_A[1]);
  nor nor_1 (Equal, xor_1_out, xor_2_out);
endmodule
module core3 (
  input  SETA_ORB,
  input  ADDRORLINE,
  input  INVALORFLUSH,
  input  IORD,
  input  Interrupt,
  input  RWDS_I,
  input  Data_Moving,
  input  [7:0] Bit8_Mem_Data_In,
  input  Mem_Read,
  input  Mem_Write,
  input  Mem_Clock,
  input  [26:0] Mem_Address_In,
  input  Memory_Request_C,
  input  clk,
  input  reset,
  output RWDS_O,
  output [7:0] Bit8_Mem_Data_out,
  output [3:0] Mem_Index,
  output [1:0] Mem_Type,
  output [15:0] Core_Data_Out,
  output [26:0] Core_Address_Out,
  output Memory_Grant_C
);

  wire and_5_out, and_6_out, and_9_out, and_10_out, and_12_out, and_13_out, and_14_out, and_15_out,
       and_16_out, and_17_out, and_18_out, and_19_out, and_20_out, and_21_out, and_23_out, and_24_out,
       and_25_out, and_27_out, and_28_out, and_29_out, and_30_out, and_31_out, and_33_out, and_38_out,
       and_39_out, and_40_out, and_41_out, and_42_out, and_43_out, and_44_out, and_45_out, and_46_out,
       and_47_out, and_48_out, and_49_out, and_50_out, and_51_out, and_52_out, and_53_out, and_54_out,
       and_55_out, and_56_out, bit2_equal_1_equal, bit2_equal_2_equal, bit2_equal_3_equal,
       bit2_equal_4_equal, bit3_latching_arbiter_1_ga, bit3_latching_arbiter_1_gb, bit4_equal_1_equal,
       bit4_equal_2_equal, bit4_equal_3_equal, bit4_equal_4_equal, Bit16_Path_A_Enable, Bit16_Path_A_Select,
       Bit16_Path_B_Enable, CLK_t, condition_evaluator_1_condition_state, d_ff_1_q, d_ff_5_q, d_ff_6_q,
       data_cache_2_way_1_ram_read, data_cache_2_way_1_ram_write, data_cache_2_way_1_rwds, DCache_Stall,
       demultiplexer_1_out0, demultiplexer_1_out1, demultiplexer_1_out2, demultiplexer_1_out3,
       demultiplexer_5_out0, demultiplexer_5_out1, demultiplexer_5_out2, demultiplexer_5_out3,
       demultiplexer_6_out0, demultiplexer_6_out1, demultiplexer_6_out2, demultiplexer_6_out3,
       demultiplexer_7_out0, demultiplexer_7_out1, demultiplexer_8_out0, demultiplexer_8_out1,
       demultiplexer_8_out2, demultiplexer_9_out0, demultiplexer_9_out1, demultiplexer_10_out0,
       demultiplexer_10_out1, demultiplexer_10_out2, demultiplexer_10_out3, demultiplexer_10_out4,
       demultiplexer_10_out5, demultiplexer_10_out6, demultiplexer_10_out7, demultiplexer_10_out8,
       demultiplexer_10_out9, demultiplexer_10_out10, demultiplexer_10_out11, demultiplexer_10_out12,
       demultiplexer_10_out13, demultiplexer_10_out14, demultiplexer_10_out15, demultiplexer_11_out0,
       demultiplexer_11_out1, demultiplexer_11_out2, demultiplexer_11_out3, DisableTopHalfOfRegisters,
       EXE_MEM_Pipeline_write, Fetch_Unit_Target, Hardware_Interrupt, ICache_Stall, IDK, ImmediateToA,
       Injecting_Instruction, instruction_cache_2_way_1_ram_read, instruction_cache_2_way_1_rwds,
       InstructionAssert, Mem_Read_Hazard_Stall, MemoryOffsetAssert, mmu3_1_p22, mmu3_1_p24, mmu3_1_p25,
       mmu3_1_p26, MMU_Stall, multiplexer_12_out, multiplexer_15_out, Nop_Next, nor_1_out, nor_2_out,
       nor_3_out, not_1_out, not_2_out, not_3_out, not_4_out, not_6_out, not_7_out, Not_Core_Stalling,
       Not_Mute_EXE_Foward, Not_Mute_MEM_Forward, or_1_out, or_3_out, or_4_out, or_5_out, or_6_out, or_7_out,
       or_8_out, or_9_out, or_10_out, or_11_out, or_12_out, or_13_out, or_15_out, or_17_out, or_19_out,
       or_20_out, or_23_out, pull_resistor_12_node, READ_EXE_Pipeline_Write, SuppressNextInjection_qn,
       undriven, UsingStartupRom;
  wire [0:0] Two_Write_Field_LSB;
  wire [1:0] Bit16_Path_B_Select, bit_extender_14_out, bit_extender_16_out, priority_encoder_1_out,
       Privillege_Register_q, pull_resistor_7_node, register_5_q, register_7_q, register_11_q, Virtual_Mode_q;
  wire [1:1] and_22_out;
  wire [2:0] WriteStage_out;
  wire [3:0] alu4_1_p1, alu4_1_p6, Bit16_Path_B_Register_Select, bit_extender_1_out, bit_extender_5_out,
       bit_extender_6_out, bit_extender_7_out, bit_extender_23_out, BranchImmediate, multiplexer_13_out,
       pull_resistor_6_node, register_10_q, register_18_q;
  wire [4:0] Bit16_Path_A_Register_Select, bit_extender_2_out, bit_extender_3_out, bit_extender_4_out;
  wire [4:3] pull_resistor_2_node;
  wire [5:0] Opcode;
  wire [5:5] and_11_out;
  wire [6:0] MemoryStage_out;
  wire [7:0] bit_extender_13_out, bit_extender_15_out, Context_Register_q, data_cache_2_way_1_memory_byte,
       Memory_Region_Register_q, register_6_q, register_8_q, register_16_q;
  wire [9:0] bit_extender_8_out, bit_extender_9_out, bit_extender_10_out, multiplexer_9_out;
  wire [10:0] EXE_Write, Inner_EXE_Write, MEM_Write_t, pull_resistor_4_node, pull_resistor_16_node,
       register_1_q, WB_Write_q;
  wire [11:0] register_17_q;
  wire [12:0] bit_extender_24_out;
  wire [13:0] EXE_Memory, pull_resistor_3_node, pull_resistor_15_node, register_15_q, register_20_q;
  wire [14:0] bit_extender_22_out;
  wire [15:0] alu4_1_p5, and_32_out, bit_extender_17_out, bit_extender_18_out, bit_extender_19_out,
       bit_extender_20_out, controlled_buffer_31_out, controlled_buffer_32_out, controlled_buffer_51_out,
       controlled_buffer_60_out, Current_Instruction, Forwarding_Control, ICache_Result,
       InstructionImmediate, mmu3_1_p9, multiplexer_14_out, Next_Instruction, pull_resistor_9_node,
       pull_resistor_10_node, pull_resistor_19_node, register_2_q, register_13_q, register_14_q,
       register_25_q, register_file_1_readline_a, register_file_1_readline_b, StartupRomValue;
  wire [22:0] Readstage_out;
  wire [23:0] EXE_Control, pull_resistor_5_node;
  wire [25:0] register_21_q;
  wire [26:0] bit_extender_21_out, mmu3_1_p21, multiplexer_16_out;
  wire [26:1] Next_Instruction_Address;
  wire [31:0] adder_1_out, bit16_to_32_side_select_extender_1_bit32_out, bit32_side_select_1_bit32_out,
       Bit32_To_Fetch_Unit, bit32_toggle_inverter_toggle_shift1_1_out_4, bit_extender_12_out,
       controlled_buffer_4_out, controlled_buffer_30_out, controlled_buffer_35_out, controlled_buffer_44_out,
       Frame_Pointer_q, General_32_Bit_Register_q, Memory_Offset_q, pull_resistor_8_node,
       pull_resistor_17_node, pull_resistor_18_node, register_4_q, register_12_q, register_22_q,
       register_24_q, Stack_Pointer_q;

  Pull_Resistor #(.pull(1)) pull_resistor_1 (.node(EXE_MEM_Pipeline_write));
  D_Flip_Flop d_ff_1 (.D(Interrupt), .clk(CLK_t), .Q(d_ff_1_q), .reset(reset));  // open: Qn, preset
  and and_1 (Hardware_Interrupt, ~Injecting_Instruction, d_ff_1_q);  // AND_Gate
  PLA #(.in_width(6), .out_width(23), .\table ("000000 00000000000000000000000\n000001 00000000000000000101000\n000010 00000000000000000101000\n000011 00000000000000000101000\n000100 00000000000000000101000\n000101 00000000000000000101000\n000110 00000000000000000101000\n000111 00000000000000000101000\n001000 00000000010000000101000\n001001 00000000000000000101000\n001010 00000000000000000101000\n001011 00000000100000010101000\n001100 00000000000000001101000\n001101 00000000100000010101000\n001110 00000000000000001101000\n001111 00000000000000001101000\n010000 00000000000000001101000\n010001 00000000000000001101000\n010010 00000000000000000101000\n010011 00000000000000000101000\n010100 00000000000000000101000\n010101 00000000111001010101000\n010110 00000000111001010101000\n010111 00000000111001010101000\n011000 00000000111001010101000\n011001 00000000000000000000000\n011010 00001100000110100001000\n011011 00000000000000000011000\n011100 00000010010011010101000\n011101 00000000000111001101000\n011110 00000100000111000101000\n011111 01011010010011000100000\n100000 01001100000011000111000\n100001 01001100000010000101000\n100010 00111000100010000101000\n100011 00111000100010010101000\n100100 00000000111001010101000\n100101 00000000000110100001101\n100110 01000001000000010100000\n100111 01000001000000010100000\n101000 01000001010000010100000\n101001 01000001010000010100000\n101010 11000000001010000001000\n101011 11000000000010000001000\n101100 00000000000110000101000\n101101 00000100000010000001000\n101110 00000000000000000000000\n101111 00000010000110000001000\n110000 00001100000010000101000\n110001 00000000000000000000000\n110010 00000000000000000000000\n110011 00000000000000000000000\n110100 00000000000000000000000\n110101 00000000000000000000000\n110110 00000000000000000000000\n110111 00000000000000000000000\n111000 00000000000000000000000\n111001 00000000000000000000000\n111010 00000000000000000000000\n111011 00000000000000000000000\n111100 00000000000000000000000\n111101 00000000000000000000000\n111110 00000000000000000000000\n111111 01000001000000000000000")) Readstage (
    .in(Opcode),
    .out({Readstage_out[22:8], Bit16_Path_B_Select, Bit16_Path_B_Enable, Bit16_Path_A_Select, Bit16_Path_A_Enable, Readstage_out[2:0]}));
  PLA #(.in_width(6), .out_width(24), .\table ("000000 000000000000000000000000\n000001 000000100000001000000000\n000010 000000100001001000000000\n000011 000000100010001000000000\n000100 000000100011001000000000\n000101 000000100100001000000000\n000110 000000100101001000000000\n000111 000000100110001000000000\n001000 000000100111001000000000\n001001 000000101000001000000000\n001010 000000101001001000000000\n001011 000000100000001000000000\n001100 000000100000001000000000\n001101 000000100010001000000000\n001110 000000100010001000000000\n001111 000000101010001000000000\n010000 000000101011001000000000\n010001 000000101100001000000000\n010010 000000101010001000000000\n010011 000000101011001000000000\n010100 000000101100001000000000\n010101 000000100110001000000000\n010110 000000100111001000000000\n010111 000000101001001000000000\n011000 000000101000001000000000\n011001 000000000000000000000000\n011010 000001000000100000001000\n011011 000000000000100000000000\n011100 010000000000000000000001\n011101 010000000000000000000001\n011110 010000000000000000000001\n011111 000000000000010000000001\n100000 000000000000010000000001\n100001 000000000000010000000001\n100010 000000010000010000001010\n100011 010000000000000000001001\n100100 001000000000100000000000\n100101 000001000000100000001000\n100110 110010010000000000000001\n100111 110010000000000000000001\n101000 110110010000000000000001\n101001 110110000000000000000001\n101010 100010000000000000000001\n101011 100110000000000000000001\n101100 000000101101001000000000\n101101 000000000000100000000001\n101110 000000000000000000000000\n101111 000000000000000000000001\n110000 000000000000010000000001\n110001 000000000000000000000000\n110010 000000000000000000000000\n110011 000000000000000000000000\n110100 000000000000000000000000\n110101 000000000000000000000000\n110110 000000000000000000000000\n110111 000000000000000000000000\n111000 000000000000000000000000\n111001 000000000000000000000000\n111010 000000000000000000000000\n111011 000000000000000000000000\n111100 000000000000000000000000\n111101 000000000000000000000000\n111110 000000000000000000000000\n111111 000010000000000000000010")) EXEstage (
    .in(Opcode), .out(EXE_Control));
  PLA #(.in_width(6), .out_width(7), .\table ("000000 0000000\n000001 0010000\n000010 0010000\n000011 0010000\n000100 0010000\n000101 0010000\n000110 0010000\n000111 0010000\n001000 0001000\n001001 0010000\n001010 0010000\n001011 0010000\n001100 0010000\n001101 0010000\n001110 0010000\n001111 0010000\n010000 0010000\n010001 0010000\n010010 0010000\n010011 0010000\n010100 0010000\n010101 0010000\n010110 0010000\n010111 0010000\n011000 0010000\n011001 0000000\n011010 0010000\n011011 0010000\n011100 1101000\n011101 1101000\n011110 1101000\n011111 1101100\n100000 1100100\n100001 1100100\n100010 0100110\n100011 0101010\n100100 0010000\n100101 0010000\n100110 0000000\n100111 0000000\n101000 0000000\n101001 0000000\n101010 0000000\n101011 0000000\n101100 0000000\n101101 0100001\n101110 0000000\n101111 1101000\n110000 1100100\n110001 0000000\n110010 0000000\n110011 0000000\n110100 0000000\n110101 0000000\n110110 0000000\n110111 0000000\n111000 0000000\n111001 0000000\n111010 0000000\n111011 0000000\n111100 0000000\n111101 0000000\n111110 0000000\n111111 0000000")) MemoryStage (
    .in(Opcode), .out({MemoryStage_out[6], EXE_Memory[13:10], MemoryStage_out[1:0]}));
  PLA #(.in_width(6), .out_width(3), .\table ("000000 000\n000001 001\n000010 001\n000011 001\n000100 001\n000101 001\n000110 001\n000111 001\n001000 001\n001001 001\n001010 001\n001011 001\n001100 001\n001101 001\n001110 001\n001111 001\n010000 001\n010001 001\n010010 001\n010011 001\n010100 001\n010101 001\n010110 001\n010111 001\n011000 001\n011001 000\n011010 000\n011011 001\n011100 001\n011101 001\n011110 001\n011111 000\n100000 000\n100001 000\n100010 010\n100011 011\n100100 001\n100101 000\n100110 000\n100111 000\n101000 000\n101001 000\n101010 000\n101011 000\n101100 001\n101101 000\n101110 000\n101111 001\n110000 000\n110001 000\n110010 000\n110011 000\n110100 000\n110101 000\n110110 000\n110111 000\n111000 000\n111001 000\n111010 000\n111011 000\n111100 000\n111101 000\n111110 000\n111111 000")) WriteStage (
    .in(Opcode), .out(WriteStage_out));
  PLA #(.in_width(6), .out_width(3), .\table ("000000 000")) InstructionControl (.in(Opcode));  // open: out
  Multiplexer multiplexer_1 (
    .in0(MemoryStage_out[1]), .in1(BranchImmediate[3]), .out(EXE_Memory[9]), .sel(MemoryStage_out[6]));
  // Probe on {Opcode, BranchImmediate, Two_Write_Field_LSB[0], pull_resistor_2_node, EXE_Memory[2:0]}
  Pull_Resistor pull_resistor_2 (.node({Opcode, BranchImmediate, Two_Write_Field_LSB[0], pull_resistor_2_node, EXE_Memory[2:0]}));
  assign {Opcode, BranchImmediate, Two_Write_Field_LSB[0], pull_resistor_2_node, EXE_Memory[2:0]} = not_1_out ? Current_Instruction : 16'bz;  // Controlled_Buffer controlled_buffer_1
  not not_1 (not_1_out, Nop_Next);
  and and_2 (EXE_Memory[4], MemoryStage_out[0], Two_Write_Field_LSB[0]);
  and and_3 (EXE_Memory[3], MemoryStage_out[0], ~Two_Write_Field_LSB[0]);  // AND_Gate
  not not_2 (not_2_out, BranchImmediate[3]);
  Demultiplexer #(.select(2)) demultiplexer_1 (
    .out0(demultiplexer_1_out0), .out1(demultiplexer_1_out1), .out2(demultiplexer_1_out2),
    .out3(demultiplexer_1_out3), .in(IDK), .sel(BranchImmediate[2:1]));
  and and_4 (IDK, Readstage_out[8], BranchImmediate[3]);
  Multiplexer #(.width(2)) multiplexer_2 (
    .in0({BranchImmediate[0], Two_Write_Field_LSB[0]}), .in1(EXE_Memory[1:0]), .out(EXE_Write[9:8]),
    .sel(Readstage_out[20]));
  or or_1 (or_1_out, demultiplexer_1_out3, demultiplexer_1_out2, demultiplexer_1_out0);
  or or_2 (DisableTopHalfOfRegisters, and_5_out, and_6_out);
  and and_5 (and_5_out, ~Readstage_out[22], Readstage_out[21]);  // AND_Gate
  and and_6 (and_6_out, Readstage_out[21], Bit16_Path_A_Register_Select[4]);
  assign bit_extender_1_out = {{1{1'b0}}, {Two_Write_Field_LSB[0], pull_resistor_2_node}};  // Bit_Extender bit_extender_1
  assign bit_extender_2_out = {{2{1'b0}}, EXE_Memory[2:0]};  // Bit_Extender bit_extender_2
  assign bit_extender_3_out = {{2{1'b0}}, {Two_Write_Field_LSB[0], pull_resistor_2_node}};  // Bit_Extender bit_extender_3
  assign bit_extender_4_out = {{1{1'b0}}, BranchImmediate};  // Bit_Extender bit_extender_4
  Bit_Extender #(.in_width(5), .out_width(4), .\type ("zero")) bit_extender_5 (
    .in({pull_resistor_2_node, EXE_Memory[2:0]}), .out(bit_extender_5_out));
  Bit_Extender #(.in_width(5), .out_width(4), .\type ("zero")) bit_extender_6 (
    .in({BranchImmediate, Two_Write_Field_LSB[0]}), .out(bit_extender_6_out));
  and and_7 (ImmediateToA, Readstage_out[19], nor_1_out);
  Bit_Extender #(.in_width(5), .out_width(4), .\type ("zero")) bit_extender_7 (
    .in(bit_extender_2_out), .out(bit_extender_7_out));
  Multiplexer #(.select(2), .width(5)) multiplexer_3 (
    .in0(bit_extender_3_out), .in1(bit_extender_2_out), .in2({pull_resistor_2_node, EXE_Memory[2:0]}),
    .in3(bit_extender_4_out), .out(Bit16_Path_A_Register_Select), .sel(Readstage_out[10:9]));
  Demultiplexer demultiplexer_2 (
    .out0(MemoryOffsetAssert), .out1(InstructionAssert), .in(DisableTopHalfOfRegisters),
    .sel(Readstage_out[15]));
  Multiplexer #(.select(2), .width(4)) multiplexer_4 (
    .in0(BranchImmediate), .in1(bit_extender_6_out), .in2(bit_extender_1_out), .out(EXE_Write[3:0]),
    .sel(Readstage_out[12:11]));  // open: in3
  Multiplexer #(.select(2), .width(4)) multiplexer_5 (
    .in0(bit_extender_7_out), .in1(bit_extender_5_out), .in2(BranchImmediate), .in3(bit_extender_6_out),
    .out(Bit16_Path_B_Register_Select), .sel(Readstage_out[18:17]));
  nor nor_1 (nor_1_out, ~Bit16_Path_A_Register_Select[4], Bit16_Path_A_Register_Select[3], Bit16_Path_A_Register_Select[2]);  // NOR_Gate
  Multiplexer multiplexer_6 (.in0(WriteStage_out[0]), .in1(not_2_out), .out(EXE_Write[4]), .sel(Readstage_out[8]));
  Multiplexer multiplexer_7 (.in0(WriteStage_out[1]), .in1(or_1_out), .out(EXE_Write[10]), .sel(Readstage_out[8]));
  Multiplexer multiplexer_8 (
    .in0(WriteStage_out[2]), .in1(demultiplexer_1_out1), .out(EXE_Write[7]), .sel(Readstage_out[8]));
  and and_8 (Injecting_Instruction, Readstage_out[2], SuppressNextInjection_qn);
  and and_9 (and_9_out, Readstage_out[0], SuppressNextInjection_qn);
  and and_10 (and_10_out, Readstage_out[1], SuppressNextInjection_qn);
  and and_11 (and_11_out[5], Two_Write_Field_LSB[0], ~Readstage_out[16]);  // AND_Gate
  and and_12 (and_12_out, Readstage_out[16], Two_Write_Field_LSB[0]);
  assign bit_extender_8_out = {{4{1'b0}}, {and_11_out[5], pull_resistor_2_node, EXE_Memory[2:0]}};  // Bit_Extender bit_extender_8
  assign bit_extender_9_out = {{7{1'b0}}, EXE_Memory[2:0]};  // Bit_Extender bit_extender_9
  assign bit_extender_10_out = {{6{1'b0}}, BranchImmediate};  // Bit_Extender bit_extender_10
  Multiplexer #(.select(2), .width(10)) multiplexer_9 (
    .in0({BranchImmediate, Two_Write_Field_LSB[0], pull_resistor_2_node, EXE_Memory[2:0]}),
    .in1(bit_extender_8_out), .in2(bit_extender_9_out), .in3(bit_extender_10_out), .out(multiplexer_9_out),
    .sel(Readstage_out[14:13]));
  // Multiplexer multiplexer_10: pin names not known; wires that end beside it: BranchImmediate[3], and_12_out, Two_Write_Field_LSB[0], BranchImmediate[3]
  D_Flip_Flop d_ff_2 (.D(and_13_out), .clk(CLK_t), .Qn(Not_Mute_EXE_Foward));  // open: Q, preset, reset
  and and_13 (and_13_out, READ_EXE_Pipeline_Write, and_9_out);
  D_Flip_Flop d_ff_3 (.D(and_14_out), .clk(CLK_t), .Qn(Not_Mute_MEM_Forward));  // open: Q, preset, reset
  and and_14 (and_14_out, READ_EXE_Pipeline_Write, and_10_out);
  D_Flip_Flop SuppressNextInjection (
    .D(and_15_out), .clk(CLK_t), .Qn(SuppressNextInjection_qn));  // open: Q, preset, reset
  and and_15 (and_15_out, READ_EXE_Pipeline_Write, Injecting_Instruction);
  assign InstructionImmediate = {{6{1'b0}}, multiplexer_9_out};  // Bit_Extender bit_extender_11
  Register #(.width(11)) register_1 (
    .D(MEM_Write_t), .en(EXE_MEM_Pipeline_write), .clk(CLK_t), .Q(register_1_q));  // open: clr
  or or_3 (or_3_out, Hardware_Interrupt, Injecting_Instruction);
  not not_3 (not_3_out, UsingStartupRom);
  Demultiplexer #(.select(2)) demultiplexer_3 (
    .in(register_1_q[10]), .sel(register_1_q[9:8]));  // open: out0, out1, out2, out3
  Demultiplexer #(.select(2)) demultiplexer_4 (
    .in(register_1_q[7]), .sel(register_1_q[6:5]));  // open: out0, out1, out2, out3
  Multiplexer #(.select(2), .width(16)) multiplexer_11 (
    .in0(ICache_Result), .in1(StartupRomValue),
    .in2({Current_Instruction[15:10], Current_Instruction[4:0], Current_Instruction[9:5]}), .in3({16{1'b0}}),
    .out(Next_Instruction), .sel(priority_encoder_1_out));
  Priority_Encoder #(.select(2)) priority_encoder_1 (
    .in0(not_3_out), .in1(UsingStartupRom), .in2(or_3_out), .in3(Fetch_Unit_Target),
    .out(priority_encoder_1_out));  // open: gs, en_out, en_in
  buf and_16 (and_16_out, ICache_Stall);  // AND_Gate AND_Gate
  Register #(.width(11)) WB_Write (
    .D(MEM_Write_t), .en(EXE_MEM_Pipeline_write), .clk(CLK_t), .Q(WB_Write_q));  // open: clr
  Register #(.trigger("falling"), .width(16)) register_2 (
    .D(Next_Instruction), .en(1'b1), .clk(CLK_t), .Q(register_2_q), .clr(reset));
  nor nor_2 (nor_2_out, Injecting_Instruction, Mem_Read_Hazard_Stall, Hardware_Interrupt, and_16_out, DCache_Stall);
  nor nor_3 (nor_3_out, Mem_Read_Hazard_Stall, DCache_Stall, and_16_out);
  Counter #(.max('h3ffffff), .width(26)) counter_1 (
    .clr(reset), .load(Fetch_Unit_Target), .up(1'b1), .count(nor_2_out), .clk(CLK_t),
    .D(Bit32_To_Fetch_Unit[26:1]), .Q(Next_Instruction_Address));  // open: carry
  Register #(.width(16)) register_3 (
    .D(register_2_q), .en(nor_3_out), .clk(CLK_t), .Q(Current_Instruction), .clr(reset));
  Demultiplexer #(.select(2)) demultiplexer_5 (
    .out0(demultiplexer_5_out0), .out1(demultiplexer_5_out1), .out2(demultiplexer_5_out2),
    .out3(demultiplexer_5_out3), .in(WB_Write_q[10]), .sel(WB_Write_q[9:8]));
  Demultiplexer #(.select(2)) demultiplexer_6 (
    .out0(demultiplexer_6_out0), .out1(demultiplexer_6_out1), .out2(demultiplexer_6_out2),
    .out3(demultiplexer_6_out3), .in(WB_Write_q[7]), .sel(WB_Write_q[6:5]));
  Demultiplexer demultiplexer_7 (
    .out0(demultiplexer_7_out0), .out1(demultiplexer_7_out1), .in(Bit16_Path_A_Enable),
    .sel(Bit16_Path_A_Select));
  Demultiplexer #(.select(2)) demultiplexer_8 (
    .out0(demultiplexer_8_out0), .out1(demultiplexer_8_out1), .out2(demultiplexer_8_out2),
    .in(Bit16_Path_B_Enable), .sel(Bit16_Path_B_Select));  // open: out3
  Demultiplexer demultiplexer_9 (
    .out0(demultiplexer_9_out0), .out1(demultiplexer_9_out1), .in(demultiplexer_7_out0),
    .sel(Bit16_Path_A_Register_Select[4]));
  assign bit_extender_12_out = {{5{1'b0}}, {Next_Instruction_Address, 1'b0}};  // Bit_Extender bit_extender_12
  Register #(.trigger("falling"), .width(32)) register_4 (
    .D(bit_extender_12_out), .en(Not_Core_Stalling), .clk(CLK_t), .Q(register_4_q));  // open: clr
  Register #(.trigger("falling"), .width(32)) Memory_Offset (
    .D(register_24_q), .en(demultiplexer_5_out0), .clk(CLK_t), .Q(Memory_Offset_q));  // open: clr
  Register #(.trigger("falling"), .width(32)) Frame_Pointer (
    .D(register_24_q), .en(demultiplexer_5_out1), .clk(CLK_t), .Q(Frame_Pointer_q));  // open: clr
  Register #(.trigger("falling"), .width(32)) Stack_Pointer (
    .D(register_24_q), .en(demultiplexer_5_out2), .clk(CLK_t), .Q(Stack_Pointer_q));  // open: clr
  Register #(.trigger("falling"), .width(32)) General_32_Bit_Register (
    .D(register_24_q), .en(demultiplexer_5_out3), .clk(CLK_t), .Q(General_32_Bit_Register_q));  // open: clr
  Register #(.trigger("falling"), .width(32)) Instruction_Pointer (
    .D(register_4_q), .en(Not_Core_Stalling), .clk(CLK_t));  // open: Q, clr
  Bit_Extender #(.in_width(16), .out_width(8), .\type ("zero")) bit_extender_13 (
    .in(register_25_q), .out(bit_extender_13_out));
  Bit_Extender #(.in_width(16), .out_width(2), .\type ("zero")) bit_extender_14 (
    .in(register_25_q), .out(bit_extender_14_out));
  Bit_Extender #(.in_width(16), .out_width(8), .\type ("zero")) bit_extender_15 (
    .in(register_25_q), .out(bit_extender_15_out));
  Bit_Extender #(.in_width(16), .out_width(2), .\type ("zero")) bit_extender_16 (
    .in(register_25_q), .out(bit_extender_16_out));
  Register_File register_file_1 (
    .Write_Data(register_25_q), .Read_Address_B(Bit16_Path_B_Register_Select),
    .Read_B_Enable(demultiplexer_8_out0), .Read_Address_A(Bit16_Path_A_Register_Select[3:0]),
    .Read_A_Enable(demultiplexer_9_out0), .Write_Address(WB_Write_q[3:0]), .Write_Enable(WB_Write_q[4]),
    .Clock(CLK_t), .ReadLine_A(register_file_1_readline_a), .ReadLine_B(register_file_1_readline_b));  // open: Clear_All_Registers
  Register #(.trigger("falling")) Context_Register (
    .D(bit_extender_13_out), .en(demultiplexer_6_out0), .clk(CLK_t), .Q(Context_Register_q));  // open: clr
  Register #(.trigger("falling"), .width(2)) Privillege_Register (
    .D(bit_extender_14_out), .en(demultiplexer_6_out1), .clk(CLK_t), .Q(Privillege_Register_q));  // open: clr
  Register #(.trigger("falling")) Memory_Region_Register (
    .D(bit_extender_15_out), .en(demultiplexer_6_out2), .clk(CLK_t), .Q(Memory_Region_Register_q));  // open: clr
  Register #(.trigger("falling"), .width(2)) Virtual_Mode (
    .D(bit_extender_16_out), .en(demultiplexer_6_out3), .clk(CLK_t), .Q(Virtual_Mode_q));  // open: clr
  Register #(.width(2)) register_5 (.D(Virtual_Mode_q), .en(1'b1), .clk(CLK_t), .Q(register_5_q));  // open: clr
  Register register_6 (.D(Context_Register_q), .en(1'b1), .clk(CLK_t), .Q(register_6_q));  // open: clr
  Multiplexer multiplexer_12 (.in0(demultiplexer_9_out1), .in1(IDK), .out(multiplexer_12_out), .sel(and_22_out[1]));
  assign register_file_1_readline_a = demultiplexer_10_out8 ? Memory_Offset_q[15:0] : 16'bz;  // Controlled_Buffer controlled_buffer_2
  assign register_file_1_readline_a = demultiplexer_10_out12 ? Memory_Offset_q[31:16] : 16'bz;  // Controlled_Buffer controlled_buffer_3
  assign controlled_buffer_4_out = and_17_out ? Memory_Offset_q : 32'bz;  // Controlled_Buffer controlled_buffer_4
  and and_17 (and_17_out, or_4_out, or_5_out);
  assign register_file_1_readline_a = demultiplexer_10_out9 ? Frame_Pointer_q[15:0] : 16'bz;  // Controlled_Buffer controlled_buffer_5
  assign register_file_1_readline_a = demultiplexer_10_out13 ? Frame_Pointer_q[31:16] : 16'bz;  // Controlled_Buffer controlled_buffer_6
  assign controlled_buffer_4_out = and_18_out ? Frame_Pointer_q : 32'bz;  // Controlled_Buffer controlled_buffer_7
  and and_18 (and_18_out, or_6_out, or_7_out);
  assign register_file_1_readline_a = demultiplexer_10_out10 ? Stack_Pointer_q[15:0] : 16'bz;  // Controlled_Buffer controlled_buffer_8
  assign register_file_1_readline_a = demultiplexer_10_out14 ? Stack_Pointer_q[31:16] : 16'bz;  // Controlled_Buffer controlled_buffer_9
  assign controlled_buffer_4_out = and_19_out ? Stack_Pointer_q : 32'bz;  // Controlled_Buffer controlled_buffer_10
  and and_19 (and_19_out, or_8_out, or_9_out);
  assign register_file_1_readline_a = demultiplexer_10_out11 ? General_32_Bit_Register_q[15:0] : 16'bz;  // Controlled_Buffer controlled_buffer_11
  assign register_file_1_readline_a = demultiplexer_10_out15 ? General_32_Bit_Register_q[31:16] : 16'bz;  // Controlled_Buffer controlled_buffer_12
  assign controlled_buffer_4_out = and_20_out ? General_32_Bit_Register_q : 32'bz;  // Controlled_Buffer controlled_buffer_13
  and and_20 (and_20_out, or_10_out, or_11_out);
  assign bit_extender_17_out = {{8{1'b0}}, Context_Register_q};  // Bit_Extender bit_extender_17
  assign register_file_1_readline_a = demultiplexer_10_out4 ? bit_extender_17_out : 16'bz;  // Controlled_Buffer controlled_buffer_14
  assign bit_extender_18_out = {{14{1'b0}}, Privillege_Register_q};  // Bit_Extender bit_extender_18
  assign register_file_1_readline_a = demultiplexer_10_out5 ? bit_extender_18_out : 16'bz;  // Controlled_Buffer controlled_buffer_15
  assign bit_extender_19_out = {{8{1'b0}}, Memory_Region_Register_q};  // Bit_Extender bit_extender_19
  assign register_file_1_readline_a = demultiplexer_10_out6 ? bit_extender_19_out : 16'bz;  // Controlled_Buffer controlled_buffer_16
  assign bit_extender_20_out = {{14{1'b0}}, Virtual_Mode_q};  // Bit_Extender bit_extender_20
  assign register_file_1_readline_a = demultiplexer_10_out7 ? bit_extender_20_out : 16'bz;  // Controlled_Buffer controlled_buffer_17
  Register #(.width(2)) register_7 (.D(register_5_q), .en(1'b1), .clk(CLK_t), .Q(register_7_q));  // open: clr
  Register register_8 (.D(register_6_q), .en(1'b1), .clk(CLK_t), .Q(register_8_q));  // open: clr
  Multiplexer #(.width(4)) multiplexer_13 (
    .in0(Bit16_Path_A_Register_Select[3:0]), .in1(EXE_Write[3:0]), .out(multiplexer_13_out),
    .sel(and_22_out[1]));
  or or_4 (or_4_out, MemoryOffsetAssert, demultiplexer_10_out8, demultiplexer_10_out0, demultiplexer_10_out12, demultiplexer_11_out0);
  or or_5 (or_5_out, demultiplexer_11_out0, ~and_22_out[1]);  // OR_Gate
  or or_6 (or_6_out, demultiplexer_10_out13, demultiplexer_10_out9, demultiplexer_10_out1, demultiplexer_11_out1);
  or or_7 (or_7_out, demultiplexer_11_out1, ~and_22_out[1]);  // OR_Gate
  or or_8 (or_8_out, demultiplexer_10_out14, demultiplexer_10_out10, demultiplexer_10_out2, demultiplexer_11_out2);
  or or_9 (or_9_out, demultiplexer_11_out2, ~and_22_out[1]);  // OR_Gate
  or or_10 (or_10_out, InstructionAssert, demultiplexer_10_out11, demultiplexer_11_out3, demultiplexer_10_out15, demultiplexer_10_out3);
  or or_11 (or_11_out, demultiplexer_11_out3, ~and_22_out[1]);  // OR_Gate
  and and_21 (and_21_out, demultiplexer_9_out1, ~DisableTopHalfOfRegisters);  // AND_Gate
  Demultiplexer #(.select(4)) demultiplexer_10 (
    .out0(demultiplexer_10_out0), .out1(demultiplexer_10_out1), .out2(demultiplexer_10_out2),
    .out3(demultiplexer_10_out3), .out4(demultiplexer_10_out4), .out5(demultiplexer_10_out5),
    .out6(demultiplexer_10_out6), .out7(demultiplexer_10_out7), .out8(demultiplexer_10_out8),
    .out9(demultiplexer_10_out9), .out10(demultiplexer_10_out10), .out11(demultiplexer_10_out11),
    .out12(demultiplexer_10_out12), .out13(demultiplexer_10_out13), .out14(demultiplexer_10_out14),
    .out15(demultiplexer_10_out15), .in(and_21_out), .sel(Bit16_Path_A_Register_Select[3:0]));
  and and_22 (and_22_out[1], EXE_Write[3], EXE_Write[10]);
  and and_23 (and_23_out, or_12_out, READ_EXE_Pipeline_Write);
  or or_12 (or_12_out, demultiplexer_8_out1, demultiplexer_7_out1);
  Demultiplexer #(.select(2)) demultiplexer_11 (
    .out0(demultiplexer_11_out0), .out1(demultiplexer_11_out1), .out2(demultiplexer_11_out2),
    .out3(demultiplexer_11_out3), .in(and_22_out[1]), .sel(EXE_Write[1:0]));
  buf or_13 (or_13_out, undriven);  // OR_Gate OR_Gate
  Bit2_Equal bit2_equal_1 (.Bit3_B(MEM_Write_t[9:8]), .Bit3_A(multiplexer_13_out[1:0]), .Equal(bit2_equal_1_equal));
  Bit2_Equal bit2_equal_2 (.Bit3_B(MEM_Write_t[6:5]), .Bit3_A(multiplexer_13_out[1:0]), .Equal(bit2_equal_2_equal));
  Bit4_Equal bit4_equal_1 (
    .Bit4_B(MEM_Write_t[3:0]), .Bit4_A(Bit16_Path_B_Register_Select), .Equal(bit4_equal_1_equal));
  Bit4_Equal bit4_equal_2 (.Bit4_B(MEM_Write_t[3:0]), .Bit4_A(multiplexer_13_out), .Equal(bit4_equal_2_equal));
  Bit2_Equal bit2_equal_3 (.Bit3_B(Inner_EXE_Write[9:8]), .Bit3_A(multiplexer_13_out[1:0]), .Equal(bit2_equal_3_equal));
  Bit2_Equal bit2_equal_4 (.Bit3_B(Inner_EXE_Write[6:5]), .Bit3_A(multiplexer_13_out[1:0]), .Equal(bit2_equal_4_equal));
  Bit4_Equal bit4_equal_3 (
    .Bit4_B(Inner_EXE_Write[3:0]), .Bit4_A(Bit16_Path_B_Register_Select), .Equal(bit4_equal_3_equal));
  Bit4_Equal bit4_equal_4 (.Bit4_B(Inner_EXE_Write[3:0]), .Bit4_A(multiplexer_13_out), .Equal(bit4_equal_4_equal));
  D_Flip_Flop d_ff_4 (.D(and_23_out), .clk(CLK_t), .Q(Nop_Next));  // open: Qn, preset, reset
  assign register_file_1_readline_a = demultiplexer_7_out1 ? Next_Instruction : 16'bz;  // Controlled_Buffer controlled_buffer_18
  assign register_file_1_readline_b = demultiplexer_8_out1 ? Next_Instruction : 16'bz;  // Controlled_Buffer controlled_buffer_19
  nor nor_4 (UsingStartupRom, Memory_Region_Register_q[3], Memory_Region_Register_q[0], Memory_Region_Register_q[1], Memory_Region_Register_q[2], Memory_Region_Register_q[4], Memory_Region_Register_q[5], Memory_Region_Register_q[6], Memory_Region_Register_q[7]);
  and and_24 (and_24_out, ~and_32_out[7], bit2_equal_1_equal, multiplexer_12_out, multiplexer_13_out[3], ~multiplexer_13_out[2], MEM_Write_t[10], Not_Mute_MEM_Forward);  // AND_Gate
  and and_25 (and_25_out, multiplexer_13_out[2], bit2_equal_2_equal, multiplexer_12_out, ~multiplexer_13_out[3], MEM_Write_t[7], ~and_32_out[1], Not_Mute_MEM_Forward);  // AND_Gate
  and and_26 (and_32_out[3], bit4_equal_1_equal, demultiplexer_8_out0, MEM_Write_t[4], ~and_32_out[0], Not_Mute_MEM_Forward);  // AND_Gate
  and and_27 (and_27_out, bit4_equal_2_equal, MEM_Write_t[4], demultiplexer_9_out0, ~and_32_out[1], Not_Mute_MEM_Forward);  // AND_Gate
  and and_28 (and_28_out, Inner_EXE_Write[10], bit2_equal_3_equal, multiplexer_12_out, multiplexer_13_out[3], ~multiplexer_13_out[2], Not_Mute_EXE_Foward);  // AND_Gate
  Pull_Resistor pull_resistor_3 (.node(pull_resistor_3_node));
  assign pull_resistor_3_node = READ_EXE_Pipeline_Write ? {EXE_Memory[13:9], BranchImmediate, EXE_Memory[4:0]} : 14'bz;  // Controlled_Buffer controlled_buffer_20
  Register #(.width(11)) register_9 (
    .D(pull_resistor_4_node), .en(Not_Core_Stalling), .clk(CLK_t), .Q(Inner_EXE_Write));  // open: clr
  Pull_Resistor pull_resistor_4 (.node(pull_resistor_4_node));
  assign pull_resistor_4_node = READ_EXE_Pipeline_Write ? {EXE_Write[10:7], EXE_Write[9:8], EXE_Write[4:0]} : 11'bz;  // Controlled_Buffer controlled_buffer_21
  Pull_Resistor pull_resistor_5 (.node(pull_resistor_5_node));
  assign pull_resistor_5_node = READ_EXE_Pipeline_Write ? EXE_Control : 24'bz;  // Controlled_Buffer controlled_buffer_22
  assign register_file_1_readline_b = demultiplexer_8_out2 ? InstructionImmediate : 16'bz;  // Controlled_Buffer controlled_buffer_23
  assign register_file_1_readline_a = ImmediateToA ? InstructionImmediate : 16'bz;  // Controlled_Buffer controlled_buffer_24
  Register #(.width(4)) register_10 (
    .D(pull_resistor_6_node), .en(Not_Core_Stalling), .clk(CLK_t), .Q(register_10_q));  // open: clr
  Pull_Resistor pull_resistor_6 (.node(pull_resistor_6_node));
  assign pull_resistor_6_node = READ_EXE_Pipeline_Write ? BranchImmediate : 4'bz;  // Controlled_Buffer controlled_buffer_25
  and and_29 (and_29_out, ~and_32_out[7], bit2_equal_1_equal, multiplexer_12_out, Not_Mute_MEM_Forward, multiplexer_13_out[3], multiplexer_13_out[2], MEM_Write_t[10]);  // AND_Gate
  or or_14 (and_32_out[7], and_28_out, and_30_out);
  and and_30 (and_30_out, Inner_EXE_Write[10], bit2_equal_3_equal, multiplexer_12_out, multiplexer_13_out[3], multiplexer_13_out[2], Not_Mute_EXE_Foward);
  and and_31 (and_31_out, multiplexer_13_out[2], bit2_equal_4_equal, multiplexer_12_out, ~multiplexer_13_out[3], Inner_EXE_Write[7], Not_Mute_EXE_Foward);  // AND_Gate
  and and_32 (and_32_out[0], bit4_equal_3_equal, demultiplexer_8_out0, Not_Mute_EXE_Foward, Inner_EXE_Write[4]);
  and and_33 (and_33_out, bit4_equal_4_equal, demultiplexer_9_out0, Not_Mute_EXE_Foward, Inner_EXE_Write[4]);
  Register #(.width(2)) register_11 (
    .D(pull_resistor_7_node), .en(Not_Core_Stalling), .clk(CLK_t), .Q(register_11_q));  // open: clr
  Pull_Resistor pull_resistor_7 (.node(pull_resistor_7_node));
  assign pull_resistor_7_node = READ_EXE_Pipeline_Write ? {and_22_out[1], EXE_Write[2]} : 2'bz;  // Controlled_Buffer controlled_buffer_26
  Register #(.width(32)) register_12 (
    .D(pull_resistor_8_node), .en(Not_Core_Stalling), .clk(CLK_t), .Q(register_12_q));  // open: clr
  Pull_Resistor pull_resistor_8 (.node(pull_resistor_8_node));
  assign pull_resistor_8_node = READ_EXE_Pipeline_Write ? controlled_buffer_4_out : 32'bz;  // Controlled_Buffer controlled_buffer_27
  Register #(.width(16)) register_13 (
    .D(pull_resistor_9_node), .en(Not_Core_Stalling), .clk(CLK_t), .Q(register_13_q));  // open: clr
  Pull_Resistor pull_resistor_9 (.node(pull_resistor_9_node));
  assign pull_resistor_9_node = READ_EXE_Pipeline_Write ? register_file_1_readline_a : 16'bz;  // Controlled_Buffer controlled_buffer_28
  Register #(.width(16)) register_14 (
    .D(pull_resistor_10_node), .en(Not_Core_Stalling), .clk(CLK_t), .Q(register_14_q));  // open: clr
  Pull_Resistor pull_resistor_10 (.node(pull_resistor_10_node));
  assign pull_resistor_10_node = READ_EXE_Pipeline_Write ? register_file_1_readline_b : 16'bz;  // Controlled_Buffer controlled_buffer_29
  and and_34 (and_32_out[5], ~and_32_out[4], bit2_equal_1_equal, multiplexer_12_out, Not_Mute_MEM_Forward, or_15_out, MEM_Write_t[10]);  // AND_Gate
  and and_35 (and_32_out[4], Inner_EXE_Write[10], bit2_equal_3_equal, Not_Mute_EXE_Foward, multiplexer_12_out, or_17_out);
  nor nor_5 (READ_EXE_Pipeline_Write, Mem_Read_Hazard_Stall, or_23_out);
  assign controlled_buffer_30_out = Forwarding_Control[12] ? register_12_q : 32'bz;  // Controlled_Buffer controlled_buffer_30
  assign controlled_buffer_31_out = Forwarding_Control[11] ? register_13_q : 16'bz;  // Controlled_Buffer controlled_buffer_31
  assign controlled_buffer_32_out = Forwarding_Control[10] ? register_14_q : 16'bz;  // Controlled_Buffer controlled_buffer_32
  assign controlled_buffer_32_out = Forwarding_Control[8] ? controlled_buffer_35_out[31:16] : 16'bz;  // Controlled_Buffer controlled_buffer_33
  assign controlled_buffer_32_out = Forwarding_Control[9] ? controlled_buffer_35_out[15:0] : 16'bz;  // Controlled_Buffer controlled_buffer_34
  assign controlled_buffer_35_out = Forwarding_Control[7] ? register_22_q : 32'bz;  // Controlled_Buffer controlled_buffer_35
  assign controlled_buffer_35_out = Forwarding_Control[6] ? register_24_q : 32'bz;  // Controlled_Buffer controlled_buffer_36
  nor nor_6 (and_32_out[12], and_32_out[5], and_32_out[4]);
  or or_15 (or_15_out, multiplexer_13_out[3], ~multiplexer_13_out[2]);  // OR_Gate
  or or_16 (and_32_out[2], and_25_out, and_27_out);
  or or_17 (or_17_out, multiplexer_13_out[3], ~multiplexer_13_out[2]);  // OR_Gate
  or or_18 (and_32_out[1], and_31_out, and_33_out);
  or or_19 (or_19_out, and_33_out, and_32_out[0]);
  assign controlled_buffer_30_out = Forwarding_Control[5] ? register_24_q : 32'bz;  // Controlled_Buffer controlled_buffer_37
  Pull_Resistor pull_resistor_11 (.node(Mem_Read_Hazard_Stall));
  // AND_Gate and_36 has open pins: in0=or_19_out, in1=and_39_out, out=open
  Register #(.width(14)) register_15 (
    .D(pull_resistor_3_node), .en(Not_Core_Stalling), .clk(CLK_t), .Q(register_15_q));  // open: clr
  Register register_16 (
    .D(pull_resistor_5_node[7:0]), .en(Not_Core_Stalling), .clk(CLK_t), .Q(register_16_q));  // open: clr
  Register #(.width(12)) register_17 (
    .D(pull_resistor_5_node[23:12]), .en(Not_Core_Stalling), .clk(CLK_t), .Q(register_17_q));  // open: clr
  assign controlled_buffer_30_out = Forwarding_Control[4] ? register_22_q : 32'bz;  // Controlled_Buffer controlled_buffer_38
  assign controlled_buffer_31_out = Forwarding_Control[2] ? register_25_q : 16'bz;  // Controlled_Buffer controlled_buffer_39
  assign controlled_buffer_32_out = Forwarding_Control[3] ? register_25_q : 16'bz;  // Controlled_Buffer controlled_buffer_40
  assign controlled_buffer_32_out = Forwarding_Control[0] ? controlled_buffer_60_out : 16'bz;  // Controlled_Buffer controlled_buffer_41
  nor nor_7 (and_32_out[11], and_32_out[1], and_32_out[2]);
  nor nor_8 (and_32_out[10], and_32_out[3], and_32_out[0]);
  not not_4 (not_4_out, register_11_q[0]);
  Multiplexer #(.width(16)) multiplexer_14 (
    .in0(controlled_buffer_31_out), .in1(controlled_buffer_32_out), .out(multiplexer_14_out),
    .sel(register_17_q[10]));
  assign controlled_buffer_31_out = Forwarding_Control[1] ? controlled_buffer_60_out : 16'bz;  // Controlled_Buffer controlled_buffer_42
  and and_37 (Fetch_Unit_Target, register_17_q[7], or_20_out);
  or or_20 (or_20_out, ~register_17_q[8], condition_evaluator_1_condition_state);  // OR_Gate
  and and_38 (and_38_out, register_17_q[6], register_11_q[0]);
  Bit32_Side_Select bit32_side_select_1 (
    .Side_Select(not_4_out), .Side_Enable(register_11_q[1]), .bit32In(controlled_buffer_30_out),
    .Bit32_out(bit32_side_select_1_bit32_out));
  Bit16_To_32_Side_Select_Extender bit16_to_32_side_select_extender_1 (
    .HighSide(and_38_out), .Bit16_In(multiplexer_14_out),
    .Bit32_Out(bit16_to_32_side_select_extender_1_bit32_out));
  Bit32_Toggle_Inverter_Toggle_Shift1 bit32_toggle_inverter_toggle_shift1_1 (
    .Bit32_In(bit16_to_32_side_select_extender_1_bit32_out), .Invert(register_17_q[4]),
    .Shift1(register_17_q[11]), .out_4(bit32_toggle_inverter_toggle_shift1_1_out_4));
  Pull_Resistor #(.pull(1)) pull_resistor_12 (.node(pull_resistor_12_node));
  or or_21 (and_32_out[9], and_24_out, and_28_out);
  or or_22 (and_32_out[8], and_29_out, and_30_out);
  not not_5 (and_32_out[6], and_32_out[7]);
  D_Flip_Flop d_ff_5 (.D(Fetch_Unit_Target), .clk(CLK_t), .Q(d_ff_5_q));  // open: Qn, preset, reset
  Adder #(.width(32)) adder_1 (
    .a(bit32_side_select_1_bit32_out), .b(bit32_toggle_inverter_toggle_shift1_1_out_4), .out(adder_1_out),
    .cin(register_17_q[4]));  // open: cout
  Register #(.width(16)) u_Forwarding_Control (
    .D({{3{and_32_out[15]}}, and_32_out[12:0]}), .en(pull_resistor_12_node), .clk(CLK_t),
    .Q(Forwarding_Control));  // open: clr
  Pull_Resistor pull_resistor_13 (.node(and_32_out[15]));
  or or_23 (or_23_out, Fetch_Unit_Target, d_ff_5_q);
  Register #(.width(4)) register_18 (
    .D(pull_resistor_5_node[11:8]), .en(Not_Core_Stalling), .clk(CLK_t), .Q(register_18_q));  // open: clr
  assign Bit32_To_Fetch_Unit = register_16_q[1] ? bit32_side_select_1_bit32_out : 32'bz;  // Controlled_Buffer controlled_buffer_43
  assign controlled_buffer_44_out = register_16_q[4] ? bit32_side_select_1_bit32_out : 32'bz;  // Controlled_Buffer controlled_buffer_44
  assign Bit32_To_Fetch_Unit = register_16_q[0] ? adder_1_out : 32'bz;  // Controlled_Buffer controlled_buffer_45
  assign controlled_buffer_44_out = register_16_q[3] ? adder_1_out : 32'bz;  // Controlled_Buffer controlled_buffer_46
  assign controlled_buffer_44_out[15:0] = register_16_q[5] ? controlled_buffer_31_out : 16'bz;  // Controlled_Buffer controlled_buffer_47
  assign controlled_buffer_44_out[15:0] = register_16_q[7] ? controlled_buffer_32_out : 16'bz;  // Controlled_Buffer controlled_buffer_48
  assign controlled_buffer_44_out[31:16] = register_16_q[2] ? controlled_buffer_31_out : 16'bz;  // Controlled_Buffer controlled_buffer_49
  assign controlled_buffer_44_out[31:16] = register_16_q[6] ? controlled_buffer_32_out : 16'bz;  // Controlled_Buffer controlled_buffer_50
  // ALU4 alu4_1: pin names not known; wires that end beside it: alu4_1_p1[0], controlled_buffer_31_out, controlled_buffer_32_out, register_17_q[3:0], alu4_1_p5, alu4_1_p6[0], alu4_1_p6[1], alu4_1_p6[2], alu4_1_p6[3]
  Register #(.width(4)) register_19 (.D(alu4_1_p6), .en(register_17_q[5]), .clk(CLK_t), .Q(alu4_1_p1));  // open: clr
  Condition_Evaluator condition_evaluator_1 (
    .Bit4_Condition_Selector(register_10_q), .Bit4_Flags(alu4_1_p1),
    .Condition_State(condition_evaluator_1_condition_state));
  assign controlled_buffer_51_out = register_18_q[3] ? controlled_buffer_31_out : 16'bz;  // Controlled_Buffer controlled_buffer_51
  assign controlled_buffer_51_out = register_18_q[2] ? controlled_buffer_32_out : 16'bz;  // Controlled_Buffer controlled_buffer_52
  assign controlled_buffer_51_out = register_18_q[1] ? alu4_1_p5 : 16'bz;  // Controlled_Buffer controlled_buffer_53
  assign controlled_buffer_51_out[3:0] = register_18_q[0] ? alu4_1_p1 : 4'bz;  // Controlled_Buffer controlled_buffer_54
  Pull_Resistor pull_resistor_14 (.node(controlled_buffer_51_out[15:4]));
  Multiplexer multiplexer_15 (
    .in0(EXE_MEM_Pipeline_write), .in1(condition_evaluator_1_condition_state), .out(multiplexer_15_out),
    .sel(register_17_q[9]));
  Register #(.width(14)) register_20 (
    .D(pull_resistor_15_node), .en(Not_Core_Stalling), .clk(CLK_t), .Q(register_20_q));  // open: clr
  Pull_Resistor pull_resistor_15 (.node(pull_resistor_15_node));
  assign pull_resistor_15_node = EXE_MEM_Pipeline_write ? register_15_q : 14'bz;  // Controlled_Buffer controlled_buffer_55
  Register #(.width(11)) Mem_Writew (
    .D(pull_resistor_16_node), .en(Not_Core_Stalling), .clk(CLK_t), .Q(MEM_Write_t));  // open: clr
  Pull_Resistor pull_resistor_16 (.node(pull_resistor_16_node));
  assign pull_resistor_16_node = multiplexer_15_out ? Inner_EXE_Write : 11'bz;  // Controlled_Buffer controlled_buffer_56
  Register #(.width(32)) register_21 (
    .D(pull_resistor_17_node), .en(Not_Core_Stalling), .clk(CLK_t), .Q({Mem_Type, Mem_Index, register_21_q}));  // open: clr
  Pull_Resistor pull_resistor_17 (.node(pull_resistor_17_node));
  assign pull_resistor_17_node = EXE_MEM_Pipeline_write ? Bit32_To_Fetch_Unit : 32'bz;  // Controlled_Buffer controlled_buffer_57
  Register #(.width(32)) register_22 (
    .D(pull_resistor_18_node), .en(Not_Core_Stalling), .clk(CLK_t), .Q(register_22_q));  // open: clr
  Pull_Resistor pull_resistor_18 (.node(pull_resistor_18_node));
  assign pull_resistor_18_node = EXE_MEM_Pipeline_write ? controlled_buffer_44_out : 32'bz;  // Controlled_Buffer controlled_buffer_58
  Register #(.width(16)) register_23 (
    .D(pull_resistor_19_node), .en(Not_Core_Stalling), .clk(CLK_t), .Q(Core_Data_Out));  // open: clr
  Pull_Resistor pull_resistor_19 (.node(pull_resistor_19_node));
  assign pull_resistor_19_node = EXE_MEM_Pipeline_write ? controlled_buffer_51_out : 16'bz;  // Controlled_Buffer controlled_buffer_59
  assign controlled_buffer_60_out = register_20_q[12] ? Core_Data_Out : 16'bz;  // Controlled_Buffer controlled_buffer_60
  Pull_Resistor pull_resistor_20 (.node(register_22_q));
  Pull_Resistor pull_resistor_21 (.node(controlled_buffer_60_out));
  assign controlled_buffer_60_out = register_20_q[11] ? mmu3_1_p9 : 16'bz;  // Controlled_Buffer controlled_buffer_61
  Register #(.width(32)) register_24 (
    .D(register_22_q), .en(EXE_MEM_Pipeline_write), .clk(CLK_t), .Q(register_24_q));  // open: clr
  Register #(.width(16)) register_25 (
    .D(controlled_buffer_60_out), .en(EXE_MEM_Pipeline_write), .clk(CLK_t), .Q(register_25_q));  // open: clr
  // NOR_Gate nor_9 has open pins: in0=Mem_Type[0], in1=Mem_Type[1], out=open
  Bit_Extender #(.in_width(32), .out_width(27), .\type ("zero")) bit_extender_21 (
    .in({Mem_Type, Mem_Index, register_21_q}), .out(bit_extender_21_out));
  Bit_Extender #(.in_width(16), .out_width(15), .\type ("zero")) bit_extender_22 (
    .in(Core_Data_Out), .out(bit_extender_22_out));
  Bit_Extender #(.in_width(16), .out_width(4), .\type ("zero")) bit_extender_23 (
    .in(Core_Data_Out), .out(bit_extender_23_out));
  and and_39 (and_39_out, register_20_q[13], ~register_20_q[10]);  // AND_Gate
  and and_40 (and_40_out, register_20_q[5], register_20_q[4]);
  not not_6 (not_6_out, UsingStartupRom);
  and and_41 (and_41_out, register_20_q[6], register_20_q[4]);
  and and_42 (and_42_out, register_20_q[7], register_20_q[4]);
  and and_43 (and_43_out, register_20_q[8], register_20_q[4]);
  and and_44 (and_44_out, not_6_out, register_7_q[1]);
  and and_45 (and_45_out, ~register_7_q[1], not_6_out);  // AND_Gate
  Bit_Extender #(.in_width(27), .out_width(13), .\type ("zero")) bit_extender_24 (
    .in({Next_Instruction_Address, 1'b0}), .out(bit_extender_24_out));
  Multiplexer #(.width(27)) multiplexer_16 (
    .in0({Next_Instruction_Address, 1'b0}), .in1(bit_extender_21_out), .out(multiplexer_16_out),
    .sel(and_48_out));
  and and_46 (and_46_out, ~register_7_q[0], register_20_q[13]);  // AND_Gate
  and and_47 (and_47_out, register_7_q[0], register_20_q[13]);
  ROM #(.addrWidth(12), .dataWidth(16)) rom_1 (
    .addr(bit_extender_24_out[12:1]), .data({StartupRomValue[7:0], StartupRomValue[15:8]}));
  and and_48 (and_48_out, register_20_q[8], register_20_q[7], register_20_q[3]);
  D_Flip_Flop #(.trigger("low")) d_ff_6 (.D(not_7_out), .clk(CLK_t), .Q(d_ff_6_q));  // open: Qn, preset, reset
  and and_49 (and_49_out, d_ff_6_q, CLK_t);
  // MMU3 mmu3_1: pin names not known; wires that end beside it: multiplexer_16_out, and_44_out, and_45_out, bit_extender_21_out, and_47_out, and_46_out, register_20_q[9], register_20_q[10], mmu3_1_p9, register_8_q, and_43_out, register_20_q[2:0], and_42_out, bit_extender_22_out, and_41_out, bit_extender_23_out, and_40_out, 1'b1, reset, and_49_out, mmu3_1_p21, mmu3_1_p22, Core_Address_Out, mmu3_1_p24, mmu3_1_p25, mmu3_1_p26, MMU_Stall
  not not_7 (not_7_out, DCache_Stall);
  and and_50 (and_50_out, register_20_q[6], register_20_q[8], register_20_q[7], register_20_q[3]);
  and and_51 (and_51_out, ~register_20_q[6], register_20_q[8], register_20_q[7], register_20_q[3]);  // AND_Gate
  and and_52 (and_52_out, ~register_20_q[7], ~register_20_q[8], register_20_q[6], register_20_q[3]);  // AND_Gate
  and and_53 (and_53_out, register_20_q[7], ~register_20_q[8], register_20_q[6], register_20_q[3]);  // AND_Gate
  and and_54 (and_54_out, ~register_20_q[7], ~register_20_q[8], ~register_20_q[6], register_20_q[3]);  // AND_Gate
  and and_55 (and_55_out, register_20_q[7], ~register_20_q[8], ~register_20_q[6], register_20_q[3]);  // AND_Gate
  Memory_Clock memory_clock_1 (.Clock(clk), .Reset(reset), .CPU_Clock(CLK_t));  // open: RE_Clock, PSRAM_Clock, FE_Clock
  Instruction_Cache_2_Way instruction_cache_2_way_1 (
    .Read(mmu3_1_p22), .Two_Byte_Operation(mmu3_1_p22), .Invalidate_Address(and_50_out),
    .Invalidate_Line(and_51_out), .Set(register_20_q[5]), .Bit26_Address(mmu3_1_p21[25:0]),
    .Bit8_From_Memory(Bit8_Mem_Data_out), .Ram_Data_Moving(Data_Moving), .Clock(clk), .Reset(reset),
    .Bit16_To_Core(ICache_Result), .Ram_Read(instruction_cache_2_way_1_ram_read),
    .Requesting_Ram(ICache_Stall), .RWDS(instruction_cache_2_way_1_rwds));
  Data_Cache_2_Way data_cache_2_way_1 (
    .Read(mmu3_1_p24), .Write(mmu3_1_p25), .Two_Byte_Operation(mmu3_1_p26), .Flush_Address(and_52_out),
    .Invalidate_Address(and_53_out), .Flush_Line(and_54_out), .Invalidate_Line(and_55_out),
    .Set(register_20_q[5]), .Bit26_Address(Core_Address_Out[25:0]), .Bit16_Data(Core_Data_Out),
    .Bit8_From_Memory(Bit8_Mem_Data_out), .Ram_Data_Moving(Data_Moving), .Clock(clk), .Reset(reset),
    .Bit16_To_Core(mmu3_1_p9), .Ram_Write(data_cache_2_way_1_ram_write),
    .Ram_Read(data_cache_2_way_1_ram_read), .Requesting_Ram(DCache_Stall),
    .Memory_Byte(data_cache_2_way_1_memory_byte), .RWDS(data_cache_2_way_1_rwds));
  and and_56 (and_56_out, data_cache_2_way_1_ram_write, bit3_latching_arbiter_1_gb);
  Controlled_Buffer controlled_buffer_62 (.out(RWDS_I), .en(bit3_latching_arbiter_1_ga));  // open: in
  assign RWDS_I = and_56_out ? data_cache_2_way_1_rwds : 1'bz;  // Controlled_Buffer controlled_buffer_63
  assign Mem_Write = bit3_latching_arbiter_1_gb ? data_cache_2_way_1_ram_write : 1'bz;  // Controlled_Buffer controlled_buffer_64
  assign Mem_Read = bit3_latching_arbiter_1_gb ? data_cache_2_way_1_ram_read : 1'bz;  // Controlled_Buffer controlled_buffer_65
  assign Bit8_Mem_Data_In = bit3_latching_arbiter_1_gb ? data_cache_2_way_1_memory_byte : 8'bz;  // Controlled_Buffer controlled_buffer_66
  assign Mem_Address_In = bit3_latching_arbiter_1_ga ? mmu3_1_p21 : 27'bz;  // Controlled_Buffer controlled_buffer_67
  assign Mem_Address_In = bit3_latching_arbiter_1_gb ? Core_Address_Out : 27'bz;  // Controlled_Buffer controlled_buffer_68
  Bit3_Latching_Arbiter bit3_latching_arbiter_1 (
    .Reset(reset), .Clock(clk), .RA(ICache_Stall), .RB(DCache_Stall), .RC(Memory_Request_C),
    .GA(bit3_latching_arbiter_1_ga), .GB(bit3_latching_arbiter_1_gb), .GC(Memory_Grant_C));
  assign Mem_Read = bit3_latching_arbiter_1_ga ? instruction_cache_2_way_1_ram_read : 1'bz;  // Controlled_Buffer controlled_buffer_69
  nor nor_10 (Not_Core_Stalling, Mem_Read_Hazard_Stall, DCache_Stall, ICache_Stall);
  PSRAM_Controller_2 psram_controller_2_1 (
    .Clock(clk), .Reset(reset), .Read(Mem_Read), .Write(Mem_Write), .Bit8_Data(Bit8_Mem_Data_In),
    .Bit26_Address(Mem_Address_In[25:0]), .RWDS_In(RWDS_I), .RWDS_Out(RWDS_I), .Bit8_Out(Bit8_Mem_Data_out),
    .Data_Moving(Data_Moving));  // open: Setup
  // Pins of 26 and 27 bits meet at Core_Address_Out
  // Pins of 26 and 27 bits meet at Mem_Address_In
  // Pins of 26 and 27 bits meet at mmu3_1_p21

  assign Mem_Clock = clk;
  assign RWDS_O = RWDS_I;

  // Other names for the same wires on the sheet: EXE_Memory[8:5] = BranchImmediate;
  //   Two_Write_Field_LSB[3:1] = BranchImmediate[2:0]; EXE_Write[6:5] = EXE_Write[9:8];
  //   Injected_Instruction[15:0] = {Current_Instruction[15:10], Current_Instruction[4:0], Current_Instruction[9:5]};
  //   MEM_WB_Pipeline_write = EXE_MEM_Pipeline_write

  // Notes on the sheet:
  //   skipped bc causing issues and seemingly useless?
  //   v
  //   0b00000-0b01111
  //   0b10000-0b10011
  //   0b10100-0b10111
  //   0b11000-0b11011
  //   0b11100-0b11111
  //   spec
  //   32 full
  //   32 lower
  //   32upper
  //   points to the NEXT instruction
  //   holds the current instruction the decoder is decoding
  //   mem fwd
  //   32 bit write
  //   special write
  //   16 write
  //   exefwd
  //   32 forward
  //   16 forward
  //   32 - 32
  //   32 - 16
  //   16 - 32
  //   16 - 16
  //   add register protection
  //   lsb is data cache virtual mode, msb is instruction
  //   32l
  //   B
  //   A
  //   32l
  //   B
  //   A
  //   32 not
  //   32h
  //   32
  //   spec
  //   32h
  //   32
  //   spec
  //   anot
  //   bot
  //   32l
  //   32h
  //   exe 32lh
  //   mem 32
  //   exe 32
  //   memb
  //   mema
  //   exe a
  //   exeb
  //   mem32lh
  //   0=normal,1=
  //   2msb->mem access type 
  //   contents of rom_1 (hex, n*v repeats v):
  //   406c e00 806c 0 16b 826b 10a8 6a 2068 822c c06c bbaa 6d 6655 406d ff00 6186 8286 4c2c 942c 290c c5a3
  //   13mem
  //   devices must drive rwds high when writing (ascts as per-byte mask)
  //   the memory chip toggles rwds during reads
endmodule

module Bit32_Side_Select (
  input  Side_Select,
  input  Side_Enable,
  input  [31:0] bit32In,
  output [31:0] Bit32_out
);

  wire and_1_out, and_2_out, not_1_out, or_1_out, or_2_out;

  Pull_Resistor pull_resistor_1 ();  // open: node
  and and_1 (and_1_out, ~Side_Select, Side_Enable);  // AND_Gate
  and and_2 (and_2_out, Side_Select, Side_Enable);
  not not_1 (not_1_out, Side_Enable);
  or or_1 (or_1_out, and_1_out, not_1_out);
  or or_2 (or_2_out, and_2_out, not_1_out);
  assign Bit32_out[15:0] = or_1_out ? bit32In[15:0] : 16'bz;  // Controlled_Buffer controlled_buffer_1
  assign Bit32_out[31:16] = or_2_out ? bit32In[31:16] : 16'bz;  // Controlled_Buffer controlled_buffer_2
  Pull_Resistor pull_resistor_2 (.node(Bit32_out[15:0]));
  Pull_Resistor pull_resistor_3 (.node(Bit32_out[31:16]));
endmodule

module Bit16_To_32_Side_Select_Extender (
  input  HighSide,
  input  [15:0] Bit16_In,
  output [31:0] Bit32_Out
);

  Demultiplexer #(.width(16)) demultiplexer_1 (
    .out0(Bit32_Out[15:0]), .out1(Bit32_Out[31:16]), .in(Bit16_In), .sel(HighSide));
endmodule

module Bit32_Toggle_Inverter_Toggle_Shift1 (
  input  [31:0] Bit32_In,
  input  Invert,
  input  Shift1,
  output [31:0] out_4
);

  wire multiplexer_1_out, multiplexer_2_out, multiplexer_3_out, multiplexer_4_out, multiplexer_5_out,
       multiplexer_6_out, multiplexer_7_out, multiplexer_8_out, multiplexer_9_out, multiplexer_10_out,
       multiplexer_11_out, multiplexer_12_out, multiplexer_13_out, multiplexer_14_out, multiplexer_15_out,
       multiplexer_16_out, multiplexer_17_out, multiplexer_18_out, multiplexer_19_out, multiplexer_20_out,
       multiplexer_21_out, multiplexer_22_out, multiplexer_23_out, multiplexer_24_out, multiplexer_25_out,
       multiplexer_26_out, multiplexer_27_out, multiplexer_28_out, multiplexer_29_out, multiplexer_30_out,
       multiplexer_31_out, multiplexer_32_out;

  Multiplexer multiplexer_1 (.in0(Bit32_In[0]), .in1(1'b0), .out(multiplexer_1_out), .sel(Shift1));
  Multiplexer multiplexer_2 (.in0(Bit32_In[1]), .in1(Bit32_In[0]), .out(multiplexer_2_out), .sel(Shift1));
  Multiplexer multiplexer_3 (.in0(Bit32_In[2]), .in1(Bit32_In[1]), .out(multiplexer_3_out), .sel(Shift1));
  Multiplexer multiplexer_4 (.in0(Bit32_In[3]), .in1(Bit32_In[2]), .out(multiplexer_4_out), .sel(Shift1));
  Multiplexer multiplexer_5 (.in0(Bit32_In[4]), .in1(Bit32_In[3]), .out(multiplexer_5_out), .sel(Shift1));
  Multiplexer multiplexer_6 (.in0(Bit32_In[5]), .in1(Bit32_In[4]), .out(multiplexer_6_out), .sel(Shift1));
  Multiplexer multiplexer_7 (.in0(Bit32_In[6]), .in1(Bit32_In[5]), .out(multiplexer_7_out), .sel(Shift1));
  Multiplexer multiplexer_8 (.in0(Bit32_In[7]), .in1(Bit32_In[6]), .out(multiplexer_8_out), .sel(Shift1));
  Multiplexer multiplexer_9 (.in0(Bit32_In[8]), .in1(Bit32_In[7]), .out(multiplexer_9_out), .sel(Shift1));
  Multiplexer multiplexer_10 (.in0(Bit32_In[9]), .in1(Bit32_In[8]), .out(multiplexer_10_out), .sel(Shift1));
  Multiplexer multiplexer_11 (.in0(Bit32_In[10]), .in1(Bit32_In[9]), .out(multiplexer_11_out), .sel(Shift1));
  Multiplexer multiplexer_12 (.in0(Bit32_In[11]), .in1(Bit32_In[10]), .out(multiplexer_12_out), .sel(Shift1));
  Multiplexer multiplexer_13 (.in0(Bit32_In[12]), .in1(Bit32_In[11]), .out(multiplexer_13_out), .sel(Shift1));
  Multiplexer multiplexer_14 (.in0(Bit32_In[13]), .in1(Bit32_In[12]), .out(multiplexer_14_out), .sel(Shift1));
  Multiplexer multiplexer_15 (.in0(Bit32_In[14]), .in1(Bit32_In[13]), .out(multiplexer_15_out), .sel(Shift1));
  Multiplexer multiplexer_16 (.in0(Bit32_In[15]), .in1(Bit32_In[14]), .out(multiplexer_16_out), .sel(Shift1));
  Multiplexer multiplexer_17 (.in0(Bit32_In[16]), .in1(Bit32_In[15]), .out(multiplexer_17_out), .sel(Shift1));
  Multiplexer multiplexer_18 (.in0(Bit32_In[17]), .in1(Bit32_In[16]), .out(multiplexer_18_out), .sel(Shift1));
  Multiplexer multiplexer_19 (.in0(Bit32_In[18]), .in1(Bit32_In[17]), .out(multiplexer_19_out), .sel(Shift1));
  Multiplexer multiplexer_20 (.in0(Bit32_In[19]), .in1(Bit32_In[18]), .out(multiplexer_20_out), .sel(Shift1));
  Multiplexer multiplexer_21 (.in0(Bit32_In[20]), .in1(Bit32_In[19]), .out(multiplexer_21_out), .sel(Shift1));
  Multiplexer multiplexer_22 (.in0(Bit32_In[21]), .in1(Bit32_In[20]), .out(multiplexer_22_out), .sel(Shift1));
  Multiplexer multiplexer_23 (.in0(Bit32_In[22]), .in1(Bit32_In[21]), .out(multiplexer_23_out), .sel(Shift1));
  Multiplexer multiplexer_24 (.in0(Bit32_In[23]), .in1(Bit32_In[22]), .out(multiplexer_24_out), .sel(Shift1));
  Multiplexer multiplexer_25 (.in0(Bit32_In[24]), .in1(Bit32_In[23]), .out(multiplexer_25_out), .sel(Shift1));
  Multiplexer multiplexer_26 (.in0(Bit32_In[25]), .in1(Bit32_In[24]), .out(multiplexer_26_out), .sel(Shift1));
  Multiplexer multiplexer_27 (.in0(Bit32_In[26]), .in1(Bit32_In[25]), .out(multiplexer_27_out), .sel(Shift1));
  Multiplexer multiplexer_28 (.in0(Bit32_In[27]), .in1(Bit32_In[26]), .out(multiplexer_28_out), .sel(Shift1));
  Multiplexer multiplexer_29 (.in0(Bit32_In[28]), .in1(Bit32_In[27]), .out(multiplexer_29_out), .sel(Shift1));
  Multiplexer multiplexer_30 (.in0(Bit32_In[29]), .in1(Bit32_In[28]), .out(multiplexer_30_out), .sel(Shift1));
  Multiplexer multiplexer_31 (.in0(Bit32_In[30]), .in1(Bit32_In[29]), .out(multiplexer_31_out), .sel(Shift1));
  Multiplexer multiplexer_32 (.in0(Bit32_In[31]), .in1(Bit32_In[30]), .out(multiplexer_32_out), .sel(Shift1));
  xor xor_1 (out_4[0], multiplexer_1_out, Invert);
  xor xor_2 (out_4[1], multiplexer_2_out, Invert);
  xor xor_3 (out_4[2], multiplexer_3_out, Invert);
  xor xor_4 (out_4[3], multiplexer_4_out, Invert);
  xor xor_5 (out_4[4], multiplexer_5_out, Invert);
  xor xor_6 (out_4[5], multiplexer_6_out, Invert);
  xor xor_7 (out_4[6], multiplexer_7_out, Invert);
  xor xor_8 (out_4[7], multiplexer_8_out, Invert);
  xor xor_9 (out_4[8], multiplexer_9_out, Invert);
  xor xor_10 (out_4[9], multiplexer_10_out, Invert);
  xor xor_11 (out_4[10], multiplexer_11_out, Invert);
  xor xor_12 (out_4[11], multiplexer_12_out, Invert);
  xor xor_13 (out_4[12], multiplexer_13_out, Invert);
  xor xor_14 (out_4[13], multiplexer_14_out, Invert);
  xor xor_15 (out_4[14], multiplexer_15_out, Invert);
  xor xor_16 (out_4[15], multiplexer_16_out, Invert);
  xor xor_17 (out_4[16], multiplexer_17_out, Invert);
  xor xor_18 (out_4[17], multiplexer_18_out, Invert);
  xor xor_19 (out_4[18], multiplexer_19_out, Invert);
  xor xor_20 (out_4[19], multiplexer_20_out, Invert);
  xor xor_21 (out_4[20], multiplexer_21_out, Invert);
  xor xor_22 (out_4[21], multiplexer_22_out, Invert);
  xor xor_23 (out_4[22], multiplexer_23_out, Invert);
  xor xor_24 (out_4[23], multiplexer_24_out, Invert);
  xor xor_25 (out_4[24], multiplexer_25_out, Invert);
  xor xor_26 (out_4[25], multiplexer_26_out, Invert);
  xor xor_27 (out_4[26], multiplexer_27_out, Invert);
  xor xor_28 (out_4[27], multiplexer_28_out, Invert);
  xor xor_29 (out_4[28], multiplexer_29_out, Invert);
  xor xor_30 (out_4[29], multiplexer_30_out, Invert);
  xor xor_31 (out_4[30], multiplexer_31_out, Invert);
  xor xor_32 (out_4[31], multiplexer_32_out, Invert);
endmodule

module core4 (
);

  wire and_1_out, and_2_out, and_6_out, and_7_out, and_8_out, and_9_out, and_10_out, and_11_out, and_12_out,
       and_13_out, and_14_out, and_15_out, and_16_out, and_17_out, and_18_out, and_19_out, and_20_out,
       and_21_out, and_23_out, and_24_out, and_25_out, and_26_out, and_27_out, and_28_out, and_29_out,
       and_30_out, and_31_out, and_32_out, and_33_out, and_34_out, and_35_out, and_36_out, and_37_out,
       and_38_out, and_39_out, and_40_out, bit3_latching_arbiter_1_ga, bit3_latching_arbiter_1_gb,
       Bit16_Path_A_Enable, Bit16_Path_B_Enable, Bit32_Assert_Enable, Bit32_Assert_Select, buffer_1_out,
       buffer_2_out, buffer_3_out, buffer_4_out, clock, condition_evaluator_1_condition_state,
       controlled_buffer_39_out, controlled_buffer_41_out, controlled_buffer_44_out, d_ff_1_q,
       data_cache_2_way_1_ram_read, data_cache_2_way_1_ram_write, data_cache_2_way_1_requesting_ram,
       data_cache_2_way_1_rwds, DCache_Stall, decoder_1_out0, decoder_1_out1, decoder_1_out2, decoder_1_out3,
       decoder_1_out8, decoder_1_out9, decoder_1_out10, decoder_1_out11, decoder_1_out12, decoder_1_out13,
       decoder_1_out14, decoder_1_out15, decoder_2_out0, decoder_2_out1, decoder_2_out2, decoder_3_out0,
       decoder_3_out1, decoder_3_out2, decoder_4_out0, decoder_4_out1, decoder_5_out0, decoder_5_out1,
       decoder_5_out2, decoder_5_out3, decoder_5_out8, decoder_5_out9, decoder_5_out10, decoder_5_out11,
       decoder_5_out12, decoder_5_out13, decoder_5_out14, decoder_5_out15, decoder_6_out0, decoder_6_out1,
       decoder_6_out2, decoder_6_out3, decoder_6_out8, decoder_6_out9, decoder_6_out10, decoder_6_out11,
       decoder_6_out12, decoder_6_out13, decoder_6_out14, decoder_6_out15, Fetch_Unit_Target,
       Hardware_Interrupt, ICache_Stall, Injecting_Instruction, instruction_cache_2_way_1_ram_read,
       instruction_cache_2_way_1_requesting_ram, mmu3_1_data_read, mmu3_1_data_two_byte, mmu3_1_data_write,
       mmu3_1_instruction_read, MMU_Fault, MMU_Stall, nor_1_out, nor_2_out, nor_3_out, not_1_out, not_2_out,
       not_3_out, or_1_out, or_3_out, or_4_out, or_5_out, or_6_out, or_7_out,
       psram_controller_2_1_data_moving, reset, undriven, undriven_4, undriven_5, undriven_6, undriven_7,
       undriven_10, undriven_14, undriven_15, UsingStartupRom;
  wire [1:0] Bit16_Path_A_Source_Select, Bit16_Path_B_Select, Bit16_Path_B_Source_Select,
       priority_encoder_1_out, undriven_9, Virtual_Mode;
  wire [3:0] alu4_1_p1, alu4_1_p6, bit_extender_9_out, BranchImmediate, mmu3_1_bit4_faults, multiplexer_8_out;
  wire [4:0] bit_extender_1_out, bit_extender_2_out, bit_extender_3_out, Read_Path_A, Read_Path_B,
       Write_Field_Execute, Write_Field_Write;
  wire [5:5] and_3_out;
  wire [6:0] Memory_Control;
  wire [7:0] controlled_buffer_43_out, data_cache_2_way_1_memory_byte, Memory_Stage_Context,
       psram_controller_2_1_bit8_out;
  wire [9:0] bit_extender_4_out, bit_extender_5_out, bit_extender_6_out, multiplexer_5_out;
  wire [14:0] Memory_Config_Memory;
  wire [14:4] Memory_Config_Execute;
  wire [15:0] alu4_1_p2, alu4_1_p3, alu4_1_p5, bit_extender_10_out, controlled_buffer_26_out,
       controlled_buffer_26_out_2, controlled_buffer_34_out, Current_Instruction,
       data_cache_2_way_1_bit16_to_core, FP_bit16_high, FP_bit16_low, GP_bit16_high, GP_bit16_low,
       ICache_Result, Injected_Instruction, InstructionImmediate, MO_bit16_high, MO_bit16_low,
       multiplexer_7_out, Next_Instruction, register_1_q, register_file_1_readline_a,
       register_file_1_readline_b, SP_bit16_high, SP_bit16_low, Startup_Rom_Value, undriven_3, undriven_12;
  wire [22:0] Readstage_out;
  wire [23:0] EXE_Control, undriven_11;
  wire [25:0] controlled_buffer_38_out, mmu3_1_bit26_data_address_out, mmu3_1_bit26_instruction_address_out,
       multiplexer_10_out, undriven_13;
  wire [25:1] Bit32_To_Fetch_Unit, Next_Instruction_Address;
  wire [31:0] adder_1_out, bit16_to_32_side_select_extender_1_bit32_out, bit32_side_select_1_bit32_out,
       bit32_toggle_inverter_toggle_shift1_1_out_4, bit_extender_8_out, controlled_buffer_1_out,
       controlled_buffer_28_out, FP_bit32_out, GP_bit32_out, Instruction_pointer_q, MO_bit32_out,
       register_3_q, SP_bit32_out, undriven_2, undriven_8;

  PLA #(.in_width(6), .out_width(23), .\table ("000000 00000000000000000000000\n000001 00000000000000000101000\n000010 00000000000000000101000\n000011 00000000000000000101000\n000100 00000000000000000101000\n000101 00000000000000000101000\n000110 00000000000000000101000\n000111 00000000000000000101000\n001000 00000000010000000101000\n001001 00000000000000000101000\n001010 00000000000000000101000\n001011 00000000100000010101000\n001100 00000000000000001101000\n001101 00000000100000010101000\n001110 00000000000000001101000\n001111 00000000000000001101000\n010000 00000000000000001101000\n010001 00000000000000001101000\n010010 00000000000000000101000\n010011 00000000000000000101000\n010100 00000000000000000101000\n010101 00000000111001010101000\n010110 00000000111001010101000\n010111 00000000111001010101000\n011000 00000000111001010101000\n011001 00000000000000000000000\n011010 00001100000110100001000\n011011 00000000000000000011000\n011100 00000010010011010101000\n011101 00000000000111001101000\n011110 00000100000111000101000\n011111 01011010010011000100000\n100000 01001100000011000111000\n100001 01001100000010000101000\n100010 00111000100010000101000\n100011 00111000100010010101000\n100100 00000000111001010101000\n100101 00000000000110100001101\n100110 01000001000000010100000\n100111 01000001000000010100000\n101000 01000001010000010100000\n101001 01000001010000010100000\n101010 11000000001010000001000\n101011 11000000000010000001000\n101100 00000000000110000101000\n101101 00000100000010000001000\n101110 00000000000000000000000\n101111 00000010000110000001000\n110000 00001100000010000101000\n110001 00000000000000000000000\n110010 00000000000000000000000\n110011 00000000000000000000000\n110100 00000000000000000000000\n110101 00000000000000000000000\n110110 00000000000000000000000\n110111 00000000000000000000000\n111000 00000000000000000000000\n111001 00000000000000000000000\n111010 00000000000000000000000\n111011 00000000000000000000000\n111100 00000000000000000000000\n111101 00000000000000000000000\n111110 00000000000000000000000\n111111 01000001000000000000000")) Readstage (
    .in(Current_Instruction[15:10]),
    .out({Readstage_out[22:8], Bit16_Path_B_Select, Bit16_Path_B_Enable, Bit16_Path_A_Enable, Readstage_out[3:0]}));
  PLA #(.in_width(6), .out_width(24), .\table ("000000 000000000000000000000000\n000001 000000100000001000000000\n000010 000000100001001000000000\n000011 000000100010001000000000\n000100 000000100011001000000000\n000101 000000100100001000000000\n000110 000000100101001000000000\n000111 000000100110001000000000\n001000 000000100111001000000000\n001001 000000101000001000000000\n001010 000000101001001000000000\n001011 000000100000001000000000\n001100 000000100000001000000000\n001101 000000100010001000000000\n001110 000000100010001000000000\n001111 000000101010001000000000\n010000 000000101011001000000000\n010001 000000101100001000000000\n010010 000000101010001000000000\n010011 000000101011001000000000\n010100 000000101100001000000000\n010101 000000100110001000000000\n010110 000000100111001000000000\n010111 000000101001001000000000\n011000 000000101000001000000000\n011001 000000000000000000000000\n011010 000001000000100000001000\n011011 000000000000100000000000\n011100 010000000000000000000001\n011101 010000000000000000000001\n011110 010000000000000000000001\n011111 000000000000010000000001\n100000 000000000000010000000001\n100001 000000000000010000000001\n100010 000000010000010000001010\n100011 010000000000000000001001\n100100 001000000000100000000000\n100101 000001000000100000001000\n100110 110010010000000000000001\n100111 110010000000000000000001\n101000 110110010000000000000001\n101001 110110000000000000000001\n101010 100010000000000000000001\n101011 100110000000000000000001\n101100 000000101101001000000000\n101101 000000000000100000000001\n101110 000000000000000000000000\n101111 000000000000000000000001\n110000 000000000000010000000001\n110001 000000000000000000000000\n110010 000000000000000000000000\n110011 000000000000000000000000\n110100 000000000000000000000000\n110101 000000000000000000000000\n110110 000000000000000000000000\n110111 000000000000000000000000\n111000 000000000000000000000000\n111001 000000000000000000000000\n111010 000000000000000000000000\n111011 000000000000000000000000\n111100 000000000000000000000000\n111101 000000000000000000000000\n111110 000000000000000000000000\n111111 000010000000000000000010")) EXEstage (
    .in(Current_Instruction[15:10]), .out(EXE_Control));
  PLA #(.in_width(6), .out_width(7), .\table ("000000 0000000\n000001 0010000\n000010 0010000\n000011 0010000\n000100 0010000\n000101 0010000\n000110 0010000\n000111 0010000\n001000 0001000\n001001 0010000\n001010 0010000\n001011 0010000\n001100 0010000\n001101 0010000\n001110 0010000\n001111 0010000\n010000 0010000\n010001 0010000\n010010 0010000\n010011 0010000\n010100 0010000\n010101 0010000\n010110 0010000\n010111 0010000\n011000 0010000\n011001 0000000\n011010 0010000\n011011 0010000\n011100 1101000\n011101 1101000\n011110 1101000\n011111 1101100\n100000 1100100\n100001 1100100\n100010 0100110\n100011 0101010\n100100 0010000\n100101 0010000\n100110 0000000\n100111 0000000\n101000 0000000\n101001 0000000\n101010 0000000\n101011 0000000\n101100 0000000\n101101 0100001\n101110 0000000\n101111 1101000\n110000 1100100\n110001 0000000\n110010 0000000\n110011 0000000\n110100 0000000\n110101 0000000\n110110 0000000\n110111 0000000\n111000 0000000\n111001 0000000\n111010 0000000\n111011 0000000\n111100 0000000\n111101 0000000\n111110 0000000\n111111 0000000")) MemoryStage (
    .in(Current_Instruction[15:10]),
    .out({Memory_Control[6], Memory_Config_Execute[14:11], Memory_Control[1:0]}));
  PLA #(.in_width(6), .out_width(3), .\table ("000000 000\n000001 001\n000010 001\n000011 001\n000100 001\n000101 001\n000110 001\n000111 001\n001000 001\n001001 001\n001010 001\n001011 001\n001100 001\n001101 001\n001110 001\n001111 001\n010000 001\n010001 001\n010010 001\n010011 001\n010100 001\n010101 001\n010110 001\n010111 001\n011000 001\n011001 000\n011010 000\n011011 001\n011100 001\n011101 001\n011110 001\n011111 000\n100000 000\n100001 000\n100010 010\n100011 011\n100100 001\n100101 000\n100110 000\n100111 000\n101000 000\n101001 000\n101010 000\n101011 000\n101100 001\n101101 000\n101110 000\n101111 001\n110000 000\n110001 000\n110010 000\n110011 000\n110100 000\n110101 000\n110110 000\n110111 000\n111000 000\n111001 000\n111010 000\n111011 000\n111100 000\n111101 000\n111110 000\n111111 000")) WriteStage (.in(Current_Instruction[15:10]));  // open: out
  Multiplexer #(.select(2), .width(5)) multiplexer_1 (
    .in0(bit_extender_2_out), .in1(Current_Instruction[4:0]), .in2(bit_extender_1_out),
    .in3({BranchImmediate, Current_Instruction[5]}), .out(Read_Path_B));  // open: sel
  and and_1 (and_1_out, ~Readstage_out[22], Readstage_out[21]);  // AND_Gate
  Multiplexer #(.select(2), .width(5)) multiplexer_2 (
    .in0(bit_extender_3_out), .in1(bit_extender_2_out), .in2(Current_Instruction[4:0]),
    .in3(bit_extender_1_out), .out(Read_Path_A));  // open: sel
  Multiplexer #(.select(2), .width(16)) multiplexer_3 (
    .in0(ICache_Result), .in1(Startup_Rom_Value), .in2(Injected_Instruction), .in3({16{1'b0}}),
    .out(Next_Instruction), .sel(priority_encoder_1_out));
  Priority_Encoder #(.select(2)) priority_encoder_1 (
    .in0(not_1_out), .in1(UsingStartupRom), .in2(or_1_out), .in3(Fetch_Unit_Target),
    .out(priority_encoder_1_out));
  not not_1 (not_1_out, UsingStartupRom);
  or or_1 (or_1_out, Injecting_Instruction, Hardware_Interrupt);
  // OR_Gate or_2 has open pins: in0=and_1_out, in1=and_2_out, out=open
  buf and_2 (and_2_out, Readstage_out[21]);  // AND_Gate
  assign bit_extender_1_out = {{1{1'b0}}, BranchImmediate};  // Bit_Extender bit_extender_1
  Multiplexer #(.select(2), .width(5)) multiplexer_4 (
    .in0(bit_extender_1_out), .in1({BranchImmediate, Current_Instruction[5]}), .in2(bit_extender_3_out),
    .in3(Current_Instruction[4:0]), .out(Write_Field_Execute));  // open: sel
  assign bit_extender_2_out = {{2{1'b0}}, Current_Instruction[2:0]};  // Bit_Extender bit_extender_2
  assign bit_extender_3_out = {{2{1'b0}}, Current_Instruction[5:3]};  // Bit_Extender bit_extender_3
  Register #(.trigger("falling"), .width(16)) register_1 (
    .D(Next_Instruction), .en(1'b1), .clk(clock), .Q(register_1_q), .clr(reset));
  nor nor_1 (nor_1_out, ICache_Stall, DCache_Stall, Hardware_Interrupt);
  and and_3 (and_3_out[5], ~Readstage_out[16], Current_Instruction[5]);  // AND_Gate
  nor nor_2 (nor_2_out, Injecting_Instruction, ICache_Stall, DCache_Stall, Hardware_Interrupt, Hardware_Interrupt);
  Register #(.width(16)) register_2 (
    .D(register_1_q), .en(nor_1_out), .clk(clock),
    .Q({Current_Instruction[15:10], BranchImmediate, Current_Instruction[5:0]}), .clr(reset));
  assign bit_extender_4_out = {{4{1'b0}}, {and_3_out[5], Current_Instruction[4:0]}};  // Bit_Extender bit_extender_4
  assign bit_extender_5_out = {{7{1'b0}}, Current_Instruction[2:0]};  // Bit_Extender bit_extender_5
  assign bit_extender_6_out = {{6{1'b0}}, BranchImmediate};  // Bit_Extender bit_extender_6
  Multiplexer #(.select(2), .width(10)) multiplexer_5 (
    .in0({BranchImmediate, Current_Instruction[5:0]}), .in1(bit_extender_4_out), .in2(bit_extender_5_out),
    .in3(bit_extender_6_out), .out(multiplexer_5_out));  // open: sel
  Counter #(.max('h1ffffff), .width(25)) counter_1 (
    .clr(reset), .load(Fetch_Unit_Target), .up(1'b1), .count(nor_2_out), .clk(clock),
    .D(Bit32_To_Fetch_Unit), .Q(Next_Instruction_Address));  // open: carry
  Multiplexer multiplexer_6 (
    .in0(Memory_Control[1]), .in1(BranchImmediate[3]), .out(Memory_Config_Execute[10]),
    .sel(Memory_Control[6]));
  assign InstructionImmediate = {{6{1'b0}}, multiplexer_5_out};  // Bit_Extender bit_extender_7
  and and_4 (Memory_Config_Execute[5], Memory_Control[0], Current_Instruction[5]);
  and and_5 (Memory_Config_Execute[4], Memory_Control[0], ~Current_Instruction[5]);  // AND_Gate
  and and_6 (and_6_out, undriven, ~Write_Field_Write[4]);  // AND_Gate
  and and_7 (and_7_out, Write_Field_Write[4], undriven);
  Decoder #(.select(4)) decoder_1 (
    .out0(decoder_1_out0), .out1(decoder_1_out1), .out2(decoder_1_out2), .out3(decoder_1_out3),
    .out8(decoder_1_out8), .out9(decoder_1_out9), .out10(decoder_1_out10), .out11(decoder_1_out11),
    .out12(decoder_1_out12), .out13(decoder_1_out13), .out14(decoder_1_out14), .out15(decoder_1_out15),
    .sel(Write_Field_Write[3:0]), .en(and_6_out));  // open: out4, out5, out6, out7
  Decoder #(.select(2)) decoder_2 (
    .out0(decoder_2_out0), .out1(decoder_2_out1), .out2(decoder_2_out2), .sel(Bit16_Path_B_Source_Select),
    .en(Bit16_Path_A_Enable));  // open: out3
  Decoder #(.select(2)) decoder_3 (
    .out0(decoder_3_out0), .out1(decoder_3_out1), .out2(decoder_3_out2), .sel(Bit16_Path_A_Source_Select),
    .en(Bit16_Path_B_Enable));  // open: out3
  Decoder decoder_4 (.out0(decoder_4_out0), .out1(decoder_4_out1), .sel(Bit32_Assert_Select), .en(Bit32_Assert_Enable));
  and and_8 (and_8_out, Read_Path_B[4], decoder_2_out0);
  and and_9 (and_9_out, Read_Path_A[4], decoder_3_out0);
  and and_10 (and_10_out, ~Read_Path_B[4], decoder_2_out0);  // AND_Gate
  and and_11 (and_11_out, ~Read_Path_A[4], decoder_3_out0);  // AND_Gate
  Register #(.trigger("falling"), .width(32)) register_3 (
    .D(bit_extender_8_out), .en(undriven_6), .clk(undriven_7), .Q(register_3_q));  // open: clr
  assign bit_extender_8_out = {{6{Next_Instruction_Address[25]}}, {Next_Instruction_Address, 1'b0}};  // Bit_Extender bit_extender_8
  Register #(.trigger("falling"), .width(32)) Instruction_pointer (
    .D(register_3_q), .en(undriven_6), .clk(undriven_7), .Q(Instruction_pointer_q));  // open: clr
  Bit32_Split_Register MO (
    .F_Write(decoder_1_out0), .L_Write(decoder_1_out8), .H_Write(decoder_1_out12), .Bit32_In(undriven_2),
    .Bit16_In(undriven_3), .Clock(undriven_4), .Reset(undriven_5), .Bit32_Out(MO_bit32_out),
    .Bit16_Low(MO_bit16_low), .Bit16_High(MO_bit16_high));
  Bit32_Split_Register SP (
    .F_Write(decoder_1_out1), .L_Write(decoder_1_out9), .H_Write(decoder_1_out13), .Bit32_In(undriven_2),
    .Bit16_In(undriven_3), .Clock(undriven_4), .Reset(undriven_5), .Bit32_Out(SP_bit32_out),
    .Bit16_Low(SP_bit16_low), .Bit16_High(SP_bit16_high));
  Bit32_Split_Register FP (
    .F_Write(decoder_1_out2), .L_Write(decoder_1_out10), .H_Write(decoder_1_out14), .Bit32_In(undriven_2),
    .Bit16_In(undriven_3), .Clock(undriven_4), .Reset(undriven_5), .Bit32_Out(FP_bit32_out),
    .Bit16_Low(FP_bit16_low), .Bit16_High(FP_bit16_high));
  Bit32_Split_Register GP (
    .F_Write(decoder_1_out3), .L_Write(decoder_1_out11), .H_Write(decoder_1_out15), .Bit32_In(undriven_2),
    .Bit16_In(undriven_3), .Clock(undriven_4), .Reset(undriven_5), .Bit32_Out(GP_bit32_out),
    .Bit16_Low(GP_bit16_low), .Bit16_High(GP_bit16_high));
  Register_File register_file_1 (
    .Write_Data(undriven_3), .Read_Address_B(Read_Path_B[3:0]), .Read_B_Enable(and_10_out),
    .Read_Address_A(Read_Path_A[3:0]), .Read_A_Enable(and_11_out), .Write_Address(Write_Field_Write[3:0]),
    .Write_Enable(and_7_out), .Clock(undriven_4), .Clear_All_Registers(undriven_5),
    .ReadLine_A(register_file_1_readline_a), .ReadLine_B(register_file_1_readline_b));
  assign controlled_buffer_1_out = or_3_out ? MO_bit32_out : 32'bz;  // Controlled_Buffer controlled_buffer_1
  and and_12 (and_12_out, decoder_5_out0, nor_3_out);
  or or_3 (or_3_out, and_12_out, buffer_4_out, and_13_out);
  and and_13 (and_13_out, decoder_6_out0, ~and_20_out, nor_3_out);  // AND_Gate
  assign register_file_1_readline_a = decoder_5_out8 ? MO_bit16_low : 16'bz;  // Controlled_Buffer controlled_buffer_2
  assign register_file_1_readline_a = decoder_5_out12 ? MO_bit16_high : 16'bz;  // Controlled_Buffer controlled_buffer_3
  assign register_file_1_readline_b = decoder_6_out8 ? MO_bit16_low : 16'bz;  // Controlled_Buffer controlled_buffer_4
  assign register_file_1_readline_b = decoder_6_out12 ? MO_bit16_high : 16'bz;  // Controlled_Buffer controlled_buffer_5
  assign controlled_buffer_1_out = or_4_out ? SP_bit32_out : 32'bz;  // Controlled_Buffer controlled_buffer_6
  and and_14 (and_14_out, decoder_5_out1, nor_3_out);
  or or_4 (or_4_out, and_14_out, and_15_out);
  and and_15 (and_15_out, decoder_6_out1, ~and_20_out, nor_3_out);  // AND_Gate
  assign register_file_1_readline_a = decoder_5_out9 ? SP_bit16_low : 16'bz;  // Controlled_Buffer controlled_buffer_7
  assign register_file_1_readline_a = decoder_5_out13 ? SP_bit16_high : 16'bz;  // Controlled_Buffer controlled_buffer_8
  assign register_file_1_readline_b = decoder_6_out9 ? SP_bit16_low : 16'bz;  // Controlled_Buffer controlled_buffer_9
  assign register_file_1_readline_b = decoder_6_out13 ? SP_bit16_high : 16'bz;  // Controlled_Buffer controlled_buffer_10
  assign controlled_buffer_1_out = or_5_out ? FP_bit32_out : 32'bz;  // Controlled_Buffer controlled_buffer_11
  and and_16 (and_16_out, decoder_5_out2, nor_3_out);
  or or_5 (or_5_out, and_16_out, and_17_out);
  and and_17 (and_17_out, decoder_6_out2, ~and_20_out, nor_3_out);  // AND_Gate
  assign register_file_1_readline_a = decoder_5_out10 ? FP_bit16_low : 16'bz;  // Controlled_Buffer controlled_buffer_12
  assign register_file_1_readline_a = decoder_5_out14 ? FP_bit16_high : 16'bz;  // Controlled_Buffer controlled_buffer_13
  assign register_file_1_readline_b = decoder_6_out10 ? FP_bit16_low : 16'bz;  // Controlled_Buffer controlled_buffer_14
  assign register_file_1_readline_b = decoder_6_out14 ? FP_bit16_high : 16'bz;  // Controlled_Buffer controlled_buffer_15
  assign controlled_buffer_1_out = or_6_out ? GP_bit32_out : 32'bz;  // Controlled_Buffer controlled_buffer_16
  and and_18 (and_18_out, decoder_5_out3, nor_3_out);
  or or_6 (or_6_out, and_18_out, and_19_out);
  and and_19 (and_19_out, decoder_6_out3, ~and_20_out, nor_3_out);  // AND_Gate
  assign register_file_1_readline_a = decoder_5_out11 ? GP_bit16_low : 16'bz;  // Controlled_Buffer controlled_buffer_17
  assign register_file_1_readline_a = decoder_5_out15 ? GP_bit16_high : 16'bz;  // Controlled_Buffer controlled_buffer_18
  assign register_file_1_readline_b = decoder_6_out11 ? GP_bit16_low : 16'bz;  // Controlled_Buffer controlled_buffer_19
  assign register_file_1_readline_b = decoder_6_out15 ? GP_bit16_high : 16'bz;  // Controlled_Buffer controlled_buffer_20
  assign controlled_buffer_1_out = buffer_3_out ? Instruction_pointer_q : 32'bz;  // Controlled_Buffer controlled_buffer_21
  and and_20 (and_20_out, and_9_out, ~Read_Path_A[3], ~Read_Path_A[2]);  // AND_Gate
  nor nor_3 (nor_3_out, decoder_4_out1, decoder_4_out0);
  buf buffer_1 (buffer_1_out, decoder_4_out1);
  buf buffer_2 (buffer_2_out, decoder_4_out0);
  buf buffer_3 (buffer_3_out, buffer_1_out);
  buf buffer_4 (buffer_4_out, buffer_2_out);
  Decoder #(.select(4)) decoder_5 (
    .out0(decoder_5_out0), .out1(decoder_5_out1), .out2(decoder_5_out2), .out3(decoder_5_out3),
    .out8(decoder_5_out8), .out9(decoder_5_out9), .out10(decoder_5_out10), .out11(decoder_5_out11),
    .out12(decoder_5_out12), .out13(decoder_5_out13), .out14(decoder_5_out14), .out15(decoder_5_out15),
    .sel(Read_Path_A[3:0]), .en(and_9_out));  // open: out4, out5, out6, out7
  Decoder #(.select(4)) decoder_6 (
    .out0(decoder_6_out0), .out1(decoder_6_out1), .out2(decoder_6_out2), .out3(decoder_6_out3),
    .out8(decoder_6_out8), .out9(decoder_6_out9), .out10(decoder_6_out10), .out11(decoder_6_out11),
    .out12(decoder_6_out12), .out13(decoder_6_out13), .out14(decoder_6_out14), .out15(decoder_6_out15),
    .sel(Read_Path_B[3:0]), .en(and_8_out));  // open: out4, out5, out6, out7
  and and_21 (and_21_out, undriven_11[18], undriven_9[0]);
  Multiplexer #(.width(16)) multiplexer_7 (
    .in0(alu4_1_p2), .in1(alu4_1_p3), .out(multiplexer_7_out), .sel(undriven_11[22]));
  not not_2 (not_2_out, undriven_9[0]);
  and and_22 (Fetch_Unit_Target, undriven_11[19], or_7_out);
  or or_7 (or_7_out, ~undriven_11[20], condition_evaluator_1_condition_state);  // OR_Gate
  Bit32_Side_Select bit32_side_select_1 (
    .Side_Select(not_2_out), .Side_Enable(undriven_9[1]), .bit32In(undriven_8),
    .Bit32_out(bit32_side_select_1_bit32_out));
  Bit16_To_32_Side_Select_Extender bit16_to_32_side_select_extender_1 (
    .HighSide(and_21_out), .Bit16_In(multiplexer_7_out),
    .Bit32_Out(bit16_to_32_side_select_extender_1_bit32_out));
  assign register_file_1_readline_a = decoder_3_out1 ? InstructionImmediate : 16'bz;  // Controlled_Buffer controlled_buffer_22
  assign register_file_1_readline_b = decoder_2_out1 ? InstructionImmediate : 16'bz;  // Controlled_Buffer controlled_buffer_23
  assign register_file_1_readline_a = decoder_3_out2 ? Next_Instruction : 16'bz;  // Controlled_Buffer controlled_buffer_24
  assign register_file_1_readline_b = decoder_2_out2 ? Next_Instruction : 16'bz;  // Controlled_Buffer controlled_buffer_25
  Bit32_Toggle_Inverter_Toggle_Shift1 bit32_toggle_inverter_toggle_shift1_1 (
    .Bit32_In(bit16_to_32_side_select_extender_1_bit32_out), .Invert(undriven_11[16]),
    .Shift1(undriven_11[23]), .out_4(bit32_toggle_inverter_toggle_shift1_1_out_4));
  Bit_Extender #(.in_width(16), .out_width(4), .\type ("zero")) bit_extender_9 (
    .in(alu4_1_p2), .out(bit_extender_9_out));
  D_Flip_Flop d_ff_1 (.D(Fetch_Unit_Target), .Q(d_ff_1_q));  // open: clk, Qn, preset, reset
  Adder #(.width(32)) adder_1 (
    .a(bit32_side_select_1_bit32_out), .b(bit32_toggle_inverter_toggle_shift1_1_out_4), .out(adder_1_out),
    .cin(undriven_11[16]));  // open: cout
  // OR_Gate or_8 has open pins: in0=Fetch_Unit_Target, in1=d_ff_1_q, out=open
  // ALU4 alu4_1: pin names not known; wires that end beside it: alu4_1_p1[0], alu4_1_p2, alu4_1_p3, undriven_11[15:12], alu4_1_p5, alu4_1_p6[0], alu4_1_p6[1], alu4_1_p6[2], alu4_1_p6[3]
  Multiplexer #(.width(4)) multiplexer_8 (
    .in0(alu4_1_p6), .in1(bit_extender_9_out), .out(multiplexer_8_out), .sel(undriven_10));
  Register #(.width(4)) register_4 (.D(multiplexer_8_out), .en(undriven_11[17]), .Q(alu4_1_p1));  // open: clk, clr
  assign {controlled_buffer_26_out_2, controlled_buffer_26_out} = undriven_11[4] ? bit32_side_select_1_bit32_out : 32'bz;  // Controlled_Buffer controlled_buffer_26
  assign {controlled_buffer_26_out_2, controlled_buffer_26_out} = undriven_11[3] ? adder_1_out : 32'bz;  // Controlled_Buffer controlled_buffer_27
  assign controlled_buffer_28_out = undriven_11[1] ? bit32_side_select_1_bit32_out : 32'bz;  // Controlled_Buffer controlled_buffer_28
  assign controlled_buffer_28_out = undriven_11[0] ? adder_1_out : 32'bz;  // Controlled_Buffer controlled_buffer_29
  assign controlled_buffer_26_out_2 = undriven_11[2] ? alu4_1_p2 : 16'bz;  // Controlled_Buffer controlled_buffer_30
  assign controlled_buffer_26_out_2 = undriven_11[6] ? alu4_1_p3 : 16'bz;  // Controlled_Buffer controlled_buffer_31
  assign controlled_buffer_26_out = undriven_11[5] ? alu4_1_p2 : 16'bz;  // Controlled_Buffer controlled_buffer_32
  assign controlled_buffer_26_out = undriven_11[7] ? alu4_1_p3 : 16'bz;  // Controlled_Buffer controlled_buffer_33
  assign controlled_buffer_34_out = undriven_11[11] ? alu4_1_p2 : 16'bz;  // Controlled_Buffer controlled_buffer_34
  assign controlled_buffer_34_out = undriven_11[10] ? alu4_1_p3 : 16'bz;  // Controlled_Buffer controlled_buffer_35
  assign controlled_buffer_34_out = undriven_11[9] ? alu4_1_p5 : 16'bz;  // Controlled_Buffer controlled_buffer_36
  assign controlled_buffer_34_out = undriven_11[8] ? bit_extender_10_out : 16'bz;  // Controlled_Buffer controlled_buffer_37
  assign bit_extender_10_out = {{12{1'b0}}, alu4_1_p1};  // Bit_Extender bit_extender_10
  Multiplexer multiplexer_9 (.in1(condition_evaluator_1_condition_state), .sel(undriven_11[21]));  // open: in0, out
  Condition_Evaluator condition_evaluator_1 (
    .Bit4_Flags(alu4_1_p1), .Condition_State(condition_evaluator_1_condition_state));  // open: Bit4_Condition_Selector
  and and_23 (and_23_out, Memory_Config_Memory[5], Memory_Config_Memory[6]);
  and and_24 (and_24_out, Memory_Config_Memory[5], Memory_Config_Memory[7]);
  and and_25 (and_25_out, Memory_Config_Memory[5], Memory_Config_Memory[8]);
  and and_26 (and_26_out, Memory_Config_Memory[5], Memory_Config_Memory[9]);
  and and_27 (and_27_out, Memory_Config_Memory[14], ~Virtual_Mode[0]);  // AND_Gate
  and and_28 (and_28_out, Virtual_Mode[0], Memory_Config_Memory[14]);
  not not_3 (not_3_out, UsingStartupRom);
  and and_29 (and_29_out, Virtual_Mode[1], ~not_3_out);  // AND_Gate
  and and_30 (and_30_out, Virtual_Mode[1], not_3_out);
  and and_31 (and_31_out, Memory_Config_Memory[9], Memory_Config_Memory[8], Memory_Config_Memory[4]);
  Multiplexer #(.width(26)) multiplexer_10 (
    .in0({Next_Instruction_Address, 1'b0}), .in1(undriven_13), .out(multiplexer_10_out), .sel(and_31_out));
  and and_32 (and_32_out, Memory_Config_Memory[7], Memory_Config_Memory[9], Memory_Config_Memory[8], Memory_Config_Memory[4]);
  and and_33 (and_33_out, ~Memory_Config_Memory[7], Memory_Config_Memory[9], Memory_Config_Memory[8], Memory_Config_Memory[4]);  // AND_Gate
  and and_34 (and_34_out, ~Memory_Config_Memory[8], ~Memory_Config_Memory[9], Memory_Config_Memory[7], Memory_Config_Memory[4]);  // AND_Gate
  and and_35 (and_35_out, Memory_Config_Memory[8], ~Memory_Config_Memory[9], Memory_Config_Memory[7], Memory_Config_Memory[4]);  // AND_Gate
  and and_36 (and_36_out, ~Memory_Config_Memory[8], ~Memory_Config_Memory[9], ~Memory_Config_Memory[7], Memory_Config_Memory[4]);  // AND_Gate
  and and_37 (and_37_out, Memory_Config_Memory[8], ~Memory_Config_Memory[9], ~Memory_Config_Memory[7], Memory_Config_Memory[4]);  // AND_Gate
  MMU3 mmu3_1 (
    .Bit8_Context_Id(Memory_Stage_Context), .Bit4_Lower_Flag_Mask(Memory_Config_Memory[3:0]),
    .Lower_Flag_Mask_Enable(and_26_out), .Bit14_Target_Page(undriven_12[13:0]),
    .Invalidate_Target_Page(and_25_out), .Bit3_Target_Translation_Page(undriven_12[13:11]),
    .Invalidate_Translation_Page(and_24_out), .Invalidate_All(and_23_out),
    .Bit27_Instruction_Address(multiplexer_10_out), .Instruction_Translate(and_30_out),
    .Instruction_Passthrough(and_29_out), .Bit27_Data_Address(undriven_13), .Data_Translate(and_28_out),
    .Data_Passthrough(and_27_out), .Two_Byte_Operation(Memory_Config_Memory[10]),
    .Data_Direction(Memory_Config_Memory[11]), .Bit16_From_Data_Cache(data_cache_2_way_1_bit16_to_core),
    .Bit4_Faults(mmu3_1_bit4_faults), .Is_Fault(MMU_Fault), .Stall(MMU_Stall),
    .Bit26_Instruction_Address_Out(mmu3_1_bit26_instruction_address_out),
    .Instruction_Read(mmu3_1_instruction_read), .Bit26_Data_Address_Out(mmu3_1_bit26_data_address_out),
    .Data_Read(mmu3_1_data_read), .Data_Write(mmu3_1_data_write), .Data_Two_Byte(mmu3_1_data_two_byte));  // open: Enable, Reset, Clock
  Instruction_Cache_2_Way instruction_cache_2_way_1 (
    .Read(mmu3_1_instruction_read), .Two_Byte_Operation(mmu3_1_instruction_read),
    .Invalidate_Address(and_32_out), .Invalidate_Line(and_33_out), .Set(Memory_Config_Memory[6]),
    .Bit26_Address(mmu3_1_bit26_instruction_address_out), .Bit8_From_Memory(psram_controller_2_1_bit8_out),
    .Ram_Data_Moving(and_40_out), .Clock(undriven_14), .Reset(undriven_15),
    .Ram_Read(instruction_cache_2_way_1_ram_read), .Requesting_Ram(instruction_cache_2_way_1_requesting_ram));  // open: Bit16_To_Core, RWDS
  Data_Cache_2_Way data_cache_2_way_1 (
    .Read(mmu3_1_data_read), .Write(mmu3_1_data_write), .Two_Byte_Operation(mmu3_1_data_two_byte),
    .Flush_Address(and_34_out), .Invalidate_Address(and_35_out), .Flush_Line(and_36_out),
    .Invalidate_Line(and_37_out), .Set(Memory_Config_Memory[6]),
    .Bit26_Address(mmu3_1_bit26_data_address_out), .Bit16_Data(undriven_12),
    .Bit8_From_Memory(psram_controller_2_1_bit8_out), .Ram_Data_Moving(and_39_out), .Clock(undriven_14),
    .Reset(undriven_15), .Bit16_To_Core(data_cache_2_way_1_bit16_to_core),
    .Ram_Write(data_cache_2_way_1_ram_write), .Ram_Read(data_cache_2_way_1_ram_read),
    .Requesting_Ram(data_cache_2_way_1_requesting_ram), .Memory_Byte(data_cache_2_way_1_memory_byte),
    .RWDS(data_cache_2_way_1_rwds));
  and and_38 (and_38_out, data_cache_2_way_1_ram_write, bit3_latching_arbiter_1_gb);
  assign controlled_buffer_38_out = bit3_latching_arbiter_1_ga ? mmu3_1_bit26_instruction_address_out : 26'bz;  // Controlled_Buffer controlled_buffer_38
  assign controlled_buffer_39_out = bit3_latching_arbiter_1_ga ? instruction_cache_2_way_1_ram_read : 1'bz;  // Controlled_Buffer controlled_buffer_39
  assign controlled_buffer_38_out = bit3_latching_arbiter_1_gb ? mmu3_1_bit26_data_address_out : 26'bz;  // Controlled_Buffer controlled_buffer_40
  assign controlled_buffer_41_out = bit3_latching_arbiter_1_gb ? data_cache_2_way_1_ram_write : 1'bz;  // Controlled_Buffer controlled_buffer_41
  assign controlled_buffer_39_out = bit3_latching_arbiter_1_gb ? data_cache_2_way_1_ram_read : 1'bz;  // Controlled_Buffer controlled_buffer_42
  assign controlled_buffer_43_out = bit3_latching_arbiter_1_gb ? data_cache_2_way_1_memory_byte : 8'bz;  // Controlled_Buffer controlled_buffer_43
  assign controlled_buffer_44_out = and_38_out ? data_cache_2_way_1_rwds : 1'bz;  // Controlled_Buffer controlled_buffer_44
  Bit3_Latching_Arbiter bit3_latching_arbiter_1 (
    .Reset(undriven_15), .Clock(undriven_14), .RA(instruction_cache_2_way_1_requesting_ram),
    .RB(data_cache_2_way_1_requesting_ram), .GA(bit3_latching_arbiter_1_ga), .GB(bit3_latching_arbiter_1_gb));  // open: RC, GC
  and and_39 (and_39_out, psram_controller_2_1_data_moving, bit3_latching_arbiter_1_ga);
  and and_40 (and_40_out, psram_controller_2_1_data_moving, bit3_latching_arbiter_1_gb);
  PSRAM_Controller_2 psram_controller_2_1 (
    .Clock(undriven_14), .Reset(undriven_15), .Read(controlled_buffer_39_out),
    .Write(controlled_buffer_41_out), .Bit8_Data(controlled_buffer_43_out),
    .Bit26_Address(controlled_buffer_38_out), .RWDS_In(controlled_buffer_44_out),
    .Bit8_Out(psram_controller_2_1_bit8_out), .Data_Moving(psram_controller_2_1_data_moving));  // open: RWDS_Out, Setup

  // Other names for the same wires on the sheet: Bit16_Path_A_Select = Bit16_Path_A_Enable;
  //   Memory_Config_Execute (some bits) = {BranchImmediate, Current_Instruction[3:0]};
  //   Current_Instruction[9:6] = BranchImmediate; Opcode[5:0] = Current_Instruction[15:10];
  //   Mem_Read_Hazard_Stall = Hardware_Interrupt; Memory_Control[5:2] = Memory_Config_Execute[14:11]

  // Notes on the sheet:
  //   note 1.3
  //   N1
  //   N2
  //   N3
  //   2A
  //   clarification in note 1.2
  //   Write Field Select
  //   Read Path A
  //   Read Path B
  //   2B
  //   disable 6 msb to b 5 (NOTE 1.1)
  //   0=m, 1=i
  //   B DISABLE IF A
  //   IF 00,01,or 10 then relative 32 needs to be asserted
  //   memory assert and instruction assert overrides
  //   note 1.X
  //   (add, avoiding bus contention)
  //   IA  MA 
  //   remove bc of new 32 bit approach?
  //   ?????????
  //   16 bit result
  //   32 bit result
  //   32 bit memory
  //   note 3.3
  //   note 3.2
  //   note 3.1
endmodule

module Bit32_Split_Register (
  input  F_Write,
  input  L_Write,
  input  H_Write,
  input  [31:0] Bit32_In,
  input  [15:0] Bit16_In,
  input  Clock,
  input  Reset,
  output [31:0] Bit32_Out,
  output [15:0] Bit16_Low,
  output [15:0] Bit16_High
);

  wire or_1_out, or_2_out;
  wire [15:0] multiplexer_1_out, multiplexer_2_out;

  Multiplexer #(.width(16)) multiplexer_1 (
    .in0(Bit32_In[15:0]), .in1(Bit16_In), .out(multiplexer_1_out), .sel(L_Write));
  Multiplexer #(.width(16)) multiplexer_2 (
    .in0(Bit32_In[31:16]), .in1(Bit16_In), .out(multiplexer_2_out), .sel(H_Write));
  or or_1 (or_1_out, F_Write, L_Write);
  or or_2 (or_2_out, F_Write, H_Write);
  Register #(.trigger("falling"), .width(16)) register_1 (
    .D(multiplexer_1_out), .en(or_1_out), .clk(Clock), .Q(Bit16_Low), .clr(Reset));
  Register #(.trigger("falling"), .width(16)) register_2 (
    .D(multiplexer_2_out), .en(or_2_out), .clk(Clock), .Q(Bit16_High), .clr(Reset));

  assign Bit32_Out = {Bit16_High, Bit16_Low};
endmodule

module port_concept (
);

  wire buffer_1_out, d_ff_1_q, undriven_2, undriven_3, undriven_4;
  wire [7:0] controlled_buffer_1_out, undriven;

  assign controlled_buffer_1_out = undriven_3 ? undriven : 8'bz;  // Controlled_Buffer controlled_buffer_1
  D_Flip_Flop d_ff_1 (.D(undriven_2), .clk(buffer_1_out), .Q(d_ff_1_q), .reset(undriven_4));  // open: Qn, preset
  buf buffer_1 (buffer_1_out, undriven_2);

  // Notes on the sheet:
  //   device IRQ (latch rising)
  //   CDB
  //   arbiter assert device
  //   port IRQ
  //   port IRQ reset
endmodule
module core4real (
  input  [25:0] Bit26_Memory_Out,
  input  [7:0] in_2,
  input  in_3,
  input  in_4,
  input  in_5,
  output Memory_RWDS_Out,
  output [7:0] Memory_Bit8_Data_Out,
  output Memory_Data_Moving
);

  wire and_1_out, and_2_out, and_6_out, and_7_out, and_8_out, and_9_out, and_10_out, and_11_out, and_12_out,
       and_13_out, and_14_out, and_15_out, and_16_out, and_17_out, and_18_out, and_19_out, and_20_out,
       and_21_out, and_22_out, and_23_out, and_24_out, and_25_out, and_26_out, and_27_out, and_28_out,
       and_29_out, and_30_out, and_31_out, and_32_out, and_33_out, and_38_out, and_39_out, and_40_out,
       and_42_out, and_43_out, and_44_out, and_46_out, and_47_out, and_48_out, and_54_out, and_56_out,
       and_57_out, and_60_out, and_61_out, and_62_out, and_63_out, and_64_out, and_65_out, and_66_out,
       and_67_out, and_68_out, and_69_out, and_70_out, and_71_out, and_72_out, and_73_out, and_74_out,
       and_75_out, and_76_out, and_77_out, bit2_equal_1_equal, bit2_equal_2_equal, bit2_equal_3_equal,
       bit2_equal_4_equal, bit3_latching_arbiter_1_ga, bit3_latching_arbiter_1_gb, bit4_equal_1_equal,
       bit4_equal_2_equal, bit4_equal_3_equal, bit4_equal_4_equal, Bit16_Path_A_Enable, Bit16_Path_B_Enable,
       Bit32_Assert_Enable, Bit32_Assert_Select, buffer_1_out, buffer_2_out, buffer_3_out, buffer_4_out,
       clock, comparator_1_eq, comparator_2_eq, comparator_3_eq, comparator_4_eq, comparator_5_eq,
       comparator_6_eq, comparator_7_eq, comparator_8_eq, condition_evaluator_1_condition_state, d_ff_1_q,
       data_cache_2_way_1_ram_read, data_cache_2_way_1_ram_write, data_cache_2_way_1_requesting_ram,
       data_cache_2_way_1_rwds, DCache_Stall, decoder_1_out0, decoder_1_out1, decoder_1_out2, decoder_1_out3,
       decoder_1_out4, decoder_1_out5, decoder_1_out6, decoder_1_out7, decoder_1_out8, decoder_1_out9,
       decoder_1_out10, decoder_1_out11, decoder_1_out12, decoder_1_out13, decoder_1_out14, decoder_1_out15,
       decoder_2_out0, decoder_2_out1, decoder_2_out2, decoder_3_out0, decoder_3_out1, decoder_3_out2,
       decoder_4_out0, decoder_4_out1, decoder_5_out0, decoder_5_out1, decoder_5_out2, decoder_5_out3,
       decoder_5_out4, decoder_5_out5, decoder_5_out6, decoder_5_out7, decoder_5_out8, decoder_5_out9,
       decoder_5_out10, decoder_5_out11, decoder_5_out12, decoder_5_out13, decoder_5_out14, decoder_5_out15,
       decoder_6_out0, decoder_6_out1, decoder_6_out2, decoder_6_out3, decoder_6_out4, decoder_6_out5,
       decoder_6_out6, decoder_6_out7, decoder_6_out8, decoder_6_out9, decoder_6_out10, decoder_6_out11,
       decoder_6_out12, decoder_6_out13, decoder_6_out14, decoder_6_out15, Fetch_Unit_Target,
       Hardware_Interrupt, ICache_Stall, Injecting_Instruction, instruction_cache_2_way_1_ram_read,
       instruction_cache_2_way_1_requesting_ram, mmu3_1_data_read, mmu3_1_data_two_byte, mmu3_1_data_write,
       mmu3_1_instruction_read, MMU_Fault, MMU_Stall, NOP_Execute, NOP_Memory, NOP_Writeback, nor_1_out,
       nor_2_out, nor_3_out, nor_4_out, nor_5_out, nor_6_out, nor_7_out, not_2_out, not_3_out, not_4_out,
       not_7_out, Not_Mute_EXE_Foward, Not_Mute_MEM_Forward, or_1_out, or_3_out, or_4_out, or_5_out,
       or_6_out, or_7_out, or_8_out, or_9_out, or_10_out, or_11_out, or_12_out, or_13_out, or_15_out,
       or_17_out, or_19_out, or_23_out, pull_resistor_6_node, reset, Stalling, undriven, undriven_2,
       undriven_3, undriven_4, undriven_6, undriven_12, undriven_13, undriven_14, undriven_15, undriven_16,
       undriven_17, undriven_18, undriven_19, undriven_21, undriven_22, undriven_23, undriven_24,
       undriven_25, UsingStartupRom, WE_Execute, Write_Enable_Decode, Write_Enable_Execute,
       Write_Enable_Memory, Write_Enable_Write;
  wire [1:0] Bit16_Path_A_Source_Select, Bit16_Path_B_Select, Bit16_Path_B_Source_Select,
       Immediate_Field_Select, priority_encoder_1_out, Read_Field_A_Select, Read_Field_B_Select,
       Virtual_Mode, Write_Field_Select;
  wire [3:0] alu4_1_zero, bit_extender_9_out, BranchImmediate, mmu3_1_bit4_faults, multiplexer_12_out,
       register_11_q, undriven_7, undriven_8, undriven_20;
  wire [3:3] pull_resistor_1_node;
  wire [4:0] bit_extender_1_out, bit_extender_2_out, bit_extender_3_out, multiplexer_7_out, Read_Path_A,
       Read_Path_B, undriven_5, undriven_9, undriven_10, undriven_11, Write_Field_Decode,
       Write_Field_Execute, Write_Field_Memory, Write_Field_Write;
  wire [5:5] and_3_out;
  wire [6:0] Memory_Control;
  wire [7:0] data_cache_2_way_1_memory_byte, Memory_Stage_Context;
  wire [9:0] bit_extender_4_out, bit_extender_5_out, bit_extender_6_out, multiplexer_5_out;
  wire [10:0] Inner_EXE_Write, MEM_Write;
  wire [14:0] Memory_Config_Execute, Memory_Config_Memory;
  wire [14:4] Memory_Config_Decode;
  wire [15:0] alu4_1_result, and_45_out, bit_extender_10_out, controlled_buffer_22_out,
       controlled_buffer_23_out, controlled_buffer_41_out, controlled_buffer_42_out,
       controlled_buffer_53_out, controlled_buffer_53_out_2, controlled_buffer_61_out, Current_Instruction,
       data_cache_2_way_1_bit16_to_core, decode_path_A_q, decode_path_B_q, Forwarding_Control_OLD,
       FP_bit16_high, FP_bit16_low, GP_bit16_high, GP_bit16_low, ICache_Result, Injected_Instruction,
       InstructionImmediate, MO_bit16_high, MO_bit16_low, multiplexer_9_out, multiplexer_10_out,
       multiplexer_11_out, multiplexer_14_out, Next_Instruction, pull_resistor_2_node, pull_resistor_3_node,
       pull_resistor_8_node, pull_resistor_11_node, register_1_q, register_12_q, register_15_q,
       register_file_1_readline_a, register_file_1_readline_b, SP_bit16_high, SP_bit16_low, SREG1_q, SREG2_q,
       SREG3_q, SREG4_q, Startup_Rom_Value;
  wire [18:0] and_36_out, Forwarding_Control, register_10_q;
  wire [22:0] Readstage_out;
  wire [23:0] Exe_Config_Execute, EXE_Control;
  wire [25:0] bit_extender_11_out, mmu3_1_bit26_data_address_out, mmu3_1_bit26_instruction_address_out,
       multiplexer_15_out;
  wire [25:1] Next_Instruction_Address;
  wire [31:0] adder_1_out, bit16_to_32_side_select_extender_1_bit32_out, Bit32_To_Fetch_Unit,
       bit32_toggle_inverter_toggle_shift1_1_out_4, bit_extender_8_out, controlled_buffer_1_out,
       controlled_buffer_38_out, decode_32_path_q, FP_bit32_out, GP_bit32_out, Instruction_pointer_q,
       MO_bit32_out, multiplexer_8_out, pull_resistor_4_node, pull_resistor_9_node, pull_resistor_10_node,
       pull_resistor_12_node, register_9_q, register_13_q, register_14_q, register_16_q, SP_bit32_out;

  PLA #(.in_width(6), .out_width(23), .\table ("000000 00000000000000000000000\n000001 00000000000000000101000\n000010 00000000000000000101000\n000011 00000000000000000101000\n000100 00000000000000000101000\n000101 00000000000000000101000\n000110 00000000000000000101000\n000111 00000000000000000101000\n001000 00000000010000000101000\n001001 00000000000000000101000\n001010 00000000000000000101000\n001011 00000000100000010101000\n001100 00000000000000001101000\n001101 00000000100000010101000\n001110 00000000000000001101000\n001111 00000000000000001101000\n010000 00000000000000001101000\n010001 00000000000000001101000\n010010 00000000000000000101000\n010011 00000000000000000101000\n010100 00000000000000000101000\n010101 00000000111001010101000\n010110 00000000111001010101000\n010111 00000000111001010101000\n011000 00000000111001010101000\n011001 00000000000000000000000\n011010 00001100000110100001000\n011011 00000000000000000011000\n011100 00000010010011010101000\n011101 00000000000111001101000\n011110 00000100000111000101000\n011111 01011010010011000100000\n100000 01001100000011000111000\n100001 01001100000010000101000\n100010 00111000100010000101000\n100011 00111000100010010101000\n100100 00000000111001010101000\n100101 00000000000110100001101\n100110 01000001000000010100000\n100111 01000001000000010100000\n101000 01000001010000010100000\n101001 01000001010000010100000\n101010 11000000001010000001000\n101011 11000000000010000001000\n101100 00000000000110000101000\n101101 00000100000010000001000\n101110 00000000000000000000000\n101111 00000010000110000001000\n110000 00001100000010000101000\n110001 00000000000000000000000\n110010 00000000000000000000000\n110011 00000000000000000000000\n110100 00000000000000000000000\n110101 00000000000000000000000\n110110 00000000000000000000000\n110111 00000000000000000000000\n111000 00000000000000000000000\n111001 00000000000000000000000\n111010 00000000000000000000000\n111011 00000000000000000000000\n111100 00000000000000000000000\n111101 00000000000000000000000\n111110 00000000000000000000000\n111111 01000001000000000000000")) Readstage (
    .in(Current_Instruction[15:10]),
    .out({Readstage_out[22:9], Write_Enable_Decode, Bit16_Path_B_Select, Bit16_Path_B_Enable, Bit16_Path_A_Enable, Readstage_out[3:0]}));
  PLA #(.in_width(6), .out_width(24), .\table ("000000 000000000000000000000000\n000001 000000100000001000000000\n000010 000000100001001000000000\n000011 000000100010001000000000\n000100 000000100011001000000000\n000101 000000100100001000000000\n000110 000000100101001000000000\n000111 000000100110001000000000\n001000 000000100111001000000000\n001001 000000101000001000000000\n001010 000000101001001000000000\n001011 000000100000001000000000\n001100 000000100000001000000000\n001101 000000100010001000000000\n001110 000000100010001000000000\n001111 000000101010001000000000\n010000 000000101011001000000000\n010001 000000101100001000000000\n010010 000000101010001000000000\n010011 000000101011001000000000\n010100 000000101100001000000000\n010101 000000100110001000000000\n010110 000000100111001000000000\n010111 000000101001001000000000\n011000 000000101000001000000000\n011001 000000000000000000000000\n011010 000001000000100000001000\n011011 000000000000100000000000\n011100 010000000000000000000001\n011101 010000000000000000000001\n011110 010000000000000000000001\n011111 000000000000010000000001\n100000 000000000000010000000001\n100001 000000000000010000000001\n100010 000000010000010000001010\n100011 010000000000000000001001\n100100 001000000000100000000000\n100101 000001000000100000001000\n100110 110010010000000000000001\n100111 110010000000000000000001\n101000 110110010000000000000001\n101001 110110000000000000000001\n101010 100010000000000000000001\n101011 100110000000000000000001\n101100 000000101101001000000000\n101101 000000000000100000000001\n101110 000000000000000000000000\n101111 000000000000000000000001\n110000 000000000000010000000001\n110001 000000000000000000000000\n110010 000000000000000000000000\n110011 000000000000000000000000\n110100 000000000000000000000000\n110101 000000000000000000000000\n110110 000000000000000000000000\n110111 000000000000000000000000\n111000 000000000000000000000000\n111001 000000000000000000000000\n111010 000000000000000000000000\n111011 000000000000000000000000\n111100 000000000000000000000000\n111101 000000000000000000000000\n111110 000000000000000000000000\n111111 000010000000000000000010")) EXEstage (
    .in(Current_Instruction[15:10]), .out(EXE_Control));
  PLA #(.in_width(6), .out_width(7), .\table ("000000 0000000\n000001 0010000\n000010 0010000\n000011 0010000\n000100 0010000\n000101 0010000\n000110 0010000\n000111 0010000\n001000 0001000\n001001 0010000\n001010 0010000\n001011 0010000\n001100 0010000\n001101 0010000\n001110 0010000\n001111 0010000\n010000 0010000\n010001 0010000\n010010 0010000\n010011 0010000\n010100 0010000\n010101 0010000\n010110 0010000\n010111 0010000\n011000 0010000\n011001 0000000\n011010 0010000\n011011 0010000\n011100 1101000\n011101 1101000\n011110 1101000\n011111 1101100\n100000 1100100\n100001 1100100\n100010 0100110\n100011 0101010\n100100 0010000\n100101 0010000\n100110 0000000\n100111 0000000\n101000 0000000\n101001 0000000\n101010 0000000\n101011 0000000\n101100 0000000\n101101 0100001\n101110 0000000\n101111 1101000\n110000 1100100\n110001 0000000\n110010 0000000\n110011 0000000\n110100 0000000\n110101 0000000\n110110 0000000\n110111 0000000\n111000 0000000\n111001 0000000\n111010 0000000\n111011 0000000\n111100 0000000\n111101 0000000\n111110 0000000\n111111 0000000")) MemoryStage (
    .in(Current_Instruction[15:10]),
    .out({Memory_Control[6], Memory_Config_Decode[14:11], Memory_Control[1:0]}));
  PLA #(.in_width(6), .out_width(3), .\table ("000000 000\n000001 001\n000010 001\n000011 001\n000100 001\n000101 001\n000110 001\n000111 001\n001000 001\n001001 001\n001010 001\n001011 001\n001100 001\n001101 001\n001110 001\n001111 001\n010000 001\n010001 001\n010010 001\n010011 001\n010100 001\n010101 001\n010110 001\n010111 001\n011000 001\n011001 000\n011010 000\n011011 001\n011100 001\n011101 001\n011110 001\n011111 000\n100000 000\n100001 000\n100010 010\n100011 011\n100100 001\n100101 000\n100110 000\n100111 000\n101000 000\n101001 000\n101010 000\n101011 000\n101100 001\n101101 000\n101110 000\n101111 001\n110000 000\n110001 000\n110010 000\n110011 000\n110100 000\n110101 000\n110110 000\n110111 000\n111000 000\n111001 000\n111010 000\n111011 000\n111100 000\n111101 000\n111110 000\n111111 000")) WriteStage (.in(Current_Instruction[15:10]));  // open: out
  Multiplexer #(.select(2), .width(5)) multiplexer_1 (
    .in0(bit_extender_2_out), .in1(Current_Instruction[4:0]), .in2(bit_extender_1_out),
    .in3({BranchImmediate, Current_Instruction[5]}), .out(Read_Path_B), .sel(Read_Field_B_Select));
  not not_1 (WE_Execute, Stalling);
  and and_1 (and_1_out, ~Readstage_out[22], Readstage_out[21]);  // AND_Gate
  Multiplexer #(.select(2), .width(5)) multiplexer_2 (
    .in0(bit_extender_3_out), .in1(bit_extender_2_out), .in2(Current_Instruction[4:0]),
    .in3(bit_extender_1_out), .out(Read_Path_A), .sel(Read_Field_A_Select));
  Multiplexer #(.select(2), .width(16)) multiplexer_3 (
    .in0(ICache_Result), .in1(Startup_Rom_Value), .in2(Injected_Instruction), .in3({16{1'b0}}),
    .out(Next_Instruction), .sel(priority_encoder_1_out));
  Priority_Encoder #(.select(2)) priority_encoder_1 (
    .in0(not_2_out), .in1(UsingStartupRom), .in2(or_1_out), .in3(Fetch_Unit_Target),
    .out(priority_encoder_1_out));
  not not_2 (not_2_out, UsingStartupRom);
  or or_1 (or_1_out, Injecting_Instruction, Hardware_Interrupt);
  // OR_Gate or_2 has open pins: in0=and_1_out, in1=and_2_out, out=open
  buf and_2 (and_2_out, Readstage_out[21]);  // AND_Gate
  assign bit_extender_1_out = {{1{1'b0}}, BranchImmediate};  // Bit_Extender bit_extender_1
  Multiplexer #(.select(2), .width(5)) multiplexer_4 (
    .in0(bit_extender_1_out), .in1({BranchImmediate, Current_Instruction[5]}), .in2(bit_extender_3_out),
    .in3(Current_Instruction[4:0]), .out(Write_Field_Decode), .sel(Write_Field_Select));
  assign bit_extender_2_out = {{2{1'b0}}, Current_Instruction[2:0]};  // Bit_Extender bit_extender_2
  assign bit_extender_3_out = {{2{1'b0}}, Current_Instruction[5:3]};  // Bit_Extender bit_extender_3
  Register #(.trigger("falling"), .width(16)) register_1 (
    .D(Next_Instruction), .en(1'b1), .clk(clock), .Q(register_1_q), .clr(reset));
  Register #(.width(6)) register_2 (
    .D({Write_Field_Decode, Write_Enable_Decode}), .Q({Write_Field_Execute, Write_Enable_Execute}));  // open: en, clk, clr
  nor nor_1 (nor_1_out, ICache_Stall, DCache_Stall, Hardware_Interrupt);
  and and_3 (and_3_out[5], ~Readstage_out[16], Current_Instruction[5]);  // AND_Gate
  Register #(.width(6)) register_3 (
    .D({Write_Field_Execute, Write_Enable_Execute}), .Q({Write_Field_Memory, Write_Enable_Memory}));  // open: en, clk, clr
  Register #(.width(15)) register_4 (
    .D({Memory_Config_Decode[14:10], BranchImmediate, Memory_Config_Decode[5:4], Current_Instruction[3:0]}),
    .Q(Memory_Config_Execute));  // open: en, clk, clr
  Register #(.width(24)) register_5 (.D(EXE_Control), .Q(Exe_Config_Execute));  // open: en, clk, clr
  nor nor_2 (nor_2_out, Injecting_Instruction, ICache_Stall, DCache_Stall, Hardware_Interrupt, Hardware_Interrupt);
  Register #(.width(6)) register_6 (
    .D({Write_Field_Memory, Write_Enable_Memory}), .Q({Write_Field_Write, Write_Enable_Write}));  // open: en, clk, clr
  Register #(.width(15)) register_7 (.D(Memory_Config_Execute), .Q(Memory_Config_Memory));  // open: en, clk, clr
  Register #(.width(16)) register_8 (
    .D(register_1_q), .en(nor_1_out), .clk(clock),
    .Q({Current_Instruction[15:10], BranchImmediate, Current_Instruction[5:0]}), .clr(reset));
  assign bit_extender_4_out = {{4{1'b0}}, {and_3_out[5], Current_Instruction[4:0]}};  // Bit_Extender bit_extender_4
  assign bit_extender_5_out = {{7{1'b0}}, Current_Instruction[2:0]};  // Bit_Extender bit_extender_5
  assign bit_extender_6_out = {{6{1'b0}}, BranchImmediate};  // Bit_Extender bit_extender_6
  Multiplexer #(.select(2), .width(10)) multiplexer_5 (
    .in0({BranchImmediate, Current_Instruction[5:0]}), .in1(bit_extender_4_out), .in2(bit_extender_5_out),
    .in3(bit_extender_6_out), .out(multiplexer_5_out), .sel(Immediate_Field_Select));
  Counter #(.max('h1ffffff), .width(25)) counter_1 (
    .clr(reset), .load(Fetch_Unit_Target), .up(1'b1), .count(nor_2_out), .clk(clock),
    .D(Bit32_To_Fetch_Unit[25:1]), .Q(Next_Instruction_Address));  // open: carry
  Multiplexer multiplexer_6 (
    .in0(Memory_Control[1]), .in1(BranchImmediate[3]), .out(Memory_Config_Decode[10]), .sel(Memory_Control[6]));
  assign InstructionImmediate = {{6{1'b0}}, multiplexer_5_out};  // Bit_Extender bit_extender_7
  and and_4 (Memory_Config_Decode[5], Memory_Control[0], Current_Instruction[5]);
  and and_5 (Memory_Config_Decode[4], Memory_Control[0], ~Current_Instruction[5]);  // AND_Gate
  and and_6 (and_6_out, Write_Enable_Write, ~Write_Field_Write[4]);  // AND_Gate
  and and_7 (and_7_out, Write_Field_Write[4], Write_Enable_Write);
  Decoder #(.select(4)) decoder_1 (
    .out0(decoder_1_out0), .out1(decoder_1_out1), .out2(decoder_1_out2), .out3(decoder_1_out3),
    .out4(decoder_1_out4), .out5(decoder_1_out5), .out6(decoder_1_out6), .out7(decoder_1_out7),
    .out8(decoder_1_out8), .out9(decoder_1_out9), .out10(decoder_1_out10), .out11(decoder_1_out11),
    .out12(decoder_1_out12), .out13(decoder_1_out13), .out14(decoder_1_out14), .out15(decoder_1_out15),
    .sel(Write_Field_Write[3:0]), .en(and_6_out));
  Decoder #(.select(2)) decoder_2 (
    .out0(decoder_2_out0), .out1(decoder_2_out1), .out2(decoder_2_out2), .sel(Bit16_Path_B_Source_Select),
    .en(Bit16_Path_A_Enable));  // open: out3
  Decoder #(.select(2)) decoder_3 (
    .out0(decoder_3_out0), .out1(decoder_3_out1), .out2(decoder_3_out2), .sel(Bit16_Path_A_Source_Select),
    .en(Bit16_Path_B_Enable));  // open: out3
  Pull_Resistor pull_resistor_1 (.node(pull_resistor_1_node[3]));
  Multiplexer #(.width(5)) multiplexer_7 (
    .in0(Read_Path_A), .in1({Bit32_Assert_Enable, {4{pull_resistor_1_node[3]}}}), .out(multiplexer_7_out),
    .sel(Bit32_Assert_Enable));
  Decoder decoder_4 (.out0(decoder_4_out0), .out1(decoder_4_out1), .sel(Bit32_Assert_Select), .en(Bit32_Assert_Enable));
  and and_8 (and_8_out, Read_Path_B[4], decoder_2_out0);
  and and_9 (and_9_out, multiplexer_7_out[4], decoder_3_out0);
  and and_10 (and_10_out, ~Read_Path_B[4], decoder_2_out0);  // AND_Gate
  and and_11 (and_11_out, ~multiplexer_7_out[4], decoder_3_out0);  // AND_Gate
  Register #(.trigger("falling"), .width(32)) register_9 (
    .D(bit_extender_8_out), .en(undriven_3), .clk(undriven_4), .Q(register_9_q));  // open: clr
  assign bit_extender_8_out = {{6{1'b0}}, {Next_Instruction_Address, 1'b0}};  // Bit_Extender bit_extender_8
  Forwarding_Control_Manager forwarding_control_manager_1 (
    .Write_Field_Execute(Write_Field_Execute), .Write_Enable_Execute(Write_Enable_Execute),
    .Write_Field_Memory(Write_Field_Memory), .Write_Enable_Memory(Write_Enable_Memory),
    .Read_Path_A(multiplexer_7_out), .Read_Path_B(Read_Path_B), .control(Forwarding_Control));  // open: clock
  Register #(.trigger("falling"), .width(32)) Instruction_pointer (
    .D(register_9_q), .en(undriven_3), .clk(undriven_4), .Q(Instruction_pointer_q));  // open: clr
  Register #(.width(16)) SREG1 (.D(register_15_q), .en(decoder_1_out4), .Q(SREG1_q));  // open: clk, clr
  Register #(.width(16)) SREG2 (.D(register_15_q), .en(decoder_1_out5), .Q(SREG2_q));  // open: clk, clr
  Register #(.width(16)) SREG3 (.D(register_15_q), .en(decoder_1_out6), .Q(SREG3_q));  // open: clk, clr
  Register #(.width(16)) SREG4 (.D(register_15_q), .en(decoder_1_out7), .Q(SREG4_q));  // open: clk, clr
  Bit32_Split_Register MO (
    .F_Write(decoder_1_out0), .L_Write(decoder_1_out8), .H_Write(decoder_1_out12), .Bit32_In(register_16_q),
    .Bit16_In(register_15_q), .Clock(undriven), .Reset(undriven_2), .Bit32_Out(MO_bit32_out),
    .Bit16_Low(MO_bit16_low), .Bit16_High(MO_bit16_high));
  Bit32_Split_Register SP (
    .F_Write(decoder_1_out1), .L_Write(decoder_1_out9), .H_Write(decoder_1_out13), .Bit32_In(register_16_q),
    .Bit16_In(register_15_q), .Clock(undriven), .Reset(undriven_2), .Bit32_Out(SP_bit32_out),
    .Bit16_Low(SP_bit16_low), .Bit16_High(SP_bit16_high));
  Bit32_Split_Register FP (
    .F_Write(decoder_1_out2), .L_Write(decoder_1_out10), .H_Write(decoder_1_out14), .Bit32_In(register_16_q),
    .Bit16_In(register_15_q), .Clock(undriven), .Reset(undriven_2), .Bit32_Out(FP_bit32_out),
    .Bit16_Low(FP_bit16_low), .Bit16_High(FP_bit16_high));
  Bit32_Split_Register GP (
    .F_Write(decoder_1_out3), .L_Write(decoder_1_out11), .H_Write(decoder_1_out15), .Bit32_In(register_16_q),
    .Bit16_In(register_15_q), .Clock(undriven), .Reset(undriven_2), .Bit32_Out(GP_bit32_out),
    .Bit16_Low(GP_bit16_low), .Bit16_High(GP_bit16_high));
  Register_File register_file_1 (
    .Write_Data(register_15_q), .Read_Address_B(Read_Path_B[3:0]), .Read_B_Enable(and_10_out),
    .Read_Address_A(multiplexer_7_out[3:0]), .Read_A_Enable(and_11_out),
    .Write_Address(Write_Field_Write[3:0]), .Write_Enable(and_7_out), .Clock(undriven),
    .Clear_All_Registers(undriven_2), .ReadLine_A(register_file_1_readline_a),
    .ReadLine_B(register_file_1_readline_b));
  assign controlled_buffer_1_out = or_3_out ? MO_bit32_out : 32'bz;  // Controlled_Buffer controlled_buffer_1
  and and_12 (and_12_out, decoder_5_out0, nor_3_out);
  or or_3 (or_3_out, and_12_out, buffer_4_out, and_13_out);
  and and_13 (and_13_out, decoder_6_out0, ~and_20_out, nor_3_out);  // AND_Gate
  assign register_file_1_readline_a = decoder_5_out8 ? MO_bit16_low : 16'bz;  // Controlled_Buffer controlled_buffer_2
  assign register_file_1_readline_a = decoder_5_out12 ? MO_bit16_high : 16'bz;  // Controlled_Buffer controlled_buffer_3
  assign register_file_1_readline_b = decoder_6_out8 ? MO_bit16_low : 16'bz;  // Controlled_Buffer controlled_buffer_4
  assign register_file_1_readline_b = decoder_6_out12 ? MO_bit16_high : 16'bz;  // Controlled_Buffer controlled_buffer_5
  assign controlled_buffer_1_out = or_4_out ? SP_bit32_out : 32'bz;  // Controlled_Buffer controlled_buffer_6
  and and_14 (and_14_out, decoder_5_out1, nor_3_out);
  or or_4 (or_4_out, and_14_out, and_15_out);
  and and_15 (and_15_out, decoder_6_out1, ~and_20_out, nor_3_out);  // AND_Gate
  assign register_file_1_readline_a = decoder_5_out9 ? SP_bit16_low : 16'bz;  // Controlled_Buffer controlled_buffer_7
  assign register_file_1_readline_a = decoder_5_out13 ? SP_bit16_high : 16'bz;  // Controlled_Buffer controlled_buffer_8
  assign register_file_1_readline_b = decoder_6_out9 ? SP_bit16_low : 16'bz;  // Controlled_Buffer controlled_buffer_9
  assign register_file_1_readline_b = decoder_6_out13 ? SP_bit16_high : 16'bz;  // Controlled_Buffer controlled_buffer_10
  assign controlled_buffer_1_out = or_5_out ? FP_bit32_out : 32'bz;  // Controlled_Buffer controlled_buffer_11
  and and_16 (and_16_out, decoder_5_out2, nor_3_out);
  or or_5 (or_5_out, and_16_out, and_17_out);
  and and_17 (and_17_out, decoder_6_out2, ~and_20_out, nor_3_out);  // AND_Gate
  assign register_file_1_readline_a = decoder_5_out10 ? FP_bit16_low : 16'bz;  // Controlled_Buffer controlled_buffer_12
  assign register_file_1_readline_a = decoder_5_out14 ? FP_bit16_high : 16'bz;  // Controlled_Buffer controlled_buffer_13
  assign register_file_1_readline_b = decoder_6_out10 ? FP_bit16_low : 16'bz;  // Controlled_Buffer controlled_buffer_14
  assign register_file_1_readline_b = decoder_6_out14 ? FP_bit16_high : 16'bz;  // Controlled_Buffer controlled_buffer_15
  assign controlled_buffer_1_out = or_6_out ? GP_bit32_out : 32'bz;  // Controlled_Buffer controlled_buffer_16
  and and_18 (and_18_out, decoder_5_out3, nor_3_out);
  or or_6 (or_6_out, and_18_out, and_19_out);
  and and_19 (and_19_out, decoder_6_out3, ~and_20_out, nor_3_out);  // AND_Gate
  assign register_file_1_readline_a = decoder_5_out11 ? GP_bit16_low : 16'bz;  // Controlled_Buffer controlled_buffer_17
  assign register_file_1_readline_a = decoder_5_out15 ? GP_bit16_high : 16'bz;  // Controlled_Buffer controlled_buffer_18
  assign register_file_1_readline_b = decoder_6_out11 ? GP_bit16_low : 16'bz;  // Controlled_Buffer controlled_buffer_19
  assign register_file_1_readline_b = decoder_6_out15 ? GP_bit16_high : 16'bz;  // Controlled_Buffer controlled_buffer_20
  assign controlled_buffer_1_out = buffer_3_out ? Instruction_pointer_q : 32'bz;  // Controlled_Buffer controlled_buffer_21
  assign controlled_buffer_22_out = decoder_5_out4 ? SREG1_q : 16'bz;  // Controlled_Buffer controlled_buffer_22
  assign controlled_buffer_23_out = decoder_6_out4 ? SREG1_q : 16'bz;  // Controlled_Buffer controlled_buffer_23
  assign controlled_buffer_22_out = decoder_5_out5 ? SREG2_q : 16'bz;  // Controlled_Buffer controlled_buffer_24
  assign controlled_buffer_23_out = decoder_6_out5 ? SREG2_q : 16'bz;  // Controlled_Buffer controlled_buffer_25
  assign controlled_buffer_22_out = decoder_5_out6 ? SREG3_q : 16'bz;  // Controlled_Buffer controlled_buffer_26
  assign controlled_buffer_23_out = decoder_6_out6 ? SREG3_q : 16'bz;  // Controlled_Buffer controlled_buffer_27
  assign controlled_buffer_22_out = decoder_5_out7 ? SREG4_q : 16'bz;  // Controlled_Buffer controlled_buffer_28
  assign controlled_buffer_23_out = decoder_6_out7 ? SREG4_q : 16'bz;  // Controlled_Buffer controlled_buffer_29
  and and_20 (and_20_out, and_9_out, ~multiplexer_7_out[3], ~multiplexer_7_out[2]);  // AND_Gate
  nor nor_3 (nor_3_out, decoder_4_out1, decoder_4_out0);
  buf buffer_1 (buffer_1_out, decoder_4_out1);
  buf buffer_2 (buffer_2_out, decoder_4_out0);
  buf buffer_3 (buffer_3_out, buffer_1_out);
  buf buffer_4 (buffer_4_out, buffer_2_out);
  Decoder #(.select(4)) decoder_5 (
    .out0(decoder_5_out0), .out1(decoder_5_out1), .out2(decoder_5_out2), .out3(decoder_5_out3),
    .out4(decoder_5_out4), .out5(decoder_5_out5), .out6(decoder_5_out6), .out7(decoder_5_out7),
    .out8(decoder_5_out8), .out9(decoder_5_out9), .out10(decoder_5_out10), .out11(decoder_5_out11),
    .out12(decoder_5_out12), .out13(decoder_5_out13), .out14(decoder_5_out14), .out15(decoder_5_out15),
    .sel(multiplexer_7_out[3:0]), .en(and_9_out));
  Decoder #(.select(4)) decoder_6 (
    .out0(decoder_6_out0), .out1(decoder_6_out1), .out2(decoder_6_out2), .out3(decoder_6_out3),
    .out4(decoder_6_out4), .out5(decoder_6_out5), .out6(decoder_6_out6), .out7(decoder_6_out7),
    .out8(decoder_6_out8), .out9(decoder_6_out9), .out10(decoder_6_out10), .out11(decoder_6_out11),
    .out12(decoder_6_out12), .out13(decoder_6_out13), .out14(decoder_6_out14), .out15(decoder_6_out15),
    .sel(Read_Path_B[3:0]), .en(and_8_out));
  assign register_file_1_readline_a = decoder_3_out1 ? InstructionImmediate : 16'bz;  // Controlled_Buffer controlled_buffer_30
  assign register_file_1_readline_b = decoder_2_out1 ? InstructionImmediate : 16'bz;  // Controlled_Buffer controlled_buffer_31
  assign register_file_1_readline_a = decoder_3_out2 ? Next_Instruction : 16'bz;  // Controlled_Buffer controlled_buffer_32
  assign register_file_1_readline_b = decoder_2_out2 ? Next_Instruction : 16'bz;  // Controlled_Buffer controlled_buffer_33
  and and_21 (and_21_out, ~undriven_10[2], ~undriven_10[3], undriven_10[4]);  // AND_Gate
  and and_22 (and_22_out, ~undriven_11[2], ~undriven_11[3], undriven_11[4]);  // AND_Gate
  Pull_Resistor pull_resistor_2 (.node(pull_resistor_2_node));
  assign pull_resistor_2_node = NOP_Execute ? register_file_1_readline_a : 16'bz;  // Controlled_Buffer controlled_buffer_34
  Pull_Resistor pull_resistor_3 (.node(pull_resistor_3_node));
  assign pull_resistor_3_node = NOP_Execute ? register_file_1_readline_b : 16'bz;  // Controlled_Buffer controlled_buffer_35
  Pull_Resistor pull_resistor_4 (.node(pull_resistor_4_node));
  assign pull_resistor_4_node = NOP_Execute ? controlled_buffer_1_out : 32'bz;  // Controlled_Buffer controlled_buffer_36
  and and_23 (and_23_out, ~undriven_9[4], ~undriven_9[3], undriven_9[2]);  // AND_Gate
  and and_24 (and_24_out, undriven_10[3], undriven_10[4]);
  and and_25 (and_25_out, ~undriven_9[4], ~undriven_9[3], undriven_9[2]);  // AND_Gate
  and and_26 (and_26_out, undriven_11[3], undriven_11[4]);
  Register #(.width(16)) decode_path_A (
    .D(pull_resistor_2_node), .en(WE_Execute), .clk(undriven_6), .Q(decode_path_A_q), .clr(reset));
  Register #(.width(16)) decode_path_B (
    .D(pull_resistor_3_node), .en(WE_Execute), .clk(undriven_6), .Q(decode_path_B_q), .clr(reset));
  Register #(.width(32)) decode_32_path (
    .D(pull_resistor_4_node), .en(WE_Execute), .clk(undriven_6), .Q(decode_32_path_q), .clr(reset));
  and and_27 (and_27_out, ~undriven_10[4], ~undriven_10[3], undriven_10[2]);  // AND_Gate
  and and_28 (and_28_out, undriven_9[4], undriven_9[3]);
  and and_29 (and_29_out, undriven_10[4], undriven_10[3]);
  and and_30 (and_30_out, ~undriven_11[4], ~undriven_11[3], undriven_11[2]);  // AND_Gate
  and and_31 (and_31_out, undriven_9[4], undriven_9[3]);
  and and_32 (and_32_out, undriven_11[4], undriven_11[3]);
  or or_7 (or_7_out, and_23_out, and_27_out);
  or or_8 (or_8_out, and_28_out, and_29_out);
  Comparator #(.mode("unsigned"), .width(2)) comparator_1 (
    .a(undriven_5[1:0]), .b(undriven_10[1:0]), .eq(comparator_1_eq));  // open: gt, lt
  Comparator #(.mode("unsigned"), .width(2)) comparator_2 (
    .a(undriven_9[1:0]), .b(undriven_10[1:0]), .eq(comparator_2_eq));  // open: gt, lt
  or or_9 (or_9_out, and_25_out, and_30_out);
  or or_10 (or_10_out, and_31_out, and_32_out);
  Comparator #(.mode("unsigned"), .width(2)) comparator_3 (
    .a(undriven_5[1:0]), .b(undriven_11[1:0]), .eq(comparator_3_eq));  // open: gt, lt
  Comparator #(.mode("unsigned"), .width(2)) comparator_4 (
    .a(undriven_9[1:0]), .b(undriven_11[1:0]), .eq(comparator_4_eq));  // open: gt, lt
  Multiplexer #(.width(32)) multiplexer_8 (
    .in0(register_16_q), .in1(register_14_q), .out(multiplexer_8_out), .sel(Forwarding_Control[6]));
  Controlled_Buffer #(.width(32)) controlled_buffer_37 (.in(register_16_q));  // open: out, en
  assign controlled_buffer_38_out = Forwarding_Control[5] ? register_16_q : 32'bz;  // Controlled_Buffer controlled_buffer_38
  Controlled_Buffer #(.width(32)) controlled_buffer_39 (.in(register_14_q));  // open: out, en
  assign controlled_buffer_38_out = Forwarding_Control[4] ? register_14_q : 32'bz;  // Controlled_Buffer controlled_buffer_40
  or or_11 (or_11_out, comparator_1_eq, comparator_2_eq);
  nor nor_4 (nor_4_out, undriven_9[4], undriven_10[4]);
  Comparator #(.mode("unsigned"), .width(4)) comparator_5 (
    .a(undriven_9[3:0]), .b(undriven_10[3:0]), .eq(comparator_5_eq));  // open: gt, lt
  nor nor_5 (nor_5_out, undriven_5[4], undriven_10[4]);
  Comparator #(.mode("unsigned"), .width(4)) comparator_6 (
    .a(undriven_5[3:0]), .b(undriven_10[3:0]), .eq(comparator_6_eq));  // open: gt, lt
  or or_12 (or_12_out, comparator_3_eq, comparator_4_eq);
  nor nor_6 (nor_6_out, undriven_9[4], undriven_11[4]);
  Comparator #(.mode("unsigned"), .width(4)) comparator_7 (
    .a(undriven_9[3:0]), .b(undriven_11[3:0]), .eq(comparator_7_eq));  // open: gt, lt
  nor nor_7 (nor_7_out, undriven_5[4], undriven_11[4]);
  Comparator #(.mode("unsigned"), .width(4)) comparator_8 (
    .a(undriven_5[3:0]), .b(undriven_11[3:0]), .eq(comparator_8_eq));  // open: gt, lt
  assign controlled_buffer_41_out = Forwarding_Control[12] ? decode_path_A_q : 16'bz;  // Controlled_Buffer controlled_buffer_41
  assign controlled_buffer_42_out = Forwarding_Control[11] ? decode_path_B_q : 16'bz;  // Controlled_Buffer controlled_buffer_42
  assign controlled_buffer_38_out = Forwarding_Control[13] ? decode_32_path_q : 32'bz;  // Controlled_Buffer controlled_buffer_43
  assign controlled_buffer_42_out = Forwarding_Control[7] ? multiplexer_8_out[15:0] : 16'bz;  // Controlled_Buffer controlled_buffer_44
  assign controlled_buffer_42_out = Forwarding_Control[8] ? multiplexer_8_out[31:16] : 16'bz;  // Controlled_Buffer controlled_buffer_45
  assign controlled_buffer_41_out = Forwarding_Control[9] ? multiplexer_8_out[15:0] : 16'bz;  // Controlled_Buffer controlled_buffer_46
  assign controlled_buffer_41_out = Forwarding_Control[10] ? multiplexer_8_out[31:16] : 16'bz;  // Controlled_Buffer controlled_buffer_47
  assign controlled_buffer_42_out = Forwarding_Control[3] ? register_15_q : 16'bz;  // Controlled_Buffer controlled_buffer_48
  assign controlled_buffer_41_out = Forwarding_Control[2] ? register_15_q : 16'bz;  // Controlled_Buffer controlled_buffer_49
  assign controlled_buffer_42_out = Forwarding_Control[0] ? register_12_q : 16'bz;  // Controlled_Buffer controlled_buffer_50
  assign controlled_buffer_41_out = Forwarding_Control[1] ? register_12_q : 16'bz;  // Controlled_Buffer controlled_buffer_51
  Multiplexer #(.select(2), .width(16)) multiplexer_9 (
    .in0(decode_32_path_q[15:0]), .in1(decode_32_path_q[15:0]), .in2(register_15_q), .in3(register_12_q),
    .out(multiplexer_9_out), .sel(Forwarding_Control[18:17]));
  Multiplexer #(.select(2), .width(16)) multiplexer_10 (
    .in0(decode_32_path_q[31:16]), .in1(decode_32_path_q[31:16]), .in2(register_15_q), .in3(register_12_q),
    .out(multiplexer_10_out), .sel(Forwarding_Control[16:15]));
  buf or_13 (or_13_out, undriven_14);  // OR_Gate OR_Gate
  Bit2_Equal bit2_equal_1 (.Bit3_B(MEM_Write[6:5]), .Bit3_A(undriven_8[1:0]), .Equal(bit2_equal_1_equal));
  and and_33 (and_33_out, and_26_out, undriven_13, or_9_out);
  and and_34 (and_36_out[7], and_22_out, undriven_13, or_10_out);
  not not_3 (not_3_out, and_32_out);
  and and_35 (and_36_out[4], or_12_out, undriven_13, and_22_out);
  and and_36 (and_36_out[0], nor_6_out, undriven_13, comparator_7_eq);
  and and_37 (and_36_out[1], nor_7_out, undriven_13, comparator_8_eq);
  assign controlled_buffer_38_out = Forwarding_Control[14] ? {multiplexer_10_out, multiplexer_9_out} : 32'bz;  // Controlled_Buffer controlled_buffer_52
  Bit2_Equal bit2_equal_2 (.Bit3_B(MEM_Write[9:8]), .Bit3_A(undriven_8[1:0]), .Equal(bit2_equal_2_equal));
  Bit4_Equal bit4_equal_1 (.Bit4_B(MEM_Write[3:0]), .Bit4_A(undriven_7), .Equal(bit4_equal_1_equal));
  Bit4_Equal bit4_equal_2 (.Bit4_B(MEM_Write[3:0]), .Bit4_A(undriven_8), .Equal(bit4_equal_2_equal));
  Bit2_Equal bit2_equal_3 (.Bit3_B(Inner_EXE_Write[9:8]), .Bit3_A(undriven_8[1:0]), .Equal(bit2_equal_3_equal));
  Bit2_Equal bit2_equal_4 (.Bit3_B(Inner_EXE_Write[6:5]), .Bit3_A(undriven_8[1:0]), .Equal(bit2_equal_4_equal));
  Bit4_Equal bit4_equal_3 (.Bit4_B(Inner_EXE_Write[3:0]), .Bit4_A(undriven_7), .Equal(bit4_equal_3_equal));
  Bit4_Equal bit4_equal_4 (.Bit4_B(Inner_EXE_Write[3:0]), .Bit4_A(undriven_8), .Equal(bit4_equal_4_equal));
  and and_38 (and_38_out, ~and_45_out[7], bit2_equal_2_equal, undriven_17, undriven_8[3], ~undriven_8[2], MEM_Write[10], Not_Mute_MEM_Forward);  // AND_Gate
  and and_39 (and_39_out, ~and_45_out[7], bit2_equal_2_equal, undriven_17, Not_Mute_MEM_Forward, undriven_8[3], undriven_8[2], MEM_Write[10]);  // AND_Gate
  and and_40 (and_40_out, undriven_8[2], bit2_equal_1_equal, undriven_17, ~undriven_8[3], MEM_Write[7], ~and_45_out[1], Not_Mute_MEM_Forward);  // AND_Gate
  and and_41 (and_45_out[3], bit4_equal_1_equal, undriven_15, MEM_Write[4], ~and_45_out[0], Not_Mute_MEM_Forward);  // AND_Gate
  and and_42 (and_42_out, bit4_equal_2_equal, MEM_Write[4], undriven_16, ~and_45_out[1], Not_Mute_MEM_Forward);  // AND_Gate
  or or_14 (and_45_out[7], and_43_out, and_54_out);
  and and_43 (and_43_out, Inner_EXE_Write[10], bit2_equal_3_equal, undriven_17, undriven_8[3], ~undriven_8[2], Not_Mute_EXE_Foward);  // AND_Gate
  and and_44 (and_44_out, undriven_8[2], bit2_equal_4_equal, undriven_17, ~undriven_8[3], Inner_EXE_Write[7], Not_Mute_EXE_Foward);  // AND_Gate
  and and_45 (and_45_out[0], bit4_equal_3_equal, undriven_15, Not_Mute_EXE_Foward, Inner_EXE_Write[4]);
  and and_46 (and_46_out, bit4_equal_4_equal, undriven_16, Not_Mute_EXE_Foward, Inner_EXE_Write[4]);
  and and_47 (and_47_out, undriven_12, and_24_out, or_7_out, ~and_33_out);  // AND_Gate
  and and_48 (and_48_out, undriven_10[2], ~and_33_out);  // AND_Gate
  // AND_Gate and_49 has open pins: in0=undriven_12, in1=and_21_out, in2=or_8_out, in3=and_36_out[7], out=open
  not not_4 (not_4_out, and_29_out);
  and and_50 (and_36_out[5], undriven_12, or_11_out, and_21_out, ~and_36_out[4]);  // AND_Gate
  and and_51 (and_36_out[3], nor_4_out, undriven_12, ~and_36_out[0], comparator_5_eq);  // AND_Gate
  and and_52 (and_36_out[2], nor_5_out, undriven_12, ~and_36_out[1], comparator_6_eq);  // AND_Gate
  and and_53 (and_45_out[5], ~and_45_out[4], bit2_equal_2_equal, undriven_17, Not_Mute_MEM_Forward, or_15_out, MEM_Write[10]);  // AND_Gate
  and and_54 (and_54_out, Inner_EXE_Write[10], bit2_equal_3_equal, undriven_17, undriven_8[3], undriven_8[2], Not_Mute_EXE_Foward);
  and and_55 (and_45_out[4], Inner_EXE_Write[10], bit2_equal_3_equal, Not_Mute_EXE_Foward, undriven_17, or_17_out);
  nor nor_8 (and_45_out[12], and_45_out[5], and_45_out[4]);
  or or_15 (or_15_out, undriven_8[3], ~undriven_8[2]);  // OR_Gate
  or or_16 (and_45_out[2], and_40_out, and_42_out);
  or or_17 (or_17_out, undriven_8[3], ~undriven_8[2]);  // OR_Gate
  or or_18 (and_45_out[1], and_44_out, and_46_out);
  or or_19 (or_19_out, and_46_out, and_45_out[0]);
  or or_20 (and_36_out[15], and_47_out, and_33_out);
  or or_21 (and_36_out[9], and_48_out, undriven_11[2]);
  and and_56 (and_56_out, not_4_out, ~and_36_out[7]);  // AND_Gate
  and and_57 (and_57_out, and_36_out[7], not_3_out);
  Multiplexer #(.width(16)) multiplexer_11 (
    .in0(controlled_buffer_41_out), .in1(controlled_buffer_42_out), .out(multiplexer_11_out),
    .sel(Exe_Config_Execute[22]));
  Pull_Resistor pull_resistor_5 (.node(Hardware_Interrupt));
  // AND_Gate and_58 has open pins: in0=or_19_out, in1=undriven_18, out=open
  or or_22 (and_36_out[6], and_56_out, and_57_out);
  nor nor_9 (and_45_out[11], and_45_out[1], and_45_out[2]);
  nor nor_10 (and_45_out[10], and_45_out[3], and_45_out[0]);
  not not_5 (and_36_out[8], and_36_out[9]);
  nor nor_11 (and_36_out[13], and_36_out[4], and_36_out[5]);
  Bit16_To_32_Side_Select_Extender bit16_to_32_side_select_extender_1 (
    .HighSide(Exe_Config_Execute[18]), .Bit16_In(multiplexer_11_out),
    .Bit32_Out(bit16_to_32_side_select_extender_1_bit32_out));
  Register #(.width(19)) register_10 (.D(and_36_out), .en(1'b1), .clk(clock), .Q(register_10_q));  // open: clr
  nor nor_12 (and_36_out[12], and_36_out[1], and_36_out[2]);
  nor nor_13 (and_36_out[11], and_36_out[0], and_36_out[3]);
  and and_59 (Fetch_Unit_Target, Exe_Config_Execute[19], or_23_out);
  or or_23 (or_23_out, ~Exe_Config_Execute[20], condition_evaluator_1_condition_state);  // OR_Gate
  Bit32_Toggle_Inverter_Toggle_Shift1 bit32_toggle_inverter_toggle_shift1_1 (
    .Bit32_In(bit16_to_32_side_select_extender_1_bit32_out), .Invert(Exe_Config_Execute[16]),
    .Shift1(Exe_Config_Execute[23]), .out_4(bit32_toggle_inverter_toggle_shift1_1_out_4));
  Bit_Extender #(.in_width(16), .out_width(4), .\type ("zero")) bit_extender_9 (
    .in(controlled_buffer_41_out), .out(bit_extender_9_out));
  Pull_Resistor #(.pull(1)) pull_resistor_6 (.node(pull_resistor_6_node));
  or or_24 (and_45_out[9], and_38_out, and_43_out);
  or or_25 (and_45_out[8], and_39_out, and_54_out);
  not not_6 (and_45_out[6], and_45_out[7]);
  D_Flip_Flop d_ff_1 (.D(Fetch_Unit_Target), .Q(d_ff_1_q));  // open: clk, Qn, preset, reset
  Adder #(.width(32)) adder_1 (
    .a(controlled_buffer_38_out), .b(bit32_toggle_inverter_toggle_shift1_1_out_4), .out(adder_1_out),
    .cin(Exe_Config_Execute[16]));  // open: cout
  Register #(.width(16)) u_Forwarding_Control_OLD (
    .D({{3{and_45_out[15]}}, and_45_out[12:0]}), .en(pull_resistor_6_node), .clk(clock),
    .Q(Forwarding_Control_OLD));  // open: clr
  Pull_Resistor pull_resistor_7 (.node(and_45_out[15]));
  // OR_Gate or_26 has open pins: in0=Fetch_Unit_Target, in1=d_ff_1_q, out=open
  ALU4 alu4_1 (
    .Bit4_ALU_Control(Exe_Config_Execute[15:12]), .CIN(register_11_q[1]), .Bit16_A(controlled_buffer_42_out),
    .Bit16_B(controlled_buffer_41_out), .result(alu4_1_result), .zero(alu4_1_zero[0]),
    .carry(alu4_1_zero[1]), .overflow(alu4_1_zero[2]), .negative(alu4_1_zero[3]));
  Register #(.width(4)) register_11 (
    .D(multiplexer_12_out), .en(Exe_Config_Execute[17]), .Q(register_11_q));  // open: clk, clr
  Multiplexer #(.width(4)) multiplexer_12 (
    .in0(alu4_1_zero), .in1(bit_extender_9_out), .out(multiplexer_12_out), .sel(undriven_19));
  assign {controlled_buffer_53_out_2, controlled_buffer_53_out} = Exe_Config_Execute[4] ? controlled_buffer_38_out : 32'bz;  // Controlled_Buffer controlled_buffer_53
  assign {controlled_buffer_53_out_2, controlled_buffer_53_out} = Exe_Config_Execute[3] ? adder_1_out : 32'bz;  // Controlled_Buffer controlled_buffer_54
  assign Bit32_To_Fetch_Unit = Exe_Config_Execute[1] ? controlled_buffer_38_out : 32'bz;  // Controlled_Buffer controlled_buffer_55
  assign Bit32_To_Fetch_Unit = Exe_Config_Execute[0] ? adder_1_out : 32'bz;  // Controlled_Buffer controlled_buffer_56
  assign bit_extender_10_out = {{12{1'b0}}, register_11_q};  // Bit_Extender bit_extender_10
  assign controlled_buffer_53_out_2 = Exe_Config_Execute[2] ? controlled_buffer_41_out : 16'bz;  // Controlled_Buffer controlled_buffer_57
  assign controlled_buffer_53_out_2 = Exe_Config_Execute[6] ? controlled_buffer_42_out : 16'bz;  // Controlled_Buffer controlled_buffer_58
  assign controlled_buffer_53_out = Exe_Config_Execute[5] ? controlled_buffer_41_out : 16'bz;  // Controlled_Buffer controlled_buffer_59
  assign controlled_buffer_53_out = Exe_Config_Execute[7] ? controlled_buffer_42_out : 16'bz;  // Controlled_Buffer controlled_buffer_60
  assign controlled_buffer_61_out = Exe_Config_Execute[11] ? controlled_buffer_41_out : 16'bz;  // Controlled_Buffer controlled_buffer_61
  assign controlled_buffer_61_out = Exe_Config_Execute[10] ? controlled_buffer_42_out : 16'bz;  // Controlled_Buffer controlled_buffer_62
  assign controlled_buffer_61_out = Exe_Config_Execute[9] ? alu4_1_result : 16'bz;  // Controlled_Buffer controlled_buffer_63
  assign controlled_buffer_61_out = Exe_Config_Execute[8] ? bit_extender_10_out : 16'bz;  // Controlled_Buffer controlled_buffer_64
  Condition_Evaluator condition_evaluator_1 (
    .Bit4_Condition_Selector(undriven_20), .Bit4_Flags(register_11_q),
    .Condition_State(condition_evaluator_1_condition_state));
  Multiplexer multiplexer_13 (
    .in1(condition_evaluator_1_condition_state), .sel(Exe_Config_Execute[21]));  // open: in0, out
  Pull_Resistor pull_resistor_8 (.node(pull_resistor_8_node));
  assign pull_resistor_8_node = NOP_Memory ? controlled_buffer_61_out : 16'bz;  // Controlled_Buffer controlled_buffer_65
  Pull_Resistor pull_resistor_9 (.node(pull_resistor_9_node));
  assign pull_resistor_9_node = NOP_Memory ? Bit32_To_Fetch_Unit : 32'bz;  // Controlled_Buffer controlled_buffer_66
  Pull_Resistor pull_resistor_10 (.node(pull_resistor_10_node));
  assign pull_resistor_10_node = NOP_Memory ? {controlled_buffer_53_out_2, controlled_buffer_53_out} : 32'bz;  // Controlled_Buffer controlled_buffer_67
  Register #(.width(16)) register_12 (
    .D(pull_resistor_8_node), .en(WE_Execute), .clk(undriven_21), .Q(register_12_q), .clr(reset));
  Register #(.width(32)) register_13 (
    .D(pull_resistor_9_node), .en(WE_Execute), .clk(undriven_21), .Q(register_13_q), .clr(reset));
  Register #(.width(32)) register_14 (
    .D(pull_resistor_10_node), .en(WE_Execute), .clk(undriven_21), .Q(register_14_q), .clr(reset));
  Bit_Extender #(.in_width(32), .out_width(26), .\type ("zero")) bit_extender_11 (
    .in(register_13_q), .out(bit_extender_11_out));
  Multiplexer #(.width(16)) multiplexer_14 (
    .in0(register_12_q), .in1(data_cache_2_way_1_bit16_to_core), .out(multiplexer_14_out), .sel(undriven_22));
  Pull_Resistor pull_resistor_11 (.node(pull_resistor_11_node));
  assign pull_resistor_11_node = NOP_Writeback ? multiplexer_14_out : 16'bz;  // Controlled_Buffer controlled_buffer_68
  Pull_Resistor pull_resistor_12 (.node(pull_resistor_12_node));
  assign pull_resistor_12_node = NOP_Writeback ? register_14_q : 32'bz;  // Controlled_Buffer controlled_buffer_69
  Register #(.width(16)) register_15 (
    .D(pull_resistor_11_node), .en(WE_Execute), .clk(undriven_23), .Q(register_15_q), .clr(reset));
  Register #(.width(32)) register_16 (
    .D(pull_resistor_12_node), .en(WE_Execute), .clk(undriven_23), .Q(register_16_q), .clr(reset));
  and and_60 (and_60_out, Memory_Config_Memory[5], Memory_Config_Memory[6]);
  and and_61 (and_61_out, Memory_Config_Memory[5], Memory_Config_Memory[7]);
  and and_62 (and_62_out, Memory_Config_Memory[5], Memory_Config_Memory[8]);
  and and_63 (and_63_out, Memory_Config_Memory[5], Memory_Config_Memory[9]);
  and and_64 (and_64_out, Memory_Config_Memory[14], ~Virtual_Mode[0]);  // AND_Gate
  and and_65 (and_65_out, Virtual_Mode[0], Memory_Config_Memory[14]);
  not not_7 (not_7_out, UsingStartupRom);
  and and_66 (and_66_out, Virtual_Mode[1], ~not_7_out);  // AND_Gate
  and and_67 (and_67_out, Virtual_Mode[1], not_7_out);
  and and_68 (and_68_out, Memory_Config_Memory[9], Memory_Config_Memory[8], Memory_Config_Memory[4]);
  Multiplexer #(.width(26)) multiplexer_15 (
    .in0({Next_Instruction_Address, 1'b0}), .in1(bit_extender_11_out), .out(multiplexer_15_out),
    .sel(and_68_out));
  and and_69 (and_69_out, Memory_Config_Memory[7], Memory_Config_Memory[9], Memory_Config_Memory[8], Memory_Config_Memory[4]);
  and and_70 (and_70_out, ~Memory_Config_Memory[7], Memory_Config_Memory[9], Memory_Config_Memory[8], Memory_Config_Memory[4]);  // AND_Gate
  and and_71 (and_71_out, ~Memory_Config_Memory[8], ~Memory_Config_Memory[9], Memory_Config_Memory[7], Memory_Config_Memory[4]);  // AND_Gate
  and and_72 (and_72_out, Memory_Config_Memory[8], ~Memory_Config_Memory[9], Memory_Config_Memory[7], Memory_Config_Memory[4]);  // AND_Gate
  and and_73 (and_73_out, ~Memory_Config_Memory[8], ~Memory_Config_Memory[9], ~Memory_Config_Memory[7], Memory_Config_Memory[4]);  // AND_Gate
  and and_74 (and_74_out, Memory_Config_Memory[8], ~Memory_Config_Memory[9], ~Memory_Config_Memory[7], Memory_Config_Memory[4]);  // AND_Gate
  MMU3 mmu3_1 (
    .Bit8_Context_Id(Memory_Stage_Context), .Bit4_Lower_Flag_Mask(Memory_Config_Memory[3:0]),
    .Lower_Flag_Mask_Enable(and_63_out), .Bit14_Target_Page(register_12_q[13:0]),
    .Invalidate_Target_Page(and_62_out), .Bit3_Target_Translation_Page(register_12_q[13:11]),
    .Invalidate_Translation_Page(and_61_out), .Invalidate_All(and_60_out),
    .Bit27_Instruction_Address(multiplexer_15_out), .Instruction_Translate(and_67_out),
    .Instruction_Passthrough(and_66_out), .Bit27_Data_Address(bit_extender_11_out),
    .Data_Translate(and_65_out), .Data_Passthrough(and_64_out),
    .Two_Byte_Operation(Memory_Config_Memory[10]), .Data_Direction(Memory_Config_Memory[11]),
    .Bit16_From_Data_Cache(data_cache_2_way_1_bit16_to_core), .Bit4_Faults(mmu3_1_bit4_faults),
    .Is_Fault(MMU_Fault), .Stall(MMU_Stall),
    .Bit26_Instruction_Address_Out(mmu3_1_bit26_instruction_address_out),
    .Instruction_Read(mmu3_1_instruction_read), .Bit26_Data_Address_Out(mmu3_1_bit26_data_address_out),
    .Data_Read(mmu3_1_data_read), .Data_Write(mmu3_1_data_write), .Data_Two_Byte(mmu3_1_data_two_byte));  // open: Enable, Reset, Clock
  Instruction_Cache_2_Way instruction_cache_2_way_1 (
    .Read(mmu3_1_instruction_read), .Two_Byte_Operation(mmu3_1_instruction_read),
    .Invalidate_Address(and_69_out), .Invalidate_Line(and_70_out), .Set(Memory_Config_Memory[6]),
    .Bit26_Address(mmu3_1_bit26_instruction_address_out), .Bit8_From_Memory(Memory_Bit8_Data_Out),
    .Ram_Data_Moving(and_77_out), .Clock(undriven_24), .Reset(undriven_25),
    .Ram_Read(instruction_cache_2_way_1_ram_read), .Requesting_Ram(instruction_cache_2_way_1_requesting_ram));  // open: Bit16_To_Core, RWDS
  Data_Cache_2_Way data_cache_2_way_1 (
    .Read(mmu3_1_data_read), .Write(mmu3_1_data_write), .Two_Byte_Operation(mmu3_1_data_two_byte),
    .Flush_Address(and_71_out), .Invalidate_Address(and_72_out), .Flush_Line(and_73_out),
    .Invalidate_Line(and_74_out), .Set(Memory_Config_Memory[6]),
    .Bit26_Address(mmu3_1_bit26_data_address_out), .Bit16_Data(register_12_q),
    .Bit8_From_Memory(Memory_Bit8_Data_Out), .Ram_Data_Moving(and_76_out), .Clock(undriven_24),
    .Reset(undriven_25), .Bit16_To_Core(data_cache_2_way_1_bit16_to_core),
    .Ram_Write(data_cache_2_way_1_ram_write), .Ram_Read(data_cache_2_way_1_ram_read),
    .Requesting_Ram(data_cache_2_way_1_requesting_ram), .Memory_Byte(data_cache_2_way_1_memory_byte),
    .RWDS(data_cache_2_way_1_rwds));
  and and_75 (and_75_out, data_cache_2_way_1_ram_write, bit3_latching_arbiter_1_gb);
  assign Bit26_Memory_Out = bit3_latching_arbiter_1_ga ? mmu3_1_bit26_instruction_address_out : 26'bz;  // Controlled_Buffer controlled_buffer_70
  assign in_5 = bit3_latching_arbiter_1_ga ? instruction_cache_2_way_1_ram_read : 1'bz;  // Controlled_Buffer controlled_buffer_71
  assign Bit26_Memory_Out = bit3_latching_arbiter_1_gb ? mmu3_1_bit26_data_address_out : 26'bz;  // Controlled_Buffer controlled_buffer_72
  assign in_4 = bit3_latching_arbiter_1_gb ? data_cache_2_way_1_ram_write : 1'bz;  // Controlled_Buffer controlled_buffer_73
  assign in_5 = bit3_latching_arbiter_1_gb ? data_cache_2_way_1_ram_read : 1'bz;  // Controlled_Buffer controlled_buffer_74
  assign in_2 = bit3_latching_arbiter_1_gb ? data_cache_2_way_1_memory_byte : 8'bz;  // Controlled_Buffer controlled_buffer_75
  assign in_3 = and_75_out ? data_cache_2_way_1_rwds : 1'bz;  // Controlled_Buffer controlled_buffer_76
  Bit3_Latching_Arbiter bit3_latching_arbiter_1 (
    .Reset(undriven_25), .Clock(undriven_24), .RA(instruction_cache_2_way_1_requesting_ram),
    .RB(data_cache_2_way_1_requesting_ram), .GA(bit3_latching_arbiter_1_ga), .GB(bit3_latching_arbiter_1_gb));  // open: RC, GC
  and and_76 (and_76_out, Memory_Data_Moving, bit3_latching_arbiter_1_ga);
  and and_77 (and_77_out, Memory_Data_Moving, bit3_latching_arbiter_1_gb);
  PSRAM_Controller_2 psram_controller_2_1 (
    .Clock(undriven_24), .Reset(undriven_25), .Read(in_5), .Write(in_4), .Bit8_Data(in_2),
    .Bit26_Address(Bit26_Memory_Out), .RWDS_In(in_3), .RWDS_Out(in_3), .Bit8_Out(Memory_Bit8_Data_Out),
    .Data_Moving(Memory_Data_Moving));  // open: Setup

  assign Memory_RWDS_Out = in_3;

  // Other names for the same wires on the sheet: Bit16_Path_A_Select = Bit16_Path_A_Enable;
  //   Memory_Config_Decode (some bits) = {BranchImmediate, Current_Instruction[3:0]};
  //   Current_Instruction[9:6] = BranchImmediate; Opcode[5:0] = Current_Instruction[15:10];
  //   Mem_Read_Hazard_Stall = Hardware_Interrupt; Memory_Control[5:2] = Memory_Config_Decode[14:11];
  //   WE_Memory = WE_Execute; WE_Writeback = WE_Execute

  // Notes on the sheet:
  //   note 1.3
  //   N1
  //   N2
  //   N3
  //   2A
  //   clarification in note 1.2
  //   Write Field Select
  //   Read Path A
  //   Read Path B
  //   2B
  //   disable 6 msb to b 5 (NOTE 1.1)
  //   b
  //   0=m, 1=i
  //   a
  //   ex
  //   mm
  //   B DISABLE IF A
  //   IF 00,01,or 10 then relative 32 needs to be asserted
  //   memory assert and instruction assert overrides
  //   note 1.X
  //   (add, avoiding bus contention)
  //   IA  MA 
  //   maybe just disable all possible read triggers instead of intrudicng ajnother gate delay
  //   actually just redo forwarding logic
  //   as in like 1 in ex, another in mem
  //   wb
  //   handle double half writes
  //   (high low)
  //   and so then both must be passed
  //   mem
  //   16 to 32
  //   high or low (low = 0)
  //   32 to 16
  //   A or B (0 = A)
  //   32 to 32
  //   16 to b
  //   16 to a
  //   32l
  //   B
  //   A
  //   32l
  //   B
  //   A
  //   16 to 32
  //   32 to 16
  //   A or B (0 = A)
  //   32 to 32
  //   16 to b
  //   16 to a
  //   mem
  //   32 not
  //   32h
  //   spec
  //   32h
  //   spec
  //   high or low (low = 0)
  //   32
  //   32
  //   wb
  //   anot
  //   bot
  //   32l
  //   32h
  //   mem 32
  //   exe 32
  //   memb
  //   mema
  //   exe a
  //   exe 32lh
  //   mem32lh
  //   exeb
  //   ?????????
  //   16 bit result
  //   32 bit memory
  //   32 bit result
  //   note 3.3
  //   note 3.2
  //   note 3.1
endmodule

module fulltest (
);

  core4real core4real_1 ();  // open: Bit26_Memory_Out, in_2, in_3, in_4, in_5, Memory_RWDS_Out, Memory_Bit8_Data_Out, Memory_Data_Moving
endmodule

module Bit15x8Cache (
  input  [2:0] Bit3_Query,
  input  [14:0] Bit15_Write_Value,
  input  Write_Enable,
  input  Reset_Enable,
  input  Clock,
  input  Query,
  input  Clear,
  output [14:0] Bit15_Result,
  output Value_Cached
);

  wire and_1_out, and_2_out, and_3_out, and_4_out, and_5_out, and_6_out, and_7_out, and_8_out,
       demultiplexer_1_out0, demultiplexer_1_out1, demultiplexer_1_out2, demultiplexer_1_out3,
       demultiplexer_1_out4, demultiplexer_1_out5, demultiplexer_1_out6, demultiplexer_1_out7, or_1_out,
       or_2_out;
  wire [14:0] bit_extender_1_out, controlled_buffer_1_out;
  wire [15:0] register_1_q, register_2_q, register_3_q, register_4_q, register_5_q, register_6_q,
       register_7_q, register_8_q;

  or or_1 (or_1_out, Write_Enable, Reset_Enable);
  Register #(.width(16)) register_1 (
    .D({Write_Enable, Bit15_Write_Value}), .en(and_1_out), .clk(Clock), .Q(register_1_q), .clr(Clear));
  and and_1 (and_1_out, demultiplexer_1_out0, or_1_out);
  Register #(.width(16)) register_2 (
    .D({Write_Enable, Bit15_Write_Value}), .en(and_2_out), .clk(Clock), .Q(register_2_q), .clr(Clear));
  and and_2 (and_2_out, demultiplexer_1_out1, or_1_out);
  Register #(.width(16)) register_3 (
    .D({Write_Enable, Bit15_Write_Value}), .en(and_3_out), .clk(Clock), .Q(register_3_q), .clr(Clear));
  and and_3 (and_3_out, demultiplexer_1_out2, or_1_out);
  Register #(.width(16)) register_4 (
    .D({Write_Enable, Bit15_Write_Value}), .en(and_4_out), .clk(Clock), .Q(register_4_q), .clr(Clear));
  and and_4 (and_4_out, demultiplexer_1_out3, or_1_out);
  Register #(.width(16)) register_5 (
    .D({Write_Enable, Bit15_Write_Value}), .en(and_5_out), .clk(Clock), .Q(register_5_q), .clr(Clear));
  and and_5 (and_5_out, demultiplexer_1_out4, or_1_out);
  Register #(.width(16)) register_6 (
    .D({Write_Enable, Bit15_Write_Value}), .en(and_6_out), .clk(Clock), .Q(register_6_q), .clr(Clear));
  and and_6 (and_6_out, demultiplexer_1_out5, or_1_out);
  Register #(.width(16)) register_7 (
    .D({Write_Enable, Bit15_Write_Value}), .en(and_7_out), .clk(Clock), .Q(register_7_q), .clr(Clear));
  and and_7 (and_7_out, demultiplexer_1_out6, or_1_out);
  Register #(.width(16)) register_8 (
    .D({Write_Enable, Bit15_Write_Value}), .en(and_8_out), .clk(Clock), .Q(register_8_q), .clr(Clear));
  and and_8 (and_8_out, demultiplexer_1_out7, or_1_out);
  assign {Value_Cached, controlled_buffer_1_out} = demultiplexer_1_out0 ? register_1_q : 16'bz;  // Controlled_Buffer controlled_buffer_1
  assign {Value_Cached, controlled_buffer_1_out} = demultiplexer_1_out1 ? register_2_q : 16'bz;  // Controlled_Buffer controlled_buffer_2
  assign {Value_Cached, controlled_buffer_1_out} = demultiplexer_1_out2 ? register_3_q : 16'bz;  // Controlled_Buffer controlled_buffer_3
  assign {Value_Cached, controlled_buffer_1_out} = demultiplexer_1_out3 ? register_4_q : 16'bz;  // Controlled_Buffer controlled_buffer_4
  assign {Value_Cached, controlled_buffer_1_out} = demultiplexer_1_out4 ? register_5_q : 16'bz;  // Controlled_Buffer controlled_buffer_5
  assign {Value_Cached, controlled_buffer_1_out} = demultiplexer_1_out5 ? register_6_q : 16'bz;  // Controlled_Buffer controlled_buffer_6
  assign {Value_Cached, controlled_buffer_1_out} = demultiplexer_1_out6 ? register_7_q : 16'bz;  // Controlled_Buffer controlled_buffer_7
  assign {Value_Cached, controlled_buffer_1_out} = demultiplexer_1_out7 ? register_8_q : 16'bz;  // Controlled_Buffer controlled_buffer_8
  or or_2 (or_2_out, or_1_out, Query);
  Demultiplexer #(.select(3)) demultiplexer_1 (
    .out0(demultiplexer_1_out0), .out1(demultiplexer_1_out1), .out2(demultiplexer_1_out2),
    .out3(demultiplexer_1_out3), .out4(demultiplexer_1_out4), .out5(demultiplexer_1_out5),
    .out6(demultiplexer_1_out6), .out7(demultiplexer_1_out7), .in(or_2_out), .sel(Bit3_Query));
  Pull_Resistor pull_resistor_1 (.node({Value_Cached, controlled_buffer_1_out}));
  Bit_Extender #(.in_width(16), .out_width(15), .\type ("zero")) bit_extender_1 (
    .in({Value_Cached, controlled_buffer_1_out}), .out(bit_extender_1_out));
  assign Bit15_Result = Value_Cached ? bit_extender_1_out : 15'bz;  // Controlled_Buffer controlled_buffer_9

  // Notes on the sheet:
  //   just redo this bruh
endmodule

module Forwarding_Control_Manager (
  input  [4:0] Write_Field_Execute,
  input  Write_Enable_Execute,
  input  [4:0] Write_Field_Memory,
  input  Write_Enable_Memory,
  input  [4:0] Read_Path_A,
  input  [4:0] Read_Path_B,
  input  clock,
  output [18:0] control
);

  wire n0_out, n1_out, n2_out, n3_out, n4_out, n5_out, n6_out, n7_out, n8_out, n10_out, n11_out, n12_out,
       n13_out, n14_out, n16_out, n17_out, n18_out, n19_out, n20_out, n21_out, n22_out, n23_out, n24_out,
       n25_out, n27_out, n28_out, n29_out, n30_out, n31_out, n32_out, n34_out, n35_out, n36_out, n37_out,
       n38_out, n39_out, n40_out, n42_out, n43_out, n44_out, n45_out, n46_out, n47_out, n48_out, n49_out,
       n51_out, n52_out, n53_out, n55_out, n56_out, n57_out, n58_out, n61_out, n62_out, n63_out, n66_out,
       n67_out, n68_out, n71_out, n72_out, n73_out, n74_out, n77_out, n78_out, n79_out, n81_out, n82_out,
       n83_out, n85_out, n86_out, n87_out, n89_out;
  wire [18:0] n9_out;

  and n71 (n71_out, Read_Path_A[4], Read_Path_A[3], Read_Path_A[2]);
  and n70 (n9_out[15], Write_Field_Execute[4], Write_Field_Execute[3], Write_Field_Execute[2]);
  and n66 (n66_out, Read_Path_A[4], Read_Path_A[3]);
  and n76 (n9_out[17], Write_Field_Execute[4], Write_Field_Execute[3], n38_out);
  not n6 (n6_out, Write_Field_Execute[3]);
  not n38 (n38_out, Write_Field_Execute[2]);
  and n37 (n37_out, Write_Field_Execute[4], Write_Field_Execute[3]);
  and n39 (n39_out, Write_Field_Execute[4], n38_out);
  or n40 (n40_out, n37_out, n39_out);
  xnor n4 (n4_out, Write_Field_Execute[0], Read_Path_A[0]);
  xnor n3 (n3_out, Write_Field_Execute[1], Read_Path_A[1]);
  xnor n2 (n2_out, Write_Field_Execute[2], Read_Path_A[2]);
  xnor n1 (n1_out, Write_Field_Execute[3], Read_Path_A[3]);
  xnor n0 (n0_out, Write_Field_Execute[4], Read_Path_A[4]);
  not n5 (n5_out, Write_Field_Execute[4]);
  and n7 (n7_out, Write_Field_Execute[4], Write_Field_Execute[2], n6_out);
  or n8 (n8_out, n7_out, n5_out);
  or n73 (n73_out, n71_out, n72_out);
  and n72 (n72_out, Read_Path_B[4], Read_Path_B[3], Read_Path_B[2]);
  and n9 (n9_out[0], n8_out, n4_out, n3_out, n2_out, n1_out, n0_out, Write_Enable_Execute);
  or n68 (n68_out, n66_out, n67_out);
  not n63 (n63_out, Read_Path_B[2]);
  and n51 (n51_out, n4_out, n3_out);
  and n34 (n34_out, n0_out, n1_out, n2_out, n3_out, n4_out);
  not n16 (n16_out, n9_out[0]);
  and n67 (n67_out, Read_Path_B[4], Read_Path_B[3]);
  and n78 (n78_out, n63_out, Read_Path_B[3], Read_Path_B[4]);
  or n53 (n53_out, n51_out, n52_out);
  and n54 (n9_out[6], n40_out, Write_Enable_Execute, n53_out);
  and n69 (n9_out[14], n68_out, n58_out, n56_out);
  not n89 (n89_out, n9_out[14]);
  xnor n14 (n14_out, Write_Field_Execute[0], Read_Path_B[0]);
  xnor n13 (n13_out, Write_Field_Execute[1], Read_Path_B[1]);
  xnor n12 (n12_out, Write_Field_Execute[2], Read_Path_B[2]);
  xnor n11 (n11_out, Write_Field_Execute[3], Read_Path_B[3]);
  xnor n10 (n10_out, Write_Field_Execute[4], Read_Path_B[4]);
  or n79 (n79_out, n78_out, n77_out);
  and n15 (n9_out[1], n8_out, n10_out, n11_out, n12_out, n13_out, n14_out, Write_Enable_Execute);
  and n77 (n77_out, n57_out, Read_Path_A[3], Read_Path_A[4]);
  not n57 (n57_out, Read_Path_A[2]);
  and n52 (n52_out, n14_out, n13_out);
  and n35 (n35_out, n14_out, n13_out, n12_out, n11_out, n10_out);
  or n36 (n36_out, n34_out, n35_out);
  and n41 (n9_out[4], n36_out, n40_out, Write_Enable_Execute);
  not n27 (n27_out, n9_out[1]);
  or n58 (n58_out, n37_out, n39_out, n46_out, n48_out);
  not n22 (n22_out, Write_Field_Memory[4]);
  not n23 (n23_out, Write_Field_Memory[3]);
  and n24 (n24_out, Write_Field_Memory[4], Write_Field_Memory[2], n23_out);
  or n25 (n25_out, n22_out, n24_out);
  not n42 (n42_out, n9_out[4]);
  xnor n21 (n21_out, Write_Field_Memory[0], Read_Path_A[0]);
  xnor n20 (n20_out, Write_Field_Memory[1], Read_Path_A[1]);
  xnor n19 (n19_out, Write_Field_Memory[2], Read_Path_A[2]);
  xnor n18 (n18_out, Write_Field_Memory[3], Read_Path_A[3]);
  xnor n17 (n17_out, Write_Field_Memory[4], Read_Path_A[4]);
  and n26 (n9_out[2], n16_out, Write_Enable_Memory, n21_out, n20_out, n19_out, n18_out, n17_out, n25_out);
  and n55 (n55_out, n21_out, n20_out);
  and n43 (n43_out, n17_out, n18_out, n19_out, n21_out, n20_out);
  or n56 (n56_out, n51_out, n55_out);
  and n46 (n46_out, Write_Field_Memory[4], Write_Field_Memory[3]);
  or n49 (n49_out, n46_out, n48_out);
  and n59 (n9_out[7], n56_out, n58_out, Write_Field_Memory[3], Write_Field_Memory[4], n57_out);
  and n60 (n9_out[8], n56_out, n58_out, Write_Field_Memory[3], Write_Field_Memory[4], Read_Path_A[2]);
  and n64 (n9_out[9], n63_out, Read_Path_B[3], Read_Path_B[4], n62_out, n58_out);
  and n65 (n9_out[10], Read_Path_B[3], Read_Path_B[4], Read_Path_B[2], n58_out, n62_out);
  xnor n32 (n32_out, Write_Field_Memory[0], Read_Path_B[0]);
  xnor n31 (n31_out, Write_Field_Memory[1], Read_Path_B[1]);
  xnor n30 (n30_out, Write_Field_Memory[2], Read_Path_B[2]);
  xnor n29 (n29_out, Write_Field_Memory[3], Read_Path_B[3]);
  xnor n28 (n28_out, Write_Field_Memory[4], Read_Path_B[4]);
  not n47 (n47_out, Write_Field_Memory[2]);
  and n48 (n48_out, Write_Field_Memory[4], n47_out);
  and n50 (n9_out[5], n49_out, n45_out, n42_out, Write_Enable_Memory);
  not n90 (n42_out, n9_out[5]);
  not n83 (n83_out, n9_out[2]);
  not n81 (n81_out, n9_out[7]);
  not n82 (n82_out, n9_out[8]);
  not n85 (n85_out, n9_out[9]);
  not n86 (n86_out, n9_out[10]);
  and n84 (n9_out[11], n82_out, n81_out, n83_out, n16_out);
  and n33 (n9_out[3], n25_out, n27_out, n28_out, n29_out, n30_out, n31_out, n32_out, Write_Enable_Memory);
  not n87 (n87_out, n9_out[3]);
  and n80 (n9_out[18], n79_out, n74_out);
  and n88 (n9_out[12], n86_out, n85_out, n27_out, n87_out);
  and n61 (n61_out, n32_out, n31_out);
  and n44 (n44_out, n32_out, n31_out, n30_out, n28_out, n29_out);
  or n45 (n45_out, n43_out, n44_out);
  and n74 (n74_out, n51_out, n52_out, n55_out, n61_out);
  and n75 (n9_out[16], n73_out, n74_out);
  and n91 (n9_out[13], n42_out, n42_out, n89_out);
  or n62 (n62_out, n52_out, n61_out);
  Register #(.width(19)) register_1 (.D(n9_out), .en(1'b1), .clk(clock), .Q(control));  // open: clr
endmodule

// VHDL entity the, as the project stores it:
--------------------------------------------------------------------------------
-- Project :
-- File    :
-- Autor   :
-- Date    :
--
--------------------------------------------------------------------------------
-- Description :
--
--------------------------------------------------------------------------------

LIBRARY ieee;
USE ieee.std_logic_1164.all;

ENTITY the IS
  PORT (
  ------------------------------------------------------------------------------
  --Insert input ports below
    clock      : IN  std_logic;                    -- input bit example
    val        : IN  std_logic_vector(3 DOWNTO 0); -- input vector example
  ------------------------------------------------------------------------------
  --Insert output ports below
    max        : OUT std_logic;                    -- output bit example
    cpt        : OUT std_logic_vector(3 DOWNTO 0)  -- output vector example
    );
END the;

--------------------------------------------------------------------------------
--Complete your VHDL description below
--------------------------------------------------------------------------------

ARCHITECTURE TypeArchitecture OF the IS

BEGIN


END TypeArchitecture;
