// Logisim project pleaseee.circ as structural Verilog
module core (
);

  wire alu3_1_p3, bit3_latching_arbiter_1_ga, bit3_latching_arbiter_1_gb, controlled_buffer_3_out,
       controlled_buffer_4_out, controlled_buffer_5_out, data_cache_2_way_1_ram_read,
       data_cache_2_way_1_ram_write, data_cache_2_way_1_requesting_ram, data_cache_2_way_1_rwds,
       instruction_cache_2_way_1_ram_read, instruction_cache_2_way_1_requesting_ram,
       instruction_cache_2_way_1_rwds, instruction_pointer_2_1_p2, mmu2_1_auto_memory_read_data,
       mmu2_1_auto_memory_write_data, mmu2_1_memory_read_instruction, mmu2_1_two_byte_op,
       psram_controller_2_1_data_moving, undriven, undriven_3, undriven_4, undriven_5, undriven_6,
       undriven_7, undriven_8, undriven_9, undriven_10, undriven_12, undriven_17, undriven_18, undriven_19,
       undriven_20, undriven_21, undriven_22, undriven_23, undriven_24, undriven_25, undriven_26,
       undriven_27, undriven_28, undriven_29, undriven_30, undriven_31, undriven_32, undriven_33,
       undriven_34, undriven_35, undriven_36, undriven_37, undriven_38, undriven_39, undriven_40,
       undriven_41, undriven_42, undriven_43, undriven_44, undriven_45, wide_register_file_1_p2,
       wide_register_file_1_p3, wide_register_file_1_p4, wide_register_file_1_p5, wide_register_file_1_p6,
       wide_register_file_1_p7;
  wire [1:0] undriven_14, undriven_16;
  wire [2:0] undriven_15;
  wire [3:0] undriven_2, undriven_11, undriven_13;
  wire [7:0] Context_Register_q, controlled_buffer_7_out, data_buffer_r0_1_special_8,
       data_buffer_r1_1_special_8, data_buffer_r2_1_special_8, data_cache_2_way_1_memory_byte,
       IO_MEMORY_REGISTER_q, multiplexer_4_out, Privillege_Register_q, psram_controller_2_1_bit8_out;
  wire [14:0] bit_extender_8_out;
  wire [15:0] alu3_1_p4, data_buffer_r0_1_regular_a, data_buffer_r0_1_regular_b, data_buffer_r1_1_regular_b,
       data_buffer_r2_1_regular_a, Data_To_DCache, forwarding_latch_1_bit16_held,
       forwarding_latch_2_bit16_held, From_DCache, mmu2_1_bit16_memory_out, multiplexer_1_out,
       multiplexer_2_out, multiplexer_5_out, register_file_1_readline_a, register_file_1_readline_b;
  wire [26:0] address_generation_unit_1_p1, bit_extender_1_out, bit_extender_2_out, bit_extender_3_out,
       controlled_buffer_1_out, Frame_Pointer_q, instruction_pointer_2_1_p5,
       mmu2_1_bit27_data_memory_address, mmu2_1_bit27_instruction_memory_address,
       stack_pointer_1_bit27_stack_address;
  wire [31:0] Address_To_DCache, bit_extender_4_out, bit_extender_5_out, bit_extender_6_out,
       bit_extender_7_out, data_buffer_r0_1_wide_32, forwarding_latch_1_bit32_held,
       forwarding_latch_2_bit32_held, multiplexer_3_out, multiplexer_6_out, wide_register_file_1_p1,
       wide_register_file_1_p8;

  Bit_Extender #(.in_width(32), .out_width(27), .\type ("zero")) bit_extender_1 (
    .in(wide_register_file_1_p1), .out(bit_extender_1_out));
  Bit_Extender #(.in_width(32), .out_width(27), .\type ("zero")) bit_extender_2 (
    .in(wide_register_file_1_p1), .out(bit_extender_2_out));
  Bit_Extender #(.in_width(32), .out_width(27), .\type ("zero")) bit_extender_3 (
    .in(wide_register_file_1_p1), .out(bit_extender_3_out));
  Register IO_MEMORY_REGISTER (
    .D(data_buffer_r2_1_special_8), .en(undriven_7), .clk(wide_register_file_1_p6), .Q(IO_MEMORY_REGISTER_q),
    .clr(wide_register_file_1_p7));
  Register Context_Register (
    .D(data_buffer_r2_1_special_8), .en(undriven_6), .clk(wide_register_file_1_p6), .Q(Context_Register_q),
    .clr(wide_register_file_1_p7));
  Register #(.width(27)) Frame_Pointer (
    .D(bit_extender_3_out), .en(undriven_5), .clk(wide_register_file_1_p6), .Q(Frame_Pointer_q),
    .clr(wide_register_file_1_p7));
  Register Privillege_Register (
    .D(data_buffer_r2_1_special_8), .en(undriven_4), .clk(wide_register_file_1_p6),
    .Q(Privillege_Register_q), .clr(wide_register_file_1_p7));
  Register_File register_file_1 (
    .Write_Data(data_buffer_r2_1_regular_a), .Read_Address_B(undriven_13), .Read_B_Enable(undriven_12),
    .Read_Address_A(undriven_11), .Read_A_Enable(undriven_10), .Write_Address(undriven_2),
    .Write_Enable(undriven), .Clock(wide_register_file_1_p6), .Clear_All_Registers(wide_register_file_1_p7),
    .ReadLine_A(register_file_1_readline_a), .ReadLine_B(register_file_1_readline_b));
  Stack_Pointer stack_pointer_1 (
    .Bit27_Address(bit_extender_2_out), .Set(undriven_3), .Push(undriven_9), .Pop(undriven_8),
    .Clock(wide_register_file_1_p6), .Reset(wide_register_file_1_p7),
    .Bit27_Stack_Address(stack_pointer_1_bit27_stack_address));
  // Wide_Register_File wide_register_file_1: pin names not known; wires that end beside it: wide_register_file_1_p1, wide_register_file_1_p2, wide_register_file_1_p3, wide_register_file_1_p4, wide_register_file_1_p5, wide_register_file_1_p6, wide_register_file_1_p7, wide_register_file_1_p8
  // Instruction_Pointer_2 instruction_pointer_2_1: pin names not known; wires that end beside it: bit_extender_1_out, instruction_pointer_2_1_p2, wide_register_file_1_p6, wide_register_file_1_p7, instruction_pointer_2_1_p5
  Data_Buffer_R2 data_buffer_r2_1 (
    .Bit8(data_buffer_r1_1_special_8), .Bit32(Address_To_DCache), .Bit16_A(multiplexer_2_out),
    .Special_8(data_buffer_r2_1_special_8), .Wide_32(wide_register_file_1_p1),
    .Regular_A(data_buffer_r2_1_regular_a));  // open: Write_Enable, Clock, Reset
  Data_Buffer_R1 data_buffer_r1_1 (
    .Bit8(data_buffer_r0_1_special_8), .Bit32(multiplexer_3_out), .Bit16_A(multiplexer_1_out),
    .Bit16_B(data_buffer_r0_1_regular_b), .Special_8(data_buffer_r1_1_special_8),
    .Wide_32(Address_To_DCache), .Regular_A(Data_To_DCache), .Regular_B(data_buffer_r1_1_regular_b));  // open: Write_Enable, Clock, Reset
  Multiplexer #(.width(16)) multiplexer_1 (
    .in0(data_buffer_r0_1_regular_a), .in1(alu3_1_p4), .out(multiplexer_1_out), .sel(undriven_22));
  Multiplexer #(.select(2), .width(16)) multiplexer_2 (
    .in0(Data_To_DCache), .in1(data_buffer_r1_1_regular_b), .in2(From_DCache), .out(multiplexer_2_out));  // open: in3, sel
  Multiplexer #(.width(32)) multiplexer_3 (
    .in0(data_buffer_r0_1_wide_32), .in1(bit_extender_7_out), .out(multiplexer_3_out), .sel(undriven_23));
  Data_Buffer_R0 data_buffer_r0_1 (
    .Bit8(multiplexer_4_out), .Bit32(multiplexer_6_out), .Bit16_A(multiplexer_5_out),
    .Bit16_B(register_file_1_readline_b), .Special_8(data_buffer_r0_1_special_8),
    .Wide_32(data_buffer_r0_1_wide_32), .Regular_A(data_buffer_r0_1_regular_a),
    .Regular_B(data_buffer_r0_1_regular_b));  // open: Write_Enable, Clock, Reset
  assign bit_extender_4_out = {{5{1'b0}}, instruction_pointer_2_1_p5};  // Bit_Extender bit_extender_4
  assign bit_extender_5_out = {{5{1'b0}}, stack_pointer_1_bit27_stack_address};  // Bit_Extender bit_extender_5
  Multiplexer #(.select(2), .width(8)) multiplexer_4 (
    .in0(IO_MEMORY_REGISTER_q), .in1(Context_Register_q), .in2(Privillege_Register_q),
    .out(multiplexer_4_out), .sel(undriven_14));  // open: in3
  assign bit_extender_6_out = {{5{1'b0}}, Frame_Pointer_q};  // Bit_Extender bit_extender_6
  Multiplexer #(.select(2), .width(16)) multiplexer_5 (
    .in0(register_file_1_readline_a), .in1(forwarding_latch_1_bit16_held),
    .in2(forwarding_latch_2_bit16_held), .out(multiplexer_5_out), .sel(undriven_16));  // open: in3
  Multiplexer #(.select(3), .width(32)) multiplexer_6 (
    .in0(wide_register_file_1_p8), .in1(bit_extender_4_out), .in2(bit_extender_5_out),
    .in3(bit_extender_6_out), .in4(forwarding_latch_1_bit32_held), .in5(forwarding_latch_2_bit32_held),
    .out(multiplexer_6_out), .sel(undriven_15));  // open: in6, in7
  Forwarding_Latch forwarding_latch_1 (
    .Bit32(bit_extender_7_out), .Bit16(alu3_1_p4), .Bit32_Held(forwarding_latch_1_bit32_held),
    .Bit16_Held(forwarding_latch_1_bit16_held));  // open: Write_Enable, Clock, Reset
  Forwarding_Latch forwarding_latch_2 (
    .Bit32(Address_To_DCache), .Bit16(multiplexer_2_out), .Bit32_Held(forwarding_latch_2_bit32_held),
    .Bit16_Held(forwarding_latch_2_bit16_held));  // open: Write_Enable, Clock, Reset
  AGU_Helper agu_helper_1 (
    .Bit32_In(data_buffer_r0_1_wide_32), .Scale_WE(undriven_21), .Base_WE(undriven_20), .Imm_WE(undriven_19),
    .Index_WE(undriven_18), .Clock(alu3_1_p3), .Reset(undriven_17));  // open: Scale, Base, Immediate, Index
  // ALU3 alu3_1: pin names not known; wires that end beside it: data_buffer_r0_1_regular_a, data_buffer_r0_1_regular_b, alu3_1_p3, alu3_1_p4
  assign bit_extender_7_out = {{5{1'b0}}, address_generation_unit_1_p1};  // Bit_Extender bit_extender_7
  // Address_Generation_Unit address_generation_unit_1: pin names not known; wires that end beside it: address_generation_unit_1_p1
  Register #(.width(16)) Instruction_Register ();  // open: D, en, clk, Q, clr
  Bit_Extender #(.in_width(16), .out_width(15), .\type ("zero")) bit_extender_8 (
    .in(data_buffer_r0_1_regular_a), .out(bit_extender_8_out));
  MMU2 mmu2_1 (
    .Lower_Flag_Mask_Enable(undriven_41), .Instruction_Read(undriven_42),
    .Translate_Instruction(undriven_43), .Bit27_Instruction_Address_In(instruction_pointer_2_1_p5),
    .Bit15_Target_Page(bit_extender_8_out), .Specific_Page_Management(undriven_40), .Data_Write(undriven_35),
    .Data_Read(undriven_36), .Reset(undriven_45), .Clock(undriven_44), .Allocate(undriven_37),
    .Deallocate(undriven_38), .Translate_Data(undriven_33), .Context_Switch(undriven_39),
    .Two_Byte_Operation(undriven_34), .Bit8_Context_Id(Context_Register_q),
    .Auto_Memory_Read_Data(mmu2_1_auto_memory_read_data),
    .Auto_Memory_Write_Data(mmu2_1_auto_memory_write_data), .Two_Byte_Op(mmu2_1_two_byte_op),
    .Memory_Read_Instruction(mmu2_1_memory_read_instruction),
    .Bit27_Data_Memory_Address(mmu2_1_bit27_data_memory_address), .Bit16_Memory_Out(mmu2_1_bit16_memory_out),
    .Bit27_Instruction_Memory_Address(mmu2_1_bit27_instruction_memory_address));  // open: Bit5_Lower_Flag_Mask, Enable, Bit27_Virtual_Memory_Address, Bit16_From_Memory, Stall_Core, Out_Of_Pages, Context_Max_Pages_Allocated, Multipage_Virtual_Page_Overflow, Page_Not_Allocated, Translation_Page_Not_Allocated, Fault
  Instruction_Cache_2_Way instruction_cache_2_way_1 (
    .Read(mmu2_1_memory_read_instruction), .Two_Byte_Operation(undriven_24),
    .Invalidate_Address(undriven_25), .Invalidate_Line(undriven_26), .Set(undriven_27),
    .Bit27_Address(mmu2_1_bit27_instruction_memory_address),
    .Bit8_From_Memory(psram_controller_2_1_bit8_out), .Ram_Data_Moving(psram_controller_2_1_data_moving),
    .Clock(undriven_44), .Reset(undriven_45), .Ram_Read(instruction_cache_2_way_1_ram_read),
    .Requesting_Ram(instruction_cache_2_way_1_requesting_ram), .RWDS(instruction_cache_2_way_1_rwds));  // open: Bit16_To_Core
  Data_Cache_2_Way data_cache_2_way_1 (
    .Read(mmu2_1_auto_memory_read_data), .Write(mmu2_1_auto_memory_write_data),
    .Two_Byte_Operation(mmu2_1_two_byte_op), .Flush_Address(undriven_28), .Invalidate_Address(undriven_29),
    .Flush_Line(undriven_30), .Invalidate_Line(undriven_31), .Set(undriven_32),
    .Bit27_Address(mmu2_1_bit27_data_memory_address), .Bit16_Data(mmu2_1_bit16_memory_out),
    .Bit8_From_Memory(psram_controller_2_1_bit8_out), .Ram_Data_Moving(psram_controller_2_1_data_moving),
    .Clock(undriven_44), .Reset(undriven_45), .Ram_Write(data_cache_2_way_1_ram_write),
    .Ram_Read(data_cache_2_way_1_ram_read), .Requesting_Ram(data_cache_2_way_1_requesting_ram),
    .Memory_Byte(data_cache_2_way_1_memory_byte), .RWDS(data_cache_2_way_1_rwds));  // open: Bit16_To_Core
  assign controlled_buffer_1_out = bit3_latching_arbiter_1_gb ? mmu2_1_bit27_data_memory_address : 27'bz;  // Controlled_Buffer controlled_buffer_1
  assign controlled_buffer_1_out = bit3_latching_arbiter_1_ga ? mmu2_1_bit27_instruction_memory_address : 27'bz;  // Controlled_Buffer controlled_buffer_2
  assign controlled_buffer_3_out = bit3_latching_arbiter_1_ga ? instruction_cache_2_way_1_ram_read : 1'bz;  // Controlled_Buffer controlled_buffer_3
  assign controlled_buffer_4_out = bit3_latching_arbiter_1_gb ? instruction_cache_2_way_1_rwds : 1'bz;  // Controlled_Buffer controlled_buffer_4
  assign controlled_buffer_5_out = bit3_latching_arbiter_1_gb ? data_cache_2_way_1_ram_write : 1'bz;  // Controlled_Buffer controlled_buffer_5
  assign controlled_buffer_3_out = bit3_latching_arbiter_1_gb ? data_cache_2_way_1_ram_read : 1'bz;  // Controlled_Buffer controlled_buffer_6
  assign controlled_buffer_7_out = bit3_latching_arbiter_1_gb ? data_cache_2_way_1_memory_byte : 8'bz;  // Controlled_Buffer controlled_buffer_7
  assign controlled_buffer_4_out = bit3_latching_arbiter_1_gb ? data_cache_2_way_1_rwds : 1'bz;  // Controlled_Buffer controlled_buffer_8
  Bit3_Latching_Arbiter bit3_latching_arbiter_1 (
    .Reset(undriven_45), .Clock(undriven_44), .RA(instruction_cache_2_way_1_requesting_ram),
    .RB(data_cache_2_way_1_requesting_ram), .GA(bit3_latching_arbiter_1_ga), .GB(bit3_latching_arbiter_1_gb));  // open: RC, GC
  PSRAM_Controller_2 psram_controller_2_1 (
    .Clock(undriven_44), .Reset(undriven_45), .Read(controlled_buffer_3_out),
    .Write(controlled_buffer_5_out), .Bit8_Data(controlled_buffer_7_out),
    .Bit27_Address(controlled_buffer_1_out), .RWDS_In(controlled_buffer_4_out),
    .Bit8_Out(psram_controller_2_1_bit8_out), .Data_Moving(psram_controller_2_1_data_moving));  // open: RWDS_Out, Setup

  // Notes on the sheet:
  //   8bit special wb
  //   32 wb
  //   16 wb
  //   writeback and maybe decoded
  //   control
  //   decoded logic
  //   control
  //   simplyfy control and consider fpu vs simd vs none
  //   handle flags
endmodule

module Bit16_Add (
  input  FP_Op,
  input  Carry_In,
  input  [15:0] Bit16_A,
  input  [15:0] Bit16_B,
  output [15:0] Bit16_Result,
  output Carry_Out
);

  wire and_1_out, and_2_out, and_3_out, and_4_out, and_5_out, and_6_out, and_7_out, and_8_out, and_9_out,
       and_10_out, and_11_out, and_12_out, and_13_out, and_14_out, and_15_out, and_16_out, and_17_out,
       bit4_cla_logic_1_c2, bit4_cla_logic_1_c3, bit4_cla_logic_1_c4, bit4_cla_logic_1_cout,
       bit4_cla_logic_1_pg, bit4_cla_logic_2_c2, bit4_cla_logic_2_c3, bit4_cla_logic_2_c4,
       bit4_cla_logic_2_cout, bit4_cla_logic_2_pg, bit4_cla_logic_3_c2, bit4_cla_logic_3_c3,
       bit4_cla_logic_3_c4, bit4_cla_logic_3_cout, bit4_cla_logic_3_pg, bit4_cla_logic_4_c2,
       bit4_cla_logic_4_c3, bit4_cla_logic_4_c4, bit4_cla_logic_4_cout, bit4_cla_logic_4_pg,
       bit4_cla_logic_5_c2, bit4_cla_logic_5_c3, bit4_cla_logic_5_c4, bit4_cla_logic_5_cout, xor_1_out,
       xor_2_out, xor_3_out, xor_4_out, xor_5_out, xor_6_out, xor_7_out, xor_8_out, xor_9_out, xor_10_out,
       xor_11_out, xor_12_out, xor_13_out, xor_14_out, xor_15_out, xor_16_out;

  xor xor_1 (xor_1_out, Bit16_A[0], Bit16_B[0]);
  and and_1 (and_1_out, Bit16_B[0], Bit16_A[0]);
  xor xor_2 (xor_2_out, Bit16_A[1], Bit16_B[1]);
  and and_2 (and_2_out, Bit16_B[1], Bit16_A[1]);
  xor xor_3 (xor_3_out, Bit16_A[2], Bit16_B[2]);
  and and_3 (and_3_out, Bit16_B[2], Bit16_A[2]);
  xor xor_4 (xor_4_out, Bit16_A[3], Bit16_B[3]);
  and and_4 (and_4_out, Bit16_B[3], Bit16_A[3]);
  xor xor_5 (xor_5_out, Bit16_A[4], Bit16_B[4]);
  and and_5 (and_5_out, Bit16_B[4], Bit16_A[4]);
  xor xor_6 (xor_6_out, Bit16_A[5], Bit16_B[5]);
  and and_6 (and_6_out, Bit16_B[5], Bit16_A[5]);
  xor xor_7 (xor_7_out, Bit16_A[6], Bit16_B[6]);
  and and_7 (and_7_out, Bit16_B[6], Bit16_A[6]);
  xor xor_8 (xor_8_out, Bit16_A[7], Bit16_B[7]);
  and and_8 (and_8_out, Bit16_B[7], Bit16_A[7]);
  xor xor_9 (xor_9_out, Bit16_A[8], Bit16_B[8]);
  and and_9 (and_9_out, Bit16_B[8], Bit16_A[8]);
  xor xor_10 (xor_10_out, Bit16_A[9], Bit16_B[9]);
  and and_10 (and_10_out, Bit16_B[9], Bit16_A[9]);
  xor xor_11 (xor_11_out, Bit16_A[10], Bit16_B[10]);
  and and_11 (and_11_out, Bit16_B[10], Bit16_A[10]);
  xor xor_12 (xor_12_out, Bit16_A[11], Bit16_B[11]);
  and and_12 (and_12_out, Bit16_B[11], Bit16_A[11]);
  xor xor_13 (xor_13_out, Bit16_A[12], Bit16_B[12]);
  and and_13 (and_13_out, Bit16_B[12], Bit16_A[12]);
  xor xor_14 (xor_14_out, Bit16_A[13], Bit16_B[13]);
  and and_14 (and_14_out, Bit16_B[13], Bit16_A[13]);
  xor xor_15 (xor_15_out, Bit16_A[14], Bit16_B[14]);
  and and_15 (and_15_out, Bit16_B[14], Bit16_A[14]);
  xor xor_16 (xor_16_out, Bit16_A[15], Bit16_B[15]);
  and and_16 (and_16_out, Bit16_B[15], Bit16_A[15]);
  xor xor_17 (Bit16_Result[0], Carry_In, xor_1_out);
  xor xor_18 (Bit16_Result[1], bit4_cla_logic_1_c2, xor_2_out);
  xor xor_19 (Bit16_Result[2], bit4_cla_logic_1_c3, xor_3_out);
  xor xor_20 (Bit16_Result[3], bit4_cla_logic_1_c4, xor_4_out);
  xor xor_21 (Bit16_Result[4], bit4_cla_logic_5_c2, xor_5_out);
  xor xor_22 (Bit16_Result[5], bit4_cla_logic_2_c2, xor_6_out);
  xor xor_23 (Bit16_Result[6], bit4_cla_logic_2_c3, xor_7_out);
  xor xor_24 (Bit16_Result[7], bit4_cla_logic_2_c4, xor_8_out);
  xor xor_25 (Bit16_Result[8], bit4_cla_logic_5_c3, xor_9_out);
  xor xor_26 (Bit16_Result[9], bit4_cla_logic_3_c2, xor_10_out);
  xor xor_27 (Bit16_Result[10], bit4_cla_logic_3_c3, xor_11_out);
  xor xor_28 (Bit16_Result[11], bit4_cla_logic_3_c4, xor_12_out);
  xor xor_29 (Bit16_Result[12], bit4_cla_logic_5_c4, xor_13_out);
  xor xor_30 (Bit16_Result[13], bit4_cla_logic_4_c2, xor_14_out);
  xor xor_31 (Bit16_Result[14], bit4_cla_logic_4_c3, xor_15_out);
  xor xor_32 (Bit16_Result[15], bit4_cla_logic_4_c4, xor_16_out);
  Bit4_CLA_Logic bit4_cla_logic_1 (
    .Cin(Carry_In), .P1(xor_1_out), .G1(and_1_out), .P2(xor_2_out), .G2(and_2_out), .P3(xor_3_out),
    .G3(and_3_out), .P4(xor_4_out), .G4(and_4_out), .C2(bit4_cla_logic_1_c2), .C3(bit4_cla_logic_1_c3),
    .C4(bit4_cla_logic_1_c4), .COUT(bit4_cla_logic_1_cout), .PG(bit4_cla_logic_1_pg));
  Bit4_CLA_Logic bit4_cla_logic_2 (
    .Cin(bit4_cla_logic_5_c2), .P1(xor_5_out), .G1(and_5_out), .P2(xor_6_out), .G2(and_6_out),
    .P3(xor_7_out), .G3(and_7_out), .P4(xor_8_out), .G4(and_8_out), .C2(bit4_cla_logic_2_c2),
    .C3(bit4_cla_logic_2_c3), .C4(bit4_cla_logic_2_c4), .COUT(bit4_cla_logic_2_cout), .PG(bit4_cla_logic_2_pg));
  Bit4_CLA_Logic bit4_cla_logic_3 (
    .Cin(bit4_cla_logic_5_c3), .P1(xor_9_out), .G1(and_9_out), .P2(xor_10_out), .G2(and_10_out),
    .P3(xor_11_out), .G3(and_11_out), .P4(xor_12_out), .G4(and_12_out), .C2(bit4_cla_logic_3_c2),
    .C3(bit4_cla_logic_3_c3), .C4(bit4_cla_logic_3_c4), .COUT(bit4_cla_logic_3_cout), .PG(bit4_cla_logic_3_pg));
  Bit4_CLA_Logic bit4_cla_logic_4 (
    .Cin(bit4_cla_logic_5_c4), .P1(xor_13_out), .G1(and_13_out), .P2(xor_14_out), .G2(and_14_out),
    .P3(xor_15_out), .G3(and_15_out), .P4(xor_16_out), .G4(and_16_out), .C2(bit4_cla_logic_4_c2),
    .C3(bit4_cla_logic_4_c3), .C4(bit4_cla_logic_4_c4), .COUT(bit4_cla_logic_4_cout), .PG(bit4_cla_logic_4_pg));
  Bit4_CLA_Logic bit4_cla_logic_5 (
    .Cin(Carry_In), .P1(bit4_cla_logic_1_pg), .G1(bit4_cla_logic_1_cout), .P2(bit4_cla_logic_2_pg),
    .G2(bit4_cla_logic_2_cout), .P3(bit4_cla_logic_3_pg), .G3(bit4_cla_logic_3_cout),
    .P4(bit4_cla_logic_4_pg), .G4(bit4_cla_logic_4_cout), .C2(bit4_cla_logic_5_c2), .C3(bit4_cla_logic_5_c3),
    .C4(bit4_cla_logic_5_c4), .COUT(bit4_cla_logic_5_cout));  // open: PG
  and and_17 (and_17_out, Bit16_Result[11], FP_Op);
  or or_1 (Carry_Out, bit4_cla_logic_5_cout, and_17_out);
endmodule

module Bit16_ALU (
  input  in_1,
  input  in_2,
  input  Clock,
  input  [4:0] Bit5_Opcode,
  input  Signed_Integer_Operation,
  input  [15:0] Bit16_A,
  input  [15:0] Bit16_B,
  input  in_8,
  input  fpop,
  input  [3:0] PLACEHOLDER,
  input  [15:0] PLACEHOLDER2,
  input  in_12,
  input  [15:0] in_13,
  input  [15:0] in_14,
  input  in_15,
  input  [23:0] in_16,
  input  [23:0] in_17,
  input  in_18,
  input  in_19,
  output CPU_WAIT_FOR_ALU_OP,
  output Carry,
  output Borrow,
  output Negative,
  output Overflow,
  output Zero,
  output [15:0] out_26,
  output out_27,
  output [23:0] out_28,
  output [23:0] out_29
);

  wire and_1_out, and_2_out, and_3_out, and_4_out, and_5_out, and_6_out, and_7_out, and_8_out, and_9_out,
       and_10_out, and_11_out, and_12_out, and_13_out, and_14_out, and_15_out, and_16_out, and_17_out,
       and_18_out, and_19_out, and_20_out, and_21_out, and_22_out, and_23_out, and_24_out, and_25_out,
       and_26_out, and_27_out, and_28_out, and_29_out, and_30_out, and_31_out, and_32_out, and_33_out,
       and_34_out, bit5_adder_1_cout, bit24_adder_1_bit16_c_out, bit24_adder_1_c_out,
       bit24_adder_2_bit16_c_out, bit24_adder_2_c_out, d_ff_2_qn, d_ff_3_qn, d_ff_4_qn, d_ff_5_qn, d_ff_6_qn,
       demultiplexer_1_out1, demultiplexer_1_out2, demultiplexer_1_out4, demultiplexer_1_out11,
       demultiplexer_2_out0, demultiplexer_2_out1, demultiplexer_2_out2, demultiplexer_2_out3,
       demultiplexer_2_out4, demultiplexer_2_out5, demultiplexer_2_out6, demultiplexer_2_out7,
       demultiplexer_2_out8, demultiplexer_2_out9, demultiplexer_2_out10, demultiplexer_2_out11,
       demultiplexer_2_out12, demultiplexer_2_out13, demultiplexer_2_out14, demultiplexer_2_out15,
       demultiplexer_2_out16, demultiplexer_2_out17, demultiplexer_2_out18, demultiplexer_2_out19,
       demultiplexer_2_out20, demultiplexer_2_out21, demultiplexer_2_out22, demultiplexer_2_out23,
       demultiplexer_3_out0, demultiplexer_3_out1, demultiplexer_3_out2, demultiplexer_3_out3,
       demultiplexer_3_out4, demultiplexer_3_out5, demultiplexer_3_out6, demultiplexer_3_out7,
       demultiplexer_3_out8, demultiplexer_3_out9, demultiplexer_3_out10, demultiplexer_3_out11,
       demultiplexer_3_out12, demultiplexer_3_out13, demultiplexer_3_out14, demultiplexer_3_out15,
       demultiplexer_3_out16, demultiplexer_3_out17, demultiplexer_3_out18, demultiplexer_3_out19,
       demultiplexer_3_out20, demultiplexer_3_out21, demultiplexer_3_out22, demultiplexer_3_out23, nor_1_out,
       not_1_out, not_2_out, not_3_out, not_4_out, not_5_out, not_6_out, not_7_out, not_8_out, or_1_out,
       or_2_out, or_3_out, or_4_out, or_8_out, or_13_out;
  wire [0:0] or_14_out;
  wire [3:0] bit4_controlled_buffer_1_bit4_out, bit4_controlled_buffer_2_bit4_out,
       bit4_twos_complementer_1_bit4_result, bit5_adder_1_bit5_result, or_6_out;
  wire [4:0] bit5_twos_complementer_1_bit5_result, d_ff_6_q;
  wire [4:4] bit5_adder_1_bit5_result_2;
  wire [14:0] undriven_2;
  wire [15:0] bit16_controlled_buffer_1_bit16_out, bit16_controlled_buffer_2_bit16_out,
       bit16_multiplier_1_lower_word, bit16_multiplier_1_upper_word, or_5_out,
       twos_complementer_1_bit16_result, twos_complementer_2_bit16_result;
  wire [15:10] undriven;
  wire [23:0] bit16_to_bit24_1_bit24, bit16_to_bit24_2_bit24, bit16_to_bit24_3_bit24, bit16_to_bit24_4_bit24,
       bit16t24_right_shift_1_bit24_result, bit24_adder_1_bit24_result, bit24_adder_2_bit24_result,
       bit24_controlled_buffer_1_bit24_out, bit24_controlled_buffer_2_bit24_out,
       bit24_controlled_buffer_3_bit24_out, bit24_controlled_buffer_4_bit24_out,
       bit24_controlled_buffer_5_bit24_out, bit24_controlled_buffer_6_bit24_out,
       bit24_controlled_buffer_7_bit24_out, bit24_controlled_buffer_8_bit24_out,
       bit24_divider_1_bit24_adder_a, bit24_divider_1_bit24_adder_b, or_7_out, or_10_out, or_11_out,
       or_12_out, register_1_q, s_r_ff_24_q;

  // Probe on in_13[14:10]
  // Probe on in_13[14:10]
  // Probe on in_13[14:10]
  // Probe on in_14[14:10]
  // Probe on in_14[14:10]
  // Probe on in_14[14:10]
  Bit5_Twos_Complementer bit5_twos_complementer_1 (
    .Bit5_In(in_14[14:10]), .Bit5_Result(bit5_twos_complementer_1_bit5_result));
  // Probe on {bit5_adder_1_bit5_result_2[4], bit5_adder_1_bit5_result}
  // Probe on {bit5_adder_1_bit5_result_2[4], bit5_adder_1_bit5_result}
  // Probe on {bit5_adder_1_bit5_result_2[4], bit5_adder_1_bit5_result}
  Bit5_Adder bit5_adder_1 (
    .Cin(in_12), .Bit5_A(in_13[14:10]), .Bit5_B(bit5_twos_complementer_1_bit5_result),
    .Bit5_Result({bit5_adder_1_bit5_result_2[4], bit5_adder_1_bit5_result}), .Cout(bit5_adder_1_cout));
  // Probe on {6'b000001, in_14[9:0]}
  // Probe on {6'b000001, in_14[9:0]}
  // Probe on {6'b000001, in_14[9:0]}
  // Probe on {6'b000001, in_13[9:0]}
  // Probe on {6'b000001, in_13[9:0]}
  // Probe on {6'b000001, in_13[9:0]}
  D_Flip_Flop #(.trigger("falling")) d_ff_1 (.clk(in_2));  // open: D, Q, Qn, preset, reset
  // Probe on Bit16_A
  // Probe on Bit16_B
  Demultiplexer #(.select(4)) demultiplexer_1 (
    .out1(demultiplexer_1_out1), .out2(demultiplexer_1_out2), .out4(demultiplexer_1_out4),
    .out11(demultiplexer_1_out11), .in(not_1_out), .sel(Bit5_Opcode[3:0]));  // open: out0, out3, out5, out6, out7, out8, out9, out10, out12, out13, out14, out15
  not not_1 (not_1_out, Bit5_Opcode[4]);
  // Probe on {in_8, undriven_2}
  and and_1 (and_1_out, fpop, ~bit5_adder_1_cout);  // AND_Gate
  and and_2 (and_2_out, fpop, bit5_adder_1_cout);
  and and_3 (and_3_out, ~Bit5_Opcode[2], Bit5_Opcode[3], not_1_out);  // AND_Gate
  and and_4 (and_4_out, Bit5_Opcode[3], not_1_out, ~Bit5_Opcode[2], or_2_out);  // AND_Gate
  Bit4_Twos_Complementer bit4_twos_complementer_1 (
    .Bit4_In(bit5_adder_1_bit5_result), .Bit4_Result(bit4_twos_complementer_1_bit4_result));
  not not_2 (not_2_out, bit5_adder_1_bit5_result_2[4]);
  or or_1 (or_1_out, demultiplexer_1_out1, demultiplexer_1_out2);
  or or_2 (or_2_out, demultiplexer_1_out4, demultiplexer_1_out11);
  or or_3 (or_3_out, and_4_out, and_3_out, Signed_Integer_Operation);
  or or_4 (or_4_out, and_4_out, Signed_Integer_Operation);
  Demultiplexer #(.select(5)) demultiplexer_2 (
    .out0(demultiplexer_2_out0), .out1(demultiplexer_2_out1), .out2(demultiplexer_2_out2),
    .out3(demultiplexer_2_out3), .out4(demultiplexer_2_out4), .out5(demultiplexer_2_out5),
    .out6(demultiplexer_2_out6), .out7(demultiplexer_2_out7), .out8(demultiplexer_2_out8),
    .out9(demultiplexer_2_out9), .out10(demultiplexer_2_out10), .out11(demultiplexer_2_out11),
    .out12(demultiplexer_2_out12), .out13(demultiplexer_2_out13), .out14(demultiplexer_2_out14),
    .out15(demultiplexer_2_out15), .out16(demultiplexer_2_out16), .out17(demultiplexer_2_out17),
    .out18(demultiplexer_2_out18), .out19(demultiplexer_2_out19), .out20(demultiplexer_2_out20),
    .out21(demultiplexer_2_out21), .out22(demultiplexer_2_out22), .out23(demultiplexer_2_out23),
    .in(and_5_out), .sel(d_ff_6_q));  // open: out24, out25, out26, out27, out28, out29, out30, out31
  and and_5 (and_5_out, or_13_out, or_2_out);
  Bit16_Controlled_Buffer bit16_controlled_buffer_1 (
    .Enable(and_2_out), .Bit16_In({6'b000001, in_14[9:0]}), .Bit16_Out(bit16_controlled_buffer_1_bit16_out));
  Bit16_Controlled_Buffer bit16_controlled_buffer_2 (
    .Enable(and_1_out), .Bit16_In({6'b000001, in_13[9:0]}), .Bit16_Out(bit16_controlled_buffer_2_bit16_out));
  Bit4_Controlled_Buffer bit4_controlled_buffer_1 (
    .Bit4_In(bit4_twos_complementer_1_bit4_result), .Enable(bit5_adder_1_bit5_result_2[4]),
    .Bit4_Out(bit4_controlled_buffer_1_bit4_out));
  Bit4_Controlled_Buffer bit4_controlled_buffer_2 (
    .Bit4_In(bit5_adder_1_bit5_result), .Enable(not_2_out), .Bit4_Out(bit4_controlled_buffer_2_bit4_out));
  S_R_Flip_Flop s_r_ff_1 (
    .S(demultiplexer_2_out23), .R(in_1), .clk(and_6_out), .Q(s_r_ff_24_q[23]), .reset(not_4_out));  // open: Qn, preset
  not not_3 (not_3_out, or_2_out);
  assign or_5_out = bit16_controlled_buffer_1_bit16_out | PLACEHOLDER2 | bit16_controlled_buffer_2_bit16_out;  // OR_Gate or_5, 16 bits wide
  assign or_6_out = bit4_controlled_buffer_1_bit4_out | PLACEHOLDER | bit4_controlled_buffer_2_bit4_out;  // OR_Gate or_6, 4 bits wide
  // Probe on or_6_out
  // Probe on or_6_out
  // Probe on or_6_out
  S_R_Flip_Flop s_r_ff_2 (
    .S(demultiplexer_2_out22), .R(in_1), .clk(and_6_out), .Q(s_r_ff_24_q[22]), .reset(not_4_out));  // open: Qn, preset
  nor nor_1 (nor_1_out, d_ff_6_q[4], d_ff_6_q[3], d_ff_6_q[2], d_ff_6_q[1], ~or_2_out);  // NOR_Gate
  and and_6 (and_6_out, or_2_out, Clock);
  not not_4 (not_4_out, or_2_out);
  Bit16_To_Bit24 bit16_to_bit24_1 (.Bit24(bit16_to_bit24_1_bit24));  // open: Bit16
  Bit16_To_Bit24 bit16_to_bit24_2 (.Bit24(bit16_to_bit24_2_bit24));  // open: Bit16
  D_Flip_Flop #(.trigger("falling")) d_ff_2 (
    .D(d_ff_2_qn), .clk(and_6_out), .Q(d_ff_6_q[4]), .Qn(d_ff_2_qn), .reset(not_4_out));  // open: preset
  Bit24_Controlled_Buffer bit24_controlled_buffer_1 (
    .Enable(not_3_out), .Bit24_In(bit16_to_bit24_3_bit24), .Bit24_Out(bit24_controlled_buffer_1_bit24_out));
  Bit16_To_Bit24 bit16_to_bit24_3 (.Bit24(bit16_to_bit24_3_bit24));  // open: Bit16
  Twos_Complementer twos_complementer_1 (
    .Cut_MSB(or_3_out), .Bit16_Input(Bit16_A), .Bit16_Result(twos_complementer_1_bit16_result));  // open: Floating_Point_Bit_Strip, Allow_Twos_Complement
  Twos_Complementer twos_complementer_2 (
    .Cut_MSB(or_4_out), .Allow_Twos_Complement(demultiplexer_1_out2), .Bit16_Input(Bit16_B),
    .Bit16_Result(twos_complementer_2_bit16_result));  // open: Floating_Point_Bit_Strip
  S_R_Flip_Flop s_r_ff_3 (
    .S(demultiplexer_2_out21), .R(in_1), .clk(and_6_out), .Q(s_r_ff_24_q[21]), .reset(not_4_out));  // open: Qn, preset
  D_Flip_Flop #(.trigger("falling")) d_ff_3 (
    .D(d_ff_3_qn), .clk(d_ff_6_q[4]), .Q(d_ff_6_q[3]), .Qn(d_ff_3_qn), .reset(not_4_out));  // open: preset
  assign or_7_out = register_1_q | bit24_controlled_buffer_1_bit24_out;  // OR_Gate or_7, 24 bits wide
  Bit24_Adder bit24_adder_1 (
    .Bit24_A(bit24_divider_1_bit24_adder_a), .Bit24_B(bit24_divider_1_bit24_adder_b),
    .Bit16_C_OUT(bit24_adder_1_bit16_c_out), .Bit24_Result(bit24_adder_1_bit24_result),
    .C_OUT(bit24_adder_1_c_out));  // open: C_In
  S_R_Flip_Flop s_r_ff_4 (
    .S(demultiplexer_2_out20), .R(in_1), .clk(and_6_out), .Q(s_r_ff_24_q[20]), .reset(not_4_out));  // open: Qn, preset
  D_Flip_Flop #(.trigger("falling")) d_ff_4 (
    .D(d_ff_4_qn), .clk(d_ff_6_q[3]), .Q(d_ff_6_q[2]), .Qn(d_ff_4_qn), .reset(not_4_out));  // open: preset
  // Probe on bit16t24_right_shift_1_bit24_result
  // Probe on bit16t24_right_shift_1_bit24_result
  // Probe on bit16t24_right_shift_1_bit24_result
  Bit16T24_Right_Shift bit16t24_right_shift_1 (
    .Bit16_Data(or_5_out), .Bit4_Shift(or_6_out), .Bit24_Result(bit16t24_right_shift_1_bit24_result),
    .Bit16_Result(out_26));  // open: Shift_Overflow_For_Bit16
  Bit24_Divider bit24_divider_1 (
    .Clock(in_15), .Bit24_Dividend(in_16), .Bit24_Divisor(in_17), .Int_Div(in_19), .FLOAT_Div(in_18),
    .Bit16_C_Out_Adder(bit24_adder_1_bit16_c_out), .Bit24_Result(bit24_adder_1_bit24_result),
    .C_Out_Adder(bit24_adder_1_c_out), .Divider_Running(out_27), .Bit24_Remainder(out_28),
    .Bit24_Quotient(out_29), .Bit24_Adder_A(bit24_divider_1_bit24_adder_a),
    .Bit24_Adder_B(bit24_divider_1_bit24_adder_b));
  S_R_Flip_Flop s_r_ff_5 (
    .S(demultiplexer_2_out19), .R(in_1), .clk(and_6_out), .Q(s_r_ff_24_q[19]), .reset(not_4_out));  // open: Qn, preset
  Demultiplexer #(.select(5)) demultiplexer_3 (
    .out0(demultiplexer_3_out0), .out1(demultiplexer_3_out1), .out2(demultiplexer_3_out2),
    .out3(demultiplexer_3_out3), .out4(demultiplexer_3_out4), .out5(demultiplexer_3_out5),
    .out6(demultiplexer_3_out6), .out7(demultiplexer_3_out7), .out8(demultiplexer_3_out8),
    .out9(demultiplexer_3_out9), .out10(demultiplexer_3_out10), .out11(demultiplexer_3_out11),
    .out12(demultiplexer_3_out12), .out13(demultiplexer_3_out13), .out14(demultiplexer_3_out14),
    .out15(demultiplexer_3_out15), .out16(demultiplexer_3_out16), .out17(demultiplexer_3_out17),
    .out18(demultiplexer_3_out18), .out19(demultiplexer_3_out19), .out20(demultiplexer_3_out20),
    .out21(demultiplexer_3_out21), .out22(demultiplexer_3_out22), .out23(demultiplexer_3_out23),
    .sel(d_ff_6_q));  // open: out24, out25, out26, out27, out28, out29, out30, out31, in
  D_Flip_Flop #(.trigger("falling")) d_ff_5 (
    .D(d_ff_5_qn), .clk(d_ff_6_q[2]), .Q(d_ff_6_q[1]), .Qn(d_ff_5_qn), .reset(not_4_out));  // open: preset
  Bit16_To_Bit24 bit16_to_bit24_4 (.Bit24(bit16_to_bit24_4_bit24));  // open: Bit16
  not not_5 (not_5_out, and_1_out);
  not not_6 (not_6_out, and_2_out);
  S_R_Flip_Flop s_r_ff_6 (
    .S(demultiplexer_2_out18), .R(in_1), .clk(and_6_out), .Q(s_r_ff_24_q[18]), .reset(not_4_out));  // open: Qn, preset
  D_Flip_Flop #(.trigger("falling")) d_ff_6 (
    .D(d_ff_6_qn), .clk(d_ff_6_q[1]), .Q(d_ff_6_q[0]), .Qn(d_ff_6_qn));  // open: preset, reset
  not not_7 (not_7_out, or_2_out);
  not not_8 (not_8_out, or_13_out);
  S_R_Flip_Flop s_r_ff_7 (
    .S(demultiplexer_2_out17), .R(in_1), .clk(and_6_out), .Q(s_r_ff_24_q[17]), .reset(not_4_out));  // open: Qn, preset
  Register #(.trigger("falling"), .width(24)) register_1 (
    .D({or_10_out[22:0], or_14_out[0]}), .en(or_2_out), .clk(and_6_out), .Q(register_1_q), .clr(or_8_out));
  or or_8 (or_8_out, not_7_out, not_4_out);
  S_R_Flip_Flop s_r_ff_8 (
    .S(demultiplexer_2_out16), .R(in_1), .clk(and_6_out), .Q(s_r_ff_24_q[16]), .reset(not_4_out));  // open: Qn, preset
  and and_7 (and_7_out, ~d_ff_6_q[4], d_ff_6_q[3], d_ff_6_q[2], d_ff_6_q[1], d_ff_6_q[0], demultiplexer_1_out4);  // AND_Gate
  and and_8 (and_8_out, d_ff_6_q[4], d_ff_6_q[3], ~d_ff_6_q[2], ~d_ff_6_q[1], ~d_ff_6_q[0], demultiplexer_1_out11);  // AND_Gate
  Bit24_Controlled_Buffer bit24_controlled_buffer_2 (
    .Enable(and_1_out), .Bit24_In(bit16t24_right_shift_1_bit24_result),
    .Bit24_Out(bit24_controlled_buffer_2_bit24_out));
  Bit24_Controlled_Buffer bit24_controlled_buffer_3 (
    .Enable(or_1_out), .Bit24_In(bit16_to_bit24_4_bit24), .Bit24_Out(bit24_controlled_buffer_3_bit24_out));
  Bit24_Controlled_Buffer bit24_controlled_buffer_4 (
    .Enable(and_2_out), .Bit24_In(bit16t24_right_shift_1_bit24_result),
    .Bit24_Out(bit24_controlled_buffer_4_bit24_out));
  Bit24_Controlled_Buffer bit24_controlled_buffer_5 (
    .Enable(not_5_out), .Bit24_In(bit16_to_bit24_2_bit24), .Bit24_Out(bit24_controlled_buffer_5_bit24_out));
  Bit24_Controlled_Buffer bit24_controlled_buffer_6 (
    .Enable(not_6_out), .Bit24_In(bit16_to_bit24_1_bit24), .Bit24_Out(bit24_controlled_buffer_6_bit24_out));
  S_R_Flip_Flop s_r_ff_9 (
    .S(demultiplexer_2_out15), .R(in_1), .clk(and_6_out), .Q(s_r_ff_24_q[15]), .reset(not_4_out));  // open: Qn, preset
  or or_9 (CPU_WAIT_FOR_ALU_OP, and_7_out, and_8_out);
  Bit24_Controlled_Buffer bit24_controlled_buffer_7 (
    .Enable(not_8_out), .Bit24_In(register_1_q), .Bit24_Out(bit24_controlled_buffer_7_bit24_out));
  Bit24_Controlled_Buffer bit24_controlled_buffer_8 (
    .Enable(or_13_out), .Bit24_In(bit24_adder_2_bit24_result), .Bit24_Out(bit24_controlled_buffer_8_bit24_out));
  S_R_Flip_Flop s_r_ff_10 (
    .S(demultiplexer_2_out14), .R(in_1), .clk(and_6_out), .Q(s_r_ff_24_q[14]), .reset(not_4_out));  // open: Qn, preset
  and and_9 (and_9_out, demultiplexer_3_out23, bit16_to_bit24_3_bit24[23]);
  and and_10 (and_10_out, demultiplexer_3_out22, bit16_to_bit24_3_bit24[22]);
  assign or_10_out = bit24_controlled_buffer_7_bit24_out | bit24_controlled_buffer_8_bit24_out;  // OR_Gate or_10, 24 bits wide
  assign or_11_out = or_7_out | bit24_controlled_buffer_5_bit24_out | bit24_controlled_buffer_2_bit24_out;  // OR_Gate or_11, 24 bits wide
  assign or_12_out = bit24_controlled_buffer_3_bit24_out | bit24_controlled_buffer_6_bit24_out | bit24_controlled_buffer_4_bit24_out;  // OR_Gate or_12, 24 bits wide
  and and_11 (and_11_out, demultiplexer_3_out21, bit16_to_bit24_3_bit24[21]);
  and and_12 (and_12_out, demultiplexer_3_out20, bit16_to_bit24_3_bit24[20]);
  S_R_Flip_Flop s_r_ff_11 (
    .S(demultiplexer_2_out13), .R(in_1), .clk(and_6_out), .Q(s_r_ff_24_q[13]), .reset(not_4_out));  // open: Qn, preset
  and and_13 (and_13_out, demultiplexer_3_out19, bit16_to_bit24_3_bit24[19]);
  and and_14 (and_14_out, demultiplexer_3_out18, bit16_to_bit24_3_bit24[18]);
  and and_15 (and_15_out, demultiplexer_3_out17, bit16_to_bit24_3_bit24[17]);
  S_R_Flip_Flop s_r_ff_12 (
    .S(demultiplexer_2_out12), .R(in_1), .clk(and_6_out), .Q(s_r_ff_24_q[12]), .reset(not_4_out));  // open: Qn, preset
  and and_16 (and_16_out, demultiplexer_3_out16, bit16_to_bit24_3_bit24[16]);
  and and_17 (and_17_out, demultiplexer_3_out15, bit16_to_bit24_3_bit24[15]);
  and and_18 (and_18_out, demultiplexer_3_out14, bit16_to_bit24_3_bit24[14]);
  or or_13 (or_13_out, and_19_out, and_22_out);
  and and_19 (and_19_out, demultiplexer_1_out11, bit24_adder_2_c_out);
  Bit24_Adder bit24_adder_2 (
    .Bit24_A(or_11_out), .Bit24_B(or_12_out), .Bit16_C_OUT(bit24_adder_2_bit16_c_out),
    .Bit24_Result(bit24_adder_2_bit24_result), .C_OUT(bit24_adder_2_c_out));  // open: C_In
  S_R_Flip_Flop s_r_ff_13 (
    .S(demultiplexer_2_out11), .R(in_1), .clk(and_6_out), .Q(s_r_ff_24_q[11]), .reset(not_4_out));  // open: Qn, preset
  and and_20 (and_20_out, demultiplexer_3_out13, bit16_to_bit24_3_bit24[13]);
  and and_21 (and_21_out, demultiplexer_3_out12, bit16_to_bit24_3_bit24[12]);
  and and_22 (and_22_out, demultiplexer_1_out4, bit24_adder_2_bit16_c_out);
  S_R_Flip_Flop s_r_ff_14 (
    .S(demultiplexer_2_out10), .R(in_1), .clk(and_6_out), .Q(s_r_ff_24_q[10]), .reset(not_4_out));  // open: Qn, preset
  and and_23 (and_23_out, demultiplexer_3_out11, bit16_to_bit24_3_bit24[11]);
  and and_24 (and_24_out, demultiplexer_3_out10, bit16_to_bit24_3_bit24[10]);
  and and_25 (and_25_out, demultiplexer_3_out9, bit16_to_bit24_3_bit24[9]);
  S_R_Flip_Flop s_r_ff_15 (
    .S(demultiplexer_2_out9), .R(in_1), .clk(and_6_out), .Q(s_r_ff_24_q[9]), .reset(not_4_out));  // open: Qn, preset
  and and_26 (and_26_out, demultiplexer_3_out8, bit16_to_bit24_3_bit24[8]);
  and and_27 (and_27_out, demultiplexer_3_out7, bit16_to_bit24_3_bit24[7]);
  and and_28 (and_28_out, demultiplexer_3_out6, bit16_to_bit24_3_bit24[6]);
  S_R_Flip_Flop s_r_ff_16 (
    .S(demultiplexer_2_out8), .R(in_1), .clk(and_6_out), .Q(s_r_ff_24_q[8]), .reset(not_4_out));  // open: Qn, preset
  and and_29 (and_29_out, demultiplexer_3_out5, bit16_to_bit24_3_bit24[5]);
  and and_30 (and_30_out, demultiplexer_3_out4, bit16_to_bit24_3_bit24[4]);
  Bit16_Controlled_Buffer bit16_controlled_buffer_3 (.Bit16_In({undriven, undriven_2[9:0]}));  // open: Enable, Bit16_Out
  S_R_Flip_Flop s_r_ff_17 (
    .S(demultiplexer_2_out7), .R(in_1), .clk(and_6_out), .Q(s_r_ff_24_q[7]), .reset(not_4_out));  // open: Qn, preset
  and and_31 (and_31_out, demultiplexer_3_out3, bit16_to_bit24_3_bit24[3]);
  and and_32 (and_32_out, demultiplexer_3_out2, bit16_to_bit24_3_bit24[2]);
  and and_33 (and_33_out, demultiplexer_3_out1, bit16_to_bit24_3_bit24[1]);
  S_R_Flip_Flop s_r_ff_18 (
    .S(demultiplexer_2_out6), .R(in_1), .clk(and_6_out), .Q(s_r_ff_24_q[6]), .reset(not_4_out));  // open: Qn, preset
  and and_34 (and_34_out, demultiplexer_3_out0, bit16_to_bit24_3_bit24[0]);
  or or_14 (or_14_out[0], and_34_out, and_33_out, and_32_out, and_31_out, and_30_out, and_29_out, and_28_out, and_27_out, and_26_out, and_25_out, and_24_out, and_23_out, and_21_out, and_20_out, and_18_out, and_17_out, and_16_out, and_15_out, and_14_out, and_13_out, and_12_out, and_11_out, and_10_out, and_9_out);
  S_R_Flip_Flop s_r_ff_19 (
    .S(demultiplexer_2_out5), .R(in_1), .clk(and_6_out), .Q(s_r_ff_24_q[5]), .reset(not_4_out));  // open: Qn, preset
  S_R_Flip_Flop s_r_ff_20 (
    .S(demultiplexer_2_out4), .R(in_1), .clk(and_6_out), .Q(s_r_ff_24_q[4]), .reset(not_4_out));  // open: Qn, preset
  S_R_Flip_Flop s_r_ff_21 (
    .S(demultiplexer_2_out3), .R(in_1), .clk(and_6_out), .Q(s_r_ff_24_q[3]), .reset(not_4_out));  // open: Qn, preset
  S_R_Flip_Flop s_r_ff_22 (
    .S(demultiplexer_2_out2), .R(in_1), .clk(and_6_out), .Q(s_r_ff_24_q[2]), .reset(not_4_out));  // open: Qn, preset
  Bit16_Multiplier bit16_multiplier_1 (
    .Lower_Word(bit16_multiplier_1_lower_word), .Upper_Word(bit16_multiplier_1_upper_word));  // open: Bit16_B, Bit16_A
  S_R_Flip_Flop s_r_ff_23 (
    .S(demultiplexer_2_out1), .R(in_1), .clk(and_6_out), .Q(s_r_ff_24_q[1]), .reset(not_4_out));  // open: Qn, preset
  S_R_Flip_Flop s_r_ff_24 (
    .S(demultiplexer_2_out0), .R(in_1), .clk(and_6_out), .Q(s_r_ff_24_q[0]), .reset(not_4_out));  // open: Qn, preset
  Bit16_Controlled_Buffer bit16_controlled_buffer_4 (.Bit16_In(bit16_multiplier_1_lower_word));  // open: Enable, Bit16_Out
  Bit16_Controlled_Buffer bit16_controlled_buffer_5 (.Bit16_In(bit16_multiplier_1_upper_word));  // open: Enable, Bit16_Out

  // Notes on the sheet:
  //   FP OP
  //   FP DIV
  //   FDIV
  //   IDIV
  //   this line may go low 1 clock before its meant to
  //   unsigned subtraction carry
  //   LSB IS FAR LEFT. SPLITTER NEEDS INVERSION
endmodule

module Twos_Complementer (
  input  Floating_Point_Bit_Strip,
  input  Cut_MSB,
  input  Allow_Twos_Complement,
  input  [15:0] Bit16_Input,
  output [15:0] Bit16_Result
);

  wire and_1_out, and_2_out, and_3_out, and_4_out, and_5_out, and_6_out, and_7_out, and_8_out, and_9_out,
       and_10_out, and_11_out, and_12_out, and_13_out, and_14_out, and_15_out, or_1_out, or_2_out, or_3_out,
       or_4_out, or_5_out, or_6_out, or_7_out, or_8_out, or_9_out, or_10_out, or_11_out, or_12_out,
       or_13_out, or_14_out, or_15_out, xor_10_out, xor_11_out, xor_12_out, xor_13_out, xor_14_out,
       xor_15_out;

  or or_1 (or_1_out, Floating_Point_Bit_Strip, Cut_MSB);
  and and_1 (and_1_out, Bit16_Input[0], Allow_Twos_Complement);
  and and_2 (and_2_out, Bit16_Result[1], Allow_Twos_Complement);
  or or_2 (or_2_out, and_1_out, and_2_out);
  and and_3 (and_3_out, Bit16_Result[2], Allow_Twos_Complement);
  or or_3 (or_3_out, and_1_out, and_2_out, and_3_out);
  and and_4 (and_4_out, Bit16_Result[3], Allow_Twos_Complement);
  or or_4 (or_4_out, and_1_out, and_2_out, and_3_out, and_4_out);
  and and_5 (and_5_out, Bit16_Result[4], Allow_Twos_Complement);
  or or_5 (or_5_out, and_1_out, and_2_out, and_3_out, and_4_out, and_5_out);
  and and_6 (and_6_out, Bit16_Result[5], Allow_Twos_Complement);
  or or_6 (or_6_out, and_1_out, and_2_out, and_3_out, and_4_out, and_5_out, and_6_out);
  and and_7 (and_7_out, Bit16_Result[6], Allow_Twos_Complement);
  or or_7 (or_7_out, and_1_out, and_2_out, and_3_out, and_4_out, and_5_out, and_6_out, and_7_out);
  and and_8 (and_8_out, Bit16_Result[7], Allow_Twos_Complement);
  or or_8 (or_8_out, and_1_out, and_2_out, and_3_out, and_4_out, and_5_out, and_6_out, and_7_out, and_8_out);
  and and_9 (and_9_out, Bit16_Result[8], Allow_Twos_Complement);
  or or_9 (or_9_out, and_1_out, and_2_out, and_3_out, and_4_out, and_5_out, and_6_out, and_7_out, and_8_out, and_9_out);
  and and_10 (and_10_out, Bit16_Result[9], Allow_Twos_Complement);
  or or_10 (or_10_out, and_1_out, and_2_out, and_3_out, and_4_out, and_5_out, and_6_out, and_7_out, and_8_out, and_9_out, and_10_out);
  and and_11 (and_11_out, xor_10_out, Allow_Twos_Complement);
  or or_11 (or_11_out, and_1_out, and_2_out, and_3_out, and_4_out, and_5_out, and_6_out, and_7_out, and_8_out, and_9_out, and_10_out, and_11_out);
  and and_12 (and_12_out, xor_11_out, Allow_Twos_Complement);
  or or_12 (or_12_out, and_1_out, and_2_out, and_3_out, and_4_out, and_5_out, and_6_out, and_7_out, and_8_out, and_9_out, and_10_out, and_11_out, and_12_out);
  and and_13 (and_13_out, xor_12_out, Allow_Twos_Complement);
  or or_13 (or_13_out, and_1_out, and_2_out, and_3_out, and_4_out, and_5_out, and_6_out, and_7_out, and_8_out, and_9_out, and_10_out, and_11_out, and_12_out, and_13_out);
  and and_14 (and_14_out, xor_13_out, Allow_Twos_Complement);
  or or_14 (or_14_out, and_1_out, and_2_out, and_3_out, and_4_out, and_5_out, and_6_out, and_7_out, and_8_out, and_9_out, and_10_out, and_11_out, and_12_out, and_13_out, and_14_out);
  and and_15 (and_15_out, xor_14_out, Allow_Twos_Complement);
  or or_15 (or_15_out, and_1_out, and_2_out, and_3_out, and_4_out, and_5_out, and_6_out, and_7_out, and_8_out, and_9_out, and_10_out, and_11_out, and_12_out, and_13_out, and_14_out, and_15_out);
  xor xor_1 (Bit16_Result[1], and_1_out, Bit16_Input[1]);
  xor xor_2 (Bit16_Result[2], or_2_out, Bit16_Input[2]);
  xor xor_3 (Bit16_Result[3], or_3_out, Bit16_Input[3]);
  xor xor_4 (Bit16_Result[4], or_4_out, Bit16_Input[4]);
  xor xor_5 (Bit16_Result[5], or_5_out, Bit16_Input[5]);
  xor xor_6 (Bit16_Result[6], or_6_out, Bit16_Input[6]);
  xor xor_7 (Bit16_Result[7], or_7_out, Bit16_Input[7]);
  xor xor_8 (Bit16_Result[8], or_8_out, Bit16_Input[8]);
  xor xor_9 (Bit16_Result[9], or_9_out, Bit16_Input[9]);
  xor xor_10 (xor_10_out, or_10_out, Bit16_Input[10]);
  xor xor_11 (xor_11_out, or_11_out, Bit16_Input[11]);
  xor xor_12 (xor_12_out, or_12_out, Bit16_Input[12]);
  xor xor_13 (xor_13_out, or_13_out, Bit16_Input[13]);
  xor xor_14 (xor_14_out, or_14_out, Bit16_Input[14]);
  and and_16 (Bit16_Result[15], ~or_1_out, xor_15_out);  // AND_Gate
  xor xor_15 (xor_15_out, or_15_out, Bit16_Input[15]);
  or or_16 (Bit16_Result[10], Floating_Point_Bit_Strip, xor_10_out);
  and and_17 (Bit16_Result[11], ~Floating_Point_Bit_Strip, xor_11_out);  // AND_Gate
  and and_18 (Bit16_Result[12], ~Floating_Point_Bit_Strip, xor_12_out);  // AND_Gate
  and and_19 (Bit16_Result[13], ~Floating_Point_Bit_Strip, xor_13_out);  // AND_Gate
  and and_20 (Bit16_Result[14], ~Floating_Point_Bit_Strip, xor_14_out);  // AND_Gate

  assign Bit16_Result[0] = Bit16_Input[0];

  // Notes on the sheet:
  //   bc "implied" leading bit
endmodule
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module Bit16_Divider (
  input  [15:0] Bit16_Dividend,
  input  [15:0] Bit16_Divisor,
  output [15:0] Bit16_Quotient,
  output [15:0] Bit16_Remainder
);

  wire and_1_out, and_2_out, and_3_out, and_4_out, and_5_out, and_6_out, and_7_out, and_8_out, and_9_out,
       and_10_out, and_11_out, and_12_out, and_13_out, and_14_out, and_15_out, not_1_out, not_2_out,
       not_3_out, not_4_out, not_5_out, not_6_out, not_7_out, not_8_out, not_9_out, not_10_out, not_11_out,
       not_12_out, not_13_out, not_14_out, not_15_out, not_16_out, or_1_out, or_2_out, or_3_out, or_4_out,
       or_5_out, or_6_out, or_7_out, or_8_out, or_9_out, or_10_out, or_11_out, or_12_out, or_13_out,
       or_14_out, undriven;
  wire [15:0] bit16_add_16_bit16_result, bit16_controlled_buffer_1_bit16_out,
       bit16_controlled_buffer_2_bit16_out, bit16_controlled_buffer_3_bit16_out,
       bit16_controlled_buffer_4_bit16_out, bit16_controlled_buffer_5_bit16_out,
       bit16_controlled_buffer_6_bit16_out, bit16_controlled_buffer_7_bit16_out,
       bit16_controlled_buffer_8_bit16_out, bit16_controlled_buffer_9_bit16_out,
       bit16_controlled_buffer_10_bit16_out, bit16_controlled_buffer_11_bit16_out,
       bit16_controlled_buffer_12_bit16_out, bit16_controlled_buffer_13_bit16_out,
       bit16_controlled_buffer_14_bit16_out, bit16_controlled_buffer_15_bit16_out,
       bit16_controlled_buffer_16_bit16_out, bit16_controlled_buffer_17_bit16_out,
       bit16_controlled_buffer_18_bit16_out, bit16_controlled_buffer_19_bit16_out,
       bit16_controlled_buffer_20_bit16_out, bit16_controlled_buffer_21_bit16_out,
       bit16_controlled_buffer_22_bit16_out, bit16_controlled_buffer_23_bit16_out,
       bit16_controlled_buffer_24_bit16_out, bit16_controlled_buffer_25_bit16_out,
       bit16_controlled_buffer_26_bit16_out, bit16_controlled_buffer_27_bit16_out,
       bit16_controlled_buffer_28_bit16_out, bit16_controlled_buffer_29_bit16_out,
       bit16_controlled_buffer_30_bit16_out, bit16_controlled_buffer_31_bit16_out,
       bit16_controlled_buffer_32_bit16_out, or_29_out;
  wire [15:1] bit16_add_1_bit16_result, bit16_add_2_bit16_result, bit16_add_3_bit16_result,
       bit16_add_4_bit16_result, bit16_add_5_bit16_result, bit16_add_6_bit16_result,
       bit16_add_7_bit16_result, bit16_add_8_bit16_result, bit16_add_9_bit16_result,
       bit16_add_10_bit16_result, bit16_add_11_bit16_result, bit16_add_12_bit16_result,
       bit16_add_13_bit16_result, bit16_add_14_bit16_result, bit16_add_15_bit16_result, or_15_out, or_16_out,
       or_17_out, or_18_out, or_19_out, or_20_out, or_21_out, or_22_out, or_23_out, or_24_out, or_25_out,
       or_26_out, or_27_out, or_28_out, xor_1_out;
  wire [15:15] bit16_add_1_bit16_result_2, bit16_add_2_bit16_result_2, bit16_add_3_bit16_result_2,
       bit16_add_4_bit16_result_2, bit16_add_5_bit16_result_2, bit16_add_6_bit16_result_2,
       bit16_add_7_bit16_result_2, bit16_add_8_bit16_result_2, bit16_add_9_bit16_result_2,
       bit16_add_10_bit16_result_2, bit16_add_11_bit16_result_2, bit16_add_12_bit16_result_2,
       bit16_add_13_bit16_result_2, bit16_add_14_bit16_result_2, bit16_add_15_bit16_result_2, or_15_out_2,
       or_16_out_2, or_17_out_2, or_18_out_2, or_19_out_2, or_20_out_2, or_21_out_2, or_22_out_2,
       or_23_out_2, or_24_out_2, or_25_out_2, or_26_out_2, or_27_out_2, or_28_out_2;

  and and_1 (and_1_out, Bit16_Divisor[0], 1'b1);
  and and_2 (and_2_out, xor_1_out[1], 1'b1);
  or or_1 (or_1_out, and_1_out, and_2_out);
  and and_3 (and_3_out, xor_1_out[2], 1'b1);
  or or_2 (or_2_out, and_1_out, and_2_out, and_3_out);
  and and_4 (and_4_out, xor_1_out[3], 1'b1);
  or or_3 (or_3_out, and_1_out, and_2_out, and_3_out, and_4_out);
  and and_5 (and_5_out, xor_1_out[4], 1'b1);
  or or_4 (or_4_out, and_1_out, and_2_out, and_3_out, and_4_out, and_5_out);
  and and_6 (and_6_out, xor_1_out[5], 1'b1);
  or or_5 (or_5_out, and_1_out, and_2_out, and_3_out, and_4_out, and_5_out, and_6_out);
  and and_7 (and_7_out, xor_1_out[6], 1'b1);
  or or_6 (or_6_out, and_1_out, and_2_out, and_3_out, and_4_out, and_5_out, and_6_out, and_7_out);
  and and_8 (and_8_out, xor_1_out[7], 1'b1);
  or or_7 (or_7_out, and_1_out, and_2_out, and_3_out, and_4_out, and_5_out, and_6_out, and_7_out, and_8_out);
  and and_9 (and_9_out, xor_1_out[8], 1'b1);
  or or_8 (or_8_out, and_1_out, and_2_out, and_3_out, and_4_out, and_5_out, and_6_out, and_7_out, and_8_out, and_9_out);
  and and_10 (and_10_out, xor_1_out[9], 1'b1);
  or or_9 (or_9_out, and_1_out, and_2_out, and_3_out, and_4_out, and_5_out, and_6_out, and_7_out, and_8_out, and_9_out, and_10_out);
  and and_11 (and_11_out, xor_1_out[10], 1'b1);
  or or_10 (or_10_out, and_1_out, and_2_out, and_3_out, and_4_out, and_5_out, and_6_out, and_7_out, and_8_out, and_9_out, and_10_out, and_11_out);
  and and_12 (and_12_out, xor_1_out[11], 1'b1);
  or or_11 (or_11_out, and_1_out, and_2_out, and_3_out, and_4_out, and_5_out, and_6_out, and_7_out, and_8_out, and_9_out, and_10_out, and_11_out, and_12_out);
  and and_13 (and_13_out, xor_1_out[12], 1'b1);
  or or_12 (or_12_out, and_1_out, and_2_out, and_3_out, and_4_out, and_5_out, and_6_out, and_7_out, and_8_out, and_9_out, and_10_out, and_11_out, and_12_out, and_13_out);
  and and_14 (and_14_out, xor_1_out[13], 1'b1);
  or or_13 (or_13_out, and_1_out, and_2_out, and_3_out, and_4_out, and_5_out, and_6_out, and_7_out, and_8_out, and_9_out, and_10_out, and_11_out, and_12_out, and_13_out, and_14_out);
  and and_15 (and_15_out, xor_1_out[14], 1'b1);
  or or_14 (or_14_out, and_1_out, and_2_out, and_3_out, and_4_out, and_5_out, and_6_out, and_7_out, and_8_out, and_9_out, and_10_out, and_11_out, and_12_out, and_13_out, and_14_out, and_15_out);
  xor xor_1 (xor_1_out[1], and_1_out, Bit16_Divisor[1]);
  xor xor_2 (xor_1_out[2], or_1_out, Bit16_Divisor[2]);
  xor xor_3 (xor_1_out[3], or_2_out, Bit16_Divisor[3]);
  xor xor_4 (xor_1_out[4], or_3_out, Bit16_Divisor[4]);
  xor xor_5 (xor_1_out[5], or_4_out, Bit16_Divisor[5]);
  xor xor_6 (xor_1_out[6], or_5_out, Bit16_Divisor[6]);
  xor xor_7 (xor_1_out[7], or_6_out, Bit16_Divisor[7]);
  xor xor_8 (xor_1_out[8], or_7_out, Bit16_Divisor[8]);
  xor xor_9 (xor_1_out[9], or_8_out, Bit16_Divisor[9]);
  xor xor_10 (xor_1_out[10], or_9_out, Bit16_Divisor[10]);
  xor xor_11 (xor_1_out[11], or_10_out, Bit16_Divisor[11]);
  xor xor_12 (xor_1_out[12], or_11_out, Bit16_Divisor[12]);
  xor xor_13 (xor_1_out[13], or_12_out, Bit16_Divisor[13]);
  xor xor_14 (xor_1_out[14], or_13_out, Bit16_Divisor[14]);
  xor xor_15 (xor_1_out[15], or_14_out, Bit16_Divisor[15]);
  not not_1 (not_1_out, Bit16_Quotient[15]);
  not not_2 (not_2_out, Bit16_Quotient[14]);
  not not_3 (not_3_out, Bit16_Quotient[13]);
  not not_4 (not_4_out, Bit16_Quotient[12]);
  not not_5 (not_5_out, Bit16_Quotient[11]);
  not not_6 (not_6_out, Bit16_Quotient[10]);
  not not_7 (not_7_out, Bit16_Quotient[9]);
  not not_8 (not_8_out, Bit16_Quotient[8]);
  not not_9 (not_9_out, Bit16_Quotient[7]);
  not not_10 (not_10_out, Bit16_Quotient[6]);
  not not_11 (not_11_out, Bit16_Quotient[5]);
  not not_12 (not_12_out, Bit16_Quotient[4]);
  not not_13 (not_13_out, Bit16_Quotient[3]);
  not not_14 (not_14_out, Bit16_Quotient[2]);
  not not_15 (not_15_out, Bit16_Quotient[1]);
  not not_16 (not_16_out, Bit16_Quotient[0]);
  Bit16_Controlled_Buffer bit16_controlled_buffer_1 (
    .Enable(Bit16_Quotient[15]), .Bit16_In({bit16_add_11_bit16_result, Bit16_Dividend[14]}),
    .Bit16_Out(bit16_controlled_buffer_1_bit16_out));
  Bit16_Controlled_Buffer bit16_controlled_buffer_2 (
    .Enable(not_1_out), .Bit16_In({{14{1'b0}}, Bit16_Dividend[15:14]}),
    .Bit16_Out(bit16_controlled_buffer_2_bit16_out));
  assign {or_15_out_2[15], or_15_out} = bit16_controlled_buffer_2_bit16_out | bit16_controlled_buffer_1_bit16_out;  // OR_Gate or_15, 16 bits wide
  Bit16_Add bit16_add_1 (
    .Bit16_A({xor_1_out, Bit16_Divisor[0]}), .Bit16_B({or_15_out_2[15], or_15_out}),
    .Bit16_Result({bit16_add_1_bit16_result_2[15], bit16_add_1_bit16_result}), .Carry_Out(Bit16_Quotient[14]));  // open: FP_Op, Carry_In
  Bit16_Controlled_Buffer bit16_controlled_buffer_3 (
    .Enable(Bit16_Quotient[14]), .Bit16_In({bit16_add_1_bit16_result, Bit16_Dividend[13]}),
    .Bit16_Out(bit16_controlled_buffer_3_bit16_out));
  Bit16_Controlled_Buffer bit16_controlled_buffer_4 (
    .Enable(not_2_out), .Bit16_In({or_15_out, Bit16_Dividend[13]}),
    .Bit16_Out(bit16_controlled_buffer_4_bit16_out));
  assign {or_16_out_2[15], or_16_out} = bit16_controlled_buffer_4_bit16_out | bit16_controlled_buffer_3_bit16_out;  // OR_Gate or_16, 16 bits wide
  Bit16_Add bit16_add_2 (
    .Bit16_A({or_16_out_2[15], or_16_out}), .Bit16_B({xor_1_out, Bit16_Divisor[0]}),
    .Bit16_Result({bit16_add_2_bit16_result_2[15], bit16_add_2_bit16_result}), .Carry_Out(Bit16_Quotient[13]));  // open: FP_Op, Carry_In
  Bit16_Controlled_Buffer bit16_controlled_buffer_5 (
    .Enable(Bit16_Quotient[13]), .Bit16_In({bit16_add_2_bit16_result, Bit16_Dividend[12]}),
    .Bit16_Out(bit16_controlled_buffer_5_bit16_out));
  Bit16_Controlled_Buffer bit16_controlled_buffer_6 (
    .Enable(not_3_out), .Bit16_In({or_16_out, Bit16_Dividend[12]}),
    .Bit16_Out(bit16_controlled_buffer_6_bit16_out));
  assign {or_17_out_2[15], or_17_out} = bit16_controlled_buffer_6_bit16_out | bit16_controlled_buffer_5_bit16_out;  // OR_Gate or_17, 16 bits wide
  Bit16_Add bit16_add_3 (
    .Bit16_A({or_17_out_2[15], or_17_out}), .Bit16_B({xor_1_out, Bit16_Divisor[0]}),
    .Bit16_Result({bit16_add_3_bit16_result_2[15], bit16_add_3_bit16_result}), .Carry_Out(Bit16_Quotient[12]));  // open: FP_Op, Carry_In
  Bit16_Controlled_Buffer bit16_controlled_buffer_7 (
    .Enable(Bit16_Quotient[12]), .Bit16_In({bit16_add_3_bit16_result, Bit16_Dividend[11]}),
    .Bit16_Out(bit16_controlled_buffer_7_bit16_out));
  Bit16_Controlled_Buffer bit16_controlled_buffer_8 (
    .Enable(not_4_out), .Bit16_In({or_17_out, Bit16_Dividend[11]}),
    .Bit16_Out(bit16_controlled_buffer_8_bit16_out));
  assign {or_18_out_2[15], or_18_out} = bit16_controlled_buffer_8_bit16_out | bit16_controlled_buffer_7_bit16_out;  // OR_Gate or_18, 16 bits wide
  Bit16_Add bit16_add_4 (
    .Bit16_A({xor_1_out, Bit16_Divisor[0]}), .Bit16_B({or_18_out_2[15], or_18_out}),
    .Bit16_Result({bit16_add_4_bit16_result_2[15], bit16_add_4_bit16_result}), .Carry_Out(Bit16_Quotient[11]));  // open: FP_Op, Carry_In
  Bit16_Controlled_Buffer bit16_controlled_buffer_9 (
    .Enable(Bit16_Quotient[11]), .Bit16_In({bit16_add_4_bit16_result, Bit16_Dividend[10]}),
    .Bit16_Out(bit16_controlled_buffer_9_bit16_out));
  Bit16_Controlled_Buffer bit16_controlled_buffer_10 (
    .Enable(not_5_out), .Bit16_In({or_18_out, Bit16_Dividend[10]}),
    .Bit16_Out(bit16_controlled_buffer_10_bit16_out));
  assign {or_19_out_2[15], or_19_out} = bit16_controlled_buffer_10_bit16_out | bit16_controlled_buffer_9_bit16_out;  // OR_Gate or_19, 16 bits wide
  Bit16_Controlled_Buffer bit16_controlled_buffer_11 (
    .Enable(Bit16_Quotient[10]), .Bit16_In({bit16_add_12_bit16_result, Bit16_Dividend[9]}),
    .Bit16_Out(bit16_controlled_buffer_11_bit16_out));
  Bit16_Controlled_Buffer bit16_controlled_buffer_12 (
    .Enable(not_6_out), .Bit16_In({or_19_out, Bit16_Dividend[9]}),
    .Bit16_Out(bit16_controlled_buffer_12_bit16_out));
  assign {or_20_out_2[15], or_20_out} = bit16_controlled_buffer_12_bit16_out | bit16_controlled_buffer_11_bit16_out;  // OR_Gate or_20, 16 bits wide
  Bit16_Add bit16_add_5 (
    .Bit16_A({xor_1_out, Bit16_Divisor[0]}), .Bit16_B({or_20_out_2[15], or_20_out}),
    .Bit16_Result({bit16_add_5_bit16_result_2[15], bit16_add_5_bit16_result}), .Carry_Out(Bit16_Quotient[9]));  // open: FP_Op, Carry_In
  Bit16_Controlled_Buffer bit16_controlled_buffer_13 (
    .Enable(Bit16_Quotient[9]), .Bit16_In({bit16_add_5_bit16_result, Bit16_Dividend[8]}),
    .Bit16_Out(bit16_controlled_buffer_13_bit16_out));
  Bit16_Controlled_Buffer bit16_controlled_buffer_14 (
    .Enable(not_7_out), .Bit16_In({or_20_out, Bit16_Dividend[8]}),
    .Bit16_Out(bit16_controlled_buffer_14_bit16_out));
  assign {or_21_out_2[15], or_21_out} = bit16_controlled_buffer_14_bit16_out | bit16_controlled_buffer_13_bit16_out;  // OR_Gate or_21, 16 bits wide
  Bit16_Controlled_Buffer bit16_controlled_buffer_15 (
    .Enable(Bit16_Quotient[8]), .Bit16_In({bit16_add_13_bit16_result, Bit16_Dividend[7]}),
    .Bit16_Out(bit16_controlled_buffer_15_bit16_out));
  Bit16_Controlled_Buffer bit16_controlled_buffer_16 (
    .Enable(not_8_out), .Bit16_In({or_21_out, Bit16_Dividend[7]}),
    .Bit16_Out(bit16_controlled_buffer_16_bit16_out));
  assign {or_22_out_2[15], or_22_out} = bit16_controlled_buffer_16_bit16_out | bit16_controlled_buffer_15_bit16_out;  // OR_Gate or_22, 16 bits wide
  Bit16_Controlled_Buffer bit16_controlled_buffer_17 (
    .Enable(Bit16_Quotient[7]), .Bit16_In({bit16_add_14_bit16_result, Bit16_Dividend[6]}),
    .Bit16_Out(bit16_controlled_buffer_17_bit16_out));
  Bit16_Controlled_Buffer bit16_controlled_buffer_18 (
    .Enable(not_9_out), .Bit16_In({or_22_out, Bit16_Dividend[6]}),
    .Bit16_Out(bit16_controlled_buffer_18_bit16_out));
  assign {or_23_out_2[15], or_23_out} = bit16_controlled_buffer_18_bit16_out | bit16_controlled_buffer_17_bit16_out;  // OR_Gate or_23, 16 bits wide
  Bit16_Add bit16_add_6 (
    .Bit16_A({xor_1_out, Bit16_Divisor[0]}), .Bit16_B({or_23_out_2[15], or_23_out}),
    .Bit16_Result({bit16_add_6_bit16_result_2[15], bit16_add_6_bit16_result}), .Carry_Out(Bit16_Quotient[6]));  // open: FP_Op, Carry_In
  Bit16_Controlled_Buffer bit16_controlled_buffer_19 (
    .Enable(Bit16_Quotient[6]), .Bit16_In({bit16_add_6_bit16_result, Bit16_Dividend[5]}),
    .Bit16_Out(bit16_controlled_buffer_19_bit16_out));
  Bit16_Controlled_Buffer bit16_controlled_buffer_20 (
    .Enable(not_10_out), .Bit16_In({or_23_out, Bit16_Dividend[5]}),
    .Bit16_Out(bit16_controlled_buffer_20_bit16_out));
  assign {or_24_out_2[15], or_24_out} = bit16_controlled_buffer_20_bit16_out | bit16_controlled_buffer_19_bit16_out;  // OR_Gate or_24, 16 bits wide
  Bit16_Add bit16_add_7 (
    .Bit16_A({xor_1_out, Bit16_Divisor[0]}), .Bit16_B({or_24_out_2[15], or_24_out}),
    .Bit16_Result({bit16_add_7_bit16_result_2[15], bit16_add_7_bit16_result}), .Carry_Out(Bit16_Quotient[5]));  // open: FP_Op, Carry_In
  Bit16_Controlled_Buffer bit16_controlled_buffer_21 (
    .Enable(Bit16_Quotient[5]), .Bit16_In({bit16_add_7_bit16_result, Bit16_Dividend[4]}),
    .Bit16_Out(bit16_controlled_buffer_21_bit16_out));
  Bit16_Controlled_Buffer bit16_controlled_buffer_22 (
    .Enable(not_11_out), .Bit16_In({or_24_out, Bit16_Dividend[4]}),
    .Bit16_Out(bit16_controlled_buffer_22_bit16_out));
  assign {or_25_out_2[15], or_25_out} = bit16_controlled_buffer_22_bit16_out | bit16_controlled_buffer_21_bit16_out;  // OR_Gate or_25, 16 bits wide
  Bit16_Add bit16_add_8 (
    .Bit16_A({xor_1_out, Bit16_Divisor[0]}), .Bit16_B({or_25_out_2[15], or_25_out}),
    .Bit16_Result({bit16_add_8_bit16_result_2[15], bit16_add_8_bit16_result}), .Carry_Out(Bit16_Quotient[4]));  // open: FP_Op, Carry_In
  Bit16_Controlled_Buffer bit16_controlled_buffer_23 (
    .Enable(Bit16_Quotient[4]), .Bit16_In({bit16_add_8_bit16_result, Bit16_Dividend[3]}),
    .Bit16_Out(bit16_controlled_buffer_23_bit16_out));
  Bit16_Controlled_Buffer bit16_controlled_buffer_24 (
    .Enable(not_12_out), .Bit16_In({or_25_out, Bit16_Dividend[3]}),
    .Bit16_Out(bit16_controlled_buffer_24_bit16_out));
  assign {or_26_out_2[15], or_26_out} = bit16_controlled_buffer_24_bit16_out | bit16_controlled_buffer_23_bit16_out;  // OR_Gate or_26, 16 bits wide
  Bit16_Add bit16_add_9 (
    .Bit16_A({xor_1_out, Bit16_Divisor[0]}), .Bit16_B({or_26_out_2[15], or_26_out}),
    .Bit16_Result({bit16_add_9_bit16_result_2[15], bit16_add_9_bit16_result}), .Carry_Out(Bit16_Quotient[3]));  // open: FP_Op, Carry_In
  Bit16_Controlled_Buffer bit16_controlled_buffer_25 (
    .Enable(Bit16_Quotient[3]), .Bit16_In({bit16_add_9_bit16_result, Bit16_Dividend[2]}),
    .Bit16_Out(bit16_controlled_buffer_25_bit16_out));
  Bit16_Controlled_Buffer bit16_controlled_buffer_26 (
    .Enable(not_13_out), .Bit16_In({or_26_out, Bit16_Dividend[2]}),
    .Bit16_Out(bit16_controlled_buffer_26_bit16_out));
  assign {or_27_out_2[15], or_27_out} = bit16_controlled_buffer_26_bit16_out | bit16_controlled_buffer_25_bit16_out;  // OR_Gate or_27, 16 bits wide
  Bit16_Add bit16_add_10 (
    .Bit16_A({xor_1_out, Bit16_Divisor[0]}), .Bit16_B({or_27_out_2[15], or_27_out}),
    .Bit16_Result({bit16_add_10_bit16_result_2[15], bit16_add_10_bit16_result}), .Carry_Out(Bit16_Quotient[2]));  // open: FP_Op, Carry_In
  Bit16_Controlled_Buffer bit16_controlled_buffer_27 (
    .Enable(Bit16_Quotient[2]), .Bit16_In({bit16_add_10_bit16_result, Bit16_Dividend[1]}),
    .Bit16_Out(bit16_controlled_buffer_27_bit16_out));
  Bit16_Controlled_Buffer bit16_controlled_buffer_28 (
    .Enable(not_14_out), .Bit16_In({or_27_out, Bit16_Dividend[1]}),
    .Bit16_Out(bit16_controlled_buffer_28_bit16_out));
  assign {or_28_out_2[15], or_28_out} = bit16_controlled_buffer_28_bit16_out | bit16_controlled_buffer_27_bit16_out;  // OR_Gate or_28, 16 bits wide
  Bit16_Controlled_Buffer bit16_controlled_buffer_29 (
    .Enable(Bit16_Quotient[1]), .Bit16_In({bit16_add_15_bit16_result, Bit16_Dividend[0]}),
    .Bit16_Out(bit16_controlled_buffer_29_bit16_out));
  Bit16_Controlled_Buffer bit16_controlled_buffer_30 (
    .Enable(not_15_out), .Bit16_In({or_28_out, Bit16_Dividend[0]}),
    .Bit16_Out(bit16_controlled_buffer_30_bit16_out));
  assign or_29_out = bit16_controlled_buffer_30_bit16_out | bit16_controlled_buffer_29_bit16_out;  // OR_Gate or_29, 16 bits wide
  Bit16_Controlled_Buffer bit16_controlled_buffer_31 (
    .Enable(Bit16_Quotient[0]), .Bit16_In(bit16_add_16_bit16_result),
    .Bit16_Out(bit16_controlled_buffer_31_bit16_out));
  Bit16_Controlled_Buffer bit16_controlled_buffer_32 (
    .Enable(not_16_out), .Bit16_In(or_29_out), .Bit16_Out(bit16_controlled_buffer_32_bit16_out));
  Bit16_Add bit16_add_11 (
    .Carry_In(undriven), .Bit16_A({{15{1'b0}}, Bit16_Dividend[15]}), .Bit16_B({xor_1_out, Bit16_Divisor[0]}),
    .Bit16_Result({bit16_add_11_bit16_result_2[15], bit16_add_11_bit16_result}),
    .Carry_Out(Bit16_Quotient[15]));  // open: FP_Op
  Bit16_Add bit16_add_12 (
    .Bit16_A({or_19_out_2[15], or_19_out}), .Bit16_B({xor_1_out, Bit16_Divisor[0]}),
    .Bit16_Result({bit16_add_12_bit16_result_2[15], bit16_add_12_bit16_result}),
    .Carry_Out(Bit16_Quotient[10]));  // open: FP_Op, Carry_In
  Bit16_Add bit16_add_13 (
    .Bit16_A({or_21_out_2[15], or_21_out}), .Bit16_B({xor_1_out, Bit16_Divisor[0]}),
    .Bit16_Result({bit16_add_13_bit16_result_2[15], bit16_add_13_bit16_result}), .Carry_Out(Bit16_Quotient[8]));  // open: FP_Op, Carry_In
  Bit16_Add bit16_add_14 (
    .Bit16_A({xor_1_out, Bit16_Divisor[0]}), .Bit16_B({or_22_out_2[15], or_22_out}),
    .Bit16_Result({bit16_add_14_bit16_result_2[15], bit16_add_14_bit16_result}), .Carry_Out(Bit16_Quotient[7]));  // open: FP_Op, Carry_In
  Bit16_Add bit16_add_15 (
    .Bit16_A({xor_1_out, Bit16_Divisor[0]}), .Bit16_B({or_28_out_2[15], or_28_out}),
    .Bit16_Result({bit16_add_15_bit16_result_2[15], bit16_add_15_bit16_result}), .Carry_Out(Bit16_Quotient[1]));  // open: FP_Op, Carry_In
  Bit16_Add bit16_add_16 (
    .Bit16_A(or_29_out), .Bit16_B({xor_1_out, Bit16_Divisor[0]}), .Bit16_Result(bit16_add_16_bit16_result),
    .Carry_Out(Bit16_Quotient[0]));  // open: FP_Op, Carry_In
  assign Bit16_Remainder = bit16_controlled_buffer_32_bit16_out | bit16_controlled_buffer_31_bit16_out;  // OR_Gate or_30, 16 bits wide
  // Probe on Bit16_Quotient
  // Probe on Bit16_Remainder
endmodule

module Bit4_CLA_Logic (
  input  Cin,
  input  P1,
  input  G1,
  input  P2,
  input  G2,
  input  P3,
  input  G3,
  input  P4,
  input  G4,
  output C2,
  output C3,
  output C4,
  output COUT,
  output PG
);

  wire and_1_out, and_2_out, and_3_out, and_4_out, and_5_out, and_6_out, and_7_out, and_8_out, and_9_out,
       and_10_out;

  or or_1 (C2, G1, and_1_out);
  or or_2 (C3, G2, and_2_out, and_3_out);
  or or_3 (C4, G3, and_4_out, and_5_out, and_6_out);
  or or_4 (COUT, G4, and_7_out, and_8_out, and_9_out, and_10_out);
  and and_1 (and_1_out, P1, Cin);
  and and_2 (and_2_out, P2, G1);
  and and_3 (and_3_out, P2, P1, Cin);
  and and_4 (and_4_out, G2, P3);
  and and_5 (and_5_out, P3, P2, G1);
  and and_6 (and_6_out, P3, P2, Cin, P1);
  and and_7 (and_7_out, G3, P4);
  and and_8 (and_8_out, P4, P3, G2);
  and and_9 (and_9_out, P4, P3, P2, G1);
  and and_10 (and_10_out, P4, P3, P2, P1, Cin);
  and and_11 (PG, P1, P2, P3, P4);
endmodule

module Bit16_Left_Shift (
  input  [15:0] Bit16_Data,
  input  [3:0] Bit4_Shift,
  output [15:0] Bit16_Result,
  output Shift_Overflow
);

  wire and_1_out, and_2_out, and_3_out, and_4_out, and_5_out, and_6_out, and_7_out, and_8_out, and_9_out,
       and_10_out, and_11_out, and_12_out, and_13_out, and_14_out, and_15_out, and_16_out, and_17_out,
       and_18_out, and_19_out, and_20_out, and_21_out, and_22_out, and_23_out, and_24_out, and_25_out,
       and_26_out, and_27_out, and_28_out, and_29_out, and_30_out, and_31_out, and_32_out, and_33_out,
       and_34_out, and_35_out, and_36_out, and_37_out, and_38_out, and_39_out, and_40_out, and_41_out,
       and_42_out, and_43_out, and_44_out, and_45_out, and_46_out, and_47_out, and_48_out, and_49_out,
       and_50_out, and_51_out, and_52_out, and_53_out, and_54_out, and_55_out, and_56_out, and_57_out,
       and_58_out, and_59_out, and_60_out, and_61_out, and_62_out, and_63_out, and_64_out, and_65_out,
       and_66_out, and_67_out, and_69_out, and_70_out, and_71_out, and_72_out, and_73_out, and_74_out,
       and_75_out, and_77_out, and_78_out, and_79_out, and_80_out, and_81_out, and_82_out, and_83_out,
       and_85_out, and_86_out, and_87_out, and_88_out, and_89_out, and_90_out, and_91_out, and_93_out,
       and_94_out, and_95_out, and_96_out, and_97_out, and_98_out, and_99_out, and_101_out, and_102_out,
       and_103_out, and_104_out, and_105_out, and_106_out, and_107_out, and_109_out, and_110_out,
       and_111_out, and_112_out, and_113_out, and_114_out, and_115_out, and_117_out, and_118_out,
       and_119_out, and_120_out, and_121_out, and_122_out, and_123_out, and_125_out, and_126_out,
       and_127_out, and_128_out, or_2_out, or_3_out, or_4_out, or_6_out, or_7_out, or_8_out, or_10_out,
       or_11_out, or_12_out, or_14_out, or_15_out, or_16_out, or_18_out, or_19_out, or_20_out, or_22_out,
       or_23_out, or_24_out, or_26_out, or_27_out, or_28_out, or_30_out, or_31_out, or_32_out, or_34_out,
       or_35_out, or_36_out, or_37_out, or_38_out, or_39_out, or_40_out, or_41_out, or_42_out, or_43_out,
       or_44_out, or_45_out, or_46_out, or_47_out, or_48_out, or_49_out, or_50_out;

  or or_1 (Shift_Overflow, and_5_out, and_7_out, and_15_out, and_9_out, and_17_out, and_25_out, and_34_out, and_11_out, and_19_out, and_27_out, and_36_out, and_43_out, and_51_out, and_59_out, and_67_out);
  and and_1 (and_1_out, ~Bit4_Shift[0], Bit16_Data[15]);  // AND_Gate
  or or_2 (or_2_out, and_1_out, and_13_out);
  and and_2 (and_2_out, ~Bit4_Shift[1], or_2_out);  // AND_Gate
  or or_3 (or_3_out, and_2_out, and_23_out);
  and and_3 (and_3_out, ~Bit4_Shift[2], or_3_out);  // AND_Gate
  or or_4 (or_4_out, and_3_out, and_41_out);
  and and_4 (and_4_out, ~Bit4_Shift[3], or_4_out);  // AND_Gate
  or or_5 (Bit16_Result[15], and_4_out, and_75_out);
  and and_5 (and_5_out, Bit16_Data[15], Bit4_Shift[0]);
  and and_6 (and_6_out, ~Bit4_Shift[0], Bit16_Data[14]);  // AND_Gate
  or or_6 (or_6_out, and_6_out, and_21_out);
  and and_7 (and_7_out, or_2_out, Bit4_Shift[1]);
  and and_8 (and_8_out, ~Bit4_Shift[1], or_6_out);  // AND_Gate
  or or_7 (or_7_out, and_8_out, and_32_out);
  and and_9 (and_9_out, or_3_out, Bit4_Shift[2]);
  and and_10 (and_10_out, ~Bit4_Shift[2], or_7_out);  // AND_Gate
  or or_8 (or_8_out, and_10_out, and_49_out);
  and and_11 (and_11_out, or_4_out, Bit4_Shift[3]);
  and and_12 (and_12_out, ~Bit4_Shift[3], or_8_out);  // AND_Gate
  or or_9 (Bit16_Result[14], and_12_out, and_83_out);
  and and_13 (and_13_out, Bit16_Data[14], Bit4_Shift[0]);
  and and_14 (and_14_out, ~Bit4_Shift[0], Bit16_Data[13]);  // AND_Gate
  or or_10 (or_10_out, and_14_out, and_30_out);
  and and_15 (and_15_out, or_6_out, Bit4_Shift[1]);
  and and_16 (and_16_out, ~Bit4_Shift[1], or_10_out);  // AND_Gate
  or or_11 (or_11_out, and_16_out, and_39_out);
  and and_17 (and_17_out, or_7_out, Bit4_Shift[2]);
  and and_18 (and_18_out, ~Bit4_Shift[2], or_11_out);  // AND_Gate
  or or_12 (or_12_out, and_18_out, and_57_out);
  and and_19 (and_19_out, or_8_out, Bit4_Shift[3]);
  and and_20 (and_20_out, ~Bit4_Shift[3], or_12_out);  // AND_Gate
  or or_13 (Bit16_Result[13], and_20_out, and_91_out);
  and and_21 (and_21_out, Bit16_Data[13], Bit4_Shift[0]);
  and and_22 (and_22_out, ~Bit4_Shift[0], Bit16_Data[12]);  // AND_Gate
  or or_14 (or_14_out, and_22_out, and_37_out);
  and and_23 (and_23_out, or_10_out, Bit4_Shift[1]);
  and and_24 (and_24_out, ~Bit4_Shift[1], or_14_out);  // AND_Gate
  or or_15 (or_15_out, and_24_out, and_47_out);
  and and_25 (and_25_out, or_11_out, Bit4_Shift[2]);
  and and_26 (and_26_out, ~Bit4_Shift[2], or_15_out);  // AND_Gate
  or or_16 (or_16_out, and_26_out, and_65_out);
  and and_27 (and_27_out, or_12_out, Bit4_Shift[3]);
  and and_28 (and_28_out, ~Bit4_Shift[3], or_16_out);  // AND_Gate
  or or_17 (Bit16_Result[12], and_28_out, and_99_out);
  and and_29 (and_29_out, ~Bit4_Shift[0], Bit16_Data[11]);  // AND_Gate
  and and_30 (and_30_out, Bit16_Data[12], Bit4_Shift[0]);
  or or_18 (or_18_out, and_29_out, and_45_out);
  and and_31 (and_31_out, ~Bit4_Shift[1], or_18_out);  // AND_Gate
  and and_32 (and_32_out, or_14_out, Bit4_Shift[1]);
  or or_19 (or_19_out, and_31_out, and_55_out);
  and and_33 (and_33_out, ~Bit4_Shift[2], or_19_out);  // AND_Gate
  and and_34 (and_34_out, or_15_out, Bit4_Shift[2]);
  or or_20 (or_20_out, and_33_out, and_73_out);
  and and_35 (and_35_out, ~Bit4_Shift[3], or_20_out);  // AND_Gate
  and and_36 (and_36_out, or_16_out, Bit4_Shift[3]);
  or or_21 (Bit16_Result[11], and_35_out, and_107_out);
  and and_37 (and_37_out, Bit16_Data[11], Bit4_Shift[0]);
  and and_38 (and_38_out, ~Bit4_Shift[0], Bit16_Data[10]);  // AND_Gate
  or or_22 (or_22_out, and_38_out, and_53_out);
  and and_39 (and_39_out, or_18_out, Bit4_Shift[1]);
  and and_40 (and_40_out, ~Bit4_Shift[1], or_22_out);  // AND_Gate
  or or_23 (or_23_out, and_40_out, and_63_out);
  and and_41 (and_41_out, or_19_out, Bit4_Shift[2]);
  and and_42 (and_42_out, ~Bit4_Shift[2], or_23_out);  // AND_Gate
  or or_24 (or_24_out, and_42_out, and_81_out);
  and and_43 (and_43_out, or_20_out, Bit4_Shift[3]);
  and and_44 (and_44_out, ~Bit4_Shift[3], or_24_out);  // AND_Gate
  or or_25 (Bit16_Result[10], and_44_out, and_115_out);
  and and_45 (and_45_out, Bit16_Data[10], Bit4_Shift[0]);
  and and_46 (and_46_out, ~Bit4_Shift[0], Bit16_Data[9]);  // AND_Gate
  or or_26 (or_26_out, and_46_out, and_61_out);
  and and_47 (and_47_out, or_22_out, Bit4_Shift[1]);
  and and_48 (and_48_out, ~Bit4_Shift[1], or_26_out);  // AND_Gate
  or or_27 (or_27_out, and_48_out, and_71_out);
  and and_49 (and_49_out, or_23_out, Bit4_Shift[2]);
  and and_50 (and_50_out, ~Bit4_Shift[2], or_27_out);  // AND_Gate
  or or_28 (or_28_out, and_50_out, and_89_out);
  and and_51 (and_51_out, or_24_out, Bit4_Shift[3]);
  and and_52 (and_52_out, ~Bit4_Shift[3], or_28_out);  // AND_Gate
  or or_29 (Bit16_Result[9], and_52_out, and_123_out);
  and and_53 (and_53_out, Bit16_Data[9], Bit4_Shift[0]);
  and and_54 (and_54_out, ~Bit4_Shift[0], Bit16_Data[8]);  // AND_Gate
  or or_30 (or_30_out, and_54_out, and_69_out);
  and and_55 (and_55_out, or_26_out, Bit4_Shift[1]);
  and and_56 (and_56_out, ~Bit4_Shift[1], or_30_out);  // AND_Gate
  or or_31 (or_31_out, and_56_out, and_79_out);
  and and_57 (and_57_out, or_27_out, Bit4_Shift[2]);
  and and_58 (and_58_out, ~Bit4_Shift[2], or_31_out);  // AND_Gate
  or or_32 (or_32_out, and_58_out, and_97_out);
  and and_59 (and_59_out, or_28_out, Bit4_Shift[3]);
  and and_60 (and_60_out, ~Bit4_Shift[3], or_32_out);  // AND_Gate
  or or_33 (Bit16_Result[8], and_60_out, and_128_out);
  and and_61 (and_61_out, Bit16_Data[8], Bit4_Shift[0]);
  and and_62 (and_62_out, ~Bit4_Shift[0], Bit16_Data[7]);  // AND_Gate
  or or_34 (or_34_out, and_62_out, and_77_out);
  and and_63 (and_63_out, or_30_out, Bit4_Shift[1]);
  and and_64 (and_64_out, ~Bit4_Shift[1], or_34_out);  // AND_Gate
  or or_35 (or_35_out, and_64_out, and_87_out);
  and and_65 (and_65_out, or_31_out, Bit4_Shift[2]);
  and and_66 (and_66_out, ~Bit4_Shift[2], or_35_out);  // AND_Gate
  or or_36 (or_36_out, and_66_out, and_105_out);
  and and_67 (and_67_out, or_32_out, Bit4_Shift[3]);
  and and_68 (Bit16_Result[7], ~Bit4_Shift[3], or_36_out);  // AND_Gate
  and and_69 (and_69_out, Bit16_Data[7], Bit4_Shift[0]);
  and and_70 (and_70_out, ~Bit4_Shift[0], Bit16_Data[6]);  // AND_Gate
  or or_37 (or_37_out, and_70_out, and_85_out);
  and and_71 (and_71_out, or_34_out, Bit4_Shift[1]);
  and and_72 (and_72_out, ~Bit4_Shift[1], or_37_out);  // AND_Gate
  or or_38 (or_38_out, and_72_out, and_95_out);
  and and_73 (and_73_out, or_35_out, Bit4_Shift[2]);
  and and_74 (and_74_out, ~Bit4_Shift[2], or_38_out);  // AND_Gate
  or or_39 (or_39_out, and_74_out, and_113_out);
  and and_75 (and_75_out, or_36_out, Bit4_Shift[3]);
  and and_76 (Bit16_Result[6], ~Bit4_Shift[3], or_39_out);  // AND_Gate
  and and_77 (and_77_out, Bit16_Data[6], Bit4_Shift[0]);
  and and_78 (and_78_out, ~Bit4_Shift[0], Bit16_Data[5]);  // AND_Gate
  or or_40 (or_40_out, and_78_out, and_93_out);
  and and_79 (and_79_out, or_37_out, Bit4_Shift[1]);
  and and_80 (and_80_out, ~Bit4_Shift[1], or_40_out);  // AND_Gate
  or or_41 (or_41_out, and_80_out, and_103_out);
  and and_81 (and_81_out, or_38_out, Bit4_Shift[2]);
  and and_82 (and_82_out, ~Bit4_Shift[2], or_41_out);  // AND_Gate
  or or_42 (or_42_out, and_82_out, and_121_out);
  and and_83 (and_83_out, or_39_out, Bit4_Shift[3]);
  and and_84 (Bit16_Result[5], ~Bit4_Shift[3], or_42_out);  // AND_Gate
  and and_85 (and_85_out, Bit16_Data[5], Bit4_Shift[0]);
  and and_86 (and_86_out, ~Bit4_Shift[0], Bit16_Data[4]);  // AND_Gate
  or or_43 (or_43_out, and_86_out, and_101_out);
  and and_87 (and_87_out, or_40_out, Bit4_Shift[1]);
  and and_88 (and_88_out, ~Bit4_Shift[1], or_43_out);  // AND_Gate
  or or_44 (or_44_out, and_88_out, and_111_out);
  and and_89 (and_89_out, or_41_out, Bit4_Shift[2]);
  and and_90 (and_90_out, ~Bit4_Shift[2], or_44_out);  // AND_Gate
  or or_45 (or_45_out, and_90_out, and_127_out);
  and and_91 (and_91_out, or_42_out, Bit4_Shift[3]);
  and and_92 (Bit16_Result[4], ~Bit4_Shift[3], or_45_out);  // AND_Gate
  and and_93 (and_93_out, Bit16_Data[4], Bit4_Shift[0]);
  and and_94 (and_94_out, ~Bit4_Shift[0], Bit16_Data[3]);  // AND_Gate
  or or_46 (or_46_out, and_94_out, and_109_out);
  and and_95 (and_95_out, or_43_out, Bit4_Shift[1]);
  and and_96 (and_96_out, ~Bit4_Shift[1], or_46_out);  // AND_Gate
  or or_47 (or_47_out, and_96_out, and_119_out);
  and and_97 (and_97_out, or_44_out, Bit4_Shift[2]);
  and and_98 (and_98_out, ~Bit4_Shift[2], or_47_out);  // AND_Gate
  and and_99 (and_99_out, or_45_out, Bit4_Shift[3]);
  and and_100 (Bit16_Result[3], ~Bit4_Shift[3], and_98_out);  // AND_Gate
  and and_101 (and_101_out, Bit16_Data[3], Bit4_Shift[0]);
  and and_102 (and_102_out, ~Bit4_Shift[0], Bit16_Data[2]);  // AND_Gate
  or or_48 (or_48_out, and_102_out, and_117_out);
  and and_103 (and_103_out, or_46_out, Bit4_Shift[1]);
  and and_104 (and_104_out, ~Bit4_Shift[1], or_48_out);  // AND_Gate
  or or_49 (or_49_out, and_104_out, and_126_out);
  and and_105 (and_105_out, or_47_out, Bit4_Shift[2]);
  and and_106 (and_106_out, ~Bit4_Shift[2], or_49_out);  // AND_Gate
  and and_107 (and_107_out, and_98_out, Bit4_Shift[3]);
  and and_108 (Bit16_Result[2], ~Bit4_Shift[3], and_106_out);  // AND_Gate
  and and_109 (and_109_out, Bit16_Data[2], Bit4_Shift[0]);
  and and_110 (and_110_out, ~Bit4_Shift[0], Bit16_Data[1]);  // AND_Gate
  or or_50 (or_50_out, and_110_out, and_125_out);
  and and_111 (and_111_out, or_48_out, Bit4_Shift[1]);
  and and_112 (and_112_out, ~Bit4_Shift[1], or_50_out);  // AND_Gate
  and and_113 (and_113_out, or_49_out, Bit4_Shift[2]);
  and and_114 (and_114_out, ~Bit4_Shift[2], and_112_out);  // AND_Gate
  and and_115 (and_115_out, and_106_out, Bit4_Shift[3]);
  and and_116 (Bit16_Result[1], ~Bit4_Shift[3], and_114_out);  // AND_Gate
  and and_117 (and_117_out, Bit16_Data[1], Bit4_Shift[0]);
  and and_118 (and_118_out, ~Bit4_Shift[0], Bit16_Data[0]);  // AND_Gate
  and and_119 (and_119_out, or_50_out, Bit4_Shift[1]);
  and and_120 (and_120_out, ~Bit4_Shift[1], and_118_out);  // AND_Gate
  and and_121 (and_121_out, and_112_out, Bit4_Shift[2]);
  and and_122 (and_122_out, ~Bit4_Shift[2], and_120_out);  // AND_Gate
  and and_123 (and_123_out, and_114_out, Bit4_Shift[3]);
  and and_124 (Bit16_Result[0], ~Bit4_Shift[3], and_122_out);  // AND_Gate
  and and_125 (and_125_out, Bit16_Data[0], Bit4_Shift[0]);
  and and_126 (and_126_out, and_118_out, Bit4_Shift[1]);
  and and_127 (and_127_out, and_120_out, Bit4_Shift[2]);
  and and_128 (and_128_out, and_122_out, Bit4_Shift[3]);
endmodule

module Bit16_Right_Shift (
  input  [15:0] Bit16_Data,
  input  [3:0] Bit4_Shift,
  output [15:0] Bit16_Result,
  output Shift_Overflow
);

  wire and_1_out, and_2_out, and_3_out, and_4_out, and_5_out, and_6_out, and_7_out, and_8_out, and_9_out,
       and_10_out, and_11_out, and_12_out, and_13_out, and_14_out, and_15_out, and_16_out, and_17_out,
       and_18_out, and_19_out, and_20_out, and_21_out, and_22_out, and_23_out, and_24_out, and_25_out,
       and_26_out, and_27_out, and_28_out, and_29_out, and_30_out, and_31_out, and_32_out, and_33_out,
       and_34_out, and_35_out, and_36_out, and_37_out, and_38_out, and_39_out, and_40_out, and_41_out,
       and_42_out, and_43_out, and_44_out, and_45_out, and_46_out, and_47_out, and_48_out, and_49_out,
       and_50_out, and_51_out, and_52_out, and_53_out, and_54_out, and_55_out, and_56_out, and_57_out,
       and_58_out, and_59_out, and_60_out, and_61_out, and_62_out, and_63_out, and_64_out, and_65_out,
       and_66_out, and_67_out, and_69_out, and_70_out, and_71_out, and_72_out, and_73_out, and_74_out,
       and_75_out, and_77_out, and_78_out, and_79_out, and_80_out, and_81_out, and_82_out, and_83_out,
       and_85_out, and_86_out, and_87_out, and_88_out, and_89_out, and_90_out, and_91_out, and_93_out,
       and_94_out, and_95_out, and_96_out, and_97_out, and_98_out, and_99_out, and_101_out, and_102_out,
       and_103_out, and_104_out, and_105_out, and_106_out, and_107_out, and_109_out, and_110_out,
       and_111_out, and_112_out, and_113_out, and_114_out, and_115_out, and_117_out, and_118_out,
       and_119_out, and_120_out, and_121_out, and_122_out, and_123_out, and_125_out, and_126_out,
       and_127_out, and_128_out, or_2_out, or_3_out, or_4_out, or_6_out, or_7_out, or_8_out, or_10_out,
       or_11_out, or_12_out, or_14_out, or_15_out, or_16_out, or_18_out, or_19_out, or_20_out, or_22_out,
       or_23_out, or_24_out, or_26_out, or_27_out, or_28_out, or_30_out, or_31_out, or_32_out, or_34_out,
       or_35_out, or_36_out, or_37_out, or_38_out, or_39_out, or_40_out, or_41_out, or_42_out, or_43_out,
       or_44_out, or_45_out, or_46_out, or_47_out, or_48_out, or_49_out, or_50_out;

  or or_1 (Shift_Overflow, and_5_out, and_7_out, and_15_out, and_9_out, and_17_out, and_25_out, and_33_out, and_11_out, and_19_out, and_27_out, and_35_out, and_43_out, and_52_out, and_59_out, and_67_out);
  and and_1 (and_1_out, ~Bit4_Shift[0], Bit16_Data[0]);  // AND_Gate
  and and_2 (and_2_out, ~Bit4_Shift[1], or_2_out);  // AND_Gate
  and and_3 (and_3_out, ~Bit4_Shift[2], or_3_out);  // AND_Gate
  and and_4 (and_4_out, ~Bit4_Shift[3], or_4_out);  // AND_Gate
  and and_5 (and_5_out, Bit16_Data[0], Bit4_Shift[0]);
  and and_6 (and_6_out, ~Bit4_Shift[0], Bit16_Data[1]);  // AND_Gate
  or or_2 (or_2_out, and_1_out, and_13_out);
  and and_7 (and_7_out, or_2_out, Bit4_Shift[1]);
  and and_8 (and_8_out, ~Bit4_Shift[1], or_6_out);  // AND_Gate
  or or_3 (or_3_out, and_2_out, and_23_out);
  and and_9 (and_9_out, or_3_out, Bit4_Shift[2]);
  and and_10 (and_10_out, ~Bit4_Shift[2], or_7_out);  // AND_Gate
  or or_4 (or_4_out, and_3_out, and_41_out);
  and and_11 (and_11_out, or_4_out, Bit4_Shift[3]);
  and and_12 (and_12_out, ~Bit4_Shift[3], or_8_out);  // AND_Gate
  or or_5 (Bit16_Result[0], and_4_out, and_75_out);
  and and_13 (and_13_out, Bit16_Data[1], Bit4_Shift[0]);
  and and_14 (and_14_out, ~Bit4_Shift[0], Bit16_Data[2]);  // AND_Gate
  or or_6 (or_6_out, and_6_out, and_21_out);
  and and_15 (and_15_out, or_6_out, Bit4_Shift[1]);
  and and_16 (and_16_out, ~Bit4_Shift[1], or_10_out);  // AND_Gate
  or or_7 (or_7_out, and_8_out, and_31_out);
  and and_17 (and_17_out, or_7_out, Bit4_Shift[2]);
  and and_18 (and_18_out, ~Bit4_Shift[2], or_11_out);  // AND_Gate
  or or_8 (or_8_out, and_10_out, and_50_out);
  and and_19 (and_19_out, or_8_out, Bit4_Shift[3]);
  and and_20 (and_20_out, ~Bit4_Shift[3], or_12_out);  // AND_Gate
  or or_9 (Bit16_Result[1], and_12_out, and_83_out);
  and and_21 (and_21_out, Bit16_Data[2], Bit4_Shift[0]);
  and and_22 (and_22_out, ~Bit4_Shift[0], Bit16_Data[3]);  // AND_Gate
  or or_10 (or_10_out, and_14_out, and_29_out);
  and and_23 (and_23_out, or_10_out, Bit4_Shift[1]);
  and and_24 (and_24_out, ~Bit4_Shift[1], or_14_out);  // AND_Gate
  or or_11 (or_11_out, and_16_out, and_39_out);
  and and_25 (and_25_out, or_11_out, Bit4_Shift[2]);
  and and_26 (and_26_out, ~Bit4_Shift[2], or_15_out);  // AND_Gate
  or or_12 (or_12_out, and_18_out, and_57_out);
  and and_27 (and_27_out, or_12_out, Bit4_Shift[3]);
  and and_28 (and_28_out, ~Bit4_Shift[3], or_16_out);  // AND_Gate
  or or_13 (Bit16_Result[2], and_20_out, and_91_out);
  and and_29 (and_29_out, Bit16_Data[3], Bit4_Shift[0]);
  and and_30 (and_30_out, ~Bit4_Shift[0], Bit16_Data[4]);  // AND_Gate
  or or_14 (or_14_out, and_22_out, and_37_out);
  and and_31 (and_31_out, or_14_out, Bit4_Shift[1]);
  and and_32 (and_32_out, ~Bit4_Shift[1], or_18_out);  // AND_Gate
  or or_15 (or_15_out, and_24_out, and_48_out);
  and and_33 (and_33_out, or_15_out, Bit4_Shift[2]);
  and and_34 (and_34_out, ~Bit4_Shift[2], or_19_out);  // AND_Gate
  or or_16 (or_16_out, and_26_out, and_65_out);
  and and_35 (and_35_out, or_16_out, Bit4_Shift[3]);
  and and_36 (and_36_out, ~Bit4_Shift[3], or_20_out);  // AND_Gate
  or or_17 (Bit16_Result[3], and_28_out, and_99_out);
  and and_37 (and_37_out, Bit16_Data[4], Bit4_Shift[0]);
  and and_38 (and_38_out, ~Bit4_Shift[0], Bit16_Data[5]);  // AND_Gate
  or or_18 (or_18_out, and_30_out, and_46_out);
  and and_39 (and_39_out, or_18_out, Bit4_Shift[1]);
  and and_40 (and_40_out, ~Bit4_Shift[1], or_22_out);  // AND_Gate
  or or_19 (or_19_out, and_32_out, and_55_out);
  and and_41 (and_41_out, or_19_out, Bit4_Shift[2]);
  and and_42 (and_42_out, ~Bit4_Shift[2], or_23_out);  // AND_Gate
  or or_20 (or_20_out, and_34_out, and_73_out);
  and and_43 (and_43_out, or_20_out, Bit4_Shift[3]);
  and and_44 (and_44_out, ~Bit4_Shift[3], or_24_out);  // AND_Gate
  or or_21 (Bit16_Result[4], and_36_out, and_107_out);
  and and_45 (and_45_out, ~Bit4_Shift[0], Bit16_Data[6]);  // AND_Gate
  and and_46 (and_46_out, Bit16_Data[5], Bit4_Shift[0]);
  or or_22 (or_22_out, and_38_out, and_53_out);
  and and_47 (and_47_out, ~Bit4_Shift[1], or_26_out);  // AND_Gate
  and and_48 (and_48_out, or_22_out, Bit4_Shift[1]);
  or or_23 (or_23_out, and_40_out, and_63_out);
  and and_49 (and_49_out, ~Bit4_Shift[2], or_27_out);  // AND_Gate
  and and_50 (and_50_out, or_23_out, Bit4_Shift[2]);
  or or_24 (or_24_out, and_42_out, and_81_out);
  and and_51 (and_51_out, ~Bit4_Shift[3], or_28_out);  // AND_Gate
  and and_52 (and_52_out, or_24_out, Bit4_Shift[3]);
  or or_25 (Bit16_Result[5], and_44_out, and_115_out);
  and and_53 (and_53_out, Bit16_Data[6], Bit4_Shift[0]);
  and and_54 (and_54_out, ~Bit4_Shift[0], Bit16_Data[7]);  // AND_Gate
  or or_26 (or_26_out, and_45_out, and_61_out);
  and and_55 (and_55_out, or_26_out, Bit4_Shift[1]);
  and and_56 (and_56_out, ~Bit4_Shift[1], or_30_out);  // AND_Gate
  or or_27 (or_27_out, and_47_out, and_71_out);
  and and_57 (and_57_out, or_27_out, Bit4_Shift[2]);
  and and_58 (and_58_out, ~Bit4_Shift[2], or_31_out);  // AND_Gate
  or or_28 (or_28_out, and_49_out, and_89_out);
  and and_59 (and_59_out, or_28_out, Bit4_Shift[3]);
  and and_60 (and_60_out, ~Bit4_Shift[3], or_32_out);  // AND_Gate
  or or_29 (Bit16_Result[6], and_51_out, and_123_out);
  and and_61 (and_61_out, Bit16_Data[7], Bit4_Shift[0]);
  and and_62 (and_62_out, ~Bit4_Shift[0], Bit16_Data[8]);  // AND_Gate
  or or_30 (or_30_out, and_54_out, and_69_out);
  and and_63 (and_63_out, or_30_out, Bit4_Shift[1]);
  and and_64 (and_64_out, ~Bit4_Shift[1], or_34_out);  // AND_Gate
  or or_31 (or_31_out, and_56_out, and_79_out);
  and and_65 (and_65_out, or_31_out, Bit4_Shift[2]);
  and and_66 (and_66_out, ~Bit4_Shift[2], or_35_out);  // AND_Gate
  or or_32 (or_32_out, and_58_out, and_97_out);
  and and_67 (and_67_out, or_32_out, Bit4_Shift[3]);
  and and_68 (Bit16_Result[8], ~Bit4_Shift[3], or_36_out);  // AND_Gate
  or or_33 (Bit16_Result[7], and_60_out, and_128_out);
  and and_69 (and_69_out, Bit16_Data[8], Bit4_Shift[0]);
  and and_70 (and_70_out, ~Bit4_Shift[0], Bit16_Data[9]);  // AND_Gate
  or or_34 (or_34_out, and_62_out, and_77_out);
  and and_71 (and_71_out, or_34_out, Bit4_Shift[1]);
  and and_72 (and_72_out, ~Bit4_Shift[1], or_37_out);  // AND_Gate
  or or_35 (or_35_out, and_64_out, and_87_out);
  and and_73 (and_73_out, or_35_out, Bit4_Shift[2]);
  and and_74 (and_74_out, ~Bit4_Shift[2], or_38_out);  // AND_Gate
  or or_36 (or_36_out, and_66_out, and_105_out);
  and and_75 (and_75_out, or_36_out, Bit4_Shift[3]);
  and and_76 (Bit16_Result[9], ~Bit4_Shift[3], or_39_out);  // AND_Gate
  and and_77 (and_77_out, Bit16_Data[9], Bit4_Shift[0]);
  and and_78 (and_78_out, ~Bit4_Shift[0], Bit16_Data[10]);  // AND_Gate
  or or_37 (or_37_out, and_70_out, and_85_out);
  and and_79 (and_79_out, or_37_out, Bit4_Shift[1]);
  and and_80 (and_80_out, ~Bit4_Shift[1], or_40_out);  // AND_Gate
  or or_38 (or_38_out, and_72_out, and_95_out);
  and and_81 (and_81_out, or_38_out, Bit4_Shift[2]);
  and and_82 (and_82_out, ~Bit4_Shift[2], or_41_out);  // AND_Gate
  or or_39 (or_39_out, and_74_out, and_113_out);
  and and_83 (and_83_out, or_39_out, Bit4_Shift[3]);
  and and_84 (Bit16_Result[10], ~Bit4_Shift[3], or_42_out);  // AND_Gate
  and and_85 (and_85_out, Bit16_Data[10], Bit4_Shift[0]);
  and and_86 (and_86_out, ~Bit4_Shift[0], Bit16_Data[11]);  // AND_Gate
  or or_40 (or_40_out, and_78_out, and_93_out);
  and and_87 (and_87_out, or_40_out, Bit4_Shift[1]);
  and and_88 (and_88_out, ~Bit4_Shift[1], or_43_out);  // AND_Gate
  or or_41 (or_41_out, and_80_out, and_103_out);
  and and_89 (and_89_out, or_41_out, Bit4_Shift[2]);
  and and_90 (and_90_out, ~Bit4_Shift[2], or_44_out);  // AND_Gate
  or or_42 (or_42_out, and_82_out, and_121_out);
  and and_91 (and_91_out, or_42_out, Bit4_Shift[3]);
  and and_92 (Bit16_Result[11], ~Bit4_Shift[3], or_45_out);  // AND_Gate
  and and_93 (and_93_out, Bit16_Data[11], Bit4_Shift[0]);
  and and_94 (and_94_out, ~Bit4_Shift[0], Bit16_Data[12]);  // AND_Gate
  or or_43 (or_43_out, and_86_out, and_101_out);
  and and_95 (and_95_out, or_43_out, Bit4_Shift[1]);
  and and_96 (and_96_out, ~Bit4_Shift[1], or_46_out);  // AND_Gate
  or or_44 (or_44_out, and_88_out, and_111_out);
  and and_97 (and_97_out, or_44_out, Bit4_Shift[2]);
  and and_98 (and_98_out, ~Bit4_Shift[2], or_47_out);  // AND_Gate
  or or_45 (or_45_out, and_90_out, and_127_out);
  and and_99 (and_99_out, or_45_out, Bit4_Shift[3]);
  and and_100 (Bit16_Result[12], ~Bit4_Shift[3], and_98_out);  // AND_Gate
  and and_101 (and_101_out, Bit16_Data[12], Bit4_Shift[0]);
  and and_102 (and_102_out, ~Bit4_Shift[0], Bit16_Data[13]);  // AND_Gate
  or or_46 (or_46_out, and_94_out, and_109_out);
  and and_103 (and_103_out, or_46_out, Bit4_Shift[1]);
  and and_104 (and_104_out, ~Bit4_Shift[1], or_48_out);  // AND_Gate
  or or_47 (or_47_out, and_96_out, and_119_out);
  and and_105 (and_105_out, or_47_out, Bit4_Shift[2]);
  and and_106 (and_106_out, ~Bit4_Shift[2], or_49_out);  // AND_Gate
  and and_107 (and_107_out, and_98_out, Bit4_Shift[3]);
  and and_108 (Bit16_Result[13], ~Bit4_Shift[3], and_106_out);  // AND_Gate
  and and_109 (and_109_out, Bit16_Data[13], Bit4_Shift[0]);
  and and_110 (and_110_out, ~Bit4_Shift[0], Bit16_Data[14]);  // AND_Gate
  or or_48 (or_48_out, and_102_out, and_117_out);
  and and_111 (and_111_out, or_48_out, Bit4_Shift[1]);
  and and_112 (and_112_out, ~Bit4_Shift[1], or_50_out);  // AND_Gate
  or or_49 (or_49_out, and_104_out, and_126_out);
  and and_113 (and_113_out, or_49_out, Bit4_Shift[2]);
  and and_114 (and_114_out, ~Bit4_Shift[2], and_112_out);  // AND_Gate
  and and_115 (and_115_out, and_106_out, Bit4_Shift[3]);
  and and_116 (Bit16_Result[14], ~Bit4_Shift[3], and_114_out);  // AND_Gate
  and and_117 (and_117_out, Bit16_Data[14], Bit4_Shift[0]);
  and and_118 (and_118_out, ~Bit4_Shift[0], Bit16_Data[15]);  // AND_Gate
  or or_50 (or_50_out, and_110_out, and_125_out);
  and and_119 (and_119_out, or_50_out, Bit4_Shift[1]);
  and and_120 (and_120_out, ~Bit4_Shift[1], and_118_out);  // AND_Gate
  and and_121 (and_121_out, and_112_out, Bit4_Shift[2]);
  and and_122 (and_122_out, ~Bit4_Shift[2], and_120_out);  // AND_Gate
  and and_123 (and_123_out, and_114_out, Bit4_Shift[3]);
  and and_124 (Bit16_Result[15], ~Bit4_Shift[3], and_122_out);  // AND_Gate
  and and_125 (and_125_out, Bit16_Data[15], Bit4_Shift[0]);
  and and_126 (and_126_out, and_118_out, Bit4_Shift[1]);
  and and_127 (and_127_out, and_120_out, Bit4_Shift[2]);
  and and_128 (and_128_out, and_122_out, Bit4_Shift[3]);
endmodule

module Bit4_Controlled_Buffer (
  input  [3:0] Bit4_In,
  input  Enable,
  output [3:0] Bit4_Out
);

  and and_1 (Bit4_Out[0], Bit4_In[0], Enable);
  and and_2 (Bit4_Out[1], Bit4_In[1], Enable);
  and and_3 (Bit4_Out[2], Bit4_In[2], Enable);
  and and_4 (Bit4_Out[3], Bit4_In[3], Enable);
endmodule

module Bit4_Twos_Complementer (
  input  [3:0] Bit4_In,
  output [3:0] Bit4_Result
);

  wire or_1_out, or_2_out;

  or or_1 (or_1_out, Bit4_In[0], Bit4_Result[1]);
  or or_2 (or_2_out, Bit4_In[0], Bit4_Result[1], Bit4_Result[2]);
  xor xor_1 (Bit4_Result[1], Bit4_In[1], Bit4_In[0]);
  xor xor_2 (Bit4_Result[2], Bit4_In[2], or_1_out);
  xor xor_3 (Bit4_Result[3], Bit4_In[3], or_2_out);

  assign Bit4_Result[0] = Bit4_In[0];
endmodule

module Bit4_Adder (
  input  Cin,
  input  [3:0] Bit4_A,
  input  [3:0] Bit4_B,
  output Cout,
  output [3:0] Bit4_Result
);

  wire and_1_out, and_2_out, and_3_out, and_4_out, bit4_cla_logic_1_c2, bit4_cla_logic_1_c3,
       bit4_cla_logic_1_c4, xor_1_out, xor_2_out, xor_3_out, xor_4_out;

  xor xor_1 (xor_1_out, Bit4_A[0], Bit4_B[0]);
  and and_1 (and_1_out, Bit4_B[0], Bit4_A[0]);
  xor xor_2 (xor_2_out, Bit4_A[1], Bit4_B[1]);
  and and_2 (and_2_out, Bit4_B[1], Bit4_A[1]);
  xor xor_3 (xor_3_out, Bit4_A[2], Bit4_B[2]);
  and and_3 (and_3_out, Bit4_B[2], Bit4_A[2]);
  xor xor_4 (xor_4_out, Bit4_A[3], Bit4_B[3]);
  and and_4 (and_4_out, Bit4_B[3], Bit4_A[3]);
  xor xor_5 (Bit4_Result[3], xor_4_out, Cin);
  xor xor_6 (Bit4_Result[2], xor_3_out, bit4_cla_logic_1_c2);
  xor xor_7 (Bit4_Result[0], xor_1_out, bit4_cla_logic_1_c4);
  xor xor_8 (Bit4_Result[1], xor_2_out, bit4_cla_logic_1_c3);
  Bit4_CLA_Logic bit4_cla_logic_1 (
    .Cin(Cin), .P1(xor_1_out), .G1(and_1_out), .P2(xor_2_out), .G2(and_2_out), .P3(xor_3_out),
    .G3(and_3_out), .P4(xor_4_out), .G4(and_4_out), .C2(bit4_cla_logic_1_c2), .C3(bit4_cla_logic_1_c3),
    .C4(bit4_cla_logic_1_c4), .COUT(Cout));  // open: PG
endmodule

module Bit5_Adder (
  input  Cin,
  input  [4:0] Bit5_A,
  input  [4:0] Bit5_B,
  output [4:0] Bit5_Result,
  output Cout
);

  wire and_1_out, and_2_out, and_3_out, and_4_out, and_5_out, and_6_out, and_7_out, and_8_out, and_9_out,
       and_10_out, and_11_out, and_12_out, and_13_out, and_14_out, and_15_out, and_16_out, and_17_out,
       and_18_out, and_19_out, and_20_out, or_1_out, or_2_out, or_3_out, or_4_out, xor_1_out, xor_2_out,
       xor_3_out, xor_4_out, xor_5_out;

  xor xor_1 (xor_1_out, Bit5_B[3], Bit5_A[3]);
  and and_1 (and_1_out, Bit5_A[3], Bit5_B[3]);
  xor xor_2 (xor_2_out, Bit5_B[4], Bit5_A[4]);
  and and_2 (and_2_out, Bit5_A[4], Bit5_B[4]);
  xor xor_3 (xor_3_out, Bit5_B[0], Bit5_A[0]);
  and and_3 (and_3_out, Bit5_A[0], Bit5_B[0]);
  xor xor_4 (xor_4_out, Bit5_B[1], Bit5_A[1]);
  and and_4 (and_4_out, Bit5_A[1], Bit5_B[1]);
  xor xor_5 (xor_5_out, Bit5_B[2], Bit5_A[2]);
  and and_5 (and_5_out, Bit5_A[2], Bit5_B[2]);
  xor xor_6 (Bit5_Result[3], or_3_out, xor_1_out);
  xor xor_7 (Bit5_Result[4], or_4_out, xor_2_out);
  xor xor_8 (Bit5_Result[2], or_2_out, xor_5_out);
  xor xor_9 (Bit5_Result[0], Cin, xor_3_out);
  or or_1 (or_1_out, and_3_out, and_6_out);
  xor xor_10 (Bit5_Result[1], or_1_out, xor_4_out);
  or or_2 (or_2_out, and_4_out, and_7_out, and_8_out);
  or or_3 (or_3_out, and_5_out, and_9_out, and_10_out, and_11_out);
  or or_4 (or_4_out, and_1_out, and_12_out, and_13_out, and_14_out, and_15_out);
  or or_5 (Cout, and_2_out, and_16_out, and_17_out, and_18_out, and_19_out, and_20_out);
  and and_6 (and_6_out, xor_3_out, Cin);
  and and_7 (and_7_out, xor_4_out, and_3_out);
  and and_8 (and_8_out, xor_4_out, xor_3_out, Cin);
  and and_9 (and_9_out, and_4_out, xor_5_out);
  and and_10 (and_10_out, xor_5_out, xor_4_out, and_3_out);
  and and_11 (and_11_out, xor_5_out, xor_4_out, Cin, xor_3_out);
  and and_12 (and_12_out, and_5_out, xor_1_out);
  and and_13 (and_13_out, xor_1_out, xor_5_out, and_4_out);
  and and_14 (and_14_out, xor_1_out, xor_5_out, xor_4_out, and_3_out);
  and and_15 (and_15_out, xor_1_out, xor_5_out, xor_4_out, xor_3_out, Cin);
  and and_16 (and_16_out, xor_2_out, and_1_out);
  and and_17 (and_17_out, xor_2_out, xor_1_out, and_5_out);
  and and_18 (and_18_out, xor_2_out, xor_1_out, xor_5_out, and_4_out);
  and and_19 (and_19_out, xor_2_out, xor_1_out, xor_5_out, xor_4_out, and_3_out);
  and and_20 (and_20_out, xor_2_out, xor_1_out, xor_5_out, xor_4_out, xor_3_out, Cin);

  // Notes on the sheet:
  //   0
endmodule

module Bit5_Twos_Complementer (
  input  [4:0] Bit5_In,
  output [4:0] Bit5_Result
);

  wire or_1_out, or_2_out, or_3_out;

  or or_1 (or_1_out, Bit5_In[0], Bit5_Result[1]);
  or or_2 (or_2_out, Bit5_In[0], Bit5_Result[1], Bit5_Result[2]);
  or or_3 (or_3_out, Bit5_Result[3], Bit5_Result[1], Bit5_Result[2], Bit5_In[0]);
  xor xor_1 (Bit5_Result[1], Bit5_In[1], Bit5_In[0]);
  xor xor_2 (Bit5_Result[2], Bit5_In[2], or_1_out);
  xor xor_3 (Bit5_Result[3], Bit5_In[3], or_2_out);
  xor xor_4 (Bit5_Result[4], or_3_out, Bit5_In[4]);

  assign Bit5_Result[0] = Bit5_In[0];
endmodule

module Bit16T24_Right_Shift (
  input  [15:0] Bit16_Data,
  input  [3:0] Bit4_Shift,
  output [23:0] Bit24_Result,
  output [15:0] Bit16_Result,
  output Shift_Overflow_For_Bit16
);

  wire and_1_out, and_2_out, and_3_out, and_4_out, and_5_out, and_6_out, and_7_out, and_8_out, and_9_out,
       and_10_out, and_11_out, and_12_out, and_13_out, and_14_out, and_15_out, and_16_out, and_17_out,
       and_18_out, and_19_out, and_20_out, and_21_out, and_22_out, and_23_out, and_24_out, and_25_out,
       and_26_out, and_27_out, and_28_out, and_29_out, and_30_out, and_31_out, and_32_out, and_33_out,
       and_34_out, and_35_out, and_36_out, and_37_out, and_38_out, and_39_out, and_40_out, and_41_out,
       and_42_out, and_43_out, and_44_out, and_45_out, and_46_out, and_47_out, and_48_out, and_49_out,
       and_50_out, and_51_out, and_52_out, and_53_out, and_54_out, and_55_out, and_56_out, and_57_out,
       and_58_out, and_59_out, and_60_out, and_61_out, and_62_out, and_63_out, and_64_out, and_65_out,
       and_66_out, and_67_out, and_68_out, and_69_out, and_70_out, and_71_out, and_72_out, and_73_out,
       and_74_out, and_75_out, and_76_out, and_77_out, and_78_out, and_79_out, and_80_out, and_81_out,
       and_82_out, and_83_out, and_84_out, and_86_out, and_87_out, and_88_out, and_89_out, and_90_out,
       and_91_out, and_92_out, and_94_out, and_95_out, and_96_out, and_97_out, and_98_out, and_99_out,
       and_100_out, and_102_out, and_103_out, and_104_out, and_105_out, and_106_out, and_107_out,
       and_108_out, and_110_out, and_111_out, and_112_out, and_113_out, and_114_out, and_115_out,
       and_116_out, and_118_out, and_119_out, and_120_out, and_121_out, and_122_out, and_123_out,
       and_124_out, and_126_out, and_127_out, and_128_out, and_129_out, and_130_out, and_131_out,
       and_132_out, and_134_out, and_135_out, and_136_out, and_137_out, and_138_out, and_139_out,
       and_140_out, and_142_out, or_6_out, or_8_out, or_10_out, or_11_out, or_13_out, or_14_out, or_16_out,
       or_17_out, or_18_out, or_20_out, or_21_out, or_22_out, or_24_out, or_25_out, or_26_out, or_28_out,
       or_29_out, or_30_out, or_32_out, or_33_out, or_34_out, or_36_out, or_37_out, or_38_out, or_40_out,
       or_41_out, or_42_out, or_44_out, or_45_out, or_46_out, or_48_out, or_49_out, or_50_out, or_51_out,
       or_52_out, or_53_out, or_54_out, or_55_out, or_56_out, or_57_out, or_58_out, or_59_out, or_60_out,
       or_61_out, or_62_out, or_63_out, or_64_out;

  or or_1 (Shift_Overflow_For_Bit16, and_16_out, and_18_out, and_26_out, and_20_out, and_28_out, and_36_out, and_44_out, and_22_out, and_30_out, and_38_out, and_46_out, and_54_out, and_62_out, and_70_out, and_78_out);
  or or_2 (Bit24_Result[0], and_2_out, and_22_out);
  or or_3 (Bit24_Result[1], and_4_out, and_30_out);
  or or_4 (Bit24_Result[2], and_8_out, and_38_out);
  or or_5 (Bit24_Result[3], and_14_out, and_46_out);
  or or_6 (or_6_out, and_6_out, and_20_out);
  and and_1 (and_1_out, ~Bit4_Shift[3], or_6_out);  // AND_Gate
  and and_2 (and_2_out, or_6_out, Bit4_Shift[3]);
  or or_7 (Bit24_Result[4], and_1_out, and_54_out);
  or or_8 (or_8_out, and_12_out, and_28_out);
  and and_3 (and_3_out, ~Bit4_Shift[3], or_8_out);  // AND_Gate
  and and_4 (and_4_out, or_8_out, Bit4_Shift[3]);
  or or_9 (Bit24_Result[5], and_3_out, and_62_out);
  or or_10 (or_10_out, and_10_out, and_18_out);
  and and_5 (and_5_out, ~Bit4_Shift[2], or_10_out);  // AND_Gate
  and and_6 (and_6_out, or_10_out, Bit4_Shift[2]);
  or or_11 (or_11_out, and_5_out, and_36_out);
  and and_7 (and_7_out, ~Bit4_Shift[3], or_11_out);  // AND_Gate
  and and_8 (and_8_out, or_11_out, Bit4_Shift[3]);
  or or_12 (Bit24_Result[6], and_7_out, and_70_out);
  and and_9 (and_9_out, ~Bit4_Shift[1], and_16_out);  // AND_Gate
  and and_10 (and_10_out, and_16_out, Bit4_Shift[1]);
  or or_13 (or_13_out, and_9_out, and_26_out);
  and and_11 (and_11_out, ~Bit4_Shift[2], or_13_out);  // AND_Gate
  and and_12 (and_12_out, or_13_out, Bit4_Shift[2]);
  or or_14 (or_14_out, and_11_out, and_44_out);
  and and_13 (and_13_out, ~Bit4_Shift[3], or_14_out);  // AND_Gate
  and and_14 (and_14_out, or_14_out, Bit4_Shift[3]);
  or or_15 (Bit24_Result[7], and_13_out, and_78_out);
  and and_15 (and_15_out, ~Bit4_Shift[0], Bit16_Data[0]);  // AND_Gate
  and and_16 (and_16_out, Bit16_Data[0], Bit4_Shift[0]);
  or or_16 (or_16_out, and_15_out, and_24_out);
  and and_17 (and_17_out, ~Bit4_Shift[1], or_16_out);  // AND_Gate
  and and_18 (and_18_out, or_16_out, Bit4_Shift[1]);
  or or_17 (or_17_out, and_17_out, and_34_out);
  and and_19 (and_19_out, ~Bit4_Shift[2], or_17_out);  // AND_Gate
  and and_20 (and_20_out, or_17_out, Bit4_Shift[2]);
  or or_18 (or_18_out, and_19_out, and_52_out);
  and and_21 (and_21_out, ~Bit4_Shift[3], or_18_out);  // AND_Gate
  and and_22 (and_22_out, or_18_out, Bit4_Shift[3]);
  or or_19 (Bit16_Result[0], and_21_out, and_86_out);
  and and_23 (and_23_out, ~Bit4_Shift[0], Bit16_Data[1]);  // AND_Gate
  and and_24 (and_24_out, Bit16_Data[1], Bit4_Shift[0]);
  or or_20 (or_20_out, and_23_out, and_32_out);
  and and_25 (and_25_out, ~Bit4_Shift[1], or_20_out);  // AND_Gate
  and and_26 (and_26_out, or_20_out, Bit4_Shift[1]);
  or or_21 (or_21_out, and_25_out, and_42_out);
  and and_27 (and_27_out, ~Bit4_Shift[2], or_21_out);  // AND_Gate
  and and_28 (and_28_out, or_21_out, Bit4_Shift[2]);
  or or_22 (or_22_out, and_27_out, and_60_out);
  and and_29 (and_29_out, ~Bit4_Shift[3], or_22_out);  // AND_Gate
  and and_30 (and_30_out, or_22_out, Bit4_Shift[3]);
  or or_23 (Bit16_Result[1], and_29_out, and_94_out);
  and and_31 (and_31_out, ~Bit4_Shift[0], Bit16_Data[2]);  // AND_Gate
  and and_32 (and_32_out, Bit16_Data[2], Bit4_Shift[0]);
  or or_24 (or_24_out, and_31_out, and_40_out);
  and and_33 (and_33_out, ~Bit4_Shift[1], or_24_out);  // AND_Gate
  and and_34 (and_34_out, or_24_out, Bit4_Shift[1]);
  or or_25 (or_25_out, and_33_out, and_50_out);
  and and_35 (and_35_out, ~Bit4_Shift[2], or_25_out);  // AND_Gate
  and and_36 (and_36_out, or_25_out, Bit4_Shift[2]);
  or or_26 (or_26_out, and_35_out, and_68_out);
  and and_37 (and_37_out, ~Bit4_Shift[3], or_26_out);  // AND_Gate
  and and_38 (and_38_out, or_26_out, Bit4_Shift[3]);
  or or_27 (Bit16_Result[2], and_37_out, and_102_out);
  and and_39 (and_39_out, ~Bit4_Shift[0], Bit16_Data[3]);  // AND_Gate
  and and_40 (and_40_out, Bit16_Data[3], Bit4_Shift[0]);
  or or_28 (or_28_out, and_39_out, and_48_out);
  and and_41 (and_41_out, ~Bit4_Shift[1], or_28_out);  // AND_Gate
  and and_42 (and_42_out, or_28_out, Bit4_Shift[1]);
  or or_29 (or_29_out, and_41_out, and_58_out);
  and and_43 (and_43_out, ~Bit4_Shift[2], or_29_out);  // AND_Gate
  and and_44 (and_44_out, or_29_out, Bit4_Shift[2]);
  or or_30 (or_30_out, and_43_out, and_76_out);
  and and_45 (and_45_out, ~Bit4_Shift[3], or_30_out);  // AND_Gate
  and and_46 (and_46_out, or_30_out, Bit4_Shift[3]);
  or or_31 (Bit16_Result[3], and_45_out, and_110_out);
  and and_47 (and_47_out, ~Bit4_Shift[0], Bit16_Data[4]);  // AND_Gate
  and and_48 (and_48_out, Bit16_Data[4], Bit4_Shift[0]);
  or or_32 (or_32_out, and_47_out, and_56_out);
  and and_49 (and_49_out, ~Bit4_Shift[1], or_32_out);  // AND_Gate
  and and_50 (and_50_out, or_32_out, Bit4_Shift[1]);
  or or_33 (or_33_out, and_49_out, and_66_out);
  and and_51 (and_51_out, ~Bit4_Shift[2], or_33_out);  // AND_Gate
  and and_52 (and_52_out, or_33_out, Bit4_Shift[2]);
  or or_34 (or_34_out, and_51_out, and_84_out);
  and and_53 (and_53_out, ~Bit4_Shift[3], or_34_out);  // AND_Gate
  and and_54 (and_54_out, or_34_out, Bit4_Shift[3]);
  or or_35 (Bit16_Result[4], and_53_out, and_118_out);
  and and_55 (and_55_out, ~Bit4_Shift[0], Bit16_Data[5]);  // AND_Gate
  and and_56 (and_56_out, Bit16_Data[5], Bit4_Shift[0]);
  or or_36 (or_36_out, and_55_out, and_64_out);
  and and_57 (and_57_out, ~Bit4_Shift[1], or_36_out);  // AND_Gate
  and and_58 (and_58_out, or_36_out, Bit4_Shift[1]);
  or or_37 (or_37_out, and_57_out, and_74_out);
  and and_59 (and_59_out, ~Bit4_Shift[2], or_37_out);  // AND_Gate
  and and_60 (and_60_out, or_37_out, Bit4_Shift[2]);
  or or_38 (or_38_out, and_59_out, and_92_out);
  and and_61 (and_61_out, ~Bit4_Shift[3], or_38_out);  // AND_Gate
  and and_62 (and_62_out, or_38_out, Bit4_Shift[3]);
  or or_39 (Bit16_Result[5], and_61_out, and_126_out);
  and and_63 (and_63_out, ~Bit4_Shift[0], Bit16_Data[6]);  // AND_Gate
  and and_64 (and_64_out, Bit16_Data[6], Bit4_Shift[0]);
  or or_40 (or_40_out, and_63_out, and_72_out);
  and and_65 (and_65_out, ~Bit4_Shift[1], or_40_out);  // AND_Gate
  and and_66 (and_66_out, or_40_out, Bit4_Shift[1]);
  or or_41 (or_41_out, and_65_out, and_82_out);
  and and_67 (and_67_out, ~Bit4_Shift[2], or_41_out);  // AND_Gate
  and and_68 (and_68_out, or_41_out, Bit4_Shift[2]);
  or or_42 (or_42_out, and_67_out, and_100_out);
  and and_69 (and_69_out, ~Bit4_Shift[3], or_42_out);  // AND_Gate
  and and_70 (and_70_out, or_42_out, Bit4_Shift[3]);
  or or_43 (Bit16_Result[6], and_69_out, and_134_out);
  and and_71 (and_71_out, ~Bit4_Shift[0], Bit16_Data[7]);  // AND_Gate
  and and_72 (and_72_out, Bit16_Data[7], Bit4_Shift[0]);
  or or_44 (or_44_out, and_71_out, and_80_out);
  and and_73 (and_73_out, ~Bit4_Shift[1], or_44_out);  // AND_Gate
  and and_74 (and_74_out, or_44_out, Bit4_Shift[1]);
  or or_45 (or_45_out, and_73_out, and_90_out);
  and and_75 (and_75_out, ~Bit4_Shift[2], or_45_out);  // AND_Gate
  and and_76 (and_76_out, or_45_out, Bit4_Shift[2]);
  or or_46 (or_46_out, and_75_out, and_108_out);
  and and_77 (and_77_out, ~Bit4_Shift[3], or_46_out);  // AND_Gate
  and and_78 (and_78_out, or_46_out, Bit4_Shift[3]);
  or or_47 (Bit16_Result[7], and_77_out, and_142_out);
  and and_79 (and_79_out, ~Bit4_Shift[0], Bit16_Data[8]);  // AND_Gate
  and and_80 (and_80_out, Bit16_Data[8], Bit4_Shift[0]);
  or or_48 (or_48_out, and_79_out, and_88_out);
  and and_81 (and_81_out, ~Bit4_Shift[1], or_48_out);  // AND_Gate
  and and_82 (and_82_out, or_48_out, Bit4_Shift[1]);
  or or_49 (or_49_out, and_81_out, and_98_out);
  and and_83 (and_83_out, ~Bit4_Shift[2], or_49_out);  // AND_Gate
  and and_84 (and_84_out, or_49_out, Bit4_Shift[2]);
  or or_50 (or_50_out, and_83_out, and_116_out);
  and and_85 (Bit16_Result[8], ~Bit4_Shift[3], or_50_out);  // AND_Gate
  and and_86 (and_86_out, or_50_out, Bit4_Shift[3]);
  and and_87 (and_87_out, ~Bit4_Shift[0], Bit16_Data[9]);  // AND_Gate
  and and_88 (and_88_out, Bit16_Data[9], Bit4_Shift[0]);
  or or_51 (or_51_out, and_87_out, and_96_out);
  and and_89 (and_89_out, ~Bit4_Shift[1], or_51_out);  // AND_Gate
  and and_90 (and_90_out, or_51_out, Bit4_Shift[1]);
  or or_52 (or_52_out, and_89_out, and_106_out);
  and and_91 (and_91_out, ~Bit4_Shift[2], or_52_out);  // AND_Gate
  and and_92 (and_92_out, or_52_out, Bit4_Shift[2]);
  or or_53 (or_53_out, and_91_out, and_124_out);
  and and_93 (Bit16_Result[9], ~Bit4_Shift[3], or_53_out);  // AND_Gate
  and and_94 (and_94_out, or_53_out, Bit4_Shift[3]);
  and and_95 (and_95_out, ~Bit4_Shift[0], Bit16_Data[10]);  // AND_Gate
  and and_96 (and_96_out, Bit16_Data[10], Bit4_Shift[0]);
  or or_54 (or_54_out, and_95_out, and_104_out);
  and and_97 (and_97_out, ~Bit4_Shift[1], or_54_out);  // AND_Gate
  and and_98 (and_98_out, or_54_out, Bit4_Shift[1]);
  or or_55 (or_55_out, and_97_out, and_114_out);
  and and_99 (and_99_out, ~Bit4_Shift[2], or_55_out);  // AND_Gate
  and and_100 (and_100_out, or_55_out, Bit4_Shift[2]);
  or or_56 (or_56_out, and_99_out, and_132_out);
  and and_101 (Bit16_Result[10], ~Bit4_Shift[3], or_56_out);  // AND_Gate
  and and_102 (and_102_out, or_56_out, Bit4_Shift[3]);
  and and_103 (and_103_out, ~Bit4_Shift[0], Bit16_Data[11]);  // AND_Gate
  and and_104 (and_104_out, Bit16_Data[11], Bit4_Shift[0]);
  or or_57 (or_57_out, and_103_out, and_112_out);
  and and_105 (and_105_out, ~Bit4_Shift[1], or_57_out);  // AND_Gate
  and and_106 (and_106_out, or_57_out, Bit4_Shift[1]);
  or or_58 (or_58_out, and_105_out, and_122_out);
  and and_107 (and_107_out, ~Bit4_Shift[2], or_58_out);  // AND_Gate
  and and_108 (and_108_out, or_58_out, Bit4_Shift[2]);
  or or_59 (or_59_out, and_107_out, and_140_out);
  and and_109 (Bit16_Result[11], ~Bit4_Shift[3], or_59_out);  // AND_Gate
  and and_110 (and_110_out, or_59_out, Bit4_Shift[3]);
  and and_111 (and_111_out, ~Bit4_Shift[0], Bit16_Data[12]);  // AND_Gate
  and and_112 (and_112_out, Bit16_Data[12], Bit4_Shift[0]);
  or or_60 (or_60_out, and_111_out, and_120_out);
  and and_113 (and_113_out, ~Bit4_Shift[1], or_60_out);  // AND_Gate
  and and_114 (and_114_out, or_60_out, Bit4_Shift[1]);
  or or_61 (or_61_out, and_113_out, and_130_out);
  and and_115 (and_115_out, ~Bit4_Shift[2], or_61_out);  // AND_Gate
  and and_116 (and_116_out, or_61_out, Bit4_Shift[2]);
  and and_117 (Bit16_Result[12], ~Bit4_Shift[3], and_115_out);  // AND_Gate
  and and_118 (and_118_out, and_115_out, Bit4_Shift[3]);
  and and_119 (and_119_out, ~Bit4_Shift[0], Bit16_Data[13]);  // AND_Gate
  and and_120 (and_120_out, Bit16_Data[13], Bit4_Shift[0]);
  or or_62 (or_62_out, and_119_out, and_128_out);
  and and_121 (and_121_out, ~Bit4_Shift[1], or_62_out);  // AND_Gate
  and and_122 (and_122_out, or_62_out, Bit4_Shift[1]);
  or or_63 (or_63_out, and_121_out, and_138_out);
  and and_123 (and_123_out, ~Bit4_Shift[2], or_63_out);  // AND_Gate
  and and_124 (and_124_out, or_63_out, Bit4_Shift[2]);
  and and_125 (Bit16_Result[13], ~Bit4_Shift[3], and_123_out);  // AND_Gate
  and and_126 (and_126_out, and_123_out, Bit4_Shift[3]);
  and and_127 (and_127_out, ~Bit4_Shift[0], Bit16_Data[14]);  // AND_Gate
  and and_128 (and_128_out, Bit16_Data[14], Bit4_Shift[0]);
  or or_64 (or_64_out, and_127_out, and_136_out);
  and and_129 (and_129_out, ~Bit4_Shift[1], or_64_out);  // AND_Gate
  and and_130 (and_130_out, or_64_out, Bit4_Shift[1]);
  and and_131 (and_131_out, ~Bit4_Shift[2], and_129_out);  // AND_Gate
  and and_132 (and_132_out, and_129_out, Bit4_Shift[2]);
  and and_133 (Bit16_Result[14], ~Bit4_Shift[3], and_131_out);  // AND_Gate
  and and_134 (and_134_out, and_131_out, Bit4_Shift[3]);
  and and_135 (and_135_out, ~Bit4_Shift[0], Bit16_Data[15]);  // AND_Gate
  and and_136 (and_136_out, Bit16_Data[15], Bit4_Shift[0]);
  and and_137 (and_137_out, ~Bit4_Shift[1], and_135_out);  // AND_Gate
  and and_138 (and_138_out, and_135_out, Bit4_Shift[1]);
  and and_139 (and_139_out, ~Bit4_Shift[2], and_137_out);  // AND_Gate
  and and_140 (and_140_out, and_137_out, Bit4_Shift[2]);
  and and_141 (Bit16_Result[15], ~Bit4_Shift[3], and_139_out);  // AND_Gate
  and and_142 (and_142_out, and_139_out, Bit4_Shift[3]);

  assign Bit24_Result[23:8] = Bit16_Result;
endmodule

module Bit16T24O16_Adder (
  input  FP_Op,
  input  Carry_In,
  input  [15:0] Bit16_A,
  input  [15:0] Bit16_B,
  output [15:0] Bit16_Result,
  output Carry_Out
);

  wire and_1_out, and_2_out, and_3_out, and_4_out, and_5_out, and_6_out, and_7_out, and_8_out, and_9_out,
       and_10_out, and_11_out, and_12_out, and_13_out, and_14_out, and_15_out, and_16_out, and_17_out,
       bit4_cla_logic_1_c2, bit4_cla_logic_1_c3, bit4_cla_logic_1_c4, bit4_cla_logic_1_cout,
       bit4_cla_logic_1_pg, bit4_cla_logic_2_c2, bit4_cla_logic_2_c3, bit4_cla_logic_2_c4,
       bit4_cla_logic_2_cout, bit4_cla_logic_2_pg, bit4_cla_logic_3_c2, bit4_cla_logic_3_c3,
       bit4_cla_logic_3_c4, bit4_cla_logic_3_cout, bit4_cla_logic_3_pg, bit4_cla_logic_4_c2,
       bit4_cla_logic_4_c3, bit4_cla_logic_4_c4, bit4_cla_logic_4_cout, bit4_cla_logic_4_pg,
       bit4_cla_logic_5_c2, bit4_cla_logic_5_c3, bit4_cla_logic_5_c4, bit4_cla_logic_5_cout, xor_1_out,
       xor_2_out, xor_3_out, xor_4_out, xor_5_out, xor_6_out, xor_7_out, xor_8_out, xor_9_out, xor_10_out,
       xor_11_out, xor_12_out, xor_13_out, xor_14_out, xor_15_out, xor_16_out;

  xor xor_1 (xor_1_out, Bit16_A[0], Bit16_B[0]);
  and and_1 (and_1_out, Bit16_B[0], Bit16_A[0]);
  xor xor_2 (xor_2_out, Bit16_A[1], Bit16_B[1]);
  and and_2 (and_2_out, Bit16_B[1], Bit16_A[1]);
  xor xor_3 (xor_3_out, Bit16_A[2], Bit16_B[2]);
  and and_3 (and_3_out, Bit16_B[2], Bit16_A[2]);
  xor xor_4 (xor_4_out, Bit16_A[3], Bit16_B[3]);
  and and_4 (and_4_out, Bit16_B[3], Bit16_A[3]);
  xor xor_5 (xor_5_out, Bit16_A[4], Bit16_B[4]);
  and and_5 (and_5_out, Bit16_B[4], Bit16_A[4]);
  xor xor_6 (xor_6_out, Bit16_A[5], Bit16_B[5]);
  and and_6 (and_6_out, Bit16_B[5], Bit16_A[5]);
  xor xor_7 (xor_7_out, Bit16_A[6], Bit16_B[6]);
  and and_7 (and_7_out, Bit16_B[6], Bit16_A[6]);
  xor xor_8 (xor_8_out, Bit16_A[7], Bit16_B[7]);
  and and_8 (and_8_out, Bit16_B[7], Bit16_A[7]);
  xor xor_9 (xor_9_out, Bit16_A[8], Bit16_B[8]);
  and and_9 (and_9_out, Bit16_B[8], Bit16_A[8]);
  xor xor_10 (xor_10_out, Bit16_A[9], Bit16_B[9]);
  and and_10 (and_10_out, Bit16_B[9], Bit16_A[9]);
  xor xor_11 (xor_11_out, Bit16_A[10], Bit16_B[10]);
  and and_11 (and_11_out, Bit16_B[10], Bit16_A[10]);
  xor xor_12 (xor_12_out, Bit16_A[11], Bit16_B[11]);
  and and_12 (and_12_out, Bit16_B[11], Bit16_A[11]);
  xor xor_13 (xor_13_out, Bit16_A[12], Bit16_B[12]);
  and and_13 (and_13_out, Bit16_B[12], Bit16_A[12]);
  xor xor_14 (xor_14_out, Bit16_A[13], Bit16_B[13]);
  and and_14 (and_14_out, Bit16_B[13], Bit16_A[13]);
  xor xor_15 (xor_15_out, Bit16_A[14], Bit16_B[14]);
  and and_15 (and_15_out, Bit16_B[14], Bit16_A[14]);
  xor xor_16 (xor_16_out, Bit16_A[15], Bit16_B[15]);
  and and_16 (and_16_out, Bit16_B[15], Bit16_A[15]);
  xor xor_17 (Bit16_Result[0], Carry_In, xor_1_out);
  xor xor_18 (Bit16_Result[1], bit4_cla_logic_1_c2, xor_2_out);
  xor xor_19 (Bit16_Result[2], bit4_cla_logic_1_c3, xor_3_out);
  xor xor_20 (Bit16_Result[3], bit4_cla_logic_1_c4, xor_4_out);
  xor xor_21 (Bit16_Result[4], bit4_cla_logic_5_c2, xor_5_out);
  xor xor_22 (Bit16_Result[5], bit4_cla_logic_2_c2, xor_6_out);
  xor xor_23 (Bit16_Result[6], bit4_cla_logic_2_c3, xor_7_out);
  xor xor_24 (Bit16_Result[7], bit4_cla_logic_2_c4, xor_8_out);
  xor xor_25 (Bit16_Result[8], bit4_cla_logic_5_c3, xor_9_out);
  xor xor_26 (Bit16_Result[9], bit4_cla_logic_3_c2, xor_10_out);
  xor xor_27 (Bit16_Result[10], bit4_cla_logic_3_c3, xor_11_out);
  xor xor_28 (Bit16_Result[11], bit4_cla_logic_3_c4, xor_12_out);
  xor xor_29 (Bit16_Result[12], bit4_cla_logic_5_c4, xor_13_out);
  xor xor_30 (Bit16_Result[13], bit4_cla_logic_4_c2, xor_14_out);
  xor xor_31 (Bit16_Result[14], bit4_cla_logic_4_c3, xor_15_out);
  xor xor_32 (Bit16_Result[15], bit4_cla_logic_4_c4, xor_16_out);
  Bit4_CLA_Logic bit4_cla_logic_1 (
    .Cin(Carry_In), .P1(xor_1_out), .G1(and_1_out), .P2(xor_2_out), .G2(and_2_out), .P3(xor_3_out),
    .G3(and_3_out), .P4(xor_4_out), .G4(and_4_out), .C2(bit4_cla_logic_1_c2), .C3(bit4_cla_logic_1_c3),
    .C4(bit4_cla_logic_1_c4), .COUT(bit4_cla_logic_1_cout), .PG(bit4_cla_logic_1_pg));
  Bit4_CLA_Logic bit4_cla_logic_2 (
    .Cin(bit4_cla_logic_5_c2), .P1(xor_5_out), .G1(and_5_out), .P2(xor_6_out), .G2(and_6_out),
    .P3(xor_7_out), .G3(and_7_out), .P4(xor_8_out), .G4(and_8_out), .C2(bit4_cla_logic_2_c2),
    .C3(bit4_cla_logic_2_c3), .C4(bit4_cla_logic_2_c4), .COUT(bit4_cla_logic_2_cout), .PG(bit4_cla_logic_2_pg));
  Bit4_CLA_Logic bit4_cla_logic_3 (
    .Cin(bit4_cla_logic_5_c3), .P1(xor_9_out), .G1(and_9_out), .P2(xor_10_out), .G2(and_10_out),
    .P3(xor_11_out), .G3(and_11_out), .P4(xor_12_out), .G4(and_12_out), .C2(bit4_cla_logic_3_c2),
    .C3(bit4_cla_logic_3_c3), .C4(bit4_cla_logic_3_c4), .COUT(bit4_cla_logic_3_cout), .PG(bit4_cla_logic_3_pg));
  Bit4_CLA_Logic bit4_cla_logic_4 (
    .Cin(bit4_cla_logic_5_c4), .P1(xor_13_out), .G1(and_13_out), .P2(xor_14_out), .G2(and_14_out),
    .P3(xor_15_out), .G3(and_15_out), .P4(xor_16_out), .G4(and_16_out), .C2(bit4_cla_logic_4_c2),
    .C3(bit4_cla_logic_4_c3), .C4(bit4_cla_logic_4_c4), .COUT(bit4_cla_logic_4_cout), .PG(bit4_cla_logic_4_pg));
  Bit4_CLA_Logic bit4_cla_logic_5 (
    .Cin(Carry_In), .P1(bit4_cla_logic_1_pg), .G1(bit4_cla_logic_1_cout), .P2(bit4_cla_logic_2_pg),
    .G2(bit4_cla_logic_2_cout), .P3(bit4_cla_logic_3_pg), .G3(bit4_cla_logic_3_cout),
    .P4(bit4_cla_logic_4_pg), .G4(bit4_cla_logic_4_cout), .C2(bit4_cla_logic_5_c2), .C3(bit4_cla_logic_5_c3),
    .C4(bit4_cla_logic_5_c4), .COUT(bit4_cla_logic_5_cout));  // open: PG
  and and_17 (and_17_out, Bit16_Result[11], FP_Op);
  or or_1 (Carry_Out, bit4_cla_logic_5_cout, and_17_out);
endmodule

module Bit8_CLA_Logic (
  input  C_In,
  input  P0,
  input  G0,
  input  P1,
  input  G1,
  input  P2,
  input  G2,
  input  P3,
  input  G3,
  input  P4,
  input  G4,
  input  P5,
  input  G5,
  input  P6,
  input  G6,
  input  P7,
  input  G7,
  output C1,
  output C2,
  output C3,
  output C4,
  output C5,
  output C6,
  output C7,
  output C_OUT,
  output PG
);

  wire and_1_out, and_2_out, and_3_out, and_4_out, and_5_out, and_6_out, and_7_out, and_8_out, and_9_out,
       and_10_out, and_11_out, and_12_out, and_13_out, and_14_out, and_15_out, and_16_out, and_17_out,
       and_18_out, and_19_out, and_20_out, and_21_out, and_22_out, and_23_out, and_24_out, and_25_out,
       and_26_out, and_27_out, and_28_out, and_29_out, and_30_out, and_31_out, and_32_out, and_33_out,
       and_34_out, and_35_out, and_36_out;

  and and_1 (and_1_out, C_In, P0);
  and and_2 (and_2_out, P1, G0);
  and and_3 (and_3_out, P1, P0, C_In);
  and and_4 (and_4_out, G1, P2);
  and and_5 (and_5_out, G0, P1, P2);
  and and_6 (and_6_out, C_In, P0, P1, P2);
  and and_7 (and_7_out, G2, P3);
  and and_8 (and_8_out, G1, P2, P3);
  and and_9 (and_9_out, G0, P1, P2, P3);
  and and_10 (and_10_out, C_In, P0, P1, P2, P3);
  and and_11 (and_11_out, G3, P4);
  and and_12 (and_12_out, G2, P3, P4);
  and and_13 (and_13_out, G1, P2, P3, P4);
  and and_14 (and_14_out, G0, P1, P2, P3, P4);
  and and_15 (and_15_out, C_In, P0, P1, P2, P3, P4);
  and and_16 (and_16_out, G4, P5);
  and and_17 (and_17_out, G3, P4, P5);
  and and_18 (and_18_out, G2, P3, P4, P5);
  and and_19 (and_19_out, G1, P2, P3, P4, P5);
  and and_20 (and_20_out, G0, P1, P2, P3, P4, P5);
  and and_21 (and_21_out, C_In, P0, P1, P2, P3, P4, P5);
  and and_22 (and_22_out, G5, P6);
  and and_23 (and_23_out, G4, P5, P6);
  and and_24 (and_24_out, G3, P4, P5, P6);
  and and_25 (and_25_out, G2, P3, P4, P5, P6);
  and and_26 (and_26_out, G1, P2, P3, P4, P5, P6);
  and and_27 (and_27_out, G0, P1, P2, P3, P4, P5, P6);
  and and_28 (and_28_out, C_In, P0, P1, P2, P3, P4, P5, P6);
  and and_29 (and_29_out, G6, P7);
  and and_30 (and_30_out, G5, P6, P7);
  and and_31 (and_31_out, G4, P5, P6, P7);
  and and_32 (and_32_out, G3, P4, P5, P6, P7);
  and and_33 (and_33_out, G2, P3, P4, P5, P6, P7);
  and and_34 (and_34_out, G1, P2, P3, P4, P5, P6, P7);
  and and_35 (and_35_out, G0, P1, P2, P3, P4, P5, P6, P7);
  and and_36 (and_36_out, C_In, P0, P1, P2, P3, P4, P5, P6, P7);
  and and_37 (PG, P7, P6, P5, P4, P3, P2, P1, P0);
  or or_1 (C1, and_1_out, G0);
  or or_2 (C2, G1, and_2_out, and_3_out);
  or or_3 (C3, G2, and_4_out, and_5_out, and_6_out);
  or or_4 (C4, G3, and_7_out, and_8_out, and_9_out, and_10_out);
  or or_5 (C5, G4, and_11_out, and_12_out, and_13_out, and_14_out, and_15_out);
  or or_6 (C6, G5, and_16_out, and_17_out, and_18_out, and_19_out, and_20_out, and_21_out);
  or or_7 (C7, G6, and_22_out, and_23_out, and_24_out, and_25_out, and_26_out, and_27_out, and_28_out);
  or or_8 (C_OUT, G7, and_29_out, and_30_out, and_31_out, and_32_out, and_33_out, and_34_out, and_35_out, and_36_out);
endmodule

module Bit3_CLA_Logic (
  input  C_In,
  input  P0,
  input  G0,
  input  P1,
  input  G1,
  input  P2,
  input  G2,
  output C1,
  output C2,
  output C_OUT,
  output PG
);

  wire and_1_out, and_2_out, and_3_out, and_4_out, and_5_out, and_6_out;

  and and_1 (and_1_out, C_In, P0);
  and and_2 (and_2_out, P1, G0);
  and and_3 (and_3_out, P1, P0, C_In);
  and and_4 (and_4_out, G1, P2);
  and and_5 (and_5_out, G0, P1, P2);
  and and_6 (and_6_out, C_In, P0, P1, P2);
  and and_7 (PG, P0, P1, P2);
  or or_1 (C1, and_1_out, G0);
  or or_2 (C2, G1, and_2_out, and_3_out);
  or or_3 (C_OUT, G2, and_4_out, and_5_out, and_6_out);
endmodule

module Bit24_Adder (
  input  C_In,
  input  [23:0] Bit24_A,
  input  [23:0] Bit24_B,
  output Bit16_C_OUT,
  output [23:0] Bit24_Result,
  output C_OUT
);

  wire and_1_out, and_2_out, and_3_out, and_4_out, and_5_out, and_6_out, and_7_out, and_8_out, and_9_out,
       and_10_out, and_11_out, and_12_out, and_13_out, and_14_out, and_15_out, and_16_out, and_17_out,
       and_18_out, and_19_out, and_20_out, and_21_out, and_22_out, and_23_out, and_24_out,
       bit3_cla_logic_1_c1, bit8_cla_logic_1_c1, bit8_cla_logic_1_c2, bit8_cla_logic_1_c3,
       bit8_cla_logic_1_c4, bit8_cla_logic_1_c5, bit8_cla_logic_1_c6, bit8_cla_logic_1_c7,
       bit8_cla_logic_1_c_out, bit8_cla_logic_1_pg, bit8_cla_logic_2_c1, bit8_cla_logic_2_c2,
       bit8_cla_logic_2_c3, bit8_cla_logic_2_c4, bit8_cla_logic_2_c5, bit8_cla_logic_2_c6,
       bit8_cla_logic_2_c7, bit8_cla_logic_2_c_out, bit8_cla_logic_2_pg, bit8_cla_logic_3_c1,
       bit8_cla_logic_3_c2, bit8_cla_logic_3_c3, bit8_cla_logic_3_c4, bit8_cla_logic_3_c5,
       bit8_cla_logic_3_c6, bit8_cla_logic_3_c7, bit8_cla_logic_3_c_out, bit8_cla_logic_3_pg, xor_1_out,
       xor_2_out, xor_3_out, xor_4_out, xor_5_out, xor_6_out, xor_7_out, xor_8_out, xor_9_out, xor_10_out,
       xor_11_out, xor_12_out, xor_13_out, xor_14_out, xor_15_out, xor_16_out, xor_17_out, xor_18_out,
       xor_19_out, xor_20_out, xor_21_out, xor_22_out, xor_23_out, xor_24_out;

  xor xor_1 (xor_1_out, Bit24_A[0], Bit24_B[0]);
  and and_1 (and_1_out, Bit24_B[0], Bit24_A[0]);
  xor xor_2 (xor_2_out, Bit24_A[1], Bit24_B[1]);
  and and_2 (and_2_out, Bit24_B[1], Bit24_A[1]);
  xor xor_3 (xor_3_out, Bit24_A[2], Bit24_B[2]);
  and and_3 (and_3_out, Bit24_B[2], Bit24_A[2]);
  xor xor_4 (xor_4_out, Bit24_A[3], Bit24_B[3]);
  and and_4 (and_4_out, Bit24_B[3], Bit24_A[3]);
  xor xor_5 (xor_5_out, Bit24_A[4], Bit24_B[4]);
  and and_5 (and_5_out, Bit24_B[4], Bit24_A[4]);
  xor xor_6 (xor_6_out, Bit24_A[5], Bit24_B[5]);
  and and_6 (and_6_out, Bit24_B[5], Bit24_A[5]);
  xor xor_7 (xor_7_out, Bit24_A[6], Bit24_B[6]);
  and and_7 (and_7_out, Bit24_B[6], Bit24_A[6]);
  xor xor_8 (xor_8_out, Bit24_A[7], Bit24_B[7]);
  and and_8 (and_8_out, Bit24_B[7], Bit24_A[7]);
  xor xor_9 (xor_9_out, Bit24_A[8], Bit24_B[8]);
  and and_9 (and_9_out, Bit24_B[8], Bit24_A[8]);
  xor xor_10 (xor_10_out, Bit24_A[9], Bit24_B[9]);
  and and_10 (and_10_out, Bit24_B[9], Bit24_A[9]);
  xor xor_11 (xor_11_out, Bit24_A[10], Bit24_B[10]);
  and and_11 (and_11_out, Bit24_B[10], Bit24_A[10]);
  xor xor_12 (xor_12_out, Bit24_A[11], Bit24_B[11]);
  and and_12 (and_12_out, Bit24_B[11], Bit24_A[11]);
  xor xor_13 (xor_13_out, Bit24_A[12], Bit24_B[12]);
  and and_13 (and_13_out, Bit24_B[12], Bit24_A[12]);
  xor xor_14 (xor_14_out, Bit24_A[13], Bit24_B[13]);
  and and_14 (and_14_out, Bit24_B[13], Bit24_A[13]);
  xor xor_15 (xor_15_out, Bit24_A[14], Bit24_B[14]);
  and and_15 (and_15_out, Bit24_B[14], Bit24_A[14]);
  xor xor_16 (xor_16_out, Bit24_A[15], Bit24_B[15]);
  and and_16 (and_16_out, Bit24_B[15], Bit24_A[15]);
  xor xor_17 (xor_17_out, Bit24_A[16], Bit24_B[16]);
  and and_17 (and_17_out, Bit24_B[16], Bit24_A[16]);
  xor xor_18 (xor_18_out, Bit24_A[17], Bit24_B[17]);
  and and_18 (and_18_out, Bit24_B[17], Bit24_A[17]);
  xor xor_19 (xor_19_out, Bit24_A[18], Bit24_B[18]);
  and and_19 (and_19_out, Bit24_B[18], Bit24_A[18]);
  xor xor_20 (xor_20_out, Bit24_A[19], Bit24_B[19]);
  and and_20 (and_20_out, Bit24_B[19], Bit24_A[19]);
  xor xor_21 (xor_21_out, Bit24_A[20], Bit24_B[20]);
  and and_21 (and_21_out, Bit24_B[20], Bit24_A[20]);
  xor xor_22 (xor_22_out, Bit24_A[21], Bit24_B[21]);
  and and_22 (and_22_out, Bit24_B[21], Bit24_A[21]);
  xor xor_23 (xor_23_out, Bit24_A[22], Bit24_B[22]);
  and and_23 (and_23_out, Bit24_B[22], Bit24_A[22]);
  xor xor_24 (xor_24_out, Bit24_A[23], Bit24_B[23]);
  and and_24 (and_24_out, Bit24_B[23], Bit24_A[23]);
  xor xor_25 (Bit24_Result[0], C_In, xor_1_out);
  xor xor_26 (Bit24_Result[1], bit8_cla_logic_1_c1, xor_2_out);
  xor xor_27 (Bit24_Result[2], bit8_cla_logic_1_c2, xor_3_out);
  xor xor_28 (Bit24_Result[3], bit8_cla_logic_1_c3, xor_4_out);
  xor xor_29 (Bit24_Result[4], bit8_cla_logic_1_c4, xor_5_out);
  xor xor_30 (Bit24_Result[5], bit8_cla_logic_1_c5, xor_6_out);
  xor xor_31 (Bit24_Result[6], bit8_cla_logic_1_c6, xor_7_out);
  xor xor_32 (Bit24_Result[7], bit8_cla_logic_1_c7, xor_8_out);
  xor xor_33 (Bit24_Result[8], bit3_cla_logic_1_c1, xor_9_out);
  xor xor_34 (Bit24_Result[9], bit8_cla_logic_2_c1, xor_10_out);
  xor xor_35 (Bit24_Result[10], bit8_cla_logic_2_c2, xor_11_out);
  xor xor_36 (Bit24_Result[11], bit8_cla_logic_2_c3, xor_12_out);
  xor xor_37 (Bit24_Result[12], bit8_cla_logic_2_c4, xor_13_out);
  xor xor_38 (Bit24_Result[13], bit8_cla_logic_2_c5, xor_14_out);
  xor xor_39 (Bit24_Result[14], bit8_cla_logic_2_c6, xor_15_out);
  xor xor_40 (Bit24_Result[15], bit8_cla_logic_2_c7, xor_16_out);
  xor xor_41 (Bit24_Result[16], Bit16_C_OUT, xor_17_out);
  xor xor_42 (Bit24_Result[17], bit8_cla_logic_3_c1, xor_18_out);
  xor xor_43 (Bit24_Result[18], bit8_cla_logic_3_c2, xor_19_out);
  xor xor_44 (Bit24_Result[19], bit8_cla_logic_3_c3, xor_20_out);
  xor xor_45 (Bit24_Result[20], bit8_cla_logic_3_c4, xor_21_out);
  xor xor_46 (Bit24_Result[21], bit8_cla_logic_3_c5, xor_22_out);
  xor xor_47 (Bit24_Result[22], bit8_cla_logic_3_c6, xor_23_out);
  xor xor_48 (Bit24_Result[23], bit8_cla_logic_3_c7, xor_24_out);
  Bit8_CLA_Logic bit8_cla_logic_1 (
    .C_In(C_In), .P0(xor_1_out), .G0(and_1_out), .P1(xor_2_out), .G1(and_2_out), .P2(xor_3_out),
    .G2(and_3_out), .P3(xor_4_out), .G3(and_4_out), .P4(xor_5_out), .G4(and_5_out), .P5(xor_6_out),
    .G5(and_6_out), .P6(xor_7_out), .G6(and_7_out), .P7(xor_8_out), .G7(and_8_out), .C1(bit8_cla_logic_1_c1),
    .C2(bit8_cla_logic_1_c2), .C3(bit8_cla_logic_1_c3), .C4(bit8_cla_logic_1_c4), .C5(bit8_cla_logic_1_c5),
    .C6(bit8_cla_logic_1_c6), .C7(bit8_cla_logic_1_c7), .C_OUT(bit8_cla_logic_1_c_out),
    .PG(bit8_cla_logic_1_pg));
  Bit8_CLA_Logic bit8_cla_logic_2 (
    .C_In(bit3_cla_logic_1_c1), .P0(xor_9_out), .G0(and_9_out), .P1(xor_10_out), .G1(and_10_out),
    .P2(xor_11_out), .G2(and_11_out), .P3(xor_12_out), .G3(and_12_out), .P4(xor_13_out), .G4(and_13_out),
    .P5(xor_14_out), .G5(and_14_out), .P6(xor_15_out), .G6(and_15_out), .P7(xor_16_out), .G7(and_16_out),
    .C1(bit8_cla_logic_2_c1), .C2(bit8_cla_logic_2_c2), .C3(bit8_cla_logic_2_c3), .C4(bit8_cla_logic_2_c4),
    .C5(bit8_cla_logic_2_c5), .C6(bit8_cla_logic_2_c6), .C7(bit8_cla_logic_2_c7),
    .C_OUT(bit8_cla_logic_2_c_out), .PG(bit8_cla_logic_2_pg));
  Bit8_CLA_Logic bit8_cla_logic_3 (
    .C_In(Bit16_C_OUT), .P0(xor_17_out), .G0(and_17_out), .P1(xor_18_out), .G1(and_18_out), .P2(xor_19_out),
    .G2(and_19_out), .P3(xor_20_out), .G3(and_20_out), .P4(xor_21_out), .G4(and_21_out), .P5(xor_22_out),
    .G5(and_22_out), .P6(xor_23_out), .G6(and_23_out), .P7(xor_24_out), .G7(and_24_out),
    .C1(bit8_cla_logic_3_c1), .C2(bit8_cla_logic_3_c2), .C3(bit8_cla_logic_3_c3), .C4(bit8_cla_logic_3_c4),
    .C5(bit8_cla_logic_3_c5), .C6(bit8_cla_logic_3_c6), .C7(bit8_cla_logic_3_c7),
    .C_OUT(bit8_cla_logic_3_c_out), .PG(bit8_cla_logic_3_pg));
  Bit3_CLA_Logic bit3_cla_logic_1 (
    .C_In(C_In), .P0(bit8_cla_logic_1_pg), .G0(bit8_cla_logic_1_c_out), .P1(bit8_cla_logic_2_pg),
    .G1(bit8_cla_logic_2_c_out), .P2(bit8_cla_logic_3_pg), .G2(bit8_cla_logic_3_c_out),
    .C1(bit3_cla_logic_1_c1), .C2(Bit16_C_OUT), .C_OUT(C_OUT));  // open: PG
endmodule

module Bit24_To_Bit16 (
  input  [23:0] Bit24,
  output [15:0] Bit16
);


  assign Bit16 = Bit24[23:8];
endmodule

module Bit16_To_Bit24 (
  input  [15:0] Bit16,
  output [23:0] Bit24
);


  assign Bit24 = {{8{1'b0}}, Bit16};
endmodule

module Bit24_Controlled_Buffer (
  input  Enable,
  input  [23:0] Bit24_In,
  output [23:0] Bit24_Out
);

  and and_1 (Bit24_Out[0], Bit24_In[0], Enable);
  and and_2 (Bit24_Out[1], Bit24_In[1], Enable);
  and and_3 (Bit24_Out[2], Bit24_In[2], Enable);
  and and_4 (Bit24_Out[3], Bit24_In[3], Enable);
  and and_5 (Bit24_Out[4], Bit24_In[4], Enable);
  and and_6 (Bit24_Out[5], Bit24_In[5], Enable);
  and and_7 (Bit24_Out[6], Bit24_In[6], Enable);
  and and_8 (Bit24_Out[7], Bit24_In[7], Enable);
  and and_9 (Bit24_Out[8], Bit24_In[8], Enable);
  and and_10 (Bit24_Out[9], Bit24_In[9], Enable);
  and and_11 (Bit24_Out[10], Bit24_In[10], Enable);
  and and_12 (Bit24_Out[11], Bit24_In[11], Enable);
  and and_13 (Bit24_Out[12], Bit24_In[12], Enable);
  and and_14 (Bit24_Out[13], Bit24_In[13], Enable);
  and and_15 (Bit24_Out[14], Bit24_In[14], Enable);
  and and_16 (Bit24_Out[15], Bit24_In[15], Enable);
  and and_17 (Bit24_Out[16], Bit24_In[16], Enable);
  and and_18 (Bit24_Out[17], Bit24_In[17], Enable);
  and and_19 (Bit24_Out[18], Bit24_In[18], Enable);
  and and_20 (Bit24_Out[19], Bit24_In[19], Enable);
  and and_21 (Bit24_Out[20], Bit24_In[20], Enable);
  and and_22 (Bit24_Out[21], Bit24_In[21], Enable);
  and and_23 (Bit24_Out[22], Bit24_In[22], Enable);
  and and_24 (Bit24_Out[23], Bit24_In[23], Enable);
endmodule

module alu2 (
  input  [3:0] Bit5_Opcode,
  input  Signed_Integer_Operation,
  input  [15:0] Bit16_Input_A,
  input  [15:0] Bit16_Input_B,
  input  [15:0] in_5,
  input  [15:0] in_6,
  input  in_7,
  input  [15:0] in_8,
  input  [15:0] in_9,
  input  [15:0] in_10,
  output [15:0] out_11,
  output [15:0] out_12,
  output [15:0] out_13,
  output [15:0] out_14,
  output [15:0] out_15,
  output [15:0] out_16,
  output [15:0] out_17
);

  wire bit16_float_exponent_unit_1_p10, bit16_float_exponent_unit_1_p11, bit16_float_exponent_unit_1_p12,
       bit24_adder_1_c_out, not_1_out, not_2_out, undriven;
  wire [1:0] bit24_adder_1_bit24_result_2;
  wire [3:0] bit16_float_exponent_unit_1_p6;
  wire [4:0] bit16_float_exponent_unit_1_p9;
  wire [13:0] bit16t24_right_shift_2_bit24_result;
  wire [15:0] bit16_float_exponent_unit_1_p5;
  wire [21:0] bit24_adder_1_bit24_result;
  wire [23:0] bit16_float_exponent_unit_1_p7, bit16_float_exponent_unit_1_p8,
       bit16t24_right_shift_1_bit24_result, bit24_controlled_buffer_1_bit24_out,
       bit24_controlled_buffer_2_bit24_out, bit24_controlled_buffer_3_bit24_out,
       bit24_controlled_buffer_4_bit24_out, bit24_twos_complementer_1_bit24_out,
       bit24_twos_complementer_2_bit24_out, or_1_out, or_2_out;
  wire [23:1] undriven_2;

  Demultiplexer #(.select(4)) demultiplexer_1 (
    .in(1'b1), .sel(Bit5_Opcode));  // open: out0, out1, out2, out3, out4, out5, out6, out7, out8, out9, out10, out11, out12, out13, out14, out15
  FPAdder #(.fpwidth(16)) fpadder_1 (.a(in_5), .b(in_6), .out(out_11));
  FPAdder #(.fpwidth(16)) fpadder_2 (.a(in_8), .b(in_9), .out(out_16));
  // fpu3 fpu3_1: pin names not known
  // Bit24_Divider bit24_divider_1: pin names not known
  Bit16_Multiplier bit16_multiplier_1 ();  // open: Bit16_B, Bit16_A, Lower_Word, Upper_Word
  Bit16T24_Right_Shift bit16t24_right_shift_1 (
    .Bit16_Data(bit16_float_exponent_unit_1_p5), .Bit4_Shift(bit16_float_exponent_unit_1_p6),
    .Bit24_Result(bit16t24_right_shift_1_bit24_result));  // open: Bit16_Result, Shift_Overflow_For_Bit16
  Bit16_Left_Shift bit16_left_shift_1 ();  // open: Bit16_Data, Bit4_Shift, Bit16_Result, Shift_Overflow
  // Bit16_Float_Exponent_Unit bit16_float_exponent_unit_1: pin names not known; wires that end beside it: bit16t24_right_shift_1_bit24_result, in_7, in_8, in_9, bit16_float_exponent_unit_1_p5, bit16_float_exponent_unit_1_p6, bit16_float_exponent_unit_1_p7, bit16_float_exponent_unit_1_p8, bit16_float_exponent_unit_1_p9, bit16_float_exponent_unit_1_p10, bit16_float_exponent_unit_1_p11, bit16_float_exponent_unit_1_p12
  not not_1 (not_1_out, bit16_float_exponent_unit_1_p11);
  Bit24_Twos_Complementer bit24_twos_complementer_1 (
    .Bit24_In(bit16_float_exponent_unit_1_p7), .Bit24_Out(bit24_twos_complementer_1_bit24_out));
  not not_2 (not_2_out, bit16_float_exponent_unit_1_p12);
  Bit24_Twos_Complementer bit24_twos_complementer_2 (
    .Bit24_In(bit16_float_exponent_unit_1_p8), .Bit24_Out(bit24_twos_complementer_2_bit24_out));
  Bit24_Controlled_Buffer bit24_controlled_buffer_1 (
    .Enable(not_1_out), .Bit24_In(bit16_float_exponent_unit_1_p7),
    .Bit24_Out(bit24_controlled_buffer_1_bit24_out));
  Bit24_Controlled_Buffer bit24_controlled_buffer_2 (
    .Enable(bit16_float_exponent_unit_1_p11), .Bit24_In(bit24_twos_complementer_1_bit24_out),
    .Bit24_Out(bit24_controlled_buffer_2_bit24_out));
  Bit24_Controlled_Buffer bit24_controlled_buffer_3 (
    .Enable(not_2_out), .Bit24_In(bit16_float_exponent_unit_1_p8),
    .Bit24_Out(bit24_controlled_buffer_3_bit24_out));
  Bit24_Controlled_Buffer bit24_controlled_buffer_4 (
    .Enable(bit16_float_exponent_unit_1_p12), .Bit24_In(bit24_twos_complementer_2_bit24_out),
    .Bit24_Out(bit24_controlled_buffer_4_bit24_out));
  assign or_1_out = bit24_controlled_buffer_1_bit24_out | bit24_controlled_buffer_2_bit24_out;  // OR_Gate or_1, 24 bits wide
  assign or_2_out = bit24_controlled_buffer_3_bit24_out | bit24_controlled_buffer_4_bit24_out;  // OR_Gate or_2, 24 bits wide
  Bit24_Adder bit24_adder_1 (
    .Bit24_A(or_1_out), .Bit24_B(or_2_out),
    .Bit24_Result({bit24_adder_1_bit24_result_2[0], bit24_adder_1_bit24_result_2[1], bit24_adder_1_bit24_result}),
    .C_OUT(bit24_adder_1_c_out));  // open: C_In, Bit16_C_OUT
  Priority_Encoder #(.select(5)) priority_encoder_1 (
    .in0(undriven_2[1]), .in1(undriven_2[2]), .in2(undriven_2[3]), .in3(undriven_2[4]), .in4(undriven_2[5]),
    .in5(undriven_2[6]), .in6(undriven_2[7]), .in7(undriven_2[8]), .in8(undriven_2[9]), .in9(undriven_2[10]),
    .in10(undriven_2[11]), .in11(undriven_2[12]), .in12(undriven_2[13]), .in13(undriven_2[14]),
    .in14(undriven_2[15]), .in15(undriven_2[16]), .in16(undriven_2[17]), .in17(undriven_2[18]),
    .in18(undriven_2[19]), .in19(undriven_2[20]), .in20(undriven_2[21]), .in21(undriven_2[22]),
    .in22(undriven_2[23]));  // open: in23, in24, in25, in26, in27, in28, in29, in30, in31, out, gs, en_out, en_in
  Bit5_Adder bit5_adder_1 (
    .Cin(undriven), .Bit5_A(bit16_float_exponent_unit_1_p9), .Bit5_B({3'b000, bit24_adder_1_bit24_result_2}),
    .Bit5_Result(out_12[14:10]));  // open: Cout
  Bit16T24_Right_Shift bit16t24_right_shift_2 (
    .Bit16_Data(bit24_adder_1_bit24_result[21:6]), .Bit4_Shift({3'b000, bit24_adder_1_bit24_result_2[0]}),
    .Bit24_Result({out_12[9:0], bit16t24_right_shift_2_bit24_result}));  // open: Bit16_Result, Shift_Overflow_For_Bit16

  assign out_12[15] = 1'b0;
  assign out_13 = {1'b0, out_12[14:0]};
  assign out_14 = in_9;
  assign out_15 = in_10;
  assign out_17 = out_16;
endmodule

module Bit24_Twos_Complementer (
  input  [23:0] Bit24_In,
  output [23:0] Bit24_Out
);

  wire or_1_out, or_2_out, or_3_out, or_4_out, or_5_out, or_6_out, or_7_out, or_8_out, or_9_out, or_10_out,
       or_11_out, or_12_out, or_13_out, or_14_out, or_15_out, or_16_out, or_17_out, or_18_out, or_19_out,
       or_20_out, or_21_out, or_22_out;

  or or_1 (or_1_out, Bit24_In[0], Bit24_Out[1]);
  or or_2 (or_2_out, Bit24_In[0], Bit24_Out[1], Bit24_Out[2]);
  or or_3 (or_3_out, Bit24_In[0], Bit24_Out[1], Bit24_Out[2], Bit24_Out[3]);
  or or_4 (or_4_out, Bit24_In[0], Bit24_Out[1], Bit24_Out[2], Bit24_Out[3], Bit24_Out[4]);
  or or_5 (or_5_out, Bit24_In[0], Bit24_Out[1], Bit24_Out[2], Bit24_Out[3], Bit24_Out[4], Bit24_Out[5]);
  or or_6 (or_6_out, Bit24_In[0], Bit24_Out[1], Bit24_Out[2], Bit24_Out[3], Bit24_Out[4], Bit24_Out[5], Bit24_Out[6]);
  or or_7 (or_7_out, Bit24_In[0], Bit24_Out[1], Bit24_Out[2], Bit24_Out[3], Bit24_Out[4], Bit24_Out[5], Bit24_Out[6], Bit24_Out[7]);
  or or_8 (or_8_out, Bit24_In[0], Bit24_Out[1], Bit24_Out[2], Bit24_Out[3], Bit24_Out[4], Bit24_Out[5], Bit24_Out[6], Bit24_Out[7], Bit24_Out[8]);
  or or_9 (or_9_out, Bit24_In[0], Bit24_Out[1], Bit24_Out[2], Bit24_Out[3], Bit24_Out[4], Bit24_Out[5], Bit24_Out[6], Bit24_Out[7], Bit24_Out[8], Bit24_Out[9]);
  or or_10 (or_10_out, Bit24_In[0], Bit24_Out[1], Bit24_Out[2], Bit24_Out[3], Bit24_Out[4], Bit24_Out[5], Bit24_Out[6], Bit24_Out[7], Bit24_Out[8], Bit24_Out[9], Bit24_Out[10]);
  or or_11 (or_11_out, Bit24_In[0], Bit24_Out[1], Bit24_Out[2], Bit24_Out[3], Bit24_Out[4], Bit24_Out[5], Bit24_Out[6], Bit24_Out[7], Bit24_Out[8], Bit24_Out[9], Bit24_Out[10], Bit24_Out[11]);
  or or_12 (or_12_out, Bit24_In[0], Bit24_Out[1], Bit24_Out[2], Bit24_Out[3], Bit24_Out[4], Bit24_Out[5], Bit24_Out[6], Bit24_Out[7], Bit24_Out[8], Bit24_Out[9], Bit24_Out[10], Bit24_Out[11], Bit24_Out[12]);
  or or_13 (or_13_out, Bit24_In[0], Bit24_Out[1], Bit24_Out[2], Bit24_Out[3], Bit24_Out[4], Bit24_Out[5], Bit24_Out[6], Bit24_Out[7], Bit24_Out[8], Bit24_Out[9], Bit24_Out[10], Bit24_Out[11], Bit24_Out[12], Bit24_Out[13]);
  or or_14 (or_14_out, Bit24_In[0], Bit24_Out[1], Bit24_Out[2], Bit24_Out[3], Bit24_Out[4], Bit24_Out[5], Bit24_Out[6], Bit24_Out[7], Bit24_Out[8], Bit24_Out[9], Bit24_Out[10], Bit24_Out[11], Bit24_Out[12], Bit24_Out[13], Bit24_Out[14]);
  or or_15 (or_15_out, Bit24_In[0], Bit24_Out[1], Bit24_Out[2], Bit24_Out[3], Bit24_Out[4], Bit24_Out[5], Bit24_Out[6], Bit24_Out[7], Bit24_Out[8], Bit24_Out[9], Bit24_Out[10], Bit24_Out[11], Bit24_Out[12], Bit24_Out[13], Bit24_Out[14], Bit24_Out[15]);
  or or_16 (or_16_out, Bit24_In[0], Bit24_Out[1], Bit24_Out[2], Bit24_Out[3], Bit24_Out[4], Bit24_Out[5], Bit24_Out[6], Bit24_Out[7], Bit24_Out[8], Bit24_Out[9], Bit24_Out[10], Bit24_Out[11], Bit24_Out[12], Bit24_Out[13], Bit24_Out[14], Bit24_Out[15], Bit24_Out[16]);
  or or_17 (or_17_out, Bit24_In[0], Bit24_Out[1], Bit24_Out[2], Bit24_Out[3], Bit24_Out[4], Bit24_Out[5], Bit24_Out[6], Bit24_Out[7], Bit24_Out[8], Bit24_Out[9], Bit24_Out[10], Bit24_Out[11], Bit24_Out[12], Bit24_Out[13], Bit24_Out[14], Bit24_Out[15], Bit24_Out[16], Bit24_Out[17]);
  or or_18 (or_18_out, Bit24_In[0], Bit24_Out[1], Bit24_Out[2], Bit24_Out[3], Bit24_Out[4], Bit24_Out[5], Bit24_Out[6], Bit24_Out[7], Bit24_Out[8], Bit24_Out[9], Bit24_Out[10], Bit24_Out[11], Bit24_Out[12], Bit24_Out[13], Bit24_Out[14], Bit24_Out[15], Bit24_Out[16], Bit24_Out[17], Bit24_Out[18]);
  or or_19 (or_19_out, Bit24_In[0], Bit24_Out[1], Bit24_Out[2], Bit24_Out[3], Bit24_Out[4], Bit24_Out[5], Bit24_Out[6], Bit24_Out[7], Bit24_Out[8], Bit24_Out[9], Bit24_Out[10], Bit24_Out[11], Bit24_Out[12], Bit24_Out[13], Bit24_Out[14], Bit24_Out[15], Bit24_Out[16], Bit24_Out[17], Bit24_Out[18], Bit24_Out[19]);
  or or_20 (or_20_out, Bit24_In[0], Bit24_Out[1], Bit24_Out[2], Bit24_Out[3], Bit24_Out[4], Bit24_Out[5], Bit24_Out[6], Bit24_Out[7], Bit24_Out[8], Bit24_Out[9], Bit24_Out[10], Bit24_Out[11], Bit24_Out[12], Bit24_Out[13], Bit24_Out[14], Bit24_Out[15], Bit24_Out[16], Bit24_Out[17], Bit24_Out[18], Bit24_Out[19], Bit24_Out[20]);
  or or_21 (or_21_out, Bit24_In[0], Bit24_Out[1], Bit24_Out[2], Bit24_Out[3], Bit24_Out[4], Bit24_Out[5], Bit24_Out[6], Bit24_Out[7], Bit24_Out[8], Bit24_Out[9], Bit24_Out[10], Bit24_Out[11], Bit24_Out[12], Bit24_Out[13], Bit24_Out[14], Bit24_Out[15], Bit24_Out[16], Bit24_Out[17], Bit24_Out[18], Bit24_Out[19], Bit24_Out[20], Bit24_Out[21]);
  or or_22 (or_22_out, Bit24_In[0], Bit24_Out[1], Bit24_Out[2], Bit24_Out[3], Bit24_Out[4], Bit24_Out[5], Bit24_Out[6], Bit24_Out[7], Bit24_Out[8], Bit24_Out[9], Bit24_Out[10], Bit24_Out[11], Bit24_Out[12], Bit24_Out[13], Bit24_Out[14], Bit24_Out[15], Bit24_Out[16], Bit24_Out[17], Bit24_Out[18], Bit24_Out[19], Bit24_Out[20], Bit24_Out[21], Bit24_Out[22]);
  xor xor_1 (Bit24_Out[1], Bit24_In[1], Bit24_In[0]);
  xor xor_2 (Bit24_Out[2], Bit24_In[2], or_1_out);
  xor xor_3 (Bit24_Out[3], Bit24_In[3], or_2_out);
  xor xor_4 (Bit24_Out[4], Bit24_In[4], or_3_out);
  xor xor_5 (Bit24_Out[5], Bit24_In[5], or_4_out);
  xor xor_6 (Bit24_Out[6], Bit24_In[6], or_5_out);
  xor xor_7 (Bit24_Out[7], Bit24_In[7], or_6_out);
  xor xor_8 (Bit24_Out[8], Bit24_In[8], or_7_out);
  xor xor_9 (Bit24_Out[9], Bit24_In[9], or_8_out);
  xor xor_10 (Bit24_Out[10], Bit24_In[10], or_9_out);
  xor xor_11 (Bit24_Out[11], Bit24_In[11], or_10_out);
  xor xor_12 (Bit24_Out[12], Bit24_In[12], or_11_out);
  xor xor_13 (Bit24_Out[13], Bit24_In[13], or_12_out);
  xor xor_14 (Bit24_Out[14], Bit24_In[14], or_13_out);
  xor xor_15 (Bit24_Out[15], Bit24_In[15], or_14_out);
  xor xor_16 (Bit24_Out[16], Bit24_In[16], or_15_out);
  xor xor_17 (Bit24_Out[17], Bit24_In[17], or_16_out);
  xor xor_18 (Bit24_Out[18], Bit24_In[18], or_17_out);
  xor xor_19 (Bit24_Out[19], Bit24_In[19], or_18_out);
  xor xor_20 (Bit24_Out[20], Bit24_In[20], or_19_out);
  xor xor_21 (Bit24_Out[21], Bit24_In[21], or_20_out);
  xor xor_22 (Bit24_Out[22], Bit24_In[22], or_21_out);
  xor xor_23 (Bit24_Out[23], Bit24_In[23], or_22_out);

  assign Bit24_Out[0] = Bit24_In[0];
endmodule
module Bit24_Divider (
  input  Clock,
  input  [23:0] Bit24_Dividend,
  input  [23:0] Bit24_Divisor,
  input  Int_Div,
  input  FLOAT_Div,
  input  Bit16_C_Out_Adder,
  input  [23:0] Bit24_Result,
  input  C_Out_Adder,
  output Divider_Running,
  output [23:0] Bit24_Remainder,
  output [23:0] Bit24_Quotient,
  output [23:0] Bit24_Adder_A,
  output [23:0] Bit24_Adder_B
);

  wire and_1_out, and_2_out, and_3_out, and_4_out, and_5_out, and_6_out, and_8_out, and_9_out, and_10_out,
       and_11_out, and_12_out, and_13_out, and_14_out, and_15_out, and_16_out, and_17_out, and_18_out,
       and_19_out, and_20_out, and_21_out, and_22_out, and_23_out, and_24_out, and_25_out, and_26_out,
       and_27_out, and_28_out, and_29_out, and_30_out, and_31_out, d_ff_1_q, d_ff_2_qn, d_ff_3_qn, d_ff_4_qn,
       d_ff_5_qn, d_ff_6_qn, d_ff_7_q, demultiplexer_1_out1, demultiplexer_1_out2, demultiplexer_1_out3,
       demultiplexer_1_out4, demultiplexer_1_out5, demultiplexer_1_out6, demultiplexer_1_out7,
       demultiplexer_1_out8, demultiplexer_1_out9, demultiplexer_1_out10, demultiplexer_1_out11,
       demultiplexer_1_out12, demultiplexer_1_out13, demultiplexer_1_out14, demultiplexer_1_out15,
       demultiplexer_1_out16, demultiplexer_1_out17, demultiplexer_1_out18, demultiplexer_1_out19,
       demultiplexer_1_out20, demultiplexer_1_out21, demultiplexer_1_out22, demultiplexer_1_out23,
       demultiplexer_1_out24, demultiplexer_2_out0, demultiplexer_2_out1, demultiplexer_2_out2,
       demultiplexer_2_out3, demultiplexer_2_out4, demultiplexer_2_out5, demultiplexer_2_out6,
       demultiplexer_2_out7, demultiplexer_2_out8, demultiplexer_2_out9, demultiplexer_2_out10,
       demultiplexer_2_out11, demultiplexer_2_out12, demultiplexer_2_out13, demultiplexer_2_out14,
       demultiplexer_2_out15, demultiplexer_2_out16, demultiplexer_2_out17, demultiplexer_2_out18,
       demultiplexer_2_out19, demultiplexer_2_out20, demultiplexer_2_out21, demultiplexer_2_out22,
       demultiplexer_2_out23, nor_1_out, not_1_out, or_1_out, or_2_out;
  wire [0:0] or_4_out;
  wire [4:0] d_ff_2_q;
  wire [23:0] bit24_controlled_buffer_1_bit24_out, bit24_controlled_buffer_2_bit24_out, or_3_out;

  D_Flip_Flop d_ff_1 (.D(nor_1_out), .clk(Clock), .Q(d_ff_1_q));  // open: Qn, preset, reset
  and and_1 (and_1_out, Int_Div, d_ff_1_q);
  nor nor_1 (nor_1_out, d_ff_2_q[0], d_ff_2_q[1], d_ff_2_q[2], d_ff_2_q[3], d_ff_2_q[4]);
  D_Flip_Flop #(.trigger("falling")) d_ff_2 (
    .D(d_ff_2_qn), .clk(and_2_out), .Q(d_ff_2_q[0]), .Qn(d_ff_2_qn), .reset(and_6_out));  // open: preset
  and and_2 (and_2_out, Clock, or_1_out);
  D_Flip_Flop #(.trigger("falling")) d_ff_3 (
    .D(d_ff_3_qn), .clk(d_ff_2_q[0]), .Q(d_ff_2_q[1]), .Qn(d_ff_3_qn), .reset(and_6_out));  // open: preset
  Bit24_Inverter bit24_inverter_1 (.Bit24_In(Bit24_Divisor), .Bit24_Out(Bit24_Adder_B));
  or or_1 (or_1_out, Int_Div, FLOAT_Div);
  D_Flip_Flop #(.trigger("falling")) d_ff_4 (
    .D(d_ff_4_qn), .clk(d_ff_2_q[1]), .Q(d_ff_2_q[2]), .Qn(d_ff_4_qn), .reset(and_6_out));  // open: preset
  D_Flip_Flop #(.trigger("falling")) d_ff_5 (
    .D(d_ff_5_qn), .clk(d_ff_2_q[2]), .Q(d_ff_2_q[3]), .Qn(d_ff_5_qn), .preset(and_1_out), .reset(and_6_out));
  D_Flip_Flop #(.trigger("falling")) d_ff_6 (
    .D(d_ff_6_qn), .clk(d_ff_2_q[3]), .Q(d_ff_2_q[4]), .Qn(d_ff_6_qn), .reset(and_6_out));  // open: preset
  Register #(.trigger("falling"), .width(24)) register_1 (
    .D({or_3_out[22:0], or_4_out[0]}), .en(or_1_out), .clk(and_2_out), .Q(Bit24_Adder_A), .clr(and_6_out));
  and and_3 (and_3_out, Int_Div, Bit16_C_Out_Adder);
  not not_1 (not_1_out, or_2_out);
  or or_2 (or_2_out, and_3_out, and_4_out);
  and and_4 (and_4_out, FLOAT_Div, C_Out_Adder);
  D_Flip_Flop #(.trigger("falling")) d_ff_7 (.D(and_5_out), .clk(and_2_out), .Q(d_ff_7_q));  // open: Qn, preset, reset
  and and_5 (and_5_out, d_ff_2_q[0], ~d_ff_2_q[1], ~d_ff_2_q[2], d_ff_2_q[3], d_ff_2_q[4], or_1_out);  // AND_Gate
  and and_6 (and_6_out, d_ff_7_q, and_2_out);
  Demultiplexer #(.select(5)) demultiplexer_1 (
    .out1(demultiplexer_1_out1), .out2(demultiplexer_1_out2), .out3(demultiplexer_1_out3),
    .out4(demultiplexer_1_out4), .out5(demultiplexer_1_out5), .out6(demultiplexer_1_out6),
    .out7(demultiplexer_1_out7), .out8(demultiplexer_1_out8), .out9(demultiplexer_1_out9),
    .out10(demultiplexer_1_out10), .out11(demultiplexer_1_out11), .out12(demultiplexer_1_out12),
    .out13(demultiplexer_1_out13), .out14(demultiplexer_1_out14), .out15(demultiplexer_1_out15),
    .out16(demultiplexer_1_out16), .out17(demultiplexer_1_out17), .out18(demultiplexer_1_out18),
    .out19(demultiplexer_1_out19), .out20(demultiplexer_1_out20), .out21(demultiplexer_1_out21),
    .out22(demultiplexer_1_out22), .out23(demultiplexer_1_out23), .out24(demultiplexer_1_out24),
    .in(or_2_out), .sel(d_ff_2_q));  // open: out0, out25, out26, out27, out28, out29, out30, out31
  Bit24_Controlled_Buffer bit24_controlled_buffer_1 (
    .Enable(not_1_out), .Bit24_In(Bit24_Adder_A), .Bit24_Out(bit24_controlled_buffer_1_bit24_out));
  Bit24_Controlled_Buffer bit24_controlled_buffer_2 (
    .Enable(or_2_out), .Bit24_In(Bit24_Result), .Bit24_Out(bit24_controlled_buffer_2_bit24_out));
  S_R_Flip_Flop s_r_ff_1 (
    .S(demultiplexer_1_out24), .R(and_6_out), .clk(and_2_out), .Q(Bit24_Quotient[0]), .reset(and_6_out));  // open: Qn, preset
  and and_7 (Divider_Running, ~and_5_out, or_1_out);  // AND_Gate
  assign or_3_out = bit24_controlled_buffer_1_bit24_out | bit24_controlled_buffer_2_bit24_out;  // OR_Gate or_3, 24 bits wide
  S_R_Flip_Flop s_r_ff_2 (
    .S(demultiplexer_1_out23), .R(and_6_out), .clk(and_2_out), .Q(Bit24_Quotient[1]), .reset(and_6_out));  // open: Qn, preset
  S_R_Flip_Flop s_r_ff_3 (
    .S(demultiplexer_1_out22), .R(and_6_out), .clk(and_2_out), .Q(Bit24_Quotient[2]), .reset(and_6_out));  // open: Qn, preset
  S_R_Flip_Flop s_r_ff_4 (
    .S(demultiplexer_1_out21), .R(and_6_out), .clk(and_2_out), .Q(Bit24_Quotient[3]), .reset(and_6_out));  // open: Qn, preset
  Demultiplexer #(.select(5)) demultiplexer_2 (
    .out0(demultiplexer_2_out0), .out1(demultiplexer_2_out1), .out2(demultiplexer_2_out2),
    .out3(demultiplexer_2_out3), .out4(demultiplexer_2_out4), .out5(demultiplexer_2_out5),
    .out6(demultiplexer_2_out6), .out7(demultiplexer_2_out7), .out8(demultiplexer_2_out8),
    .out9(demultiplexer_2_out9), .out10(demultiplexer_2_out10), .out11(demultiplexer_2_out11),
    .out12(demultiplexer_2_out12), .out13(demultiplexer_2_out13), .out14(demultiplexer_2_out14),
    .out15(demultiplexer_2_out15), .out16(demultiplexer_2_out16), .out17(demultiplexer_2_out17),
    .out18(demultiplexer_2_out18), .out19(demultiplexer_2_out19), .out20(demultiplexer_2_out20),
    .out21(demultiplexer_2_out21), .out22(demultiplexer_2_out22), .out23(demultiplexer_2_out23),
    .in(or_1_out), .sel(d_ff_2_q));  // open: out24, out25, out26, out27, out28, out29, out30, out31
  or or_4 (or_4_out[0], and_8_out, and_9_out, and_10_out, and_11_out, and_12_out, and_13_out, and_14_out, and_15_out, and_16_out, and_17_out, and_18_out, and_19_out, and_20_out, and_21_out, and_22_out, and_23_out, and_24_out, and_25_out, and_26_out, and_27_out, and_28_out, and_29_out, and_30_out, and_31_out);
  S_R_Flip_Flop s_r_ff_5 (
    .S(demultiplexer_1_out20), .R(and_6_out), .clk(and_2_out), .Q(Bit24_Quotient[4]), .reset(and_6_out));  // open: Qn, preset
  and and_8 (and_8_out, Bit24_Dividend[23], demultiplexer_2_out0);
  S_R_Flip_Flop s_r_ff_6 (
    .S(demultiplexer_1_out19), .R(and_6_out), .clk(and_2_out), .Q(Bit24_Quotient[5]), .reset(and_6_out));  // open: Qn, preset
  and and_9 (and_9_out, Bit24_Dividend[22], demultiplexer_2_out1);
  and and_10 (and_10_out, Bit24_Dividend[21], demultiplexer_2_out2);
  S_R_Flip_Flop s_r_ff_7 (
    .S(demultiplexer_1_out18), .R(and_6_out), .clk(and_2_out), .Q(Bit24_Quotient[6]), .reset(and_6_out));  // open: Qn, preset
  and and_11 (and_11_out, Bit24_Dividend[20], demultiplexer_2_out3);
  and and_12 (and_12_out, Bit24_Dividend[19], demultiplexer_2_out4);
  S_R_Flip_Flop s_r_ff_8 (
    .S(demultiplexer_1_out17), .R(and_6_out), .clk(and_2_out), .Q(Bit24_Quotient[7]), .reset(and_6_out));  // open: Qn, preset
  and and_13 (and_13_out, Bit24_Dividend[18], demultiplexer_2_out5);
  and and_14 (and_14_out, Bit24_Dividend[17], demultiplexer_2_out6);
  S_R_Flip_Flop s_r_ff_9 (
    .S(demultiplexer_1_out16), .R(and_6_out), .clk(and_2_out), .Q(Bit24_Quotient[8]), .reset(and_6_out));  // open: Qn, preset
  and and_15 (and_15_out, Bit24_Dividend[16], demultiplexer_2_out7);
  and and_16 (and_16_out, Bit24_Dividend[15], demultiplexer_2_out8);
  S_R_Flip_Flop s_r_ff_10 (
    .S(demultiplexer_1_out15), .R(and_6_out), .clk(and_2_out), .Q(Bit24_Quotient[9]), .reset(and_6_out));  // open: Qn, preset
  and and_17 (and_17_out, Bit24_Dividend[14], demultiplexer_2_out9);
  and and_18 (and_18_out, Bit24_Dividend[13], demultiplexer_2_out10);
  and and_19 (and_19_out, Bit24_Dividend[12], demultiplexer_2_out11);
  and and_20 (and_20_out, Bit24_Dividend[11], demultiplexer_2_out12);
  S_R_Flip_Flop s_r_ff_11 (
    .S(demultiplexer_1_out14), .R(and_6_out), .clk(and_2_out), .Q(Bit24_Quotient[10]), .reset(and_6_out));  // open: Qn, preset
  and and_21 (and_21_out, Bit24_Dividend[10], demultiplexer_2_out13);
  and and_22 (and_22_out, Bit24_Dividend[9], demultiplexer_2_out14);
  S_R_Flip_Flop s_r_ff_12 (
    .S(demultiplexer_1_out13), .R(and_6_out), .clk(and_2_out), .Q(Bit24_Quotient[11]), .reset(and_6_out));  // open: Qn, preset
  and and_23 (and_23_out, Bit24_Dividend[8], demultiplexer_2_out15);
  and and_24 (and_24_out, Bit24_Dividend[7], demultiplexer_2_out16);
  S_R_Flip_Flop s_r_ff_13 (
    .S(demultiplexer_1_out12), .R(and_6_out), .clk(and_2_out), .Q(Bit24_Quotient[12]), .reset(and_6_out));  // open: Qn, preset
  and and_25 (and_25_out, Bit24_Dividend[6], demultiplexer_2_out17);
  and and_26 (and_26_out, Bit24_Dividend[5], demultiplexer_2_out18);
  S_R_Flip_Flop s_r_ff_14 (
    .S(demultiplexer_1_out11), .R(and_6_out), .clk(and_2_out), .Q(Bit24_Quotient[13]), .reset(and_6_out));  // open: Qn, preset
  and and_27 (and_27_out, Bit24_Dividend[4], demultiplexer_2_out19);
  and and_28 (and_28_out, Bit24_Dividend[3], demultiplexer_2_out20);
  S_R_Flip_Flop s_r_ff_15 (
    .S(demultiplexer_1_out10), .R(and_6_out), .clk(and_2_out), .Q(Bit24_Quotient[14]), .reset(and_6_out));  // open: Qn, preset
  and and_29 (and_29_out, Bit24_Dividend[2], demultiplexer_2_out21);
  and and_30 (and_30_out, Bit24_Dividend[1], demultiplexer_2_out22);
  S_R_Flip_Flop s_r_ff_16 (
    .S(demultiplexer_1_out9), .R(and_6_out), .clk(and_2_out), .Q(Bit24_Quotient[15]), .reset(and_6_out));  // open: Qn, preset
  and and_31 (and_31_out, Bit24_Dividend[0], demultiplexer_2_out23);
  S_R_Flip_Flop s_r_ff_17 (
    .S(demultiplexer_1_out8), .R(and_6_out), .clk(and_2_out), .Q(Bit24_Quotient[16]), .reset(and_6_out));  // open: Qn, preset
  S_R_Flip_Flop s_r_ff_18 (
    .S(demultiplexer_1_out7), .R(and_6_out), .clk(and_2_out), .Q(Bit24_Quotient[17]), .reset(and_6_out));  // open: Qn, preset
  S_R_Flip_Flop s_r_ff_19 (
    .S(demultiplexer_1_out6), .R(and_6_out), .clk(and_2_out), .Q(Bit24_Quotient[18]), .reset(and_6_out));  // open: Qn, preset
  S_R_Flip_Flop s_r_ff_20 (
    .S(demultiplexer_1_out5), .R(and_6_out), .clk(and_2_out), .Q(Bit24_Quotient[19]), .reset(and_6_out));  // open: Qn, preset
  S_R_Flip_Flop s_r_ff_21 (
    .S(demultiplexer_1_out4), .R(and_6_out), .clk(and_2_out), .Q(Bit24_Quotient[20]), .reset(and_6_out));  // open: Qn, preset
  S_R_Flip_Flop s_r_ff_22 (
    .S(demultiplexer_1_out3), .R(and_6_out), .clk(and_2_out), .Q(Bit24_Quotient[21]), .reset(and_6_out));  // open: Qn, preset
  S_R_Flip_Flop s_r_ff_23 (
    .S(demultiplexer_1_out2), .R(and_6_out), .clk(and_2_out), .Q(Bit24_Quotient[22]), .reset(and_6_out));  // open: Qn, preset
  S_R_Flip_Flop s_r_ff_24 (
    .S(demultiplexer_1_out1), .R(and_6_out), .clk(and_2_out), .Q(Bit24_Quotient[23]), .reset(and_6_out));  // open: Qn, preset

  assign Bit24_Remainder = Bit24_Adder_A;

  // Notes on the sheet:
  //   the adder Cin needs to be active when dividing bc thats an inverter above here not a twscmpletner
  //   REMAINDER AND QUOTIENT ARE VALID AFTER RISING EDGE ON 17th cycle
  //   RESULTS ARE CLEARED ON RISING EDGE OF 19th
  //   DIVIDER IS READY TO USE AFTER falling edge of 19th
endmodule

module Bit16_To_Bit24_High_Byte (
  input  [15:0] Bit16,
  output [23:0] Bit24
);


  assign Bit24 = {Bit16, {8{1'b0}}};
endmodule

module Bit16_To_Bit24_Low_Byte (
  input  [15:0] Bit16,
  output [23:0] Bit24
);


  assign Bit24 = {{8{1'b0}}, Bit16};
endmodule

module Bit5_Controlled_Buffer (
  input  [4:0] Bit5_In,
  input  Enable,
  output [4:0] Bit5_Out
);

  and and_1 (Bit5_Out[0], Bit5_In[0], Enable);
  and and_2 (Bit5_Out[1], Bit5_In[1], Enable);
  and and_3 (Bit5_Out[2], Bit5_In[2], Enable);
  and and_4 (Bit5_Out[3], Bit5_In[3], Enable);
  and and_5 (Bit5_Out[4], Bit5_In[4], Enable);
endmodule

module Bit16_Float_Exponent_Unit (
  input  [23:0] Bit24_Right_Shift_Result,
  input  DIV,
  input  MUL,
  input  ADD_OR_SUB,
  input  [15:0] A16,
  input  [15:0] B16,
  output [15:0] Bit16_Right_Shift_Data,
  output [3:0] Bit4_Right_Shift,
  output [23:0] Mantissa_B_Div_And_Mul_Shifted,
  output [23:0] Mantissa_A_Mul_Shifted,
  output [23:0] Mantissa_A_Add_Shifted,
  output [23:0] Mantissa_A_Sub_Shifted,
  output [23:0] Mantissa_B_Add_Shifted,
  output [23:0] Mantissa_B_Sub_Shifted,
  output [4:0] Initial_Add_Sub_Exponent,
  output [4:0] Result_Exponent_A_Sub_B_DIV,
  output [4:0] Result_Exponent_A_Add_B_MUL,
  output Result_Sign,
  output Exponent_Overflow,
  output Exponent_Underflow,
  output A_Negative,
  output B_Negative
);

  wire and_1_out, and_2_out, and_3_out, and_4_out, and_5_out, and_6_out, and_7_out, and_8_out, and_9_out,
       and_10_out, and_11_out, bit5_adder_3_cout, bit5_adder_4_cout, bit5_adder_6_cout, nor_1_out, nor_2_out,
       not_1_out, not_2_out, not_3_out, not_4_out, or_6_out, or_7_out, or_8_out, xor_1_out;
  wire [3:0] bit4_controlled_buffer_1_bit4_out, bit4_controlled_buffer_2_bit4_out,
       bit4_twos_complementer_1_bit4_result;
  wire [4:0] bit5_adder_1_bit5_result, bit5_adder_2_bit5_result, bit5_adder_3_bit5_result,
       bit5_adder_4_bit5_result, bit5_adder_5_bit5_result, bit5_adder_6_bit5_result,
       bit5_adder_7_bit5_result, bit5_controlled_buffer_1_bit5_out, bit5_controlled_buffer_2_bit5_out,
       bit5_twos_complementer_1_bit5_result, bit5_twos_complementer_2_bit5_result;
  wire [10:10] or_1_out, or_2_out;
  wire [15:0] bit16_controlled_buffer_1_bit16_out, bit16_controlled_buffer_2_bit16_out;
  wire [23:0] bit16_to_bit24_high_byte_1_bit24, bit16_to_bit24_high_byte_2_bit24,
       bit16_to_bit24_low_byte_1_bit24, bit16_to_bit24_low_byte_2_bit24, bit24_controlled_buffer_3_bit24_out,
       bit24_controlled_buffer_4_bit24_out, bit24_controlled_buffer_5_bit24_out,
       bit24_controlled_buffer_6_bit24_out;
  wire [23:20] or_9_out, or_10_out;

  or or_1 (or_1_out[10], A16[10], A16[11], A16[12], A16[13], A16[14]);
  or or_2 (or_2_out[10], B16[10], B16[11], B16[12], B16[13], B16[14]);
  Bit5_Adder bit5_adder_1 (
    .Bit5_A(A16[14:10]), .Bit5_B(5'b10001), .Bit5_Result(bit5_adder_1_bit5_result));  // open: Cin, Cout
  Bit5_Adder bit5_adder_2 (
    .Bit5_A(B16[14:10]), .Bit5_B(5'b10001), .Bit5_Result(bit5_adder_2_bit5_result));  // open: Cin, Cout
  Bit5_Twos_Complementer bit5_twos_complementer_1 (
    .Bit5_In(bit5_adder_2_bit5_result), .Bit5_Result(bit5_twos_complementer_1_bit5_result));
  Bit5_Twos_Complementer bit5_twos_complementer_2 (
    .Bit5_In(B16[14:10]), .Bit5_Result(bit5_twos_complementer_2_bit5_result));
  Bit5_Controlled_Buffer bit5_controlled_buffer_1 (
    .Bit5_In(A16[14:10]), .Enable(and_2_out), .Bit5_Out(bit5_controlled_buffer_1_bit5_out));
  Bit5_Controlled_Buffer bit5_controlled_buffer_2 (
    .Bit5_In(B16[14:10]), .Enable(and_1_out), .Bit5_Out(bit5_controlled_buffer_2_bit5_out));
  assign Initial_Add_Sub_Exponent = bit5_controlled_buffer_1_bit5_out | bit5_controlled_buffer_2_bit5_out;  // OR_Gate or_3, 5 bits wide
  and and_1 (and_1_out, ADD_OR_SUB, ~bit5_adder_3_cout);  // AND_Gate
  and and_2 (and_2_out, ADD_OR_SUB, bit5_adder_3_cout);
  Bit5_Adder bit5_adder_3 (
    .Bit5_A(A16[14:10]), .Bit5_B(bit5_twos_complementer_2_bit5_result),
    .Bit5_Result(bit5_adder_3_bit5_result), .Cout(bit5_adder_3_cout));  // open: Cin
  Bit5_Adder bit5_adder_4 (
    .Bit5_A(bit5_adder_1_bit5_result), .Bit5_B(bit5_adder_2_bit5_result),
    .Bit5_Result(bit5_adder_4_bit5_result), .Cout(bit5_adder_4_cout));  // open: Cin
  Bit5_Adder bit5_adder_5 (
    .Bit5_A(bit5_adder_4_bit5_result), .Bit5_B(5'b01111), .Bit5_Result(bit5_adder_5_bit5_result));  // open: Cin, Cout
  Bit5_Adder bit5_adder_6 (
    .Bit5_A(bit5_adder_1_bit5_result), .Bit5_B(bit5_twos_complementer_1_bit5_result),
    .Bit5_Result(bit5_adder_6_bit5_result), .Cout(bit5_adder_6_cout));  // open: Cin
  not not_1 (not_1_out, bit5_adder_6_cout);
  Bit5_Adder bit5_adder_7 (
    .Bit5_A(bit5_adder_6_bit5_result), .Bit5_B(5'b01111), .Bit5_Result(bit5_adder_7_bit5_result));  // open: Cin, Cout
  Bit16_To_Bit24_Low_Byte bit16_to_bit24_low_byte_1 (
    .Bit16({{5{1'b0}}, or_2_out[10], B16[9:0]}), .Bit24(bit16_to_bit24_low_byte_1_bit24));
  Bit16_To_Bit24_Low_Byte bit16_to_bit24_low_byte_2 (
    .Bit16({{5{1'b0}}, or_1_out[10], A16[9:0]}), .Bit24(bit16_to_bit24_low_byte_2_bit24));
  Bit16_To_Bit24_High_Byte bit16_to_bit24_high_byte_1 (
    .Bit16({{5{1'b0}}, or_1_out[10], A16[9:0]}), .Bit24(bit16_to_bit24_high_byte_1_bit24));
  Bit16_To_Bit24_High_Byte bit16_to_bit24_high_byte_2 (
    .Bit16({{5{1'b0}}, or_2_out[10], B16[9:0]}), .Bit24(bit16_to_bit24_high_byte_2_bit24));
  Bit16_Controlled_Buffer bit16_controlled_buffer_1 (
    .Enable(and_1_out), .Bit16_In({{5{1'b0}}, or_1_out[10], A16[9:0]}),
    .Bit16_Out(bit16_controlled_buffer_1_bit16_out));
  Bit16_Controlled_Buffer bit16_controlled_buffer_2 (
    .Enable(and_2_out), .Bit16_In({{5{1'b0}}, or_2_out[10], B16[9:0]}),
    .Bit16_Out(bit16_controlled_buffer_2_bit16_out));
  assign Bit16_Right_Shift_Data = bit16_controlled_buffer_1_bit16_out | bit16_controlled_buffer_2_bit16_out;  // OR_Gate or_4, 16 bits wide
  Bit4_Twos_Complementer bit4_twos_complementer_1 (
    .Bit4_In(bit5_adder_3_bit5_result[3:0]), .Bit4_Result(bit4_twos_complementer_1_bit4_result));
  not not_2 (not_2_out, bit5_adder_3_bit5_result[4]);
  and and_3 (and_3_out, not_2_out, ADD_OR_SUB);
  Bit4_Controlled_Buffer bit4_controlled_buffer_1 (
    .Bit4_In(bit4_twos_complementer_1_bit4_result), .Enable(bit5_adder_3_bit5_result[4]),
    .Bit4_Out(bit4_controlled_buffer_1_bit4_out));
  Bit4_Controlled_Buffer bit4_controlled_buffer_2 (
    .Bit4_In(bit5_adder_3_bit5_result[3:0]), .Enable(and_3_out), .Bit4_Out(bit4_controlled_buffer_2_bit4_out));
  and and_4 (and_4_out, bit5_adder_3_cout, bit5_adder_3_bit5_result[4]);
  nor nor_1 (nor_1_out, bit5_adder_3_bit5_result[4], bit5_adder_3_cout);
  and and_5 (and_5_out, ~bit5_adder_3_bit5_result[0], ~bit5_adder_3_bit5_result[1], ~bit5_adder_3_bit5_result[2], ~bit5_adder_3_bit5_result[3], bit5_adder_3_bit5_result[4]);  // AND_Gate
  Bit5_Controlled_Buffer bit5_controlled_buffer_3 (
    .Bit5_In(bit5_adder_7_bit5_result), .Enable(DIV), .Bit5_Out(Result_Exponent_A_Sub_B_DIV));
  Bit5_Controlled_Buffer bit5_controlled_buffer_4 (
    .Bit5_In(bit5_adder_5_bit5_result), .Enable(MUL), .Bit5_Out(Result_Exponent_A_Add_B_MUL));
  assign Bit4_Right_Shift = bit4_controlled_buffer_1_bit4_out | bit4_controlled_buffer_2_bit4_out;  // OR_Gate or_5, 4 bits wide
  nor nor_2 (nor_2_out, and_4_out, nor_1_out, and_5_out);
  not not_3 (not_3_out, and_1_out);
  and and_6 (and_6_out, nor_2_out, and_1_out);
  and and_7 (and_7_out, ADD_OR_SUB, not_3_out);
  and and_8 (and_8_out, nor_2_out, and_2_out);
  not not_4 (not_4_out, and_2_out);
  or or_6 (or_6_out, DIV, MUL);
  or or_7 (or_7_out, DIV, and_7_out);
  and and_9 (and_9_out, ADD_OR_SUB, not_4_out);
  Bit24_Controlled_Buffer bit24_controlled_buffer_1 (
    .Enable(or_6_out), .Bit24_In(bit16_to_bit24_low_byte_1_bit24), .Bit24_Out(Mantissa_B_Div_And_Mul_Shifted));
  Bit24_Controlled_Buffer bit24_controlled_buffer_2 (
    .Enable(MUL), .Bit24_In(bit16_to_bit24_low_byte_2_bit24), .Bit24_Out(Mantissa_A_Mul_Shifted));
  Bit24_Controlled_Buffer bit24_controlled_buffer_3 (
    .Enable(and_6_out), .Bit24_In(Bit24_Right_Shift_Result), .Bit24_Out(bit24_controlled_buffer_3_bit24_out));
  Bit24_Controlled_Buffer bit24_controlled_buffer_4 (
    .Enable(or_7_out), .Bit24_In(bit16_to_bit24_high_byte_1_bit24),
    .Bit24_Out(bit24_controlled_buffer_4_bit24_out));
  Bit24_Controlled_Buffer bit24_controlled_buffer_5 (
    .Enable(and_8_out), .Bit24_In(Bit24_Right_Shift_Result), .Bit24_Out(bit24_controlled_buffer_5_bit24_out));
  Bit24_Controlled_Buffer bit24_controlled_buffer_6 (
    .Enable(and_9_out), .Bit24_In(bit16_to_bit24_high_byte_2_bit24),
    .Bit24_Out(bit24_controlled_buffer_6_bit24_out));
  xor xor_1 (xor_1_out, B16[15], A16[15]);
  or or_8 (or_8_out, A16[15], B16[15]);
  assign {or_9_out, Mantissa_A_Add_Shifted[23:4]} = bit24_controlled_buffer_3_bit24_out | bit24_controlled_buffer_4_bit24_out;  // OR_Gate or_9, 24 bits wide
  assign {or_10_out, Mantissa_B_Add_Shifted[23:4]} = bit24_controlled_buffer_5_bit24_out | bit24_controlled_buffer_6_bit24_out;  // OR_Gate or_10, 24 bits wide
  and and_10 (and_10_out, or_6_out, xor_1_out);
  and and_11 (and_11_out, ADD_OR_SUB, or_8_out);
  or or_11 (Result_Sign, and_10_out, and_11_out);
  and and_12 (Exponent_Overflow, bit5_adder_4_cout, DIV);
  and and_13 (Exponent_Underflow, not_1_out, MUL);

  assign A_Negative = A16[15];
  assign B_Negative = B16[15];
  assign Mantissa_A_Add_Shifted[3:0] = 4'b0000;
  assign Mantissa_A_Sub_Shifted = {Mantissa_A_Add_Shifted[22:4], {5{1'b0}}};
  assign Mantissa_B_Add_Shifted[3:0] = 4'b0000;
  assign Mantissa_B_Sub_Shifted = {Mantissa_B_Add_Shifted[22:4], {5{1'b0}}};
endmodule

module fpu2 (
  input  Add,
  input  Sub,
  input  Mul,
  input  Div,
  input  [15:0] in_5,
  input  [15:0] in_6,
  input  [15:0] in_7,
  input  [15:0] in_8,
  input  [31:0] in_9,
  input  [4:0] in_10,
  input  [4:0] in_11,
  input  [4:0] in_12,
  input  [15:0] in_13,
  output [4:0] out_14,
  output [4:0] out_15,
  output [4:0] out_16,
  output [4:0] out_17,
  output [15:0] out_18,
  output [15:0] out_19,
  output [15:0] out_20,
  output [4:0] out_21,
  output [4:0] out_22,
  output [15:0] out_23,
  output [4:0] out_24,
  output [4:0] out_25,
  output [4:0] out_26,
  output [4:0] out_27
);

  wire and_1_out, and_2_out, and_3_out, and_4_out, and_5_out, and_6_out, and_7_out, and_8_out, and_9_out,
       and_10_out, and_11_out, and_12_out, and_13_out, and_14_out, and_15_out, and_16_out, and_17_out,
       and_18_out, and_19_out, and_20_out, and_21_out, and_22_out, and_23_out, and_24_out, and_25_out,
       and_26_out, and_27_out, and_28_out, and_29_out, and_30_out, and_31_out, and_32_out, and_33_out,
       and_34_out, and_35_out, and_36_out, and_37_out, and_38_out, and_40_out, and_41_out, bit5_adder_2_cout,
       bit5_adder_4_cout, bit5_adder_6_cout, bit5_adder_7_cout, bit5_adder_8_cout, bit5_adder_10_cout,
       bit5_adder_11_cout, bit5_greater_than_1_a_greater_b, bit10_add_one_1_carry_out, bit24_adder_1_c_out,
       nand_1_out, nand_2_out, nand_5_out, nor_1_out, nor_2_out, nor_3_out, nor_4_out, nor_5_out, not_1_out,
       not_2_out, or_1_out, or_2_out, or_3_out, or_4_out, or_7_out, or_10_out, or_11_out, or_12_out,
       or_13_out, or_15_out, or_16_out, or_17_out, or_19_out, or_20_out, or_21_out, or_22_out, or_23_out,
       or_24_out, or_25_out, or_28_out, or_29_out, or_30_out, or_31_out, or_33_out, undriven_2, xnor_1_out,
       xor_1_out, xor_2_out, xor_3_out, xor_4_out, xor_5_out, xor_6_out, xor_7_out, xor_8_out;
  wire [4:0] bit5_add_one_2_bit5_out, bit5_add_one_3_bit5_out, bit5_adder_1_bit5_result,
       bit5_adder_2_bit5_result, bit5_adder_3_bit5_result, bit5_adder_4_bit5_result,
       bit5_adder_5_bit5_result, bit5_adder_6_bit5_result, bit5_adder_9_bit5_result,
       bit5_adder_10_bit5_result, bit5_adder_11_bit5_result, bit5_controlled_buffer_1_bit5_out,
       bit5_controlled_buffer_2_bit5_out, bit5_controlled_buffer_3_bit5_out,
       bit5_controlled_buffer_5_bit5_out, bit5_controlled_buffer_6_bit5_out,
       bit5_controlled_buffer_7_bit5_out, bit5_controlled_buffer_8_bit5_out,
       bit5_controlled_buffer_9_bit5_out, bit5_controlled_buffer_10_bit5_out,
       bit5_controlled_buffer_11_bit5_out, bit5_controlled_buffer_12_bit5_out, bit5_inverter_1_bit5_out,
       bit5_inverter_2_bit5_out, bit5_inverter_3_bit5_out, bit5_inverter_4_bit5_out,
       bit5_inverter_5_bit5_out, bit5_inverter_6_bit5_out, bit5_toggle_twscmplmtr_1_bit5_result,
       bit5_toggle_twscmplmtr_3_bit5_result, bit5_toggle_twscmplmtr_6_bit5_result,
       bit5_twos_complementer_1_bit5_result, bit5_twos_complementer_2_bit5_result, or_26_out, or_27_out,
       or_32_out, priority_encoder_1_out, undriven, undriven_3;
  wire [4:1] bit5_add_one_1_bit5_out;
  wire [4:4] bit5_add_one_1_bit5_out_2;
  wire [9:0] bit10_add_one_1_bit10_out, bit10_controlled_buffer_1_bit10_out;
  wire [10:0] bit11_controlled_buffer_1_bit11_out, bit11_controlled_buffer_2_bit11_out,
       bit11_controlled_buffer_3_bit11_out, bit11_controlled_buffer_4_bit11_out,
       bit11_controlled_buffer_5_bit11_out, bit11_controlled_buffer_6_bit11_out,
       bit11_controlled_buffer_7_bit11_out, bit11_controlled_buffer_8_bit11_out, or_8_out, or_9_out;
  wire [10:10] or_5_out, or_6_out;
  wire [15:0] bit11_to_bit16_high_3_bit16_out, bit11_to_bit16_high_4_bit16_out,
       bit11_to_bit16_low_1_bit16_out, bit11_to_bit16_low_2_bit16_out, bit11_to_bit16_low_3_bit16_out,
       bit16_controlled_buffer_1_bit16_out, bit16_controlled_buffer_2_bit16_out,
       bit16_multiplier_1_lower_word, bit16_multiplier_1_upper_word;
  wire [15:15] and_39_out;
  wire [23:0] bit16_to_bit24_high_byte_1_bit24, bit16_to_bit24_high_byte_2_bit24,
       bit16_to_bit24_low_byte_1_bit24, bit24_adder_1_bit24_result, bit24_controlled_buffer_1_bit24_out,
       bit24_controlled_buffer_2_bit24_out, bit24_controlled_buffer_3_bit24_out,
       bit24_controlled_buffer_4_bit24_out, bit24_toggle_twscmplmtr_1_bit24_out,
       bit24_toggle_twscmplmtr_2_bit24_out, bit24_toggle_twscmplmtr_3_bit24_out,
       bit32_to_bit24_high_1_bit24_out, divider_1_out, divider_1_rem;
  wire [31:0] bit11_to_bit32_high_1_bit32_out, bit32_left_shift_1_bit32_result,
       bit32_right_shift_1_bit32_result, or_18_out;

  // Probe on in_13
  // Probe on in_7
  // Probe on in_8
  // Probe on in_7
  // Probe on in_7
  // Probe on in_8
  FPAdder #(.fpwidth(16)) fpadder_1 (.a(in_8), .b(in_7), .out(out_18));
  FPSubtractor #(.fpwidth(16)) fpsubtractor_1 (.a(in_7), .b(in_8), .out(out_20));
  FPMultiplier #(.fpwidth(16)) fpmultiplier_1 (.a(in_8), .b(in_7), .out(out_19));
  FPDivider #(.fpwidth(16)) fpdivider_1 (.a(in_7), .b(in_8), .out(out_23));
  or or_1 (or_1_out, Add, Sub);
  or or_2 (or_2_out, Mul, Div);
  // Probe on out_18
  // Probe on out_20
  // Probe on out_20[14:10]
  // Probe on out_23
  or or_3 (or_3_out, in_7[0], in_7[1], in_7[2], in_7[3], in_7[4], in_7[5], in_7[6], in_7[7], in_7[8], in_7[9]);
  or or_4 (or_4_out, in_8[0], in_8[1], in_8[2], in_8[3], in_8[4], in_8[5], in_8[6], in_8[7], in_8[8], in_8[9]);
  or or_5 (or_5_out[10], in_7[10], in_7[11], in_7[12], in_7[13], in_7[14]);
  or or_6 (or_6_out[10], in_8[10], in_8[11], in_8[12], in_8[13], in_8[14]);
  // Probe on out_19
  // Probe on {and_39_out[15], bit5_add_one_3_bit5_out, bit10_controlled_buffer_1_bit10_out}
  // Probe on {and_39_out[15], bit5_add_one_3_bit5_out, bit10_controlled_buffer_1_bit10_out}
  and and_1 (and_1_out, in_7[9], or_3_out, in_7[10], in_7[11], in_7[12], in_7[13], in_7[14]);
  and and_2 (and_2_out, ~in_7[9], or_3_out, in_7[10], in_7[11], in_7[12], in_7[13], in_7[14]);  // AND_Gate
  and and_3 (and_3_out, ~in_7[9], in_7[10], in_7[11], in_7[12], in_7[13], in_7[14]);  // AND_Gate
  nor nor_1 (nor_1_out, in_7[0], in_7[1], in_7[2], in_7[3], in_7[4], in_7[5], in_7[6], in_7[7], in_7[8], in_7[9], in_7[10], in_7[11], in_7[12], in_7[13], in_7[14]);
  and and_4 (and_4_out, in_8[9], or_4_out, in_8[10], in_8[11], in_8[12], in_8[13], in_8[14]);
  and and_5 (and_5_out, ~in_8[9], or_4_out, in_8[10], in_8[11], in_8[12], in_8[13], in_8[14]);  // AND_Gate
  and and_6 (and_6_out, ~in_8[9], in_8[10], in_8[11], in_8[12], in_8[13], in_8[14]);  // AND_Gate
  nor nor_2 (nor_2_out, in_8[0], in_8[1], in_8[2], in_8[3], in_8[4], in_8[5], in_8[6], in_8[7], in_8[8], in_8[9], in_8[10], in_8[11], in_8[12], in_8[13], in_8[14]);
  Bit5_Inverter bit5_inverter_1 (.Bit5_In(out_23[14:10]), .Bit5_Out(bit5_inverter_1_bit5_out));
  Bit5_Inverter bit5_inverter_2 (.Bit5_In(in_8[14:10]), .Bit5_Out(bit5_inverter_2_bit5_out));
  and and_7 (and_7_out, or_1_out, ~not_1_out);  // AND_Gate
  and and_8 (and_8_out, or_1_out, not_1_out);
  // Probe on bit5_inverter_5_bit5_out
  // Probe on bit5_add_one_3_bit5_out
  Bit5_Inverter bit5_inverter_3 (.Bit5_In(out_20[14:10]), .Bit5_Out(bit5_inverter_3_bit5_out));
  and and_9 (and_9_out, and_3_out, and_6_out, Div);
  and and_10 (and_10_out, or_1_out, ~not_1_out);  // AND_Gate
  and and_11 (and_11_out, or_1_out, not_1_out);
  and and_12 (and_12_out, or_1_out, not_1_out);
  and and_13 (and_13_out, or_1_out, ~not_1_out);  // AND_Gate
  Bit5_Toggle_TwsCmplmtr bit5_toggle_twscmplmtr_1 (
    .Bit5_Input(in_8[14:10]), .Enable_Twos(Div), .Bit5_Result(bit5_toggle_twscmplmtr_1_bit5_result));
  Bit5_Inverter bit5_inverter_4 (.Bit5_In(out_19[14:10]), .Bit5_Out(bit5_inverter_4_bit5_out));
  // Probe on bit5_inverter_5_bit5_out
  Bit5_Adder bit5_adder_1 (
    .Cin(1'b1), .Bit5_A(bit5_add_one_3_bit5_out), .Bit5_B(bit5_inverter_1_bit5_out),
    .Bit5_Result(bit5_adder_1_bit5_result));  // open: Cout
  and and_14 (and_14_out, nor_1_out, nor_2_out, Div);
  and and_15 (and_15_out, and_3_out, nor_2_out, Mul);
  Bit5_Adder bit5_adder_2 (
    .Cin(1'b1), .Bit5_A(in_7[14:10]), .Bit5_B(bit5_inverter_2_bit5_out),
    .Bit5_Result(bit5_adder_2_bit5_result), .Cout(bit5_adder_2_cout));
  // Probe on bit5_adder_3_bit5_result
  // Probe on bit5_adder_1_bit5_result
  and and_16 (and_16_out, nor_1_out, and_6_out, Mul);
  Bit11_Controlled_Buffer bit11_controlled_buffer_1 (
    .Enable(Mul), .Bit11_In({or_5_out[10], in_7[9:0]}), .Bit11_Out(bit11_controlled_buffer_1_bit11_out));
  Bit11_Controlled_Buffer bit11_controlled_buffer_2 (
    .Enable(Mul), .Bit11_In({or_6_out[10], in_8[9:0]}), .Bit11_Out(bit11_controlled_buffer_2_bit11_out));
  Bit11_Controlled_Buffer bit11_controlled_buffer_3 (
    .Enable(Div), .Bit11_In({or_5_out[10], in_7[9:0]}), .Bit11_Out(bit11_controlled_buffer_3_bit11_out));
  Bit11_Controlled_Buffer bit11_controlled_buffer_4 (
    .Enable(Div), .Bit11_In({or_6_out[10], in_8[9:0]}), .Bit11_Out(bit11_controlled_buffer_4_bit11_out));
  Bit11_Controlled_Buffer bit11_controlled_buffer_5 (
    .Enable(and_10_out), .Bit11_In({or_5_out[10], in_7[9:0]}), .Bit11_Out(bit11_controlled_buffer_5_bit11_out));
  Bit11_Controlled_Buffer bit11_controlled_buffer_6 (
    .Enable(and_11_out), .Bit11_In({or_6_out[10], in_8[9:0]}), .Bit11_Out(bit11_controlled_buffer_6_bit11_out));
  Bit11_Controlled_Buffer bit11_controlled_buffer_7 (
    .Enable(and_12_out), .Bit11_In({or_5_out[10], in_7[9:0]}), .Bit11_Out(bit11_controlled_buffer_7_bit11_out));
  Bit11_Controlled_Buffer bit11_controlled_buffer_8 (
    .Enable(and_13_out), .Bit11_In({or_6_out[10], in_8[9:0]}), .Bit11_Out(bit11_controlled_buffer_8_bit11_out));
  not not_1 (not_1_out, bit5_adder_2_cout);
  Bit5_Controlled_Buffer bit5_controlled_buffer_1 (
    .Bit5_In(in_7[14:10]), .Enable(and_7_out), .Bit5_Out(bit5_controlled_buffer_1_bit5_out));
  Bit5_Controlled_Buffer bit5_controlled_buffer_2 (
    .Bit5_In(in_8[14:10]), .Enable(and_8_out), .Bit5_Out(bit5_controlled_buffer_2_bit5_out));
  Bit5_Adder bit5_adder_3 (
    .Cin(1'b1), .Bit5_A(bit5_add_one_3_bit5_out), .Bit5_B(bit5_inverter_3_bit5_out),
    .Bit5_Result(bit5_adder_3_bit5_result));  // open: Cout
  and and_17 (and_17_out, and_3_out, and_6_out, or_7_out, xor_2_out);
  or or_7 (or_7_out, Add, Sub);
  xor xor_1 (xor_1_out, in_7[15], Sub);
  assign or_8_out = bit11_controlled_buffer_5_bit11_out | bit11_controlled_buffer_6_bit11_out;  // OR_Gate or_8, 11 bits wide
  assign or_9_out = bit11_controlled_buffer_7_bit11_out | bit11_controlled_buffer_8_bit11_out;  // OR_Gate or_9, 11 bits wide
  Bit5_Adder bit5_adder_4 (
    .Bit5_A(in_7[14:10]), .Bit5_B(bit5_toggle_twscmplmtr_1_bit5_result),
    .Bit5_Result(bit5_adder_4_bit5_result), .Cout(bit5_adder_4_cout));  // open: Cin
  Bit5_Adder bit5_adder_5 (
    .Cin(1'b1), .Bit5_A(bit5_add_one_3_bit5_out), .Bit5_B(bit5_inverter_4_bit5_out),
    .Bit5_Result(bit5_adder_5_bit5_result));  // open: Cout
  and and_18 (and_18_out, ~xor_3_out, or_7_out, and_6_out, and_3_out);  // AND_Gate
  xor xor_2 (xor_2_out, xor_1_out, in_8[15]);
  xor xor_3 (xor_3_out, xor_1_out, in_8[15]);
  // Probe on bit5_adder_5_bit5_result
  and and_19 (and_19_out, ~or_10_out, nor_2_out);  // AND_Gate
  or or_10 (or_10_out, and_1_out, and_2_out, and_3_out, nor_1_out);
  Bit11_To_Bit16_High bit11_to_bit16_high_1 ();  // open: Bit11_In, Bit16_Out
  Bit11_To_Bit16_High bit11_to_bit16_high_2 ();  // open: Bit11_In, Bit16_Out
  Bit11_To_Bit16_Low bit11_to_bit16_low_1 (
    .Bit11_In(bit11_controlled_buffer_1_bit11_out), .Bit16_Out(bit11_to_bit16_low_1_bit16_out));
  Bit11_To_Bit16_Low bit11_to_bit16_low_2 (
    .Bit11_In(bit11_controlled_buffer_2_bit11_out), .Bit16_Out(bit11_to_bit16_low_2_bit16_out));
  Bit11_To_Bit16_High bit11_to_bit16_high_3 (
    .Bit11_In(bit11_controlled_buffer_3_bit11_out), .Bit16_Out(bit11_to_bit16_high_3_bit16_out));
  Bit11_To_Bit16_Low bit11_to_bit16_low_3 (
    .Bit11_In(bit11_controlled_buffer_4_bit11_out), .Bit16_Out(bit11_to_bit16_low_3_bit16_out));
  and and_20 (and_20_out, not_1_out, in_8[15]);
  and and_21 (and_21_out, ~not_1_out, in_8[15]);  // AND_Gate
  xor xor_4 (xor_4_out, or_10_out, or_11_out);
  or or_11 (or_11_out, and_4_out, and_5_out, and_6_out, nor_2_out);
  Bit11_To_Bit16_High bit11_to_bit16_high_4 (.Bit11_In(or_8_out), .Bit16_Out(bit11_to_bit16_high_4_bit16_out));
  Bit16_To_Bit24_High_Byte bit16_to_bit24_high_byte_1 (
    .Bit16(bit11_to_bit16_high_4_bit16_out), .Bit24(bit16_to_bit24_high_byte_1_bit24));
  and and_22 (and_22_out, ~not_1_out, in_7[15]);  // AND_Gate
  and and_23 (and_23_out, not_1_out, in_7[15]);
  Bit5_Toggle_TwsCmplmtr bit5_toggle_twscmplmtr_2 (.Bit5_Input(5'b10001), .Enable_Twos(Mul));  // open: Bit5_Result
  and and_24 (and_24_out, Mul, xor_4_out, xor_5_out);
  xor xor_5 (xor_5_out, and_3_out, and_6_out);
  or or_12 (or_12_out, and_20_out, and_22_out);
  or or_13 (or_13_out, and_21_out, and_23_out);
  Bit11_To_Bit32_High bit11_to_bit32_high_1 (.Bit11_In(or_9_out), .Bit32_Out(bit11_to_bit32_high_1_bit32_out));
  Bit5_Toggle_TwsCmplmtr bit5_toggle_twscmplmtr_3 (
    .Bit5_Input(bit5_adder_2_bit5_result), .Enable_Twos(not_1_out),
    .Bit5_Result(bit5_toggle_twscmplmtr_3_bit5_result));
  Bit5_Adder bit5_adder_6 (
    .Bit5_A(bit5_adder_4_bit5_result), .Bit5_B({1'b0, {4{Div}}}), .Bit5_Result(bit5_adder_6_bit5_result),
    .Cout(bit5_adder_6_cout));  // open: Cin
  Bit5_Toggle_TwsCmplmtr bit5_toggle_twscmplmtr_4 (.Bit5_Input(in_11), .Enable_Twos(1'b1), .Bit5_Result(out_21));
  Bit16_To_Bit24_High_Byte bit16_to_bit24_high_byte_2 (
    .Bit16(bit11_to_bit16_high_3_bit16_out), .Bit24(bit16_to_bit24_high_byte_2_bit24));
  Bit16_To_Bit24_Low_Byte bit16_to_bit24_low_byte_1 (
    .Bit16(bit11_to_bit16_low_3_bit16_out), .Bit24(bit16_to_bit24_low_byte_1_bit24));
  and and_25 (and_25_out, not_1_out, Sub);
  and and_26 (and_26_out, Sub, ~not_1_out);  // AND_Gate
  nor nor_3 (nor_3_out, bit5_adder_6_cout, bit5_adder_4_cout);
  xor xor_6 (xor_6_out, and_25_out, or_12_out);
  xor xor_7 (xor_7_out, and_26_out, or_13_out);
  Divider #(.width(24)) divider_1 (
    .a(bit16_to_bit24_high_byte_2_bit24), .b(bit16_to_bit24_low_byte_1_bit24), .out(divider_1_out),
    .rem(divider_1_rem));  // open: upper
  xor xor_8 (xor_8_out, xor_6_out, xor_7_out);
  xnor xnor_1 (xnor_1_out, xor_6_out, xor_7_out);
  and and_27 (and_27_out, xor_6_out, ~xor_7_out);  // AND_Gate
  and and_28 (and_28_out, xor_7_out, ~xor_6_out);  // AND_Gate
  Bit5_Controlled_Buffer bit5_controlled_buffer_3 (
    .Bit5_In(bit5_toggle_twscmplmtr_3_bit5_result), .Enable(or_1_out),
    .Bit5_Out(bit5_controlled_buffer_3_bit5_out));
  Bit5_Controlled_Buffer bit5_controlled_buffer_4 (
    .Bit5_In(bit5_adder_6_bit5_result), .Enable(or_2_out), .Bit5_Out(out_15));
  Bit5_Adder bit5_adder_7 (
    .Bit5_A(out_21), .Bit5_B(in_10), .Bit5_Result(out_22), .Cout(bit5_adder_7_cout));  // open: Cin
  // Probe on divider_1_out
  assign out_14 = bit5_controlled_buffer_1_bit5_out | bit5_controlled_buffer_2_bit5_out | out_15;  // OR_Gate or_14, 5 bits wide
  Bit16_Multiplier bit16_multiplier_1 (
    .Bit16_B(bit11_to_bit16_low_1_bit16_out), .Bit16_A(bit11_to_bit16_low_2_bit16_out),
    .Lower_Word(bit16_multiplier_1_lower_word), .Upper_Word(bit16_multiplier_1_upper_word));
  and and_29 (and_29_out, xor_6_out, xor_8_out);
  and and_30 (and_30_out, xor_6_out, xnor_1_out);
  Bit24_Toggle_TwsCmplmtr bit24_toggle_twscmplmtr_1 (
    .Enable(and_27_out), .Bit24_In(bit16_to_bit24_high_byte_1_bit24),
    .Bit24_Out(bit24_toggle_twscmplmtr_1_bit24_out));
  Bit24_Toggle_TwsCmplmtr bit24_toggle_twscmplmtr_2 (
    .Enable(and_28_out), .Bit24_In(bit32_to_bit24_high_1_bit24_out),
    .Bit24_Out(bit24_toggle_twscmplmtr_2_bit24_out));
  Bit32_Right_Shift bit32_right_shift_1 (
    .Bit32_In(bit11_to_bit32_high_1_bit32_out), .Bit5_Shift(bit5_controlled_buffer_3_bit5_out),
    .Bit32_Result(bit32_right_shift_1_bit32_result));
  nor nor_4 (nor_4_out, out_15[0], out_15[1], out_15[2], out_15[3], out_15[4]);
  or or_15 (or_15_out, and_29_out, and_30_out);
  or or_16 (or_16_out, nor_3_out, nor_4_out);
  nor nor_5 (nor_5_out, bit5_adder_7_cout, bit5_adder_8_cout);
  Bit5_Adder bit5_adder_8 (
    .Bit5_A(out_22), .Bit5_B(in_12), .Bit5_Result(out_25), .Cout(bit5_adder_8_cout));  // open: Cin
  and and_31 (and_31_out, Div, or_16_out);
  Bit24_Controlled_Buffer bit24_controlled_buffer_1 (
    .Enable(or_1_out), .Bit24_In(bit24_toggle_twscmplmtr_1_bit24_out),
    .Bit24_Out(bit24_controlled_buffer_1_bit24_out));
  Bit24_Controlled_Buffer bit24_controlled_buffer_2 (
    .Enable(or_1_out), .Bit24_In(bit24_toggle_twscmplmtr_2_bit24_out),
    .Bit24_Out(bit24_controlled_buffer_2_bit24_out));
  Bit32_To_Bit24_High bit32_to_bit24_high_1 (
    .Bit32_In(bit32_right_shift_1_bit32_result), .Bit24_Out(bit32_to_bit24_high_1_bit24_out));
  Bit16_Controlled_Buffer bit16_controlled_buffer_1 (
    .Enable(Mul), .Bit16_In(bit16_multiplier_1_lower_word), .Bit16_Out(bit16_controlled_buffer_1_bit16_out));
  Bit16_Controlled_Buffer bit16_controlled_buffer_2 (
    .Enable(Mul), .Bit16_In(bit16_multiplier_1_upper_word), .Bit16_Out(bit16_controlled_buffer_2_bit16_out));
  Bit5_Toggle_TwsCmplmtr bit5_toggle_twscmplmtr_5 (
    .Bit5_Input(out_25), .Enable_Twos(bit5_adder_8_cout), .Bit5_Result(out_26));
  Bit24_Controlled_Buffer bit24_controlled_buffer_3 (
    .Enable(Div), .Bit24_In(divider_1_out), .Bit24_Out(bit24_controlled_buffer_3_bit24_out));
  Bit24_Controlled_Buffer bit24_controlled_buffer_4 (
    .Enable(or_1_out), .Bit24_In(bit24_toggle_twscmplmtr_3_bit24_out),
    .Bit24_Out(bit24_controlled_buffer_4_bit24_out));
  Bit24_Adder bit24_adder_1 (
    .Bit24_A(bit24_controlled_buffer_1_bit24_out), .Bit24_B(bit24_controlled_buffer_2_bit24_out),
    .Bit24_Result(bit24_adder_1_bit24_result), .C_OUT(bit24_adder_1_c_out));  // open: C_In, Bit16_C_OUT
  and and_32 (and_32_out, or_1_out, or_17_out);
  or or_17 (or_17_out, not_2_out, and_33_out);
  and and_33 (and_33_out, xnor_1_out, ~bit24_adder_1_c_out);  // AND_Gate
  not not_2 (not_2_out, xnor_1_out);
  assign or_18_out = {bit16_controlled_buffer_2_bit16_out, bit16_controlled_buffer_1_bit16_out} | {bit24_controlled_buffer_3_bit24_out, {8{1'b0}}} | {bit24_controlled_buffer_4_bit24_out, {8{1'b0}}};  // OR_Gate or_18, 32 bits wide
  and and_34 (and_34_out, or_18_out[31], Mul);
  or or_19 (or_19_out, Mul, Div, and_32_out);
  Priority_Encoder #(.select(5)) priority_encoder_1 (
    .in0(or_18_out[0]), .in1(or_18_out[1]), .in2(or_18_out[2]), .in3(or_18_out[3]), .in4(or_18_out[4]),
    .in5(or_18_out[5]), .in6(or_18_out[6]), .in7(or_18_out[7]), .in8(or_18_out[8]), .in9(or_18_out[9]),
    .in10(or_18_out[10]), .in11(or_18_out[11]), .in12(or_18_out[12]), .in13(or_18_out[13]),
    .in14(or_18_out[14]), .in15(or_18_out[15]), .in16(or_18_out[16]), .in17(or_18_out[17]),
    .in18(or_18_out[18]), .in19(or_18_out[19]), .in20(or_18_out[20]), .in21(or_18_out[21]),
    .in22(or_18_out[22]), .in23(or_18_out[23]), .in24(or_18_out[24]), .in25(or_18_out[25]),
    .in26(or_18_out[26]), .in27(or_18_out[27]), .in28(or_18_out[28]), .in29(or_18_out[29]),
    .in30(or_18_out[30]), .in31(or_18_out[31]), .out(priority_encoder_1_out), .en_in(or_23_out));  // open: gs, en_out
  or or_20 (or_20_out, and_34_out, and_32_out);
  // Probe on out_14
  // Probe on out_14
  or or_21 (or_21_out, Div, Add, Sub, Mul);
  // Probe on priority_encoder_1_out
  // Probe on priority_encoder_1_out
  or or_22 (or_22_out, bit24_adder_1_bit24_result[0], bit24_adder_1_bit24_result[1], bit24_adder_1_bit24_result[2], bit24_adder_1_bit24_result[3], bit24_adder_1_bit24_result[4], bit24_adder_1_bit24_result[5], bit24_adder_1_bit24_result[6], bit24_adder_1_bit24_result[7], bit24_adder_1_bit24_result[8], bit24_adder_1_bit24_result[9], bit24_adder_1_bit24_result[10], bit24_adder_1_bit24_result[11], bit24_adder_1_bit24_result[13], bit24_adder_1_bit24_result[14], bit24_adder_1_bit24_result[15], bit24_adder_1_bit24_result[16], bit24_adder_1_bit24_result[17], bit24_adder_1_bit24_result[18], bit24_adder_1_bit24_result[19], bit24_adder_1_bit24_result[20], bit24_adder_1_bit24_result[21], bit24_adder_1_bit24_result[22], bit24_adder_1_bit24_result[23], bit24_adder_1_bit24_result[12]);
  and and_35 (and_35_out, or_21_out, or_23_out);
  or or_23 (or_23_out, or_18_out[0], or_18_out[1], or_18_out[2], or_18_out[3], or_18_out[4], or_18_out[5], or_18_out[6], or_18_out[7], or_18_out[8], or_18_out[9], or_18_out[10], or_18_out[11], or_18_out[12], or_18_out[13], or_18_out[14], or_18_out[15], or_18_out[17], or_18_out[18], or_18_out[19], or_18_out[20], or_18_out[21], or_18_out[22], or_18_out[23], or_18_out[24], or_18_out[25], or_18_out[26], or_18_out[27], or_18_out[28], or_18_out[29], or_18_out[30], or_18_out[31], or_18_out[16]);
  nand nand_1 (nand_1_out, and_31_out, Div);
  Bit24_Toggle_TwsCmplmtr bit24_toggle_twscmplmtr_3 (
    .Enable(and_29_out), .Bit24_In(bit24_adder_1_bit24_result),
    .Bit24_Out(bit24_toggle_twscmplmtr_3_bit24_out));
  Bit5_Controlled_Buffer bit5_controlled_buffer_5 (
    .Bit5_In(bit5_adder_9_bit5_result), .Enable(Div), .Bit5_Out(bit5_controlled_buffer_5_bit5_out));
  Bit5_Controlled_Buffer bit5_controlled_buffer_6 (
    .Bit5_In(bit5_adder_9_bit5_result), .Enable(or_19_out), .Bit5_Out(bit5_controlled_buffer_6_bit5_out));
  Bit5_Controlled_Buffer bit5_controlled_buffer_7 (
    .Bit5_In(bit5_inverter_5_bit5_out), .Enable(or_20_out), .Bit5_Out(bit5_controlled_buffer_7_bit5_out));
  Bit5_Adder bit5_adder_9 (
    .Bit5_A(bit5_inverter_5_bit5_out), .Bit5_B(bit5_controlled_buffer_8_bit5_out),
    .Bit5_Result(bit5_adder_9_bit5_result));  // open: Cin, Cout
  Bit5_Controlled_Buffer bit5_controlled_buffer_8 (
    .Bit5_In(bit5_inverter_6_bit5_out), .Enable(and_31_out), .Bit5_Out(bit5_controlled_buffer_8_bit5_out));
  Bit5_Inverter bit5_inverter_5 (.Bit5_In(priority_encoder_1_out), .Bit5_Out(bit5_inverter_5_bit5_out));
  Bit5_Inverter bit5_inverter_6 (.Bit5_In({bit5_add_one_1_bit5_out, 1'b0}), .Bit5_Out(bit5_inverter_6_bit5_out));
  Bit5_Twos_Complementer bit5_twos_complementer_1 (
    .Bit5_In(out_14), .Bit5_Result(bit5_twos_complementer_1_bit5_result));
  Bit5_Add_One bit5_add_one_1 (
    .Add_One(and_31_out), .Bit5_In(bit5_twos_complementer_1_bit5_result),
    .Bit5_Out({bit5_add_one_1_bit5_out_2[4], bit5_add_one_1_bit5_out}));  // open: Carry_Out
  Bit5_Controlled_Buffer bit5_controlled_buffer_9 (
    .Bit5_In(out_14), .Enable(nand_1_out), .Bit5_Out(bit5_controlled_buffer_9_bit5_out));
  or or_24 (or_24_out, divider_1_rem[11], divider_1_rem[0], divider_1_rem[1], divider_1_rem[2], divider_1_rem[3], divider_1_rem[4], divider_1_rem[5], divider_1_rem[6], divider_1_rem[7], divider_1_rem[8], divider_1_rem[9], divider_1_rem[10], divider_1_rem[12], divider_1_rem[13], divider_1_rem[14], divider_1_rem[15], divider_1_rem[16], divider_1_rem[17], divider_1_rem[18], divider_1_rem[19], divider_1_rem[20], divider_1_rem[21], divider_1_rem[22], divider_1_rem[23]);
  and and_36 (and_36_out, or_24_out, Div);
  or or_25 (or_25_out, Sub, or_23_out);
  assign or_26_out = bit5_controlled_buffer_7_bit5_out | bit5_controlled_buffer_5_bit5_out;  // OR_Gate or_26, 5 bits wide
  assign or_27_out = bit5_twos_complementer_2_bit5_result | bit5_controlled_buffer_9_bit5_out;  // OR_Gate or_27, 5 bits wide
  // Probe on undriven_2
  // Probe on undriven_2
  or or_28 (or_28_out, and_37_out, and_34_out);
  and and_37 (and_37_out, ~xor_8_out, bit24_adder_1_c_out);  // AND_Gate
  // Probe on or_32_out
  // Probe on or_32_out
  Bit5_Add_One bit5_add_one_2 (
    .Add_One(and_35_out), .Bit5_In(bit5_controlled_buffer_6_bit5_out), .Bit5_Out(bit5_add_one_2_bit5_out));  // open: Carry_Out
  Bit5_Twos_Complementer bit5_twos_complementer_2 (
    .Bit5_In({bit5_add_one_1_bit5_out_2[4], bit5_add_one_1_bit5_out}),
    .Bit5_Result(bit5_twos_complementer_2_bit5_result));
  and and_38 (and_38_out, Div, bit5_greater_than_1_a_greater_b);
  nand nand_2 (nand_2_out, Div, bit5_greater_than_1_a_greater_b);
  Bit5_Greater_Than bit5_greater_than_1 (
    .Bit5_A(bit5_controlled_buffer_6_bit5_out), .Bit5_B(undriven),
    .A_Greater_B(bit5_greater_than_1_a_greater_b));
  Bit5_Adder bit5_adder_10 (
    .Cin(or_28_out), .Bit5_A(bit5_toggle_twscmplmtr_6_bit5_result), .Bit5_B(or_27_out),
    .Bit5_Result(bit5_adder_10_bit5_result), .Cout(bit5_adder_10_cout));
  or or_29 (or_29_out, or_22_out, Div, Mul);
  Bit5_Toggle_TwsCmplmtr bit5_toggle_twscmplmtr_6 (
    .Bit5_Input(or_26_out), .Enable_Twos(or_25_out), .Bit5_Result(bit5_toggle_twscmplmtr_6_bit5_result));
  or or_30 (or_30_out, Div, or_22_out);
  and and_39 (and_39_out[15], or_30_out, or_15_out);
  Bit5_Controlled_Buffer bit5_controlled_buffer_10 (
    .Bit5_In(undriven_3), .Enable(and_38_out), .Bit5_Out(bit5_controlled_buffer_10_bit5_out));
  Bit5_Controlled_Buffer bit5_controlled_buffer_11 (
    .Bit5_In(bit5_controlled_buffer_6_bit5_out), .Enable(nand_2_out),
    .Bit5_Out(bit5_controlled_buffer_11_bit5_out));
  // Probe on {Mul, Div, 1'b0, Div, Mul}
  // Probe on {Mul, Div, 1'b0, Div, Mul}
  Bit32_Left_Shift bit32_left_shift_1 (
    .Bit32_In(or_18_out), .Bit5_Shift(bit5_add_one_2_bit5_out), .Bit32_Result(bit32_left_shift_1_bit32_result));
  Bit5_Controlled_Buffer bit5_controlled_buffer_12 (
    .Bit5_In(bit5_adder_10_bit5_result), .Enable(or_29_out), .Bit5_Out(bit5_controlled_buffer_12_bit5_out));
  // Probe on bit5_controlled_buffer_12_bit5_out
  // Probe on bit5_controlled_buffer_12_bit5_out
  // NAND_Gate nand_3 is placed but not wired
  or or_31 (or_31_out, and_36_out, bit32_left_shift_1_bit32_result[0], bit32_left_shift_1_bit32_result[1], bit32_left_shift_1_bit32_result[2], bit32_left_shift_1_bit32_result[3], bit32_left_shift_1_bit32_result[4], bit32_left_shift_1_bit32_result[5], bit32_left_shift_1_bit32_result[6], bit32_left_shift_1_bit32_result[7], bit32_left_shift_1_bit32_result[8], bit32_left_shift_1_bit32_result[9], bit32_left_shift_1_bit32_result[10], bit32_left_shift_1_bit32_result[11], bit32_left_shift_1_bit32_result[12], bit32_left_shift_1_bit32_result[13], bit32_left_shift_1_bit32_result[14], bit32_left_shift_1_bit32_result[15], bit32_left_shift_1_bit32_result[16], bit32_left_shift_1_bit32_result[17], bit32_left_shift_1_bit32_result[18], bit32_left_shift_1_bit32_result[19]);
  // NAND_Gate nand_4 has open pins: in3=and_40_out, out=open
  // AND_Gate and_40 has open pins: out=and_40_out
  assign or_32_out = bit5_controlled_buffer_10_bit5_out | bit5_controlled_buffer_11_bit5_out;  // OR_Gate or_32, 5 bits wide
  and and_41 (and_41_out, bit32_left_shift_1_bit32_result[21], or_33_out);
  or or_33 (or_33_out, or_31_out, bit32_left_shift_1_bit32_result[20]);
  // Probe on bit5_adder_11_bit5_result
  // Probe on bit5_adder_11_bit5_result
  Bit5_Adder bit5_adder_11 (
    .Bit5_A(bit5_controlled_buffer_12_bit5_out), .Bit5_B({Mul, Div, 1'b0, Div, Mul}),
    .Bit5_Result(bit5_adder_11_bit5_result), .Cout(bit5_adder_11_cout));  // open: Cin
  Bit10_Add_One bit10_add_one_1 (
    .Add_One(and_41_out), .Bit10_In(bit32_left_shift_1_bit32_result[31:22]),
    .Bit10_Out(bit10_add_one_1_bit10_out), .Carry_Out(bit10_add_one_1_carry_out));
  Bit5_Add_One bit5_add_one_3 (
    .Add_One(bit10_add_one_1_carry_out), .Bit5_In(bit5_adder_11_bit5_result),
    .Bit5_Out(bit5_add_one_3_bit5_out));  // open: Carry_Out
  // Probe on bit5_add_one_3_bit5_out
  // Probe on bit5_add_one_3_bit5_out
  nand nand_5 (nand_5_out, bit5_add_one_3_bit5_out[0], bit5_add_one_3_bit5_out[1], bit5_add_one_3_bit5_out[2], bit5_add_one_3_bit5_out[3], bit5_add_one_3_bit5_out[4]);
  Bit10_Controlled_Buffer bit10_controlled_buffer_1 (
    .Enable(1'b1), .Bit10_In(bit10_add_one_1_bit10_out), .Bit10_Out(bit10_controlled_buffer_1_bit10_out));
  // Probe on {and_39_out[15], bit5_add_one_3_bit5_out, bit10_controlled_buffer_1_bit10_out}
  // Probe on {and_39_out[15], bit5_add_one_3_bit5_out, bit10_controlled_buffer_1_bit10_out}

  assign out_16 = in_7[14:10];
  assign out_17 = in_8[14:10];
  assign out_24 = in_11;
  assign out_27 = in_12;

  // Notes on the sheet:
  //   snan
  //   qnan
  //   infinity
  //   zero
  //   snan
  //   qnan
  //   infinity
  //   zero
  //   sorts of nan!
  //   infinities
endmodule

module Bit4_Toggle_TwsCmplmtr (
  input  [3:0] Bit4_Input,
  input  Enable_Twos,
  output [3:0] Bit4_Result
);

  wire and_1_out, and_2_out, and_3_out, or_1_out, or_2_out;

  or or_1 (or_1_out, Bit4_Input[0], Bit4_Result[1]);
  or or_2 (or_2_out, Bit4_Input[0], Bit4_Result[1], Bit4_Result[2]);
  xor xor_1 (Bit4_Result[1], Bit4_Input[1], and_1_out);
  and and_1 (and_1_out, Enable_Twos, Bit4_Input[0]);
  xor xor_2 (Bit4_Result[2], Bit4_Input[2], and_2_out);
  and and_2 (and_2_out, Enable_Twos, or_1_out);
  xor xor_3 (Bit4_Result[3], Bit4_Input[3], and_3_out);
  and and_3 (and_3_out, Enable_Twos, or_2_out);

  assign Bit4_Result[0] = Bit4_Input[0];
endmodule

module Bit5_Toggle_TwsCmplmtr (
  input  [4:0] Bit5_Input,
  input  Enable_Twos,
  output [4:0] Bit5_Result
);

  wire and_1_out, and_2_out, and_3_out, and_4_out, or_1_out, or_2_out, or_3_out;

  or or_1 (or_1_out, Bit5_Input[0], Bit5_Result[1]);
  or or_2 (or_2_out, Bit5_Input[0], Bit5_Result[1], Bit5_Result[2]);
  or or_3 (or_3_out, Bit5_Result[3], Bit5_Result[2], Bit5_Result[1], Bit5_Input[0]);
  xor xor_1 (Bit5_Result[1], Bit5_Input[1], and_1_out);
  and and_1 (and_1_out, Enable_Twos, Bit5_Input[0]);
  xor xor_2 (Bit5_Result[2], Bit5_Input[2], and_2_out);
  and and_2 (and_2_out, Enable_Twos, or_1_out);
  xor xor_3 (Bit5_Result[3], Bit5_Input[3], and_3_out);
  and and_3 (and_3_out, Enable_Twos, or_2_out);
  and and_4 (and_4_out, Enable_Twos, or_3_out);
  xor xor_4 (Bit5_Result[4], Bit5_Input[4], and_4_out);

  assign Bit5_Result[0] = Bit5_Input[0];
endmodule

module Bit24_Toggle_TwsCmplmtr (
  input  Enable,
  input  [23:0] Bit24_In,
  output [23:0] Bit24_Out
);

  wire and_1_out, and_2_out, and_3_out, and_4_out, and_5_out, and_6_out, and_7_out, and_8_out, and_9_out,
       and_10_out, and_11_out, and_12_out, and_13_out, and_14_out, and_15_out, and_16_out, and_17_out,
       and_18_out, and_19_out, and_20_out, and_21_out, and_22_out, and_23_out, or_1_out, or_2_out, or_3_out,
       or_4_out, or_5_out, or_6_out, or_7_out, or_8_out, or_9_out, or_10_out, or_11_out, or_12_out,
       or_13_out, or_14_out, or_15_out, or_16_out, or_17_out, or_18_out, or_19_out, or_20_out, or_21_out,
       or_22_out;

  or or_1 (or_1_out, Bit24_In[0], Bit24_Out[1]);
  or or_2 (or_2_out, Bit24_In[0], Bit24_Out[1], Bit24_Out[2]);
  or or_3 (or_3_out, Bit24_In[0], Bit24_Out[1], Bit24_Out[2], Bit24_Out[3]);
  or or_4 (or_4_out, Bit24_In[0], Bit24_Out[1], Bit24_Out[2], Bit24_Out[3], Bit24_Out[4]);
  or or_5 (or_5_out, Bit24_In[0], Bit24_Out[1], Bit24_Out[2], Bit24_Out[3], Bit24_Out[4], Bit24_Out[5]);
  or or_6 (or_6_out, Bit24_In[0], Bit24_Out[1], Bit24_Out[2], Bit24_Out[3], Bit24_Out[4], Bit24_Out[5], Bit24_Out[6]);
  or or_7 (or_7_out, Bit24_In[0], Bit24_Out[1], Bit24_Out[2], Bit24_Out[3], Bit24_Out[4], Bit24_Out[5], Bit24_Out[6], Bit24_Out[7]);
  or or_8 (or_8_out, Bit24_In[0], Bit24_Out[1], Bit24_Out[2], Bit24_Out[3], Bit24_Out[4], Bit24_Out[5], Bit24_Out[6], Bit24_Out[7], Bit24_Out[8]);
  or or_9 (or_9_out, Bit24_In[0], Bit24_Out[1], Bit24_Out[2], Bit24_Out[3], Bit24_Out[4], Bit24_Out[5], Bit24_Out[6], Bit24_Out[7], Bit24_Out[8], Bit24_Out[9]);
  or or_10 (or_10_out, Bit24_In[0], Bit24_Out[1], Bit24_Out[2], Bit24_Out[3], Bit24_Out[4], Bit24_Out[5], Bit24_Out[6], Bit24_Out[7], Bit24_Out[8], Bit24_Out[9], Bit24_Out[10]);
  or or_11 (or_11_out, Bit24_In[0], Bit24_Out[1], Bit24_Out[2], Bit24_Out[3], Bit24_Out[4], Bit24_Out[5], Bit24_Out[6], Bit24_Out[7], Bit24_Out[8], Bit24_Out[9], Bit24_Out[10], Bit24_Out[11]);
  or or_12 (or_12_out, Bit24_In[0], Bit24_Out[1], Bit24_Out[2], Bit24_Out[3], Bit24_Out[4], Bit24_Out[5], Bit24_Out[6], Bit24_Out[7], Bit24_Out[8], Bit24_Out[9], Bit24_Out[10], Bit24_Out[11], Bit24_Out[12]);
  or or_13 (or_13_out, Bit24_In[0], Bit24_Out[1], Bit24_Out[2], Bit24_Out[3], Bit24_Out[4], Bit24_Out[5], Bit24_Out[6], Bit24_Out[7], Bit24_Out[8], Bit24_Out[9], Bit24_Out[10], Bit24_Out[11], Bit24_Out[12], Bit24_Out[13]);
  or or_14 (or_14_out, Bit24_In[0], Bit24_Out[1], Bit24_Out[2], Bit24_Out[3], Bit24_Out[4], Bit24_Out[5], Bit24_Out[6], Bit24_Out[7], Bit24_Out[8], Bit24_Out[9], Bit24_Out[10], Bit24_Out[11], Bit24_Out[12], Bit24_Out[13], Bit24_Out[14]);
  or or_15 (or_15_out, Bit24_In[0], Bit24_Out[1], Bit24_Out[2], Bit24_Out[3], Bit24_Out[4], Bit24_Out[5], Bit24_Out[6], Bit24_Out[7], Bit24_Out[8], Bit24_Out[9], Bit24_Out[10], Bit24_Out[11], Bit24_Out[12], Bit24_Out[13], Bit24_Out[14], Bit24_Out[15]);
  or or_16 (or_16_out, Bit24_In[0], Bit24_Out[1], Bit24_Out[2], Bit24_Out[3], Bit24_Out[4], Bit24_Out[5], Bit24_Out[6], Bit24_Out[7], Bit24_Out[8], Bit24_Out[9], Bit24_Out[10], Bit24_Out[11], Bit24_Out[12], Bit24_Out[13], Bit24_Out[14], Bit24_Out[15], Bit24_Out[16]);
  or or_17 (or_17_out, Bit24_In[0], Bit24_Out[1], Bit24_Out[2], Bit24_Out[3], Bit24_Out[4], Bit24_Out[5], Bit24_Out[6], Bit24_Out[7], Bit24_Out[8], Bit24_Out[9], Bit24_Out[10], Bit24_Out[11], Bit24_Out[12], Bit24_Out[13], Bit24_Out[14], Bit24_Out[15], Bit24_Out[16], Bit24_Out[17]);
  or or_18 (or_18_out, Bit24_In[0], Bit24_Out[1], Bit24_Out[2], Bit24_Out[3], Bit24_Out[4], Bit24_Out[5], Bit24_Out[6], Bit24_Out[7], Bit24_Out[8], Bit24_Out[9], Bit24_Out[10], Bit24_Out[11], Bit24_Out[12], Bit24_Out[13], Bit24_Out[14], Bit24_Out[15], Bit24_Out[16], Bit24_Out[17], Bit24_Out[18]);
  or or_19 (or_19_out, Bit24_In[0], Bit24_Out[1], Bit24_Out[2], Bit24_Out[3], Bit24_Out[4], Bit24_Out[5], Bit24_Out[6], Bit24_Out[7], Bit24_Out[8], Bit24_Out[9], Bit24_Out[10], Bit24_Out[11], Bit24_Out[12], Bit24_Out[13], Bit24_Out[14], Bit24_Out[15], Bit24_Out[16], Bit24_Out[17], Bit24_Out[18], Bit24_Out[19]);
  or or_20 (or_20_out, Bit24_In[0], Bit24_Out[1], Bit24_Out[2], Bit24_Out[3], Bit24_Out[4], Bit24_Out[5], Bit24_Out[6], Bit24_Out[7], Bit24_Out[8], Bit24_Out[9], Bit24_Out[10], Bit24_Out[11], Bit24_Out[12], Bit24_Out[13], Bit24_Out[14], Bit24_Out[15], Bit24_Out[16], Bit24_Out[17], Bit24_Out[18], Bit24_Out[19], Bit24_Out[20]);
  or or_21 (or_21_out, Bit24_In[0], Bit24_Out[1], Bit24_Out[2], Bit24_Out[3], Bit24_Out[4], Bit24_Out[5], Bit24_Out[6], Bit24_Out[7], Bit24_Out[8], Bit24_Out[9], Bit24_Out[10], Bit24_Out[11], Bit24_Out[12], Bit24_Out[13], Bit24_Out[14], Bit24_Out[15], Bit24_Out[16], Bit24_Out[17], Bit24_Out[18], Bit24_Out[19], Bit24_Out[20], Bit24_Out[21]);
  or or_22 (or_22_out, Bit24_In[0], Bit24_Out[1], Bit24_Out[2], Bit24_Out[3], Bit24_Out[4], Bit24_Out[5], Bit24_Out[6], Bit24_Out[7], Bit24_Out[8], Bit24_Out[9], Bit24_Out[10], Bit24_Out[11], Bit24_Out[12], Bit24_Out[13], Bit24_Out[14], Bit24_Out[15], Bit24_Out[16], Bit24_Out[17], Bit24_Out[18], Bit24_Out[19], Bit24_Out[20], Bit24_Out[21], Bit24_Out[22]);
  xor xor_1 (Bit24_Out[1], Bit24_In[1], and_1_out);
  and and_1 (and_1_out, Bit24_In[0], Enable);
  xor xor_2 (Bit24_Out[2], Bit24_In[2], and_2_out);
  and and_2 (and_2_out, or_1_out, Enable);
  xor xor_3 (Bit24_Out[3], Bit24_In[3], and_3_out);
  and and_3 (and_3_out, or_2_out, Enable);
  xor xor_4 (Bit24_Out[4], Bit24_In[4], and_4_out);
  and and_4 (and_4_out, Enable, or_3_out);
  xor xor_5 (Bit24_Out[5], Bit24_In[5], and_5_out);
  and and_5 (and_5_out, Enable, or_4_out);
  xor xor_6 (Bit24_Out[6], Bit24_In[6], and_6_out);
  and and_6 (and_6_out, Enable, or_5_out);
  xor xor_7 (Bit24_Out[7], Bit24_In[7], and_7_out);
  and and_7 (and_7_out, Enable, or_6_out);
  xor xor_8 (Bit24_Out[8], Bit24_In[8], and_8_out);
  and and_8 (and_8_out, Enable, or_7_out);
  xor xor_9 (Bit24_Out[9], Bit24_In[9], and_9_out);
  and and_9 (and_9_out, Enable, or_8_out);
  xor xor_10 (Bit24_Out[10], Bit24_In[10], and_10_out);
  and and_10 (and_10_out, Enable, or_9_out);
  xor xor_11 (Bit24_Out[11], Bit24_In[11], and_11_out);
  and and_11 (and_11_out, Enable, or_10_out);
  xor xor_12 (Bit24_Out[12], Bit24_In[12], and_12_out);
  and and_12 (and_12_out, Enable, or_11_out);
  xor xor_13 (Bit24_Out[13], Bit24_In[13], and_13_out);
  and and_13 (and_13_out, Enable, or_12_out);
  xor xor_14 (Bit24_Out[14], Bit24_In[14], and_14_out);
  and and_14 (and_14_out, Enable, or_13_out);
  xor xor_15 (Bit24_Out[15], Bit24_In[15], and_15_out);
  and and_15 (and_15_out, Enable, or_14_out);
  xor xor_16 (Bit24_Out[16], Bit24_In[16], and_16_out);
  and and_16 (and_16_out, Enable, or_15_out);
  xor xor_17 (Bit24_Out[17], Bit24_In[17], and_17_out);
  and and_17 (and_17_out, Enable, or_16_out);
  xor xor_18 (Bit24_Out[18], Bit24_In[18], and_18_out);
  and and_18 (and_18_out, Enable, or_17_out);
  xor xor_19 (Bit24_Out[19], Bit24_In[19], and_19_out);
  and and_19 (and_19_out, Enable, or_18_out);
  xor xor_20 (Bit24_Out[20], Bit24_In[20], and_20_out);
  and and_20 (and_20_out, Enable, or_19_out);
  xor xor_21 (Bit24_Out[21], Bit24_In[21], and_21_out);
  and and_21 (and_21_out, Enable, or_20_out);
  xor xor_22 (Bit24_Out[22], Bit24_In[22], and_22_out);
  and and_22 (and_22_out, Enable, or_21_out);
  xor xor_23 (Bit24_Out[23], Bit24_In[23], and_23_out);
  and and_23 (and_23_out, Enable, or_22_out);

  assign Bit24_Out[0] = Bit24_In[0];
endmodule

module Bit24_Inverter (
  input  [23:0] Bit24_In,
  output [23:0] Bit24_Out
);

  not not_1 (Bit24_Out[0], Bit24_In[0]);
  not not_2 (Bit24_Out[1], Bit24_In[1]);
  not not_3 (Bit24_Out[2], Bit24_In[2]);
  not not_4 (Bit24_Out[3], Bit24_In[3]);
  not not_5 (Bit24_Out[4], Bit24_In[4]);
  not not_6 (Bit24_Out[5], Bit24_In[5]);
  not not_7 (Bit24_Out[6], Bit24_In[6]);
  not not_8 (Bit24_Out[7], Bit24_In[7]);
  not not_9 (Bit24_Out[8], Bit24_In[8]);
  not not_10 (Bit24_Out[9], Bit24_In[9]);
  not not_11 (Bit24_Out[10], Bit24_In[10]);
  not not_12 (Bit24_Out[11], Bit24_In[11]);
  not not_13 (Bit24_Out[12], Bit24_In[12]);
  not not_14 (Bit24_Out[13], Bit24_In[13]);
  not not_15 (Bit24_Out[14], Bit24_In[14]);
  not not_16 (Bit24_Out[15], Bit24_In[15]);
  not not_17 (Bit24_Out[16], Bit24_In[16]);
  not not_18 (Bit24_Out[17], Bit24_In[17]);
  not not_19 (Bit24_Out[18], Bit24_In[18]);
  not not_20 (Bit24_Out[19], Bit24_In[19]);
  not not_21 (Bit24_Out[20], Bit24_In[20]);
  not not_22 (Bit24_Out[21], Bit24_In[21]);
  not not_23 (Bit24_Out[22], Bit24_In[22]);
  not not_24 (Bit24_Out[23], Bit24_In[23]);
endmodule

module Bit4_Inverter (
  input  [3:0] Bit4_In,
  output [3:0] Bit4_Out
);

  not not_1 (Bit4_Out[0], Bit4_In[0]);
  not not_2 (Bit4_Out[1], Bit4_In[1]);
  not not_3 (Bit4_Out[2], Bit4_In[2]);
  not not_4 (Bit4_Out[3], Bit4_In[3]);
endmodule

module Bit5_Inverter (
  input  [4:0] Bit5_In,
  output [4:0] Bit5_Out
);

  not not_1 (Bit5_Out[0], Bit5_In[0]);
  not not_2 (Bit5_Out[1], Bit5_In[1]);
  not not_3 (Bit5_Out[2], Bit5_In[2]);
  not not_4 (Bit5_Out[3], Bit5_In[3]);
  not not_5 (Bit5_Out[4], Bit5_In[4]);
endmodule

module Bit11_To_Bit16_High (
  input  [10:0] Bit11_In,
  output [15:0] Bit16_Out
);


  assign Bit16_Out = {Bit11_In, {5{1'b0}}};
endmodule

module Bit11_Controlled_Buffer (
  input  Enable,
  input  [10:0] Bit11_In,
  output [10:0] Bit11_Out
);

  and and_1 (Bit11_Out[0], Bit11_In[0], Enable);
  and and_2 (Bit11_Out[1], Bit11_In[1], Enable);
  and and_3 (Bit11_Out[2], Bit11_In[2], Enable);
  and and_4 (Bit11_Out[3], Bit11_In[3], Enable);
  and and_5 (Bit11_Out[4], Bit11_In[4], Enable);
  and and_6 (Bit11_Out[5], Bit11_In[5], Enable);
  and and_7 (Bit11_Out[6], Bit11_In[6], Enable);
  and and_8 (Bit11_Out[7], Bit11_In[7], Enable);
  and and_9 (Bit11_Out[8], Bit11_In[8], Enable);
  and and_10 (Bit11_Out[9], Bit11_In[9], Enable);
  and and_11 (Bit11_Out[10], Bit11_In[10], Enable);
endmodule

module Bit32_Left_Shift (
  input  [31:0] Bit32_In,
  input  [4:0] Bit5_Shift,
  output [31:0] Bit32_Result
);

  wire and_2_out, and_3_out, and_4_out, and_5_out, and_6_out, and_7_out, and_8_out, and_9_out, and_10_out,
       and_11_out, and_12_out, and_13_out, and_14_out, and_15_out, and_16_out, and_17_out, and_18_out,
       and_19_out, and_20_out, and_21_out, and_22_out, and_23_out, and_24_out, and_25_out, and_26_out,
       and_27_out, and_28_out, and_29_out, and_30_out, and_31_out, and_32_out, and_33_out, and_34_out,
       and_35_out, and_36_out, and_37_out, and_38_out, and_39_out, and_40_out, and_41_out, and_42_out,
       and_43_out, and_44_out, and_45_out, and_46_out, and_47_out, and_48_out, and_49_out, and_50_out,
       and_51_out, and_52_out, and_53_out, and_54_out, and_55_out, and_56_out, and_57_out, and_58_out,
       and_59_out, and_60_out, and_61_out, and_62_out, and_63_out, and_64_out, and_65_out, and_66_out,
       and_67_out, and_68_out, and_69_out, and_70_out, and_71_out, and_72_out, and_73_out, and_74_out,
       and_75_out, and_76_out, and_77_out, and_78_out, and_79_out, and_80_out, and_81_out, and_82_out,
       and_83_out, and_84_out, and_85_out, and_86_out, and_87_out, and_88_out, and_89_out, and_90_out,
       and_91_out, and_92_out, and_93_out, and_94_out, and_95_out, and_96_out, and_97_out, and_98_out,
       and_99_out, and_100_out, and_101_out, and_102_out, and_103_out, and_104_out, and_105_out, and_106_out,
       and_107_out, and_108_out, and_109_out, and_110_out, and_111_out, and_112_out, and_113_out,
       and_114_out, and_115_out, and_116_out, and_117_out, and_118_out, and_119_out, and_120_out,
       and_121_out, and_122_out, and_123_out, and_124_out, and_125_out, and_126_out, and_127_out,
       and_128_out, and_129_out, and_130_out, and_131_out, and_132_out, and_133_out, and_134_out,
       and_135_out, and_136_out, and_137_out, and_138_out, and_139_out, and_140_out, and_141_out,
       and_143_out, and_144_out, and_145_out, and_146_out, and_147_out, and_148_out, and_149_out,
       and_150_out, and_152_out, and_153_out, and_154_out, and_155_out, and_156_out, and_157_out,
       and_158_out, and_159_out, and_161_out, and_162_out, and_163_out, and_164_out, and_165_out,
       and_166_out, and_167_out, and_168_out, and_169_out, and_171_out, and_172_out, and_173_out,
       and_174_out, and_175_out, and_176_out, and_177_out, and_178_out, and_180_out, and_181_out,
       and_182_out, and_183_out, and_184_out, and_185_out, and_186_out, and_187_out, and_189_out,
       and_190_out, and_191_out, and_192_out, and_193_out, and_194_out, and_195_out, and_196_out,
       and_198_out, and_199_out, and_200_out, and_201_out, and_202_out, and_203_out, and_204_out,
       and_205_out, and_207_out, and_208_out, and_209_out, and_210_out, and_211_out, and_212_out,
       and_213_out, and_214_out, and_215_out, and_216_out, and_217_out, and_218_out, and_219_out,
       and_220_out, and_221_out, and_223_out, and_224_out, and_225_out, and_226_out, and_227_out,
       and_228_out, and_229_out, and_230_out, and_232_out, and_233_out, and_234_out, and_235_out,
       and_236_out, and_237_out, and_238_out, and_239_out, and_241_out, and_242_out, and_243_out,
       and_244_out, and_245_out, and_246_out, and_247_out, and_248_out, and_249_out, and_251_out,
       and_252_out, and_253_out, and_254_out, and_255_out, and_256_out, and_257_out, and_258_out,
       and_260_out, and_261_out, and_262_out, and_263_out, and_264_out, and_265_out, and_266_out,
       and_267_out, and_269_out, and_270_out, and_271_out, and_272_out, and_273_out, and_274_out,
       and_275_out, and_276_out, and_278_out, and_279_out, and_280_out, and_281_out, and_282_out,
       and_283_out, and_284_out, and_285_out, and_287_out, and_288_out, and_289_out, and_290_out, or_1_out,
       or_2_out, or_3_out, or_4_out, or_6_out, or_7_out, or_8_out, or_9_out, or_11_out, or_12_out, or_13_out,
       or_14_out, or_16_out, or_17_out, or_18_out, or_20_out, or_21_out, or_22_out, or_24_out, or_25_out,
       or_26_out, or_28_out, or_29_out, or_30_out, or_32_out, or_33_out, or_34_out, or_35_out, or_36_out,
       or_37_out, or_38_out, or_39_out, or_41_out, or_42_out, or_43_out, or_44_out, or_46_out, or_47_out,
       or_48_out, or_49_out, or_51_out, or_52_out, or_53_out, or_54_out, or_56_out, or_57_out, or_58_out,
       or_60_out, or_61_out, or_62_out, or_64_out, or_65_out, or_66_out, or_68_out, or_69_out, or_70_out,
       or_72_out, or_73_out, or_74_out, or_75_out, or_76_out, or_77_out, or_78_out, or_79_out, or_81_out,
       or_82_out, or_83_out, or_84_out, or_85_out, or_86_out, or_87_out, or_88_out, or_89_out, or_90_out,
       or_91_out, or_92_out, or_93_out, or_94_out, or_95_out, or_96_out, or_97_out, or_98_out, or_99_out,
       or_100_out, or_101_out, or_102_out, or_103_out, or_104_out, or_105_out, or_106_out, or_107_out,
       or_108_out, or_109_out, or_110_out, or_111_out, or_112_out, or_113_out, or_114_out, or_115_out,
       or_116_out, or_117_out, or_118_out, or_119_out, or_120_out, or_121_out, or_122_out, or_123_out,
       or_124_out, or_125_out, or_126_out, or_127_out, or_128_out, or_129_out;

  // AND_Gate and_1 has open pins: in0=Bit5_Shift[0], in1=Bit32_In[31], out=open
  and and_2 (and_2_out, ~Bit5_Shift[0], Bit32_In[31]);  // AND_Gate
  or or_1 (or_1_out, and_2_out, and_7_out);
  and and_3 (and_3_out, ~Bit5_Shift[1], or_1_out);  // AND_Gate
  or or_2 (or_2_out, and_3_out, and_15_out);
  and and_4 (and_4_out, ~Bit5_Shift[2], or_2_out);  // AND_Gate
  or or_3 (or_3_out, and_4_out, and_30_out);
  and and_5 (and_5_out, ~Bit5_Shift[3], or_3_out);  // AND_Gate
  or or_4 (or_4_out, and_5_out, and_61_out);
  and and_6 (and_6_out, ~Bit5_Shift[4], or_4_out);  // AND_Gate
  or or_5 (Bit32_Result[31], and_6_out, and_134_out);
  and and_7 (and_7_out, Bit5_Shift[0], Bit32_In[30]);
  and and_8 (and_8_out, ~Bit5_Shift[0], Bit32_In[30]);  // AND_Gate
  or or_6 (or_6_out, and_8_out, and_13_out);
  and and_9 (and_9_out, ~Bit5_Shift[1], or_6_out);  // AND_Gate
  or or_7 (or_7_out, and_9_out, and_22_out);
  and and_10 (and_10_out, ~Bit5_Shift[2], or_7_out);  // AND_Gate
  or or_8 (or_8_out, and_10_out, and_37_out);
  and and_11 (and_11_out, ~Bit5_Shift[3], or_8_out);  // AND_Gate
  or or_9 (or_9_out, and_11_out, and_68_out);
  and and_12 (and_12_out, ~Bit5_Shift[4], or_9_out);  // AND_Gate
  or or_10 (Bit32_Result[30], and_12_out, and_143_out);
  and and_13 (and_13_out, Bit5_Shift[0], Bit32_In[29]);
  and and_14 (and_14_out, ~Bit5_Shift[0], Bit32_In[29]);  // AND_Gate
  or or_11 (or_11_out, and_14_out, and_20_out);
  and and_15 (and_15_out, Bit5_Shift[1], or_11_out);
  and and_16 (and_16_out, ~Bit5_Shift[1], or_11_out);  // AND_Gate
  or or_12 (or_12_out, and_16_out, and_28_out);
  and and_17 (and_17_out, ~Bit5_Shift[2], or_12_out);  // AND_Gate
  or or_13 (or_13_out, and_17_out, and_45_out);
  and and_18 (and_18_out, ~Bit5_Shift[3], or_13_out);  // AND_Gate
  or or_14 (or_14_out, and_18_out, and_76_out);
  and and_19 (and_19_out, ~Bit5_Shift[4], or_14_out);  // AND_Gate
  or or_15 (Bit32_Result[29], and_19_out, and_152_out);
  and and_20 (and_20_out, Bit5_Shift[0], Bit32_In[28]);
  and and_21 (and_21_out, ~Bit5_Shift[0], Bit32_In[28]);  // AND_Gate
  and and_22 (and_22_out, Bit5_Shift[1], or_20_out);
  and and_23 (and_23_out, ~Bit5_Shift[1], or_20_out);  // AND_Gate
  or or_16 (or_16_out, and_23_out, and_36_out);
  and and_24 (and_24_out, ~Bit5_Shift[2], or_16_out);  // AND_Gate
  or or_17 (or_17_out, and_24_out, and_52_out);
  and and_25 (and_25_out, ~Bit5_Shift[3], or_17_out);  // AND_Gate
  or or_18 (or_18_out, and_25_out, and_92_out);
  and and_26 (and_26_out, ~Bit5_Shift[4], or_18_out);  // AND_Gate
  or or_19 (Bit32_Result[28], and_26_out, and_161_out);
  and and_27 (and_27_out, Bit5_Shift[0], Bit32_In[27]);
  or or_20 (or_20_out, and_21_out, and_27_out);
  and and_28 (and_28_out, Bit5_Shift[1], or_24_out);
  and and_29 (and_29_out, ~Bit5_Shift[1], or_24_out);  // AND_Gate
  and and_30 (and_30_out, Bit5_Shift[2], or_25_out);
  and and_31 (and_31_out, ~Bit5_Shift[2], or_25_out);  // AND_Gate
  or or_21 (or_21_out, and_31_out, and_59_out);
  and and_32 (and_32_out, ~Bit5_Shift[3], or_21_out);  // AND_Gate
  or or_22 (or_22_out, and_32_out, and_100_out);
  and and_33 (and_33_out, ~Bit5_Shift[4], or_22_out);  // AND_Gate
  or or_23 (Bit32_Result[27], and_33_out, and_178_out);
  and and_34 (and_34_out, ~Bit5_Shift[0], Bit32_In[27]);  // AND_Gate
  and and_35 (and_35_out, Bit5_Shift[0], Bit32_In[26]);
  or or_24 (or_24_out, and_34_out, and_35_out);
  and and_36 (and_36_out, Bit5_Shift[1], or_28_out);
  or or_25 (or_25_out, and_29_out, and_44_out);
  and and_37 (and_37_out, Bit5_Shift[2], or_29_out);
  and and_38 (and_38_out, ~Bit5_Shift[2], or_29_out);  // AND_Gate
  and and_39 (and_39_out, ~Bit5_Shift[3], or_30_out);  // AND_Gate
  or or_26 (or_26_out, and_39_out, and_108_out);
  and and_40 (and_40_out, ~Bit5_Shift[4], or_26_out);  // AND_Gate
  or or_27 (Bit32_Result[26], and_40_out, and_187_out);
  and and_41 (and_41_out, ~Bit5_Shift[0], Bit32_In[26]);  // AND_Gate
  and and_42 (and_42_out, Bit5_Shift[0], Bit32_In[25]);
  or or_28 (or_28_out, and_41_out, and_42_out);
  and and_43 (and_43_out, ~Bit5_Shift[1], or_28_out);  // AND_Gate
  and and_44 (and_44_out, Bit5_Shift[1], or_32_out);
  or or_29 (or_29_out, and_43_out, and_50_out);
  and and_45 (and_45_out, Bit5_Shift[2], or_33_out);
  or or_30 (or_30_out, and_38_out, and_66_out);
  and and_46 (and_46_out, ~Bit5_Shift[3], or_34_out);  // AND_Gate
  and and_47 (and_47_out, ~Bit5_Shift[4], or_35_out);  // AND_Gate
  or or_31 (Bit32_Result[25], and_47_out, and_196_out);
  and and_48 (and_48_out, Bit5_Shift[0], Bit32_In[24]);
  and and_49 (and_49_out, ~Bit5_Shift[0], Bit32_In[25]);  // AND_Gate
  or or_32 (or_32_out, and_49_out, and_48_out);
  and and_50 (and_50_out, Bit5_Shift[1], or_36_out);
  and and_51 (and_51_out, ~Bit5_Shift[1], or_32_out);  // AND_Gate
  or or_33 (or_33_out, and_51_out, and_57_out);
  and and_52 (and_52_out, Bit5_Shift[2], or_37_out);
  and and_53 (and_53_out, ~Bit5_Shift[2], or_33_out);  // AND_Gate
  or or_34 (or_34_out, and_53_out, and_82_out);
  or or_35 (or_35_out, and_46_out, and_116_out);
  and and_54 (and_54_out, ~Bit5_Shift[4], or_39_out);  // AND_Gate
  and and_55 (and_55_out, ~Bit5_Shift[0], Bit32_In[24]);  // AND_Gate
  or or_36 (or_36_out, and_55_out, and_62_out);
  and and_56 (and_56_out, ~Bit5_Shift[1], or_36_out);  // AND_Gate
  and and_57 (and_57_out, Bit5_Shift[1], or_41_out);
  or or_37 (or_37_out, and_56_out, and_72_out);
  and and_58 (and_58_out, ~Bit5_Shift[2], or_37_out);  // AND_Gate
  and and_59 (and_59_out, Bit5_Shift[2], or_42_out);
  or or_38 (or_38_out, and_58_out, and_90_out);
  and and_60 (and_60_out, ~Bit5_Shift[3], or_38_out);  // AND_Gate
  and and_61 (and_61_out, Bit5_Shift[3], or_43_out);
  or or_39 (or_39_out, and_60_out, and_125_out);
  or or_40 (Bit32_Result[24], and_54_out, and_205_out);
  and and_62 (and_62_out, Bit5_Shift[0], Bit32_In[23]);
  and and_63 (and_63_out, ~Bit5_Shift[0], Bit32_In[23]);  // AND_Gate
  or or_41 (or_41_out, and_63_out, and_70_out);
  and and_64 (and_64_out, ~Bit5_Shift[1], or_41_out);  // AND_Gate
  or or_42 (or_42_out, and_64_out, and_80_out);
  and and_65 (and_65_out, ~Bit5_Shift[2], or_42_out);  // AND_Gate
  and and_66 (and_66_out, Bit5_Shift[2], or_47_out);
  or or_43 (or_43_out, and_65_out, and_98_out);
  and and_67 (and_67_out, ~Bit5_Shift[3], or_43_out);  // AND_Gate
  and and_68 (and_68_out, Bit5_Shift[3], or_48_out);
  or or_44 (or_44_out, and_67_out, and_133_out);
  and and_69 (and_69_out, ~Bit5_Shift[4], or_44_out);  // AND_Gate
  or or_45 (Bit32_Result[23], and_69_out, and_214_out);
  and and_70 (and_70_out, Bit5_Shift[0], Bit32_In[22]);
  and and_71 (and_71_out, ~Bit5_Shift[0], Bit32_In[22]);  // AND_Gate
  or or_46 (or_46_out, and_71_out, and_78_out);
  and and_72 (and_72_out, Bit5_Shift[1], or_46_out);
  and and_73 (and_73_out, ~Bit5_Shift[1], or_46_out);  // AND_Gate
  or or_47 (or_47_out, and_73_out, and_88_out);
  and and_74 (and_74_out, ~Bit5_Shift[2], or_47_out);  // AND_Gate
  or or_48 (or_48_out, and_74_out, and_106_out);
  and and_75 (and_75_out, ~Bit5_Shift[3], or_48_out);  // AND_Gate
  and and_76 (and_76_out, Bit5_Shift[3], or_53_out);
  or or_49 (or_49_out, and_75_out, and_141_out);
  and and_77 (and_77_out, ~Bit5_Shift[4], or_49_out);  // AND_Gate
  or or_50 (Bit32_Result[22], and_77_out, and_223_out);
  and and_78 (and_78_out, Bit5_Shift[0], Bit32_In[21]);
  and and_79 (and_79_out, ~Bit5_Shift[0], Bit32_In[21]);  // AND_Gate
  or or_51 (or_51_out, and_79_out, and_86_out);
  and and_80 (and_80_out, Bit5_Shift[1], or_51_out);
  and and_81 (and_81_out, ~Bit5_Shift[1], or_51_out);  // AND_Gate
  or or_52 (or_52_out, and_81_out, and_96_out);
  and and_82 (and_82_out, Bit5_Shift[2], or_52_out);
  and and_83 (and_83_out, ~Bit5_Shift[2], or_52_out);  // AND_Gate
  or or_53 (or_53_out, and_83_out, and_115_out);
  and and_84 (and_84_out, ~Bit5_Shift[3], or_53_out);  // AND_Gate
  or or_54 (or_54_out, and_84_out, and_150_out);
  and and_85 (and_85_out, ~Bit5_Shift[4], or_54_out);  // AND_Gate
  or or_55 (Bit32_Result[21], and_85_out, and_232_out);
  and and_86 (and_86_out, Bit5_Shift[0], Bit32_In[20]);
  and and_87 (and_87_out, ~Bit5_Shift[0], Bit32_In[20]);  // AND_Gate
  and and_88 (and_88_out, Bit5_Shift[1], or_60_out);
  and and_89 (and_89_out, ~Bit5_Shift[1], or_60_out);  // AND_Gate
  or or_56 (or_56_out, and_89_out, and_105_out);
  and and_90 (and_90_out, Bit5_Shift[2], or_56_out);
  and and_91 (and_91_out, ~Bit5_Shift[2], or_56_out);  // AND_Gate
  or or_57 (or_57_out, and_91_out, and_124_out);
  and and_92 (and_92_out, Bit5_Shift[3], or_57_out);
  and and_93 (and_93_out, ~Bit5_Shift[3], or_57_out);  // AND_Gate
  or or_58 (or_58_out, and_93_out, and_168_out);
  and and_94 (and_94_out, ~Bit5_Shift[4], or_58_out);  // AND_Gate
  or or_59 (Bit32_Result[20], and_94_out, and_241_out);
  and and_95 (and_95_out, Bit5_Shift[0], Bit32_In[19]);
  or or_60 (or_60_out, and_87_out, and_95_out);
  and and_96 (and_96_out, Bit5_Shift[1], or_64_out);
  and and_97 (and_97_out, ~Bit5_Shift[1], or_64_out);  // AND_Gate
  and and_98 (and_98_out, Bit5_Shift[2], or_65_out);
  and and_99 (and_99_out, ~Bit5_Shift[2], or_65_out);  // AND_Gate
  or or_61 (or_61_out, and_99_out, and_131_out);
  and and_100 (and_100_out, Bit5_Shift[3], or_61_out);
  and and_101 (and_101_out, ~Bit5_Shift[3], or_61_out);  // AND_Gate
  or or_62 (or_62_out, and_101_out, and_176_out);
  and and_102 (and_102_out, ~Bit5_Shift[4], or_62_out);  // AND_Gate
  or or_63 (Bit32_Result[19], and_102_out, and_258_out);
  and and_103 (and_103_out, ~Bit5_Shift[0], Bit32_In[19]);  // AND_Gate
  and and_104 (and_104_out, Bit5_Shift[0], Bit32_In[18]);
  or or_64 (or_64_out, and_103_out, and_104_out);
  and and_105 (and_105_out, Bit5_Shift[1], or_68_out);
  or or_65 (or_65_out, and_97_out, and_114_out);
  and and_106 (and_106_out, Bit5_Shift[2], or_69_out);
  and and_107 (and_107_out, ~Bit5_Shift[2], or_69_out);  // AND_Gate
  and and_108 (and_108_out, Bit5_Shift[3], or_70_out);
  and and_109 (and_109_out, ~Bit5_Shift[3], or_70_out);  // AND_Gate
  or or_66 (or_66_out, and_109_out, and_185_out);
  and and_110 (and_110_out, ~Bit5_Shift[4], or_66_out);  // AND_Gate
  or or_67 (Bit32_Result[18], and_110_out, and_267_out);
  and and_111 (and_111_out, ~Bit5_Shift[0], Bit32_In[18]);  // AND_Gate
  and and_112 (and_112_out, Bit5_Shift[0], Bit32_In[17]);
  or or_68 (or_68_out, and_111_out, and_112_out);
  and and_113 (and_113_out, ~Bit5_Shift[1], or_68_out);  // AND_Gate
  and and_114 (and_114_out, Bit5_Shift[1], or_72_out);
  or or_69 (or_69_out, and_113_out, and_122_out);
  and and_115 (and_115_out, Bit5_Shift[2], or_73_out);
  or or_70 (or_70_out, and_107_out, and_139_out);
  and and_116 (and_116_out, Bit5_Shift[3], or_74_out);
  and and_117 (and_117_out, ~Bit5_Shift[3], or_74_out);  // AND_Gate
  and and_118 (and_118_out, ~Bit5_Shift[4], or_75_out);  // AND_Gate
  or or_71 (Bit32_Result[17], and_118_out, and_276_out);
  and and_119 (and_119_out, ~Bit5_Shift[0], Bit32_In[17]);  // AND_Gate
  and and_120 (and_120_out, Bit5_Shift[0], Bit32_In[16]);
  or or_72 (or_72_out, and_119_out, and_120_out);
  and and_121 (and_121_out, ~Bit5_Shift[1], or_72_out);  // AND_Gate
  and and_122 (and_122_out, Bit5_Shift[1], or_76_out);
  or or_73 (or_73_out, and_121_out, and_129_out);
  and and_123 (and_123_out, ~Bit5_Shift[2], or_73_out);  // AND_Gate
  and and_124 (and_124_out, Bit5_Shift[2], or_77_out);
  or or_74 (or_74_out, and_123_out, and_157_out);
  and and_125 (and_125_out, Bit5_Shift[3], or_78_out);
  or or_75 (or_75_out, and_117_out, and_194_out);
  and and_126 (and_126_out, ~Bit5_Shift[4], or_79_out);  // AND_Gate
  and and_127 (and_127_out, ~Bit5_Shift[0], Bit32_In[16]);  // AND_Gate
  or or_76 (or_76_out, and_127_out, and_135_out);
  and and_128 (and_128_out, ~Bit5_Shift[1], or_76_out);  // AND_Gate
  and and_129 (and_129_out, Bit5_Shift[1], or_81_out);
  or or_77 (or_77_out, and_128_out, and_146_out);
  and and_130 (and_130_out, ~Bit5_Shift[2], or_77_out);  // AND_Gate
  and and_131 (and_131_out, Bit5_Shift[2], or_82_out);
  or or_78 (or_78_out, and_130_out, and_166_out);
  and and_132 (and_132_out, ~Bit5_Shift[3], or_78_out);  // AND_Gate
  and and_133 (and_133_out, Bit5_Shift[3], or_83_out);
  or or_79 (or_79_out, and_132_out, and_204_out);
  and and_134 (and_134_out, Bit5_Shift[4], or_84_out);
  or or_80 (Bit32_Result[16], and_126_out, and_285_out);
  and and_135 (and_135_out, Bit5_Shift[0], Bit32_In[15]);
  and and_136 (and_136_out, ~Bit5_Shift[0], Bit32_In[15]);  // AND_Gate
  or or_81 (or_81_out, and_136_out, and_144_out);
  and and_137 (and_137_out, ~Bit5_Shift[1], or_81_out);  // AND_Gate
  or or_82 (or_82_out, and_137_out, and_155_out);
  and and_138 (and_138_out, ~Bit5_Shift[2], or_82_out);  // AND_Gate
  and and_139 (and_139_out, Bit5_Shift[2], or_86_out);
  or or_83 (or_83_out, and_138_out, and_174_out);
  and and_140 (and_140_out, ~Bit5_Shift[3], or_83_out);  // AND_Gate
  and and_141 (and_141_out, Bit5_Shift[3], or_87_out);
  or or_84 (or_84_out, and_140_out, and_213_out);
  and and_142 (Bit32_Result[15], ~Bit5_Shift[4], or_84_out);  // AND_Gate
  and and_143 (and_143_out, Bit5_Shift[4], or_88_out);
  and and_144 (and_144_out, Bit5_Shift[0], Bit32_In[14]);
  and and_145 (and_145_out, ~Bit5_Shift[0], Bit32_In[14]);  // AND_Gate
  or or_85 (or_85_out, and_145_out, and_153_out);
  and and_146 (and_146_out, Bit5_Shift[1], or_85_out);
  and and_147 (and_147_out, ~Bit5_Shift[1], or_85_out);  // AND_Gate
  or or_86 (or_86_out, and_147_out, and_164_out);
  and and_148 (and_148_out, ~Bit5_Shift[2], or_86_out);  // AND_Gate
  or or_87 (or_87_out, and_148_out, and_183_out);
  and and_149 (and_149_out, ~Bit5_Shift[3], or_87_out);  // AND_Gate
  and and_150 (and_150_out, Bit5_Shift[3], or_91_out);
  or or_88 (or_88_out, and_149_out, and_221_out);
  and and_151 (Bit32_Result[14], ~Bit5_Shift[4], or_88_out);  // AND_Gate
  and and_152 (and_152_out, Bit5_Shift[4], or_92_out);
  and and_153 (and_153_out, Bit5_Shift[0], Bit32_In[13]);
  and and_154 (and_154_out, ~Bit5_Shift[0], Bit32_In[13]);  // AND_Gate
  or or_89 (or_89_out, and_154_out, and_162_out);
  and and_155 (and_155_out, Bit5_Shift[1], or_89_out);
  and and_156 (and_156_out, ~Bit5_Shift[1], or_89_out);  // AND_Gate
  or or_90 (or_90_out, and_156_out, and_172_out);
  and and_157 (and_157_out, Bit5_Shift[2], or_90_out);
  and and_158 (and_158_out, ~Bit5_Shift[2], or_90_out);  // AND_Gate
  or or_91 (or_91_out, and_158_out, and_193_out);
  and and_159 (and_159_out, ~Bit5_Shift[3], or_91_out);  // AND_Gate
  or or_92 (or_92_out, and_159_out, and_230_out);
  and and_160 (Bit32_Result[13], ~Bit5_Shift[4], or_92_out);  // AND_Gate
  and and_161 (and_161_out, Bit5_Shift[4], or_95_out);
  and and_162 (and_162_out, Bit5_Shift[0], Bit32_In[12]);
  and and_163 (and_163_out, ~Bit5_Shift[0], Bit32_In[12]);  // AND_Gate
  and and_164 (and_164_out, Bit5_Shift[1], or_96_out);
  and and_165 (and_165_out, ~Bit5_Shift[1], or_96_out);  // AND_Gate
  or or_93 (or_93_out, and_165_out, and_182_out);
  and and_166 (and_166_out, Bit5_Shift[2], or_93_out);
  and and_167 (and_167_out, ~Bit5_Shift[2], or_93_out);  // AND_Gate
  or or_94 (or_94_out, and_167_out, and_203_out);
  and and_168 (and_168_out, Bit5_Shift[3], or_94_out);
  and and_169 (and_169_out, ~Bit5_Shift[3], or_94_out);  // AND_Gate
  or or_95 (or_95_out, and_169_out, and_248_out);
  and and_170 (Bit32_Result[12], ~Bit5_Shift[4], or_95_out);  // AND_Gate
  and and_171 (and_171_out, Bit5_Shift[0], Bit32_In[11]);
  or or_96 (or_96_out, and_163_out, and_171_out);
  and and_172 (and_172_out, Bit5_Shift[1], or_99_out);
  and and_173 (and_173_out, ~Bit5_Shift[1], or_99_out);  // AND_Gate
  and and_174 (and_174_out, Bit5_Shift[2], or_100_out);
  and and_175 (and_175_out, ~Bit5_Shift[2], or_100_out);  // AND_Gate
  or or_97 (or_97_out, and_175_out, and_211_out);
  and and_176 (and_176_out, Bit5_Shift[3], or_97_out);
  and and_177 (and_177_out, ~Bit5_Shift[3], or_97_out);  // AND_Gate
  or or_98 (or_98_out, and_177_out, and_256_out);
  and and_178 (and_178_out, Bit5_Shift[4], or_98_out);
  and and_179 (Bit32_Result[11], ~Bit5_Shift[4], or_98_out);  // AND_Gate
  and and_180 (and_180_out, ~Bit5_Shift[0], Bit32_In[11]);  // AND_Gate
  and and_181 (and_181_out, Bit5_Shift[0], Bit32_In[10]);
  or or_99 (or_99_out, and_180_out, and_181_out);
  and and_182 (and_182_out, Bit5_Shift[1], or_102_out);
  or or_100 (or_100_out, and_173_out, and_192_out);
  and and_183 (and_183_out, Bit5_Shift[2], or_103_out);
  and and_184 (and_184_out, ~Bit5_Shift[2], or_103_out);  // AND_Gate
  and and_185 (and_185_out, Bit5_Shift[3], or_104_out);
  and and_186 (and_186_out, ~Bit5_Shift[3], or_104_out);  // AND_Gate
  or or_101 (or_101_out, and_186_out, and_265_out);
  and and_187 (and_187_out, Bit5_Shift[4], or_101_out);
  and and_188 (Bit32_Result[10], ~Bit5_Shift[4], or_101_out);  // AND_Gate
  and and_189 (and_189_out, ~Bit5_Shift[0], Bit32_In[10]);  // AND_Gate
  and and_190 (and_190_out, Bit5_Shift[0], Bit32_In[9]);
  or or_102 (or_102_out, and_189_out, and_190_out);
  and and_191 (and_191_out, ~Bit5_Shift[1], or_102_out);  // AND_Gate
  and and_192 (and_192_out, Bit5_Shift[1], or_105_out);
  or or_103 (or_103_out, and_191_out, and_201_out);
  and and_193 (and_193_out, Bit5_Shift[2], or_106_out);
  or or_104 (or_104_out, and_184_out, and_219_out);
  and and_194 (and_194_out, Bit5_Shift[3], or_107_out);
  and and_195 (and_195_out, ~Bit5_Shift[3], or_107_out);  // AND_Gate
  and and_196 (and_196_out, Bit5_Shift[4], or_108_out);
  and and_197 (Bit32_Result[9], ~Bit5_Shift[4], or_108_out);  // AND_Gate
  and and_198 (and_198_out, ~Bit5_Shift[0], Bit32_In[9]);  // AND_Gate
  and and_199 (and_199_out, Bit5_Shift[0], Bit32_In[8]);
  or or_105 (or_105_out, and_198_out, and_199_out);
  and and_200 (and_200_out, ~Bit5_Shift[1], or_105_out);  // AND_Gate
  and and_201 (and_201_out, Bit5_Shift[1], or_109_out);
  or or_106 (or_106_out, and_200_out, and_209_out);
  and and_202 (and_202_out, ~Bit5_Shift[2], or_106_out);  // AND_Gate
  and and_203 (and_203_out, Bit5_Shift[2], or_110_out);
  or or_107 (or_107_out, and_202_out, and_237_out);
  and and_204 (and_204_out, Bit5_Shift[3], or_111_out);
  or or_108 (or_108_out, and_195_out, and_274_out);
  and and_205 (and_205_out, Bit5_Shift[4], or_112_out);
  and and_206 (Bit32_Result[8], ~Bit5_Shift[4], or_112_out);  // AND_Gate
  and and_207 (and_207_out, ~Bit5_Shift[0], Bit32_In[8]);  // AND_Gate
  or or_109 (or_109_out, and_207_out, and_215_out);
  and and_208 (and_208_out, ~Bit5_Shift[1], or_109_out);  // AND_Gate
  and and_209 (and_209_out, Bit5_Shift[1], or_113_out);
  or or_110 (or_110_out, and_208_out, and_226_out);
  and and_210 (and_210_out, ~Bit5_Shift[2], or_110_out);  // AND_Gate
  and and_211 (and_211_out, Bit5_Shift[2], or_114_out);
  or or_111 (or_111_out, and_210_out, and_246_out);
  and and_212 (and_212_out, ~Bit5_Shift[3], or_111_out);  // AND_Gate
  and and_213 (and_213_out, Bit5_Shift[3], or_115_out);
  or or_112 (or_112_out, and_212_out, and_284_out);
  and and_214 (and_214_out, Bit5_Shift[4], and_220_out);
  and and_215 (and_215_out, Bit5_Shift[0], Bit32_In[7]);
  and and_216 (and_216_out, ~Bit5_Shift[0], Bit32_In[7]);  // AND_Gate
  or or_113 (or_113_out, and_216_out, and_224_out);
  and and_217 (and_217_out, ~Bit5_Shift[1], or_113_out);  // AND_Gate
  or or_114 (or_114_out, and_217_out, and_235_out);
  and and_218 (and_218_out, ~Bit5_Shift[2], or_114_out);  // AND_Gate
  and and_219 (and_219_out, Bit5_Shift[2], or_117_out);
  or or_115 (or_115_out, and_218_out, and_254_out);
  and and_220 (and_220_out, ~Bit5_Shift[3], or_115_out);  // AND_Gate
  and and_221 (and_221_out, Bit5_Shift[3], or_118_out);
  and and_222 (Bit32_Result[7], ~Bit5_Shift[4], and_220_out);  // AND_Gate
  and and_223 (and_223_out, Bit5_Shift[4], and_229_out);
  and and_224 (and_224_out, Bit5_Shift[0], Bit32_In[6]);
  and and_225 (and_225_out, ~Bit5_Shift[0], Bit32_In[6]);  // AND_Gate
  or or_116 (or_116_out, and_225_out, and_233_out);
  and and_226 (and_226_out, Bit5_Shift[1], or_116_out);
  and and_227 (and_227_out, ~Bit5_Shift[1], or_116_out);  // AND_Gate
  or or_117 (or_117_out, and_227_out, and_244_out);
  and and_228 (and_228_out, ~Bit5_Shift[2], or_117_out);  // AND_Gate
  or or_118 (or_118_out, and_228_out, and_263_out);
  and and_229 (and_229_out, ~Bit5_Shift[3], or_118_out);  // AND_Gate
  and and_230 (and_230_out, Bit5_Shift[3], or_121_out);
  and and_231 (Bit32_Result[6], ~Bit5_Shift[4], and_229_out);  // AND_Gate
  and and_232 (and_232_out, Bit5_Shift[4], and_239_out);
  and and_233 (and_233_out, Bit5_Shift[0], Bit32_In[5]);
  and and_234 (and_234_out, ~Bit5_Shift[0], Bit32_In[5]);  // AND_Gate
  or or_119 (or_119_out, and_234_out, and_242_out);
  and and_235 (and_235_out, Bit5_Shift[1], or_119_out);
  and and_236 (and_236_out, ~Bit5_Shift[1], or_119_out);  // AND_Gate
  or or_120 (or_120_out, and_236_out, and_252_out);
  and and_237 (and_237_out, Bit5_Shift[2], or_120_out);
  and and_238 (and_238_out, ~Bit5_Shift[2], or_120_out);  // AND_Gate
  or or_121 (or_121_out, and_238_out, and_273_out);
  and and_239 (and_239_out, ~Bit5_Shift[3], or_121_out);  // AND_Gate
  and and_240 (Bit32_Result[5], ~Bit5_Shift[4], and_239_out);  // AND_Gate
  and and_241 (and_241_out, Bit5_Shift[4], and_249_out);
  and and_242 (and_242_out, Bit5_Shift[0], Bit32_In[4]);
  and and_243 (and_243_out, ~Bit5_Shift[0], Bit32_In[4]);  // AND_Gate
  and and_244 (and_244_out, Bit5_Shift[1], or_124_out);
  and and_245 (and_245_out, ~Bit5_Shift[1], or_124_out);  // AND_Gate
  or or_122 (or_122_out, and_245_out, and_262_out);
  and and_246 (and_246_out, Bit5_Shift[2], or_122_out);
  and and_247 (and_247_out, ~Bit5_Shift[2], or_122_out);  // AND_Gate
  or or_123 (or_123_out, and_247_out, and_283_out);
  and and_248 (and_248_out, Bit5_Shift[3], or_123_out);
  and and_249 (and_249_out, ~Bit5_Shift[3], or_123_out);  // AND_Gate
  and and_250 (Bit32_Result[4], ~Bit5_Shift[4], and_249_out);  // AND_Gate
  and and_251 (and_251_out, Bit5_Shift[0], Bit32_In[3]);
  or or_124 (or_124_out, and_243_out, and_251_out);
  and and_252 (and_252_out, Bit5_Shift[1], or_125_out);
  and and_253 (and_253_out, ~Bit5_Shift[1], or_125_out);  // AND_Gate
  and and_254 (and_254_out, Bit5_Shift[2], or_126_out);
  and and_255 (and_255_out, ~Bit5_Shift[2], or_126_out);  // AND_Gate
  and and_256 (and_256_out, Bit5_Shift[3], and_255_out);
  and and_257 (and_257_out, ~Bit5_Shift[3], and_255_out);  // AND_Gate
  and and_258 (and_258_out, Bit5_Shift[4], and_257_out);
  and and_259 (Bit32_Result[3], ~Bit5_Shift[4], and_257_out);  // AND_Gate
  and and_260 (and_260_out, ~Bit5_Shift[0], Bit32_In[3]);  // AND_Gate
  and and_261 (and_261_out, Bit5_Shift[0], Bit32_In[2]);
  or or_125 (or_125_out, and_260_out, and_261_out);
  and and_262 (and_262_out, Bit5_Shift[1], or_127_out);
  or or_126 (or_126_out, and_253_out, and_272_out);
  and and_263 (and_263_out, Bit5_Shift[2], or_128_out);
  and and_264 (and_264_out, ~Bit5_Shift[2], or_128_out);  // AND_Gate
  and and_265 (and_265_out, Bit5_Shift[3], and_264_out);
  and and_266 (and_266_out, ~Bit5_Shift[3], and_264_out);  // AND_Gate
  and and_267 (and_267_out, Bit5_Shift[4], and_266_out);
  and and_268 (Bit32_Result[2], ~Bit5_Shift[4], and_266_out);  // AND_Gate
  and and_269 (and_269_out, ~Bit5_Shift[0], Bit32_In[2]);  // AND_Gate
  and and_270 (and_270_out, Bit5_Shift[0], Bit32_In[1]);
  or or_127 (or_127_out, and_269_out, and_270_out);
  and and_271 (and_271_out, ~Bit5_Shift[1], or_127_out);  // AND_Gate
  and and_272 (and_272_out, Bit5_Shift[1], or_129_out);
  or or_128 (or_128_out, and_271_out, and_281_out);
  and and_273 (and_273_out, Bit5_Shift[2], and_280_out);
  and and_274 (and_274_out, Bit5_Shift[3], and_282_out);
  and and_275 (and_275_out, ~Bit5_Shift[3], and_282_out);  // AND_Gate
  and and_276 (and_276_out, Bit5_Shift[4], and_275_out);
  and and_277 (Bit32_Result[1], ~Bit5_Shift[4], and_275_out);  // AND_Gate
  and and_278 (and_278_out, ~Bit5_Shift[0], Bit32_In[1]);  // AND_Gate
  and and_279 (and_279_out, Bit5_Shift[0], Bit32_In[0]);
  or or_129 (or_129_out, and_278_out, and_279_out);
  and and_280 (and_280_out, ~Bit5_Shift[1], or_129_out);  // AND_Gate
  and and_281 (and_281_out, Bit5_Shift[1], and_287_out);
  and and_282 (and_282_out, ~Bit5_Shift[2], and_280_out);  // AND_Gate
  and and_283 (and_283_out, Bit5_Shift[2], and_288_out);
  and and_284 (and_284_out, Bit5_Shift[3], and_289_out);
  and and_285 (and_285_out, Bit5_Shift[4], and_290_out);
  and and_286 (Bit32_Result[0], ~Bit5_Shift[4], and_290_out);  // AND_Gate
  and and_287 (and_287_out, ~Bit5_Shift[0], Bit32_In[0]);  // AND_Gate
  and and_288 (and_288_out, ~Bit5_Shift[1], and_287_out);  // AND_Gate
  and and_289 (and_289_out, ~Bit5_Shift[2], and_288_out);  // AND_Gate
  and and_290 (and_290_out, ~Bit5_Shift[3], and_289_out);  // AND_Gate
endmodule
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