// Logisim project forwarding.circ as structural Verilog: 1 circuit, main circuit main
module main (
  input  exr4,
  input  exr3,
  input  exr2,
  input  exr1,
  input  exr0,
  input  exreI,
  input  exreM,
  input  mem4,
  input  mem3,
  input  mem2,
  input  mem1,
  input  mem0,
  input  memeI,
  input  memeM,
  input  rda4,
  input  rda3,
  input  rda2,
  input  rda1,
  input  rda0,
  input  rdb4,
  input  rdb3,
  input  rdb2,
  input  rdb1,
  input  rdb0,
  output exre,
  output meme,
  output m_16_t_a,
  output m_16_t_b,
  output w_16_t_a,
  output w_16_t_b,
  output m_32_t_32,
  output w_32_t_32,
  output w_or_m_32_t_16_a_or_b,
  output _32_t_16_a_l,
  output _32_t_16_a_h,
  output _32_t_16_b_l,
  output _32_t_16_b_h,
  output _16_t_32,
  output _16_t_32_h_sl,
  output _16_t_32_h_en,
  output _16_t_32_l_sl,
  output _16_t_32_l_en,
  output a_norm,
  output b_norm,
  output _32_norm
);

  wire g18_out, g19_out, g20_out, g21_out, g22_out, g23_out, g24_out, g25_out, g26_out, g27_out, g34_out,
       g35_out, g36_out, g37_out, g38_out, g39_out, g41_out, g47_out, g48_out, g49_out, g50_out, g51_out,
       g52_out, g53_out, g54_out, g55_out, g56_out, g58_out, g59_out, g60_out, g61_out, g62_out, g63_out,
       g64_out, g66_out, g67_out, g68_out, g69_out, g70_out, g72_out, g73_out, g74_out, g75_out, g76_out,
       g77_out, g79_out, g80_out, g81_out, g83_out, g84_out, g85_out, g86_out, g87_out, g88_out, g90_out,
       g92_out, g93_out, g94_out, g95_out, g97_out, g99_out, g100_out, g101_out, g102_out, g106_out,
       g107_out, g108_out, g109_out, g110_out, g111_out, g115_out, g117_out, g118_out, g119_out, g121_out,
       g122_out, g123_out, g125_out, g126_out;

  and g4 (exre, exreI, exreM);
  and g7 (meme, memeI, memeM);
  xnor g18 (g18_out, exr4, rda4);
  xnor g19 (g19_out, exr3, rda3);
  xnor g20 (g20_out, exr2, rda2);
  xnor g21 (g21_out, exr1, rda1);
  xnor g22 (g22_out, exr0, rda0);
  not g24 (g24_out, exr4);
  not g25 (g25_out, exr3);
  xnor g34 (g34_out, exr4, rdb4);
  xnor g35 (g35_out, exr3, rdb3);
  xnor g36 (g36_out, exr2, rdb2);
  xnor g37 (g37_out, exr1, rdb1);
  xnor g38 (g38_out, exr0, rdb0);
  xnor g47 (g47_out, rda4, mem4);
  xnor g48 (g48_out, rda3, mem3);
  xnor g49 (g49_out, rda2, mem2);
  xnor g50 (g50_out, rda1, mem1);
  xnor g51 (g51_out, rda0, mem0);
  not g53 (g53_out, mem4);
  not g54 (g54_out, mem3);
  xnor g59 (g59_out, rdb4, mem4);
  xnor g60 (g60_out, rdb3, mem3);
  xnor g61 (g61_out, rdb2, mem2);
  xnor g62 (g62_out, rdb1, mem1);
  xnor g63 (g63_out, rdb0, mem0);
  and g67 (g67_out, exr4, exr3);
  not g68 (g68_out, exr2);
  and g74 (g74_out, mem4, mem3);
  not g75 (g75_out, mem2);
  not g86 (g86_out, rda2);
  not g94 (g94_out, rdb2);
  and g99 (g99_out, rda4, rda3);
  and g100 (g100_out, rdb4, rdb3);
  and g105 (_16_t_32_h_sl, exreI, exreM, exr4, exr3, exr2);
  and g90 (g90_out, rda4, rda3, rda2);
  and g97 (g97_out, rdb4, rdb3, rdb2);
  and g26 (g26_out, exr4, exr2, g25_out);
  and g55 (g55_out, mem4, mem2, g54_out);
  and g23 (g23_out, g18_out, g19_out, g20_out, g21_out, g22_out);
  and g39 (g39_out, g34_out, g35_out, g36_out, g37_out, g38_out);
  and g69 (g69_out, exr4, g68_out);
  and g52 (g52_out, g47_out, g48_out, g49_out, g50_out, g51_out);
  and g64 (g64_out, g59_out, g60_out, g61_out, g62_out, g63_out);
  and g76 (g76_out, mem4, g75_out);
  and g79 (g79_out, g21_out, g22_out);
  and g80 (g80_out, g37_out, g38_out);
  or g83 (g83_out, exre, meme);
  and g84 (g84_out, g50_out, g51_out);
  and g92 (g92_out, g62_out, g63_out);
  or g101 (g101_out, g99_out, g100_out);
  or g102 (g102_out, g67_out, g74_out);
  or g106 (g106_out, g90_out, g97_out);
  and g107 (g107_out, exreI, exreM, g21_out, g22_out);
  and g108 (g108_out, memeI, memeM, g50_out, g51_out);
  and g109 (g109_out, exreI, exreM, g37_out, g38_out);
  and g110 (g110_out, memeI, memeM, g62_out, g63_out);
  and g114 (_16_t_32_l_sl, exreI, exreM, exr4, exr3, g68_out);
  and g87 (g87_out, rda4, rda3, g86_out);
  and g95 (g95_out, rdb4, rdb3, g94_out);
  or g27 (g27_out, g24_out, g26_out);
  or g56 (g56_out, g53_out, g55_out);
  or g66 (g66_out, g23_out, g39_out);
  or g70 (g70_out, g67_out, g69_out);
  or g73 (g73_out, g52_out, g64_out);
  or g77 (g77_out, g74_out, g76_out);
  or g81 (g81_out, g79_out, g80_out);
  or g85 (g85_out, g79_out, g84_out);
  or g88 (g88_out, g67_out, g69_out, g74_out, g76_out);
  or g93 (g93_out, g80_out, g92_out);
  or g111 (g111_out, g107_out, g108_out, g109_out, g110_out);
  or g115 (g115_out, g87_out, g95_out);
  and g28 (m_16_t_a, exreI, exreM, g18_out, g19_out, g20_out, g21_out, g22_out, g27_out);
  and g40 (m_16_t_b, exreI, exreM, g27_out, g34_out, g35_out, g36_out, g37_out, g38_out);
  and g71 (m_32_t_32, exreI, exreM, g66_out, g70_out);
  and g82 (w_or_m_32_t_16_a_or_b, exreI, exreM, g70_out, g81_out);
  and g89 (_32_t_16_a_l, rda4, rda3, g83_out, g85_out, g86_out, g88_out);
  and g91 (_32_t_16_a_h, rda4, rda3, rda2, g83_out, g85_out, g88_out);
  and g96 (_32_t_16_b_l, rdb4, rdb3, g83_out, g88_out, g93_out, g94_out);
  and g98 (_32_t_16_b_h, rdb4, rdb3, rdb2, g83_out, g88_out, g93_out);
  and g103 (_16_t_32, g83_out, g85_out, g101_out, g102_out);
  and g112 (_16_t_32_h_en, g106_out, g111_out);
  and g116 (_16_t_32_l_en, g111_out, g115_out);
  not g41 (g41_out, m_16_t_a);
  not g58 (g58_out, m_16_t_b);
  not g72 (g72_out, m_32_t_32);
  not g117 (g117_out, _32_t_16_a_l);
  not g118 (g118_out, _32_t_16_a_h);
  not g121 (g121_out, _32_t_16_b_l);
  not g122 (g122_out, _32_t_16_b_h);
  not g125 (g125_out, _16_t_32);
  and g57 (w_16_t_a, memeI, memeM, g41_out, g47_out, g48_out, g49_out, g50_out, g51_out, g56_out);
  and g65 (w_16_t_b, memeI, memeM, g56_out, g58_out, g59_out, g60_out, g61_out, g62_out, g63_out);
  and g78 (w_32_t_32, memeI, memeM, g72_out, g73_out, g77_out);
  not g119 (g119_out, w_16_t_a);
  not g123 (g123_out, w_16_t_b);
  not g126 (g126_out, w_32_t_32);
  and g120 (a_norm, g41_out, g117_out, g118_out, g119_out);
  and g124 (b_norm, g58_out, g121_out, g122_out, g123_out);
  and g127 (_32_norm, g72_out, g125_out, g126_out);
endmodule
